// Logisim project FSM_ALL_test2.circ as structural Verilog: 10 circuits, main circuit DIGITAL_CLOCK
module DIGITAL_CLOCK (
  output Buzzer0,
  output Buzzer1
);

  wire AlarmOn, and_1_out, B0_out, B1_out, ButtonManager_1_chmode, ButtonManager_1_d0, ButtonManager_1_d1,
       ChM, clk, clk2k, clk4, d_ff_3_q, DipSwitch_1_sw2, or_1_out, or_2_out, or_3_out, RC, RESET;
  wire [1:0] d_ff_1_q, demultiplexer_1_out1, demultiplexer_1_out2, demultiplexer_1_out3,
       demultiplexer_1_out4, demultiplexer_1_out5, demultiplexer_1_out6;
  wire [2:0] FSM_ALL_1_state, STATE;
  wire [7:0] AllSegLeds_1_sevseg_0, AllSegLeds_1_sevseg_1, AllSegLeds_1_sevseg_2, AllSegLeds_1_sevseg_3,
       AllSegLeds_1_sevseg_4, AllSegLeds_1_sevseg_5, ChangementFuseauHoraire_1_utccode;
  wire [23:0] Alarm_1, Alarm_2, Anim_1, Anim_2, Capita_1, Capita_2, Chrono_1, Chrono_2, LT_1, LT_2,
       multiplexer_1_out, multiplexer_2_out, Music_1, Music_2, Timer_1, Timer_2, UTC_1, UTC_2;

  Clock clock_1 (.out(clk));
  Button B1 (.out(B1_out));
  Button B0 (.out(B0_out));
  DipSwitch #(.number(10)) DipSwitch_1 (
    .sw1(ChM), .sw2(DipSwitch_1_sw2), .sw5(RESET));  // open: sw3, sw4, sw6, sw7, sw8, sw9, sw10
  or or_1 (or_1_out, d_ff_1_q[0], d_ff_1_q[1], d_ff_3_q);
  Multiplexer #(.select(3), .width(24), .enable("false")) multiplexer_1 (
    .in0(Anim_1), .in1(UTC_1), .in2(Chrono_1), .in3(Timer_1), .in4(Alarm_1), .in5(Capita_1), .in6(Music_1),
    .in7(LT_1), .out(multiplexer_1_out), .sel(STATE));
  Multiplexer #(.select(3), .width(24), .enable("false")) multiplexer_2 (
    .in0(Anim_2), .in1(UTC_2), .in2(Chrono_2), .in3(Timer_2), .in4(Alarm_2), .in5(Capita_2), .in6(Music_2),
    .in7(LT_2), .out(multiplexer_2_out), .sel(STATE));
  changeFrequency32k_2k changeFrequency32k_2k_1 (.CLK32k(clk), .RESET(RESET), .CLK2k(clk2k));
  AllSegLeds AllSegLeds_1 (
    .sevsegCode_5(multiplexer_1_out[7:0]), .sevsegCode_4(multiplexer_1_out[15:8]),
    .sevsegCode_3(multiplexer_1_out[23:16]), .sevsegCode_2(multiplexer_2_out[7:0]),
    .sevsegCode_1(multiplexer_2_out[15:8]), .sevsegCode_0(multiplexer_2_out[23:16]),
    .sevseg_5(AllSegLeds_1_sevseg_5), .sevseg_4(AllSegLeds_1_sevseg_4), .sevseg_3(AllSegLeds_1_sevseg_3),
    .sevseg_2(AllSegLeds_1_sevseg_2), .sevseg_1(AllSegLeds_1_sevseg_1), .sevseg_0(AllSegLeds_1_sevseg_0));
  D_Flip_Flop d_ff_1 (.D(ButtonManager_1_d0), .clk(clk), .Q(d_ff_1_q[0]), .reset(or_2_out));  // open: Qn, preset
  ButtonManager ButtonManager_1 (
    .DIP(ChM), .RESET(or_1_out), .C2(d_ff_3_q), .C1(d_ff_1_q[1]), .C0(d_ff_1_q[0]), .B1(B1_out), .B0(B0_out),
    .D0(ButtonManager_1_d0), .D1(ButtonManager_1_d1), .chMode(ButtonManager_1_chmode));
  or or_2 (or_2_out, ChM, RESET);
  _7_Segment_Display SSD5 (
    .g(AllSegLeds_1_sevseg_5[0]), .f(AllSegLeds_1_sevseg_5[1]), .a(AllSegLeds_1_sevseg_5[6]),
    .b(AllSegLeds_1_sevseg_5[5]), .e(AllSegLeds_1_sevseg_5[2]), .d(AllSegLeds_1_sevseg_5[3]),
    .c(AllSegLeds_1_sevseg_5[4]), .dp(AllSegLeds_1_sevseg_5[7]));
  changeFrequency2k_4 changeFrequency2k_4_1 (.CLK2k(clk2k), .RESET(RESET), .CLK4(clk4));
  D_Flip_Flop d_ff_2 (.D(ButtonManager_1_d1), .clk(clk), .Q(d_ff_1_q[1]), .reset(or_3_out));  // open: Qn, preset
  or or_3 (or_3_out, ChM, RESET);
  _7_Segment_Display SSD4 (
    .g(AllSegLeds_1_sevseg_4[0]), .f(AllSegLeds_1_sevseg_4[1]), .a(AllSegLeds_1_sevseg_4[6]),
    .b(AllSegLeds_1_sevseg_4[5]), .e(AllSegLeds_1_sevseg_4[2]), .d(AllSegLeds_1_sevseg_4[3]),
    .c(AllSegLeds_1_sevseg_4[4]), .dp(AllSegLeds_1_sevseg_4[7]));
  D_Flip_Flop d_ff_3 (.D(ButtonManager_1_chmode), .clk(clk), .Q(d_ff_3_q), .reset(RESET));  // open: Qn, preset
  _7_Segment_Display SSD3 (
    .g(AllSegLeds_1_sevseg_3[0]), .f(AllSegLeds_1_sevseg_3[1]), .a(AllSegLeds_1_sevseg_3[6]),
    .b(AllSegLeds_1_sevseg_3[5]), .e(AllSegLeds_1_sevseg_3[2]), .d(AllSegLeds_1_sevseg_3[3]),
    .c(AllSegLeds_1_sevseg_3[4]), .dp(AllSegLeds_1_sevseg_3[7]));
  _7_Segment_Display SSD2 (
    .g(AllSegLeds_1_sevseg_2[0]), .f(AllSegLeds_1_sevseg_2[1]), .a(AllSegLeds_1_sevseg_2[6]),
    .b(AllSegLeds_1_sevseg_2[5]), .e(AllSegLeds_1_sevseg_2[2]), .d(AllSegLeds_1_sevseg_2[3]),
    .c(AllSegLeds_1_sevseg_2[4]), .dp(AllSegLeds_1_sevseg_2[7]));
  and and_1 (and_1_out, ~FSM_ALL_1_state[0], ~FSM_ALL_1_state[1], ~FSM_ALL_1_state[2]);  // AND_Gate
  _7_Segment_Display SSD1 (
    .g(AllSegLeds_1_sevseg_1[0]), .f(AllSegLeds_1_sevseg_1[1]), .a(AllSegLeds_1_sevseg_1[6]),
    .b(AllSegLeds_1_sevseg_1[5]), .e(AllSegLeds_1_sevseg_1[2]), .d(AllSegLeds_1_sevseg_1[3]),
    .c(AllSegLeds_1_sevseg_1[4]), .dp(AllSegLeds_1_sevseg_1[7]));
  or or_4 (RC, RESET, and_1_out);
  FSM_ALL FSM_ALL_1 (.ChMode(d_ff_3_q), .DIP(ChM), .RESET(RESET), .CLK32k(clk), .STATE(FSM_ALL_1_state));
  _7_Segment_Display SSD0 (
    .g(AllSegLeds_1_sevseg_0[0]), .f(AllSegLeds_1_sevseg_0[1]), .a(AllSegLeds_1_sevseg_0[6]),
    .b(AllSegLeds_1_sevseg_0[5]), .e(AllSegLeds_1_sevseg_0[2]), .d(AllSegLeds_1_sevseg_0[3]),
    .c(AllSegLeds_1_sevseg_0[4]), .dp(AllSegLeds_1_sevseg_0[7]));
  Demultiplexer #(.select(3), .width(2), .enable("false")) demultiplexer_1 (
    .out1(demultiplexer_1_out1), .out2(demultiplexer_1_out2), .out3(demultiplexer_1_out3),
    .out4(demultiplexer_1_out4), .out5(demultiplexer_1_out5), .out6(demultiplexer_1_out6), .in(d_ff_1_q),
    .sel(FSM_ALL_1_state));  // open: out0, out7
  hourFSM hourFSM_1 (
    .RESET(RC), .B1_B0(demultiplexer_1_out1), .ChM(ChM), .CLK32K(clk), .CLK2k(clk2k), .CLK4(clk4),
    .sevsegCode_5(UTC_1[7:0]), .sevsegCode_4(UTC_1[15:8]), .sevsegCode_3(UTC_1[23:16]),
    .sevsegCode_2(UTC_2[7:0]), .sevsegCode_1(UTC_2[15:8]), .sevsegCode_0(UTC_2[23:16]));
  CHRONO u_CHRONO_1 (
    .RESET(RC), .B1_B0(demultiplexer_1_out2), .ChMode(ChM), .CLK32k(clk), .Min_Led2(Chrono_1[7:0]),
    .Min_Led1(Chrono_1[15:8]), .Sec_Led2(Chrono_1[23:16]), .Sec_Led1(Chrono_2[7:0]),
    .Milli_Led2(Chrono_2[15:8]), .Milli_Led1(Chrono_2[23:16]));
  timerFSM timer (
    .RESET(RC), .B1_B0(demultiplexer_1_out3), .DIP(DipSwitch_1_sw2), .ChM(ChM), .CLK32k(clk), .CLK2k(clk2k),
    .CLK4(clk4), .sevsegCode_5(Timer_1[7:0]), .sevsegCode_4(Timer_1[15:8]), .sevsegCode_3(Timer_1[23:16]),
    .sevsegCode_2(Timer_2[7:0]), .sevsegCode_1(Timer_2[15:8]), .sevsegCode_0(Timer_2[23:16]));
  ChangementFuseauHoraire ChangementFuseauHoraire_1 (
    .RESET(RC), .B1_B0(demultiplexer_1_out5), .ChM(ChM), .CLK32k(clk), .Letter1(Capita_1[7:0]),
    .Letter2(Capita_1[15:8]), .Letter3(Capita_1[23:16]), .Letter4(Capita_2[7:0]), .Letter5(Capita_2[15:8]),
    .Letter6(Capita_2[23:16]), .UTCCode(ChangementFuseauHoraire_1_utccode));
  MUSIC u_MUSIC_1 (
    .ALARM(AlarmOn), .B1_B0(demultiplexer_1_out6), .RESET(RC), .CLK32k(clk), .Buzzer1(Buzzer1),
    .L1(Music_1[7:0]), .L2(Music_1[15:8]), .L3(Music_1[23:16]), .L4(Music_2[7:0]), .L5(Music_2[15:8]),
    .L6(Music_2[23:16]));
  ANIMATION ANIMATION_1 (
    .State(FSM_ALL_1_state), .L1(Anim_1[7:0]), .L2(Anim_1[15:8]), .L3(Anim_1[23:16]), .L4(Anim_2[7:0]),
    .L5(Anim_2[15:8]), .L6(Anim_2[23:16]));
  AnimControl AnimControl_1 (.Transition(ChM), .State(FSM_ALL_1_state), .Anim(STATE));
  changeTimeZone changeTimeZone_1 (
    .SSDCode_5(UTC_1[7:0]), .SSDCode_4(UTC_1[15:8]), .SSDCode_3(UTC_1[23:16]), .SSDCode_2(UTC_2[7:0]),
    .SSDCode_1(UTC_2[15:8]), .SSDCode_0(UTC_2[23:16]), .UTCCode_8(ChangementFuseauHoraire_1_utccode),
    .sevsegCode_5(LT_1[7:0]), .sevsegCode_4(LT_1[15:8]), .sevsegCode_3(LT_1[23:16]),
    .sevsegCode_2(LT_2[7:0]), .sevsegCode_1(LT_2[15:8]), .sevsegCode_0(LT_2[23:16]));
  alarm u_alarm_1 (
    .RESET(RESET), .B1_B0(demultiplexer_1_out4), .SSDCode_5(LT_1[7:0]), .SSDCode_4(LT_1[15:8]),
    .SSDCode_3(LT_1[23:16]), .SSDCode_2(LT_2[7:0]), .ChM(ChM), .CLK32K(clk), .CLK2k(clk2k), .CLK4(clk4),
    .sevsegCode_5(Alarm_1[7:0]), .sevsegCode_4(Alarm_1[15:8]), .sevsegCode_3(Alarm_1[23:16]),
    .sevsegCode_2(Alarm_2[7:0]), .sevsegCode_1(Alarm_2[15:8]), .sevsegCode_0(Alarm_2[23:16]), .BUZZER(AlarmOn));

  assign Buzzer0 = 1'b0;

  // Notes on the sheet:
  //   LedGauche
  //   LedDroite
endmodule

module FSM_ALL (
  input  ChMode,
  input  DIP,
  input  RESET,
  input  CLK32k,
  output [2:0] STATE
);

  wire TransLogic_1_d0, TransLogic_1_d1, TransLogic_1_d2;

  TransLogic TransLogic_1 (
    .B1(ChMode), .DIP(DIP), .C2(STATE[2]), .C1(STATE[1]), .C0(STATE[0]), .D2(TransLogic_1_d2),
    .D1(TransLogic_1_d1), .D0(TransLogic_1_d0));
  D_Flip_Flop d_ff_1 (.D(TransLogic_1_d2), .clk(CLK32k), .Q(STATE[2]), .reset(RESET));  // open: Qn, preset
  D_Flip_Flop d_ff_2 (.D(TransLogic_1_d1), .clk(CLK32k), .Q(STATE[1]), .reset(RESET));  // open: Qn, preset
  D_Flip_Flop d_ff_3 (.D(TransLogic_1_d0), .clk(CLK32k), .Q(STATE[0]), .reset(RESET));  // open: Qn, preset
endmodule

module ButtonManager (
  input  DIP,
  input  RESET,
  input  C2,
  input  C1,
  input  C0,
  input  B1,
  input  B0,
  output D0,
  output D1,
  output chMode
);

  wire d_ff_1_q, d_ff_1_qn, d_ff_2_q, d_ff_2_qn, not_1_out, not_2_out, not_3_out, not_4_out, not_5_out,
       not_6_out, not_7_out, not_8_out, not_9_out, not_10_out;

  D_Flip_Flop d_ff_1 (.D(d_ff_1_qn), .clk(B1), .Q(d_ff_1_q), .Qn(d_ff_1_qn), .reset(RESET));  // open: preset
  D_Flip_Flop d_ff_2 (.D(d_ff_2_qn), .clk(B0), .Q(d_ff_2_q), .Qn(d_ff_2_qn), .reset(RESET));  // open: preset
  not not_1 (not_1_out, DIP);
  not not_2 (not_2_out, RESET);
  not not_3 (not_3_out, C2);
  not not_4 (not_4_out, DIP);
  not not_5 (not_5_out, RESET);
  not not_6 (not_6_out, C2);
  not not_7 (not_7_out, RESET);
  not not_8 (not_8_out, C2);
  not not_9 (not_9_out, C1);
  not not_10 (not_10_out, C0);
  and and_1 (D0, not_1_out, not_2_out, not_3_out, d_ff_1_q);
  and and_2 (D1, not_4_out, not_5_out, not_6_out, d_ff_2_q);
  and and_3 (chMode, DIP, not_7_out, not_8_out, not_9_out, not_10_out, d_ff_2_q);
endmodule

module TransLogic (
  input  B1,
  input  DIP,
  input  C2,
  input  C1,
  input  C0,
  output D2,
  output D1,
  output D0
);

  wire and_1_out, and_2_out, and_3_out, and_4_out, and_5_out, and_6_out, and_7_out, and_8_out, and_9_out,
       and_10_out, and_11_out, and_12_out, and_13_out, not_1_out, not_2_out, not_3_out, not_4_out, not_5_out,
       not_6_out, not_7_out, not_8_out, not_9_out, not_10_out, not_11_out, not_12_out;

  not not_1 (not_1_out, C2);
  not not_2 (not_2_out, C1);
  not not_3 (not_3_out, B1);
  not not_4 (not_4_out, DIP);
  not not_5 (not_5_out, C0);
  not not_6 (not_6_out, B1);
  and and_1 (and_1_out, not_6_out, C2);
  not not_7 (not_7_out, DIP);
  and and_2 (and_2_out, not_7_out, C2);
  and and_3 (and_3_out, C2, not_8_out);
  not not_8 (not_8_out, C1);
  and and_4 (and_4_out, C2, not_9_out);
  not not_9 (not_9_out, C0);
  and and_5 (and_5_out, B1, DIP, not_1_out, C1, C0);
  not not_10 (not_10_out, B1);
  and and_6 (and_6_out, not_10_out, C1);
  not not_11 (not_11_out, DIP);
  and and_7 (and_7_out, not_11_out, C1);
  and and_8 (and_8_out, C1, not_12_out);
  not not_12 (not_12_out, C0);
  and and_9 (and_9_out, B1, DIP, not_2_out, C0);
  and and_10 (and_10_out, not_3_out, C0);
  and and_11 (and_11_out, not_4_out, C0);
  and and_12 (and_12_out, C2, C1, C0);
  and and_13 (and_13_out, B1, DIP, not_5_out);
  or or_1 (D2, and_1_out, and_2_out, and_3_out, and_4_out, and_5_out);
  or or_2 (D1, and_6_out, and_7_out, and_8_out, and_9_out);
  or or_3 (D0, and_10_out, and_11_out, and_12_out, and_13_out);
endmodule

module DecoderToSegLed (
  input  e5,
  input  e4,
  input  e3,
  input  e2,
  input  e1,
  input  e0,
  output o,
  output a,
  output b,
  output c,
  output d,
  output e,
  output f,
  output g
);

  wire and_1_out, and_2_out, and_3_out, and_4_out, and_5_out, and_6_out, and_7_out, and_8_out, and_9_out,
       and_10_out, and_11_out, and_12_out, and_13_out, and_14_out, and_15_out, and_16_out, and_17_out,
       and_18_out, and_19_out, and_20_out, and_21_out, and_22_out, and_23_out, and_24_out, and_25_out,
       and_26_out, and_27_out, and_28_out, and_29_out, and_30_out, and_31_out, and_32_out, and_33_out,
       and_34_out, and_35_out, and_36_out, and_37_out, and_38_out, and_39_out, and_40_out, and_41_out,
       and_42_out, and_43_out, and_44_out, and_45_out, and_46_out, and_47_out, and_48_out, and_49_out,
       and_50_out, and_51_out, and_52_out, and_53_out, not_1_out, not_2_out, not_3_out, not_4_out, not_5_out,
       not_6_out, not_7_out, not_8_out, not_9_out, not_10_out, not_11_out, not_12_out, not_13_out,
       not_14_out, not_15_out, not_16_out, not_17_out, not_18_out, not_19_out, not_20_out, not_21_out,
       not_22_out, not_23_out, not_24_out, not_25_out, not_26_out, not_27_out, not_28_out, not_29_out,
       not_30_out, not_31_out, not_32_out, not_33_out, not_34_out, not_35_out, not_36_out, not_37_out,
       not_38_out, not_39_out, not_40_out, not_41_out, not_42_out, not_43_out, not_44_out, not_45_out,
       not_46_out, not_47_out, not_48_out, not_49_out, not_50_out, not_51_out, not_52_out, not_53_out,
       not_54_out, not_55_out, not_56_out, not_57_out, not_58_out, not_59_out, not_60_out, not_61_out,
       not_62_out, not_63_out, not_64_out, not_65_out, not_66_out, not_67_out, not_68_out, not_69_out,
       not_70_out, not_71_out, not_72_out, not_73_out, not_74_out, not_75_out, not_76_out, not_77_out,
       not_78_out, not_79_out, not_80_out, not_81_out, not_82_out, not_83_out, not_84_out, not_85_out,
       not_86_out, not_87_out, not_88_out, not_89_out, not_90_out, not_91_out, not_92_out, not_93_out,
       not_94_out, not_95_out, not_96_out;

  not not_1 (not_1_out, e2);
  not not_2 (not_2_out, e1);
  not not_3 (not_3_out, e0);
  not not_4 (not_4_out, e4);
  not not_5 (not_5_out, e3);
  not not_6 (not_6_out, e3);
  not not_7 (not_7_out, e1);
  not not_8 (not_8_out, e4);
  not not_9 (not_9_out, e4);
  not not_10 (not_10_out, e0);
  not not_11 (not_11_out, e2);
  not not_12 (not_12_out, e1);
  not not_13 (not_13_out, e2);
  not not_14 (not_14_out, e4);
  not not_15 (not_15_out, e3);
  not not_16 (not_16_out, e1);
  not not_17 (not_17_out, e0);
  not not_18 (not_18_out, e4);
  not not_19 (not_19_out, e2);
  not not_20 (not_20_out, e0);
  not not_21 (not_21_out, e3);
  not not_22 (not_22_out, e2);
  not not_23 (not_23_out, e4);
  not not_24 (not_24_out, e3);
  not not_25 (not_25_out, e2);
  not not_26 (not_26_out, e1);
  not not_27 (not_27_out, e4);
  not not_28 (not_28_out, e1);
  not not_29 (not_29_out, e3);
  not not_30 (not_30_out, e1);
  not not_31 (not_31_out, e0);
  not not_32 (not_32_out, e3);
  not not_33 (not_33_out, e2);
  not not_34 (not_34_out, e1);
  not not_35 (not_35_out, e3);
  not not_36 (not_36_out, e2);
  not not_37 (not_37_out, e1);
  not not_38 (not_38_out, e4);
  not not_39 (not_39_out, e3);
  not not_40 (not_40_out, e4);
  not not_41 (not_41_out, e2);
  not not_42 (not_42_out, e0);
  not not_43 (not_43_out, e4);
  not not_44 (not_44_out, e3);
  not not_45 (not_45_out, e2);
  not not_46 (not_46_out, e0);
  not not_47 (not_47_out, e4);
  not not_48 (not_48_out, e3);
  not not_49 (not_49_out, e0);
  not not_50 (not_50_out, e2);
  not not_51 (not_51_out, e4);
  not not_52 (not_52_out, e1);
  not not_53 (not_53_out, e4);
  not not_54 (not_54_out, e1);
  not not_55 (not_55_out, e1);
  not not_56 (not_56_out, e0);
  not not_57 (not_57_out, e3);
  not not_58 (not_58_out, e1);
  not not_59 (not_59_out, e0);
  not not_60 (not_60_out, e3);
  not not_61 (not_61_out, e2);
  and and_1 (and_1_out, not_61_out, not_62_out);
  not not_62 (not_62_out, e0);
  not not_63 (not_63_out, e4);
  and and_2 (and_2_out, not_63_out, e1, not_64_out);
  not not_64 (not_64_out, e0);
  not not_65 (not_65_out, e4);
  and and_3 (and_3_out, not_65_out, e3, e1);
  and and_4 (and_4_out, e3, e2, not_66_out);
  not not_66 (not_66_out, e1);
  and and_5 (and_5_out, e4, not_67_out, not_68_out);
  not not_67 (not_67_out, e3);
  not not_68 (not_68_out, e1);
  and and_6 (and_6_out, e4, not_69_out, e2);
  not not_69 (not_69_out, e3);
  not not_70 (not_70_out, e1);
  not not_71 (not_71_out, e0);
  not not_72 (not_72_out, e4);
  not not_73 (not_73_out, e0);
  not not_74 (not_74_out, e3);
  not not_75 (not_75_out, e1);
  not not_76 (not_76_out, e2);
  not not_77 (not_77_out, e4);
  not not_78 (not_78_out, e0);
  not not_79 (not_79_out, e3);
  not not_80 (not_80_out, e2);
  not not_81 (not_81_out, e0);
  not not_82 (not_82_out, e3);
  not not_83 (not_83_out, e1);
  not not_84 (not_84_out, e4);
  not not_85 (not_85_out, e2);
  not not_86 (not_86_out, e4);
  not not_87 (not_87_out, e0);
  not not_88 (not_88_out, e4);
  not not_89 (not_89_out, e3);
  not not_90 (not_90_out, e1);
  not not_91 (not_91_out, e2);
  not not_92 (not_92_out, e4);
  not not_93 (not_93_out, e2);
  not not_94 (not_94_out, e1);
  not not_95 (not_95_out, e3);
  not not_96 (not_96_out, e0);
  and and_7 (and_7_out, not_1_out, not_2_out, not_3_out);
  and and_8 (and_8_out, not_4_out, not_5_out, e1);
  and and_9 (and_9_out, not_6_out, e2, not_7_out, e0);
  and and_10 (and_10_out, not_8_out, e2, e1);
  and and_11 (and_11_out, not_9_out, e3, not_10_out);
  and and_12 (and_12_out, e3, not_11_out, not_12_out);
  and and_13 (and_13_out, e4, e3, not_13_out, e0);
  and and_14 (and_14_out, not_14_out, not_15_out, not_16_out, not_17_out);
  and and_15 (and_15_out, not_18_out, not_19_out, not_20_out);
  and and_16 (and_16_out, not_21_out, not_22_out, e0);
  and and_17 (and_17_out, not_23_out, not_24_out, e1, e0);
  and and_18 (and_18_out, e3, not_25_out, not_26_out);
  and and_19 (and_19_out, not_27_out, e3, not_28_out, e0);
  and and_20 (and_20_out, e4, not_29_out, not_30_out, e0);
  and and_21 (and_21_out, e4, e3, e2, e1, not_31_out);
  and and_22 (and_22_out, not_32_out, not_33_out, not_34_out);
  and and_23 (and_23_out, not_35_out, e0);
  and and_24 (and_24_out, not_36_out, e0);
  and and_25 (and_25_out, not_37_out, e0);
  and and_26 (and_26_out, not_38_out, not_39_out, e2);
  and and_27 (and_27_out, not_40_out, e3, not_41_out);
  and and_28 (and_28_out, e4, e2, e1, not_42_out);
  and and_29 (and_29_out, not_43_out, not_44_out, not_45_out, not_46_out);
  and and_30 (and_30_out, not_47_out, not_48_out, e1, not_49_out);
  and and_31 (and_31_out, not_50_out, e1, e0);
  and and_32 (and_32_out, not_51_out, e2, not_52_out, e0);
  and and_33 (and_33_out, not_53_out, e3, not_54_out);
  and and_34 (and_34_out, e3, e2, not_55_out);
  and and_35 (and_35_out, e3, e2, not_56_out);
  and and_36 (and_36_out, e4, not_57_out, not_58_out, not_59_out);
  and and_37 (and_37_out, e4, not_60_out, e1, e0);
  and and_38 (and_38_out, not_70_out, not_71_out);
  and and_39 (and_39_out, not_72_out, e2, not_73_out);
  and and_40 (and_40_out, not_74_out, e2, not_75_out);
  and and_41 (and_41_out, e3, not_76_out, e0);
  and and_42 (and_42_out, not_77_out, e3, e1);
  and and_43 (and_43_out, e3, e2, not_78_out);
  and and_44 (and_44_out, e4, not_79_out, not_80_out, not_81_out);
  and and_45 (and_45_out, e4, not_82_out, not_83_out);
  and and_46 (and_46_out, not_84_out, not_85_out, e1);
  and and_47 (and_47_out, not_86_out, e1, not_87_out);
  and and_48 (and_48_out, not_88_out, not_89_out, e2, not_90_out);
  and and_49 (and_49_out, e3, not_91_out);
  and and_50 (and_50_out, not_92_out, e3, e0);
  and and_51 (and_51_out, e4, not_93_out, not_94_out, e0);
  and and_52 (and_52_out, e4, not_95_out, e2, e1);
  and and_53 (and_53_out, e4, e3, not_96_out);
  or or_1 (a, and_7_out, and_8_out, and_9_out, and_10_out, and_11_out, and_12_out, and_13_out);
  or or_2 (b, and_14_out, and_15_out, and_16_out, and_17_out, and_18_out, and_19_out, and_20_out, and_21_out);
  or or_3 (c, and_22_out, and_23_out, and_24_out, and_25_out, and_26_out, and_27_out, and_28_out);
  or or_4 (d, and_29_out, and_30_out, and_31_out, and_32_out, and_33_out, and_34_out, and_35_out, and_36_out, and_37_out);
  or or_5 (e, and_1_out, and_2_out, and_3_out, and_4_out, and_5_out, and_6_out);
  or or_6 (f, and_38_out, and_39_out, and_40_out, and_41_out, and_42_out, and_43_out, and_44_out, and_45_out);
  or or_7 (g, and_46_out, and_47_out, and_48_out, and_49_out, and_50_out, and_51_out, and_52_out, and_53_out);

  assign o = e5;
endmodule

module SegLed1 (
  input  [7:0] sevsegCode,
  output [7:0] sevensegment
);

  wire [4:0] bit_extender_1_out;

  Bit_Extender #(.in_width(7), .out_width(5), .\type ("zero")) bit_extender_1 (
    .in(sevsegCode[6:0]), .out(bit_extender_1_out));
  DecoderToSegLed DecoderToSegLed_1 (
    .e5(sevsegCode[7]), .e4(bit_extender_1_out[4]), .e3(bit_extender_1_out[3]), .e2(bit_extender_1_out[2]),
    .e1(bit_extender_1_out[1]), .e0(bit_extender_1_out[0]), .o(sevensegment[7]), .a(sevensegment[6]),
    .b(sevensegment[5]), .c(sevensegment[4]), .d(sevensegment[3]), .e(sevensegment[2]), .f(sevensegment[1]),
    .g(sevensegment[0]));
endmodule

module AllSegLeds (
  input  [7:0] sevsegCode_5,
  input  [7:0] sevsegCode_4,
  input  [7:0] sevsegCode_3,
  input  [7:0] sevsegCode_2,
  input  [7:0] sevsegCode_1,
  input  [7:0] sevsegCode_0,
  output [7:0] sevseg_5,
  output [7:0] sevseg_4,
  output [7:0] sevseg_3,
  output [7:0] sevseg_2,
  output [7:0] sevseg_1,
  output [7:0] sevseg_0
);

  SegLed1 SegLed1_1 (.sevsegCode(sevsegCode_5), .sevensegment(sevseg_5));
  SegLed1 SegLed1_2 (.sevsegCode(sevsegCode_4), .sevensegment(sevseg_4));
  SegLed1 SegLed1_3 (.sevsegCode(sevsegCode_3), .sevensegment(sevseg_3));
  SegLed1 SegLed1_4 (.sevsegCode(sevsegCode_2), .sevensegment(sevseg_2));
  SegLed1 SegLed1_5 (.sevsegCode(sevsegCode_1), .sevensegment(sevseg_1));
  SegLed1 SegLed1_6 (.sevsegCode(sevsegCode_0), .sevensegment(sevseg_0));
endmodule

module AnimControl (
  input  Transition,
  input  [2:0] State,
  output [2:0] Anim
);

  wire not_1_out, not_2_out, not_3_out;

  not not_1 (not_1_out, Transition);
  not not_2 (not_2_out, Transition);
  not not_3 (not_3_out, Transition);
  and and_1 (Anim[2], not_1_out, State[2]);
  and and_2 (Anim[1], not_2_out, State[1]);
  and and_3 (Anim[0], not_3_out, State[0]);
endmodule

module changeFrequency32k_2k (
  input  CLK32k,
  input  RESET,
  output CLK2k
);

  wire d_ff_1_q, d_ff_1_qn, d_ff_2_q, d_ff_2_qn, d_ff_3_q, d_ff_3_qn, d_ff_4_qn;

  D_Flip_Flop d_ff_1 (.D(d_ff_1_qn), .clk(CLK32k), .Q(d_ff_1_q), .Qn(d_ff_1_qn), .reset(RESET));  // open: preset
  D_Flip_Flop d_ff_2 (.D(d_ff_2_qn), .clk(d_ff_1_q), .Q(d_ff_2_q), .Qn(d_ff_2_qn), .reset(RESET));  // open: preset
  D_Flip_Flop d_ff_3 (.D(d_ff_3_qn), .clk(d_ff_2_q), .Q(d_ff_3_q), .Qn(d_ff_3_qn), .reset(RESET));  // open: preset
  D_Flip_Flop d_ff_4 (.D(d_ff_4_qn), .clk(d_ff_3_q), .Q(CLK2k), .Qn(d_ff_4_qn), .reset(RESET));  // open: preset
endmodule

module changeFrequency2k_4 (
  input  CLK2k,
  input  RESET,
  output CLK4
);

  wire d_ff_1_q, d_ff_1_qn, d_ff_2_q, d_ff_2_qn, d_ff_3_q, d_ff_3_qn, d_ff_4_q, d_ff_4_qn, d_ff_5_q,
       d_ff_5_qn, d_ff_6_q, d_ff_6_qn, d_ff_7_q, d_ff_7_qn, d_ff_8_q, d_ff_8_qn, d_ff_9_qn;

  D_Flip_Flop d_ff_1 (.D(d_ff_1_qn), .clk(CLK2k), .Q(d_ff_1_q), .Qn(d_ff_1_qn), .reset(RESET));  // open: preset
  D_Flip_Flop d_ff_2 (.D(d_ff_2_qn), .clk(d_ff_1_q), .Q(d_ff_2_q), .Qn(d_ff_2_qn), .reset(RESET));  // open: preset
  D_Flip_Flop d_ff_3 (.D(d_ff_3_qn), .clk(d_ff_2_q), .Q(d_ff_3_q), .Qn(d_ff_3_qn), .reset(RESET));  // open: preset
  D_Flip_Flop d_ff_4 (.D(d_ff_4_qn), .clk(d_ff_3_q), .Q(d_ff_4_q), .Qn(d_ff_4_qn), .reset(RESET));  // open: preset
  D_Flip_Flop d_ff_5 (.D(d_ff_5_qn), .clk(d_ff_4_q), .Q(d_ff_5_q), .Qn(d_ff_5_qn), .reset(RESET));  // open: preset
  D_Flip_Flop d_ff_6 (.D(d_ff_6_qn), .clk(d_ff_5_q), .Q(d_ff_6_q), .Qn(d_ff_6_qn), .reset(RESET));  // open: preset
  D_Flip_Flop d_ff_7 (.D(d_ff_7_qn), .clk(d_ff_6_q), .Q(d_ff_7_q), .Qn(d_ff_7_qn), .reset(RESET));  // open: preset
  D_Flip_Flop d_ff_8 (.D(d_ff_8_qn), .clk(d_ff_7_q), .Q(d_ff_8_q), .Qn(d_ff_8_qn), .reset(RESET));  // open: preset
  D_Flip_Flop d_ff_9 (.D(d_ff_9_qn), .clk(d_ff_8_q), .Q(CLK4), .Qn(d_ff_9_qn), .reset(RESET));  // open: preset
endmodule
