// Logisim project hourModule.circ as structural Verilog: 26 circuits, main circuit hourFSM
module hourFSM (
  input  RESET,
  input  [1:0] B1_B0,
  input  ChM,
  input  CLK32K,
  input  CLK2k,
  input  CLK4,
  output [7:0] sevsegCode_5,
  output [7:0] sevsegCode_4,
  output [7:0] sevsegCode_3,
  output [7:0] sevsegCode_2,
  output [7:0] sevsegCode_1,
  output [7:0] sevsegCode_0
);

  wire changeHour_1_hloadtendi, changeHour_1_hloaduendi, changeHour_1_minloadtendi,
       changeHour_1_minloaduendi, changeHour_1_secloadtendi, changeHour_1_secloaduendi, HOUR_1_hloadt,
       HOUR_1_hloadu, HOUR_1_minloadt, HOUR_1_minloadu, HOUR_1_secloadt, HOUR_1_secloadu;
  wire [1:0] and_1_out;
  wire [3:0] changeHour_1_hloadt_4, changeHour_1_hloadu_4, changeHour_1_minloadt_4, changeHour_1_minloadu_4,
       changeHour_1_secloadt_4, changeHour_1_secloadu_4, HOUR_1_ht_4, HOUR_1_hu_4, HOUR_1_mint_4,
       HOUR_1_minu_4, HOUR_1_sect_4, HOUR_1_secu_4;

  and and_1 (and_1_out[0], B1_B0[0], ~ChM);  // AND_Gate
  and and_2 (and_1_out[1], B1_B0[1], ~ChM);  // AND_Gate
  changeHour changeHour_1 (
    .B1_B0(and_1_out), .ResetSelector(ChM), .clk(CLK32K), .HloadT_4(changeHour_1_hloadt_4),
    .HloadTEnDi(changeHour_1_hloadtendi), .HloadU_4(changeHour_1_hloadu_4),
    .HloadUEnDi(changeHour_1_hloaduendi), .MINloadT_4(changeHour_1_minloadt_4),
    .MINloadTEnDi(changeHour_1_minloadtendi), .MINloadU_4(changeHour_1_minloadu_4),
    .MINloadUEnDi(changeHour_1_minloaduendi), .SECloadT_4(changeHour_1_secloadt_4),
    .SECloadTEnDi(changeHour_1_secloadtendi), .SECloadU_4(changeHour_1_secloadu_4),
    .SECloadUEnDi(changeHour_1_secloaduendi));
  HOUR HOUR_1 (
    .RESET(RESET), .CLK2k(CLK2k), .HloadT_4(changeHour_1_hloadt_4), .HloadTEnDi(changeHour_1_hloadtendi),
    .HloadU_4(changeHour_1_hloadu_4), .HloadUEnDi(changeHour_1_hloaduendi),
    .MINloadT_4(changeHour_1_minloadt_4), .MINloadTEnDi(changeHour_1_minloadtendi),
    .MINloadU_4(changeHour_1_minloadu_4), .MINloadUEnDi(changeHour_1_minloaduendi),
    .SECloadT_4(changeHour_1_secloadt_4), .SECloadTEnDi(changeHour_1_secloadtendi),
    .SECloadU_4(changeHour_1_secloadu_4), .SECloadUEnDi(changeHour_1_secloaduendi), .HT_4(HOUR_1_ht_4),
    .HU_4(HOUR_1_hu_4), .MINT_4(HOUR_1_mint_4), .MINU_4(HOUR_1_minu_4), .SECT_4(HOUR_1_sect_4),
    .SECU_4(HOUR_1_secu_4), .HloadT(HOUR_1_hloadt), .HloadU(HOUR_1_hloadu), .MINloadT(HOUR_1_minloadt),
    .MINloadU(HOUR_1_minloadu), .SECloadT(HOUR_1_secloadt), .SECloadU(HOUR_1_secloadu));
  hourView_HMS hourView_HMS_1 (
    .HT_4(HOUR_1_ht_4), .HU_4(HOUR_1_hu_4), .MINT_4(HOUR_1_mint_4), .MINU_4(HOUR_1_minu_4),
    .SECT_4(HOUR_1_sect_4), .SECU_4(HOUR_1_secu_4), .HloadT(HOUR_1_hloadt), .HloadU(HOUR_1_hloadu),
    .MINloadT(HOUR_1_minloadt), .MINloadU(HOUR_1_minloadu), .SECloadT(HOUR_1_secloadt),
    .SECloadU(HOUR_1_secloadu), .RESET(RESET), .CLK4(CLK4), .sevsegCode_5(sevsegCode_5),
    .sevsegCode_4(sevsegCode_4), .sevsegCode_3(sevsegCode_3), .sevsegCode_2(sevsegCode_2),
    .sevsegCode_1(sevsegCode_1), .sevsegCode_0(sevsegCode_0));
endmodule

module zeroTwo (
  input  IN1,
  input  IN0,
  input  TickIN,
  output TickOUT,
  output OUT1,
  output OUT0
);

  wire and_2_out, and_3_out, and_4_out, and_5_out, not_1_out, not_2_out, not_3_out, not_4_out, not_5_out,
       not_6_out, not_7_out, not_8_out;

  not not_1 (not_1_out, IN0);
  not not_2 (not_2_out, IN1);
  not not_3 (not_3_out, IN0);
  not not_4 (not_4_out, TickIN);
  not not_5 (not_5_out, IN1);
  not not_6 (not_6_out, IN0);
  not not_7 (not_7_out, IN1);
  not not_8 (not_8_out, TickIN);
  and and_1 (TickOUT, IN1, not_1_out, TickIN);
  and and_2 (and_2_out, not_2_out, IN0, TickIN);
  and and_3 (and_3_out, IN1, not_3_out, not_4_out);
  and and_4 (and_4_out, not_5_out, not_6_out, TickIN);
  and and_5 (and_5_out, not_7_out, IN0, not_8_out);
  or or_1 (OUT1, and_2_out, and_3_out);
  or or_2 (OUT0, and_4_out, and_5_out);
endmodule

module zeroFive (
  input  IN2,
  input  IN1,
  input  IN0,
  input  TickIN,
  output TickOUT,
  output OUT2,
  output OUT1,
  output OUT0
);

  wire and_1_out, and_2_out, and_3_out, and_4_out, and_5_out, and_6_out, and_7_out, nand_1_out, nand_2_out,
       nand_3_out, nand_4_out, nand_5_out, nand_6_out, nand_7_out, nand_8_out, nand_9_out, nand_10_out,
       nand_11_out, nand_12_out, not_1_out, not_2_out, not_3_out, not_4_out, not_5_out, not_6_out, not_7_out,
       not_8_out, not_9_out, not_10_out, not_11_out, not_12_out, not_13_out, not_14_out;

  not not_1 (not_1_out, IN2);
  not not_2 (not_2_out, IN1);
  not not_3 (not_3_out, IN2);
  not not_4 (not_4_out, IN0);
  not not_5 (not_5_out, IN2);
  not not_6 (not_6_out, TickIN);
  not not_7 (not_7_out, IN2);
  not not_8 (not_8_out, IN0);
  not not_9 (not_9_out, IN1);
  not not_10 (not_10_out, IN0);
  not not_11 (not_11_out, IN2);
  not not_12 (not_12_out, TickIN);
  not not_13 (not_13_out, IN1);
  not not_14 (not_14_out, TickIN);
  nand nand_1 (nand_1_out, IN1, IN1);
  nand nand_2 (nand_2_out, IN1, IN1);
  nand nand_3 (nand_3_out, IN2, IN2);
  nand nand_4 (nand_4_out, IN1, IN1);
  nand nand_5 (nand_5_out, IN0, IN0);
  nand nand_6 (nand_6_out, IN1, IN1);
  nand nand_7 (nand_7_out, TickIN, TickIN);
  and and_1 (and_1_out, not_1_out, not_2_out, IN0, TickIN);
  and and_2 (and_2_out, not_3_out, IN1, not_4_out);
  and and_3 (and_3_out, not_5_out, IN1, not_6_out);
  and and_4 (and_4_out, not_7_out, not_8_out, TickIN);
  and and_5 (and_5_out, not_9_out, not_10_out, TickIN);
  and and_6 (and_6_out, not_11_out, IN0, not_12_out);
  and and_7 (and_7_out, not_13_out, IN0, not_14_out);
  nand nand_8 (nand_8_out, TickIN, IN2, nand_1_out, IN0);
  nand nand_9 (nand_9_out, TickIN, IN2, nand_2_out, IN0);
  nand nand_10 (nand_10_out, nand_3_out, IN1, IN0, TickIN);
  nand nand_11 (nand_11_out, IN2, nand_4_out, nand_5_out);
  nand nand_12 (nand_12_out, IN2, nand_6_out, nand_7_out);
  or or_1 (OUT1, and_1_out, and_2_out, and_3_out);
  or or_2 (OUT0, and_4_out, and_5_out, and_6_out, and_7_out);
  nand nand_13 (TickOUT, nand_8_out, nand_9_out);
  nand nand_14 (OUT2, nand_10_out, nand_11_out, nand_12_out);
endmodule

module zeroNine (
  input  IN3,
  input  IN2,
  input  IN1,
  input  IN0,
  input  TickIN,
  output TickOUT,
  output OUT3,
  output OUT2,
  output OUT1,
  output OUT0
);

  wire nand_1_out, nand_2_out, nand_3_out, nand_4_out, nand_5_out, nand_6_out, nand_7_out, nand_8_out,
       nand_9_out, nand_10_out, nand_11_out, nand_12_out, nand_13_out, nand_14_out, nand_15_out, nand_16_out,
       nand_17_out, nand_18_out, nand_19_out, nand_20_out, nand_21_out, nand_22_out, nand_23_out,
       nand_24_out, nand_25_out, nand_26_out, nand_27_out, nand_28_out, nand_29_out, nand_30_out,
       nand_31_out, nand_32_out, nand_33_out, nand_34_out, nand_35_out, nand_36_out, nand_37_out,
       nand_38_out, nand_39_out, nand_40_out, nand_41_out, nand_42_out, nand_43_out, nand_44_out,
       nand_45_out, nand_46_out, nand_47_out, nand_48_out, nand_49_out, nand_50_out, nand_51_out;

  nand nand_1 (nand_1_out, IN2, IN2);
  nand nand_2 (nand_2_out, IN1, IN1);
  nand nand_3 (nand_3_out, IN2, IN2);
  nand nand_4 (nand_4_out, IN1, IN1);
  nand nand_5 (nand_5_out, TickIN, TickIN);
  nand nand_6 (nand_6_out, IN2, IN2);
  nand nand_7 (nand_7_out, IN1, IN1);
  nand nand_8 (nand_8_out, IN2, IN2);
  nand nand_9 (nand_9_out, IN1, IN1);
  nand nand_10 (nand_10_out, IN0, IN0);
  nand nand_11 (nand_11_out, IN3, IN3);
  nand nand_12 (nand_12_out, IN3, IN3);
  nand nand_13 (nand_13_out, IN2, IN2);
  nand nand_14 (nand_14_out, IN3, IN3);
  nand nand_15 (nand_15_out, IN1, IN1);
  nand nand_16 (nand_16_out, IN3, IN3);
  nand nand_17 (nand_17_out, IN0, IN0);
  nand nand_18 (nand_18_out, IN3, IN3);
  nand nand_19 (nand_19_out, TickIN, TickIN);
  nand nand_20 (nand_20_out, IN3, IN3);
  nand nand_21 (nand_21_out, IN1, IN1);
  nand nand_22 (nand_22_out, IN3, IN3);
  nand nand_23 (nand_23_out, IN0, IN0);
  nand nand_24 (nand_24_out, IN3, IN3);
  nand nand_25 (nand_25_out, TickIN, TickIN);
  nand nand_26 (nand_26_out, IN3, IN3);
  nand nand_27 (nand_27_out, IN0, IN0);
  nand nand_28 (nand_28_out, IN2, IN2);
  nand nand_29 (nand_29_out, IN1, IN1);
  nand nand_30 (nand_30_out, IN0, IN0);
  nand nand_31 (nand_31_out, IN3, IN3);
  nand nand_32 (nand_32_out, TickIN, TickIN);
  nand nand_33 (nand_33_out, IN2, IN2);
  nand nand_34 (nand_34_out, IN1, IN1);
  nand nand_35 (nand_35_out, TickIN, TickIN);
  nand nand_36 (nand_36_out, IN3, nand_1_out, nand_2_out, IN0, TickIN);
  nand nand_37 (nand_37_out, IN3, nand_3_out, nand_4_out, IN0, TickIN);
  nand nand_38 (nand_38_out, nand_5_out, IN3, nand_6_out, nand_7_out);
  nand nand_39 (nand_39_out, IN3, nand_8_out, nand_9_out, nand_10_out);
  nand nand_40 (nand_40_out, TickIN, nand_11_out, IN2, IN1, IN0);
  nand nand_41 (nand_41_out, nand_12_out, nand_13_out, IN1, IN0, TickIN);
  nand nand_42 (nand_42_out, nand_14_out, IN2, nand_15_out);
  nand nand_43 (nand_43_out, nand_16_out, IN2, nand_17_out);
  nand nand_44 (nand_44_out, nand_18_out, IN2, nand_19_out);
  nand nand_45 (nand_45_out, nand_20_out, nand_21_out, IN0, TickIN);
  nand nand_46 (nand_46_out, nand_22_out, IN1, nand_23_out);
  nand nand_47 (nand_47_out, nand_24_out, IN1, nand_25_out);
  nand nand_48 (nand_48_out, nand_26_out, nand_27_out, TickIN);
  nand nand_49 (nand_49_out, nand_28_out, nand_29_out, nand_30_out, TickIN);
  nand nand_50 (nand_50_out, nand_31_out, IN0, nand_32_out);
  nand nand_51 (nand_51_out, nand_33_out, nand_34_out, IN0, nand_35_out);
  nand nand_52 (TickOUT, nand_36_out, nand_37_out);
  nand nand_53 (OUT3, nand_38_out, nand_39_out, nand_40_out);
  nand nand_54 (OUT2, nand_41_out, nand_42_out, nand_43_out, nand_44_out);
  nand nand_55 (OUT1, nand_45_out, nand_46_out, nand_47_out);
  nand nand_56 (OUT0, nand_48_out, nand_49_out, nand_50_out, nand_51_out);
endmodule

module zeroNineHour (
  input  H,
  input  IN3,
  input  IN2,
  input  IN1,
  input  IN0,
  input  TickIN,
  output TickOUT,
  output OUT3,
  output OUT2,
  output OUT1,
  output OUT0
);

  wire and_1_out, and_2_out, and_3_out, and_4_out, and_5_out, and_6_out, and_7_out, and_8_out, and_9_out,
       and_10_out, and_11_out, and_12_out, and_13_out, and_14_out, and_15_out, and_16_out, and_17_out,
       and_18_out, and_19_out, and_20_out, and_21_out, not_1_out, not_2_out, not_3_out, not_4_out, not_5_out,
       not_6_out, not_7_out, not_8_out, not_9_out, not_10_out, not_11_out, not_12_out, not_13_out,
       not_14_out, not_15_out, not_16_out, not_17_out, not_18_out, not_19_out, not_20_out, not_21_out,
       not_22_out, not_23_out, not_24_out, not_25_out, not_26_out, not_27_out, not_28_out, not_29_out,
       not_30_out, not_31_out, not_32_out, not_33_out, not_34_out, not_35_out, not_36_out, not_37_out,
       not_38_out, not_39_out, not_40_out, not_41_out, not_42_out, not_43_out, not_44_out;

  not not_1 (not_1_out, H);
  not not_2 (not_2_out, IN3);
  not not_3 (not_3_out, IN2);
  not not_4 (not_4_out, H);
  not not_5 (not_5_out, H);
  not not_6 (not_6_out, IN0);
  not not_7 (not_7_out, H);
  not not_8 (not_8_out, TickIN);
  not not_9 (not_9_out, H);
  not not_10 (not_10_out, IN2);
  not not_11 (not_11_out, H);
  not not_12 (not_12_out, IN1);
  not not_13 (not_13_out, H);
  not not_14 (not_14_out, IN0);
  not not_15 (not_15_out, H);
  not not_16 (not_16_out, TickIN);
  not not_17 (not_17_out, H);
  not not_18 (not_18_out, IN3);
  not not_19 (not_19_out, IN1);
  not not_20 (not_20_out, IN3);
  not not_21 (not_21_out, IN2);
  not not_22 (not_22_out, IN1);
  not not_23 (not_23_out, H);
  not not_24 (not_24_out, IN0);
  not not_25 (not_25_out, H);
  not not_26 (not_26_out, TickIN);
  not not_27 (not_27_out, IN3);
  not not_28 (not_28_out, IN2);
  not not_29 (not_29_out, IN0);
  not not_30 (not_30_out, IN3);
  not not_31 (not_31_out, IN2);
  not not_32 (not_32_out, TickIN);
  not not_33 (not_33_out, H);
  not not_34 (not_34_out, H);
  not not_35 (not_35_out, IN0);
  not not_36 (not_36_out, IN3);
  not not_37 (not_37_out, IN2);
  not not_38 (not_38_out, IN0);
  not not_39 (not_39_out, H);
  not not_40 (not_40_out, TickIN);
  not not_41 (not_41_out, IN3);
  not not_42 (not_42_out, IN2);
  not not_43 (not_43_out, TickIN);
  not not_44 (not_44_out, H);
  and and_1 (and_1_out, not_1_out, IN3, IN0, TickIN);
  and and_2 (and_2_out, H, not_2_out, not_3_out, IN1, IN0, TickIN);
  and and_3 (and_3_out, not_4_out, IN2, IN1, IN0, TickIN);
  and and_4 (and_4_out, not_5_out, IN3, not_6_out);
  and and_5 (and_5_out, not_7_out, IN3, not_8_out);
  and and_6 (and_6_out, not_9_out, not_10_out, IN1, IN0, TickIN);
  and and_7 (and_7_out, not_11_out, IN2, not_12_out);
  and and_8 (and_8_out, not_13_out, IN2, not_14_out);
  and and_9 (and_9_out, not_15_out, IN2, not_16_out);
  and and_10 (and_10_out, not_17_out, not_18_out, not_19_out, IN0, TickIN);
  and and_11 (and_11_out, not_20_out, not_21_out, not_22_out, IN0, TickIN);
  and and_12 (and_12_out, not_23_out, IN1, not_24_out);
  and and_13 (and_13_out, not_25_out, IN1, not_26_out);
  and and_14 (and_14_out, not_27_out, not_28_out, IN1, not_29_out);
  and and_15 (and_15_out, not_30_out, not_31_out, IN1, not_32_out);
  and and_16 (and_16_out, not_33_out, IN3, IN2);
  and and_17 (and_17_out, not_34_out, not_35_out, TickIN);
  and and_18 (and_18_out, not_36_out, not_37_out, not_38_out, TickIN);
  and and_19 (and_19_out, not_39_out, IN0, not_40_out);
  and and_20 (and_20_out, not_41_out, not_42_out, IN0, not_43_out);
  and and_21 (and_21_out, not_44_out, IN3, IN2);
  or or_1 (TickOUT, and_1_out, and_2_out);
  or or_2 (OUT3, and_3_out, and_4_out, and_5_out);
  or or_3 (OUT2, and_6_out, and_7_out, and_8_out, and_9_out);
  or or_4 (OUT1, and_10_out, and_11_out, and_12_out, and_13_out, and_14_out, and_15_out, and_16_out);
  or or_5 (OUT0, and_17_out, and_18_out, and_19_out, and_20_out, and_21_out);
endmodule

module zeroTwentythree (
  input  TickIN,
  input  [3:0] loadT_4,
  input  loadTEnDi,
  input  [3:0] loadU_4,
  input  loadUEnDi,
  input  CLK2k,
  input  RESET,
  output TickOUT,
  output [3:0] curT_4,
  output [3:0] curU_4
);

  wire and_1_out, and_2_out, and_3_out, and_4_out, and_5_out, and_6_out, and_7_out, load_2_1_out0,
       load_2_1_out1, load_4_1_out0, load_4_1_out1, load_4_1_out2, load_4_1_out3, zeroNineHour_1_out0,
       zeroNineHour_1_out1, zeroNineHour_1_out2, zeroNineHour_1_out3, zeroNineHour_1_tickout, zeroTwo_1_out0,
       zeroTwo_1_out1;
  wire [1:0] d_ff_2_q;

  and and_1 (and_1_out, d_ff_2_q[1], ~d_ff_2_q[0]);  // AND_Gate
  zeroTwo zeroTwo_1 (
    .IN1(d_ff_2_q[1]), .IN0(d_ff_2_q[0]), .TickIN(zeroNineHour_1_tickout), .TickOUT(TickOUT),
    .OUT1(zeroTwo_1_out1), .OUT0(zeroTwo_1_out0));
  zeroNineHour zeroNineHour_1 (
    .H(and_1_out), .IN3(curU_4[3]), .IN2(curU_4[2]), .IN1(curU_4[1]), .IN0(curU_4[0]), .TickIN(TickIN),
    .TickOUT(zeroNineHour_1_tickout), .OUT3(zeroNineHour_1_out3), .OUT2(zeroNineHour_1_out2),
    .OUT1(zeroNineHour_1_out1), .OUT0(zeroNineHour_1_out0));
  load_2 load_2_1 (
    .IN1(zeroTwo_1_out1), .IN0(zeroTwo_1_out0), .loadValue(loadT_4), .loadEnDi(loadTEnDi),
    .OUT1(load_2_1_out1), .OUT0(load_2_1_out0));
  load_4 load_4_1 (
    .IN3(zeroNineHour_1_out3), .IN2(zeroNineHour_1_out2), .IN1(zeroNineHour_1_out1),
    .IN0(zeroNineHour_1_out0), .loadValue(loadU_4), .loadEnDi(loadUEnDi), .OUT3(load_4_1_out3),
    .OUT2(load_4_1_out2), .OUT1(load_4_1_out1), .OUT0(load_4_1_out0));
  and and_2 (and_2_out, ~RESET, load_2_1_out1);  // AND_Gate
  and and_3 (and_3_out, ~RESET, load_2_1_out0);  // AND_Gate
  and and_4 (and_4_out, ~RESET, load_4_1_out3);  // AND_Gate
  and and_5 (and_5_out, ~RESET, load_4_1_out2);  // AND_Gate
  and and_6 (and_6_out, ~RESET, load_4_1_out1);  // AND_Gate
  and and_7 (and_7_out, ~RESET, load_4_1_out0);  // AND_Gate
  D_Flip_Flop d_ff_1 (.D(and_2_out), .clk(CLK2k), .Q(d_ff_2_q[1]), .reset(RESET));  // open: Qn, preset
  D_Flip_Flop d_ff_2 (.D(and_3_out), .clk(CLK2k), .Q(d_ff_2_q[0]), .reset(RESET));  // open: Qn, preset
  D_Flip_Flop d_ff_3 (.D(and_4_out), .clk(CLK2k), .Q(curU_4[3]), .reset(RESET));  // open: Qn, preset
  D_Flip_Flop d_ff_4 (.D(and_5_out), .clk(CLK2k), .Q(curU_4[2]), .reset(RESET));  // open: Qn, preset
  D_Flip_Flop d_ff_5 (.D(and_6_out), .clk(CLK2k), .Q(curU_4[1]), .reset(RESET));  // open: Qn, preset
  D_Flip_Flop d_ff_6 (.D(and_7_out), .clk(CLK2k), .Q(curU_4[0]), .reset(RESET));  // open: Qn, preset
  assign curT_4 = {{2{1'b0}}, d_ff_2_q};  // Bit_Extender bit_extender_1
endmodule

module zeroFiftynine (
  input  TickIN,
  input  [3:0] loadT_4,
  input  loadTEnDi,
  input  [3:0] loadU_4,
  input  loadUEnDi,
  input  CLK2k,
  input  RESET,
  output TickOUT,
  output [3:0] curT_4,
  output [3:0] curU_4
);

  wire and_1_out, and_2_out, and_3_out, and_4_out, and_5_out, and_6_out, and_7_out, load_3_1_out0,
       load_3_1_out1, load_3_1_out2, load_4_1_out0, load_4_1_out1, load_4_1_out2, load_4_1_out3,
       zeroFive_1_out0, zeroFive_1_out1, zeroFive_1_out2, zeroNine_1_out0, zeroNine_1_out1, zeroNine_1_out2,
       zeroNine_1_out3, zeroNine_1_tickout;
  wire [2:0] d_ff_3_q;

  zeroFive zeroFive_1 (
    .IN2(d_ff_3_q[2]), .IN1(d_ff_3_q[1]), .IN0(d_ff_3_q[0]), .TickIN(zeroNine_1_tickout), .TickOUT(TickOUT),
    .OUT2(zeroFive_1_out2), .OUT1(zeroFive_1_out1), .OUT0(zeroFive_1_out0));
  zeroNine zeroNine_1 (
    .IN3(curU_4[3]), .IN2(curU_4[2]), .IN1(curU_4[1]), .IN0(curU_4[0]), .TickIN(TickIN),
    .TickOUT(zeroNine_1_tickout), .OUT3(zeroNine_1_out3), .OUT2(zeroNine_1_out2), .OUT1(zeroNine_1_out1),
    .OUT0(zeroNine_1_out0));
  load_3 load_3_1 (
    .IN2(zeroFive_1_out2), .IN1(zeroFive_1_out1), .IN0(zeroFive_1_out0), .loadValue(loadT_4),
    .loadEnDi(loadTEnDi), .OUT2(load_3_1_out2), .OUT1(load_3_1_out1), .OUT0(load_3_1_out0));
  load_4 load_4_1 (
    .IN3(zeroNine_1_out3), .IN2(zeroNine_1_out2), .IN1(zeroNine_1_out1), .IN0(zeroNine_1_out0),
    .loadValue(loadU_4), .loadEnDi(loadUEnDi), .OUT3(load_4_1_out3), .OUT2(load_4_1_out2),
    .OUT1(load_4_1_out1), .OUT0(load_4_1_out0));
  and and_1 (and_1_out, ~RESET, load_3_1_out2);  // AND_Gate
  and and_2 (and_2_out, ~RESET, load_3_1_out1);  // AND_Gate
  and and_3 (and_3_out, ~RESET, load_3_1_out0);  // AND_Gate
  and and_4 (and_4_out, ~RESET, load_4_1_out3);  // AND_Gate
  and and_5 (and_5_out, ~RESET, load_4_1_out2);  // AND_Gate
  and and_6 (and_6_out, ~RESET, load_4_1_out1);  // AND_Gate
  and and_7 (and_7_out, ~RESET, load_4_1_out0);  // AND_Gate
  D_Flip_Flop d_ff_1 (.D(and_1_out), .clk(CLK2k), .Q(d_ff_3_q[2]), .reset(RESET));  // open: Qn, preset
  D_Flip_Flop d_ff_2 (.D(and_2_out), .clk(CLK2k), .Q(d_ff_3_q[1]), .reset(RESET));  // open: Qn, preset
  D_Flip_Flop d_ff_3 (.D(and_3_out), .clk(CLK2k), .Q(d_ff_3_q[0]), .reset(RESET));  // open: Qn, preset
  D_Flip_Flop d_ff_4 (.D(and_4_out), .clk(CLK2k), .Q(curU_4[3]), .reset(RESET));  // open: Qn, preset
  D_Flip_Flop d_ff_5 (.D(and_5_out), .clk(CLK2k), .Q(curU_4[2]), .reset(RESET));  // open: Qn, preset
  D_Flip_Flop d_ff_6 (.D(and_6_out), .clk(CLK2k), .Q(curU_4[1]), .reset(RESET));  // open: Qn, preset
  D_Flip_Flop d_ff_7 (.D(and_7_out), .clk(CLK2k), .Q(curU_4[0]), .reset(RESET));  // open: Qn, preset
  assign curT_4 = {{1{1'b0}}, d_ff_3_q};  // Bit_Extender bit_extender_1
endmodule

module clk2k_to_ticksec (
  input  RESET,
  input  CLK2k,
  output TickSEC
);

  Counter #(.width(10), .max('h3e9)) counter_1 (
    .clr(RESET), .clk(CLK2k), .carry(TickSEC));  // open: load, up, count, D, Q
endmodule

module HOUR (
  input  RESET,
  input  CLK2k,
  input  [3:0] HloadT_4,
  input  HloadTEnDi,
  input  [3:0] HloadU_4,
  input  HloadUEnDi,
  input  [3:0] MINloadT_4,
  input  MINloadTEnDi,
  input  [3:0] MINloadU_4,
  input  MINloadUEnDi,
  input  [3:0] SECloadT_4,
  input  SECloadTEnDi,
  input  [3:0] SECloadU_4,
  input  SECloadUEnDi,
  output [3:0] HT_4,
  output [3:0] HU_4,
  output [3:0] MINT_4,
  output [3:0] MINU_4,
  output [3:0] SECT_4,
  output [3:0] SECU_4,
  output HloadT,
  output HloadU,
  output MINloadT,
  output MINloadU,
  output SECloadT,
  output SECloadU
);

  wire clk2k_to_ticksec_1_ticksec, min_tickout, sec_tickout;

  clk2k_to_ticksec clk2k_to_ticksec_1 (.RESET(RESET), .CLK2k(CLK2k), .TickSEC(clk2k_to_ticksec_1_ticksec));
  zeroTwentythree hour_1 (
    .TickIN(min_tickout), .loadT_4(HloadT_4), .loadTEnDi(HloadTEnDi), .loadU_4(HloadU_4),
    .loadUEnDi(HloadUEnDi), .CLK2k(CLK2k), .RESET(RESET), .curT_4(HT_4), .curU_4(HU_4));  // open: TickOUT
  zeroFiftynine min (
    .TickIN(sec_tickout), .loadT_4(MINloadT_4), .loadTEnDi(MINloadTEnDi), .loadU_4(MINloadU_4),
    .loadUEnDi(MINloadUEnDi), .CLK2k(CLK2k), .RESET(RESET), .TickOUT(min_tickout), .curT_4(MINT_4),
    .curU_4(MINU_4));
  zeroFiftynine sec (
    .TickIN(clk2k_to_ticksec_1_ticksec), .loadT_4(SECloadT_4), .loadTEnDi(SECloadTEnDi),
    .loadU_4(SECloadU_4), .loadUEnDi(SECloadUEnDi), .CLK2k(CLK2k), .RESET(RESET), .TickOUT(sec_tickout),
    .curT_4(SECT_4), .curU_4(SECU_4));

  assign HloadT = HloadTEnDi;
  assign HloadU = HloadUEnDi;
  assign MINloadT = MINloadTEnDi;
  assign MINloadU = MINloadUEnDi;
  assign SECloadT = SECloadTEnDi;
  assign SECloadU = SECloadUEnDi;
endmodule

module hourView_HMS (
  input  [3:0] HT_4,
  input  [3:0] HU_4,
  input  [3:0] MINT_4,
  input  [3:0] MINU_4,
  input  [3:0] SECT_4,
  input  [3:0] SECU_4,
  input  HloadT,
  input  HloadU,
  input  MINloadT,
  input  MINloadU,
  input  SECloadT,
  input  SECloadU,
  input  RESET,
  input  CLK4,
  output [7:0] sevsegCode_5,
  output [7:0] sevsegCode_4,
  output [7:0] sevsegCode_3,
  output [7:0] sevsegCode_2,
  output [7:0] sevsegCode_1,
  output [7:0] sevsegCode_0
);

  wire and_1_out, and_2_out, and_3_out, and_4_out, and_5_out, and_6_out, or_1_out, t_ff_1_q;
  wire [6:0] bit_extender_2_out, bit_extender_4_out, multiplexer_2_out, multiplexer_4_out;
  wire [7:0] bit_extender_1_out, bit_extender_3_out, bit_extender_5_out, bit_extender_6_out;

  assign bit_extender_1_out = {{4{1'b0}}, HT_4};  // Bit_Extender bit_extender_1
  assign bit_extender_2_out = {{3{1'b0}}, HU_4};  // Bit_Extender bit_extender_2
  assign bit_extender_3_out = {{4{1'b0}}, MINT_4};  // Bit_Extender bit_extender_3
  assign bit_extender_4_out = {{3{1'b0}}, MINU_4};  // Bit_Extender bit_extender_4
  assign bit_extender_5_out = {{4{1'b0}}, SECT_4};  // Bit_Extender bit_extender_5
  assign bit_extender_6_out = {{4{1'b0}}, SECU_4};  // Bit_Extender bit_extender_6
  T_Flip_Flop t_ff_1 (.T(or_1_out), .clk(CLK4), .Q(t_ff_1_q), .reset(RESET));  // open: Qn, preset
  or or_1 (or_1_out, HloadT, HloadU, MINloadT, MINloadU, SECloadT, SECloadU);
  Multiplexer #(.width(8), .enable("false")) multiplexer_1 (
    .in0(bit_extender_1_out), .in1(8'h7f), .out(sevsegCode_5), .sel(and_1_out));
  and and_1 (and_1_out, HloadT, t_ff_1_q);
  and and_2 (and_2_out, HloadU, t_ff_1_q);
  Multiplexer #(.width(7), .enable("false")) multiplexer_2 (
    .in0(bit_extender_2_out), .in1({7{1'b1}}), .out(multiplexer_2_out), .sel(and_2_out));
  Multiplexer #(.width(8), .enable("false")) multiplexer_3 (
    .in0(bit_extender_3_out), .in1(8'h7f), .out(sevsegCode_3), .sel(and_3_out));
  and and_3 (and_3_out, MINloadT, t_ff_1_q);
  Multiplexer #(.width(7), .enable("false")) multiplexer_4 (
    .in0(bit_extender_4_out), .in1({7{1'b1}}), .out(multiplexer_4_out), .sel(and_4_out));
  and and_4 (and_4_out, MINloadU, t_ff_1_q);
  assign sevsegCode_4 = {{1{1'b1}}, multiplexer_2_out};  // Bit_Extender bit_extender_7
  assign sevsegCode_2 = {{1{1'b1}}, multiplexer_4_out};  // Bit_Extender bit_extender_8
  Multiplexer #(.width(8), .enable("false")) multiplexer_5 (
    .in0(bit_extender_5_out), .in1(8'h7f), .out(sevsegCode_1), .sel(and_5_out));
  and and_5 (and_5_out, SECloadT, t_ff_1_q);
  Multiplexer #(.width(8), .enable("false")) multiplexer_6 (
    .in0(bit_extender_6_out), .in1(8'h7f), .out(sevsegCode_0), .sel(and_6_out));
  and and_6 (and_6_out, SECloadU, t_ff_1_q);
endmodule

module hourView_HM_reverse (
  input  [7:0] sevsegCode_5,
  input  [7:0] sevsegCode_4,
  input  [7:0] sevsegCode_3,
  input  [7:0] sevsegCode_2,
  output [3:0] HT_4,
  output [3:0] HU_4,
  output [3:0] MINT_4,
  output [3:0] MINU_4
);

  Bit_Extender #(.out_width(4)) bit_extender_1 (.in(sevsegCode_5), .out(HT_4));
  Bit_Extender #(.out_width(4)) bit_extender_2 (.in(sevsegCode_4), .out(HU_4));
  Bit_Extender #(.out_width(4)) bit_extender_3 (.in(sevsegCode_3), .out(MINT_4));
  Bit_Extender #(.out_width(4)) bit_extender_4 (.in(sevsegCode_2), .out(MINU_4));
endmodule

module hourView_HMS_reverse (
  input  [7:0] sevsegCode_5,
  input  [7:0] sevsegCode_4,
  input  [7:0] sevsegCode_3,
  input  [7:0] sevsegCode_2,
  input  [7:0] sevsegCode_1,
  input  [7:0] sevsegCode_0,
  output [3:0] HT_4,
  output [3:0] HU_4,
  output [3:0] MINT_4,
  output [3:0] MINU_4,
  output [3:0] SECT_4,
  output [3:0] SECU_4
);

  Bit_Extender #(.out_width(4)) bit_extender_1 (.in(sevsegCode_5), .out(HT_4));
  Bit_Extender #(.out_width(4)) bit_extender_2 (.in(sevsegCode_4), .out(HU_4));
  Bit_Extender #(.out_width(4)) bit_extender_3 (.in(sevsegCode_3), .out(MINT_4));
  Bit_Extender #(.out_width(4)) bit_extender_4 (.in(sevsegCode_2), .out(MINU_4));
  Bit_Extender #(.out_width(4)) bit_extender_5 (.in(sevsegCode_1), .out(SECT_4));
  Bit_Extender #(.out_width(4)) bit_extender_6 (.in(sevsegCode_0), .out(SECU_4));
endmodule

module hourView_HMS_Ltime (
  input  [3:0] HT_4,
  input  [3:0] HU_4,
  input  [3:0] MINT_4,
  input  [3:0] MINU_4,
  input  [3:0] SECT_4,
  input  [3:0] SECU_4,
  output [7:0] sevsegCode_5,
  output [7:0] sevsegCode_4,
  output [7:0] sevsegCode_3,
  output [7:0] sevsegCode_2,
  output [7:0] sevsegCode_1,
  output [7:0] sevsegCode_0
);

  wire [6:0] bit_extender_2_out, bit_extender_4_out;

  assign sevsegCode_5 = {{4{1'b0}}, HT_4};  // Bit_Extender bit_extender_1
  assign bit_extender_2_out = {{3{1'b0}}, HU_4};  // Bit_Extender bit_extender_2
  assign sevsegCode_3 = {{4{1'b0}}, MINT_4};  // Bit_Extender bit_extender_3
  assign bit_extender_4_out = {{3{1'b0}}, MINU_4};  // Bit_Extender bit_extender_4
  assign sevsegCode_1 = {{4{1'b0}}, SECT_4};  // Bit_Extender bit_extender_5
  assign sevsegCode_0 = {{4{1'b0}}, SECU_4};  // Bit_Extender bit_extender_6
  assign sevsegCode_4 = {{1{1'b1}}, bit_extender_2_out};  // Bit_Extender bit_extender_7
  assign sevsegCode_2 = {{1{1'b1}}, bit_extender_4_out};  // Bit_Extender bit_extender_8
endmodule

module load_2 (
  input  IN1,
  input  IN0,
  input  [3:0] loadValue,
  input  loadEnDi,
  output OUT1,
  output OUT0
);

  wire [1:0] bit_extender_1_out;

  Bit_Extender #(.in_width(4), .out_width(2), .\type ("zero")) bit_extender_1 (
    .in(loadValue), .out(bit_extender_1_out));
  Multiplexer #(.enable("false")) multiplexer_1 (.in0(IN1), .in1(bit_extender_1_out[1]), .out(OUT1), .sel(loadEnDi));
  Multiplexer #(.enable("false")) multiplexer_2 (.in0(IN0), .in1(bit_extender_1_out[0]), .out(OUT0), .sel(loadEnDi));
endmodule

module load_3 (
  input  IN2,
  input  IN1,
  input  IN0,
  input  [3:0] loadValue,
  input  loadEnDi,
  output OUT2,
  output OUT1,
  output OUT0
);

  wire [2:0] bit_extender_1_out;

  Bit_Extender #(.in_width(4), .out_width(3), .\type ("zero")) bit_extender_1 (
    .in(loadValue), .out(bit_extender_1_out));
  Multiplexer #(.enable("false")) multiplexer_1 (.in0(IN2), .in1(bit_extender_1_out[2]), .out(OUT2), .sel(loadEnDi));
  Multiplexer #(.enable("false")) multiplexer_2 (.in0(IN1), .in1(bit_extender_1_out[1]), .out(OUT1), .sel(loadEnDi));
  Multiplexer #(.enable("false")) multiplexer_3 (.in0(IN0), .in1(bit_extender_1_out[0]), .out(OUT0), .sel(loadEnDi));
endmodule

module load_4 (
  input  IN3,
  input  IN2,
  input  IN1,
  input  IN0,
  input  [3:0] loadValue,
  input  loadEnDi,
  output OUT3,
  output OUT2,
  output OUT1,
  output OUT0
);

  Multiplexer #(.enable("false")) multiplexer_1 (.in0(IN3), .in1(loadValue[3]), .out(OUT3), .sel(loadEnDi));
  Multiplexer #(.enable("false")) multiplexer_2 (.in0(IN2), .in1(loadValue[2]), .out(OUT2), .sel(loadEnDi));
  Multiplexer #(.enable("false")) multiplexer_3 (.in0(IN1), .in1(loadValue[1]), .out(OUT1), .sel(loadEnDi));
  Multiplexer #(.enable("false")) multiplexer_4 (.in0(IN0), .in1(loadValue[0]), .out(OUT0), .sel(loadEnDi));
endmodule

module changeHour (
  input  [1:0] B1_B0,
  input  ResetSelector,
  input  clk,
  output [3:0] HloadT_4,
  output HloadTEnDi,
  output [3:0] HloadU_4,
  output HloadUEnDi,
  output [3:0] MINloadT_4,
  output MINloadTEnDi,
  output [3:0] MINloadU_4,
  output MINloadUEnDi,
  output [3:0] SECloadT_4,
  output SECloadTEnDi,
  output [3:0] SECloadU_4,
  output SECloadUEnDi
);

  wire demultiplexer_1_out1, demultiplexer_1_out2, demultiplexer_1_out3, demultiplexer_1_out4,
       demultiplexer_1_out5, demultiplexer_1_out6, demultiplexer_2_out0, or_1_out;
  wire [1:0] counter_2_q, counter_3_q;
  wire [2:0] counter_1_q, counter_5_q, counter_7_q;
  wire [3:0] bit_extender_2_out, counter_4_q;

  Counter #(.width(3), .max('h6)) counter_1 (
    .clr(ResetSelector), .count(B1_B0[0]), .clk(clk), .Q(counter_1_q));  // open: load, up, D, carry
  Demultiplexer #(.select(3), .enable("false")) demultiplexer_1 (
    .out1(demultiplexer_1_out1), .out2(demultiplexer_1_out2), .out3(demultiplexer_1_out3),
    .out4(demultiplexer_1_out4), .out5(demultiplexer_1_out5), .out6(demultiplexer_1_out6), .in(B1_B0[1]),
    .sel(counter_1_q));  // open: out0, out7
  Demultiplexer #(.select(3), .enable("false")) demultiplexer_2 (
    .out0(demultiplexer_2_out0), .out1(HloadTEnDi), .out2(HloadUEnDi), .out3(MINloadTEnDi),
    .out4(MINloadUEnDi), .out5(SECloadTEnDi), .out6(SECloadUEnDi), .in(1'b1), .sel(counter_1_q));  // open: out7
  or or_1 (or_1_out, demultiplexer_2_out0, ResetSelector);
  Counter #(.width(2), .max('h2)) counter_2 (
    .clr(or_1_out), .count(demultiplexer_1_out1), .clk(clk), .Q(counter_2_q));  // open: load, up, D, carry
  assign HloadT_4 = {{2{1'b0}}, counter_2_q};  // Bit_Extender bit_extender_1
  Counter #(.width(2), .max('h3)) counter_3 (
    .clr(or_1_out), .count(demultiplexer_1_out2), .clk(clk), .Q(counter_3_q));  // open: load, up, D, carry
  Counter #(.width(4), .max('h9)) counter_4 (
    .clr(or_1_out), .count(demultiplexer_1_out2), .clk(clk), .Q(counter_4_q));  // open: load, up, D, carry
  Counter #(.width(3), .max('h5)) counter_5 (
    .clr(or_1_out), .count(demultiplexer_1_out3), .clk(clk), .Q(counter_5_q));  // open: load, up, D, carry
  Counter #(.width(4), .max('h9)) counter_6 (
    .clr(or_1_out), .count(demultiplexer_1_out4), .clk(clk), .Q(MINloadU_4));  // open: load, up, D, carry
  Counter #(.width(3), .max('h5)) counter_7 (
    .clr(or_1_out), .count(demultiplexer_1_out5), .clk(clk), .Q(counter_7_q));  // open: load, up, D, carry
  Counter #(.width(4), .max('h9)) counter_8 (
    .clr(or_1_out), .count(demultiplexer_1_out6), .clk(clk), .Q(SECloadU_4));  // open: load, up, D, carry
  assign bit_extender_2_out = {{2{1'b0}}, counter_3_q};  // Bit_Extender bit_extender_2
  assign MINloadT_4 = {{1{1'b0}}, counter_5_q};  // Bit_Extender bit_extender_3
  assign SECloadT_4 = {{1{1'b0}}, counter_7_q};  // Bit_Extender bit_extender_4
  Multiplexer #(.width(4), .enable("false")) multiplexer_1 (
    .in0(counter_4_q), .in1(bit_extender_2_out), .out(HloadU_4), .sel(counter_2_q[1]));
endmodule

module alarm (
  input  RESET,
  input  [1:0] B1_B0,
  input  [7:0] SSDCode_5,
  input  [7:0] SSDCode_4,
  input  [7:0] SSDCode_3,
  input  [7:0] SSDCode_2,
  input  ChM,
  input  CLK32K,
  input  CLK2k,
  input  CLK4,
  output [7:0] sevsegCode_5,
  output [7:0] sevsegCode_4,
  output [7:0] sevsegCode_3,
  output [7:0] sevsegCode_2,
  output [7:0] sevsegCode_1,
  output [7:0] sevsegCode_0,
  output BUZZER
);

  wire alarmHM_1_curonoff, alarmHM_1_hloadt, alarmHM_1_hloadu, alarmHM_1_minloadt, alarmHM_1_minloadu,
       alarmHM_1_onoffl, changeAlarm_1_hloadtendi, changeAlarm_1_hloaduendi, changeAlarm_1_minloadtendi,
       changeAlarm_1_minloaduendi, changeAlarm_1_onoffload, changeAlarm_1_onoffloadendi, compare_1_equal;
  wire [1:0] and_1_out;
  wire [3:0] alarmHM_1_curht_4, alarmHM_1_curhu_4, alarmHM_1_curmint_4, alarmHM_1_curminu_4,
       changeAlarm_1_hloadt_4, changeAlarm_1_hloadu_4, changeAlarm_1_minloadt_4, changeAlarm_1_minloadu_4,
       hourView_HM_reverse_1_ht_4, hourView_HM_reverse_1_hu_4, hourView_HM_reverse_1_mint_4,
       hourView_HM_reverse_1_minu_4;

  and and_1 (and_1_out[0], B1_B0[0], ~ChM);  // AND_Gate
  and and_2 (and_1_out[1], B1_B0[1], ~ChM);  // AND_Gate
  hourView_HM_reverse hourView_HM_reverse_1 (
    .sevsegCode_5(SSDCode_5), .sevsegCode_4(SSDCode_4), .sevsegCode_3(SSDCode_3), .sevsegCode_2(SSDCode_2),
    .HT_4(hourView_HM_reverse_1_ht_4), .HU_4(hourView_HM_reverse_1_hu_4),
    .MINT_4(hourView_HM_reverse_1_mint_4), .MINU_4(hourView_HM_reverse_1_minu_4));
  changeAlarm changeAlarm_1 (
    .B1_B0(and_1_out), .ResetSelector(ChM), .CLK32K(CLK32K), .HloadT_4(changeAlarm_1_hloadt_4),
    .HloadTEnDi(changeAlarm_1_hloadtendi), .HloadU_4(changeAlarm_1_hloadu_4),
    .HloadUEnDi(changeAlarm_1_hloaduendi), .MINloadT_4(changeAlarm_1_minloadt_4),
    .MINloadTEnDi(changeAlarm_1_minloadtendi), .MINloadU_4(changeAlarm_1_minloadu_4),
    .MINloadUEnDi(changeAlarm_1_minloaduendi), .ONOFFload(changeAlarm_1_onoffload),
    .ONOFFloadEnDi(changeAlarm_1_onoffloadendi));
  alarmHM alarmHM_1 (
    .RESET(RESET), .CLK2k(CLK2k), .HloadT_4(changeAlarm_1_hloadt_4), .HloadTEnDi(changeAlarm_1_hloadtendi),
    .HloadU_4(changeAlarm_1_hloadu_4), .HloadUEnDi(changeAlarm_1_hloaduendi),
    .MINloadT_4(changeAlarm_1_minloadt_4), .MINloadTEnDi(changeAlarm_1_minloadtendi),
    .MINloadU_4(changeAlarm_1_minloadu_4), .MINloadUEnDi(changeAlarm_1_minloaduendi),
    .ONOFFload(changeAlarm_1_onoffload), .ONOFFloadEnDi(changeAlarm_1_onoffloadendi),
    .curHT_4(alarmHM_1_curht_4), .curHU_4(alarmHM_1_curhu_4), .curMINT_4(alarmHM_1_curmint_4),
    .curMINU_4(alarmHM_1_curminu_4), .curONOFF(alarmHM_1_curonoff), .HloadT(alarmHM_1_hloadt),
    .HloadU(alarmHM_1_hloadu), .MINloadT(alarmHM_1_minloadt), .MINloadU(alarmHM_1_minloadu),
    .ONOFFL(alarmHM_1_onoffl));
  compare compare_1 (
    .A3_4(alarmHM_1_curht_4), .A2_4(alarmHM_1_curhu_4), .A1_4(alarmHM_1_curmint_4),
    .A0_4(alarmHM_1_curminu_4), .B3_4(hourView_HM_reverse_1_ht_4), .B2_4(hourView_HM_reverse_1_hu_4),
    .B1_4(hourView_HM_reverse_1_mint_4), .B0_4(hourView_HM_reverse_1_minu_4), .EQUAL(compare_1_equal));
  alarmView_HM alarmView_HM_1 (
    .HT_4(alarmHM_1_curht_4), .HU_4(alarmHM_1_curhu_4), .MINT_4(alarmHM_1_curmint_4),
    .MINU_4(alarmHM_1_curminu_4), .curONOFF(alarmHM_1_curonoff), .HloadT(alarmHM_1_hloadt),
    .HloadU(alarmHM_1_hloadu), .MINloadT(alarmHM_1_minloadt), .MINloadU(alarmHM_1_minloadu),
    .ONOFFload(alarmHM_1_onoffl), .EQUAL(compare_1_equal), .RESET(RESET), .CLK4(CLK4),
    .sevsegCode_5(sevsegCode_5), .sevsegCode_4(sevsegCode_4), .sevsegCode_3(sevsegCode_3),
    .sevsegCode_2(sevsegCode_2), .sevsegCode_1(sevsegCode_1), .sevsegCode_0(sevsegCode_0), .BUZZER(BUZZER));
endmodule

module changeAlarm (
  input  [1:0] B1_B0,
  input  ResetSelector,
  input  CLK32K,
  output [3:0] HloadT_4,
  output HloadTEnDi,
  output [3:0] HloadU_4,
  output HloadUEnDi,
  output [3:0] MINloadT_4,
  output MINloadTEnDi,
  output [3:0] MINloadU_4,
  output MINloadUEnDi,
  output ONOFFload,
  output ONOFFloadEnDi
);

  wire demultiplexer_1_out1, demultiplexer_1_out2, demultiplexer_1_out3, demultiplexer_1_out4,
       demultiplexer_1_out5, demultiplexer_2_out0, or_1_out;
  wire [1:0] counter_2_q, counter_3_q;
  wire [2:0] counter_1_q, counter_5_q;
  wire [3:0] bit_extender_2_out, counter_4_q;

  Counter #(.width(3), .max('h5)) counter_1 (
    .clr(ResetSelector), .count(B1_B0[0]), .clk(CLK32K), .Q(counter_1_q));  // open: load, up, D, carry
  Demultiplexer #(.select(3), .enable("false")) demultiplexer_1 (
    .out1(demultiplexer_1_out1), .out2(demultiplexer_1_out2), .out3(demultiplexer_1_out3),
    .out4(demultiplexer_1_out4), .out5(demultiplexer_1_out5), .in(B1_B0[1]), .sel(counter_1_q));  // open: out0, out6, out7
  Demultiplexer #(.select(3), .enable("false")) demultiplexer_2 (
    .out0(demultiplexer_2_out0), .out1(HloadTEnDi), .out2(HloadUEnDi), .out3(MINloadTEnDi),
    .out4(MINloadUEnDi), .out5(ONOFFloadEnDi), .in(1'b1), .sel(counter_1_q));  // open: out6, out7
  or or_1 (or_1_out, demultiplexer_2_out0, ResetSelector);
  Counter #(.width(2), .max('h2)) counter_2 (
    .clr(or_1_out), .count(demultiplexer_1_out1), .clk(CLK32K), .Q(counter_2_q));  // open: load, up, D, carry
  Counter #(.width(2), .max('h3)) counter_3 (
    .clr(or_1_out), .count(demultiplexer_1_out2), .clk(CLK32K), .Q(counter_3_q));  // open: load, up, D, carry
  Counter #(.width(4), .max('h9)) counter_4 (
    .clr(or_1_out), .count(demultiplexer_1_out2), .clk(CLK32K), .Q(counter_4_q));  // open: load, up, D, carry
  Counter #(.width(3), .max('h5)) counter_5 (
    .clr(or_1_out), .count(demultiplexer_1_out3), .clk(CLK32K), .Q(counter_5_q));  // open: load, up, D, carry
  Counter #(.width(4), .max('h9)) counter_6 (
    .clr(or_1_out), .count(demultiplexer_1_out4), .clk(CLK32K), .Q(MINloadU_4));  // open: load, up, D, carry
  Counter #(.width(1), .max('h1)) counter_7 (
    .clr(or_1_out), .count(demultiplexer_1_out5), .clk(CLK32K), .Q(ONOFFload));  // open: load, up, D, carry
  assign HloadT_4 = {{2{1'b0}}, counter_2_q};  // Bit_Extender bit_extender_1
  assign bit_extender_2_out = {{2{1'b0}}, counter_3_q};  // Bit_Extender bit_extender_2
  assign MINloadT_4 = {{1{1'b0}}, counter_5_q};  // Bit_Extender bit_extender_3
  Multiplexer #(.width(4), .enable("false")) multiplexer_1 (
    .in0(counter_4_q), .in1(bit_extender_2_out), .out(HloadU_4), .sel(counter_2_q[1]));

  // Other names for the same wires on the sheet: clk = CLK32K
endmodule

module alarmView_HM (
  input  [3:0] HT_4,
  input  [3:0] HU_4,
  input  [3:0] MINT_4,
  input  [3:0] MINU_4,
  input  curONOFF,
  input  HloadT,
  input  HloadU,
  input  MINloadT,
  input  MINloadU,
  input  ONOFFload,
  input  EQUAL,
  input  RESET,
  input  CLK4,
  output [7:0] sevsegCode_5,
  output [7:0] sevsegCode_4,
  output [7:0] sevsegCode_3,
  output [7:0] sevsegCode_2,
  output [7:0] sevsegCode_1,
  output [7:0] sevsegCode_0,
  output BUZZER
);

  wire and_1_out, and_2_out, and_3_out, and_4_out, and_5_out, and_6_out, or_1_out, t_ff_1_q;
  wire [6:0] bit_extender_2_out, bit_extender_4_out, multiplexer_3_out, multiplexer_5_out;
  wire [7:0] bit_extender_1_out, bit_extender_3_out, multiplexer_1_out;

  assign bit_extender_1_out = {{4{1'b0}}, HT_4};  // Bit_Extender bit_extender_1
  assign bit_extender_2_out = {{3{1'b0}}, HU_4};  // Bit_Extender bit_extender_2
  assign bit_extender_3_out = {{4{1'b0}}, MINT_4};  // Bit_Extender bit_extender_3
  assign bit_extender_4_out = {{3{1'b0}}, MINU_4};  // Bit_Extender bit_extender_4
  Multiplexer #(.width(8), .enable("false")) multiplexer_1 (
    .in0(8'hf), .in1(8'h16), .out(multiplexer_1_out), .sel(curONOFF));
  or or_1 (or_1_out, HloadT, HloadU, MINloadT, MINloadU, ONOFFload);
  Multiplexer #(.width(8), .enable("false")) multiplexer_2 (
    .in0(bit_extender_1_out), .in1(8'h7f), .out(sevsegCode_5), .sel(and_1_out));
  and and_1 (and_1_out, HloadT, t_ff_1_q);
  T_Flip_Flop t_ff_1 (.T(or_1_out), .clk(CLK4), .Q(t_ff_1_q), .reset(RESET));  // open: Qn, preset
  Multiplexer #(.width(7), .enable("false")) multiplexer_3 (
    .in0(bit_extender_2_out), .in1({7{1'b1}}), .out(multiplexer_3_out), .sel(and_2_out));
  and and_2 (and_2_out, HloadU, t_ff_1_q);
  Multiplexer #(.width(8), .enable("false")) multiplexer_4 (
    .in0(bit_extender_3_out), .in1(8'h7f), .out(sevsegCode_3), .sel(and_3_out));
  and and_3 (and_3_out, MINloadT, t_ff_1_q);
  and and_4 (and_4_out, MINloadU, t_ff_1_q);
  assign sevsegCode_4 = {{1{1'b1}}, multiplexer_3_out};  // Bit_Extender bit_extender_5
  Multiplexer #(.width(7), .enable("false")) multiplexer_5 (
    .in0(bit_extender_4_out), .in1({7{1'b1}}), .out(multiplexer_5_out), .sel(and_4_out));
  assign sevsegCode_2 = {{1{1'b1}}, multiplexer_5_out};  // Bit_Extender bit_extender_6
  Multiplexer #(.width(8), .enable("false")) multiplexer_6 (
    .in0(8'h17), .in1(8'h7f), .out(sevsegCode_1), .sel(and_5_out));
  and and_5 (and_5_out, ONOFFload, t_ff_1_q);
  Multiplexer #(.width(8), .enable("false")) multiplexer_7 (
    .in0(multiplexer_1_out), .in1(8'h7f), .out(sevsegCode_0), .sel(and_6_out));
  and and_6 (and_6_out, ONOFFload, t_ff_1_q);
  and and_7 (BUZZER, curONOFF, EQUAL);
endmodule

module alarmHM (
  input  RESET,
  input  CLK2k,
  input  [3:0] HloadT_4,
  input  HloadTEnDi,
  input  [3:0] HloadU_4,
  input  HloadUEnDi,
  input  [3:0] MINloadT_4,
  input  MINloadTEnDi,
  input  [3:0] MINloadU_4,
  input  MINloadUEnDi,
  input  ONOFFload,
  input  ONOFFloadEnDi,
  output [3:0] curHT_4,
  output [3:0] curHU_4,
  output [3:0] curMINT_4,
  output [3:0] curMINU_4,
  output curONOFF,
  output HloadT,
  output HloadU,
  output MINloadT,
  output MINloadU,
  output ONOFFL
);

  wire and_1_out, and_2_out, and_3_out, and_4_out, and_5_out, and_6_out, and_7_out, and_8_out, and_9_out,
       and_10_out, and_11_out, and_12_out, and_13_out, load_2_1_out0, load_2_1_out1, load_3_1_out0,
       load_3_1_out1, load_3_1_out2, load_4_1_out0, load_4_1_out1, load_4_1_out2, load_4_1_out3,
       load_4_2_out0, load_4_2_out1, load_4_2_out2, load_4_2_out3, multiplexer_1_out;
  wire [1:0] d_ff_2_q;
  wire [2:0] d_ff_9_q;

  load_2 load_2_1 (
    .IN1(d_ff_2_q[1]), .IN0(d_ff_2_q[0]), .loadValue(HloadT_4), .loadEnDi(HloadTEnDi), .OUT1(load_2_1_out1),
    .OUT0(load_2_1_out0));
  load_4 load_4_2 (
    .IN3(curHU_4[3]), .IN2(curHU_4[2]), .IN1(curHU_4[1]), .IN0(curHU_4[0]), .loadValue(HloadU_4),
    .loadEnDi(HloadUEnDi), .OUT3(load_4_2_out3), .OUT2(load_4_2_out2), .OUT1(load_4_2_out1),
    .OUT0(load_4_2_out0));
  load_3 load_3_1 (
    .IN2(d_ff_9_q[2]), .IN1(d_ff_9_q[1]), .IN0(d_ff_9_q[0]), .loadValue(MINloadT_4), .loadEnDi(MINloadTEnDi),
    .OUT2(load_3_1_out2), .OUT1(load_3_1_out1), .OUT0(load_3_1_out0));
  load_4 load_4_1 (
    .IN3(curMINU_4[3]), .IN2(curMINU_4[2]), .IN1(curMINU_4[1]), .IN0(curMINU_4[0]), .loadValue(MINloadU_4),
    .loadEnDi(MINloadUEnDi), .OUT3(load_4_1_out3), .OUT2(load_4_1_out2), .OUT1(load_4_1_out1),
    .OUT0(load_4_1_out0));
  Multiplexer #(.enable("false")) multiplexer_1 (
    .in0(curONOFF), .in1(ONOFFload), .out(multiplexer_1_out), .sel(ONOFFloadEnDi));
  and and_1 (and_1_out, ~RESET, load_2_1_out1);  // AND_Gate
  and and_2 (and_2_out, ~RESET, load_2_1_out0);  // AND_Gate
  and and_3 (and_3_out, ~RESET, load_4_2_out3);  // AND_Gate
  and and_4 (and_4_out, ~RESET, load_4_2_out2);  // AND_Gate
  and and_5 (and_5_out, ~RESET, load_4_2_out1);  // AND_Gate
  and and_6 (and_6_out, ~RESET, load_4_2_out0);  // AND_Gate
  and and_7 (and_7_out, ~RESET, load_3_1_out2);  // AND_Gate
  and and_8 (and_8_out, ~RESET, load_3_1_out1);  // AND_Gate
  and and_9 (and_9_out, ~RESET, load_3_1_out0);  // AND_Gate
  and and_10 (and_10_out, ~RESET, load_4_1_out3);  // AND_Gate
  and and_11 (and_11_out, ~RESET, load_4_1_out2);  // AND_Gate
  and and_12 (and_12_out, ~RESET, load_4_1_out1);  // AND_Gate
  and and_13 (and_13_out, ~RESET, load_4_1_out0);  // AND_Gate
  D_Flip_Flop d_ff_1 (.D(and_1_out), .clk(CLK2k), .Q(d_ff_2_q[1]), .reset(RESET));  // open: Qn, preset
  D_Flip_Flop d_ff_2 (.D(and_2_out), .clk(CLK2k), .Q(d_ff_2_q[0]), .reset(RESET));  // open: Qn, preset
  D_Flip_Flop d_ff_3 (.D(and_3_out), .clk(CLK2k), .Q(curHU_4[3]), .reset(RESET));  // open: Qn, preset
  D_Flip_Flop d_ff_4 (.D(and_4_out), .clk(CLK2k), .Q(curHU_4[2]), .reset(RESET));  // open: Qn, preset
  D_Flip_Flop d_ff_5 (.D(and_5_out), .clk(CLK2k), .Q(curHU_4[1]), .reset(RESET));  // open: Qn, preset
  D_Flip_Flop d_ff_6 (.D(and_6_out), .clk(CLK2k), .Q(curHU_4[0]), .reset(RESET));  // open: Qn, preset
  D_Flip_Flop d_ff_7 (.D(and_7_out), .clk(CLK2k), .Q(d_ff_9_q[2]), .reset(RESET));  // open: Qn, preset
  D_Flip_Flop d_ff_8 (.D(and_8_out), .clk(CLK2k), .Q(d_ff_9_q[1]), .reset(RESET));  // open: Qn, preset
  D_Flip_Flop d_ff_9 (.D(and_9_out), .clk(CLK2k), .Q(d_ff_9_q[0]), .reset(RESET));  // open: Qn, preset
  D_Flip_Flop d_ff_10 (.D(and_10_out), .clk(CLK2k), .Q(curMINU_4[3]), .reset(RESET));  // open: Qn, preset
  D_Flip_Flop d_ff_11 (.D(and_11_out), .clk(CLK2k), .Q(curMINU_4[2]), .reset(RESET));  // open: Qn, preset
  D_Flip_Flop d_ff_12 (.D(and_12_out), .clk(CLK2k), .Q(curMINU_4[1]), .reset(RESET));  // open: Qn, preset
  D_Flip_Flop d_ff_13 (.D(and_13_out), .clk(CLK2k), .Q(curMINU_4[0]), .reset(RESET));  // open: Qn, preset
  D_Flip_Flop d_ff_14 (.D(multiplexer_1_out), .clk(CLK2k), .Q(curONOFF), .reset(RESET));  // open: Qn, preset
  assign curHT_4 = {{2{1'b0}}, d_ff_2_q};  // Bit_Extender bit_extender_1
  assign curMINT_4 = {{1{1'b0}}, d_ff_9_q};  // Bit_Extender bit_extender_2

  assign HloadT = HloadTEnDi;
  assign HloadU = HloadUEnDi;
  assign MINloadT = MINloadTEnDi;
  assign MINloadU = MINloadUEnDi;
  assign ONOFFL = ONOFFloadEnDi;
endmodule

module compare (
  input  [3:0] A3_4,
  input  [3:0] A2_4,
  input  [3:0] A1_4,
  input  [3:0] A0_4,
  input  [3:0] B3_4,
  input  [3:0] B2_4,
  input  [3:0] B1_4,
  input  [3:0] B0_4,
  output EQUAL
);

  wire compare_4_1_equal_4, compare_4_2_equal_4, compare_4_3_equal_4, compare_4_4_equal_4;

  compare_4 compare_4_4 (.A_4(A3_4), .B_4(B3_4), .EQUAL_4(compare_4_4_equal_4));
  compare_4 compare_4_3 (.A_4(A2_4), .B_4(B2_4), .EQUAL_4(compare_4_3_equal_4));
  compare_4 compare_4_2 (.A_4(A1_4), .B_4(B1_4), .EQUAL_4(compare_4_2_equal_4));
  compare_4 compare_4_1 (.A_4(A0_4), .B_4(B0_4), .EQUAL_4(compare_4_1_equal_4));
  and and_1 (EQUAL, compare_4_4_equal_4, compare_4_3_equal_4, compare_4_2_equal_4, compare_4_1_equal_4);
endmodule

module compare_4 (
  input  [3:0] A_4,
  input  [3:0] B_4,
  output EQUAL_4
);

  wire xnor_1_out, xnor_2_out, xnor_3_out, xnor_4_out;

  xnor xnor_1 (xnor_1_out, A_4[0], B_4[0]);
  xnor xnor_2 (xnor_2_out, A_4[1], B_4[1]);
  xnor xnor_3 (xnor_3_out, A_4[2], B_4[2]);
  xnor xnor_4 (xnor_4_out, A_4[3], B_4[3]);
  and and_1 (EQUAL_4, xnor_1_out, xnor_2_out, xnor_3_out, xnor_4_out);
endmodule

module changeTimeZone (
  input  [7:0] SSDCode_5,
  input  [7:0] SSDCode_4,
  input  [7:0] SSDCode_3,
  input  [7:0] SSDCode_2,
  input  [7:0] SSDCode_1,
  input  [7:0] SSDCode_0,
  input  [7:0] UTCCode_8,
  output [7:0] sevsegCode_5,
  output [7:0] sevsegCode_4,
  output [7:0] sevsegCode_3,
  output [7:0] sevsegCode_2,
  output [7:0] sevsegCode_1,
  output [7:0] sevsegCode_0
);

  wire [3:0] H_HTimeZone_1_httz_4, H_HTimeZone_1_hutz_4, hourView_HMS_reverse_1_ht_4,
       hourView_HMS_reverse_1_hu_4, hourView_HMS_reverse_1_mint_4, hourView_HMS_reverse_1_minu_4,
       hourView_HMS_reverse_1_sect_4, hourView_HMS_reverse_1_secu_4;

  hourView_HMS_reverse hourView_HMS_reverse_1 (
    .sevsegCode_5(SSDCode_5), .sevsegCode_4(SSDCode_4), .sevsegCode_3(SSDCode_3), .sevsegCode_2(SSDCode_2),
    .sevsegCode_1(SSDCode_1), .sevsegCode_0(SSDCode_0), .HT_4(hourView_HMS_reverse_1_ht_4),
    .HU_4(hourView_HMS_reverse_1_hu_4), .MINT_4(hourView_HMS_reverse_1_mint_4),
    .MINU_4(hourView_HMS_reverse_1_minu_4), .SECT_4(hourView_HMS_reverse_1_sect_4),
    .SECU_4(hourView_HMS_reverse_1_secu_4));
  H_HTimeZone H_HTimeZone_1 (
    .HT_4(hourView_HMS_reverse_1_ht_4), .HU_4(hourView_HMS_reverse_1_hu_4), .UTCCode_8(UTCCode_8),
    .HTTZ_4(H_HTimeZone_1_httz_4), .HUTZ_4(H_HTimeZone_1_hutz_4));
  hourView_HMS_Ltime hourView_HMS_Ltime_1 (
    .HT_4(H_HTimeZone_1_httz_4), .HU_4(H_HTimeZone_1_hutz_4), .MINT_4(hourView_HMS_reverse_1_mint_4),
    .MINU_4(hourView_HMS_reverse_1_minu_4), .SECT_4(hourView_HMS_reverse_1_sect_4),
    .SECU_4(hourView_HMS_reverse_1_secu_4), .sevsegCode_5(sevsegCode_5), .sevsegCode_4(sevsegCode_4),
    .sevsegCode_3(sevsegCode_3), .sevsegCode_2(sevsegCode_2), .sevsegCode_1(sevsegCode_1),
    .sevsegCode_0(sevsegCode_0));
endmodule

module H_HTimeZone (
  input  [3:0] HT_4,
  input  [3:0] HU_4,
  input  [7:0] UTCCode_8,
  output [3:0] HTTZ_4,
  output [3:0] HUTZ_4
);

  wire [4:0] adder_2_out, bit_extender_1_out, bit_extender_2_out, bit_extender_5_out, multiplier_1_out;
  wire [6:0] adder_1_out, adder_3_out, adder_4_out, adder_5_out, adder_6_out, adder_7_out,
       bit_extender_3_out, bit_extender_4_out, multiplexer_1_out, multiplexer_2_out;

  assign bit_extender_1_out = {{1{1'b0}}, HT_4};  // Bit_Extender bit_extender_1
  assign bit_extender_2_out = {{1{1'b0}}, HU_4};  // Bit_Extender bit_extender_2
  Bit_Extender #(.out_width(7), .\type ("zero")) bit_extender_3 (.in(UTCCode_8), .out(bit_extender_3_out));
  Multiplier #(.width(5)) multiplier_1 (
    .a(bit_extender_1_out), .b(5'b01010), .out(multiplier_1_out));  // open: cin, cout
  Adder #(.width(7)) adder_1 (.a(bit_extender_3_out), .b(7'b0011000), .out(adder_1_out));  // open: cin, cout
  Adder #(.width(5)) adder_2 (.a(multiplier_1_out), .b(bit_extender_2_out), .out(adder_2_out));  // open: cin, cout
  assign bit_extender_4_out = {{2{1'b0}}, adder_2_out};  // Bit_Extender bit_extender_4
  Adder #(.width(7)) adder_3 (.a(bit_extender_4_out), .b(7'b1101000), .out(adder_3_out));  // open: cin, cout
  Adder #(.width(7)) adder_4 (.a(adder_3_out), .b(adder_1_out), .out(adder_4_out));  // open: cin, cout
  Adder #(.width(7)) adder_5 (.a(adder_4_out), .b(7'b0011000), .out(adder_5_out));  // open: cin, cout
  Adder #(.width(7)) adder_6 (.a(adder_4_out), .b(7'b1101000), .out(adder_6_out));  // open: cin, cout
  Multiplexer #(.width(7), .enable("false")) multiplexer_1 (
    .in0(adder_6_out), .in1(adder_5_out), .out(multiplexer_1_out), .sel(adder_4_out[6]));
  Adder #(.width(7)) adder_7 (.a(multiplexer_1_out), .b(7'b0011000), .out(adder_7_out));  // open: cin, cout
  Multiplexer #(.width(7), .enable("false")) multiplexer_2 (
    .in0(multiplexer_1_out), .in1(adder_7_out), .out(multiplexer_2_out), .sel(multiplexer_1_out[6]));
  Bit_Extender #(.in_width(7), .out_width(5), .\type ("zero")) bit_extender_5 (
    .in(multiplexer_2_out), .out(bit_extender_5_out));
  fivebits_to_2_4bits fivebits_to_2_4bits_1 (
    .A4(bit_extender_5_out[4]), .A3(bit_extender_5_out[3]), .A2(bit_extender_5_out[2]),
    .A1(bit_extender_5_out[1]), .A0(bit_extender_5_out[0]), .T3(HTTZ_4[3]), .T2(HTTZ_4[2]), .T1(HTTZ_4[1]),
    .T0(HTTZ_4[0]), .U3(HUTZ_4[3]), .U2(HUTZ_4[2]), .U1(HUTZ_4[1]), .U0(HUTZ_4[0]));
endmodule

module fivebits_to_2_4bits (
  input  A4,
  input  A3,
  input  A2,
  input  A1,
  input  A0,
  output T3,
  output T2,
  output T1,
  output T0,
  output U3,
  output U2,
  output U1,
  output U0
);

  wire and_1_out, and_2_out, and_3_out, and_4_out, and_5_out, and_6_out, and_7_out, and_8_out, and_9_out,
       and_10_out, and_11_out, and_12_out, and_13_out, and_14_out, and_15_out, and_16_out, and_17_out,
       and_18_out, not_1_out, not_2_out, not_3_out, not_4_out, not_5_out, not_6_out, not_7_out, not_8_out,
       not_9_out, not_10_out, not_11_out, not_12_out, not_13_out, not_14_out, not_15_out, not_16_out,
       not_17_out, not_18_out, not_19_out, not_20_out, not_21_out, not_22_out, not_23_out, not_24_out,
       not_25_out;

  and and_1 (and_1_out, A4, A2);
  and and_2 (and_2_out, A4, A3);
  not not_1 (not_1_out, A4);
  not not_2 (not_2_out, A4);
  not not_3 (not_3_out, A3);
  not not_4 (not_4_out, A2);
  not not_5 (not_5_out, A4);
  not not_6 (not_6_out, A2);
  not not_7 (not_7_out, A1);
  not not_8 (not_8_out, A3);
  not not_9 (not_9_out, A2);
  not not_10 (not_10_out, A1);
  not not_11 (not_11_out, A4);
  not not_12 (not_12_out, A3);
  not not_13 (not_13_out, A4);
  not not_14 (not_14_out, A2);
  not not_15 (not_15_out, A1);
  not not_16 (not_16_out, A2);
  not not_17 (not_17_out, A4);
  not not_18 (not_18_out, A3);
  not not_19 (not_19_out, A3);
  not not_20 (not_20_out, A4);
  not not_21 (not_21_out, A1);
  not not_22 (not_22_out, A3);
  not not_23 (not_23_out, A2);
  not not_24 (not_24_out, A1);
  not not_25 (not_25_out, A2);
  or or_1 (T1, and_1_out, and_2_out);
  and and_3 (and_3_out, not_1_out, A3, A1);
  and and_4 (and_4_out, not_2_out, A3, A2);
  and and_5 (and_5_out, A3, A2, A1);
  and and_6 (and_6_out, A4, not_3_out, not_4_out);
  and and_7 (and_7_out, not_5_out, A3, not_6_out, not_7_out);
  and and_8 (and_8_out, A4, not_8_out, not_9_out, A1);
  and and_9 (and_9_out, A4, A3, A2, not_10_out);
  and and_10 (and_10_out, not_11_out, not_12_out, A2);
  and and_11 (and_11_out, not_13_out, A2, A1);
  and and_12 (and_12_out, A4, not_14_out, not_15_out);
  and and_13 (and_13_out, A4, A3, not_16_out);
  and and_14 (and_14_out, not_17_out, not_18_out, A1);
  and and_15 (and_15_out, not_19_out, A2, A1);
  and and_16 (and_16_out, not_20_out, A3, A2, not_21_out);
  and and_17 (and_17_out, A4, not_22_out, not_23_out, not_24_out);
  and and_18 (and_18_out, A4, A3, not_25_out, A1);
  or or_2 (T0, and_3_out, and_4_out, and_5_out, and_6_out);
  or or_3 (U3, and_7_out, and_8_out, and_9_out);
  or or_4 (U2, and_10_out, and_11_out, and_12_out, and_13_out);
  or or_5 (U1, and_14_out, and_15_out, and_16_out, and_17_out, and_18_out);

  assign T2 = 1'b0;
  assign T3 = 1'b0;
  assign U0 = A0;
endmodule
