// Logisim project CHRONO.circ as structural Verilog: 9 circuits, main circuit CHRONO
module CHRONO (
  input  RESET,
  input  [1:0] B1_B0,
  output [7:0] Hour_Led2,
  output [7:0] Hour_Led1,
  output [7:0] Min_Led2,
  output [7:0] Min_Led1,
  output [7:0] Sec_Led2,
  output [7:0] Sec_Led1,
  output [7:0] Milli_Led2,
  output [7:0] Milli_Led1
);

  wire clock_1_out, not_1_out, not_2_out, TranLogic2_Chrono_1_d1, TranLogic2_Chrono_1_d2;
  wire [3:0] Dec100_Led1_1_u, Dec100_Led1_2_u, Dec100_Led1_3_u, Dec100_Led1_4_u, Dec100_Led2_1_u,
       Dec100_Led2_2_u, Dec100_Led2_3_u, Dec100_Led2_4_u;
  wire [6:0] bit_extender_2_out, bit_extender_5_out, bit_extender_8_out;
  wire [7:0] OutLogic_Chrono_1_run_reset, s_r_ff_1_q, ZeroToAll_1_centi, ZeroToAll_1_hour, ZeroToAll_1_min,
       ZeroToAll_1_sec;

  Clock clock_1 (.out(clock_1_out));
  TranLogic2_Chrono TranLogic2_Chrono_1 (
    .Q1(s_r_ff_1_q[0]), .Q2(s_r_ff_1_q[1]), .R(B1_B0[1]), .S(B1_B0[0]), .D1(TranLogic2_Chrono_1_d1),
    .D2(TranLogic2_Chrono_1_d2));
  S_R_Flip_Flop s_r_ff_1 (
    .S(TranLogic2_Chrono_1_d1), .R(not_1_out), .clk(clock_1_out), .Q(s_r_ff_1_q[0]));  // open: reset, Qn, preset
  not not_1 (not_1_out, TranLogic2_Chrono_1_d1);
  S_R_Flip_Flop s_r_ff_2 (
    .S(TranLogic2_Chrono_1_d2), .R(not_2_out), .clk(clock_1_out), .Q(s_r_ff_1_q[1]));  // open: reset, Qn, preset
  not not_2 (not_2_out, TranLogic2_Chrono_1_d2);
  OutLogic_Chrono OutLogic_Chrono_1 (.D1_D2(s_r_ff_1_q), .Run_Reset(OutLogic_Chrono_1_run_reset));
  ZeroToAll ZeroToAll_1 (
    .Sec(ZeroToAll_1_sec), .Centi(ZeroToAll_1_centi), .Run(OutLogic_Chrono_1_run_reset[0]),
    .Reset(OutLogic_Chrono_1_run_reset[1]), .Clk(clock_1_out), .Min(ZeroToAll_1_min), .Hour(ZeroToAll_1_hour));
  Dec100_Led1 Dec100_Led1_1 (
    .a(ZeroToAll_1_centi[6]), .b(ZeroToAll_1_centi[5]), .c(ZeroToAll_1_centi[4]), .d(ZeroToAll_1_centi[3]),
    .e(ZeroToAll_1_centi[2]), .f(ZeroToAll_1_centi[1]), .g(ZeroToAll_1_centi[0]), .x(Dec100_Led1_1_u[3]),
    .y(Dec100_Led1_1_u[2]), .z(Dec100_Led1_1_u[1]), .u(Dec100_Led1_1_u[0]));
  Dec100_Led1 Dec100_Led1_2 (
    .a(ZeroToAll_1_sec[6]), .b(ZeroToAll_1_sec[5]), .c(ZeroToAll_1_sec[4]), .d(ZeroToAll_1_sec[3]),
    .e(ZeroToAll_1_sec[2]), .f(ZeroToAll_1_sec[1]), .g(ZeroToAll_1_sec[0]), .x(Dec100_Led1_2_u[3]),
    .y(Dec100_Led1_2_u[2]), .z(Dec100_Led1_2_u[1]), .u(Dec100_Led1_2_u[0]));
  Dec100_Led1 Dec100_Led1_3 (
    .a(ZeroToAll_1_min[6]), .b(ZeroToAll_1_min[5]), .c(ZeroToAll_1_min[4]), .d(ZeroToAll_1_min[3]),
    .e(ZeroToAll_1_min[2]), .f(ZeroToAll_1_min[1]), .g(ZeroToAll_1_min[0]), .x(Dec100_Led1_3_u[3]),
    .y(Dec100_Led1_3_u[2]), .z(Dec100_Led1_3_u[1]), .u(Dec100_Led1_3_u[0]));
  Dec100_Led1 Dec100_Led1_4 (
    .a(ZeroToAll_1_hour[6]), .b(ZeroToAll_1_hour[5]), .c(ZeroToAll_1_hour[4]), .d(ZeroToAll_1_hour[3]),
    .e(ZeroToAll_1_hour[2]), .f(ZeroToAll_1_hour[1]), .g(ZeroToAll_1_hour[0]), .x(Dec100_Led1_4_u[3]),
    .y(Dec100_Led1_4_u[2]), .z(Dec100_Led1_4_u[1]), .u(Dec100_Led1_4_u[0]));
  Dec100_Led2 Dec100_Led2_1 (
    .a(ZeroToAll_1_centi[6]), .b(ZeroToAll_1_centi[5]), .c(ZeroToAll_1_centi[4]), .d(ZeroToAll_1_centi[3]),
    .e(ZeroToAll_1_centi[2]), .f(ZeroToAll_1_centi[1]), .g(ZeroToAll_1_centi[0]), .x(Dec100_Led2_1_u[3]),
    .y(Dec100_Led2_1_u[2]), .z(Dec100_Led2_1_u[1]), .u(Dec100_Led2_1_u[0]));
  Dec100_Led2 Dec100_Led2_2 (
    .a(ZeroToAll_1_sec[6]), .b(ZeroToAll_1_sec[5]), .c(ZeroToAll_1_sec[4]), .d(ZeroToAll_1_sec[3]),
    .e(ZeroToAll_1_sec[2]), .f(ZeroToAll_1_sec[1]), .g(ZeroToAll_1_sec[0]), .x(Dec100_Led2_2_u[3]),
    .y(Dec100_Led2_2_u[2]), .z(Dec100_Led2_2_u[1]), .u(Dec100_Led2_2_u[0]));
  Dec100_Led2 Dec100_Led2_3 (
    .a(ZeroToAll_1_min[6]), .b(ZeroToAll_1_min[5]), .c(ZeroToAll_1_min[4]), .d(ZeroToAll_1_min[3]),
    .e(ZeroToAll_1_min[2]), .f(ZeroToAll_1_min[1]), .g(ZeroToAll_1_min[0]), .x(Dec100_Led2_3_u[3]),
    .y(Dec100_Led2_3_u[2]), .z(Dec100_Led2_3_u[1]), .u(Dec100_Led2_3_u[0]));
  Dec100_Led2 Dec100_Led2_4 (
    .a(ZeroToAll_1_hour[6]), .b(ZeroToAll_1_hour[5]), .c(ZeroToAll_1_hour[4]), .d(ZeroToAll_1_hour[3]),
    .e(ZeroToAll_1_hour[2]), .f(ZeroToAll_1_hour[1]), .g(ZeroToAll_1_hour[0]), .x(Dec100_Led2_4_u[3]),
    .y(Dec100_Led2_4_u[2]), .z(Dec100_Led2_4_u[1]), .u(Dec100_Led2_4_u[0]));
  assign Hour_Led2 = {{4{1'b0}}, Dec100_Led2_4_u};  // Bit_Extender bit_extender_1
  assign bit_extender_2_out = {{3{1'b0}}, Dec100_Led1_4_u};  // Bit_Extender bit_extender_2
  assign Hour_Led1 = {{1{1'b1}}, bit_extender_2_out};  // Bit_Extender bit_extender_3
  assign Min_Led2 = {{4{1'b0}}, Dec100_Led2_3_u};  // Bit_Extender bit_extender_4
  assign bit_extender_5_out = {{3{1'b0}}, Dec100_Led1_3_u};  // Bit_Extender bit_extender_5
  assign Min_Led1 = {{1{1'b1}}, bit_extender_5_out};  // Bit_Extender bit_extender_6
  assign Sec_Led2 = {{4{1'b0}}, Dec100_Led2_2_u};  // Bit_Extender bit_extender_7
  assign bit_extender_8_out = {{3{1'b0}}, Dec100_Led1_2_u};  // Bit_Extender bit_extender_8
  assign Sec_Led1 = {{1{1'b1}}, bit_extender_8_out};  // Bit_Extender bit_extender_9
  assign Milli_Led2 = {{4{1'b0}}, Dec100_Led2_1_u};  // Bit_Extender bit_extender_10
  assign Milli_Led1 = {{4{1'b0}}, Dec100_Led1_1_u};  // Bit_Extender bit_extender_11
endmodule

module Dec100_Led1 (
  input  a,
  input  b,
  input  c,
  input  d,
  input  e,
  input  f,
  input  g,
  output x,
  output y,
  output z,
  output u
);

  wire and_1_out, and_2_out, and_3_out, and_4_out, and_5_out, and_6_out, and_7_out, and_8_out, and_9_out,
       and_10_out, and_11_out, and_12_out, and_13_out, and_14_out, and_15_out, and_16_out, and_17_out,
       and_18_out, and_19_out, and_20_out, and_21_out, and_22_out, and_23_out, and_24_out, and_25_out,
       and_26_out, and_27_out, and_28_out, and_29_out, and_30_out, and_31_out, and_32_out, and_33_out,
       and_34_out, and_35_out, and_36_out, and_37_out, and_38_out, and_39_out, and_40_out, and_41_out,
       and_42_out, not_1_out, not_2_out, not_3_out, not_4_out, not_5_out, not_6_out, not_7_out, not_8_out,
       not_9_out, not_10_out, not_11_out, not_12_out, not_13_out, not_14_out, not_15_out, not_16_out,
       not_17_out, not_18_out, not_19_out, not_20_out, not_21_out, not_22_out, not_23_out, not_24_out,
       not_25_out, not_26_out, not_27_out, not_28_out, not_29_out, not_30_out, not_31_out, not_32_out,
       not_33_out, not_34_out, not_35_out, not_36_out, not_37_out, not_38_out, not_39_out, not_40_out,
       not_41_out, not_42_out, not_43_out, not_44_out, not_45_out, not_46_out, not_47_out, not_48_out,
       not_49_out, not_50_out, not_51_out, not_52_out, not_53_out, not_54_out, not_55_out, not_56_out,
       not_57_out, not_58_out, not_59_out, not_60_out, not_61_out, not_62_out, not_63_out, not_64_out,
       not_65_out, not_66_out, not_67_out, not_68_out, not_69_out, not_70_out, not_71_out, not_72_out,
       not_73_out, not_74_out, not_75_out, not_76_out, not_77_out, not_78_out, not_79_out, not_80_out,
       not_81_out, not_82_out, not_83_out, not_84_out, not_85_out, not_86_out, not_87_out, not_88_out,
       not_89_out, not_90_out, not_91_out, not_92_out, not_93_out, not_94_out, not_95_out, not_96_out,
       not_97_out, not_98_out, not_99_out, not_100_out, not_101_out, not_102_out, not_103_out, not_104_out,
       not_105_out, not_106_out, not_107_out, not_108_out, not_109_out, not_110_out, not_111_out,
       not_112_out, not_113_out, not_114_out;

  not not_1 (not_1_out, a);
  not not_2 (not_2_out, b);
  not not_3 (not_3_out, c);
  not not_4 (not_4_out, e);
  not not_5 (not_5_out, f);
  not not_6 (not_6_out, a);
  not not_7 (not_7_out, b);
  not not_8 (not_8_out, d);
  not not_9 (not_9_out, e);
  not not_10 (not_10_out, a);
  not not_11 (not_11_out, b);
  not not_12 (not_12_out, f);
  not not_13 (not_13_out, a);
  not not_14 (not_14_out, c);
  not not_15 (not_15_out, d);
  not not_16 (not_16_out, a);
  not not_17 (not_17_out, d);
  not not_18 (not_18_out, e);
  not not_19 (not_19_out, f);
  not not_20 (not_20_out, e);
  not not_21 (not_21_out, b);
  not not_22 (not_22_out, c);
  not not_23 (not_23_out, d);
  not not_24 (not_24_out, f);
  not not_25 (not_25_out, b);
  not not_26 (not_26_out, c);
  not not_27 (not_27_out, e);
  not not_28 (not_28_out, f);
  not not_29 (not_29_out, c);
  not not_30 (not_30_out, d);
  not not_31 (not_31_out, e);
  not not_32 (not_32_out, f);
  not not_33 (not_33_out, a);
  not not_34 (not_34_out, b);
  not not_35 (not_35_out, c);
  not not_36 (not_36_out, d);
  not not_37 (not_37_out, a);
  not not_38 (not_38_out, c);
  not not_39 (not_39_out, a);
  not not_40 (not_40_out, b);
  not not_41 (not_41_out, e);
  not not_42 (not_42_out, f);
  not not_43 (not_43_out, a);
  not not_44 (not_44_out, b);
  not not_45 (not_45_out, e);
  not not_46 (not_46_out, a);
  not not_47 (not_47_out, e);
  not not_48 (not_48_out, f);
  not not_49 (not_49_out, a);
  not not_50 (not_50_out, c);
  not not_51 (not_51_out, d);
  not not_52 (not_52_out, e);
  not not_53 (not_53_out, a);
  not not_54 (not_54_out, c);
  not not_55 (not_55_out, f);
  not not_56 (not_56_out, a);
  not not_57 (not_57_out, d);
  not not_58 (not_58_out, b);
  not not_59 (not_59_out, c);
  not not_60 (not_60_out, d);
  not not_61 (not_61_out, e);
  not not_62 (not_62_out, c);
  not not_63 (not_63_out, e);
  not not_64 (not_64_out, b);
  not not_65 (not_65_out, c);
  not not_66 (not_66_out, f);
  not not_67 (not_67_out, d);
  not not_68 (not_68_out, f);
  not not_69 (not_69_out, b);
  not not_70 (not_70_out, c);
  not not_71 (not_71_out, e);
  not not_72 (not_72_out, f);
  not not_73 (not_73_out, e);
  not not_74 (not_74_out, b);
  not not_75 (not_75_out, c);
  not not_76 (not_76_out, d);
  not not_77 (not_77_out, e);
  not not_78 (not_78_out, a);
  not not_79 (not_79_out, b);
  not not_80 (not_80_out, d);
  not not_81 (not_81_out, b);
  not not_82 (not_82_out, c);
  not not_83 (not_83_out, f);
  not not_84 (not_84_out, a);
  not not_85 (not_85_out, b);
  not not_86 (not_86_out, d);
  not not_87 (not_87_out, e);
  not not_88 (not_88_out, f);
  not not_89 (not_89_out, a);
  not not_90 (not_90_out, b);
  not not_91 (not_91_out, e);
  not not_92 (not_92_out, a);
  not not_93 (not_93_out, c);
  not not_94 (not_94_out, d);
  not not_95 (not_95_out, f);
  not not_96 (not_96_out, c);
  not not_97 (not_97_out, e);
  not not_98 (not_98_out, a);
  not not_99 (not_99_out, d);
  not not_100 (not_100_out, f);
  not not_101 (not_101_out, e);
  not not_102 (not_102_out, f);
  not not_103 (not_103_out, b);
  not not_104 (not_104_out, c);
  not not_105 (not_105_out, f);
  not not_106 (not_106_out, b);
  not not_107 (not_107_out, f);
  not not_108 (not_108_out, b);
  not not_109 (not_109_out, d);
  not not_110 (not_110_out, d);
  not not_111 (not_111_out, e);
  not not_112 (not_112_out, f);
  not not_113 (not_113_out, c);
  not not_114 (not_114_out, d);
  and and_1 (and_1_out, not_1_out, not_2_out, not_3_out, d, not_4_out, not_5_out);
  and and_2 (and_2_out, not_6_out, not_7_out, c, not_8_out, not_9_out, f);
  and and_3 (and_3_out, not_10_out, not_11_out, c, d, e, not_12_out);
  and and_4 (and_4_out, not_13_out, b, not_14_out, not_15_out, e, f);
  and and_5 (and_5_out, not_16_out, b, c, not_17_out, not_18_out, not_19_out);
  and and_6 (and_6_out, b, c, d, not_20_out, f);
  and and_7 (and_7_out, a, not_21_out, not_22_out, not_23_out, e, not_24_out);
  and and_8 (and_8_out, a, not_25_out, not_26_out, d, e, f);
  and and_9 (and_9_out, a, c, d, not_27_out, not_28_out);
  and and_10 (and_10_out, a, b, not_29_out, not_30_out, not_31_out, f);
  and and_11 (and_11_out, a, b, d, e, not_32_out);
  and and_12 (and_12_out, a, b, c, e, f);
  and and_13 (and_13_out, not_33_out, not_34_out, not_35_out, not_36_out, e);
  and and_14 (and_14_out, not_37_out, not_38_out, d, e, f);
  and and_15 (and_15_out, not_39_out, not_40_out, c, not_41_out, not_42_out);
  and and_16 (and_16_out, not_43_out, not_44_out, c, d, not_45_out);
  and and_17 (and_17_out, not_46_out, c, d, not_47_out, not_48_out);
  and and_18 (and_18_out, not_49_out, b, not_50_out, not_51_out, not_52_out, f);
  and and_19 (and_19_out, not_53_out, b, not_54_out, e, not_55_out);
  and and_20 (and_20_out, not_56_out, b, c, not_57_out, e, f);
  and and_21 (and_21_out, a, not_58_out, not_59_out, not_60_out, not_61_out);
  and and_22 (and_22_out, a, not_62_out, d, not_63_out, f);
  and and_23 (and_23_out, a, not_64_out, not_65_out, d, e, not_66_out);
  and and_24 (and_24_out, a, c, not_67_out, e, not_68_out);
  and and_25 (and_25_out, a, not_69_out, c, e, f);
  and and_26 (and_26_out, a, b, not_70_out, not_71_out, not_72_out);
  and and_27 (and_27_out, a, b, c, not_73_out, f);
  and and_28 (and_28_out, not_74_out, not_75_out, not_76_out, not_77_out, f);
  and and_29 (and_29_out, not_78_out, not_79_out, not_80_out, e, f);
  and and_30 (and_30_out, not_81_out, not_82_out, d, e, not_83_out);
  and and_31 (and_31_out, not_84_out, not_85_out, c, not_86_out, not_87_out, not_88_out);
  and and_32 (and_32_out, not_89_out, not_90_out, c, d, not_91_out, f);
  and and_33 (and_33_out, not_92_out, b, not_93_out, not_94_out, not_95_out);
  and and_34 (and_34_out, b, not_96_out, d, not_97_out, f);
  and and_35 (and_35_out, not_98_out, b, d, e, f);
  and and_36 (and_36_out, b, c, not_99_out, e, not_100_out);
  and and_37 (and_37_out, b, c, d, not_101_out, not_102_out);
  and and_38 (and_38_out, a, not_103_out, not_104_out, d, not_105_out);
  and and_39 (and_39_out, a, not_106_out, d, e, not_107_out);
  and and_40 (and_40_out, a, not_108_out, c, not_109_out, f);
  and and_41 (and_41_out, a, b, not_110_out, not_111_out, not_112_out);
  and and_42 (and_42_out, a, b, not_113_out, not_114_out, e, f);
  or or_1 (x, and_1_out, and_2_out, and_3_out, and_4_out, and_5_out, and_6_out, and_7_out, and_8_out, and_9_out, and_10_out, and_11_out, and_12_out);
  or or_2 (y, and_13_out, and_14_out, and_15_out, and_16_out, and_17_out, and_18_out, and_19_out, and_20_out, and_21_out, and_22_out, and_23_out, and_24_out, and_25_out, and_26_out, and_27_out);
  or or_3 (z, and_28_out, and_29_out, and_30_out, and_31_out, and_32_out, and_33_out, and_34_out, and_35_out, and_36_out, and_37_out, and_38_out, and_39_out, and_40_out, and_41_out, and_42_out);

  assign u = g;
endmodule

module Dec100_Led2 (
  input  a,
  input  b,
  input  c,
  input  d,
  input  e,
  input  f,
  input  g,
  output x,
  output y,
  output z,
  output u
);

  wire and_1_out, and_2_out, and_3_out, and_4_out, and_5_out, and_6_out, and_7_out, and_8_out, and_9_out,
       and_10_out, and_11_out, and_12_out, and_13_out, and_14_out, and_15_out, and_16_out, and_17_out,
       and_18_out, and_19_out, and_20_out, and_21_out, and_22_out, not_1_out, not_2_out, not_3_out,
       not_4_out, not_5_out, not_6_out, not_7_out, not_8_out, not_9_out, not_10_out, not_11_out, not_12_out,
       not_13_out, not_14_out, not_15_out, not_16_out, not_17_out, not_18_out, not_19_out, not_20_out,
       not_21_out, not_22_out, not_23_out, not_24_out, not_25_out, not_26_out, not_27_out, not_28_out,
       not_29_out, not_30_out, not_31_out, not_32_out, not_33_out;

  not not_1 (not_1_out, e);
  not not_2 (not_2_out, b);
  not not_3 (not_3_out, c);
  not not_4 (not_4_out, a);
  not not_5 (not_5_out, b);
  not not_6 (not_6_out, a);
  not not_7 (not_7_out, b);
  not not_8 (not_8_out, a);
  not not_9 (not_9_out, a);
  not not_10 (not_10_out, c);
  not not_11 (not_11_out, d);
  not not_12 (not_12_out, b);
  not not_13 (not_13_out, c);
  not not_14 (not_14_out, b);
  not not_15 (not_15_out, c);
  not not_16 (not_16_out, b);
  not not_17 (not_17_out, c);
  not not_18 (not_18_out, b);
  not not_19 (not_19_out, a);
  not not_20 (not_20_out, b);
  not not_21 (not_21_out, d);
  not not_22 (not_22_out, e);
  not not_23 (not_23_out, a);
  not not_24 (not_24_out, d);
  not not_25 (not_25_out, e);
  not not_26 (not_26_out, c);
  not not_27 (not_27_out, d);
  not not_28 (not_28_out, e);
  not not_29 (not_29_out, a);
  not not_30 (not_30_out, d);
  not not_31 (not_31_out, e);
  not not_32 (not_32_out, c);
  not not_33 (not_33_out, c);
  and and_1 (and_1_out, a, c);
  or or_1 (x, and_1_out, and_2_out);
  and and_2 (and_2_out, a, b, not_1_out);
  and and_3 (and_3_out, b, d);
  or or_2 (y, and_3_out, and_4_out, and_5_out);
  and and_4 (and_4_out, b, c);
  and and_5 (and_5_out, a, not_2_out, not_3_out);
  and and_6 (and_6_out, not_4_out, not_5_out, c, e);
  and and_7 (and_7_out, not_6_out, not_7_out, c, d);
  and and_8 (and_8_out, not_8_out, c, d, e);
  and and_9 (and_9_out, not_9_out, b, not_10_out, not_11_out);
  and and_10 (and_10_out, a, not_12_out, not_13_out);
  and and_11 (and_11_out, not_14_out, not_15_out, d, f);
  and and_12 (and_12_out, not_16_out, not_17_out, d, e);
  and and_13 (and_13_out, not_18_out, d, e, f);
  and and_14 (and_14_out, not_19_out, not_20_out, c, not_21_out, not_22_out);
  and and_15 (and_15_out, not_23_out, c, not_24_out, not_25_out, f);
  and and_16 (and_16_out, b, not_26_out, not_27_out, not_28_out);
  and and_17 (and_17_out, not_29_out, b, not_30_out, e);
  and and_18 (and_18_out, b, c, d, not_31_out);
  and and_19 (and_19_out, a, not_32_out, e, f);
  and and_20 (and_20_out, a, not_33_out, d);
  and and_21 (and_21_out, a, d, f);
  and and_22 (and_22_out, a, d, e);
  or or_3 (z, and_6_out, and_7_out, and_8_out, and_9_out, and_10_out);
  or or_4 (u, and_11_out, and_12_out, and_13_out, and_14_out, and_15_out, and_16_out, and_17_out, and_18_out, and_19_out, and_20_out, and_21_out, and_22_out);
endmodule

module ZeroToAll (
  input  Run,
  input  Reset,
  input  Clk,
  output [7:0] Centi,
  output [7:0] Sec,
  output [7:0] Min,
  output [7:0] Hour
);

  wire and_1_out, and_2_out, CentiSeconds_carryout, counter_1_carry, Seconds_carryout;

  Counter #(.max('ha0)) counter_1 (
    .clr(Reset), .count(Run), .clk(Clk), .carry(counter_1_carry));  // open: load, up, D, Q
  and and_1 (and_1_out, CentiSeconds_carryout, counter_1_carry);
  and and_2 (and_2_out, and_1_out, Seconds_carryout);
  ZeroTo99 CentiSeconds (
    .Count(Centi), .CarryOut(CentiSeconds_carryout), .Clk(Clk), .CarryIn(counter_1_carry), .Reset(Reset));
  ZeroTo59 Seconds (.CarryOut(Seconds_carryout), .count(Sec), .CarryIn(and_1_out), .Reset(Reset), .Clk(Clk));
  ZeroTo59 Minutes (.count(Min), .CarryIn(and_2_out), .Reset(Reset), .Clk(Clk));  // open: CarryOut
  ZeroTo99 Hours (.Count(Hour), .Clk(Clk), .Reset(Reset));  // open: CarryOut, CarryIn
endmodule

module ZeroTo59 (
  input  CarryIn,
  input  Clk,
  input  Reset,
  output CarryOut,
  output [7:0] count
);

  wire [5:0] counter_1_q;

  Counter #(.width(6), .max('h3b)) counter_1 (
    .clr(Reset), .count(CarryIn), .clk(Clk), .carry(CarryOut), .Q(counter_1_q));  // open: load, up, D
  assign count = {{2{1'b0}}, counter_1_q};  // Bit_Extender bit_extender_1
endmodule

module ZeroTo99 (
  input  CarryIn,
  input  Clk,
  input  Reset,
  output CarryOut,
  output [7:0] Count
);

  wire [6:0] counter_1_q;

  Counter #(.width(7), .max('h63)) counter_1 (
    .clr(Reset), .count(CarryIn), .clk(Clk), .carry(CarryOut), .Q(counter_1_q));  // open: load, up, D
  assign Count = {{1{1'b0}}, counter_1_q};  // Bit_Extender bit_extender_1
endmodule

module TranLogic_Chrono (
  input  [7:0] Q1_Q2_Start_Reset,
  output [7:0] D1_D2
);

  wire and_1_out, and_2_out, and_3_out, and_4_out, and_5_out, and_6_out, and_7_out, not_1_out, not_2_out,
       not_3_out, not_4_out, not_5_out, not_6_out, not_7_out, not_8_out, not_9_out, not_10_out, not_11_out,
       not_12_out;
  wire [1:0] or_2_out;

  not not_1 (not_1_out, Q1_Q2_Start_Reset[1]);
  not not_2 (not_2_out, Q1_Q2_Start_Reset[2]);
  not not_3 (not_3_out, Q1_Q2_Start_Reset[0]);
  not not_4 (not_4_out, Q1_Q2_Start_Reset[2]);
  not not_5 (not_5_out, Q1_Q2_Start_Reset[0]);
  not not_6 (not_6_out, Q1_Q2_Start_Reset[0]);
  not not_7 (not_7_out, Q1_Q2_Start_Reset[3]);
  not not_8 (not_8_out, Q1_Q2_Start_Reset[1]);
  not not_9 (not_9_out, Q1_Q2_Start_Reset[3]);
  not not_10 (not_10_out, Q1_Q2_Start_Reset[1]);
  not not_11 (not_11_out, Q1_Q2_Start_Reset[0]);
  not not_12 (not_12_out, Q1_Q2_Start_Reset[2]);
  and and_1 (and_1_out, not_1_out, Q1_Q2_Start_Reset[0], not_2_out, Q1_Q2_Start_Reset[3]);
  and and_2 (and_2_out, Q1_Q2_Start_Reset[1], not_3_out, not_4_out);
  and and_3 (and_3_out, Q1_Q2_Start_Reset[1], not_5_out, Q1_Q2_Start_Reset[3]);
  and and_4 (and_4_out, not_6_out, Q1_Q2_Start_Reset[2], not_7_out);
  and and_5 (and_5_out, not_8_out, Q1_Q2_Start_Reset[0], not_9_out);
  and and_6 (and_6_out, not_10_out, Q1_Q2_Start_Reset[0], Q1_Q2_Start_Reset[2]);
  and and_7 (and_7_out, Q1_Q2_Start_Reset[1], not_11_out, not_12_out, Q1_Q2_Start_Reset[3]);
  or or_1 (or_2_out[1], and_1_out, and_2_out, and_3_out);
  or or_2 (or_2_out[0], and_4_out, and_5_out, and_6_out, and_7_out);
  assign D1_D2 = {{6{1'b0}}, or_2_out};  // Bit_Extender bit_extender_1
endmodule

module OutLogic_Chrono (
  input  [7:0] D1_D2,
  output [7:0] Run_Reset
);

  wire not_1_out;
  wire [1:0] and_1_out;

  not not_1 (not_1_out, D1_D2[1]);
  and and_1 (and_1_out[0], not_1_out, D1_D2[0]);
  and and_2 (and_1_out[1], D1_D2[1], D1_D2[0]);
  assign Run_Reset = {{6{1'b0}}, and_1_out};  // Bit_Extender bit_extender_1
endmodule

module TranLogic2_Chrono (
  input  Q1,
  input  Q2,
  input  R,
  input  S,
  output D1,
  output D2
);

  wire and_1_out, and_2_out, and_3_out, and_4_out, and_5_out, and_6_out, and_7_out, not_1_out, not_2_out,
       not_3_out, not_4_out, not_5_out, not_6_out, not_7_out, not_8_out, not_9_out, not_10_out, not_11_out,
       not_12_out;

  not not_1 (not_1_out, S);
  not not_2 (not_2_out, Q1);
  not not_3 (not_3_out, S);
  not not_4 (not_4_out, Q2);
  not not_5 (not_5_out, Q1);
  not not_6 (not_6_out, R);
  not not_7 (not_7_out, Q2);
  not not_8 (not_8_out, S);
  not not_9 (not_9_out, Q1);
  not not_10 (not_10_out, R);
  not not_11 (not_11_out, Q1);
  not not_12 (not_12_out, Q2);
  and and_1 (and_1_out, not_1_out, Q2, not_2_out);
  and and_2 (and_2_out, not_3_out, R, not_4_out, Q1);
  or or_1 (D2, and_1_out, and_2_out, and_3_out);
  and and_3 (and_3_out, R, Q2, not_5_out);
  and and_4 (and_4_out, not_6_out, not_7_out, Q1);
  and and_5 (and_5_out, not_8_out, R, Q2, not_9_out);
  and and_6 (and_6_out, S, not_10_out, not_11_out);
  and and_7 (and_7_out, S, not_12_out, Q1);
  or or_2 (D1, and_4_out, and_5_out, and_6_out, and_7_out);
endmodule
