// Logisim project CountDown.circ as structural Verilog: 10 circuits, main circuit CTDOWN
module CTDOWN (
  input  DIP,
  input  [1:0] B1_B0,
  output [7:0] Hour_Led2,
  output [7:0] Hour_Led1,
  output [7:0] Min_Led2,
  output [7:0] Min_Led1,
  output [7:0] Sec_Led2,
  output [7:0] Sec_Led1,
  output [7:0] out_9
);

  wire and_1_out, and_2_out, and_3_out, clock_1_out, CountControl_1_finish, d_ff_1_q, d_ff_2_q, d_ff_3_q,
       FSM_CTDOWN_1_q0, FSM_CTDOWN_1_q1, FSM_CTDOWN_1_q2, TransLogicCtDOwn_1_mount, TransLogicCtDOwn_1_reset,
       TransLogicCtDOwn_1_run;
  wire [5:0] Loader_1_minutes, Loader_1_seconds;
  wire [6:0] Loader_1_hours;
  wire [7:0] CountControl_1_min, CountControl_1_sec;

  FSM_CTDOWN FSM_CTDOWN_1 (
    .finish(CountControl_1_finish), .D2(d_ff_3_q), .D1(d_ff_2_q), .D0(d_ff_1_q), .DIP(DIP), .B1(B1_B0[0]),
    .B0(B1_B0[1]), .Q2(FSM_CTDOWN_1_q2), .Q1(FSM_CTDOWN_1_q1), .Q0(FSM_CTDOWN_1_q0));
  D_Flip_Flop d_ff_1 (.D(FSM_CTDOWN_1_q0), .clk(clock_1_out), .Q(d_ff_1_q));  // open: Qn, preset, reset
  Clock clock_1 (.out(clock_1_out));
  and and_1 (and_1_out, DIP, B1_B0[0]);
  and and_2 (and_2_out, DIP, B1_B0[1]);
  D_Flip_Flop d_ff_2 (.D(FSM_CTDOWN_1_q1), .clk(clock_1_out), .Q(d_ff_2_q));  // open: Qn, preset, reset
  D_Flip_Flop d_ff_3 (.D(FSM_CTDOWN_1_q2), .clk(clock_1_out), .Q(d_ff_3_q));  // open: Qn, preset, reset
  and and_3 (and_3_out, ~DIP, CountControl_1_finish);  // AND_Gate
  TransLogicCtDOwn TransLogicCtDOwn_1 (
    .D2(d_ff_3_q), .D1(d_ff_2_q), .D0(d_ff_1_q), .Reset(TransLogicCtDOwn_1_reset),
    .Mount(TransLogicCtDOwn_1_mount), .Run(TransLogicCtDOwn_1_run));
  Loader Loader_1 (
    .reset(and_3_out), .B1(and_1_out), .B0(and_2_out), .seconds(Loader_1_seconds),
    .minutes(Loader_1_minutes), .hours(Loader_1_hours));
  CountControl CountControl_1 (
    .Reset(TransLogicCtDOwn_1_reset), .Mount(TransLogicCtDOwn_1_mount), .Run(TransLogicCtDOwn_1_run),
    .seconds(Loader_1_seconds), .minutes(Loader_1_minutes), .hours(Loader_1_hours), .clk(clock_1_out),
    .Sec(CountControl_1_sec), .Min(CountControl_1_min), .Hour(out_9), .finish(CountControl_1_finish));
  DecoderAll DecoderAll_1 (
    .SEC(CountControl_1_sec), .MIN(CountControl_1_min), .HOUR(out_9), .L1(Hour_Led2), .L2(Hour_Led1),
    .L3(Min_Led2), .L4(Min_Led1), .L5(Sec_Led2), .L6(Sec_Led1));
endmodule

module DecoderAll (
  input  [7:0] SEC,
  input  [7:0] MIN,
  input  [7:0] HOUR,
  output [7:0] L1,
  output [7:0] L2,
  output [7:0] L3,
  output [7:0] L4,
  output [7:0] L5,
  output [7:0] L6
);

  wire [3:0] Dec100_Led1_TIMER_1_u, Dec100_Led1_TIMER_2_x, Dec100_Led1_TIMER_3_x, Dec100_Led2_TIMER_1_x,
       Dec100_Led2_TIMER_2_x, Dec100_Led2_TIMER_3_x;
  wire [6:0] bit_extender_1_out, bit_extender_2_out, bit_extender_3_out;

  Bit_Extender #(.out_width(7)) bit_extender_1 (.in(HOUR), .out(bit_extender_1_out));
  Bit_Extender #(.out_width(7)) bit_extender_2 (.in(SEC), .out(bit_extender_2_out));
  Bit_Extender #(.out_width(7)) bit_extender_3 (.in(MIN), .out(bit_extender_3_out));
  Dec100_Led1_TIMER Dec100_Led1_TIMER_1 (
    .g(bit_extender_2_out[0]), .f(bit_extender_2_out[1]), .e(bit_extender_2_out[2]),
    .d(bit_extender_2_out[3]), .c(bit_extender_2_out[4]), .b(bit_extender_2_out[5]),
    .a(bit_extender_2_out[6]), .x(Dec100_Led1_TIMER_1_u[3]), .y(Dec100_Led1_TIMER_1_u[2]),
    .z(Dec100_Led1_TIMER_1_u[1]), .u(Dec100_Led1_TIMER_1_u[0]));
  Dec100_Led1_TIMER Dec100_Led1_TIMER_2 (
    .g(bit_extender_3_out[0]), .f(bit_extender_3_out[1]), .e(bit_extender_3_out[2]),
    .d(bit_extender_3_out[3]), .c(bit_extender_3_out[4]), .b(bit_extender_3_out[5]),
    .a(bit_extender_3_out[6]), .x(Dec100_Led1_TIMER_2_x[0]), .y(Dec100_Led1_TIMER_2_x[1]),
    .z(Dec100_Led1_TIMER_2_x[2]), .u(Dec100_Led1_TIMER_2_x[3]));
  Dec100_Led1_TIMER Dec100_Led1_TIMER_3 (
    .g(bit_extender_1_out[0]), .f(bit_extender_1_out[1]), .e(bit_extender_1_out[2]),
    .d(bit_extender_1_out[3]), .c(bit_extender_1_out[4]), .b(bit_extender_1_out[5]),
    .a(bit_extender_1_out[6]), .x(Dec100_Led1_TIMER_3_x[0]), .y(Dec100_Led1_TIMER_3_x[1]),
    .z(Dec100_Led1_TIMER_3_x[2]), .u(Dec100_Led1_TIMER_3_x[3]));
  Dec100_Led2_TIMER Dec100_Led2_TIMER_1 (
    .a(bit_extender_2_out[0]), .b(bit_extender_2_out[1]), .c(bit_extender_2_out[2]),
    .d(bit_extender_2_out[3]), .e(bit_extender_2_out[4]), .f(bit_extender_2_out[5]),
    .g(bit_extender_2_out[6]), .x(Dec100_Led2_TIMER_1_x[0]), .y(Dec100_Led2_TIMER_1_x[1]),
    .z(Dec100_Led2_TIMER_1_x[2]), .u(Dec100_Led2_TIMER_1_x[3]));
  Dec100_Led2_TIMER Dec100_Led2_TIMER_2 (
    .a(bit_extender_3_out[0]), .b(bit_extender_3_out[1]), .c(bit_extender_3_out[2]),
    .d(bit_extender_3_out[3]), .e(bit_extender_3_out[4]), .f(bit_extender_3_out[5]),
    .g(bit_extender_3_out[6]), .x(Dec100_Led2_TIMER_2_x[0]), .y(Dec100_Led2_TIMER_2_x[1]),
    .z(Dec100_Led2_TIMER_2_x[2]), .u(Dec100_Led2_TIMER_2_x[3]));
  Dec100_Led2_TIMER Dec100_Led2_TIMER_3 (
    .a(bit_extender_1_out[0]), .b(bit_extender_1_out[1]), .c(bit_extender_1_out[2]),
    .d(bit_extender_1_out[3]), .e(bit_extender_1_out[4]), .f(bit_extender_1_out[5]),
    .g(bit_extender_1_out[6]), .x(Dec100_Led2_TIMER_3_x[0]), .y(Dec100_Led2_TIMER_3_x[1]),
    .z(Dec100_Led2_TIMER_3_x[2]), .u(Dec100_Led2_TIMER_3_x[3]));
  assign L1 = {{4{1'b0}}, Dec100_Led2_TIMER_3_x};  // Bit_Extender bit_extender_4
  assign L2 = {{4{1'b0}}, Dec100_Led1_TIMER_3_x};  // Bit_Extender bit_extender_5
  assign L3 = {{4{1'b0}}, Dec100_Led2_TIMER_2_x};  // Bit_Extender bit_extender_6
  assign L4 = {{4{1'b0}}, Dec100_Led1_TIMER_2_x};  // Bit_Extender bit_extender_7
  assign L5 = {{4{1'b0}}, Dec100_Led2_TIMER_1_x};  // Bit_Extender bit_extender_8
  assign L6 = {{4{1'b0}}, Dec100_Led1_TIMER_1_u};  // Bit_Extender bit_extender_9
endmodule

module CountControl (
  input  Reset,
  input  Mount,
  input  Run,
  input  [5:0] seconds,
  input  [5:0] minutes,
  input  [6:0] hours,
  input  clk,
  output [7:0] Sec,
  output [7:0] Min,
  output [7:0] Hour,
  output finish
);

  wire and_1_out, and_2_out, MinCounter_carry, SecCounter_carry;
  wire [5:0] MinCounter_q, SecCounter_q;
  wire [6:0] HourCounter_q;
  wire [7:0] and_3_out;

  and and_1 (and_1_out, SecCounter_carry, Run);
  and and_2 (and_2_out, and_1_out, MinCounter_carry);
  Counter #(.width(6), .max('h3b)) SecCounter (
    .clr(Reset), .load(Mount), .up(1'b0), .count(Run), .clk(clk), .D(seconds), .carry(SecCounter_carry),
    .Q(SecCounter_q));
  Counter #(.width(6), .max('h3b)) MinCounter (
    .clr(Reset), .load(Mount), .up(1'b0), .count(and_1_out), .clk(clk), .D(minutes),
    .carry(MinCounter_carry), .Q(MinCounter_q));
  Counter #(.width(7), .max('h63)) HourCounter (
    .clr(Reset), .load(Mount), .up(1'b0), .count(and_2_out), .clk(clk), .D(hours), .Q(HourCounter_q));  // open: carry
  assign Sec = {{2{1'b0}}, SecCounter_q};  // Bit_Extender bit_extender_1
  assign Min = {{2{1'b0}}, MinCounter_q};  // Bit_Extender bit_extender_2
  assign Hour = {{1{1'b0}}, HourCounter_q};  // Bit_Extender bit_extender_3
  assign and_3_out = ~Hour & ~Min & ~Sec;  // AND_Gate and_3, 8 bits wide
  and and_4 (finish, and_3_out[0], and_3_out[1], and_3_out[2], and_3_out[3], and_3_out[4], and_3_out[5], and_3_out[6], and_3_out[7]);
endmodule

module Loader (
  input  reset,
  input  B1,
  input  B0,
  output [5:0] seconds,
  output [5:0] minutes,
  output [6:0] hours
);

  wire valselector_1_h1, valselector_1_h2, valselector_1_m1, valselector_1_m2, valselector_1_s1,
       valselector_1_s2;
  wire [2:0] counter_1_q, counter_4_q, counter_6_q, counter_7_q;
  wire [3:0] counter_2_q, counter_3_q, counter_5_q;

  Counter #(.width(3), .max('h6)) counter_1 (
    .clr(reset), .up(1'b1), .count(1'b1), .clk(B0), .Q(counter_1_q));  // open: load, D, carry
  Counter #(.width(4), .max('hb)) counter_2 (
    .clr(reset), .up(1'b1), .count(1'b1), .clk(valselector_1_s1), .Q(counter_2_q));  // open: load, D, carry
  valselector valselector_1 (
    .B1(B1), .c(counter_1_q[2]), .b(counter_1_q[1]), .a(counter_1_q[0]), .s1(valselector_1_s1),
    .s2(valselector_1_s2), .m1(valselector_1_m1), .m2(valselector_1_m2), .h1(valselector_1_h1),
    .h2(valselector_1_h2));
  Counter #(.width(4), .max('hb)) counter_3 (
    .clr(reset), .up(1'b1), .count(1'b1), .clk(valselector_1_h1), .Q(counter_3_q));  // open: load, D, carry
  Counter #(.width(3), .max('h3)) counter_4 (
    .clr(reset), .up(1'b1), .count(1'b1), .clk(valselector_1_s2), .Q(counter_4_q));  // open: load, D, carry
  Counter #(.width(4), .max('hb)) counter_5 (
    .clr(reset), .up(1'b1), .count(1'b1), .clk(valselector_1_m1), .Q(counter_5_q));  // open: load, D, carry
  Counter #(.width(3), .max('h3)) counter_6 (
    .clr(reset), .up(1'b1), .count(1'b1), .clk(valselector_1_m2), .Q(counter_6_q));  // open: load, D, carry
  Counter #(.width(3), .max('h3)) counter_7 (
    .clr(reset), .up(1'b1), .count(1'b1), .clk(valselector_1_h2), .Q(counter_7_q));  // open: load, D, carry
  converter converter_1 (
    .s1d(counter_2_q[0]), .s1c(counter_2_q[1]), .s1b(counter_2_q[2]), .s1a(counter_2_q[3]),
    .s2c(counter_4_q[0]), .s2b(counter_4_q[1]), .s2a(counter_4_q[2]), .x(seconds[5]), .y(seconds[4]),
    .z(seconds[3]), .u(seconds[2]), .v(seconds[1]), .w(seconds[0]));
  converter converter_2 (
    .s1d(counter_5_q[0]), .s1c(counter_5_q[1]), .s1b(counter_5_q[2]), .s1a(counter_5_q[3]),
    .s2c(counter_6_q[0]), .s2b(counter_6_q[1]), .s2a(counter_6_q[2]), .x(minutes[5]), .y(minutes[4]),
    .z(minutes[3]), .u(minutes[2]), .v(minutes[1]), .w(minutes[0]));
  converter converter_3 (
    .s1d(counter_3_q[0]), .s1c(counter_3_q[1]), .s1b(counter_3_q[2]), .s1a(counter_3_q[3]),
    .s2c(counter_7_q[0]), .s2b(counter_7_q[1]), .s2a(counter_7_q[2]), .x(hours[5]), .y(hours[4]),
    .z(hours[3]), .u(hours[2]), .v(hours[1]), .w(hours[0]));
endmodule

module converter (
  input  s1d,
  input  s1c,
  input  s1b,
  input  s1a,
  input  s2c,
  input  s2b,
  input  s2a,
  output x,
  output y,
  output z,
  output u,
  output v,
  output w
);

  wire and_1_out, and_2_out, and_3_out, and_4_out, and_5_out, and_6_out, and_7_out, and_8_out, and_9_out,
       and_10_out, and_11_out, and_12_out, and_13_out, and_14_out, and_15_out, and_16_out, and_17_out,
       and_18_out, and_19_out, and_20_out, and_21_out, and_22_out, and_23_out, and_24_out, and_25_out,
       not_1_out, not_2_out, not_3_out, not_4_out, not_5_out, not_6_out, not_7_out, not_8_out, not_9_out,
       not_10_out, not_11_out, not_12_out, not_13_out, not_14_out, not_15_out, not_16_out, not_17_out,
       not_18_out, not_19_out, not_20_out, not_21_out, not_22_out, not_23_out, not_24_out, not_25_out,
       not_26_out, not_27_out, not_28_out, not_29_out, not_30_out, not_31_out, not_32_out, not_33_out,
       not_34_out, not_35_out, not_36_out, not_37_out, not_38_out;

  and and_1 (and_1_out, s2b, s2c, s1c);
  and and_2 (and_2_out, s2b, s2c, s1b);
  and and_3 (and_3_out, s2b, s2c, s1a);
  not not_1 (not_1_out, s2b);
  not not_2 (not_2_out, s2b);
  not not_3 (not_3_out, s2c);
  not not_4 (not_4_out, s1a);
  not not_5 (not_5_out, s1b);
  not not_6 (not_6_out, s1c);
  not not_7 (not_7_out, s2a);
  not not_8 (not_8_out, s2c);
  not not_9 (not_9_out, s2a);
  not not_10 (not_10_out, s2b);
  not not_11 (not_11_out, s1a);
  not not_12 (not_12_out, s1b);
  not not_13 (not_13_out, s2a);
  not not_14 (not_14_out, s2b);
  not not_15 (not_15_out, s1a);
  not not_16 (not_16_out, s1c);
  not not_17 (not_17_out, s2a);
  not not_18 (not_18_out, s1a);
  not not_19 (not_19_out, s1b);
  not not_20 (not_20_out, s1c);
  not not_21 (not_21_out, s2c);
  not not_22 (not_22_out, s2c);
  not not_23 (not_23_out, s1a);
  not not_24 (not_24_out, s1a);
  not not_25 (not_25_out, s2b);
  not not_26 (not_26_out, s2c);
  not not_27 (not_27_out, s1a);
  not not_28 (not_28_out, s2b);
  not not_29 (not_29_out, s1c);
  not not_30 (not_30_out, s2b);
  not not_31 (not_31_out, s1b);
  not not_32 (not_32_out, s2c);
  not not_33 (not_33_out, s1b);
  not not_34 (not_34_out, s1b);
  not not_35 (not_35_out, s1c);
  not not_36 (not_36_out, s2c);
  not not_37 (not_37_out, s1a);
  not not_38 (not_38_out, s1c);
  or or_1 (x, and_1_out, and_2_out, and_3_out, s2a);
  and and_4 (and_4_out, not_1_out, s2c, s1b, s1c);
  and and_5 (and_5_out, not_2_out, s2c, s1a);
  and and_6 (and_6_out, s2b, not_3_out);
  and and_7 (and_7_out, s2b, not_4_out, not_5_out, not_6_out);
  and and_8 (and_8_out, s2a, s1a);
  and and_9 (and_9_out, s2a, s2c);
  and and_10 (and_10_out, not_7_out, not_8_out, s1a);
  and and_11 (and_11_out, not_9_out, not_10_out, s2c, not_11_out, not_12_out);
  and and_12 (and_12_out, not_13_out, not_14_out, s2c, not_15_out, not_16_out);
  and and_13 (and_13_out, not_17_out, s2c, not_18_out, not_19_out, not_20_out);
  and and_14 (and_14_out, s2b, not_21_out, s1b);
  and and_15 (and_15_out, s2a, not_22_out, not_23_out);
  and and_16 (and_16_out, s2a, not_24_out, s1b, s1c);
  and and_17 (and_17_out, s2a, s2c, s1a);
  and and_18 (and_18_out, not_25_out, not_26_out, not_27_out, s1b);
  and and_19 (and_19_out, not_28_out, s1b, not_29_out);
  and and_20 (and_20_out, not_30_out, s2c, not_31_out, s1c);
  and and_21 (and_21_out, s2b, not_32_out, not_33_out);
  and and_22 (and_22_out, s2b, not_34_out, not_35_out);
  and and_23 (and_23_out, s2b, s2c, s1b, s1c);
  and and_24 (and_24_out, not_36_out, not_37_out, s1c);
  and and_25 (and_25_out, s2c, not_38_out);
  or or_2 (y, and_4_out, and_5_out, and_6_out, and_7_out, and_8_out, and_9_out);
  or or_3 (z, and_10_out, and_11_out, and_12_out, and_13_out, and_14_out, and_15_out, and_16_out, and_17_out);
  or or_4 (u, and_18_out, and_19_out, and_20_out, and_21_out, and_22_out, and_23_out);
  or or_5 (v, and_24_out, and_25_out);

  assign w = s1d;
endmodule

module Dec100_Led1_TIMER (
  input  g,
  input  f,
  input  e,
  input  d,
  input  c,
  input  b,
  input  a,
  output x,
  output y,
  output z,
  output u
);

  wire and_1_out, and_2_out, and_3_out, and_4_out, and_5_out, and_6_out, and_7_out, and_8_out, and_9_out,
       and_10_out, and_11_out, and_12_out, and_13_out, and_14_out, and_15_out, and_16_out, and_17_out,
       and_18_out, and_19_out, and_20_out, and_21_out, and_22_out, and_23_out, and_24_out, and_25_out,
       and_26_out, and_27_out, and_28_out, and_29_out, and_30_out, and_31_out, and_32_out, and_33_out,
       and_34_out, and_35_out, and_36_out, and_37_out, and_38_out, and_39_out, and_40_out, and_41_out,
       and_42_out, not_1_out, not_2_out, not_3_out, not_4_out, not_5_out, not_6_out, not_7_out, not_8_out,
       not_9_out, not_10_out, not_11_out, not_12_out, not_13_out, not_14_out, not_15_out, not_16_out,
       not_17_out, not_18_out, not_19_out, not_20_out, not_21_out, not_22_out, not_23_out, not_24_out,
       not_25_out, not_26_out, not_27_out, not_28_out, not_29_out, not_30_out, not_31_out, not_32_out,
       not_33_out, not_34_out, not_35_out, not_36_out, not_37_out, not_38_out, not_39_out, not_40_out,
       not_41_out, not_42_out, not_43_out, not_44_out, not_45_out, not_46_out, not_47_out, not_48_out,
       not_49_out, not_50_out, not_51_out, not_52_out, not_53_out, not_54_out, not_55_out, not_56_out,
       not_57_out, not_58_out, not_59_out, not_60_out, not_61_out, not_62_out, not_63_out, not_64_out,
       not_65_out, not_66_out, not_67_out, not_68_out, not_69_out, not_70_out, not_71_out, not_72_out,
       not_73_out, not_74_out, not_75_out, not_76_out, not_77_out, not_78_out, not_79_out, not_80_out,
       not_81_out, not_82_out, not_83_out, not_84_out, not_85_out, not_86_out, not_87_out, not_88_out,
       not_89_out, not_90_out, not_91_out, not_92_out, not_93_out, not_94_out, not_95_out, not_96_out,
       not_97_out, not_98_out, not_99_out, not_100_out, not_101_out, not_102_out, not_103_out, not_104_out,
       not_105_out, not_106_out, not_107_out, not_108_out, not_109_out, not_110_out, not_111_out,
       not_112_out, not_113_out, not_114_out;

  not not_1 (not_1_out, a);
  not not_2 (not_2_out, b);
  not not_3 (not_3_out, c);
  not not_4 (not_4_out, e);
  not not_5 (not_5_out, f);
  not not_6 (not_6_out, a);
  not not_7 (not_7_out, b);
  not not_8 (not_8_out, d);
  not not_9 (not_9_out, e);
  not not_10 (not_10_out, a);
  not not_11 (not_11_out, b);
  not not_12 (not_12_out, f);
  not not_13 (not_13_out, a);
  not not_14 (not_14_out, c);
  not not_15 (not_15_out, d);
  not not_16 (not_16_out, a);
  not not_17 (not_17_out, d);
  not not_18 (not_18_out, e);
  not not_19 (not_19_out, f);
  not not_20 (not_20_out, b);
  not not_21 (not_21_out, c);
  not not_22 (not_22_out, d);
  not not_23 (not_23_out, f);
  not not_24 (not_24_out, b);
  not not_25 (not_25_out, c);
  not not_26 (not_26_out, c);
  not not_27 (not_27_out, d);
  not not_28 (not_28_out, e);
  not not_29 (not_29_out, a);
  not not_30 (not_30_out, c);
  not not_31 (not_31_out, d);
  not not_32 (not_32_out, e);
  not not_33 (not_33_out, a);
  not not_34 (not_34_out, d);
  not not_35 (not_35_out, b);
  not not_36 (not_36_out, c);
  not not_37 (not_37_out, f);
  not not_38 (not_38_out, a);
  not not_39 (not_39_out, b);
  not not_40 (not_40_out, d);
  not not_41 (not_41_out, e);
  not not_42 (not_42_out, f);
  not not_43 (not_43_out, a);
  not not_44 (not_44_out, b);
  not not_45 (not_45_out, e);
  not not_46 (not_46_out, c);
  not not_47 (not_47_out, d);
  not not_48 (not_48_out, e);
  not not_49 (not_49_out, e);
  not not_50 (not_50_out, f);
  not not_51 (not_51_out, f);
  not not_52 (not_52_out, a);
  not not_53 (not_53_out, b);
  not not_54 (not_54_out, c);
  not not_55 (not_55_out, d);
  not not_56 (not_56_out, a);
  not not_57 (not_57_out, c);
  not not_58 (not_58_out, a);
  not not_59 (not_59_out, b);
  not not_60 (not_60_out, e);
  not not_61 (not_61_out, f);
  not not_62 (not_62_out, a);
  not not_63 (not_63_out, b);
  not not_64 (not_64_out, e);
  not not_65 (not_65_out, a);
  not not_66 (not_66_out, e);
  not not_67 (not_67_out, f);
  not not_68 (not_68_out, a);
  not not_69 (not_69_out, c);
  not not_70 (not_70_out, f);
  not not_71 (not_71_out, b);
  not not_72 (not_72_out, c);
  not not_73 (not_73_out, d);
  not not_74 (not_74_out, e);
  not not_75 (not_75_out, c);
  not not_76 (not_76_out, e);
  not not_77 (not_77_out, d);
  not not_78 (not_78_out, f);
  not not_79 (not_79_out, b);
  not not_80 (not_80_out, c);
  not not_81 (not_81_out, e);
  not not_82 (not_82_out, f);
  not not_83 (not_83_out, e);
  not not_84 (not_84_out, b);
  not not_85 (not_85_out, c);
  not not_86 (not_86_out, d);
  not not_87 (not_87_out, e);
  not not_88 (not_88_out, a);
  not not_89 (not_89_out, b);
  not not_90 (not_90_out, d);
  not not_91 (not_91_out, b);
  not not_92 (not_92_out, c);
  not not_93 (not_93_out, f);
  not not_94 (not_94_out, a);
  not not_95 (not_95_out, c);
  not not_96 (not_96_out, d);
  not not_97 (not_97_out, f);
  not not_98 (not_98_out, c);
  not not_99 (not_99_out, e);
  not not_100 (not_100_out, a);
  not not_101 (not_101_out, d);
  not not_102 (not_102_out, f);
  not not_103 (not_103_out, e);
  not not_104 (not_104_out, f);
  not not_105 (not_105_out, b);
  not not_106 (not_106_out, c);
  not not_107 (not_107_out, f);
  not not_108 (not_108_out, b);
  not not_109 (not_109_out, f);
  not not_110 (not_110_out, b);
  not not_111 (not_111_out, d);
  not not_112 (not_112_out, d);
  not not_113 (not_113_out, e);
  not not_114 (not_114_out, f);
  and and_1 (and_1_out, not_1_out, not_2_out, not_3_out, d, not_4_out, not_5_out);
  and and_2 (and_2_out, not_6_out, not_7_out, c, not_8_out, not_9_out, f);
  and and_3 (and_3_out, not_10_out, not_11_out, c, d, e, not_12_out);
  and and_4 (and_4_out, not_13_out, b, not_14_out, not_15_out, e, f);
  and and_5 (and_5_out, not_16_out, b, c, not_17_out, not_18_out, not_19_out);
  and and_6 (and_6_out, b, c, d, not_48_out, f);
  and and_7 (and_7_out, a, not_20_out, not_21_out, not_22_out, e, not_23_out);
  and and_8 (and_8_out, a, not_24_out, not_25_out, d, e, f);
  and and_9 (and_9_out, a, c, d, not_49_out, not_50_out);
  and and_10 (and_10_out, a, b, not_26_out, not_27_out, not_28_out, f);
  and and_11 (and_11_out, a, b, d, e, not_51_out);
  and and_12 (and_12_out, a, b, c, e, f);
  and and_13 (and_13_out, not_52_out, not_53_out, not_54_out, not_55_out, e);
  and and_14 (and_14_out, not_56_out, not_57_out, d, e, f);
  and and_15 (and_15_out, not_58_out, not_59_out, c, not_60_out, not_61_out);
  and and_16 (and_16_out, not_62_out, not_63_out, c, d, not_64_out);
  and and_17 (and_17_out, not_65_out, c, d, not_66_out, not_67_out);
  and and_18 (and_18_out, not_29_out, b, not_30_out, not_31_out, not_32_out, f);
  and and_19 (and_19_out, not_68_out, b, not_69_out, e, not_70_out);
  and and_20 (and_20_out, not_33_out, b, c, not_34_out, e, f);
  and and_21 (and_21_out, a, not_71_out, not_72_out, not_73_out, not_74_out);
  and and_22 (and_22_out, a, not_75_out, d, not_76_out, f);
  and and_23 (and_23_out, a, not_35_out, not_36_out, d, e, not_37_out);
  and and_24 (and_24_out, a, c, not_77_out, e, not_78_out);
  and and_25 (and_25_out, a, not_79_out, c, e, f);
  and and_26 (and_26_out, a, b, not_80_out, not_81_out, not_82_out);
  and and_27 (and_27_out, a, b, c, not_83_out, f);
  and and_28 (and_28_out, not_84_out, not_85_out, not_86_out, not_87_out, f);
  and and_29 (and_29_out, not_88_out, not_89_out, not_90_out, e, f);
  and and_30 (and_30_out, not_91_out, not_92_out, d, e, not_93_out);
  and and_31 (and_31_out, not_38_out, not_39_out, c, not_40_out, not_41_out, not_42_out);
  and and_32 (and_32_out, not_43_out, not_44_out, c, d, not_45_out, f);
  and and_33 (and_33_out, not_94_out, b, not_95_out, not_96_out, not_97_out);
  and and_34 (and_34_out, b, not_98_out, d, not_99_out, f);
  and and_35 (and_35_out, not_100_out, b, d, e, f);
  and and_36 (and_36_out, b, c, not_101_out, e, not_102_out);
  and and_37 (and_37_out, b, c, d, not_103_out, not_104_out);
  and and_38 (and_38_out, a, not_105_out, not_106_out, d, not_107_out);
  and and_39 (and_39_out, a, not_108_out, d, e, not_109_out);
  and and_40 (and_40_out, a, not_110_out, c, not_111_out, f);
  and and_41 (and_41_out, a, b, not_112_out, not_113_out, not_114_out);
  and and_42 (and_42_out, a, b, not_46_out, not_47_out, e, f);
  or or_1 (x, and_1_out, and_2_out, and_3_out, and_4_out, and_5_out, and_6_out, and_7_out, and_8_out, and_9_out, and_10_out, and_11_out, and_12_out);
  or or_2 (y, and_13_out, and_14_out, and_15_out, and_16_out, and_17_out, and_18_out, and_19_out, and_20_out, and_21_out, and_22_out, and_23_out, and_24_out, and_25_out, and_26_out, and_27_out);
  or or_3 (z, and_28_out, and_29_out, and_30_out, and_31_out, and_32_out, and_33_out, and_34_out, and_35_out, and_36_out, and_37_out, and_38_out, and_39_out, and_40_out, and_41_out, and_42_out);

  assign u = g;
endmodule

module Dec100_Led2_TIMER (
  input  a,
  input  b,
  input  c,
  input  d,
  input  e,
  input  f,
  input  g,
  output x,
  output y,
  output z,
  output u
);

  wire and_1_out, and_2_out, and_3_out, and_4_out, and_5_out, and_6_out, and_7_out, and_8_out, and_9_out,
       and_10_out, and_11_out, and_12_out, and_13_out, and_14_out, and_15_out, and_16_out, and_17_out,
       and_18_out, and_19_out, and_20_out, and_21_out, and_22_out, not_1_out, not_2_out, not_3_out,
       not_4_out, not_5_out, not_6_out, not_7_out, not_8_out, not_9_out, not_10_out, not_11_out, not_12_out,
       not_13_out, not_14_out, not_15_out, not_16_out, not_17_out, not_18_out, not_19_out, not_20_out,
       not_21_out, not_22_out, not_23_out, not_24_out, not_25_out, not_26_out, not_27_out, not_28_out,
       not_29_out, not_30_out, not_31_out, not_32_out, not_33_out;

  not not_1 (not_1_out, e);
  not not_2 (not_2_out, b);
  not not_3 (not_3_out, c);
  not not_4 (not_4_out, a);
  not not_5 (not_5_out, b);
  not not_6 (not_6_out, a);
  not not_7 (not_7_out, b);
  not not_8 (not_8_out, a);
  not not_9 (not_9_out, a);
  not not_10 (not_10_out, c);
  not not_11 (not_11_out, d);
  not not_12 (not_12_out, b);
  not not_13 (not_13_out, c);
  not not_14 (not_14_out, b);
  not not_15 (not_15_out, c);
  not not_16 (not_16_out, b);
  not not_17 (not_17_out, c);
  not not_18 (not_18_out, b);
  not not_19 (not_19_out, a);
  not not_20 (not_20_out, b);
  not not_21 (not_21_out, d);
  not not_22 (not_22_out, e);
  not not_23 (not_23_out, a);
  not not_24 (not_24_out, d);
  not not_25 (not_25_out, e);
  not not_26 (not_26_out, c);
  not not_27 (not_27_out, d);
  not not_28 (not_28_out, e);
  not not_29 (not_29_out, a);
  not not_30 (not_30_out, d);
  not not_31 (not_31_out, e);
  not not_32 (not_32_out, c);
  not not_33 (not_33_out, c);
  and and_1 (and_1_out, a, c);
  or or_1 (x, and_1_out, and_2_out);
  and and_2 (and_2_out, a, b, not_1_out);
  and and_3 (and_3_out, b, d);
  and and_4 (and_4_out, b, c);
  or or_2 (y, and_3_out, and_4_out, and_5_out);
  and and_5 (and_5_out, a, not_2_out, not_3_out);
  and and_6 (and_6_out, not_4_out, not_5_out, c, e);
  and and_7 (and_7_out, not_6_out, not_7_out, c, d);
  and and_8 (and_8_out, not_8_out, c, d, e);
  and and_9 (and_9_out, not_9_out, b, not_10_out, not_11_out);
  and and_10 (and_10_out, a, not_12_out, not_13_out);
  and and_11 (and_11_out, not_14_out, not_15_out, d, f);
  and and_12 (and_12_out, not_16_out, not_17_out, d, e);
  and and_13 (and_13_out, not_18_out, d, e, f);
  and and_14 (and_14_out, not_19_out, not_20_out, c, not_21_out, not_22_out);
  and and_15 (and_15_out, not_23_out, c, not_24_out, not_25_out, f);
  and and_16 (and_16_out, b, not_26_out, not_27_out, not_28_out);
  and and_17 (and_17_out, not_29_out, b, not_30_out, e);
  and and_18 (and_18_out, b, c, d, not_31_out);
  and and_19 (and_19_out, a, not_32_out, e, f);
  and and_20 (and_20_out, a, not_33_out, d);
  and and_21 (and_21_out, a, d, f);
  and and_22 (and_22_out, a, d, e);
  or or_3 (z, and_6_out, and_7_out, and_8_out, and_9_out, and_10_out);
  or or_4 (u, and_11_out, and_12_out, and_13_out, and_14_out, and_15_out, and_16_out, and_17_out, and_18_out, and_19_out, and_20_out, and_21_out, and_22_out);
endmodule

module FSM_CTDOWN (
  input  finish,
  input  D2,
  input  D1,
  input  D0,
  input  DIP,
  input  B1,
  input  B0,
  output Q2,
  output Q1,
  output Q0
);

  wire and_1_out, and_2_out, and_3_out, and_4_out, and_5_out, and_6_out, and_7_out, and_8_out, and_9_out,
       and_10_out, and_11_out, and_12_out, and_13_out, not_1_out, not_2_out, not_3_out, not_4_out, not_5_out,
       not_6_out, not_7_out, not_8_out, not_9_out, not_10_out, not_11_out, not_12_out, not_13_out,
       not_14_out, not_15_out, not_16_out, not_17_out, not_18_out, not_19_out, not_20_out, not_21_out,
       not_22_out, not_23_out, not_24_out, not_25_out, not_26_out, not_27_out, not_28_out, not_29_out,
       not_30_out;

  not not_1 (not_1_out, D1);
  not not_2 (not_2_out, D0);
  not not_3 (not_3_out, D2);
  not not_4 (not_4_out, D1);
  not not_5 (not_5_out, DIP);
  not not_6 (not_6_out, B0);
  not not_7 (not_7_out, D2);
  not not_8 (not_8_out, D0);
  not not_9 (not_9_out, B0);
  not not_10 (not_10_out, D2);
  not not_11 (not_11_out, D0);
  not not_12 (not_12_out, D2);
  not not_13 (not_13_out, D0);
  not not_14 (not_14_out, D2);
  not not_15 (not_15_out, D0);
  not not_16 (not_16_out, DIP);
  not not_17 (not_17_out, B1);
  not not_18 (not_18_out, D2);
  not not_19 (not_19_out, D1);
  not not_20 (not_20_out, B1);
  not not_21 (not_21_out, D2);
  not not_22 (not_22_out, D1);
  not not_23 (not_23_out, D2);
  not not_24 (not_24_out, D1);
  not not_25 (not_25_out, D2);
  not not_26 (not_26_out, D0);
  not not_27 (not_27_out, DIP);
  not not_28 (not_28_out, B0);
  and and_1 (and_1_out, not_1_out, not_2_out, DIP);
  and and_2 (and_2_out, D2, DIP);
  and and_3 (and_3_out, not_3_out, not_4_out, D0, not_5_out, B1, not_6_out);
  and and_4 (and_4_out, not_7_out, D1, not_8_out, not_9_out);
  and and_5 (and_5_out, not_10_out, D1, not_11_out, B1);
  and and_6 (and_6_out, not_12_out, D1, not_13_out, DIP);
  and and_7 (and_7_out, finish, not_29_out, D0);
  not not_29 (not_29_out, D1);
  and and_8 (and_8_out, not_14_out, not_15_out, not_16_out, not_17_out, B0);
  and and_9 (and_9_out, not_18_out, not_19_out, D0, not_20_out);
  and and_10 (and_10_out, not_21_out, not_22_out, D0, B0);
  and and_11 (and_11_out, not_23_out, not_24_out, D0, DIP);
  and and_12 (and_12_out, not_25_out, D1, not_26_out, not_27_out, B1, not_28_out);
  not not_30 (not_30_out, D1);
  and and_13 (and_13_out, finish, not_30_out, D0);
  or or_1 (Q2, and_1_out, and_2_out);
  or or_2 (Q1, and_3_out, and_4_out, and_5_out, and_6_out, and_7_out);
  or or_3 (Q0, and_8_out, and_9_out, and_10_out, and_11_out, and_12_out, and_13_out);
endmodule

module TransLogicCtDOwn (
  input  D2,
  input  D1,
  input  D0,
  output Reset,
  output Mount,
  output Run
);

  wire not_1_out, not_2_out, not_3_out;

  and and_1 (Reset, D1, D0);
  not not_1 (not_1_out, D1);
  not not_2 (not_2_out, D0);
  not not_3 (not_3_out, D1);
  and and_2 (Mount, not_1_out, not_2_out);
  and and_3 (Run, not_3_out, D0);
endmodule

module valselector (
  input  B1,
  input  c,
  input  b,
  input  a,
  output s1,
  output s2,
  output m1,
  output m2,
  output h1,
  output h2
);

  wire not_1_out, not_2_out, not_3_out, not_4_out, not_5_out, not_6_out, not_7_out, not_8_out, not_9_out,
       not_10_out, not_11_out;

  not not_1 (not_1_out, a);
  not not_2 (not_2_out, b);
  not not_3 (not_3_out, c);
  not not_4 (not_4_out, a);
  not not_5 (not_5_out, b);
  not not_6 (not_6_out, a);
  not not_7 (not_7_out, c);
  not not_8 (not_8_out, a);
  not not_9 (not_9_out, b);
  not not_10 (not_10_out, c);
  not not_11 (not_11_out, b);
  and and_1 (s1, B1, not_1_out, not_2_out, not_3_out);
  and and_2 (s2, B1, not_4_out, not_5_out, c);
  and and_3 (m1, B1, not_6_out, b, not_7_out);
  and and_4 (m2, B1, not_8_out, b, c);
  and and_5 (h1, B1, a, not_9_out, not_10_out);
  and and_6 (h2, B1, a, not_11_out, c);
endmodule
