// Logisim project TIMER.circ as structural Verilog: 19 circuits, main circuit timerFSM
module timerFSM (
  input  DIP,
  input  [1:0] B1_B0,
  output [7:0] sevsegCode_5,
  output [7:0] sevsegCode_4,
  output [7:0] sevsegCode_3,
  output [7:0] sevsegCode_2,
  output [7:0] sevsegCode_1,
  output [7:0] sevsegCode_0
);

  wire changeHour_1_hloadtendi, changeHour_1_hloaduendi, changeHour_1_minloadtendi,
       changeHour_1_minloaduendi, changeHour_1_secloadtendi, changeHour_1_secloaduendi, clk32k_to_2k_1_clk2k,
       clock_1_out, d_ff_1_q, d_ff_2_q, d_ff_3_q, FSMTIMER_q0, FSMTIMER_q1, FSMTIMER_q2, HOUR_1_hloadt,
       HOUR_1_hloadu, HOUR_1_minloadt, HOUR_1_minloadu, HOUR_1_secloadt, HOUR_1_secloadu, TL_reset, TL_setup,
       TL_start;
  wire [3:0] changeHour_1_hloadt_4, changeHour_1_hloadu_4, changeHour_1_minloadt_4, changeHour_1_minloadu_4,
       changeHour_1_secloadt_4, changeHour_1_secloadu_4, HOUR_1_ht_4, HOUR_1_hu_4, HOUR_1_mint_4,
       HOUR_1_minu_4, HOUR_1_sect_4, HOUR_1_secu_4;

  Clock clock_1 (.out(clock_1_out));
  fsm FSMTIMER (
    .D2(d_ff_3_q), .D1(d_ff_1_q), .D0(d_ff_2_q), .DIP(DIP), .B1(B1_B0[1]), .B0(B1_B0[0]), .Q2(FSMTIMER_q2),
    .Q1(FSMTIMER_q1), .Q0(FSMTIMER_q0));  // open: finish
  D_Flip_Flop d_ff_1 (.D(FSMTIMER_q1), .clk(clock_1_out), .Q(d_ff_1_q));  // open: Qn, preset, reset
  D_Flip_Flop d_ff_2 (.D(FSMTIMER_q0), .clk(clock_1_out), .Q(d_ff_2_q));  // open: Qn, preset, reset
  D_Flip_Flop d_ff_3 (.D(FSMTIMER_q2), .clk(clock_1_out), .Q(d_ff_3_q));  // open: Qn, preset, reset
  TransitLogic TL (.Q2(d_ff_3_q), .Q1(d_ff_1_q), .Q0(d_ff_2_q), .START(TL_start), .RESET(TL_reset), .SETUP(TL_setup));
  clk32k_to_2ksong clk32k_to_2k_1 (.CLK32k(clock_1_out), .CLK2k(clk32k_to_2k_1_clk2k));
  changeHoursong changeHour_1 (
    .DIP(TL_setup), .B1_B0(B1_B0), .HloadT_4(changeHour_1_hloadt_4), .HloadTEnDi(changeHour_1_hloadtendi),
    .HloadU_4(changeHour_1_hloadu_4), .HloadUEnDi(changeHour_1_hloaduendi),
    .MINloadT_4(changeHour_1_minloadt_4), .MINloadTEnDi(changeHour_1_minloadtendi),
    .MINloadU_4(changeHour_1_minloadu_4), .MINloadUEnDi(changeHour_1_minloaduendi),
    .SECloadT_4(changeHour_1_secloadt_4), .SECloadTEnDi(changeHour_1_secloadtendi),
    .SECloadU_4(changeHour_1_secloadu_4), .SECloadUEnDi(changeHour_1_secloaduendi));
  TIMER HOUR_1 (
    .START(TL_start), .RESET(TL_reset), .CLK2k(clk32k_to_2k_1_clk2k), .HloadT_4(changeHour_1_hloadt_4),
    .HloadTEnDi(changeHour_1_hloadtendi), .HloadU_4(changeHour_1_hloadu_4),
    .HloadUEnDi(changeHour_1_hloaduendi), .MINloadT_4(changeHour_1_minloadt_4),
    .MINloadTEnDi(changeHour_1_minloadtendi), .MINloadU_4(changeHour_1_minloadu_4),
    .MINloadUEnDi(changeHour_1_minloaduendi), .SECloadT_4(changeHour_1_secloadt_4),
    .SECloadTEnDi(changeHour_1_secloadtendi), .SECloadU_4(changeHour_1_secloadu_4),
    .SECloadUEnDi(changeHour_1_secloaduendi), .HT_4(HOUR_1_ht_4), .HU_4(HOUR_1_hu_4), .MINT_4(HOUR_1_mint_4),
    .MINU_4(HOUR_1_minu_4), .SECT_4(HOUR_1_sect_4), .SECU_4(HOUR_1_secu_4), .HloadT(HOUR_1_hloadt),
    .HloadU(HOUR_1_hloadu), .MINloadT(HOUR_1_minloadt), .MINloadU(HOUR_1_minloadu),
    .SECloadT(HOUR_1_secloadt), .SECloadU(HOUR_1_secloadu));
  hourView_HMSsong hourView_HMS_1 (
    .HT_4(HOUR_1_ht_4), .HU_4(HOUR_1_hu_4), .MINT_4(HOUR_1_mint_4), .MINU_4(HOUR_1_minu_4),
    .SECT_4(HOUR_1_sect_4), .SECU_4(HOUR_1_secu_4), .HloadT(HOUR_1_hloadt), .HloadU(HOUR_1_hloadu),
    .MINloadT(HOUR_1_minloadt), .MINloadU(HOUR_1_minloadu), .SECloadT(HOUR_1_secloadt),
    .SECloadU(HOUR_1_secloadu), .RESET(TL_reset), .CLK2k(clk32k_to_2k_1_clk2k), .sevsegCode_5(sevsegCode_5),
    .sevsegCode_4(sevsegCode_4), .sevsegCode_3(sevsegCode_3), .sevsegCode_2(sevsegCode_2),
    .sevsegCode_1(sevsegCode_1), .sevsegCode_0(sevsegCode_0));
endmodule

module TIMER (
  input  START,
  input  RESET,
  input  CLK2k,
  input  [3:0] HloadT_4,
  input  HloadTEnDi,
  input  [3:0] HloadU_4,
  input  HloadUEnDi,
  input  [3:0] MINloadT_4,
  input  MINloadTEnDi,
  input  [3:0] MINloadU_4,
  input  MINloadUEnDi,
  input  [3:0] SECloadT_4,
  input  SECloadTEnDi,
  input  [3:0] SECloadU_4,
  input  SECloadUEnDi,
  output [3:0] HT_4,
  output [3:0] HU_4,
  output [3:0] MINT_4,
  output [3:0] MINU_4,
  output [3:0] SECT_4,
  output [3:0] SECU_4,
  output HloadT,
  output HloadU,
  output MINloadT,
  output MINloadU,
  output SECloadT,
  output SECloadU
);

  wire clk2k_to_ticksec_1_ticksec, FiftyNineZeroTest_2_tickout, FiftyNineZeroTest_3_tickout;

  clk2k_to_ticksecsong clk2k_to_ticksec_1 (
    .START(START), .RESET(RESET), .CLK2k(CLK2k), .TickSEC(clk2k_to_ticksec_1_ticksec));
  FiftyNineZeroTest FiftyNineZeroTest_1 (
    .TickIn(FiftyNineZeroTest_2_tickout), .loadT_4(HloadT_4), .loadTEnDi(HloadTEnDi), .loadU_4(HloadU_4),
    .loadUEnDi(HloadUEnDi), .RESET(RESET), .CLK2K(CLK2k), .curT_3(HT_4), .curU_4(HU_4));  // open: TickOut
  FiftyNineZeroTest FiftyNineZeroTest_2 (
    .TickIn(FiftyNineZeroTest_3_tickout), .loadT_4(MINloadT_4), .loadTEnDi(MINloadTEnDi),
    .loadU_4(MINloadU_4), .loadUEnDi(MINloadUEnDi), .RESET(RESET), .CLK2K(CLK2k),
    .TickOut(FiftyNineZeroTest_2_tickout), .curT_3(MINT_4), .curU_4(MINU_4));
  FiftyNineZeroTest FiftyNineZeroTest_3 (
    .TickIn(clk2k_to_ticksec_1_ticksec), .loadT_4(SECloadT_4), .loadTEnDi(SECloadTEnDi),
    .loadU_4(SECloadU_4), .loadUEnDi(SECloadUEnDi), .RESET(RESET), .CLK2K(CLK2k),
    .TickOut(FiftyNineZeroTest_3_tickout), .curT_3(SECT_4), .curU_4(SECU_4));

  assign HloadT = HloadTEnDi;
  assign HloadU = HloadUEnDi;
  assign MINloadT = MINloadTEnDi;
  assign MINloadU = MINloadUEnDi;
  assign SECloadT = SECloadTEnDi;
  assign SECloadU = SECloadUEnDi;
endmodule

module TransitLogic (
  input  Q2,
  input  Q1,
  input  Q0,
  output START,
  output RESET,
  output SETUP
);

  wire not_1_out;

  not not_1 (not_1_out, Q1);
  and and_1 (RESET, Q1, Q0);
  and and_2 (START, not_1_out, Q0);

  assign SETUP = Q2;
endmodule

module fsm (
  input  finish,
  input  D2,
  input  D1,
  input  D0,
  input  DIP,
  input  B1,
  input  B0,
  output Q2,
  output Q1,
  output Q0
);

  wire and_1_out, and_2_out, and_3_out, and_4_out, and_5_out, and_6_out, and_7_out, and_8_out, and_9_out,
       and_10_out, and_11_out, and_12_out, and_13_out, not_1_out, not_2_out, not_3_out, not_4_out, not_5_out,
       not_6_out, not_7_out, not_8_out, not_9_out, not_10_out, not_11_out, not_12_out, not_13_out,
       not_14_out, not_15_out, not_16_out, not_17_out, not_18_out, not_19_out, not_20_out, not_21_out,
       not_22_out, not_23_out, not_24_out, not_25_out, not_26_out, not_27_out, not_28_out, not_29_out,
       not_30_out;

  not not_1 (not_1_out, D1);
  not not_2 (not_2_out, D0);
  not not_3 (not_3_out, D2);
  not not_4 (not_4_out, D1);
  not not_5 (not_5_out, DIP);
  not not_6 (not_6_out, B0);
  not not_7 (not_7_out, D2);
  not not_8 (not_8_out, D0);
  not not_9 (not_9_out, B0);
  not not_10 (not_10_out, D2);
  not not_11 (not_11_out, D0);
  not not_12 (not_12_out, D2);
  not not_13 (not_13_out, D0);
  not not_14 (not_14_out, D2);
  not not_15 (not_15_out, D0);
  not not_16 (not_16_out, DIP);
  not not_17 (not_17_out, B1);
  not not_18 (not_18_out, D2);
  not not_19 (not_19_out, D1);
  not not_20 (not_20_out, B1);
  not not_21 (not_21_out, D2);
  not not_22 (not_22_out, D1);
  not not_23 (not_23_out, D2);
  not not_24 (not_24_out, D1);
  not not_25 (not_25_out, D2);
  not not_26 (not_26_out, D0);
  not not_27 (not_27_out, DIP);
  not not_28 (not_28_out, B0);
  and and_1 (and_1_out, not_1_out, not_2_out, DIP);
  and and_2 (and_2_out, D2, DIP);
  and and_3 (and_3_out, not_3_out, not_4_out, D0, not_5_out, B1, not_6_out);
  and and_4 (and_4_out, not_7_out, D1, not_8_out, not_9_out);
  and and_5 (and_5_out, not_10_out, D1, not_11_out, B1);
  and and_6 (and_6_out, not_12_out, D1, not_13_out, DIP);
  and and_7 (and_7_out, finish, not_29_out, D0);
  not not_29 (not_29_out, D1);
  and and_8 (and_8_out, not_14_out, not_15_out, not_16_out, not_17_out, B0);
  and and_9 (and_9_out, not_18_out, not_19_out, D0, not_20_out);
  and and_10 (and_10_out, not_21_out, not_22_out, D0, B0);
  and and_11 (and_11_out, not_23_out, not_24_out, D0, DIP);
  and and_12 (and_12_out, not_25_out, D1, not_26_out, not_27_out, B1, not_28_out);
  not not_30 (not_30_out, D1);
  and and_13 (and_13_out, finish, not_30_out, D0);
  or or_1 (Q2, and_1_out, and_2_out);
  or or_2 (Q1, and_3_out, and_4_out, and_5_out, and_6_out, and_7_out);
  or or_3 (Q0, and_8_out, and_9_out, and_10_out, and_11_out, and_12_out, and_13_out);
endmodule

module fiveZero (
  input  TickIn,
  input  IN2,
  input  IN1,
  input  IN0,
  output TickOUT,
  output OUT2,
  output OUT1,
  output OUT0
);

  wire and_1_out, and_2_out, and_4_out, and_5_out, and_6_out, and_7_out, and_8_out, and_9_out, and_10_out,
       not_1_out, not_2_out, not_3_out, not_4_out, not_5_out, not_6_out, not_7_out, not_8_out, not_9_out,
       not_10_out, not_11_out, not_12_out, not_13_out;

  not not_1 (not_1_out, TickIn);
  not not_2 (not_2_out, IN2);
  not not_3 (not_3_out, IN1);
  not not_4 (not_4_out, IN0);
  not not_5 (not_5_out, TickIn);
  not not_6 (not_6_out, IN2);
  not not_7 (not_7_out, IN1);
  not not_8 (not_8_out, IN0);
  not not_9 (not_9_out, TickIn);
  not not_10 (not_10_out, IN1);
  not not_11 (not_11_out, IN0);
  not not_12 (not_12_out, TickIn);
  and and_1 (and_1_out, not_12_out, not_13_out);
  not not_13 (not_13_out, IN0);
  and and_2 (and_2_out, TickIn, IN0);
  and and_3 (TickOUT, not_1_out, not_2_out, not_3_out, not_4_out);
  and and_4 (and_4_out, not_5_out, not_6_out, not_7_out, not_8_out);
  and and_5 (and_5_out, IN2, IN0);
  and and_6 (and_6_out, IN2, IN1);
  and and_7 (and_7_out, TickIn, IN2);
  and and_8 (and_8_out, IN1, IN0);
  or or_1 (OUT1, and_8_out, and_9_out, and_10_out);
  and and_9 (and_9_out, not_9_out, IN2, not_10_out, not_11_out);
  and and_10 (and_10_out, TickIn, IN1);
  or or_2 (OUT0, and_1_out, and_2_out);
  or or_3 (OUT2, and_4_out, and_5_out, and_6_out, and_7_out);
endmodule

module nineZero (
  input  TickIn,
  input  IN3,
  input  IN2,
  input  IN1,
  input  IN0,
  output TickOUT,
  output OUT3,
  output OUT2,
  output OUT1,
  output OUT0
);

  wire and_2_out, and_3_out, and_4_out, and_5_out, and_6_out, and_7_out, and_8_out, and_9_out, and_10_out,
       and_11_out, and_12_out, and_13_out, and_14_out, and_15_out, not_1_out, not_2_out, not_3_out,
       not_4_out, not_5_out, not_6_out, not_7_out, not_8_out, not_9_out, not_10_out, not_11_out, not_12_out,
       not_13_out, not_14_out, not_15_out, not_16_out, not_17_out, not_18_out, not_19_out, not_20_out,
       not_21_out;

  not not_1 (not_1_out, TickIn);
  not not_2 (not_2_out, IN3);
  not not_3 (not_3_out, IN2);
  not not_4 (not_4_out, IN1);
  not not_5 (not_5_out, IN0);
  not not_6 (not_6_out, TickIn);
  not not_7 (not_7_out, IN3);
  not not_8 (not_8_out, IN2);
  not not_9 (not_9_out, IN1);
  not not_10 (not_10_out, IN0);
  not not_11 (not_11_out, TickIn);
  not not_12 (not_12_out, IN1);
  not not_13 (not_13_out, IN0);
  not not_14 (not_14_out, TickIn);
  not not_15 (not_15_out, IN1);
  not not_16 (not_16_out, IN0);
  not not_17 (not_17_out, TickIn);
  not not_18 (not_18_out, IN1);
  not not_19 (not_19_out, IN0);
  not not_20 (not_20_out, TickIn);
  not not_21 (not_21_out, IN0);
  and and_1 (TickOUT, not_1_out, not_2_out, not_3_out, not_4_out, not_5_out);
  and and_2 (and_2_out, not_6_out, not_7_out, not_8_out, not_9_out, not_10_out);
  and and_3 (and_3_out, IN3, IN0);
  and and_4 (and_4_out, IN3, IN1);
  and and_5 (and_5_out, TickIn, IN3);
  and and_6 (and_6_out, IN2, IN0);
  and and_7 (and_7_out, IN2, IN1);
  and and_8 (and_8_out, not_11_out, IN3, not_12_out, not_13_out);
  and and_9 (and_9_out, TickIn, IN2);
  and and_10 (and_10_out, IN1, IN0);
  and and_11 (and_11_out, not_14_out, IN2, not_15_out, not_16_out);
  and and_12 (and_12_out, not_17_out, IN3, not_18_out, not_19_out);
  and and_13 (and_13_out, TickIn, IN1);
  and and_14 (and_14_out, not_20_out, not_21_out);
  and and_15 (and_15_out, TickIn, IN0);
  or or_1 (OUT3, and_2_out, and_3_out, and_4_out, and_5_out);
  or or_2 (OUT2, and_6_out, and_7_out, and_8_out, and_9_out);
  or or_3 (OUT1, and_10_out, and_11_out, and_12_out, and_13_out);
  or or_4 (OUT0, and_14_out, and_15_out);
endmodule

module FiftyNineZeroTest (
  input  TickIn,
  input  [3:0] loadT_4,
  input  loadTEnDi,
  input  [3:0] loadU_4,
  input  loadUEnDi,
  input  RESET,
  input  CLK2K,
  output TickOut,
  output [3:0] curT_3,
  output [3:0] curU_4
);

  wire and_1_out, counter_1_carry, counter_2_carry;
  wire [2:0] bit_extender_1_out, counter_1_q, load_3song_1_out0;
  wire [3:0] counter_2_q;

  Bit_Extender #(.in_width(4), .out_width(3), .\type ("zero")) bit_extender_1 (.in(loadT_4), .out(bit_extender_1_out));
  and and_1 (and_1_out, counter_2_carry, TickIn);
  Counter #(.width(3), .max('h5)) counter_1 (
    .clr(RESET), .load(loadTEnDi), .up(1'b0), .count(and_1_out), .clk(CLK2K), .D(bit_extender_1_out),
    .carry(counter_1_carry), .Q(counter_1_q));
  Counter #(.width(4), .max('h9)) counter_2 (
    .clr(RESET), .load(loadUEnDi), .up(1'b0), .count(TickIn), .clk(CLK2K), .D(loadU_4),
    .carry(counter_2_carry), .Q(counter_2_q));
  and and_2 (TickOut, TickIn, counter_1_carry, counter_2_carry);
  load_3song load_3song_1 (.val(counter_1_q), .loadValue(loadT_4), .loadEnDi(loadTEnDi), .OUT0(load_3song_1_out0));
  load_4song load_4song_1 (.val(counter_2_q), .loadValue(loadU_4), .loadEnDi(loadUEnDi), .OUT0(curU_4));
  assign curT_3 = {{1{1'b0}}, load_3song_1_out0};  // Bit_Extender bit_extender_2
endmodule

module clk32k_to_2ksong (
  input  CLK32k,
  output CLK2k
);

  wire d_ff_1_q, d_ff_1_qn, d_ff_2_q, d_ff_2_qn, d_ff_3_q, d_ff_3_qn, d_ff_4_qn;

  D_Flip_Flop d_ff_1 (.D(d_ff_1_qn), .clk(CLK32k), .Q(d_ff_1_q), .Qn(d_ff_1_qn));  // open: preset, reset
  D_Flip_Flop d_ff_2 (.D(d_ff_2_qn), .clk(d_ff_1_q), .Q(d_ff_2_q), .Qn(d_ff_2_qn));  // open: preset, reset
  D_Flip_Flop d_ff_3 (.D(d_ff_3_qn), .clk(d_ff_2_q), .Q(d_ff_3_q), .Qn(d_ff_3_qn));  // open: preset, reset
  D_Flip_Flop d_ff_4 (.D(d_ff_4_qn), .clk(d_ff_3_q), .Q(CLK2k), .Qn(d_ff_4_qn));  // open: preset, reset
endmodule

module clk2k_to_ticksecsong (
  input  START,
  input  RESET,
  input  CLK2k,
  output TickSEC
);

  Counter #(.width(10), .max('h3e9)) counter_1 (
    .clr(RESET), .count(START), .clk(CLK2k), .carry(TickSEC));  // open: load, up, D, Q
endmodule

module hourView_HMSsong (
  input  [3:0] HT_4,
  input  [3:0] HU_4,
  input  [3:0] MINT_4,
  input  [3:0] MINU_4,
  input  [3:0] SECT_4,
  input  [3:0] SECU_4,
  input  HloadT,
  input  HloadU,
  input  MINloadT,
  input  MINloadU,
  input  SECloadT,
  input  SECloadU,
  input  RESET,
  input  CLK2k,
  output [7:0] sevsegCode_5,
  output [7:0] sevsegCode_4,
  output [7:0] sevsegCode_3,
  output [7:0] sevsegCode_2,
  output [7:0] sevsegCode_1,
  output [7:0] sevsegCode_0
);

  wire and_1_out, and_2_out, and_3_out, and_4_out, and_5_out, and_6_out, clk2k_to_4_1_clk4, or_1_out,
       t_ff_1_q;
  wire [6:0] bit_extender_2_out, bit_extender_4_out, multiplexer_2_out, multiplexer_4_out;
  wire [7:0] bit_extender_1_out, bit_extender_3_out, bit_extender_5_out, bit_extender_6_out;

  assign bit_extender_1_out = {{4{1'b0}}, HT_4};  // Bit_Extender bit_extender_1
  assign bit_extender_2_out = {{3{1'b0}}, HU_4};  // Bit_Extender bit_extender_2
  assign bit_extender_3_out = {{4{1'b0}}, MINT_4};  // Bit_Extender bit_extender_3
  assign bit_extender_4_out = {{3{1'b0}}, MINU_4};  // Bit_Extender bit_extender_4
  assign bit_extender_5_out = {{4{1'b0}}, SECT_4};  // Bit_Extender bit_extender_5
  assign bit_extender_6_out = {{4{1'b0}}, SECU_4};  // Bit_Extender bit_extender_6
  clk2k_to_4song clk2k_to_4_1 (.CLK2k(CLK2k), .CLK4(clk2k_to_4_1_clk4));
  T_Flip_Flop t_ff_1 (.T(or_1_out), .clk(clk2k_to_4_1_clk4), .Q(t_ff_1_q), .reset(RESET));  // open: Qn, preset
  or or_1 (or_1_out, HloadT, HloadU, MINloadT, MINloadU, SECloadT, SECloadU);
  Multiplexer #(.width(8), .enable("false")) multiplexer_1 (
    .in0(bit_extender_1_out), .in1(8'h7f), .out(sevsegCode_5), .sel(and_1_out));
  and and_1 (and_1_out, HloadT, t_ff_1_q);
  and and_2 (and_2_out, HloadU, t_ff_1_q);
  Multiplexer #(.width(7), .enable("false")) multiplexer_2 (
    .in0(bit_extender_2_out), .in1({7{1'b1}}), .out(multiplexer_2_out), .sel(and_2_out));
  Multiplexer #(.width(8), .enable("false")) multiplexer_3 (
    .in0(bit_extender_3_out), .in1(8'h7f), .out(sevsegCode_3), .sel(and_3_out));
  and and_3 (and_3_out, MINloadT, t_ff_1_q);
  Multiplexer #(.width(7), .enable("false")) multiplexer_4 (
    .in0(bit_extender_4_out), .in1({7{1'b1}}), .out(multiplexer_4_out), .sel(and_4_out));
  and and_4 (and_4_out, MINloadU, t_ff_1_q);
  assign sevsegCode_4 = {{1{1'b1}}, multiplexer_2_out};  // Bit_Extender bit_extender_7
  assign sevsegCode_2 = {{1{1'b1}}, multiplexer_4_out};  // Bit_Extender bit_extender_8
  Multiplexer #(.width(8), .enable("false")) multiplexer_5 (
    .in0(bit_extender_5_out), .in1(8'h7f), .out(sevsegCode_1), .sel(and_5_out));
  and and_5 (and_5_out, SECloadT, t_ff_1_q);
  Multiplexer #(.width(8), .enable("false")) multiplexer_6 (
    .in0(bit_extender_6_out), .in1(8'h7f), .out(sevsegCode_0), .sel(and_6_out));
  and and_6 (and_6_out, SECloadU, t_ff_1_q);
endmodule

module load_2song (
  input  IN1,
  input  IN0,
  input  [3:0] loadValue,
  input  loadEnDi,
  output OUT1,
  output OUT0
);

  Multiplexer #(.enable("false")) multiplexer_1 (.in0(IN1), .in1(loadValue[1]), .out(OUT1), .sel(loadEnDi));
  Multiplexer #(.enable("false")) multiplexer_2 (.in0(IN0), .in1(loadValue[0]), .out(OUT0), .sel(loadEnDi));
endmodule

module load_3song (
  input  [2:0] val,
  input  [3:0] loadValue,
  input  loadEnDi,
  output [2:0] OUT0
);

  wire [2:0] bit_extender_1_out;

  Bit_Extender #(.in_width(4), .out_width(3)) bit_extender_1 (.in(loadValue), .out(bit_extender_1_out));
  Multiplexer #(.width(3), .enable("false")) multiplexer_1 (
    .in0(val), .in1(bit_extender_1_out), .out(OUT0), .sel(loadEnDi));
endmodule

module load_4song (
  input  [3:0] val,
  input  [3:0] loadValue,
  input  loadEnDi,
  output [3:0] OUT0
);

  Multiplexer #(.width(4), .enable("false")) multiplexer_1 (.in0(val), .in1(loadValue), .out(OUT0), .sel(loadEnDi));
endmodule

module changeHoursong (
  input  DIP,
  input  [1:0] B1_B0,
  output [3:0] HloadT_4,
  output HloadTEnDi,
  output [3:0] HloadU_4,
  output HloadUEnDi,
  output [3:0] MINloadT_4,
  output MINloadTEnDi,
  output [3:0] MINloadU_4,
  output MINloadUEnDi,
  output [3:0] SECloadT_4,
  output SECloadTEnDi,
  output [3:0] SECloadU_4,
  output SECloadUEnDi
);

  wire and_1_out, and_2_out, demultiplexer_1_out1, demultiplexer_1_out2, demultiplexer_1_out3,
       demultiplexer_1_out4, demultiplexer_1_out5, demultiplexer_1_out6, demultiplexer_2_out0;
  wire [2:0] counter_1_q, counter_2_q, counter_4_q, counter_6_q;

  and and_1 (and_1_out, DIP, B1_B0[1]);
  Counter #(.width(3), .max('h6)) counter_1 (.clk(and_2_out), .Q(counter_1_q));  // open: clr, load, up, count, D, carry
  and and_2 (and_2_out, B1_B0[0], DIP);
  Demultiplexer #(.select(3), .enable("false")) demultiplexer_1 (
    .out1(demultiplexer_1_out1), .out2(demultiplexer_1_out2), .out3(demultiplexer_1_out3),
    .out4(demultiplexer_1_out4), .out5(demultiplexer_1_out5), .out6(demultiplexer_1_out6), .in(and_1_out),
    .sel(counter_1_q));  // open: out0, out7
  Demultiplexer #(.select(3), .enable("false")) demultiplexer_2 (
    .out0(demultiplexer_2_out0), .out1(HloadTEnDi), .out2(HloadUEnDi), .out3(MINloadTEnDi),
    .out4(MINloadUEnDi), .out5(SECloadTEnDi), .out6(SECloadUEnDi), .in(1'b1), .sel(counter_1_q));  // open: out7
  Counter #(.width(3), .max('h5)) counter_2 (
    .clr(demultiplexer_2_out0), .clk(demultiplexer_1_out1), .Q(counter_2_q));  // open: load, up, count, D, carry
  Counter #(.width(4), .max('h9)) counter_3 (
    .clr(demultiplexer_2_out0), .clk(demultiplexer_1_out2), .Q(HloadU_4));  // open: load, up, count, D, carry
  Counter #(.width(3), .max('h5)) counter_4 (
    .clr(demultiplexer_2_out0), .clk(demultiplexer_1_out3), .Q(counter_4_q));  // open: load, up, count, D, carry
  Counter #(.width(4), .max('h9)) counter_5 (
    .clr(demultiplexer_2_out0), .clk(demultiplexer_1_out4), .Q(MINloadU_4));  // open: load, up, count, D, carry
  Counter #(.width(3), .max('h5)) counter_6 (
    .clr(demultiplexer_2_out0), .clk(demultiplexer_1_out5), .Q(counter_6_q));  // open: load, up, count, D, carry
  Counter #(.width(4), .max('h9)) counter_7 (
    .clr(demultiplexer_2_out0), .clk(demultiplexer_1_out6), .Q(SECloadU_4));  // open: load, up, count, D, carry
  assign HloadT_4 = {{1{1'b0}}, counter_2_q};  // Bit_Extender bit_extender_1
  assign MINloadT_4 = {{1{1'b0}}, counter_4_q};  // Bit_Extender bit_extender_2
  assign SECloadT_4 = {{1{1'b0}}, counter_6_q};  // Bit_Extender bit_extender_3
endmodule

module fivebits_to_2_4bitssong (
  input  A4,
  input  A3,
  input  A2,
  input  A1,
  input  A0,
  output T3,
  output T2,
  output T1,
  output T0,
  output U3,
  output U2,
  output U1,
  output U0
);

  wire and_1_out, and_2_out, and_3_out, and_4_out, and_5_out, and_6_out, and_7_out, and_8_out, and_9_out,
       and_10_out, and_11_out, and_12_out, and_13_out, and_14_out, and_15_out, and_16_out, and_17_out,
       and_18_out, not_1_out, not_2_out, not_3_out, not_4_out, not_5_out, not_6_out, not_7_out, not_8_out,
       not_9_out, not_10_out, not_11_out, not_12_out, not_13_out, not_14_out, not_15_out, not_16_out,
       not_17_out, not_18_out, not_19_out, not_20_out, not_21_out, not_22_out, not_23_out, not_24_out,
       not_25_out;

  and and_1 (and_1_out, A4, A2);
  and and_2 (and_2_out, A4, A3);
  not not_1 (not_1_out, A4);
  not not_2 (not_2_out, A4);
  not not_3 (not_3_out, A3);
  not not_4 (not_4_out, A2);
  not not_5 (not_5_out, A4);
  not not_6 (not_6_out, A2);
  not not_7 (not_7_out, A1);
  not not_8 (not_8_out, A3);
  not not_9 (not_9_out, A2);
  not not_10 (not_10_out, A1);
  not not_11 (not_11_out, A4);
  not not_12 (not_12_out, A3);
  not not_13 (not_13_out, A4);
  not not_14 (not_14_out, A2);
  not not_15 (not_15_out, A1);
  not not_16 (not_16_out, A2);
  not not_17 (not_17_out, A4);
  not not_18 (not_18_out, A3);
  not not_19 (not_19_out, A3);
  not not_20 (not_20_out, A4);
  not not_21 (not_21_out, A1);
  not not_22 (not_22_out, A3);
  not not_23 (not_23_out, A2);
  not not_24 (not_24_out, A1);
  not not_25 (not_25_out, A2);
  or or_1 (T1, and_1_out, and_2_out);
  and and_3 (and_3_out, not_1_out, A3, A1);
  and and_4 (and_4_out, not_2_out, A3, A2);
  and and_5 (and_5_out, A3, A2, A1);
  and and_6 (and_6_out, A4, not_3_out, not_4_out);
  and and_7 (and_7_out, not_5_out, A3, not_6_out, not_7_out);
  and and_8 (and_8_out, A4, not_8_out, not_9_out, A1);
  and and_9 (and_9_out, A4, A3, A2, not_10_out);
  and and_10 (and_10_out, not_11_out, not_12_out, A2);
  and and_11 (and_11_out, not_13_out, A2, A1);
  and and_12 (and_12_out, A4, not_14_out, not_15_out);
  and and_13 (and_13_out, A4, A3, not_16_out);
  and and_14 (and_14_out, not_17_out, not_18_out, A1);
  and and_15 (and_15_out, not_19_out, A2, A1);
  and and_16 (and_16_out, not_20_out, A3, A2, not_21_out);
  and and_17 (and_17_out, A4, not_22_out, not_23_out, not_24_out);
  and and_18 (and_18_out, A4, A3, not_25_out, A1);
  or or_2 (T0, and_3_out, and_4_out, and_5_out, and_6_out);
  or or_3 (U3, and_7_out, and_8_out, and_9_out);
  or or_4 (U2, and_10_out, and_11_out, and_12_out, and_13_out);
  or or_5 (U1, and_14_out, and_15_out, and_16_out, and_17_out, and_18_out);

  assign T2 = 1'b0;
  assign T3 = 1'b0;
  assign U0 = A0;
endmodule

module DecoderToSegLed_bissong (
  input  Input_1,
  input  Input_2,
  input  Input_3,
  input  Input_4,
  input  Input_5,
  input  Input_6,
  output Output_1,
  output Output_2,
  output Output_3,
  output Output_4,
  output Output_5,
  output Output_6,
  output Output_7,
  output Output_8
);

  wire and_1_out, and_2_out, and_3_out, and_4_out, and_5_out, and_6_out, and_7_out, and_8_out, and_9_out,
       and_10_out, and_11_out, and_12_out, and_13_out, and_14_out, and_15_out, and_16_out, and_17_out,
       and_18_out, and_19_out, and_20_out, and_21_out, and_22_out, and_23_out, and_24_out, and_25_out,
       and_26_out, and_27_out, and_28_out, and_29_out, and_30_out, and_31_out, and_32_out, and_33_out,
       and_34_out, and_35_out, and_36_out, and_37_out, and_38_out, and_39_out, and_40_out, and_41_out,
       and_42_out, and_43_out, and_44_out, and_45_out, and_46_out, and_47_out, and_48_out, and_49_out,
       and_50_out, and_51_out, and_52_out, and_53_out, not_1_out, not_2_out, not_3_out, not_4_out, not_5_out,
       not_6_out, not_7_out, not_8_out, not_9_out, not_10_out, not_11_out, not_12_out, not_13_out,
       not_14_out, not_15_out, not_16_out, not_17_out, not_18_out, not_19_out, not_20_out, not_21_out,
       not_22_out, not_23_out, not_24_out, not_25_out, not_26_out, not_27_out, not_28_out, not_29_out,
       not_30_out, not_31_out, not_32_out, not_33_out, not_34_out, not_35_out, not_36_out, not_37_out,
       not_38_out, not_39_out, not_40_out, not_41_out, not_42_out, not_43_out, not_44_out, not_45_out,
       not_46_out, not_47_out, not_48_out, not_49_out, not_50_out, not_51_out, not_52_out, not_53_out,
       not_54_out, not_55_out, not_56_out, not_57_out, not_58_out, not_59_out, not_60_out, not_61_out,
       not_62_out, not_63_out, not_64_out, not_65_out, not_66_out, not_67_out, not_68_out, not_69_out,
       not_70_out, not_71_out, not_72_out, not_73_out, not_74_out, not_75_out, not_76_out, not_77_out,
       not_78_out, not_79_out, not_80_out, not_81_out, not_82_out, not_83_out, not_84_out, not_85_out,
       not_86_out, not_87_out, not_88_out, not_89_out, not_90_out, not_91_out, not_92_out, not_93_out,
       not_94_out, not_95_out, not_96_out;

  not not_1 (not_1_out, Input_4);
  not not_2 (not_2_out, Input_5);
  not not_3 (not_3_out, Input_6);
  not not_4 (not_4_out, Input_2);
  not not_5 (not_5_out, Input_3);
  not not_6 (not_6_out, Input_3);
  not not_7 (not_7_out, Input_5);
  not not_8 (not_8_out, Input_2);
  not not_9 (not_9_out, Input_2);
  not not_10 (not_10_out, Input_6);
  not not_11 (not_11_out, Input_4);
  not not_12 (not_12_out, Input_5);
  not not_13 (not_13_out, Input_4);
  not not_14 (not_14_out, Input_2);
  not not_15 (not_15_out, Input_3);
  not not_16 (not_16_out, Input_5);
  not not_17 (not_17_out, Input_6);
  not not_18 (not_18_out, Input_2);
  not not_19 (not_19_out, Input_4);
  not not_20 (not_20_out, Input_6);
  not not_21 (not_21_out, Input_3);
  not not_22 (not_22_out, Input_4);
  not not_23 (not_23_out, Input_2);
  not not_24 (not_24_out, Input_3);
  not not_25 (not_25_out, Input_4);
  not not_26 (not_26_out, Input_5);
  not not_27 (not_27_out, Input_2);
  not not_28 (not_28_out, Input_5);
  not not_29 (not_29_out, Input_3);
  not not_30 (not_30_out, Input_5);
  not not_31 (not_31_out, Input_6);
  not not_32 (not_32_out, Input_3);
  not not_33 (not_33_out, Input_4);
  not not_34 (not_34_out, Input_5);
  not not_35 (not_35_out, Input_3);
  not not_36 (not_36_out, Input_4);
  not not_37 (not_37_out, Input_5);
  not not_38 (not_38_out, Input_2);
  not not_39 (not_39_out, Input_3);
  not not_40 (not_40_out, Input_2);
  not not_41 (not_41_out, Input_4);
  not not_42 (not_42_out, Input_6);
  not not_43 (not_43_out, Input_2);
  not not_44 (not_44_out, Input_3);
  not not_45 (not_45_out, Input_4);
  not not_46 (not_46_out, Input_6);
  not not_47 (not_47_out, Input_2);
  not not_48 (not_48_out, Input_3);
  not not_49 (not_49_out, Input_6);
  not not_50 (not_50_out, Input_4);
  not not_51 (not_51_out, Input_2);
  not not_52 (not_52_out, Input_5);
  not not_53 (not_53_out, Input_2);
  not not_54 (not_54_out, Input_5);
  not not_55 (not_55_out, Input_5);
  not not_56 (not_56_out, Input_6);
  not not_57 (not_57_out, Input_3);
  not not_58 (not_58_out, Input_5);
  not not_59 (not_59_out, Input_6);
  not not_60 (not_60_out, Input_3);
  not not_61 (not_61_out, Input_4);
  not not_62 (not_62_out, Input_6);
  not not_63 (not_63_out, Input_2);
  not not_64 (not_64_out, Input_6);
  not not_65 (not_65_out, Input_2);
  not not_66 (not_66_out, Input_5);
  not not_67 (not_67_out, Input_3);
  not not_68 (not_68_out, Input_5);
  not not_69 (not_69_out, Input_3);
  not not_70 (not_70_out, Input_5);
  not not_71 (not_71_out, Input_6);
  not not_72 (not_72_out, Input_2);
  not not_73 (not_73_out, Input_6);
  not not_74 (not_74_out, Input_3);
  not not_75 (not_75_out, Input_5);
  not not_76 (not_76_out, Input_4);
  not not_77 (not_77_out, Input_2);
  not not_78 (not_78_out, Input_6);
  not not_79 (not_79_out, Input_3);
  not not_80 (not_80_out, Input_4);
  not not_81 (not_81_out, Input_6);
  not not_82 (not_82_out, Input_3);
  not not_83 (not_83_out, Input_5);
  not not_84 (not_84_out, Input_2);
  not not_85 (not_85_out, Input_4);
  not not_86 (not_86_out, Input_2);
  not not_87 (not_87_out, Input_6);
  not not_88 (not_88_out, Input_2);
  not not_89 (not_89_out, Input_3);
  not not_90 (not_90_out, Input_5);
  not not_91 (not_91_out, Input_4);
  not not_92 (not_92_out, Input_2);
  not not_93 (not_93_out, Input_4);
  not not_94 (not_94_out, Input_5);
  not not_95 (not_95_out, Input_3);
  not not_96 (not_96_out, Input_6);
  and and_1 (and_1_out, not_1_out, not_2_out, not_3_out);
  and and_2 (and_2_out, not_4_out, not_5_out, Input_5);
  and and_3 (and_3_out, not_6_out, Input_4, not_7_out, Input_6);
  and and_4 (and_4_out, not_8_out, Input_4, Input_5);
  and and_5 (and_5_out, not_9_out, Input_3, not_10_out);
  and and_6 (and_6_out, Input_3, not_11_out, not_12_out);
  and and_7 (and_7_out, Input_2, Input_3, not_13_out, Input_6);
  and and_8 (and_8_out, not_14_out, not_15_out, not_16_out, not_17_out);
  and and_9 (and_9_out, not_18_out, not_19_out, not_20_out);
  and and_10 (and_10_out, not_21_out, not_22_out, Input_6);
  and and_11 (and_11_out, not_23_out, not_24_out, Input_5, Input_6);
  and and_12 (and_12_out, Input_3, not_25_out, not_26_out);
  and and_13 (and_13_out, not_27_out, Input_3, not_28_out, Input_6);
  and and_14 (and_14_out, Input_2, not_29_out, not_30_out, Input_6);
  and and_15 (and_15_out, Input_2, Input_3, Input_4, Input_5, not_31_out);
  and and_16 (and_16_out, not_32_out, not_33_out, not_34_out);
  and and_17 (and_17_out, not_35_out, Input_6);
  and and_18 (and_18_out, not_36_out, Input_6);
  and and_19 (and_19_out, not_37_out, Input_6);
  and and_20 (and_20_out, not_38_out, not_39_out, Input_4);
  and and_21 (and_21_out, not_40_out, Input_3, not_41_out);
  and and_22 (and_22_out, Input_2, Input_4, Input_5, not_42_out);
  and and_23 (and_23_out, not_43_out, not_44_out, not_45_out, not_46_out);
  and and_24 (and_24_out, not_47_out, not_48_out, Input_5, not_49_out);
  and and_25 (and_25_out, not_50_out, Input_5, Input_6);
  and and_26 (and_26_out, not_51_out, Input_4, not_52_out, Input_6);
  and and_27 (and_27_out, not_53_out, Input_3, not_54_out);
  and and_28 (and_28_out, Input_3, Input_4, not_55_out);
  and and_29 (and_29_out, Input_3, Input_4, not_56_out);
  and and_30 (and_30_out, Input_2, not_57_out, not_58_out, not_59_out);
  and and_31 (and_31_out, Input_2, not_60_out, Input_5, Input_6);
  and and_32 (and_32_out, not_61_out, not_62_out);
  and and_33 (and_33_out, not_63_out, Input_5, not_64_out);
  and and_34 (and_34_out, not_65_out, Input_3, Input_5);
  and and_35 (and_35_out, Input_3, Input_4, not_66_out);
  and and_36 (and_36_out, Input_2, not_67_out, not_68_out);
  and and_37 (and_37_out, Input_2, not_69_out, Input_4);
  and and_38 (and_38_out, not_70_out, not_71_out);
  and and_39 (and_39_out, not_72_out, Input_4, not_73_out);
  and and_40 (and_40_out, not_74_out, Input_4, not_75_out);
  and and_41 (and_41_out, Input_3, not_76_out, Input_6);
  and and_42 (and_42_out, not_77_out, Input_3, Input_5);
  and and_43 (and_43_out, Input_3, Input_4, not_78_out);
  and and_44 (and_44_out, Input_2, not_79_out, not_80_out, not_81_out);
  and and_45 (and_45_out, Input_2, not_82_out, not_83_out);
  and and_46 (and_46_out, not_84_out, not_85_out, Input_5);
  and and_47 (and_47_out, not_86_out, Input_5, not_87_out);
  and and_48 (and_48_out, not_88_out, not_89_out, Input_4, not_90_out);
  and and_49 (and_49_out, Input_3, not_91_out);
  and and_50 (and_50_out, not_92_out, Input_3, Input_6);
  and and_51 (and_51_out, Input_2, not_93_out, not_94_out, Input_6);
  and and_52 (and_52_out, Input_2, not_95_out, Input_4, Input_5);
  and and_53 (and_53_out, Input_2, Input_3, not_96_out);
  or or_1 (Output_2, and_1_out, and_2_out, and_3_out, and_4_out, and_5_out, and_6_out, and_7_out);
  or or_2 (Output_3, and_8_out, and_9_out, and_10_out, and_11_out, and_12_out, and_13_out, and_14_out, and_15_out);
  or or_3 (Output_4, and_16_out, and_17_out, and_18_out, and_19_out, and_20_out, and_21_out, and_22_out);
  or or_4 (Output_5, and_23_out, and_24_out, and_25_out, and_26_out, and_27_out, and_28_out, and_29_out, and_30_out, and_31_out);
  or or_5 (Output_6, and_32_out, and_33_out, and_34_out, and_35_out, and_36_out, and_37_out);
  or or_6 (Output_7, and_38_out, and_39_out, and_40_out, and_41_out, and_42_out, and_43_out, and_44_out, and_45_out);
  or or_7 (Output_8, and_46_out, and_47_out, and_48_out, and_49_out, and_50_out, and_51_out, and_52_out, and_53_out);

  assign Output_1 = Input_1;
endmodule

module SegLed1_bissong (
  input  [7:0] Input_bus_1,
  output [7:0] Output_bus_1
);

  DecoderToSegLed_bissong DecoderToSegLed_bis_1 (
    .Input_1(Input_bus_1[7]), .Input_2(Input_bus_1[4]), .Input_3(Input_bus_1[3]), .Input_4(Input_bus_1[2]),
    .Input_5(Input_bus_1[1]), .Input_6(Input_bus_1[0]), .Output_1(Output_bus_1[7]),
    .Output_2(Output_bus_1[6]), .Output_3(Output_bus_1[5]), .Output_4(Output_bus_1[4]),
    .Output_5(Output_bus_1[3]), .Output_6(Output_bus_1[2]), .Output_7(Output_bus_1[1]),
    .Output_8(Output_bus_1[0]));
endmodule

module AllsegLeds_bissong (
  input  [7:0] Input_bus_1,
  input  [7:0] Input_bus_2,
  input  [7:0] Input_bus_3,
  input  [7:0] Input_bus_4,
  input  [7:0] Input_bus_5,
  input  [7:0] Input_bus_6,
  output [7:0] Output_bus_1,
  output [7:0] Output_bus_2,
  output [7:0] Output_bus_3,
  output [7:0] Output_bus_4,
  output [7:0] Output_bus_5,
  output [7:0] Output_bus_6
);

  SegLed1_bissong SegLed1_bis_1 (.Input_bus_1(Input_bus_1), .Output_bus_1(Output_bus_1));
  SegLed1_bissong SegLed1_bis_2 (.Input_bus_1(Input_bus_2), .Output_bus_1(Output_bus_2));
  SegLed1_bissong SegLed1_bis_3 (.Input_bus_1(Input_bus_3), .Output_bus_1(Output_bus_3));
  SegLed1_bissong SegLed1_bis_4 (.Input_bus_1(Input_bus_4), .Output_bus_1(Output_bus_4));
  SegLed1_bissong SegLed1_bis_5 (.Input_bus_1(Input_bus_5), .Output_bus_1(Output_bus_5));
  SegLed1_bissong SegLed1_bis_6 (.Input_bus_1(Input_bus_6), .Output_bus_1(Output_bus_6));
endmodule

module clk2k_to_4song (
  input  CLK2k,
  output CLK4
);

  wire d_ff_1_q, d_ff_1_qn, d_ff_2_q, d_ff_2_qn, d_ff_3_q, d_ff_3_qn, d_ff_4_q, d_ff_4_qn, d_ff_5_q,
       d_ff_5_qn, d_ff_6_q, d_ff_6_qn, d_ff_7_q, d_ff_7_qn, d_ff_8_q, d_ff_8_qn, d_ff_9_qn;

  D_Flip_Flop d_ff_1 (.D(d_ff_1_qn), .clk(CLK2k), .Q(d_ff_1_q), .Qn(d_ff_1_qn));  // open: preset, reset
  D_Flip_Flop d_ff_2 (.D(d_ff_2_qn), .clk(d_ff_1_q), .Q(d_ff_2_q), .Qn(d_ff_2_qn));  // open: preset, reset
  D_Flip_Flop d_ff_3 (.D(d_ff_3_qn), .clk(d_ff_2_q), .Q(d_ff_3_q), .Qn(d_ff_3_qn));  // open: preset, reset
  D_Flip_Flop d_ff_4 (.D(d_ff_4_qn), .clk(d_ff_3_q), .Q(d_ff_4_q), .Qn(d_ff_4_qn));  // open: preset, reset
  D_Flip_Flop d_ff_5 (.D(d_ff_5_qn), .clk(d_ff_4_q), .Q(d_ff_5_q), .Qn(d_ff_5_qn));  // open: preset, reset
  D_Flip_Flop d_ff_6 (.D(d_ff_6_qn), .clk(d_ff_5_q), .Q(d_ff_6_q), .Qn(d_ff_6_qn));  // open: preset, reset
  D_Flip_Flop d_ff_7 (.D(d_ff_7_qn), .clk(d_ff_6_q), .Q(d_ff_7_q), .Qn(d_ff_7_qn));  // open: preset, reset
  D_Flip_Flop d_ff_8 (.D(d_ff_8_qn), .clk(d_ff_7_q), .Q(d_ff_8_q), .Qn(d_ff_8_qn));  // open: preset, reset
  D_Flip_Flop d_ff_9 (.D(d_ff_9_qn), .clk(d_ff_8_q), .Q(CLK4), .Qn(d_ff_9_qn));  // open: preset, reset
endmodule
