// Logisim project hourModule.circ as structural Verilog: 35 circuits, main circuit changeTimeZoneOnBoard
module hourFSM (
  input  RESET,
  input  [1:0] B1_B0,
  output [7:0] sevsegCode_5,
  output [7:0] sevsegCode_4,
  output [7:0] sevsegCode_3,
  output [7:0] sevsegCode_2,
  output [7:0] sevsegCode_1,
  output [7:0] sevsegCode_0
);

  wire changeHour_1_hloadtendi, changeHour_1_hloaduendi, changeHour_1_minloadtendi,
       changeHour_1_minloaduendi, changeHour_1_secloadtendi, changeHour_1_secloaduendi, clk32k_to_2k_1_clk2k,
       clock_1_out, HOUR_1_hloadt, HOUR_1_hloadu, HOUR_1_minloadt, HOUR_1_minloadu, HOUR_1_secloadt,
       HOUR_1_secloadu;
  wire [3:0] changeHour_1_hloadt_4, changeHour_1_hloadu_4, changeHour_1_minloadt_4, changeHour_1_minloadu_4,
       changeHour_1_secloadt_4, changeHour_1_secloadu_4, HOUR_1_ht_4, HOUR_1_hu_4, HOUR_1_mint_4,
       HOUR_1_minu_4, HOUR_1_sect_4, HOUR_1_secu_4;

  Clock clock_1 (.out(clock_1_out));
  clk32k_to_2k clk32k_to_2k_1 (.CLK32k(clock_1_out), .CLK2k(clk32k_to_2k_1_clk2k));
  changeHour changeHour_1 (
    .B1_B0(B1_B0), .HloadT_4(changeHour_1_hloadt_4), .HloadTEnDi(changeHour_1_hloadtendi),
    .HloadU_4(changeHour_1_hloadu_4), .HloadUEnDi(changeHour_1_hloaduendi),
    .MINloadT_4(changeHour_1_minloadt_4), .MINloadTEnDi(changeHour_1_minloadtendi),
    .MINloadU_4(changeHour_1_minloadu_4), .MINloadUEnDi(changeHour_1_minloaduendi),
    .SECloadT_4(changeHour_1_secloadt_4), .SECloadTEnDi(changeHour_1_secloadtendi),
    .SECloadU_4(changeHour_1_secloadu_4), .SECloadUEnDi(changeHour_1_secloaduendi));
  HOUR HOUR_1 (
    .RESET(RESET), .CLK2k(clk32k_to_2k_1_clk2k), .HloadT_4(changeHour_1_hloadt_4),
    .HloadTEnDi(changeHour_1_hloadtendi), .HloadU_4(changeHour_1_hloadu_4),
    .HloadUEnDi(changeHour_1_hloaduendi), .MINloadT_4(changeHour_1_minloadt_4),
    .MINloadTEnDi(changeHour_1_minloadtendi), .MINloadU_4(changeHour_1_minloadu_4),
    .MINloadUEnDi(changeHour_1_minloaduendi), .SECloadT_4(changeHour_1_secloadt_4),
    .SECloadTEnDi(changeHour_1_secloadtendi), .SECloadU_4(changeHour_1_secloadu_4),
    .SECloadUEnDi(changeHour_1_secloaduendi), .HT_4(HOUR_1_ht_4), .HU_4(HOUR_1_hu_4), .MINT_4(HOUR_1_mint_4),
    .MINU_4(HOUR_1_minu_4), .SECT_4(HOUR_1_sect_4), .SECU_4(HOUR_1_secu_4), .HloadT(HOUR_1_hloadt),
    .HloadU(HOUR_1_hloadu), .MINloadT(HOUR_1_minloadt), .MINloadU(HOUR_1_minloadu),
    .SECloadT(HOUR_1_secloadt), .SECloadU(HOUR_1_secloadu));
  hourView_HMS hourView_HMS_1 (
    .HT_4(HOUR_1_ht_4), .HU_4(HOUR_1_hu_4), .MINT_4(HOUR_1_mint_4), .MINU_4(HOUR_1_minu_4),
    .SECT_4(HOUR_1_sect_4), .SECU_4(HOUR_1_secu_4), .HloadT(HOUR_1_hloadt), .HloadU(HOUR_1_hloadu),
    .MINloadT(HOUR_1_minloadt), .MINloadU(HOUR_1_minloadu), .SECloadT(HOUR_1_secloadt),
    .SECloadU(HOUR_1_secloadu), .RESET(RESET), .CLK2k(clk32k_to_2k_1_clk2k), .sevsegCode_5(sevsegCode_5),
    .sevsegCode_4(sevsegCode_4), .sevsegCode_3(sevsegCode_3), .sevsegCode_2(sevsegCode_2),
    .sevsegCode_1(sevsegCode_1), .sevsegCode_0(sevsegCode_0));
endmodule

module zeroTwo (
  input  IN1,
  input  IN0,
  input  TickIN,
  output TickOUT,
  output OUT1,
  output OUT0
);

  wire and_2_out, and_3_out, and_4_out, and_5_out, not_1_out, not_2_out, not_3_out, not_4_out, not_5_out,
       not_6_out, not_7_out, not_8_out;

  not not_1 (not_1_out, IN0);
  not not_2 (not_2_out, IN1);
  not not_3 (not_3_out, IN0);
  not not_4 (not_4_out, TickIN);
  not not_5 (not_5_out, IN1);
  not not_6 (not_6_out, IN0);
  not not_7 (not_7_out, IN1);
  not not_8 (not_8_out, TickIN);
  and and_1 (TickOUT, IN1, not_1_out, TickIN);
  and and_2 (and_2_out, not_2_out, IN0, TickIN);
  and and_3 (and_3_out, IN1, not_3_out, not_4_out);
  and and_4 (and_4_out, not_5_out, not_6_out, TickIN);
  and and_5 (and_5_out, not_7_out, IN0, not_8_out);
  or or_1 (OUT1, and_2_out, and_3_out);
  or or_2 (OUT0, and_4_out, and_5_out);
endmodule

module zeroFive (
  input  IN2,
  input  IN1,
  input  IN0,
  input  TickIN,
  output TickOUT,
  output OUT2,
  output OUT1,
  output OUT0
);

  wire and_1_out, and_2_out, and_3_out, and_4_out, and_5_out, and_6_out, and_7_out, nand_1_out, nand_2_out,
       nand_3_out, nand_4_out, nand_5_out, nand_6_out, nand_7_out, nand_8_out, nand_9_out, nand_10_out,
       nand_11_out, nand_12_out, not_1_out, not_2_out, not_3_out, not_4_out, not_5_out, not_6_out, not_7_out,
       not_8_out, not_9_out, not_10_out, not_11_out, not_12_out, not_13_out, not_14_out;

  not not_1 (not_1_out, IN2);
  not not_2 (not_2_out, IN1);
  not not_3 (not_3_out, IN2);
  not not_4 (not_4_out, IN0);
  not not_5 (not_5_out, IN2);
  not not_6 (not_6_out, TickIN);
  not not_7 (not_7_out, IN2);
  not not_8 (not_8_out, IN0);
  not not_9 (not_9_out, IN1);
  not not_10 (not_10_out, IN0);
  not not_11 (not_11_out, IN2);
  not not_12 (not_12_out, TickIN);
  not not_13 (not_13_out, IN1);
  not not_14 (not_14_out, TickIN);
  nand nand_1 (nand_1_out, IN1, IN1);
  nand nand_2 (nand_2_out, IN1, IN1);
  nand nand_3 (nand_3_out, IN2, IN2);
  nand nand_4 (nand_4_out, IN1, IN1);
  nand nand_5 (nand_5_out, IN0, IN0);
  nand nand_6 (nand_6_out, IN1, IN1);
  nand nand_7 (nand_7_out, TickIN, TickIN);
  and and_1 (and_1_out, not_1_out, not_2_out, IN0, TickIN);
  and and_2 (and_2_out, not_3_out, IN1, not_4_out);
  and and_3 (and_3_out, not_5_out, IN1, not_6_out);
  and and_4 (and_4_out, not_7_out, not_8_out, TickIN);
  and and_5 (and_5_out, not_9_out, not_10_out, TickIN);
  and and_6 (and_6_out, not_11_out, IN0, not_12_out);
  and and_7 (and_7_out, not_13_out, IN0, not_14_out);
  nand nand_8 (nand_8_out, TickIN, IN2, nand_1_out, IN0);
  nand nand_9 (nand_9_out, TickIN, IN2, nand_2_out, IN0);
  nand nand_10 (nand_10_out, nand_3_out, IN1, IN0, TickIN);
  nand nand_11 (nand_11_out, IN2, nand_4_out, nand_5_out);
  nand nand_12 (nand_12_out, IN2, nand_6_out, nand_7_out);
  or or_1 (OUT1, and_1_out, and_2_out, and_3_out);
  or or_2 (OUT0, and_4_out, and_5_out, and_6_out, and_7_out);
  nand nand_13 (TickOUT, nand_8_out, nand_9_out);
  nand nand_14 (OUT2, nand_10_out, nand_11_out, nand_12_out);
endmodule

module zeroNine (
  input  IN3,
  input  IN2,
  input  IN1,
  input  IN0,
  input  TickIN,
  output TickOUT,
  output OUT3,
  output OUT2,
  output OUT1,
  output OUT0
);

  wire nand_1_out, nand_2_out, nand_3_out, nand_4_out, nand_5_out, nand_6_out, nand_7_out, nand_8_out,
       nand_9_out, nand_10_out, nand_11_out, nand_12_out, nand_13_out, nand_14_out, nand_15_out, nand_16_out,
       nand_17_out, nand_18_out, nand_19_out, nand_20_out, nand_21_out, nand_22_out, nand_23_out,
       nand_24_out, nand_25_out, nand_26_out, nand_27_out, nand_28_out, nand_29_out, nand_30_out,
       nand_31_out, nand_32_out, nand_33_out, nand_34_out, nand_35_out, nand_36_out, nand_37_out,
       nand_38_out, nand_39_out, nand_40_out, nand_41_out, nand_42_out, nand_43_out, nand_44_out,
       nand_45_out, nand_46_out, nand_47_out, nand_48_out, nand_49_out, nand_50_out, nand_51_out;

  nand nand_1 (nand_1_out, IN2, IN2);
  nand nand_2 (nand_2_out, IN1, IN1);
  nand nand_3 (nand_3_out, IN2, IN2);
  nand nand_4 (nand_4_out, IN1, IN1);
  nand nand_5 (nand_5_out, TickIN, TickIN);
  nand nand_6 (nand_6_out, IN2, IN2);
  nand nand_7 (nand_7_out, IN1, IN1);
  nand nand_8 (nand_8_out, IN2, IN2);
  nand nand_9 (nand_9_out, IN1, IN1);
  nand nand_10 (nand_10_out, IN0, IN0);
  nand nand_11 (nand_11_out, IN3, IN3);
  nand nand_12 (nand_12_out, IN3, IN3);
  nand nand_13 (nand_13_out, IN2, IN2);
  nand nand_14 (nand_14_out, IN3, IN3);
  nand nand_15 (nand_15_out, IN1, IN1);
  nand nand_16 (nand_16_out, IN3, IN3);
  nand nand_17 (nand_17_out, IN0, IN0);
  nand nand_18 (nand_18_out, IN3, IN3);
  nand nand_19 (nand_19_out, TickIN, TickIN);
  nand nand_20 (nand_20_out, IN3, IN3);
  nand nand_21 (nand_21_out, IN1, IN1);
  nand nand_22 (nand_22_out, IN3, IN3);
  nand nand_23 (nand_23_out, IN0, IN0);
  nand nand_24 (nand_24_out, IN3, IN3);
  nand nand_25 (nand_25_out, TickIN, TickIN);
  nand nand_26 (nand_26_out, IN3, IN3);
  nand nand_27 (nand_27_out, IN0, IN0);
  nand nand_28 (nand_28_out, IN2, IN2);
  nand nand_29 (nand_29_out, IN1, IN1);
  nand nand_30 (nand_30_out, IN0, IN0);
  nand nand_31 (nand_31_out, IN3, IN3);
  nand nand_32 (nand_32_out, TickIN, TickIN);
  nand nand_33 (nand_33_out, IN2, IN2);
  nand nand_34 (nand_34_out, IN1, IN1);
  nand nand_35 (nand_35_out, TickIN, TickIN);
  nand nand_36 (nand_36_out, IN3, nand_1_out, nand_2_out, IN0, TickIN);
  nand nand_37 (nand_37_out, IN3, nand_3_out, nand_4_out, IN0, TickIN);
  nand nand_38 (nand_38_out, nand_5_out, IN3, nand_6_out, nand_7_out);
  nand nand_39 (nand_39_out, IN3, nand_8_out, nand_9_out, nand_10_out);
  nand nand_40 (nand_40_out, TickIN, nand_11_out, IN2, IN1, IN0);
  nand nand_41 (nand_41_out, nand_12_out, nand_13_out, IN1, IN0, TickIN);
  nand nand_42 (nand_42_out, nand_14_out, IN2, nand_15_out);
  nand nand_43 (nand_43_out, nand_16_out, IN2, nand_17_out);
  nand nand_44 (nand_44_out, nand_18_out, IN2, nand_19_out);
  nand nand_45 (nand_45_out, nand_20_out, nand_21_out, IN0, TickIN);
  nand nand_46 (nand_46_out, nand_22_out, IN1, nand_23_out);
  nand nand_47 (nand_47_out, nand_24_out, IN1, nand_25_out);
  nand nand_48 (nand_48_out, nand_26_out, nand_27_out, TickIN);
  nand nand_49 (nand_49_out, nand_28_out, nand_29_out, nand_30_out, TickIN);
  nand nand_50 (nand_50_out, nand_31_out, IN0, nand_32_out);
  nand nand_51 (nand_51_out, nand_33_out, nand_34_out, IN0, nand_35_out);
  nand nand_52 (TickOUT, nand_36_out, nand_37_out);
  nand nand_53 (OUT3, nand_38_out, nand_39_out, nand_40_out);
  nand nand_54 (OUT2, nand_41_out, nand_42_out, nand_43_out, nand_44_out);
  nand nand_55 (OUT1, nand_45_out, nand_46_out, nand_47_out);
  nand nand_56 (OUT0, nand_48_out, nand_49_out, nand_50_out, nand_51_out);
endmodule

module zeroNineHour (
  input  H,
  input  IN3,
  input  IN2,
  input  IN1,
  input  IN0,
  input  TickIN,
  output TickOUT,
  output OUT3,
  output OUT2,
  output OUT1,
  output OUT0
);

  wire and_1_out, and_2_out, and_3_out, and_4_out, and_5_out, and_6_out, and_7_out, and_8_out, and_9_out,
       and_10_out, and_11_out, and_12_out, and_13_out, and_14_out, and_15_out, and_16_out, and_17_out,
       and_18_out, and_19_out, and_20_out, and_21_out, not_1_out, not_2_out, not_3_out, not_4_out, not_5_out,
       not_6_out, not_7_out, not_8_out, not_9_out, not_10_out, not_11_out, not_12_out, not_13_out,
       not_14_out, not_15_out, not_16_out, not_17_out, not_18_out, not_19_out, not_20_out, not_21_out,
       not_22_out, not_23_out, not_24_out, not_25_out, not_26_out, not_27_out, not_28_out, not_29_out,
       not_30_out, not_31_out, not_32_out, not_33_out, not_34_out, not_35_out, not_36_out, not_37_out,
       not_38_out, not_39_out, not_40_out, not_41_out, not_42_out, not_43_out, not_44_out;

  not not_1 (not_1_out, H);
  not not_2 (not_2_out, IN3);
  not not_3 (not_3_out, IN2);
  not not_4 (not_4_out, H);
  not not_5 (not_5_out, H);
  not not_6 (not_6_out, IN0);
  not not_7 (not_7_out, H);
  not not_8 (not_8_out, TickIN);
  not not_9 (not_9_out, H);
  not not_10 (not_10_out, IN2);
  not not_11 (not_11_out, H);
  not not_12 (not_12_out, IN1);
  not not_13 (not_13_out, H);
  not not_14 (not_14_out, IN0);
  not not_15 (not_15_out, H);
  not not_16 (not_16_out, TickIN);
  not not_17 (not_17_out, H);
  not not_18 (not_18_out, IN3);
  not not_19 (not_19_out, IN1);
  not not_20 (not_20_out, IN3);
  not not_21 (not_21_out, IN2);
  not not_22 (not_22_out, IN1);
  not not_23 (not_23_out, H);
  not not_24 (not_24_out, IN0);
  not not_25 (not_25_out, H);
  not not_26 (not_26_out, TickIN);
  not not_27 (not_27_out, IN3);
  not not_28 (not_28_out, IN2);
  not not_29 (not_29_out, IN0);
  not not_30 (not_30_out, IN3);
  not not_31 (not_31_out, IN2);
  not not_32 (not_32_out, TickIN);
  not not_33 (not_33_out, H);
  not not_34 (not_34_out, H);
  not not_35 (not_35_out, IN0);
  not not_36 (not_36_out, IN3);
  not not_37 (not_37_out, IN2);
  not not_38 (not_38_out, IN0);
  not not_39 (not_39_out, H);
  not not_40 (not_40_out, TickIN);
  not not_41 (not_41_out, IN3);
  not not_42 (not_42_out, IN2);
  not not_43 (not_43_out, TickIN);
  not not_44 (not_44_out, H);
  and and_1 (and_1_out, not_1_out, IN3, IN0, TickIN);
  and and_2 (and_2_out, H, not_2_out, not_3_out, IN1, IN0, TickIN);
  and and_3 (and_3_out, not_4_out, IN2, IN1, IN0, TickIN);
  and and_4 (and_4_out, not_5_out, IN3, not_6_out);
  and and_5 (and_5_out, not_7_out, IN3, not_8_out);
  and and_6 (and_6_out, not_9_out, not_10_out, IN1, IN0, TickIN);
  and and_7 (and_7_out, not_11_out, IN2, not_12_out);
  and and_8 (and_8_out, not_13_out, IN2, not_14_out);
  and and_9 (and_9_out, not_15_out, IN2, not_16_out);
  and and_10 (and_10_out, not_17_out, not_18_out, not_19_out, IN0, TickIN);
  and and_11 (and_11_out, not_20_out, not_21_out, not_22_out, IN0, TickIN);
  and and_12 (and_12_out, not_23_out, IN1, not_24_out);
  and and_13 (and_13_out, not_25_out, IN1, not_26_out);
  and and_14 (and_14_out, not_27_out, not_28_out, IN1, not_29_out);
  and and_15 (and_15_out, not_30_out, not_31_out, IN1, not_32_out);
  and and_16 (and_16_out, not_33_out, IN3, IN2);
  and and_17 (and_17_out, not_34_out, not_35_out, TickIN);
  and and_18 (and_18_out, not_36_out, not_37_out, not_38_out, TickIN);
  and and_19 (and_19_out, not_39_out, IN0, not_40_out);
  and and_20 (and_20_out, not_41_out, not_42_out, IN0, not_43_out);
  and and_21 (and_21_out, not_44_out, IN3, IN2);
  or or_1 (TickOUT, and_1_out, and_2_out);
  or or_2 (OUT3, and_3_out, and_4_out, and_5_out);
  or or_3 (OUT2, and_6_out, and_7_out, and_8_out, and_9_out);
  or or_4 (OUT1, and_10_out, and_11_out, and_12_out, and_13_out, and_14_out, and_15_out, and_16_out);
  or or_5 (OUT0, and_17_out, and_18_out, and_19_out, and_20_out, and_21_out);
endmodule

module zeroTwentythree (
  input  TickIN,
  input  [3:0] loadT_4,
  input  loadTEnDi,
  input  [3:0] loadU_4,
  input  loadUEnDi,
  input  CLK2k,
  input  RESET,
  output TickOUT,
  output [3:0] curT_4,
  output [3:0] curU_4
);

  wire and_1_out, and_2_out, and_3_out, and_4_out, and_5_out, and_6_out, and_7_out, load_2_1_out0,
       load_2_1_out1, load_4_1_out0, load_4_1_out1, load_4_1_out2, load_4_1_out3, zeroNineH_1_out0,
       zeroNineH_1_out1, zeroNineH_1_out2, zeroNineH_1_out3, zeroNineH_1_tickout, zeroTwo_1_out0,
       zeroTwo_1_out1;
  wire [1:0] d_ff_2_q;

  and and_1 (and_1_out, d_ff_2_q[1], ~d_ff_2_q[0]);  // AND_Gate
  zeroTwo zeroTwo_1 (
    .IN1(d_ff_2_q[1]), .IN0(d_ff_2_q[0]), .TickIN(zeroNineH_1_tickout), .TickOUT(TickOUT),
    .OUT1(zeroTwo_1_out1), .OUT0(zeroTwo_1_out0));
  zeroNineHour zeroNineH_1 (
    .H(and_1_out), .IN3(curU_4[3]), .IN2(curU_4[2]), .IN1(curU_4[1]), .IN0(curU_4[0]), .TickIN(TickIN),
    .TickOUT(zeroNineH_1_tickout), .OUT3(zeroNineH_1_out3), .OUT2(zeroNineH_1_out2), .OUT1(zeroNineH_1_out1),
    .OUT0(zeroNineH_1_out0));
  load_2 load_2_1 (
    .IN1(zeroTwo_1_out1), .IN0(zeroTwo_1_out0), .loadValue(loadT_4), .loadEnDi(loadTEnDi),
    .OUT1(load_2_1_out1), .OUT0(load_2_1_out0));
  load_4 load_4_1 (
    .IN3(zeroNineH_1_out3), .IN2(zeroNineH_1_out2), .IN1(zeroNineH_1_out1), .IN0(zeroNineH_1_out0),
    .loadValue(loadU_4), .loadEnDi(loadUEnDi), .OUT3(load_4_1_out3), .OUT2(load_4_1_out2),
    .OUT1(load_4_1_out1), .OUT0(load_4_1_out0));
  and and_2 (and_2_out, ~RESET, load_2_1_out1);  // AND_Gate
  and and_3 (and_3_out, ~RESET, load_2_1_out0);  // AND_Gate
  and and_4 (and_4_out, ~RESET, load_4_1_out3);  // AND_Gate
  and and_5 (and_5_out, ~RESET, load_4_1_out2);  // AND_Gate
  and and_6 (and_6_out, ~RESET, load_4_1_out1);  // AND_Gate
  and and_7 (and_7_out, ~RESET, load_4_1_out0);  // AND_Gate
  D_Flip_Flop d_ff_1 (.D(and_2_out), .clk(CLK2k), .Q(d_ff_2_q[1]), .reset(RESET));  // open: Qn, preset
  D_Flip_Flop d_ff_2 (.D(and_3_out), .clk(CLK2k), .Q(d_ff_2_q[0]), .reset(RESET));  // open: Qn, preset
  D_Flip_Flop d_ff_3 (.D(and_4_out), .clk(CLK2k), .Q(curU_4[3]), .reset(RESET));  // open: Qn, preset
  D_Flip_Flop d_ff_4 (.D(and_5_out), .clk(CLK2k), .Q(curU_4[2]), .reset(RESET));  // open: Qn, preset
  D_Flip_Flop d_ff_5 (.D(and_6_out), .clk(CLK2k), .Q(curU_4[1]), .reset(RESET));  // open: Qn, preset
  D_Flip_Flop d_ff_6 (.D(and_7_out), .clk(CLK2k), .Q(curU_4[0]), .reset(RESET));  // open: Qn, preset
  assign curT_4 = {{2{1'b0}}, d_ff_2_q};  // Bit_Extender bit_extender_1
endmodule

module zeroFiftynine (
  input  TickIN,
  input  [3:0] loadT_4,
  input  loadTEnDi,
  input  [3:0] loadU_4,
  input  loadUEnDi,
  input  CLK2k,
  input  RESET,
  output TickOUT,
  output [3:0] curT_4,
  output [3:0] curU_4
);

  wire and_1_out, and_2_out, and_3_out, and_4_out, and_5_out, and_6_out, and_7_out, load_3_1_out0,
       load_3_1_out1, load_3_1_out2, load_4_1_out0, load_4_1_out1, load_4_1_out2, load_4_1_out3,
       zeroFive_1_out0, zeroFive_1_out1, zeroFive_1_out2, zeroNine_1_out0, zeroNine_1_out1, zeroNine_1_out2,
       zeroNine_1_out3, zeroNine_1_tickout;
  wire [2:0] d_ff_3_q;

  zeroFive zeroFive_1 (
    .IN2(d_ff_3_q[2]), .IN1(d_ff_3_q[1]), .IN0(d_ff_3_q[0]), .TickIN(zeroNine_1_tickout), .TickOUT(TickOUT),
    .OUT2(zeroFive_1_out2), .OUT1(zeroFive_1_out1), .OUT0(zeroFive_1_out0));
  zeroNine zeroNine_1 (
    .IN3(curU_4[3]), .IN2(curU_4[2]), .IN1(curU_4[1]), .IN0(curU_4[0]), .TickIN(TickIN),
    .TickOUT(zeroNine_1_tickout), .OUT3(zeroNine_1_out3), .OUT2(zeroNine_1_out2), .OUT1(zeroNine_1_out1),
    .OUT0(zeroNine_1_out0));
  load_3 load_3_1 (
    .IN2(zeroFive_1_out2), .IN1(zeroFive_1_out1), .IN0(zeroFive_1_out0), .loadValue(loadT_4),
    .loadEnDi(loadTEnDi), .OUT2(load_3_1_out2), .OUT1(load_3_1_out1), .OUT0(load_3_1_out0));
  load_4 load_4_1 (
    .IN3(zeroNine_1_out3), .IN2(zeroNine_1_out2), .IN1(zeroNine_1_out1), .IN0(zeroNine_1_out0),
    .loadValue(loadU_4), .loadEnDi(loadUEnDi), .OUT3(load_4_1_out3), .OUT2(load_4_1_out2),
    .OUT1(load_4_1_out1), .OUT0(load_4_1_out0));
  and and_1 (and_1_out, ~RESET, load_3_1_out2);  // AND_Gate
  and and_2 (and_2_out, ~RESET, load_3_1_out1);  // AND_Gate
  and and_3 (and_3_out, ~RESET, load_3_1_out0);  // AND_Gate
  and and_4 (and_4_out, ~RESET, load_4_1_out3);  // AND_Gate
  and and_5 (and_5_out, ~RESET, load_4_1_out2);  // AND_Gate
  and and_6 (and_6_out, ~RESET, load_4_1_out1);  // AND_Gate
  and and_7 (and_7_out, ~RESET, load_4_1_out0);  // AND_Gate
  D_Flip_Flop d_ff_1 (.D(and_1_out), .clk(CLK2k), .Q(d_ff_3_q[2]), .reset(RESET));  // open: Qn, preset
  D_Flip_Flop d_ff_2 (.D(and_2_out), .clk(CLK2k), .Q(d_ff_3_q[1]), .reset(RESET));  // open: Qn, preset
  D_Flip_Flop d_ff_3 (.D(and_3_out), .clk(CLK2k), .Q(d_ff_3_q[0]), .reset(RESET));  // open: Qn, preset
  D_Flip_Flop d_ff_4 (.D(and_4_out), .clk(CLK2k), .Q(curU_4[3]), .reset(RESET));  // open: Qn, preset
  D_Flip_Flop d_ff_5 (.D(and_5_out), .clk(CLK2k), .Q(curU_4[2]), .reset(RESET));  // open: Qn, preset
  D_Flip_Flop d_ff_6 (.D(and_6_out), .clk(CLK2k), .Q(curU_4[1]), .reset(RESET));  // open: Qn, preset
  D_Flip_Flop d_ff_7 (.D(and_7_out), .clk(CLK2k), .Q(curU_4[0]), .reset(RESET));  // open: Qn, preset
  assign curT_4 = {{1{1'b0}}, d_ff_3_q};  // Bit_Extender bit_extender_1
endmodule

module clk32k_to_2k (
  input  CLK32k,
  output CLK2k
);

  wire d_ff_1_q, d_ff_1_qn, d_ff_2_q, d_ff_2_qn, d_ff_3_q, d_ff_3_qn, d_ff_4_qn;

  D_Flip_Flop d_ff_1 (.D(d_ff_1_qn), .clk(CLK32k), .Q(d_ff_1_q), .Qn(d_ff_1_qn));  // open: preset, reset
  D_Flip_Flop d_ff_2 (.D(d_ff_2_qn), .clk(d_ff_1_q), .Q(d_ff_2_q), .Qn(d_ff_2_qn));  // open: preset, reset
  D_Flip_Flop d_ff_3 (.D(d_ff_3_qn), .clk(d_ff_2_q), .Q(d_ff_3_q), .Qn(d_ff_3_qn));  // open: preset, reset
  D_Flip_Flop d_ff_4 (.D(d_ff_4_qn), .clk(d_ff_3_q), .Q(CLK2k), .Qn(d_ff_4_qn));  // open: preset, reset
endmodule

module clk2k_to_ticksec (
  input  RESET,
  input  CLK2k,
  output TickSEC
);

  Counter #(.width(10), .max('h3e9)) counter_1 (
    .clr(RESET), .clk(CLK2k), .carry(TickSEC));  // open: load, up, count, D, Q
endmodule

module HOUR (
  input  RESET,
  input  CLK2k,
  input  [3:0] HloadT_4,
  input  HloadTEnDi,
  input  [3:0] HloadU_4,
  input  HloadUEnDi,
  input  [3:0] MINloadT_4,
  input  MINloadTEnDi,
  input  [3:0] MINloadU_4,
  input  MINloadUEnDi,
  input  [3:0] SECloadT_4,
  input  SECloadTEnDi,
  input  [3:0] SECloadU_4,
  input  SECloadUEnDi,
  output [3:0] HT_4,
  output [3:0] HU_4,
  output [3:0] MINT_4,
  output [3:0] MINU_4,
  output [3:0] SECT_4,
  output [3:0] SECU_4,
  output HloadT,
  output HloadU,
  output MINloadT,
  output MINloadU,
  output SECloadT,
  output SECloadU
);

  wire clk2k_to_ticksec_1_ticksec, min_tickout, sec_tickout;

  clk2k_to_ticksec clk2k_to_ticksec_1 (.RESET(RESET), .CLK2k(CLK2k), .TickSEC(clk2k_to_ticksec_1_ticksec));
  zeroTwentythree hour_1 (
    .TickIN(min_tickout), .loadT_4(HloadT_4), .loadTEnDi(HloadTEnDi), .loadU_4(HloadU_4),
    .loadUEnDi(HloadUEnDi), .CLK2k(CLK2k), .RESET(RESET), .curT_4(HT_4), .curU_4(HU_4));  // open: TickOUT
  zeroFiftynine min (
    .TickIN(sec_tickout), .loadT_4(MINloadT_4), .loadTEnDi(MINloadTEnDi), .loadU_4(MINloadU_4),
    .loadUEnDi(MINloadUEnDi), .CLK2k(CLK2k), .RESET(RESET), .TickOUT(min_tickout), .curT_4(MINT_4),
    .curU_4(MINU_4));
  zeroFiftynine sec (
    .TickIN(clk2k_to_ticksec_1_ticksec), .loadT_4(SECloadT_4), .loadTEnDi(SECloadTEnDi),
    .loadU_4(SECloadU_4), .loadUEnDi(SECloadUEnDi), .CLK2k(CLK2k), .RESET(RESET), .TickOUT(sec_tickout),
    .curT_4(SECT_4), .curU_4(SECU_4));

  assign HloadT = HloadTEnDi;
  assign HloadU = HloadUEnDi;
  assign MINloadT = MINloadTEnDi;
  assign MINloadU = MINloadUEnDi;
  assign SECloadT = SECloadTEnDi;
  assign SECloadU = SECloadUEnDi;
endmodule

module hourOnBoard_HM (
);

  wire clk_clk2k, clock_1_out, DipSwitch_1_sw1, DipSwitch_1_sw10;
  wire [3:0] hour_1_ht_4, hour_1_hu_4, hour_1_mint_4, hour_1_minu_4;
  wire [7:0] hourView_bis_1_sevsegcode_0, hourView_bis_1_sevsegcode_1, hourView_bis_1_sevsegcode_2,
       hourView_bis_1_sevsegcode_3, hourView_bis_1_sevsegcode_4, hourView_bis_1_sevsegcode_5;

  Clock clock_1 (.out(clock_1_out));
  DipSwitch #(.number(10)) DipSwitch_1 (
    .sw1(DipSwitch_1_sw1), .sw10(DipSwitch_1_sw10));  // open: sw2, sw3, sw4, sw5, sw6, sw7, sw8, sw9
  clk32k_to_2k clk (.CLK32k(clock_1_out), .CLK2k(clk_clk2k));
  HOUR hour_1 (
    .RESET(DipSwitch_1_sw1), .CLK2k(clk_clk2k), .HloadT_4(4'b0001), .HloadTEnDi(DipSwitch_1_sw10),
    .HloadU_4(4'b0111), .HloadUEnDi(DipSwitch_1_sw10), .MINloadT_4(4'b0101), .MINloadTEnDi(DipSwitch_1_sw10),
    .MINloadU_4(4'b0110), .MINloadUEnDi(DipSwitch_1_sw10), .SECloadT_4(4'b0000),
    .SECloadTEnDi(DipSwitch_1_sw10), .SECloadU_4(4'b0000), .SECloadUEnDi(DipSwitch_1_sw10),
    .HT_4(hour_1_ht_4), .HU_4(hour_1_hu_4), .MINT_4(hour_1_mint_4), .MINU_4(hour_1_minu_4));  // open: SECT_4, SECU_4, HloadT, HloadU, MINloadT, MINloadU, SECloadT, SECloadU
  hourView_HM hourView_bis_1 (
    .HT_4(hour_1_ht_4), .HU_4(hour_1_hu_4), .MINT_4(hour_1_mint_4), .MINU_4(hour_1_minu_4),
    .sevsegCode_5(hourView_bis_1_sevsegcode_5), .sevsegCode_4(hourView_bis_1_sevsegcode_4),
    .sevsegCode_3(hourView_bis_1_sevsegcode_3), .sevsegCode_2(hourView_bis_1_sevsegcode_2),
    .sevsegCode_1(hourView_bis_1_sevsegcode_1), .sevsegCode_0(hourView_bis_1_sevsegcode_0));
endmodule

module hourOnBoard_HMS (
);

  wire changeHour_1_hloadtendi, changeHour_1_hloaduendi, changeHour_1_minloadtendi,
       changeHour_1_minloaduendi, changeHour_1_secloadtendi, changeHour_1_secloaduendi, clk32k_to_2k_1_clk2k,
       clock_1_out, DipSwitch_1_sw1;
  wire [1:0] Button_0_out;
  wire [3:0] changeHour_1_hloadt_4, changeHour_1_hloadu_4, changeHour_1_minloadt_4, changeHour_1_minloadu_4,
       changeHour_1_secloadt_4, changeHour_1_secloadu_4, HOUR_1_ht_4, HOUR_1_hu_4, HOUR_1_mint_4,
       HOUR_1_minu_4, HOUR_1_sect_4, HOUR_1_secu_4;
  wire [7:0] hourViewHMS_1_sevsegcode_0, hourViewHMS_1_sevsegcode_1, hourViewHMS_1_sevsegcode_2,
       hourViewHMS_1_sevsegcode_3, hourViewHMS_1_sevsegcode_4, hourViewHMS_1_sevsegcode_5;

  Clock clock_1 (.out(clock_1_out));
  Button Button_1 (.out(Button_0_out[1]));
  Button Button_0 (.out(Button_0_out[0]));
  DipSwitch #(.number(10)) DipSwitch_1 (.sw1(DipSwitch_1_sw1));  // open: sw2, sw3, sw4, sw5, sw6, sw7, sw8, sw9, sw10
  clk32k_to_2k clk32k_to_2k_1 (.CLK32k(clock_1_out), .CLK2k(clk32k_to_2k_1_clk2k));
  changeHour changeHour_1 (
    .B1_B0(Button_0_out), .HloadT_4(changeHour_1_hloadt_4), .HloadTEnDi(changeHour_1_hloadtendi),
    .HloadU_4(changeHour_1_hloadu_4), .HloadUEnDi(changeHour_1_hloaduendi),
    .MINloadT_4(changeHour_1_minloadt_4), .MINloadTEnDi(changeHour_1_minloadtendi),
    .MINloadU_4(changeHour_1_minloadu_4), .MINloadUEnDi(changeHour_1_minloaduendi),
    .SECloadT_4(changeHour_1_secloadt_4), .SECloadTEnDi(changeHour_1_secloadtendi),
    .SECloadU_4(changeHour_1_secloadu_4), .SECloadUEnDi(changeHour_1_secloaduendi));
  HOUR HOUR_1 (
    .RESET(DipSwitch_1_sw1), .CLK2k(clk32k_to_2k_1_clk2k), .HloadT_4(changeHour_1_hloadt_4),
    .HloadTEnDi(changeHour_1_hloadtendi), .HloadU_4(changeHour_1_hloadu_4),
    .HloadUEnDi(changeHour_1_hloaduendi), .MINloadT_4(changeHour_1_minloadt_4),
    .MINloadTEnDi(changeHour_1_minloadtendi), .MINloadU_4(changeHour_1_minloadu_4),
    .MINloadUEnDi(changeHour_1_minloaduendi), .SECloadT_4(changeHour_1_secloadt_4),
    .SECloadTEnDi(changeHour_1_secloadtendi), .SECloadU_4(changeHour_1_secloadu_4),
    .SECloadUEnDi(changeHour_1_secloaduendi), .HT_4(HOUR_1_ht_4), .HU_4(HOUR_1_hu_4), .MINT_4(HOUR_1_mint_4),
    .MINU_4(HOUR_1_minu_4), .SECT_4(HOUR_1_sect_4), .SECU_4(HOUR_1_secu_4));  // open: HloadT, HloadU, MINloadT, MINloadU, SECloadT, SECloadU
  hourView_HMS hourViewHMS_1 (
    .HT_4(HOUR_1_ht_4), .HU_4(HOUR_1_hu_4), .MINT_4(HOUR_1_mint_4), .MINU_4(HOUR_1_minu_4),
    .SECT_4(HOUR_1_sect_4), .SECU_4(HOUR_1_secu_4), .sevsegCode_5(hourViewHMS_1_sevsegcode_5),
    .sevsegCode_4(hourViewHMS_1_sevsegcode_4), .sevsegCode_3(hourViewHMS_1_sevsegcode_3),
    .sevsegCode_2(hourViewHMS_1_sevsegcode_2), .sevsegCode_1(hourViewHMS_1_sevsegcode_1),
    .sevsegCode_0(hourViewHMS_1_sevsegcode_0));  // open: HloadT, HloadU, MINloadT, MINloadU, SECloadT, SECloadU, RESET, CLK2k
endmodule

module hourView_HM (
  input  [3:0] HT_4,
  input  [3:0] HU_4,
  input  [3:0] MINT_4,
  input  [3:0] MINU_4,
  output [7:0] sevsegCode_5,
  output [7:0] sevsegCode_4,
  output [7:0] sevsegCode_3,
  output [7:0] sevsegCode_2,
  output [7:0] sevsegCode_1,
  output [7:0] sevsegCode_0
);

  wire [6:0] bit_extender_2_out;

  assign sevsegCode_4 = {{4{1'b0}}, HT_4};  // Bit_Extender bit_extender_1
  assign bit_extender_2_out = {{3{1'b0}}, HU_4};  // Bit_Extender bit_extender_2
  assign sevsegCode_2 = {{4{1'b0}}, MINT_4};  // Bit_Extender bit_extender_3
  assign sevsegCode_1 = {{4{1'b0}}, MINU_4};  // Bit_Extender bit_extender_4
  assign sevsegCode_3 = {{1{1'b1}}, bit_extender_2_out};  // Bit_Extender bit_extender_5

  assign sevsegCode_0 = 8'h1f;
  assign sevsegCode_5 = 8'h1f;
endmodule

module hourView_HMS (
  input  [3:0] HT_4,
  input  [3:0] HU_4,
  input  [3:0] MINT_4,
  input  [3:0] MINU_4,
  input  [3:0] SECT_4,
  input  [3:0] SECU_4,
  input  HloadT,
  input  HloadU,
  input  MINloadT,
  input  MINloadU,
  input  SECloadT,
  input  SECloadU,
  input  RESET,
  input  CLK2k,
  output [7:0] sevsegCode_5,
  output [7:0] sevsegCode_4,
  output [7:0] sevsegCode_3,
  output [7:0] sevsegCode_2,
  output [7:0] sevsegCode_1,
  output [7:0] sevsegCode_0
);

  wire and_1_out, and_2_out, and_3_out, and_4_out, and_5_out, and_6_out, clk2k_to_4_1_clk4, or_1_out,
       t_ff_1_q;
  wire [6:0] bit_extender_2_out, bit_extender_4_out, multiplexer_2_out, multiplexer_4_out;
  wire [7:0] bit_extender_1_out, bit_extender_3_out, bit_extender_5_out, bit_extender_6_out;

  assign bit_extender_1_out = {{4{1'b0}}, HT_4};  // Bit_Extender bit_extender_1
  assign bit_extender_2_out = {{3{1'b0}}, HU_4};  // Bit_Extender bit_extender_2
  assign bit_extender_3_out = {{4{1'b0}}, MINT_4};  // Bit_Extender bit_extender_3
  assign bit_extender_4_out = {{3{1'b0}}, MINU_4};  // Bit_Extender bit_extender_4
  assign bit_extender_5_out = {{4{1'b0}}, SECT_4};  // Bit_Extender bit_extender_5
  assign bit_extender_6_out = {{4{1'b0}}, SECU_4};  // Bit_Extender bit_extender_6
  clk2k_to_4 clk2k_to_4_1 (.CLK2k(CLK2k), .CLK4(clk2k_to_4_1_clk4));
  T_Flip_Flop t_ff_1 (.T(or_1_out), .clk(clk2k_to_4_1_clk4), .Q(t_ff_1_q), .reset(RESET));  // open: Qn, preset
  or or_1 (or_1_out, HloadT, HloadU, MINloadT, MINloadU, SECloadT, SECloadU);
  Multiplexer #(.width(8), .enable("false")) multiplexer_1 (
    .in0(bit_extender_1_out), .in1(8'h7f), .out(sevsegCode_5), .sel(and_1_out));
  and and_1 (and_1_out, HloadT, t_ff_1_q);
  and and_2 (and_2_out, HloadU, t_ff_1_q);
  Multiplexer #(.width(7), .enable("false")) multiplexer_2 (
    .in0(bit_extender_2_out), .in1({7{1'b1}}), .out(multiplexer_2_out), .sel(and_2_out));
  Multiplexer #(.width(8), .enable("false")) multiplexer_3 (
    .in0(bit_extender_3_out), .in1(8'h7f), .out(sevsegCode_3), .sel(and_3_out));
  and and_3 (and_3_out, MINloadT, t_ff_1_q);
  Multiplexer #(.width(7), .enable("false")) multiplexer_4 (
    .in0(bit_extender_4_out), .in1({7{1'b1}}), .out(multiplexer_4_out), .sel(and_4_out));
  and and_4 (and_4_out, MINloadU, t_ff_1_q);
  assign sevsegCode_4 = {{1{1'b1}}, multiplexer_2_out};  // Bit_Extender bit_extender_7
  assign sevsegCode_2 = {{1{1'b1}}, multiplexer_4_out};  // Bit_Extender bit_extender_8
  Multiplexer #(.width(8), .enable("false")) multiplexer_5 (
    .in0(bit_extender_5_out), .in1(8'h7f), .out(sevsegCode_1), .sel(and_5_out));
  and and_5 (and_5_out, SECloadT, t_ff_1_q);
  Multiplexer #(.width(8), .enable("false")) multiplexer_6 (
    .in0(bit_extender_6_out), .in1(8'h7f), .out(sevsegCode_0), .sel(and_6_out));
  and and_6 (and_6_out, SECloadU, t_ff_1_q);
endmodule

module hourView_HM_reverse (
  input  [7:0] sevsegCode_5,
  input  [7:0] sevsegCode_4,
  input  [7:0] sevsegCode_3,
  input  [7:0] sevsegCode_2,
  output [3:0] HT_4,
  output [3:0] HU_4,
  output [3:0] MINT_4,
  output [3:0] MINU_4
);

  Bit_Extender #(.out_width(4)) bit_extender_1 (.in(sevsegCode_5), .out(HT_4));
  Bit_Extender #(.out_width(4)) bit_extender_2 (.in(sevsegCode_4), .out(HU_4));
  Bit_Extender #(.out_width(4)) bit_extender_3 (.in(sevsegCode_3), .out(MINT_4));
  Bit_Extender #(.out_width(4)) bit_extender_4 (.in(sevsegCode_2), .out(MINU_4));
endmodule

module hourView_HMS_reverse (
  input  [7:0] sevsegCode_5,
  input  [7:0] sevsegCode_4,
  input  [7:0] sevsegCode_3,
  input  [7:0] sevsegCode_2,
  input  [7:0] sevsegCode_1,
  input  [7:0] sevsegCode_0,
  output [3:0] HT_4,
  output [3:0] HU_4,
  output [3:0] MINT_4,
  output [3:0] MINU_4,
  output [3:0] SECT_4,
  output [3:0] SECU_4
);

  Bit_Extender #(.out_width(4)) bit_extender_1 (.in(sevsegCode_5), .out(HT_4));
  Bit_Extender #(.out_width(4)) bit_extender_2 (.in(sevsegCode_4), .out(HU_4));
  Bit_Extender #(.out_width(4)) bit_extender_3 (.in(sevsegCode_3), .out(MINT_4));
  Bit_Extender #(.out_width(4)) bit_extender_4 (.in(sevsegCode_2), .out(MINU_4));
  Bit_Extender #(.out_width(4)) bit_extender_5 (.in(sevsegCode_1), .out(SECT_4));
  Bit_Extender #(.out_width(4)) bit_extender_6 (.in(sevsegCode_0), .out(SECU_4));
endmodule

module copypasteLW (
  output out_1,
  output [7:0] H_8,
  output [7:0] MIN_8,
  output [7:0] SEC_8
);

  wire bcd_to_7_segment_decoder_2_p1, bcd_to_7_segment_decoder_4_p1, bcd_to_7_segment_decoder_6_p1,
       binairy_to_bcd_converter_1_p2, clock_1_out, d_ff_1_q, d_ff_1_qn, L_7_Segment_Display_0_p1,
       L_7_Segment_Display_1_p1, L_7_Segment_Display_2_p1, L_7_Segment_Display_3_p1,
       L_7_Segment_Display_4_p1, L_7_Segment_Display_5_p1, n7_segment_display_3_p1, n7_segment_display_5_p1,
       n7_segment_display_7_p1;
  wire [3:0] undriven, undriven_2, undriven_3, undriven_4, undriven_5, undriven_6;
  wire [7:0] multiplier_1_out, multiplier_2_out, multiplier_3_out;
  wire [8:0] counter_2_q;
  wire [9:0] counter_1_q;

  Clock clock_1 (.out(clock_1_out));
  D_Flip_Flop d_ff_1 (.D(d_ff_1_qn), .clk(clock_1_out), .Q(d_ff_1_q), .Qn(d_ff_1_qn));  // open: preset, reset
  Counter #(.width(10), .max('h3e7)) counter_1 (
    .clk(clock_1_out), .Q(counter_1_q));  // open: clr, load, up, count, D, carry
  Counter #(.width(9), .max('h1f3)) counter_2 (
    .clk(d_ff_1_q), .Q(counter_2_q));  // open: clr, load, up, count, D, carry
  Multiplier multiplier_1 (.a({4'b0000, undriven}), .b(8'ha), .out(multiplier_1_out));  // open: cin, cout
  Multiplier multiplier_2 (.a({4'b0000, undriven_2}), .b(8'ha), .out(multiplier_2_out));  // open: cin, cout
  Multiplier multiplier_3 (.a({4'b0000, undriven_3}), .b(8'ha), .out(multiplier_3_out));  // open: cin, cout
  Adder adder_1 (.a(multiplier_1_out), .b({4'b0000, undriven_5}), .out(H_8));  // open: cin, cout
  Adder adder_2 (.a(multiplier_2_out), .b({4'b0000, undriven_6}), .out(MIN_8));  // open: cin, cout
  Adder adder_3 (.a(multiplier_3_out), .b({4'b0000, undriven_4}), .out(SEC_8));  // open: cin, cout
  // BCD_to_7_Segment_decoder bcd_to_7_segment_decoder_1: pin names not known; wires that end beside it: out_1
  // BCD_to_7_Segment_decoder bcd_to_7_segment_decoder_2: pin names not known; wires that end beside it: bcd_to_7_segment_decoder_2_p1
  _7_Segment_Display u_7_segment_display_1 ();  // open: g, f, a, b, e, d, c, dp
  _7_Segment_Display u_7_segment_display_2 ();  // open: g, f, a, b, e, d, c, dp
  // Binairy_to_BCD_converter #(.binvalue(10)) binairy_to_bcd_converter_1: pin names not known; wires that end beside it: counter_1_q, binairy_to_bcd_converter_1_p2, binairy_to_bcd_converter_1_p2, bcd_to_7_segment_decoder_2_p1
  // BCD_to_7_Segment_decoder bcd_to_7_segment_decoder_3: pin names not known
  // _7_Segment_Display 7_segment_display_3: pin names not known; wires that end beside it: n7_segment_display_3_p1, n7_segment_display_3_p1
  // Binairy_to_BCD_converter binairy_to_bcd_converter_2: pin names not known; wires that end beside it: counter_2_q
  _7_Segment_Display u_7_segment_display_4 ();  // open: g, f, a, b, e, d, c, dp
  // BCD_to_7_Segment_decoder bcd_to_7_segment_decoder_4: pin names not known; wires that end beside it: bcd_to_7_segment_decoder_4_p1, bcd_to_7_segment_decoder_4_p1
  // _7_Segment_Display 7_segment_display_5: pin names not known; wires that end beside it: n7_segment_display_5_p1, n7_segment_display_5_p1
  // BCD_to_7_Segment_decoder bcd_to_7_segment_decoder_5: pin names not known
  // BCD_to_7_Segment_decoder bcd_to_7_segment_decoder_6: pin names not known; wires that end beside it: bcd_to_7_segment_decoder_6_p1, bcd_to_7_segment_decoder_6_p1
  _7_Segment_Display u_7_segment_display_6 ();  // open: g, f, a, b, e, d, c, dp
  // BCD_to_7_Segment_decoder bcd_to_7_segment_decoder_7: pin names not known
  // _7_Segment_Display 7_segment_display_7: pin names not known; wires that end beside it: n7_segment_display_7_p1, n7_segment_display_7_p1
  // _7_Segment_Display L_7_Segment_Display_5: pin names not known; wires that end beside it: L_7_Segment_Display_5_p1, L_7_Segment_Display_5_p1
  // BCD_to_7_Segment_decoder bcd_to_7_segment_decoder_8: pin names not known
  // Binairy_to_BCD_converter #(.binvalue(8)) binairy_to_bcd_converter_3: pin names not known
  // _7_Segment_Display L_7_Segment_Display_3: pin names not known; wires that end beside it: L_7_Segment_Display_3_p1, L_7_Segment_Display_3_p1
  // BCD_to_7_Segment_decoder bcd_to_7_segment_decoder_9: pin names not known
  // Binairy_to_BCD_converter #(.binvalue(8)) binairy_to_bcd_converter_4: pin names not known
  // BCD_to_7_Segment_decoder bcd_to_7_segment_decoder_10: pin names not known
  // _7_Segment_Display L_7_Segment_Display_1: pin names not known; wires that end beside it: L_7_Segment_Display_1_p1, L_7_Segment_Display_1_p1
  // Binairy_to_BCD_converter #(.binvalue(8)) binairy_to_bcd_converter_5: pin names not known
  // BCD_to_7_Segment_decoder bcd_to_7_segment_decoder_11: pin names not known
  // _7_Segment_Display L_7_Segment_Display_4: pin names not known; wires that end beside it: L_7_Segment_Display_4_p1, L_7_Segment_Display_4_p1
  // BCD_to_7_Segment_decoder bcd_to_7_segment_decoder_12: pin names not known
  // _7_Segment_Display L_7_Segment_Display_2: pin names not known; wires that end beside it: L_7_Segment_Display_2_p1, L_7_Segment_Display_2_p1
  // _7_Segment_Display L_7_Segment_Display_0: pin names not known; wires that end beside it: L_7_Segment_Display_0_p1, L_7_Segment_Display_0_p1
  // BCD_to_7_Segment_decoder bcd_to_7_segment_decoder_13: pin names not known
endmodule

module load_2 (
  input  IN1,
  input  IN0,
  input  [3:0] loadValue,
  input  loadEnDi,
  output OUT1,
  output OUT0
);

  Multiplexer #(.enable("false")) multiplexer_1 (.in0(IN1), .in1(loadValue[1]), .out(OUT1), .sel(loadEnDi));
  Multiplexer #(.enable("false")) multiplexer_2 (.in0(IN0), .in1(loadValue[0]), .out(OUT0), .sel(loadEnDi));
endmodule

module load_3 (
  input  IN2,
  input  IN1,
  input  IN0,
  input  [3:0] loadValue,
  input  loadEnDi,
  output OUT2,
  output OUT1,
  output OUT0
);

  Multiplexer #(.enable("false")) multiplexer_1 (.in0(IN2), .in1(loadValue[2]), .out(OUT2), .sel(loadEnDi));
  Multiplexer #(.enable("false")) multiplexer_2 (.in0(IN1), .in1(loadValue[1]), .out(OUT1), .sel(loadEnDi));
  Multiplexer #(.enable("false")) multiplexer_3 (.in0(IN0), .in1(loadValue[0]), .out(OUT0), .sel(loadEnDi));
endmodule

module load_4 (
  input  IN3,
  input  IN2,
  input  IN1,
  input  IN0,
  input  [3:0] loadValue,
  input  loadEnDi,
  output OUT3,
  output OUT2,
  output OUT1,
  output OUT0
);

  Multiplexer #(.enable("false")) multiplexer_1 (.in0(IN3), .in1(loadValue[3]), .out(OUT3), .sel(loadEnDi));
  Multiplexer #(.enable("false")) multiplexer_2 (.in0(IN2), .in1(loadValue[2]), .out(OUT2), .sel(loadEnDi));
  Multiplexer #(.enable("false")) multiplexer_3 (.in0(IN1), .in1(loadValue[1]), .out(OUT1), .sel(loadEnDi));
  Multiplexer #(.enable("false")) multiplexer_4 (.in0(IN0), .in1(loadValue[0]), .out(OUT0), .sel(loadEnDi));
endmodule

module changeHour (
  input  [1:0] B1_B0,
  output [3:0] HloadT_4,
  output HloadTEnDi,
  output [3:0] HloadU_4,
  output HloadUEnDi,
  output [3:0] MINloadT_4,
  output MINloadTEnDi,
  output [3:0] MINloadU_4,
  output MINloadUEnDi,
  output [3:0] SECloadT_4,
  output SECloadTEnDi,
  output [3:0] SECloadU_4,
  output SECloadUEnDi
);

  wire demultiplexer_1_out1, demultiplexer_1_out2, demultiplexer_1_out3, demultiplexer_1_out4,
       demultiplexer_1_out5, demultiplexer_1_out6, demultiplexer_2_out0;
  wire [1:0] counter_2_q, counter_3_q;
  wire [2:0] counter_1_q, counter_5_q, counter_7_q;
  wire [3:0] bit_extender_2_out, counter_4_q;

  Counter #(.width(3), .max('h6)) counter_1 (.clk(B1_B0[0]), .Q(counter_1_q));  // open: clr, load, up, count, D, carry
  Demultiplexer #(.select(3), .enable("false")) demultiplexer_1 (
    .out1(demultiplexer_1_out1), .out2(demultiplexer_1_out2), .out3(demultiplexer_1_out3),
    .out4(demultiplexer_1_out4), .out5(demultiplexer_1_out5), .out6(demultiplexer_1_out6), .in(B1_B0[1]),
    .sel(counter_1_q));  // open: out0, out7
  Demultiplexer #(.select(3), .enable("false")) demultiplexer_2 (
    .out0(demultiplexer_2_out0), .out1(HloadTEnDi), .out2(HloadUEnDi), .out3(MINloadTEnDi),
    .out4(MINloadUEnDi), .out5(SECloadTEnDi), .out6(SECloadUEnDi), .in(1'b1), .sel(counter_1_q));  // open: out7
  Counter #(.width(2), .max('h2)) counter_2 (
    .clr(demultiplexer_2_out0), .clk(demultiplexer_1_out1), .Q(counter_2_q));  // open: load, up, count, D, carry
  assign HloadT_4 = {{2{1'b0}}, counter_2_q};  // Bit_Extender bit_extender_1
  Counter #(.width(2), .max('h3)) counter_3 (
    .clr(demultiplexer_2_out0), .clk(demultiplexer_1_out2), .Q(counter_3_q));  // open: load, up, count, D, carry
  Counter #(.width(4), .max('h9)) counter_4 (
    .clr(demultiplexer_2_out0), .clk(demultiplexer_1_out2), .Q(counter_4_q));  // open: load, up, count, D, carry
  Counter #(.width(3), .max('h5)) counter_5 (
    .clr(demultiplexer_2_out0), .clk(demultiplexer_1_out3), .Q(counter_5_q));  // open: load, up, count, D, carry
  Counter #(.width(4), .max('h9)) counter_6 (
    .clr(demultiplexer_2_out0), .clk(demultiplexer_1_out4), .Q(MINloadU_4));  // open: load, up, count, D, carry
  Counter #(.width(3), .max('h5)) counter_7 (
    .clr(demultiplexer_2_out0), .clk(demultiplexer_1_out5), .Q(counter_7_q));  // open: load, up, count, D, carry
  Counter #(.width(4), .max('h9)) counter_8 (
    .clr(demultiplexer_2_out0), .clk(demultiplexer_1_out6), .Q(SECloadU_4));  // open: load, up, count, D, carry
  assign bit_extender_2_out = {{2{1'b0}}, counter_3_q};  // Bit_Extender bit_extender_2
  assign MINloadT_4 = {{1{1'b0}}, counter_5_q};  // Bit_Extender bit_extender_3
  assign SECloadT_4 = {{1{1'b0}}, counter_7_q};  // Bit_Extender bit_extender_4
  Multiplexer #(.width(4), .enable("false")) multiplexer_1 (
    .in0(counter_4_q), .in1(bit_extender_2_out), .out(HloadU_4), .sel(counter_2_q[1]));
endmodule

module alarm (
  input  RESET,
  input  [1:0] B1_B0,
  input  [7:0] SSDCode_5,
  input  [7:0] SSDCode_4,
  input  [7:0] SSDCode_3,
  input  [7:0] SSDCode_2,
  output [7:0] sevsegCode_5,
  output [7:0] sevsegCode_4,
  output [7:0] sevsegCode_3,
  output [7:0] sevsegCode_2,
  output [7:0] sevsegCode_1,
  output [7:0] sevsegCode_0,
  output BUZZER
);

  wire alarmHM_1_curonoff, alarmHM_1_hloadt, alarmHM_1_hloadu, alarmHM_1_minloadt, alarmHM_1_minloadu,
       alarmHM_1_onoffl, changeAlarm_1_hloadtendi, changeAlarm_1_hloaduendi, changeAlarm_1_minloadtendi,
       changeAlarm_1_minloaduendi, changeAlarm_1_onoffload, changeAlarm_1_onoffloadendi,
       clk32k_to_2k_1_clk2k, clock_1_out, compare_1_equal;
  wire [3:0] alarmHM_1_curht_4, alarmHM_1_curhu_4, alarmHM_1_curmint_4, alarmHM_1_curminu_4,
       changeAlarm_1_hloadt_4, changeAlarm_1_hloadu_4, changeAlarm_1_minloadt_4, changeAlarm_1_minloadu_4,
       hourView_HM_reverse_1_ht_4, hourView_HM_reverse_1_hu_4, hourView_HM_reverse_1_mint_4,
       hourView_HM_reverse_1_minu_4;
  wire [7:0] multiplexer_1_out;

  Clock clock_1 (.out(clock_1_out));
  hourView_HM_reverse hourView_HM_reverse_1 (
    .sevsegCode_5(SSDCode_5), .sevsegCode_4(SSDCode_4), .sevsegCode_3(SSDCode_3), .sevsegCode_2(SSDCode_2),
    .HT_4(hourView_HM_reverse_1_ht_4), .HU_4(hourView_HM_reverse_1_hu_4),
    .MINT_4(hourView_HM_reverse_1_mint_4), .MINU_4(hourView_HM_reverse_1_minu_4));
  clk32k_to_2k clk32k_to_2k_1 (.CLK32k(clock_1_out), .CLK2k(clk32k_to_2k_1_clk2k));
  changeAlarm changeAlarm_1 (
    .B1_B0(B1_B0), .HloadT_4(changeAlarm_1_hloadt_4), .HloadTEnDi(changeAlarm_1_hloadtendi),
    .HloadU_4(changeAlarm_1_hloadu_4), .HloadUEnDi(changeAlarm_1_hloaduendi),
    .MINloadT_4(changeAlarm_1_minloadt_4), .MINloadTEnDi(changeAlarm_1_minloadtendi),
    .MINloadU_4(changeAlarm_1_minloadu_4), .MINloadUEnDi(changeAlarm_1_minloaduendi),
    .ONOFFload(changeAlarm_1_onoffload), .ONOFFloadEnDi(changeAlarm_1_onoffloadendi));
  alarmHM alarmHM_1 (
    .RESET(RESET), .CLK2k(clk32k_to_2k_1_clk2k), .HloadT_4(changeAlarm_1_hloadt_4),
    .HloadTEnDi(changeAlarm_1_hloadtendi), .HloadU_4(changeAlarm_1_hloadu_4),
    .HloadUEnDi(changeAlarm_1_hloaduendi), .MINloadT_4(changeAlarm_1_minloadt_4),
    .MINloadTEnDi(changeAlarm_1_minloadtendi), .MINloadU_4(changeAlarm_1_minloadu_4),
    .MINloadUEnDi(changeAlarm_1_minloaduendi), .ONOFFload(changeAlarm_1_onoffload),
    .ONOFFloadEnDi(changeAlarm_1_onoffloadendi), .curHT_4(alarmHM_1_curht_4), .curHU_4(alarmHM_1_curhu_4),
    .curMINT_4(alarmHM_1_curmint_4), .curMINU_4(alarmHM_1_curminu_4), .curONOFF(alarmHM_1_curonoff),
    .HloadT(alarmHM_1_hloadt), .HloadU(alarmHM_1_hloadu), .MINloadT(alarmHM_1_minloadt),
    .MINloadU(alarmHM_1_minloadu), .ONOFFL(alarmHM_1_onoffl));
  compare compare_1 (
    .A3_4(alarmHM_1_curht_4), .A2_4(alarmHM_1_curhu_4), .A1_4(alarmHM_1_curmint_4),
    .A0_4(alarmHM_1_curminu_4), .B3_4(hourView_HM_reverse_1_ht_4), .B2_4(hourView_HM_reverse_1_hu_4),
    .B1_4(hourView_HM_reverse_1_mint_4), .B0_4(hourView_HM_reverse_1_minu_4), .EQUAL(compare_1_equal));
  Multiplexer #(.width(8), .enable("false")) multiplexer_1 (
    .in0(8'hf), .in1(8'h16), .out(multiplexer_1_out), .sel(alarmHM_1_curonoff));
  alarmView_HM alarmView_HM_1 (
    .HT_4(alarmHM_1_curht_4), .HU_4(alarmHM_1_curhu_4), .MINT_4(alarmHM_1_curmint_4),
    .MINU_4(alarmHM_1_curminu_4), .Letter_1_8(8'h17), .Letter_0_8(multiplexer_1_out),
    .HloadT(alarmHM_1_hloadt), .HloadU(alarmHM_1_hloadu), .MINloadT(alarmHM_1_minloadt),
    .MINloadU(alarmHM_1_minloadu), .ONOFFload(alarmHM_1_onoffl), .RESET(RESET), .CLK2k(clk32k_to_2k_1_clk2k),
    .sevsegCode_5(sevsegCode_5), .sevsegCode_4(sevsegCode_4), .sevsegCode_3(sevsegCode_3),
    .sevsegCode_2(sevsegCode_2), .sevsegCode_1(sevsegCode_1), .sevsegCode_0(sevsegCode_0));
  and and_1 (BUZZER, compare_1_equal, alarmHM_1_curonoff);
endmodule

module changeAlarm (
  input  [1:0] B1_B0,
  output [3:0] HloadT_4,
  output HloadTEnDi,
  output [3:0] HloadU_4,
  output HloadUEnDi,
  output [3:0] MINloadT_4,
  output MINloadTEnDi,
  output [3:0] MINloadU_4,
  output MINloadUEnDi,
  output ONOFFload,
  output ONOFFloadEnDi
);

  wire demultiplexer_1_out1, demultiplexer_1_out2, demultiplexer_1_out3, demultiplexer_1_out4,
       demultiplexer_1_out5, demultiplexer_2_out0;
  wire [1:0] counter_2_q, counter_3_q;
  wire [2:0] counter_1_q, counter_5_q;
  wire [3:0] bit_extender_2_out, counter_4_q;

  Counter #(.width(3), .max('h5)) counter_1 (.clk(B1_B0[0]), .Q(counter_1_q));  // open: clr, load, up, count, D, carry
  Demultiplexer #(.select(3), .enable("false")) demultiplexer_1 (
    .out1(demultiplexer_1_out1), .out2(demultiplexer_1_out2), .out3(demultiplexer_1_out3),
    .out4(demultiplexer_1_out4), .out5(demultiplexer_1_out5), .in(B1_B0[1]), .sel(counter_1_q));  // open: out0, out6, out7
  Demultiplexer #(.select(3), .enable("false")) demultiplexer_2 (
    .out0(demultiplexer_2_out0), .out1(HloadTEnDi), .out2(HloadUEnDi), .out3(MINloadTEnDi),
    .out4(MINloadUEnDi), .out5(ONOFFloadEnDi), .in(1'b1), .sel(counter_1_q));  // open: out6, out7
  Counter #(.width(2), .max('h2)) counter_2 (
    .clr(demultiplexer_2_out0), .clk(demultiplexer_1_out1), .Q(counter_2_q));  // open: load, up, count, D, carry
  assign HloadT_4 = {{2{1'b0}}, counter_2_q};  // Bit_Extender bit_extender_1
  Counter #(.width(2), .max('h3)) counter_3 (
    .clr(demultiplexer_2_out0), .clk(demultiplexer_1_out2), .Q(counter_3_q));  // open: load, up, count, D, carry
  Counter #(.width(4), .max('h9)) counter_4 (
    .clr(demultiplexer_2_out0), .clk(demultiplexer_1_out2), .Q(counter_4_q));  // open: load, up, count, D, carry
  Counter #(.width(3), .max('h5)) counter_5 (
    .clr(demultiplexer_2_out0), .clk(demultiplexer_1_out3), .Q(counter_5_q));  // open: load, up, count, D, carry
  Counter #(.width(4), .max('h9)) counter_6 (
    .clr(demultiplexer_2_out0), .clk(demultiplexer_1_out4), .Q(MINloadU_4));  // open: load, up, count, D, carry
  Counter #(.width(1), .max('h1)) counter_7 (
    .clr(demultiplexer_2_out0), .clk(demultiplexer_1_out5), .Q(ONOFFload));  // open: load, up, count, D, carry
  assign bit_extender_2_out = {{2{1'b0}}, counter_3_q};  // Bit_Extender bit_extender_2
  assign MINloadT_4 = {{1{1'b0}}, counter_5_q};  // Bit_Extender bit_extender_3
  Multiplexer #(.width(4), .enable("false")) multiplexer_1 (
    .in0(counter_4_q), .in1(bit_extender_2_out), .out(HloadU_4), .sel(counter_2_q[1]));
endmodule

module alarmView_HM (
  input  [3:0] HT_4,
  input  [3:0] HU_4,
  input  [3:0] MINT_4,
  input  [3:0] MINU_4,
  input  [7:0] Letter_1_8,
  input  [7:0] Letter_0_8,
  input  HloadT,
  input  HloadU,
  input  MINloadT,
  input  MINloadU,
  input  ONOFFload,
  input  RESET,
  input  CLK2k,
  output [7:0] sevsegCode_5,
  output [7:0] sevsegCode_4,
  output [7:0] sevsegCode_3,
  output [7:0] sevsegCode_2,
  output [7:0] sevsegCode_1,
  output [7:0] sevsegCode_0
);

  wire and_1_out, and_2_out, and_3_out, and_4_out, and_5_out, and_6_out, clk2k_to_4_1_clk4, or_1_out,
       t_ff_1_q;
  wire [6:0] bit_extender_2_out, bit_extender_4_out, multiplexer_2_out, multiplexer_4_out;
  wire [7:0] bit_extender_1_out, bit_extender_3_out;

  assign bit_extender_1_out = {{4{1'b0}}, HT_4};  // Bit_Extender bit_extender_1
  assign bit_extender_2_out = {{3{1'b0}}, HU_4};  // Bit_Extender bit_extender_2
  assign bit_extender_3_out = {{4{1'b0}}, MINT_4};  // Bit_Extender bit_extender_3
  assign bit_extender_4_out = {{3{1'b0}}, MINU_4};  // Bit_Extender bit_extender_4
  or or_1 (or_1_out, HloadT, HloadU, MINloadT, MINloadU, ONOFFload);
  clk2k_to_4 clk2k_to_4_1 (.CLK2k(CLK2k), .CLK4(clk2k_to_4_1_clk4));
  Multiplexer #(.width(8), .enable("false")) multiplexer_1 (
    .in0(bit_extender_1_out), .in1(8'h7f), .out(sevsegCode_5), .sel(and_1_out));
  and and_1 (and_1_out, HloadT, t_ff_1_q);
  T_Flip_Flop t_ff_1 (.T(or_1_out), .clk(clk2k_to_4_1_clk4), .Q(t_ff_1_q), .reset(RESET));  // open: Qn, preset
  Multiplexer #(.width(7), .enable("false")) multiplexer_2 (
    .in0(bit_extender_2_out), .in1({7{1'b1}}), .out(multiplexer_2_out), .sel(and_2_out));
  and and_2 (and_2_out, HloadU, t_ff_1_q);
  Multiplexer #(.width(8), .enable("false")) multiplexer_3 (
    .in0(bit_extender_3_out), .in1(8'h7f), .out(sevsegCode_3), .sel(and_3_out));
  and and_3 (and_3_out, MINloadT, t_ff_1_q);
  and and_4 (and_4_out, MINloadU, t_ff_1_q);
  assign sevsegCode_4 = {{1{1'b1}}, multiplexer_2_out};  // Bit_Extender bit_extender_5
  Multiplexer #(.width(7), .enable("false")) multiplexer_4 (
    .in0(bit_extender_4_out), .in1({7{1'b1}}), .out(multiplexer_4_out), .sel(and_4_out));
  assign sevsegCode_2 = {{1{1'b1}}, multiplexer_4_out};  // Bit_Extender bit_extender_6
  Multiplexer #(.width(8), .enable("false")) multiplexer_5 (
    .in0(Letter_1_8), .in1(8'h7f), .out(sevsegCode_1), .sel(and_5_out));
  and and_5 (and_5_out, ONOFFload, t_ff_1_q);
  Multiplexer #(.width(8), .enable("false")) multiplexer_6 (
    .in0(Letter_0_8), .in1(8'h7f), .out(sevsegCode_0), .sel(and_6_out));
  and and_6 (and_6_out, ONOFFload, t_ff_1_q);
endmodule

module alarmHM (
  input  RESET,
  input  CLK2k,
  input  [3:0] HloadT_4,
  input  HloadTEnDi,
  input  [3:0] HloadU_4,
  input  HloadUEnDi,
  input  [3:0] MINloadT_4,
  input  MINloadTEnDi,
  input  [3:0] MINloadU_4,
  input  MINloadUEnDi,
  input  ONOFFload,
  input  ONOFFloadEnDi,
  output [3:0] curHT_4,
  output [3:0] curHU_4,
  output [3:0] curMINT_4,
  output [3:0] curMINU_4,
  output curONOFF,
  output HloadT,
  output HloadU,
  output MINloadT,
  output MINloadU,
  output ONOFFL
);

  wire and_1_out, and_2_out, and_3_out, and_4_out, and_5_out, and_6_out, and_7_out, and_8_out, and_9_out,
       and_10_out, and_11_out, and_12_out, and_13_out, load_2_1_out0, load_2_1_out1, load_3_1_out0,
       load_3_1_out1, load_3_1_out2, load_4_1_out0, load_4_1_out1, load_4_1_out2, load_4_1_out3,
       load_4_2_out0, load_4_2_out1, load_4_2_out2, load_4_2_out3, multiplexer_1_out;
  wire [1:0] d_ff_2_q;
  wire [2:0] d_ff_9_q;

  load_2 load_2_1 (
    .IN1(d_ff_2_q[1]), .IN0(d_ff_2_q[0]), .loadValue(HloadT_4), .loadEnDi(HloadTEnDi), .OUT1(load_2_1_out1),
    .OUT0(load_2_1_out0));
  load_4 load_4_2 (
    .IN3(curHU_4[3]), .IN2(curHU_4[2]), .IN1(curHU_4[1]), .IN0(curHU_4[0]), .loadValue(HloadU_4),
    .loadEnDi(HloadUEnDi), .OUT3(load_4_2_out3), .OUT2(load_4_2_out2), .OUT1(load_4_2_out1),
    .OUT0(load_4_2_out0));
  load_3 load_3_1 (
    .IN2(d_ff_9_q[2]), .IN1(d_ff_9_q[1]), .IN0(d_ff_9_q[0]), .loadValue(MINloadT_4), .loadEnDi(MINloadTEnDi),
    .OUT2(load_3_1_out2), .OUT1(load_3_1_out1), .OUT0(load_3_1_out0));
  load_4 load_4_1 (
    .IN3(curMINU_4[3]), .IN2(curMINU_4[2]), .IN1(curMINU_4[1]), .IN0(curMINU_4[0]), .loadValue(MINloadU_4),
    .loadEnDi(MINloadUEnDi), .OUT3(load_4_1_out3), .OUT2(load_4_1_out2), .OUT1(load_4_1_out1),
    .OUT0(load_4_1_out0));
  Multiplexer #(.enable("false")) multiplexer_1 (
    .in0(curONOFF), .in1(ONOFFload), .out(multiplexer_1_out), .sel(ONOFFloadEnDi));
  and and_1 (and_1_out, ~RESET, load_2_1_out1);  // AND_Gate
  and and_2 (and_2_out, ~RESET, load_2_1_out0);  // AND_Gate
  and and_3 (and_3_out, ~RESET, load_4_2_out3);  // AND_Gate
  and and_4 (and_4_out, ~RESET, load_4_2_out2);  // AND_Gate
  and and_5 (and_5_out, ~RESET, load_4_2_out1);  // AND_Gate
  and and_6 (and_6_out, ~RESET, load_4_2_out0);  // AND_Gate
  and and_7 (and_7_out, ~RESET, load_3_1_out2);  // AND_Gate
  and and_8 (and_8_out, ~RESET, load_3_1_out1);  // AND_Gate
  and and_9 (and_9_out, ~RESET, load_3_1_out0);  // AND_Gate
  and and_10 (and_10_out, ~RESET, load_4_1_out3);  // AND_Gate
  and and_11 (and_11_out, ~RESET, load_4_1_out2);  // AND_Gate
  and and_12 (and_12_out, ~RESET, load_4_1_out1);  // AND_Gate
  and and_13 (and_13_out, ~RESET, load_4_1_out0);  // AND_Gate
  D_Flip_Flop d_ff_1 (.D(and_1_out), .clk(CLK2k), .Q(d_ff_2_q[1]), .reset(RESET));  // open: Qn, preset
  D_Flip_Flop d_ff_2 (.D(and_2_out), .clk(CLK2k), .Q(d_ff_2_q[0]), .reset(RESET));  // open: Qn, preset
  D_Flip_Flop d_ff_3 (.D(and_3_out), .clk(CLK2k), .Q(curHU_4[3]), .reset(RESET));  // open: Qn, preset
  D_Flip_Flop d_ff_4 (.D(and_4_out), .clk(CLK2k), .Q(curHU_4[2]), .reset(RESET));  // open: Qn, preset
  D_Flip_Flop d_ff_5 (.D(and_5_out), .clk(CLK2k), .Q(curHU_4[1]), .reset(RESET));  // open: Qn, preset
  D_Flip_Flop d_ff_6 (.D(and_6_out), .clk(CLK2k), .Q(curHU_4[0]), .reset(RESET));  // open: Qn, preset
  D_Flip_Flop d_ff_7 (.D(and_7_out), .clk(CLK2k), .Q(d_ff_9_q[2]), .reset(RESET));  // open: Qn, preset
  D_Flip_Flop d_ff_8 (.D(and_8_out), .clk(CLK2k), .Q(d_ff_9_q[1]), .reset(RESET));  // open: Qn, preset
  D_Flip_Flop d_ff_9 (.D(and_9_out), .clk(CLK2k), .Q(d_ff_9_q[0]), .reset(RESET));  // open: Qn, preset
  D_Flip_Flop d_ff_10 (.D(and_10_out), .clk(CLK2k), .Q(curMINU_4[3]), .reset(RESET));  // open: Qn, preset
  D_Flip_Flop d_ff_11 (.D(and_11_out), .clk(CLK2k), .Q(curMINU_4[2]), .reset(RESET));  // open: Qn, preset
  D_Flip_Flop d_ff_12 (.D(and_12_out), .clk(CLK2k), .Q(curMINU_4[1]), .reset(RESET));  // open: Qn, preset
  D_Flip_Flop d_ff_13 (.D(and_13_out), .clk(CLK2k), .Q(curMINU_4[0]), .reset(RESET));  // open: Qn, preset
  D_Flip_Flop d_ff_14 (.D(multiplexer_1_out), .clk(CLK2k), .Q(curONOFF), .reset(RESET));  // open: Qn, preset
  assign curHT_4 = {{2{1'b0}}, d_ff_2_q};  // Bit_Extender bit_extender_1
  assign curMINT_4 = {{1{1'b0}}, d_ff_9_q};  // Bit_Extender bit_extender_2

  assign HloadT = HloadTEnDi;
  assign HloadU = HloadUEnDi;
  assign MINloadT = MINloadTEnDi;
  assign MINloadU = MINloadUEnDi;
  assign ONOFFL = ONOFFloadEnDi;
endmodule

module compare (
  input  [3:0] A3_4,
  input  [3:0] A2_4,
  input  [3:0] A1_4,
  input  [3:0] A0_4,
  input  [3:0] B3_4,
  input  [3:0] B2_4,
  input  [3:0] B1_4,
  input  [3:0] B0_4,
  output EQUAL
);

  wire compare_4_1_equal_4, compare_4_2_equal_4, compare_4_3_equal_4, compare_4_4_equal_4;

  compare_4 compare_4_4 (.A_4(A3_4), .B_4(B3_4), .EQUAL_4(compare_4_4_equal_4));
  compare_4 compare_4_3 (.A_4(A2_4), .B_4(B2_4), .EQUAL_4(compare_4_3_equal_4));
  compare_4 compare_4_2 (.A_4(A1_4), .B_4(B1_4), .EQUAL_4(compare_4_2_equal_4));
  compare_4 compare_4_1 (.A_4(A0_4), .B_4(B0_4), .EQUAL_4(compare_4_1_equal_4));
  and and_1 (EQUAL, compare_4_4_equal_4, compare_4_3_equal_4, compare_4_2_equal_4, compare_4_1_equal_4);
endmodule

module compare_4 (
  input  [3:0] A_4,
  input  [3:0] B_4,
  output EQUAL_4
);

  wire xnor_1_out, xnor_2_out, xnor_3_out, xnor_4_out;

  xnor xnor_1 (xnor_1_out, A_4[0], B_4[0]);
  xnor xnor_2 (xnor_2_out, A_4[1], B_4[1]);
  xnor xnor_3 (xnor_3_out, A_4[2], B_4[2]);
  xnor xnor_4 (xnor_4_out, A_4[3], B_4[3]);
  and and_1 (EQUAL_4, xnor_1_out, xnor_2_out, xnor_3_out, xnor_4_out);
endmodule

module changeTimeZoneOnBoard (
);

  wire dip_sw10;
  wire [1:0] B_0_out;
  wire [7:0] AllsegLeds_bis_1_output_bus_1, AllsegLeds_bis_1_output_bus_2, AllsegLeds_bis_1_output_bus_3,
       AllsegLeds_bis_1_output_bus_4, AllsegLeds_bis_1_output_bus_5, AllsegLeds_bis_1_output_bus_6,
       hourFSM_1_sevsegcode_0, hourFSM_1_sevsegcode_1, hourFSM_1_sevsegcode_2, hourFSM_1_sevsegcode_3,
       hourFSM_1_sevsegcode_4, hourFSM_1_sevsegcode_5;

  Button B_0 (.out(B_0_out[0]));
  Button B_1 (.out(B_0_out[1]));
  DipSwitch #(.number(10)) dip (.sw10(dip_sw10));  // open: sw1, sw2, sw3, sw4, sw5, sw6, sw7, sw8, sw9
  hourFSM hourFSM_1 (
    .RESET(dip_sw10), .B1_B0(B_0_out), .sevsegCode_5(hourFSM_1_sevsegcode_5),
    .sevsegCode_4(hourFSM_1_sevsegcode_4), .sevsegCode_3(hourFSM_1_sevsegcode_3),
    .sevsegCode_2(hourFSM_1_sevsegcode_2), .sevsegCode_1(hourFSM_1_sevsegcode_1),
    .sevsegCode_0(hourFSM_1_sevsegcode_0));
  AllsegLeds_bis AllsegLeds_bis_1 (
    .Input_bus_1(hourFSM_1_sevsegcode_5), .Input_bus_2(hourFSM_1_sevsegcode_4),
    .Input_bus_3(hourFSM_1_sevsegcode_3), .Input_bus_4(hourFSM_1_sevsegcode_2),
    .Input_bus_5(hourFSM_1_sevsegcode_1), .Input_bus_6(hourFSM_1_sevsegcode_0),
    .Output_bus_1(AllsegLeds_bis_1_output_bus_1), .Output_bus_2(AllsegLeds_bis_1_output_bus_2),
    .Output_bus_3(AllsegLeds_bis_1_output_bus_3), .Output_bus_4(AllsegLeds_bis_1_output_bus_4),
    .Output_bus_5(AllsegLeds_bis_1_output_bus_5), .Output_bus_6(AllsegLeds_bis_1_output_bus_6));
  _7_Segment_Display L_7_Segment_Display_5 (
    .g(AllsegLeds_bis_1_output_bus_1[0]), .f(AllsegLeds_bis_1_output_bus_1[1]),
    .a(AllsegLeds_bis_1_output_bus_1[6]), .b(AllsegLeds_bis_1_output_bus_1[5]),
    .e(AllsegLeds_bis_1_output_bus_1[2]), .d(AllsegLeds_bis_1_output_bus_1[3]),
    .c(AllsegLeds_bis_1_output_bus_1[4]), .dp(AllsegLeds_bis_1_output_bus_1[7]));
  _7_Segment_Display L_7_Segment_Display_4 (
    .g(AllsegLeds_bis_1_output_bus_2[0]), .f(AllsegLeds_bis_1_output_bus_2[1]),
    .a(AllsegLeds_bis_1_output_bus_2[6]), .b(AllsegLeds_bis_1_output_bus_2[5]),
    .e(AllsegLeds_bis_1_output_bus_2[2]), .d(AllsegLeds_bis_1_output_bus_2[3]),
    .c(AllsegLeds_bis_1_output_bus_2[4]), .dp(AllsegLeds_bis_1_output_bus_2[7]));
  _7_Segment_Display L_7_Segment_Display_3 (
    .g(AllsegLeds_bis_1_output_bus_3[0]), .f(AllsegLeds_bis_1_output_bus_3[1]),
    .a(AllsegLeds_bis_1_output_bus_3[6]), .b(AllsegLeds_bis_1_output_bus_3[5]),
    .e(AllsegLeds_bis_1_output_bus_3[2]), .d(AllsegLeds_bis_1_output_bus_3[3]),
    .c(AllsegLeds_bis_1_output_bus_3[4]), .dp(AllsegLeds_bis_1_output_bus_3[7]));
  _7_Segment_Display L_7_Segment_Display_2 (
    .g(AllsegLeds_bis_1_output_bus_4[0]), .f(AllsegLeds_bis_1_output_bus_4[1]),
    .a(AllsegLeds_bis_1_output_bus_4[6]), .b(AllsegLeds_bis_1_output_bus_4[5]),
    .e(AllsegLeds_bis_1_output_bus_4[2]), .d(AllsegLeds_bis_1_output_bus_4[3]),
    .c(AllsegLeds_bis_1_output_bus_4[4]), .dp(AllsegLeds_bis_1_output_bus_4[7]));
  _7_Segment_Display L_7_Segment_Display_1 (
    .g(AllsegLeds_bis_1_output_bus_5[0]), .f(AllsegLeds_bis_1_output_bus_5[1]),
    .a(AllsegLeds_bis_1_output_bus_5[6]), .b(AllsegLeds_bis_1_output_bus_5[5]),
    .e(AllsegLeds_bis_1_output_bus_5[2]), .d(AllsegLeds_bis_1_output_bus_5[3]),
    .c(AllsegLeds_bis_1_output_bus_5[4]), .dp(AllsegLeds_bis_1_output_bus_5[7]));
  _7_Segment_Display L_7_Segment_Display_0 (
    .g(AllsegLeds_bis_1_output_bus_6[0]), .f(AllsegLeds_bis_1_output_bus_6[1]),
    .a(AllsegLeds_bis_1_output_bus_6[6]), .b(AllsegLeds_bis_1_output_bus_6[5]),
    .e(AllsegLeds_bis_1_output_bus_6[2]), .d(AllsegLeds_bis_1_output_bus_6[3]),
    .c(AllsegLeds_bis_1_output_bus_6[4]), .dp(AllsegLeds_bis_1_output_bus_6[7]));
endmodule

module changeTimeZone (
  input  [7:0] SSDCode_5,
  input  [7:0] SSDCode_4,
  input  [7:0] SSDCode_3,
  input  [7:0] SSDCode_2,
  input  [7:0] SSDCode_1,
  input  [7:0] SSDCode_0,
  input  [7:0] UTCCode_8,
  output [7:0] sevsegCode_5,
  output [7:0] sevsegCode_4,
  output [7:0] sevsegCode_3,
  output [7:0] sevsegCode_2,
  output [7:0] sevsegCode_1,
  output [7:0] sevsegCode_0
);

  wire [3:0] H_HTimeZone_1_httz_4, H_HTimeZone_1_hutz_4, hourView_HMS_reverse_1_ht_4,
       hourView_HMS_reverse_1_hu_4, hourView_HMS_reverse_1_mint_4, hourView_HMS_reverse_1_minu_4,
       hourView_HMS_reverse_1_sect_4, hourView_HMS_reverse_1_secu_4;

  hourView_HMS_reverse hourView_HMS_reverse_1 (
    .sevsegCode_5(SSDCode_5), .sevsegCode_4(SSDCode_4), .sevsegCode_3(SSDCode_3), .sevsegCode_2(SSDCode_2),
    .sevsegCode_1(SSDCode_1), .sevsegCode_0(SSDCode_0), .HT_4(hourView_HMS_reverse_1_ht_4),
    .HU_4(hourView_HMS_reverse_1_hu_4), .MINT_4(hourView_HMS_reverse_1_mint_4),
    .MINU_4(hourView_HMS_reverse_1_minu_4), .SECT_4(hourView_HMS_reverse_1_sect_4),
    .SECU_4(hourView_HMS_reverse_1_secu_4));
  H_HTimeZone H_HTimeZone_1 (
    .HT_4(hourView_HMS_reverse_1_ht_4), .HU_4(hourView_HMS_reverse_1_hu_4), .UTCCode_8(UTCCode_8),
    .HTTZ_4(H_HTimeZone_1_httz_4), .HUTZ_4(H_HTimeZone_1_hutz_4));
  hourView_HMS hourView_HMS_1 (
    .HT_4(H_HTimeZone_1_httz_4), .HU_4(H_HTimeZone_1_hutz_4), .MINT_4(hourView_HMS_reverse_1_mint_4),
    .MINU_4(hourView_HMS_reverse_1_minu_4), .SECT_4(hourView_HMS_reverse_1_sect_4),
    .SECU_4(hourView_HMS_reverse_1_secu_4), .sevsegCode_5(sevsegCode_5), .sevsegCode_4(sevsegCode_4),
    .sevsegCode_3(sevsegCode_3), .sevsegCode_2(sevsegCode_2), .sevsegCode_1(sevsegCode_1),
    .sevsegCode_0(sevsegCode_0));  // open: HloadT, HloadU, MINloadT, MINloadU, SECloadT, SECloadU, RESET, CLK2k
endmodule

module H_HTimeZone (
  input  [3:0] HT_4,
  input  [3:0] HU_4,
  input  [7:0] UTCCode_8,
  output [3:0] HTTZ_4,
  output [3:0] HUTZ_4
);

  wire [4:0] adder_2_out, bit_extender_1_out, bit_extender_2_out, bit_extender_5_out, multiplier_1_out;
  wire [6:0] adder_1_out, adder_3_out, adder_4_out, adder_5_out, adder_6_out, adder_7_out,
       bit_extender_3_out, bit_extender_4_out, multiplexer_1_out, multiplexer_2_out;

  assign bit_extender_1_out = {{1{1'b0}}, HT_4};  // Bit_Extender bit_extender_1
  assign bit_extender_2_out = {{1{1'b0}}, HU_4};  // Bit_Extender bit_extender_2
  Bit_Extender #(.out_width(7), .\type ("zero")) bit_extender_3 (.in(UTCCode_8), .out(bit_extender_3_out));
  Multiplier #(.width(5)) multiplier_1 (
    .a(bit_extender_1_out), .b(5'b01010), .out(multiplier_1_out));  // open: cin, cout
  Adder #(.width(7)) adder_1 (.a(bit_extender_3_out), .b(7'b0011000), .out(adder_1_out));  // open: cin, cout
  Adder #(.width(5)) adder_2 (.a(multiplier_1_out), .b(bit_extender_2_out), .out(adder_2_out));  // open: cin, cout
  assign bit_extender_4_out = {{2{1'b0}}, adder_2_out};  // Bit_Extender bit_extender_4
  Adder #(.width(7)) adder_3 (.a(bit_extender_4_out), .b(7'b1101000), .out(adder_3_out));  // open: cin, cout
  Adder #(.width(7)) adder_4 (.a(adder_3_out), .b(adder_1_out), .out(adder_4_out));  // open: cin, cout
  Adder #(.width(7)) adder_5 (.a(adder_4_out), .b(7'b1101000), .out(adder_5_out));  // open: cin, cout
  Adder #(.width(7)) adder_6 (.a(adder_4_out), .b(7'b0011000), .out(adder_6_out));  // open: cin, cout
  Multiplexer #(.width(7), .enable("false")) multiplexer_1 (
    .in0(adder_5_out), .in1(adder_6_out), .out(multiplexer_1_out), .sel(adder_4_out[6]));
  Adder #(.width(7)) adder_7 (.a(multiplexer_1_out), .b(7'b0011000), .out(adder_7_out));  // open: cin, cout
  Multiplexer #(.width(7), .enable("false")) multiplexer_2 (
    .in0(multiplexer_1_out), .in1(adder_7_out), .out(multiplexer_2_out), .sel(multiplexer_1_out[6]));
  Bit_Extender #(.in_width(7), .out_width(5), .\type ("zero")) bit_extender_5 (
    .in(multiplexer_2_out), .out(bit_extender_5_out));
  fivebits_to_2_4bits fivebits_to_2_4bits_1 (
    .A4(bit_extender_5_out[4]), .A3(bit_extender_5_out[3]), .A2(bit_extender_5_out[2]),
    .A1(bit_extender_5_out[1]), .A0(bit_extender_5_out[0]), .T3(HTTZ_4[3]), .T2(HTTZ_4[2]), .T1(HTTZ_4[1]),
    .T0(HTTZ_4[0]), .U3(HUTZ_4[3]), .U2(HUTZ_4[2]), .U1(HUTZ_4[1]), .U0(HUTZ_4[0]));
endmodule

module fivebits_to_2_4bits (
  input  A4,
  input  A3,
  input  A2,
  input  A1,
  input  A0,
  output T3,
  output T2,
  output T1,
  output T0,
  output U3,
  output U2,
  output U1,
  output U0
);

  wire and_1_out, and_2_out, and_3_out, and_4_out, and_5_out, and_6_out, and_7_out, and_8_out, and_9_out,
       and_10_out, and_11_out, and_12_out, and_13_out, and_14_out, and_15_out, and_16_out, and_17_out,
       and_18_out, not_1_out, not_2_out, not_3_out, not_4_out, not_5_out, not_6_out, not_7_out, not_8_out,
       not_9_out, not_10_out, not_11_out, not_12_out, not_13_out, not_14_out, not_15_out, not_16_out,
       not_17_out, not_18_out, not_19_out, not_20_out, not_21_out, not_22_out, not_23_out, not_24_out,
       not_25_out;

  and and_1 (and_1_out, A4, A2);
  and and_2 (and_2_out, A4, A3);
  not not_1 (not_1_out, A4);
  not not_2 (not_2_out, A4);
  not not_3 (not_3_out, A3);
  not not_4 (not_4_out, A2);
  not not_5 (not_5_out, A4);
  not not_6 (not_6_out, A2);
  not not_7 (not_7_out, A1);
  not not_8 (not_8_out, A3);
  not not_9 (not_9_out, A2);
  not not_10 (not_10_out, A1);
  not not_11 (not_11_out, A4);
  not not_12 (not_12_out, A3);
  not not_13 (not_13_out, A4);
  not not_14 (not_14_out, A2);
  not not_15 (not_15_out, A1);
  not not_16 (not_16_out, A2);
  not not_17 (not_17_out, A4);
  not not_18 (not_18_out, A3);
  not not_19 (not_19_out, A3);
  not not_20 (not_20_out, A4);
  not not_21 (not_21_out, A1);
  not not_22 (not_22_out, A3);
  not not_23 (not_23_out, A2);
  not not_24 (not_24_out, A1);
  not not_25 (not_25_out, A2);
  or or_1 (T1, and_1_out, and_2_out);
  and and_3 (and_3_out, not_1_out, A3, A1);
  and and_4 (and_4_out, not_2_out, A3, A2);
  and and_5 (and_5_out, A3, A2, A1);
  and and_6 (and_6_out, A4, not_3_out, not_4_out);
  and and_7 (and_7_out, not_5_out, A3, not_6_out, not_7_out);
  and and_8 (and_8_out, A4, not_8_out, not_9_out, A1);
  and and_9 (and_9_out, A4, A3, A2, not_10_out);
  and and_10 (and_10_out, not_11_out, not_12_out, A2);
  and and_11 (and_11_out, not_13_out, A2, A1);
  and and_12 (and_12_out, A4, not_14_out, not_15_out);
  and and_13 (and_13_out, A4, A3, not_16_out);
  and and_14 (and_14_out, not_17_out, not_18_out, A1);
  and and_15 (and_15_out, not_19_out, A2, A1);
  and and_16 (and_16_out, not_20_out, A3, A2, not_21_out);
  and and_17 (and_17_out, A4, not_22_out, not_23_out, not_24_out);
  and and_18 (and_18_out, A4, A3, not_25_out, A1);
  or or_2 (T0, and_3_out, and_4_out, and_5_out, and_6_out);
  or or_3 (U3, and_7_out, and_8_out, and_9_out);
  or or_4 (U2, and_10_out, and_11_out, and_12_out, and_13_out);
  or or_5 (U1, and_14_out, and_15_out, and_16_out, and_17_out, and_18_out);

  assign T2 = 1'b0;
  assign T3 = 1'b0;
  assign U0 = A0;
endmodule

module DecoderToSegLed_bis (
  input  Input_1,
  input  Input_2,
  input  Input_3,
  input  Input_4,
  input  Input_5,
  input  Input_6,
  output Output_1,
  output Output_2,
  output Output_3,
  output Output_4,
  output Output_5,
  output Output_6,
  output Output_7,
  output Output_8
);

  wire and_1_out, and_2_out, and_3_out, and_4_out, and_5_out, and_6_out, and_7_out, and_8_out, and_9_out,
       and_10_out, and_11_out, and_12_out, and_13_out, and_14_out, and_15_out, and_16_out, and_17_out,
       and_18_out, and_19_out, and_20_out, and_21_out, and_22_out, and_23_out, and_24_out, and_25_out,
       and_26_out, and_27_out, and_28_out, and_29_out, and_30_out, and_31_out, and_32_out, and_33_out,
       and_34_out, and_35_out, and_36_out, and_37_out, and_38_out, and_39_out, and_40_out, and_41_out,
       and_42_out, and_43_out, and_44_out, and_45_out, and_46_out, and_47_out, and_48_out, and_49_out,
       and_50_out, and_51_out, and_52_out, and_53_out, not_1_out, not_2_out, not_3_out, not_4_out, not_5_out,
       not_6_out, not_7_out, not_8_out, not_9_out, not_10_out, not_11_out, not_12_out, not_13_out,
       not_14_out, not_15_out, not_16_out, not_17_out, not_18_out, not_19_out, not_20_out, not_21_out,
       not_22_out, not_23_out, not_24_out, not_25_out, not_26_out, not_27_out, not_28_out, not_29_out,
       not_30_out, not_31_out, not_32_out, not_33_out, not_34_out, not_35_out, not_36_out, not_37_out,
       not_38_out, not_39_out, not_40_out, not_41_out, not_42_out, not_43_out, not_44_out, not_45_out,
       not_46_out, not_47_out, not_48_out, not_49_out, not_50_out, not_51_out, not_52_out, not_53_out,
       not_54_out, not_55_out, not_56_out, not_57_out, not_58_out, not_59_out, not_60_out, not_61_out,
       not_62_out, not_63_out, not_64_out, not_65_out, not_66_out, not_67_out, not_68_out, not_69_out,
       not_70_out, not_71_out, not_72_out, not_73_out, not_74_out, not_75_out, not_76_out, not_77_out,
       not_78_out, not_79_out, not_80_out, not_81_out, not_82_out, not_83_out, not_84_out, not_85_out,
       not_86_out, not_87_out, not_88_out, not_89_out, not_90_out, not_91_out, not_92_out, not_93_out,
       not_94_out, not_95_out, not_96_out;

  not not_1 (not_1_out, Input_4);
  not not_2 (not_2_out, Input_5);
  not not_3 (not_3_out, Input_6);
  not not_4 (not_4_out, Input_2);
  not not_5 (not_5_out, Input_3);
  not not_6 (not_6_out, Input_3);
  not not_7 (not_7_out, Input_5);
  not not_8 (not_8_out, Input_2);
  not not_9 (not_9_out, Input_2);
  not not_10 (not_10_out, Input_6);
  not not_11 (not_11_out, Input_4);
  not not_12 (not_12_out, Input_5);
  not not_13 (not_13_out, Input_4);
  not not_14 (not_14_out, Input_2);
  not not_15 (not_15_out, Input_3);
  not not_16 (not_16_out, Input_5);
  not not_17 (not_17_out, Input_6);
  not not_18 (not_18_out, Input_2);
  not not_19 (not_19_out, Input_4);
  not not_20 (not_20_out, Input_6);
  not not_21 (not_21_out, Input_3);
  not not_22 (not_22_out, Input_4);
  not not_23 (not_23_out, Input_2);
  not not_24 (not_24_out, Input_3);
  not not_25 (not_25_out, Input_4);
  not not_26 (not_26_out, Input_5);
  not not_27 (not_27_out, Input_2);
  not not_28 (not_28_out, Input_5);
  not not_29 (not_29_out, Input_3);
  not not_30 (not_30_out, Input_5);
  not not_31 (not_31_out, Input_6);
  not not_32 (not_32_out, Input_3);
  not not_33 (not_33_out, Input_4);
  not not_34 (not_34_out, Input_5);
  not not_35 (not_35_out, Input_3);
  not not_36 (not_36_out, Input_4);
  not not_37 (not_37_out, Input_5);
  not not_38 (not_38_out, Input_2);
  not not_39 (not_39_out, Input_3);
  not not_40 (not_40_out, Input_2);
  not not_41 (not_41_out, Input_4);
  not not_42 (not_42_out, Input_6);
  not not_43 (not_43_out, Input_2);
  not not_44 (not_44_out, Input_3);
  not not_45 (not_45_out, Input_4);
  not not_46 (not_46_out, Input_6);
  not not_47 (not_47_out, Input_2);
  not not_48 (not_48_out, Input_3);
  not not_49 (not_49_out, Input_6);
  not not_50 (not_50_out, Input_4);
  not not_51 (not_51_out, Input_2);
  not not_52 (not_52_out, Input_5);
  not not_53 (not_53_out, Input_2);
  not not_54 (not_54_out, Input_5);
  not not_55 (not_55_out, Input_5);
  not not_56 (not_56_out, Input_6);
  not not_57 (not_57_out, Input_3);
  not not_58 (not_58_out, Input_5);
  not not_59 (not_59_out, Input_6);
  not not_60 (not_60_out, Input_3);
  not not_61 (not_61_out, Input_4);
  not not_62 (not_62_out, Input_6);
  not not_63 (not_63_out, Input_2);
  not not_64 (not_64_out, Input_6);
  not not_65 (not_65_out, Input_2);
  not not_66 (not_66_out, Input_5);
  not not_67 (not_67_out, Input_3);
  not not_68 (not_68_out, Input_5);
  not not_69 (not_69_out, Input_3);
  not not_70 (not_70_out, Input_5);
  not not_71 (not_71_out, Input_6);
  not not_72 (not_72_out, Input_2);
  not not_73 (not_73_out, Input_6);
  not not_74 (not_74_out, Input_3);
  not not_75 (not_75_out, Input_5);
  not not_76 (not_76_out, Input_4);
  not not_77 (not_77_out, Input_2);
  not not_78 (not_78_out, Input_6);
  not not_79 (not_79_out, Input_3);
  not not_80 (not_80_out, Input_4);
  not not_81 (not_81_out, Input_6);
  not not_82 (not_82_out, Input_3);
  not not_83 (not_83_out, Input_5);
  not not_84 (not_84_out, Input_2);
  not not_85 (not_85_out, Input_4);
  not not_86 (not_86_out, Input_2);
  not not_87 (not_87_out, Input_6);
  not not_88 (not_88_out, Input_2);
  not not_89 (not_89_out, Input_3);
  not not_90 (not_90_out, Input_5);
  not not_91 (not_91_out, Input_4);
  not not_92 (not_92_out, Input_2);
  not not_93 (not_93_out, Input_4);
  not not_94 (not_94_out, Input_5);
  not not_95 (not_95_out, Input_3);
  not not_96 (not_96_out, Input_6);
  and and_1 (and_1_out, not_1_out, not_2_out, not_3_out);
  and and_2 (and_2_out, not_4_out, not_5_out, Input_5);
  and and_3 (and_3_out, not_6_out, Input_4, not_7_out, Input_6);
  and and_4 (and_4_out, not_8_out, Input_4, Input_5);
  and and_5 (and_5_out, not_9_out, Input_3, not_10_out);
  and and_6 (and_6_out, Input_3, not_11_out, not_12_out);
  and and_7 (and_7_out, Input_2, Input_3, not_13_out, Input_6);
  and and_8 (and_8_out, not_14_out, not_15_out, not_16_out, not_17_out);
  and and_9 (and_9_out, not_18_out, not_19_out, not_20_out);
  and and_10 (and_10_out, not_21_out, not_22_out, Input_6);
  and and_11 (and_11_out, not_23_out, not_24_out, Input_5, Input_6);
  and and_12 (and_12_out, Input_3, not_25_out, not_26_out);
  and and_13 (and_13_out, not_27_out, Input_3, not_28_out, Input_6);
  and and_14 (and_14_out, Input_2, not_29_out, not_30_out, Input_6);
  and and_15 (and_15_out, Input_2, Input_3, Input_4, Input_5, not_31_out);
  and and_16 (and_16_out, not_32_out, not_33_out, not_34_out);
  and and_17 (and_17_out, not_35_out, Input_6);
  and and_18 (and_18_out, not_36_out, Input_6);
  and and_19 (and_19_out, not_37_out, Input_6);
  and and_20 (and_20_out, not_38_out, not_39_out, Input_4);
  and and_21 (and_21_out, not_40_out, Input_3, not_41_out);
  and and_22 (and_22_out, Input_2, Input_4, Input_5, not_42_out);
  and and_23 (and_23_out, not_43_out, not_44_out, not_45_out, not_46_out);
  and and_24 (and_24_out, not_47_out, not_48_out, Input_5, not_49_out);
  and and_25 (and_25_out, not_50_out, Input_5, Input_6);
  and and_26 (and_26_out, not_51_out, Input_4, not_52_out, Input_6);
  and and_27 (and_27_out, not_53_out, Input_3, not_54_out);
  and and_28 (and_28_out, Input_3, Input_4, not_55_out);
  and and_29 (and_29_out, Input_3, Input_4, not_56_out);
  and and_30 (and_30_out, Input_2, not_57_out, not_58_out, not_59_out);
  and and_31 (and_31_out, Input_2, not_60_out, Input_5, Input_6);
  and and_32 (and_32_out, not_61_out, not_62_out);
  and and_33 (and_33_out, not_63_out, Input_5, not_64_out);
  and and_34 (and_34_out, not_65_out, Input_3, Input_5);
  and and_35 (and_35_out, Input_3, Input_4, not_66_out);
  and and_36 (and_36_out, Input_2, not_67_out, not_68_out);
  and and_37 (and_37_out, Input_2, not_69_out, Input_4);
  and and_38 (and_38_out, not_70_out, not_71_out);
  and and_39 (and_39_out, not_72_out, Input_4, not_73_out);
  and and_40 (and_40_out, not_74_out, Input_4, not_75_out);
  and and_41 (and_41_out, Input_3, not_76_out, Input_6);
  and and_42 (and_42_out, not_77_out, Input_3, Input_5);
  and and_43 (and_43_out, Input_3, Input_4, not_78_out);
  and and_44 (and_44_out, Input_2, not_79_out, not_80_out, not_81_out);
  and and_45 (and_45_out, Input_2, not_82_out, not_83_out);
  and and_46 (and_46_out, not_84_out, not_85_out, Input_5);
  and and_47 (and_47_out, not_86_out, Input_5, not_87_out);
  and and_48 (and_48_out, not_88_out, not_89_out, Input_4, not_90_out);
  and and_49 (and_49_out, Input_3, not_91_out);
  and and_50 (and_50_out, not_92_out, Input_3, Input_6);
  and and_51 (and_51_out, Input_2, not_93_out, not_94_out, Input_6);
  and and_52 (and_52_out, Input_2, not_95_out, Input_4, Input_5);
  and and_53 (and_53_out, Input_2, Input_3, not_96_out);
  or or_1 (Output_2, and_1_out, and_2_out, and_3_out, and_4_out, and_5_out, and_6_out, and_7_out);
  or or_2 (Output_3, and_8_out, and_9_out, and_10_out, and_11_out, and_12_out, and_13_out, and_14_out, and_15_out);
  or or_3 (Output_4, and_16_out, and_17_out, and_18_out, and_19_out, and_20_out, and_21_out, and_22_out);
  or or_4 (Output_5, and_23_out, and_24_out, and_25_out, and_26_out, and_27_out, and_28_out, and_29_out, and_30_out, and_31_out);
  or or_5 (Output_6, and_32_out, and_33_out, and_34_out, and_35_out, and_36_out, and_37_out);
  or or_6 (Output_7, and_38_out, and_39_out, and_40_out, and_41_out, and_42_out, and_43_out, and_44_out, and_45_out);
  or or_7 (Output_8, and_46_out, and_47_out, and_48_out, and_49_out, and_50_out, and_51_out, and_52_out, and_53_out);

  assign Output_1 = Input_1;
endmodule

module SegLed1_bis (
  input  [7:0] Input_bus_1,
  output [7:0] Output_bus_1
);

  DecoderToSegLed_bis DecoderToSegLed_bis_1 (
    .Input_1(Input_bus_1[7]), .Input_2(Input_bus_1[4]), .Input_3(Input_bus_1[3]), .Input_4(Input_bus_1[2]),
    .Input_5(Input_bus_1[1]), .Input_6(Input_bus_1[0]), .Output_1(Output_bus_1[7]),
    .Output_2(Output_bus_1[6]), .Output_3(Output_bus_1[5]), .Output_4(Output_bus_1[4]),
    .Output_5(Output_bus_1[3]), .Output_6(Output_bus_1[2]), .Output_7(Output_bus_1[1]),
    .Output_8(Output_bus_1[0]));
endmodule

module AllsegLeds_bis (
  input  [7:0] Input_bus_1,
  input  [7:0] Input_bus_2,
  input  [7:0] Input_bus_3,
  input  [7:0] Input_bus_4,
  input  [7:0] Input_bus_5,
  input  [7:0] Input_bus_6,
  output [7:0] Output_bus_1,
  output [7:0] Output_bus_2,
  output [7:0] Output_bus_3,
  output [7:0] Output_bus_4,
  output [7:0] Output_bus_5,
  output [7:0] Output_bus_6
);

  SegLed1_bis SegLed1_bis_1 (.Input_bus_1(Input_bus_1), .Output_bus_1(Output_bus_1));
  SegLed1_bis SegLed1_bis_2 (.Input_bus_1(Input_bus_2), .Output_bus_1(Output_bus_2));
  SegLed1_bis SegLed1_bis_3 (.Input_bus_1(Input_bus_3), .Output_bus_1(Output_bus_3));
  SegLed1_bis SegLed1_bis_4 (.Input_bus_1(Input_bus_4), .Output_bus_1(Output_bus_4));
  SegLed1_bis SegLed1_bis_5 (.Input_bus_1(Input_bus_5), .Output_bus_1(Output_bus_5));
  SegLed1_bis SegLed1_bis_6 (.Input_bus_1(Input_bus_6), .Output_bus_1(Output_bus_6));
endmodule

module clk2k_to_4 (
  input  CLK2k,
  output CLK4
);

  wire d_ff_1_q, d_ff_1_qn, d_ff_2_q, d_ff_2_qn, d_ff_3_q, d_ff_3_qn, d_ff_4_q, d_ff_4_qn, d_ff_5_q,
       d_ff_5_qn, d_ff_6_q, d_ff_6_qn, d_ff_7_q, d_ff_7_qn, d_ff_8_q, d_ff_8_qn, d_ff_9_qn;

  D_Flip_Flop d_ff_1 (.D(d_ff_1_qn), .clk(CLK2k), .Q(d_ff_1_q), .Qn(d_ff_1_qn));  // open: preset, reset
  D_Flip_Flop d_ff_2 (.D(d_ff_2_qn), .clk(d_ff_1_q), .Q(d_ff_2_q), .Qn(d_ff_2_qn));  // open: preset, reset
  D_Flip_Flop d_ff_3 (.D(d_ff_3_qn), .clk(d_ff_2_q), .Q(d_ff_3_q), .Qn(d_ff_3_qn));  // open: preset, reset
  D_Flip_Flop d_ff_4 (.D(d_ff_4_qn), .clk(d_ff_3_q), .Q(d_ff_4_q), .Qn(d_ff_4_qn));  // open: preset, reset
  D_Flip_Flop d_ff_5 (.D(d_ff_5_qn), .clk(d_ff_4_q), .Q(d_ff_5_q), .Qn(d_ff_5_qn));  // open: preset, reset
  D_Flip_Flop d_ff_6 (.D(d_ff_6_qn), .clk(d_ff_5_q), .Q(d_ff_6_q), .Qn(d_ff_6_qn));  // open: preset, reset
  D_Flip_Flop d_ff_7 (.D(d_ff_7_qn), .clk(d_ff_6_q), .Q(d_ff_7_q), .Qn(d_ff_7_qn));  // open: preset, reset
  D_Flip_Flop d_ff_8 (.D(d_ff_8_qn), .clk(d_ff_7_q), .Q(d_ff_8_q), .Qn(d_ff_8_qn));  // open: preset, reset
  D_Flip_Flop d_ff_9 (.D(d_ff_9_qn), .clk(d_ff_8_q), .Q(CLK4), .Qn(d_ff_9_qn));  // open: preset, reset
endmodule
