// Logisim project MAIN.circ as structural Verilog: 10 circuits, main circuit MAIN
module MAIN (
);

  wire A_out, al, B_out, buttons_1_double, clock_1_out, DipSwitch_1_sw1, DipSwitch_1_sw2,
       led_board_1_output_1, led_board_1_output_2, led_board_1_output_3, led_board_1_output_4,
       led_board_1_output_5, led_board_1_output_6, led_board_1_output_7, led_board_1_output_8,
       led_board_1_output_9, led_board_1_output_10, off, or_1_out, or_2_out, SS1_a, SS1_b, SS1_c, SS1_d,
       SS1_e, SS1_f, SS1_g, SS_0_a, SS_0_b, SS_0_c, SS_0_d, SS_0_e, SS_0_f, SS_0_g, SS_2_a, SS_2_b, SS_2_c,
       SS_2_d, SS_2_e, SS_2_f, SS_2_g, SS_3_a, SS_3_b, SS_3_c, SS_3_d, SS_3_e, SS_3_f, SS_3_g, SS_4_a,
       SS_4_b, SS_4_c, SS_4_d, SS_4_e, SS_4_f, SS_4_g, SS_5_a, SS_5_b, SS_5_c, SS_5_d, SS_5_e, SS_5_f,
       SS_5_g, TIME_SET_1_set_on;
  wire [1:0] buttons_1_single_a, demultiplexer_1_out0, demultiplexer_1_out1, m0, m1, m2, m3, m4;
  wire [2:0] n5_modes_1_mode;
  wire [3:0] TIME_SET_1_d_dotm, TIME_SET_1_d_hour, TIME_SET_1_d_minut, TIME_SET_1_d_month,
       TIME_SET_1_d_second, TIME_SET_1_dotw, TIME_SET_1_u_dotm, TIME_SET_1_u_hour, TIME_SET_1_u_minut,
       TIME_SET_1_u_month, TIME_SET_1_u_second;
  wire [4:0] demultiplexer_3_out0, multiplexer_1_out;
  wire [4:1] TIME_KEEP_1_am;
  wire [6:0] alarme_1_a0, alarme_1_a1, alarme_1_a2, alarme_1_a3, alarme_1_a4, alarme_1_a5, CHRONO_1_a0,
       CHRONO_1_a1, CHRONO_1_a2, CHRONO_1_a3, CHRONO_1_a4, CHRONO_1_a5, compte_ar_1_a0, compte_ar_1_a1,
       compte_ar_1_a2, compte_ar_1_a3, compte_ar_1_a4, compte_ar_1_a5, plex_disp_1_a0, plex_disp_1_a1,
       plex_disp_1_a2, plex_disp_1_a3, plex_disp_1_a4, plex_disp_1_a5, TIME_KEEP_1_a0, TIME_KEEP_1_a1,
       TIME_KEEP_1_a2, TIME_KEEP_1_a3, TIME_KEEP_1_a4, TIME_KEEP_1_a5, TIME_SET_1_a0, TIME_SET_1_a1,
       TIME_SET_1_a2, TIME_SET_1_a3, TIME_SET_1_a4, TIME_SET_1_a5;
  wire [7:0] TIME_KEEP_1_current_hour, TIME_KEEP_1_current_minut, TIME_KEEP_1_current_second;
  wire [9:0] alarme_1_led_alarm, multiplexer_2_out;

  DipSwitch #(.number(2)) DipSwitch_1 (.sw1(DipSwitch_1_sw1), .sw2(DipSwitch_1_sw2));
  or or_1 (or_1_out, DipSwitch_1_sw2, A_out);
  Button A (.out(A_out));
  Button B (.out(B_out));
  or or_2 (or_2_out, B_out, DipSwitch_1_sw2);
  Clock clock_1 (.out(clock_1_out));
  CHRONO CHRONO_1 (
    .AB(m2), .Clk(clock_1_out), .PoR(DipSwitch_1_sw1), .A5(CHRONO_1_a5), .A4(CHRONO_1_a4), .A3(CHRONO_1_a3),
    .A2(CHRONO_1_a2), .A1(CHRONO_1_a1), .A0(CHRONO_1_a0));
  COUNTDOWN compte_ar_1 (
    .AB(m4), .PoR(DipSwitch_1_sw1), .Clk(clock_1_out), .A5(compte_ar_1_a5), .A4(compte_ar_1_a4),
    .A3(compte_ar_1_a3), .A2(compte_ar_1_a2), .A1(compte_ar_1_a1), .A0(compte_ar_1_a0));
  buttons buttons_1 (
    .A(or_1_out), .B(or_2_out), .Clk(clock_1_out), .PoR(DipSwitch_1_sw1), .single_A(buttons_1_single_a[0]),
    .single_B(buttons_1_single_a[1]), .double(buttons_1_double));
  TIME_SET TIME_SET_1 (
    .AB(m3), .PoR(DipSwitch_1_sw1), .Clk(clock_1_out), .set_on(TIME_SET_1_set_on),
    .D_month(TIME_SET_1_d_month), .U_month(TIME_SET_1_u_month), .dotw(TIME_SET_1_dotw),
    .D_dotm(TIME_SET_1_d_dotm), .U_dotm(TIME_SET_1_u_dotm), .D_hour(TIME_SET_1_d_hour),
    .U_hour(TIME_SET_1_u_hour), .D_minut(TIME_SET_1_d_minut), .U_minut(TIME_SET_1_u_minut),
    .D_second(TIME_SET_1_d_second), .U_second(TIME_SET_1_u_second), .A5(TIME_SET_1_a5), .A4(TIME_SET_1_a4),
    .A3(TIME_SET_1_a3), .A2(TIME_SET_1_a2), .A1(TIME_SET_1_a1), .A0(TIME_SET_1_a0));
  Demultiplexer #(.width(2), .enable("false")) demultiplexer_1 (
    .out0(demultiplexer_1_out0), .out1(demultiplexer_1_out1), .in(buttons_1_single_a), .sel(al));
  TIME_KEEP TIME_KEEP_1 (
    .Clk(clock_1_out), .PoR(DipSwitch_1_sw1), .AB(m0), .D_month(TIME_SET_1_d_month),
    .U_month(TIME_SET_1_u_month), .dotw(TIME_SET_1_dotw), .D_dotm(TIME_SET_1_d_dotm),
    .U_dotm(TIME_SET_1_u_dotm), .D_hour(TIME_SET_1_d_hour), .U_hour(TIME_SET_1_u_hour),
    .D_minut(TIME_SET_1_d_minut), .U_minut(TIME_SET_1_u_minut), .D_second(TIME_SET_1_d_second),
    .U_second(TIME_SET_1_u_second), .set_on(TIME_SET_1_set_on), .A5(TIME_KEEP_1_a5), .A4(TIME_KEEP_1_a4),
    .A3(TIME_KEEP_1_a3), .A2(TIME_KEEP_1_a2), .A1(TIME_KEEP_1_a1), .A0(TIME_KEEP_1_a0),
    .current_hour(TIME_KEEP_1_current_hour), .current_minut(TIME_KEEP_1_current_minut),
    .current_second(TIME_KEEP_1_current_second), .AM(TIME_KEEP_1_am[1]), .PM(TIME_KEEP_1_am[2]));
  ALARM alarme_1 (
    .current_hour(TIME_KEEP_1_current_hour), .current_minut(TIME_KEEP_1_current_minut),
    .current_second(TIME_KEEP_1_current_second), .AB(m1), .PoR(DipSwitch_1_sw1), .Clk(clock_1_out),
    .off(off), .led_alarm(alarme_1_led_alarm), .alarm_ding(al), .alarm_on(TIME_KEEP_1_am[4]),
    .A5(alarme_1_a5), .A4(alarme_1_a4), .A3(alarme_1_a3), .A2(alarme_1_a2), .A1(alarme_1_a1), .A0(alarme_1_a0));
  or or_3 (off, demultiplexer_1_out1[0], demultiplexer_1_out1[1]);
  n5_modes n5_modes_1 (.B(buttons_1_double), .PoR(DipSwitch_1_sw1), .Clk(clock_1_out), .mode(n5_modes_1_mode));
  plex_disp plex_disp_1 (
    .mode(n5_modes_1_mode), .m0_A5(TIME_KEEP_1_a5), .m0_A4(TIME_KEEP_1_a4), .m0_A3(TIME_KEEP_1_a3),
    .m0_A2(TIME_KEEP_1_a2), .m0_A1(TIME_KEEP_1_a1), .m0_A0(TIME_KEEP_1_a0), .m1_A5(alarme_1_a5),
    .m1_A4(alarme_1_a4), .m1_A3(alarme_1_a3), .m1_A2(alarme_1_a2), .m1_A1(alarme_1_a1), .m1_A0(alarme_1_a0),
    .m2_A5(CHRONO_1_a5), .m2_A4(CHRONO_1_a4), .m2_A3(CHRONO_1_a3), .m2_A2(CHRONO_1_a2), .m2_A1(CHRONO_1_a1),
    .m2_A0(CHRONO_1_a0), .m3_A5(TIME_SET_1_a5), .m3_A4(TIME_SET_1_a4), .m3_A3(TIME_SET_1_a3),
    .m3_A2(TIME_SET_1_a2), .m3_A1(TIME_SET_1_a1), .m3_A0(TIME_SET_1_a0), .m4_A5(compte_ar_1_a5),
    .m4_A4(compte_ar_1_a4), .m4_A3(compte_ar_1_a3), .m4_A2(compte_ar_1_a2), .m4_A1(compte_ar_1_a1),
    .m4_A0(compte_ar_1_a0), .A5(plex_disp_1_a5), .A4(plex_disp_1_a4), .A3(plex_disp_1_a3),
    .A2(plex_disp_1_a2), .A1(plex_disp_1_a1), .A0(plex_disp_1_a0));
  _7_Segment_Display L_7_Segment_Display_1 (
    .g(SS_0_g), .f(SS_0_f), .a(SS_0_a), .b(SS_0_b), .e(SS_0_e), .d(SS_0_d), .c(SS_0_c));  // open: dp
  Demultiplexer #(.select(3), .width(2), .enable("false")) demultiplexer_2 (
    .out0(m0), .out1(m1), .out2(m2), .out3(m3), .out4(m4), .in(demultiplexer_1_out0), .sel(n5_modes_1_mode));  // open: out5, out6, out7
  _7_Segment_Display L_7_Segment_Display_3 (
    .g(SS_2_g), .f(SS_2_f), .a(SS_2_a), .b(SS_2_b), .e(SS_2_e), .d(SS_2_d), .c(SS_2_c));  // open: dp
  _7_Segment_Display L_7_Segment_Display_2 (
    .g(SS1_g), .f(SS1_f), .a(SS1_a), .b(SS1_b), .e(SS1_e), .d(SS1_d), .c(SS1_c));  // open: dp
  sept_segment SS1 (
    .E(SS1_e), .F(SS1_f), .D(SS1_d), .C(SS1_c), .B(SS1_b), .A(SS1_a), .Input_bus_1(plex_disp_1_a4), .G(SS1_g));
  sept_segment SS_0 (
    .E(SS_0_e), .F(SS_0_f), .D(SS_0_d), .C(SS_0_c), .B(SS_0_b), .A(SS_0_a), .Input_bus_1(plex_disp_1_a5),
    .G(SS_0_g));
  _7_Segment_Display L_7_Segment_Display_4 (
    .g(SS_3_g), .f(SS_3_f), .a(SS_3_a), .b(SS_3_b), .e(SS_3_e), .d(SS_3_d), .c(SS_3_c));  // open: dp
  sept_segment SS_2 (
    .E(SS_2_e), .F(SS_2_f), .D(SS_2_d), .C(SS_2_c), .B(SS_2_b), .A(SS_2_a), .Input_bus_1(plex_disp_1_a3),
    .G(SS_2_g));
  sept_segment SS_3 (
    .E(SS_3_e), .F(SS_3_f), .D(SS_3_d), .C(SS_3_c), .B(SS_3_b), .A(SS_3_a), .Input_bus_1(plex_disp_1_a2),
    .G(SS_3_g));
  Demultiplexer #(.select(3), .enable("false")) demultiplexer_3 (
    .out0(demultiplexer_3_out0[0]), .out1(demultiplexer_3_out0[1]), .out2(demultiplexer_3_out0[2]),
    .out3(demultiplexer_3_out0[3]), .out4(demultiplexer_3_out0[4]), .in(1'b1), .sel(n5_modes_1_mode));  // open: out5, out6, out7
  _7_Segment_Display L_7_Segment_Display_5 (
    .g(SS_4_g), .f(SS_4_f), .a(SS_4_a), .b(SS_4_b), .e(SS_4_e), .d(SS_4_d), .c(SS_4_c));  // open: dp
  _7_Segment_Display L_7_Segment_Display_6 (
    .g(SS_5_g), .f(SS_5_f), .a(SS_5_a), .b(SS_5_b), .e(SS_5_e), .d(SS_5_d), .c(SS_5_c));  // open: dp
  sept_segment SS_4 (
    .E(SS_4_e), .F(SS_4_f), .D(SS_4_d), .C(SS_4_c), .B(SS_4_b), .A(SS_4_a), .Input_bus_1(plex_disp_1_a1),
    .G(SS_4_g));
  sept_segment SS_5 (
    .E(SS_5_e), .F(SS_5_f), .D(SS_5_d), .C(SS_5_c), .B(SS_5_b), .A(SS_5_a), .Input_bus_1(plex_disp_1_a0),
    .G(SS_5_g));
  Multiplexer #(.select(3), .width(5), .enable("false")) multiplexer_1 (
    .in0({TIME_KEEP_1_am[4], 1'b0, TIME_KEEP_1_am[2:1], 1'b0}), .in1({TIME_KEEP_1_am[4], 4'b0000}),
    .in2({TIME_KEEP_1_am[4], 4'b0000}), .in3({TIME_KEEP_1_am[4], 4'b0000}),
    .in4({TIME_KEEP_1_am[4], 4'b0000}), .out(multiplexer_1_out), .sel(n5_modes_1_mode));  // open: in5, in6, in7
  led_board led_board_1 (
    .Output_7(led_board_1_output_7), .Output_8(led_board_1_output_8), .Output_6(led_board_1_output_6),
    .Output_5(led_board_1_output_5), .Output_4(led_board_1_output_4), .Output_3(led_board_1_output_3),
    .Output_2(led_board_1_output_2), .Output_1(led_board_1_output_1), .Input_bus_1(multiplexer_2_out),
    .Output_9(led_board_1_output_9), .Output_10(led_board_1_output_10));
  LED led_0 (.in(led_board_1_output_1));
  Multiplexer #(.width(10), .enable("false")) multiplexer_2 (
    .in0({multiplexer_1_out, demultiplexer_3_out0}), .in1(alarme_1_led_alarm), .out(multiplexer_2_out),
    .sel(al));
  LED led_3 (.in(led_board_1_output_4));
  LED led_4 (.in(led_board_1_output_5));
  LED led_2 (.in(led_board_1_output_3));
  LED led_1 (.in(led_board_1_output_2));
  LED led_7 (.in(led_board_1_output_8));
  LED led_5 (.in(led_board_1_output_6));
  LED led_6 (.in(led_board_1_output_7));
  LED led_8 (.in(led_board_1_output_9));
  LED led_9 (.in(led_board_1_output_10));

  // Notes on the sheet:
  //   PoR
endmodule

module TIME_KEEP (
  input  Clk,
  input  PoR,
  input  [1:0] AB,
  input  [3:0] D_month,
  input  [3:0] U_month,
  input  [3:0] dotw,
  input  [3:0] D_dotm,
  input  [3:0] U_dotm,
  input  [3:0] D_hour,
  input  [3:0] U_hour,
  input  [3:0] D_minut,
  input  [3:0] U_minut,
  input  [3:0] D_second,
  input  [3:0] U_second,
  input  set_on,
  output [6:0] A5,
  output [6:0] A4,
  output [6:0] A3,
  output [6:0] A2,
  output [6:0] A1,
  output [6:0] A0,
  output [7:0] current_hour,
  output [7:0] current_minut,
  output [7:0] current_second,
  output AM,
  output PM
);

  wire demultiplexer_3_out0, demultiplexer_3_out1, demultiplexer_3_out2, one_thirty_1_o, one_thirtyone_1_o,
       one_twentyeight_1_o, or_1_out, or_2_out, or_3_out, or_4_out, pulse, selct_reset_1_r0,
       selct_reset_1_r1, selct_reset_1_r2, switch_01_1_s, swiyth_01_2_s, zero_fiftynine_1_o,
       zero_fiftynine_2_o, zero_twetythree_1_o;
  wire [1:0] month_select_1_s0, months_1_output_bus_1;
  wire [3:0] demultiplexer_1_out0, demultiplexer_1_out1, demultiplexer_1_out2, demultiplexer_2_out0,
       demultiplexer_2_out1, demultiplexer_2_out2, gestion_US_1_d, gestion_US_1_u, mon_sun_1_d0,
       mon_sun_1_d1, months_1_mo0, months_1_mo1, multiplexer_1_out, multiplexer_2_out, one_thirty_1_n0,
       one_thirty_1_n1, one_thirtyone_1_n0, one_thirtyone_1_n1, one_twentyeight_1_n0, one_twentyeight_1_n1;
  wire [6:0] disp_ltr_1_s, disp_ltr_2_s, disp_nbr_1_s, disp_nbr_2_s, disp_nbr_3_s, disp_nbr_4_s,
       disp_nbr_5_s, disp_nbr_6_s, disp_nbr_7_s, disp_nbr_8_s, disp_nbr_9_s, disp_nbr_10_s;

  or or_1 (or_1_out, PoR, selct_reset_1_r2);
  or or_2 (or_2_out, PoR, selct_reset_1_r1);
  or or_3 (or_3_out, PoR, selct_reset_1_r0);
  month_select month_select_1 (
    .E4(D_month[0]), .E3(U_month[3]), .E2(U_month[2]), .E1(U_month[1]), .E0(U_month[0]),
    .S1(month_select_1_s0[1]), .S0(month_select_1_s0[0]));
  switch_01 switch_01_1 (.E(AB[0]), .PoR(PoR), .S(switch_01_1_s));
  Demultiplexer #(.select(2), .width(4), .enable("false")) demultiplexer_1 (
    .out0(demultiplexer_1_out0), .out1(demultiplexer_1_out1), .out2(demultiplexer_1_out2), .in(D_dotm),
    .sel(month_select_1_s0));  // open: out3
  Demultiplexer #(.select(2), .width(4), .enable("false")) demultiplexer_2 (
    .out0(demultiplexer_2_out0), .out1(demultiplexer_2_out1), .out2(demultiplexer_2_out2), .in(U_dotm),
    .sel(month_select_1_s0));  // open: out3
  Demultiplexer #(.select(2), .enable("false")) demultiplexer_3 (
    .out0(demultiplexer_3_out0), .out1(demultiplexer_3_out1), .out2(demultiplexer_3_out2),
    .in(zero_twetythree_1_o), .sel(months_1_output_bus_1));  // open: out3
  mon_sun mon_sun_1 (
    .Oi(zero_twetythree_1_o), .set_days(dotw), .set_on(set_on), .Clk(Clk), .PoR(PoR), .D1(mon_sun_1_d1),
    .D0(mon_sun_1_d0));  // open: O
  zero_fiftynine zero_fiftynine_2 (
    .Oi(zero_fiftynine_1_o), .set_D(D_minut), .set_D_on(set_on), .set_U(U_minut), .set_U_on(set_on),
    .Clk(Clk), .PoR(PoR), .O(zero_fiftynine_2_o), .D(current_minut[7:4]), .U(current_minut[3:0]));
  zero_fiftynine zero_fiftynine_1 (
    .Oi(pulse), .set_D(D_second), .set_D_on(set_on), .set_U(U_second), .set_U_on(set_on), .Clk(Clk),
    .PoR(PoR), .O(zero_fiftynine_1_o), .D(current_second[7:4]), .U(current_second[3:0]));
  switch_01 swiyth_01_2 (.E(AB[1]), .PoR(PoR), .S(swiyth_01_2_s));
  zero_twentythree zero_twetythree_1 (
    .Oi(zero_fiftynine_2_o), .set_D(D_hour), .set_D_on(set_on), .set_U(U_hour), .set_U_on(set_on), .Clk(Clk),
    .PoR(PoR), .O(zero_twetythree_1_o), .D(current_hour[7:4]), .U(current_hour[3:0]));
  select_reset_month selct_reset_1 (
    .R(set_on), .E1(month_select_1_s0[1]), .E0(month_select_1_s0[0]), .R2(selct_reset_1_r2),
    .R1(selct_reset_1_r1), .R0(selct_reset_1_r0));
  months months_1 (
    .Oi(or_4_out), .set_D(D_month), .set_D_on(set_on), .set_U(U_month), .set_U_on(set_on), .Clk(Clk),
    .PoR(PoR), .Mo1(months_1_mo1), .Mo0(months_1_mo0), .Output_bus_1(months_1_output_bus_1));
  one_thirtyone one_thirtyone_1 (
    .Oi(demultiplexer_3_out0), .set_D(demultiplexer_1_out0), .set_D_on(set_on), .set_U(demultiplexer_2_out0),
    .set_U_on(set_on), .Clk(Clk), .PoR(or_1_out), .O(one_thirtyone_1_o), .N1(one_thirtyone_1_n1),
    .N0(one_thirtyone_1_n0));
  one_thirty one_thirty_1 (
    .Oi(demultiplexer_3_out1), .set_D(demultiplexer_1_out1), .set_D_on(set_on), .set_U(demultiplexer_2_out1),
    .set_U_on(set_on), .Clk(Clk), .PoR(or_2_out), .O(one_thirty_1_o), .N1(one_thirty_1_n1),
    .N0(one_thirty_1_n0));
  one_twentyeight one_twentyeight_1 (
    .Oi(demultiplexer_3_out2), .set_D(demultiplexer_1_out2), .set_D_on(set_on), .set_U(demultiplexer_2_out2),
    .set_U_on(set_on), .Clk(Clk), .PoR(or_3_out), .O(one_twentyeight_1_o), .N1(one_twentyeight_1_n1),
    .N0(one_twentyeight_1_n0));
  or or_4 (or_4_out, one_twentyeight_1_o, one_thirty_1_o, one_thirtyone_1_o);
  frequ_sec frequ_sec_1 (.PoR(PoR), .Clk(Clk), .pulse(pulse));
  disp_nbr disp_nbr_1 (.E(months_1_mo1), .S(disp_nbr_1_s));
  disp_nbr disp_nbr_2 (.E(months_1_mo0), .S(disp_nbr_2_s));
  Multiplexer #(.select(2), .width(4), .enable("false")) multiplexer_1 (
    .in0(one_thirtyone_1_n1), .in1(one_thirty_1_n1), .in2(one_twentyeight_1_n1), .out(multiplexer_1_out),
    .sel(months_1_output_bus_1));  // open: in3
  Multiplexer #(.select(2), .width(4), .enable("false")) multiplexer_2 (
    .in0(one_thirtyone_1_n0), .in1(one_thirty_1_n0), .in2(one_twentyeight_1_n0), .out(multiplexer_2_out),
    .sel(months_1_output_bus_1));  // open: in3
  disp_ltr disp_ltr_1 (.S(disp_ltr_1_s), .E(mon_sun_1_d1));
  disp_ltr disp_ltr_2 (.S(disp_ltr_2_s), .E(mon_sun_1_d0));
  gestion_US gestion_US_1 (
    .D_in(current_hour[7:4]), .U_in(current_hour[3:0]), .US_mode(switch_01_1_s), .D(gestion_US_1_d),
    .U(gestion_US_1_u), .AM(AM), .PM(PM));
  disp_nbr disp_nbr_3 (.E(multiplexer_1_out), .S(disp_nbr_3_s));
  disp_nbr disp_nbr_4 (.E(multiplexer_2_out), .S(disp_nbr_4_s));
  disp_nbr disp_nbr_5 (.E(gestion_US_1_d), .S(disp_nbr_5_s));
  disp_nbr disp_nbr_6 (.E(gestion_US_1_u), .S(disp_nbr_6_s));
  disp_nbr disp_nbr_7 (.E(current_minut[7:4]), .S(disp_nbr_7_s));
  disp_nbr disp_nbr_8 (.E(current_minut[3:0]), .S(disp_nbr_8_s));
  disp_nbr disp_nbr_9 (.E(current_second[7:4]), .S(disp_nbr_9_s));
  disp_nbr disp_nbr_10 (.E(current_second[3:0]), .S(disp_nbr_10_s));
  Multiplexer #(.width(14), .enable("false")) multiplexer_3 (
    .in0({disp_nbr_7_s, disp_nbr_8_s}), .in1({disp_ltr_1_s, disp_ltr_2_s}), .out({A3, A2}),
    .sel(swiyth_01_2_s));
  Multiplexer #(.width(14), .enable("false")) multiplexer_4 (
    .in0({disp_nbr_9_s, disp_nbr_10_s}), .in1({disp_nbr_3_s, disp_nbr_4_s}), .out({A1, A0}),
    .sel(swiyth_01_2_s));
  Multiplexer #(.width(14), .enable("false")) multiplexer_5 (
    .in0({disp_nbr_5_s, disp_nbr_6_s}), .in1({disp_nbr_1_s, disp_nbr_2_s}), .out({A5, A4}),
    .sel(swiyth_01_2_s));

  // Other names for the same wires on the sheet: c = Clk; p = PoR
endmodule

module ALARM (
  input  [7:0] current_hour,
  input  [7:0] current_minut,
  input  [7:0] current_second,
  input  [1:0] AB,
  input  PoR,
  input  Clk,
  input  off,
  output [9:0] led_alarm,
  output alarm_ding,
  output alarm_on,
  output [6:0] A5,
  output [6:0] A4,
  output [6:0] A3,
  output [6:0] A2,
  output [6:0] A1,
  output [6:0] A0
);

  wire and_1_out, comparator_1_eq, comparator_2_eq, comparator_3_eq, demultiplexer_1_out0,
       demultiplexer_1_out1, demultiplexer_1_out2, demultiplexer_1_out3, demultiplexer_2_out0,
       demultiplexer_2_out1, demultiplexer_2_out2, demultiplexer_2_out3, multiplexer_1_out;
  wire [1:0] n4_modes_1_mode;
  wire [2:0] n6_modes_1_mode;
  wire [3:0] binairy_to_bcd_converter_1_p2, binairy_to_bcd_converter_1_p3, n10_modes_1_mode;
  wire [4:0] n24_modes_1_mode;
  wire [6:0] disp_nbr_1_s, disp_nbr_2_s, disp_nbr_3_s, disp_nbr_4_s, disp_nbr_5_s;

  n4_modes n4_modes_1 (.B(AB[1]), .PoR(PoR), .Clk(Clk), .mode(n4_modes_1_mode));
  Demultiplexer #(.select(2), .enable("false")) demultiplexer_1 (
    .out0(demultiplexer_1_out0), .out1(demultiplexer_1_out1), .out2(demultiplexer_1_out2),
    .out3(demultiplexer_1_out3), .in(AB[0]), .sel(n4_modes_1_mode));
  Demultiplexer #(.select(2), .enable("false")) demultiplexer_2 (
    .out0(demultiplexer_2_out0), .out1(demultiplexer_2_out1), .out2(demultiplexer_2_out2),
    .out3(demultiplexer_2_out3), .in(1'b1), .sel(n4_modes_1_mode));
  switch_01 switch_01_1 (.E(demultiplexer_1_out0), .PoR(PoR), .S(alarm_on));
  n6_modes n6_modes_1 (
    .B(demultiplexer_1_out2), .PoR(PoR), .Clk(Clk), .set_val(3'b000), .set_on(1'b0), .mode(n6_modes_1_mode));
  n10_modes n10_modes_1 (
    .B(demultiplexer_1_out1), .PoR(PoR), .Clk(Clk), .set_val(4'b0000), .set_on(1'b0), .mode(n10_modes_1_mode));
  n24_modes n24_modes_1 (
    .B(demultiplexer_1_out3), .PoR(PoR), .Clk(Clk), .set_val({5{1'b0}}), .set_on(1'b0),
    .mode(n24_modes_1_mode));
  // Binairy_to_BCD_converter #(.binvalue(5)) binairy_to_bcd_converter_1: pin names not known; wires that end beside it: n24_modes_1_mode, binairy_to_bcd_converter_1_p2, binairy_to_bcd_converter_1_p3
  disp_nbr disp_nbr_2 (.E({1'b0, n6_modes_1_mode}), .S(disp_nbr_2_s));
  disp_nbr disp_nbr_3 (.E(n10_modes_1_mode), .S(disp_nbr_3_s));
  disp_nbr disp_nbr_4 (.E(binairy_to_bcd_converter_1_p2), .S(disp_nbr_4_s));
  disp_nbr disp_nbr_5 (.E(binairy_to_bcd_converter_1_p3), .S(disp_nbr_5_s));
  Comparator comparator_1 (
    .a(current_hour), .b({binairy_to_bcd_converter_1_p2, binairy_to_bcd_converter_1_p3}), .eq(comparator_1_eq));  // open: gt, lt
  Comparator comparator_2 (
    .a(current_minut), .b({1'b0, n6_modes_1_mode, n10_modes_1_mode}), .eq(comparator_2_eq));  // open: gt, lt
  Comparator comparator_3 (.a(current_second), .b({8{1'b0}}), .eq(comparator_3_eq));  // open: gt, lt
  disp_nbr disp_nbr_1 (.E({3'b000, alarm_on}), .S(disp_nbr_1_s));
  and and_1 (and_1_out, comparator_1_eq, comparator_2_eq, comparator_3_eq);
  Multiplexer #(.enable("false")) multiplexer_1 (.in0(1'b0), .in1(and_1_out), .out(multiplexer_1_out), .sel(alarm_on));
  animation_led_alarm animation_led_alarm_1 (
    .ON_OFF(multiplexer_1_out), .Clk(Clk), .PoR(PoR), .off(off), .output_led(led_alarm),
    .disp_led_alarm(alarm_ding));
  blink blink_1 (.E(disp_nbr_1_s), .Clk(Clk), .PoR(PoR), .blink_on(demultiplexer_2_out0), .S(A0));
  blink blink_2 (.E(disp_nbr_2_s), .Clk(Clk), .PoR(PoR), .blink_on(demultiplexer_2_out2), .S(A3));
  blink blink_3 (.E(disp_nbr_3_s), .Clk(Clk), .PoR(PoR), .blink_on(demultiplexer_2_out1), .S(A2));
  blink blink_4 (.E(disp_nbr_4_s), .Clk(Clk), .PoR(PoR), .blink_on(demultiplexer_2_out3), .S(A5));
  blink blink_5 (.E(disp_nbr_5_s), .Clk(Clk), .PoR(PoR), .blink_on(demultiplexer_2_out3), .S(A4));

  assign A1 = {7{1'b0}};
endmodule

module CHRONO (
  input  [1:0] AB,
  input  Clk,
  input  PoR,
  output [6:0] A5,
  output [6:0] A4,
  output [6:0] A3,
  output [6:0] A2,
  output [6:0] A1,
  output [6:0] A0
);

  wire and_1_out, and_2_out, and_3_out, and_4_out, and_5_out, and_6_out, and_7_out, and_8_out, and_9_out,
       and_10_out, frequ_chrono_1_pulse, not_1_out, not_2_out, not_3_out, not_4_out, not_5_out, not_6_out,
       not_7_out, not_8_out, or_1_out, switch_01_1_s, zero_fiftynine_2_o, zero_nine_1_o, zero_nine_1_s0,
       zero_nine_1_s1, zero_nine_1_s2, zero_nine_1_s3, zero_nine_2_o, zero_nine_2_s0, zero_nine_2_s1,
       zero_nine_2_s2, zero_nine_2_s3;
  wire [3:0] s_r_ff_4_q, s_r_ff_8_q, zero_fiftynine_1_d, zero_fiftynine_1_u, zero_fiftynine_2_d,
       zero_fiftynine_2_u;

  switch_01 switch_01_1 (.E(AB[1]), .PoR(PoR), .S(switch_01_1_s));
  and and_1 (and_1_out, ~switch_01_1_s, AB[0]);  // AND_Gate
  or or_1 (or_1_out, and_1_out, PoR);
  frequ_chrono frequ_chrono_1 (.PoR(or_1_out), .Clk(Clk), .pulse(frequ_chrono_1_pulse));
  and and_2 (and_2_out, switch_01_1_s, frequ_chrono_1_pulse);
  zero_fiftynine zero_fiftynine_1 (
    .Oi(zero_fiftynine_2_o), .Clk(Clk), .PoR(or_1_out), .D(zero_fiftynine_1_d), .U(zero_fiftynine_1_u));  // open: set_D, set_D_on, set_U, set_U_on, O
  zero_fiftynine zero_fiftynine_2 (
    .Oi(zero_nine_1_o), .Clk(Clk), .PoR(or_1_out), .O(zero_fiftynine_2_o), .D(zero_fiftynine_2_d),
    .U(zero_fiftynine_2_u));  // open: set_D, set_D_on, set_U, set_U_on
  zero_nine zero_nine_1 (
    .E3(s_r_ff_4_q[3]), .E2(s_r_ff_4_q[2]), .E1(s_r_ff_4_q[1]), .E0(s_r_ff_4_q[0]), .Oi(zero_nine_2_o),
    .O(zero_nine_1_o), .S3(zero_nine_1_s3), .S2(zero_nine_1_s2), .S1(zero_nine_1_s1), .S0(zero_nine_1_s0));
  zero_nine zero_nine_2 (
    .E3(s_r_ff_8_q[3]), .E2(s_r_ff_8_q[2]), .E1(s_r_ff_8_q[1]), .E0(s_r_ff_8_q[0]), .Oi(and_2_out),
    .O(zero_nine_2_o), .S3(zero_nine_2_s3), .S2(zero_nine_2_s2), .S1(zero_nine_2_s1), .S0(zero_nine_2_s0));
  and and_3 (and_3_out, zero_nine_1_s3, ~or_1_out);  // AND_Gate
  and and_4 (and_4_out, zero_nine_1_s2, ~or_1_out);  // AND_Gate
  and and_5 (and_5_out, zero_nine_1_s1, ~or_1_out);  // AND_Gate
  and and_6 (and_6_out, zero_nine_1_s0, ~or_1_out);  // AND_Gate
  and and_7 (and_7_out, zero_nine_2_s3, ~or_1_out);  // AND_Gate
  and and_8 (and_8_out, zero_nine_2_s2, ~or_1_out);  // AND_Gate
  and and_9 (and_9_out, zero_nine_2_s1, ~or_1_out);  // AND_Gate
  and and_10 (and_10_out, zero_nine_2_s0, ~or_1_out);  // AND_Gate
  disp_nbr disp_nbr_1 (.E(zero_fiftynine_1_d), .S(A5));
  disp_nbr disp_nbr_2 (.E(zero_fiftynine_1_u), .S(A4));
  disp_nbr disp_nbr_3 (.E(zero_fiftynine_2_d), .S(A3));
  disp_nbr disp_nbr_4 (.E(zero_fiftynine_2_u), .S(A2));
  not not_1 (not_1_out, and_3_out);
  not not_2 (not_2_out, and_4_out);
  not not_3 (not_3_out, and_5_out);
  not not_4 (not_4_out, and_6_out);
  not not_5 (not_5_out, and_7_out);
  not not_6 (not_6_out, and_8_out);
  not not_7 (not_7_out, and_9_out);
  not not_8 (not_8_out, and_10_out);
  S_R_Flip_Flop s_r_ff_1 (
    .S(and_3_out), .R(not_1_out), .clk(Clk), .Q(s_r_ff_4_q[3]), .reset(or_1_out));  // open: Qn, preset
  S_R_Flip_Flop s_r_ff_2 (
    .S(and_4_out), .R(not_2_out), .clk(Clk), .Q(s_r_ff_4_q[2]), .reset(or_1_out));  // open: Qn, preset
  S_R_Flip_Flop s_r_ff_3 (
    .S(and_5_out), .R(not_3_out), .clk(Clk), .Q(s_r_ff_4_q[1]), .reset(or_1_out));  // open: Qn, preset
  S_R_Flip_Flop s_r_ff_4 (
    .S(and_6_out), .R(not_4_out), .clk(Clk), .Q(s_r_ff_4_q[0]), .reset(or_1_out));  // open: Qn, preset
  S_R_Flip_Flop s_r_ff_5 (
    .S(and_7_out), .R(not_5_out), .clk(Clk), .Q(s_r_ff_8_q[3]), .reset(or_1_out));  // open: Qn, preset
  S_R_Flip_Flop s_r_ff_6 (
    .S(and_8_out), .R(not_6_out), .clk(Clk), .Q(s_r_ff_8_q[2]), .reset(or_1_out));  // open: Qn, preset
  S_R_Flip_Flop s_r_ff_7 (
    .S(and_9_out), .R(not_7_out), .clk(Clk), .Q(s_r_ff_8_q[1]), .reset(or_1_out));  // open: Qn, preset
  S_R_Flip_Flop s_r_ff_8 (
    .S(and_10_out), .R(not_8_out), .clk(Clk), .Q(s_r_ff_8_q[0]), .reset(or_1_out));  // open: Qn, preset
  disp_nbr disp_nbr_5 (.E(s_r_ff_4_q), .S(A1));
  disp_nbr disp_nbr_6 (.E(s_r_ff_8_q), .S(A0));
endmodule

module TIME_SET (
  input  [1:0] AB,
  input  PoR,
  input  Clk,
  output set_on,
  output [3:0] D_month,
  output [3:0] U_month,
  output [3:0] dotw,
  output [3:0] D_dotm,
  output [3:0] U_dotm,
  output [3:0] D_hour,
  output [3:0] U_hour,
  output [3:0] D_minut,
  output [3:0] U_minut,
  output [3:0] D_second,
  output [3:0] U_second,
  output [6:0] A5,
  output [6:0] A4,
  output [6:0] A3,
  output [6:0] A2,
  output [6:0] A1,
  output [6:0] A0
);

  wire comparator_1_gt, demultiplexer_1_out0, demultiplexer_1_out1, demultiplexer_1_out2,
       demultiplexer_1_out3, demultiplexer_1_out4, demultiplexer_1_out5, demultiplexer_1_out6,
       demultiplexer_1_out7, demultiplexer_2_out0, demultiplexer_2_out1, demultiplexer_2_out2,
       demultiplexer_2_out3, demultiplexer_2_out4, demultiplexer_2_out5, demultiplexer_2_out6,
       demultiplexer_2_out7, demultiplexer_3_out0, demultiplexer_3_out1, demultiplexer_3_out2;
  wire [1:0] month_select_1_s0;
  wire [3:0] adder_1_out, days_output_1_z0, days_output_1_z1, n9_modes_1_mode, n12_modes_1_mode;
  wire [4:0] binairy_to_bcd_converter_2_p1, multiplexer_1_out, n24_modes_1_mode, n28_modes_1_mode,
       n30_modes_1_mode, n31_modes_1_mode;
  wire [6:0] blink_1_s, blink_2_s, blink_3_s, blink_4_s, blink_5_s, blink_6_s, blink_7_s, blink_8_s,
       blink_9_s, blink_10_s, blink_11_s, blink_12_s, disp_ltr_1_s, disp_ltr_2_s, disp_nbr_1_s, disp_nbr_2_s,
       disp_nbr_3_s, disp_nbr_4_s, disp_nbr_5_s, disp_nbr_6_s, disp_nbr_7_s, disp_nbr_8_s, disp_nbr_9_s,
       disp_nbr_10_s;

  Demultiplexer #(.select(4), .enable("false")) demultiplexer_1 (
    .out0(demultiplexer_1_out0), .out1(demultiplexer_1_out1), .out2(demultiplexer_1_out2),
    .out3(demultiplexer_1_out3), .out4(demultiplexer_1_out4), .out5(demultiplexer_1_out5),
    .out6(demultiplexer_1_out6), .out7(demultiplexer_1_out7), .out8(set_on), .in(AB[0]), .sel(n9_modes_1_mode));  // open: out9, out10, out11, out12, out13, out14, out15
  n9_modes n9_modes_1 (.B(AB[1]), .PoR(PoR), .Clk(Clk), .mode(n9_modes_1_mode));
  Comparator #(.width(5)) comparator_1 (
    .a({1'b0, n9_modes_1_mode}), .b(5'b00010), .gt(comparator_1_gt));  // open: eq, lt
  Demultiplexer #(.select(4), .enable("false")) demultiplexer_2 (
    .out0(demultiplexer_2_out0), .out1(demultiplexer_2_out1), .out2(demultiplexer_2_out2),
    .out3(demultiplexer_2_out3), .out4(demultiplexer_2_out4), .out5(demultiplexer_2_out5),
    .out6(demultiplexer_2_out6), .out7(demultiplexer_2_out7), .in(1'b1), .sel(n9_modes_1_mode));  // open: out8, out9, out10, out11, out12, out13, out14, out15
  Demultiplexer #(.select(2), .enable("false")) demultiplexer_3 (
    .out0(demultiplexer_3_out0), .out1(demultiplexer_3_out1), .out2(demultiplexer_3_out2),
    .in(demultiplexer_1_out2), .sel(month_select_1_s0));  // open: out3
  n31_modes n31_modes_1 (.B(demultiplexer_3_out0), .PoR(PoR), .Clk(Clk), .mode(n31_modes_1_mode));
  n30_modes n30_modes_1 (.B(demultiplexer_3_out1), .PoR(PoR), .Clk(Clk), .mode(n30_modes_1_mode));
  n28_modes n28_modes_1 (.B(demultiplexer_3_out2), .PoR(PoR), .Clk(Clk), .mode(n28_modes_1_mode));
  n7_modes n7_modes_1 (.B(demultiplexer_1_out1), .PoR(PoR), .Clk(Clk), .mode(dotw[2:0]));
  n12_modes n12_modes_1 (.B(demultiplexer_1_out0), .PoR(PoR), .Clk(Clk), .mode(n12_modes_1_mode));
  n6_modes n6_modes_1 (
    .B(demultiplexer_1_out6), .PoR(PoR), .Clk(Clk), .set_val(3'b000), .set_on(1'b0), .mode(U_second[2:0]));
  n10_modes n10_modes_1 (
    .B(demultiplexer_1_out7), .PoR(PoR), .Clk(Clk), .set_val(4'b0000), .set_on(1'b0), .mode(D_second));
  n6_modes n6_modes_2 (
    .B(demultiplexer_1_out4), .PoR(PoR), .Clk(Clk), .set_val(3'b000), .set_on(1'b0), .mode(U_minut[2:0]));
  n10_modes n10_modes_2 (
    .B(demultiplexer_1_out5), .PoR(PoR), .Clk(Clk), .set_val(4'b0000), .set_on(1'b0), .mode(D_minut));
  n24_modes n24_modes_1 (
    .B(demultiplexer_1_out3), .PoR(PoR), .Clk(Clk), .set_val({5{1'b0}}), .set_on(1'b0),
    .mode(n24_modes_1_mode));
  Multiplexer #(.select(2), .width(5), .enable("false")) multiplexer_1 (
    .in0(n31_modes_1_mode), .in1(n30_modes_1_mode), .in2(n28_modes_1_mode), .out(multiplexer_1_out),
    .sel(month_select_1_s0));  // open: in3
  Adder #(.width(4)) adder_1 (.a(n12_modes_1_mode), .b(4'b0000), .out(adder_1_out), .cin(1'b1));  // open: cout
  // Binairy_to_BCD_converter #(.binvalue(5)) binairy_to_bcd_converter_1: pin names not known; wires that end beside it: n24_modes_1_mode, D_hour, U_hour
  // Binairy_to_BCD_converter #(.binvalue(5)) binairy_to_bcd_converter_2: pin names not known; wires that end beside it: binairy_to_bcd_converter_2_p1, D_dotm, U_dotm
  Adder #(.width(5)) adder_2 (
    .a(multiplexer_1_out), .b({5{1'b0}}), .out(binairy_to_bcd_converter_2_p1), .cin(1'b1));  // open: cout
  // Binairy_to_BCD_converter #(.binvalue(4)) binairy_to_bcd_converter_3: pin names not known; wires that end beside it: adder_1_out, D_month, U_month
  days_output days_output_1 (
    .E2(dotw[2]), .E1(dotw[1]), .E0(dotw[0]), .W1(days_output_1_z1[3]), .X1(days_output_1_z1[2]),
    .Y1(days_output_1_z1[1]), .Z1(days_output_1_z1[0]), .W0(days_output_1_z0[3]), .X0(days_output_1_z0[2]),
    .Y0(days_output_1_z0[1]), .Z0(days_output_1_z0[0]));
  month_select month_select_1 (
    .E4(D_month[0]), .E3(U_month[3]), .E2(U_month[2]), .E1(U_month[1]), .E0(U_month[0]),
    .S1(month_select_1_s0[1]), .S0(month_select_1_s0[0]));
  disp_nbr disp_nbr_1 (.E({1'b0, U_second[2:0]}), .S(disp_nbr_1_s));
  disp_nbr disp_nbr_2 (.E(D_second), .S(disp_nbr_2_s));
  disp_nbr disp_nbr_3 (.E({1'b0, U_minut[2:0]}), .S(disp_nbr_3_s));
  disp_nbr disp_nbr_4 (.E(D_minut), .S(disp_nbr_4_s));
  disp_nbr disp_nbr_5 (.E(D_hour), .S(disp_nbr_5_s));
  disp_nbr disp_nbr_6 (.E(U_hour), .S(disp_nbr_6_s));
  disp_nbr disp_nbr_7 (.E(D_dotm), .S(disp_nbr_7_s));
  disp_nbr disp_nbr_8 (.E(U_dotm), .S(disp_nbr_8_s));
  disp_ltr disp_ltr_1 (.S(disp_ltr_1_s), .E(days_output_1_z1));
  disp_ltr disp_ltr_2 (.S(disp_ltr_2_s), .E(days_output_1_z0));
  disp_nbr disp_nbr_9 (.E(D_month), .S(disp_nbr_9_s));
  disp_nbr disp_nbr_10 (.E(U_month), .S(disp_nbr_10_s));
  blink blink_1 (.E(disp_nbr_1_s), .Clk(Clk), .PoR(PoR), .blink_on(demultiplexer_2_out6), .S(blink_1_s));
  blink blink_2 (.E(disp_nbr_2_s), .Clk(Clk), .PoR(PoR), .blink_on(demultiplexer_2_out7), .S(blink_2_s));
  blink blink_3 (.E(disp_nbr_3_s), .Clk(Clk), .PoR(PoR), .blink_on(demultiplexer_2_out4), .S(blink_3_s));
  blink blink_4 (.E(disp_nbr_4_s), .Clk(Clk), .PoR(PoR), .blink_on(demultiplexer_2_out5), .S(blink_4_s));
  blink blink_5 (.E(disp_nbr_5_s), .Clk(Clk), .PoR(PoR), .blink_on(demultiplexer_2_out3), .S(blink_5_s));
  blink blink_6 (.E(disp_nbr_6_s), .Clk(Clk), .PoR(PoR), .blink_on(demultiplexer_2_out3), .S(blink_6_s));
  blink blink_7 (.E(disp_nbr_7_s), .Clk(Clk), .PoR(PoR), .blink_on(demultiplexer_2_out2), .S(blink_7_s));
  blink blink_8 (.E(disp_nbr_8_s), .Clk(Clk), .PoR(PoR), .blink_on(demultiplexer_2_out2), .S(blink_8_s));
  blink blink_9 (.E(disp_ltr_1_s), .Clk(Clk), .PoR(PoR), .blink_on(demultiplexer_2_out1), .S(blink_9_s));
  blink blink_10 (.E(disp_ltr_2_s), .Clk(Clk), .PoR(PoR), .blink_on(demultiplexer_2_out1), .S(blink_10_s));
  blink blink_11 (.E(disp_nbr_9_s), .Clk(Clk), .PoR(PoR), .blink_on(demultiplexer_2_out0), .S(blink_11_s));
  blink blink_12 (.E(disp_nbr_10_s), .Clk(Clk), .PoR(PoR), .blink_on(demultiplexer_2_out0), .S(blink_12_s));
  Multiplexer #(.width(7), .enable("false")) multiplexer_2 (
    .in0(blink_11_s), .in1(blink_5_s), .out(A5), .sel(comparator_1_gt));
  Multiplexer #(.width(7), .enable("false")) multiplexer_3 (
    .in0(blink_12_s), .in1(blink_6_s), .out(A4), .sel(comparator_1_gt));
  Multiplexer #(.width(7), .enable("false")) multiplexer_4 (
    .in0(blink_9_s), .in1(blink_3_s), .out(A3), .sel(comparator_1_gt));
  Multiplexer #(.width(7), .enable("false")) multiplexer_5 (
    .in0(blink_10_s), .in1(blink_4_s), .out(A2), .sel(comparator_1_gt));
  Multiplexer #(.width(7), .enable("false")) multiplexer_6 (
    .in0(blink_7_s), .in1(blink_1_s), .out(A1), .sel(comparator_1_gt));
  Multiplexer #(.width(7), .enable("false")) multiplexer_7 (
    .in0(blink_8_s), .in1(blink_2_s), .out(A0), .sel(comparator_1_gt));

  assign dotw[3] = 1'b0;
  assign U_minut[3] = 1'b0;
  assign U_second[3] = 1'b0;
endmodule

module COUNTDOWN (
  input  [1:0] AB,
  input  PoR,
  input  Clk,
  output [6:0] A5,
  output [6:0] A4,
  output [6:0] A3,
  output [6:0] A2,
  output [6:0] A1,
  output [6:0] A0
);

  wire and_1_out, demultiplexer_1_out0, demultiplexer_1_out1, demultiplexer_1_out2, demultiplexer_1_out3,
       demultiplexer_1_out4, demultiplexer_1_out5, demultiplexer_2_out0, demultiplexer_2_out1,
       demultiplexer_2_out2, demultiplexer_2_out3, demultiplexer_2_out4, demultiplexer_2_out5,
       five_zero_1_bo, five_zero_2_bo, frequ_sec_1_pulse, nine_zero_1_bo, nine_zero_2_bo, or_1_out, or_2_out,
       or_3_out, or_4_out, s_r_ff_1_q, switch_01_1_s, twentythree_zero_1_bo;
  wire [2:0] five_zero_1_n, n6_modes_1_mode, n6_modes_2_mode, n6_modes_3_mode;
  wire [3:0] five_zero_2_n, n10_modes_1_mode, n10_modes_2_mode, nine_zero_1_n, nine_zero_2_n,
       twentythree_zero_1_n0, twentythree_zero_1_n1;
  wire [3:3] five_zero_1_n_2;
  wire [4:0] n24_modes_1_mode, twentythree_zero_1_val;
  wire [6:0] disp_nbr_1_s, disp_nbr_2_s, disp_nbr_3_s, disp_nbr_4_s, disp_nbr_5_s, disp_nbr_6_s;

  n6_modes n6_modes_1 (.B(AB[1]), .PoR(PoR), .Clk(Clk), .set_val(3'b000), .set_on(1'b0), .mode(n6_modes_1_mode));
  Demultiplexer #(.select(3), .enable("false")) demultiplexer_1 (
    .out0(demultiplexer_1_out0), .out1(demultiplexer_1_out1), .out2(demultiplexer_1_out2),
    .out3(demultiplexer_1_out3), .out4(demultiplexer_1_out4), .out5(demultiplexer_1_out5), .in(AB[0]),
    .sel(n6_modes_1_mode));  // open: out6, out7
  Demultiplexer #(.select(3), .enable("false")) demultiplexer_2 (
    .out0(demultiplexer_2_out0), .out1(demultiplexer_2_out1), .out2(demultiplexer_2_out2),
    .out3(demultiplexer_2_out3), .out4(demultiplexer_2_out4), .out5(demultiplexer_2_out5), .in(1'b1),
    .sel(n6_modes_1_mode));  // open: out6, out7
  or or_1 (or_1_out, PoR, or_2_out);
  frequ_sec frequ_sec_1 (.PoR(PoR), .Clk(Clk), .pulse(frequ_sec_1_pulse));
  switch_01 switch_01_1 (.E(demultiplexer_1_out5), .PoR(or_1_out), .S(switch_01_1_s));
  or or_2 (or_2_out, demultiplexer_2_out4, demultiplexer_2_out3, demultiplexer_2_out2, demultiplexer_2_out1, demultiplexer_2_out0);
  n24_modes n24_modes_1 (
    .B(demultiplexer_1_out0), .PoR(PoR), .Clk(Clk), .set_val(twentythree_zero_1_val),
    .set_on(demultiplexer_2_out5), .mode(n24_modes_1_mode));
  n6_modes n6_modes_2 (
    .B(demultiplexer_1_out1), .PoR(PoR), .Clk(Clk), .set_val(five_zero_1_n), .set_on(demultiplexer_2_out5),
    .mode(n6_modes_2_mode));
  n10_modes n10_modes_1 (
    .B(demultiplexer_1_out2), .PoR(PoR), .Clk(Clk), .set_val(nine_zero_1_n), .set_on(demultiplexer_2_out5),
    .mode(n10_modes_1_mode));
  n6_modes n6_modes_3 (
    .B(demultiplexer_1_out3), .PoR(PoR), .Clk(Clk), .set_val(five_zero_2_n[2:0]),
    .set_on(demultiplexer_2_out5), .mode(n6_modes_3_mode));
  n10_modes n10_modes_2 (
    .B(demultiplexer_1_out4), .PoR(PoR), .Clk(Clk), .set_val(nine_zero_2_n), .set_on(demultiplexer_2_out5),
    .mode(n10_modes_2_mode));
  and and_1 (and_1_out, switch_01_1_s, frequ_sec_1_pulse);
  or or_3 (or_3_out, PoR, s_r_ff_1_q);
  twentythree_zero twentythree_zero_1 (
    .Bi(five_zero_1_bo), .set_val(n24_modes_1_mode), .set_on(demultiplexer_2_out0), .PoR(or_3_out),
    .Clk(Clk), .Bo(twentythree_zero_1_bo), .N1(twentythree_zero_1_n1), .N0(twentythree_zero_1_n0),
    .val(twentythree_zero_1_val));
  five_zero five_zero_1 (
    .Bi(nine_zero_1_bo), .set_val({1'b0, n6_modes_2_mode}), .set_on(demultiplexer_2_out1), .PoR(or_3_out),
    .Clk(Clk), .Bo(five_zero_1_bo), .N({five_zero_1_n_2[3], five_zero_1_n}));
  nine_zero nine_zero_1 (
    .Bi(five_zero_2_bo), .set_val(n10_modes_1_mode), .set_on(demultiplexer_2_out2), .PoR(or_3_out),
    .Clk(Clk), .Bo(nine_zero_1_bo), .N(nine_zero_1_n));
  five_zero five_zero_2 (
    .Bi(nine_zero_2_bo), .set_val({1'b0, n6_modes_3_mode}), .set_on(demultiplexer_2_out3), .PoR(or_3_out),
    .Clk(Clk), .Bo(five_zero_2_bo), .N(five_zero_2_n));
  nine_zero nine_zero_2 (
    .Bi(and_1_out), .set_val(n10_modes_2_mode), .set_on(demultiplexer_2_out4), .PoR(or_3_out), .Clk(Clk),
    .Bo(nine_zero_2_bo), .N(nine_zero_2_n));
  disp_nbr disp_nbr_1 (.E(twentythree_zero_1_n1), .S(disp_nbr_1_s));
  disp_nbr disp_nbr_2 (.E(twentythree_zero_1_n0), .S(disp_nbr_2_s));
  disp_nbr disp_nbr_3 (.E({five_zero_1_n_2[3], five_zero_1_n}), .S(disp_nbr_3_s));
  disp_nbr disp_nbr_4 (.E(nine_zero_1_n), .S(disp_nbr_4_s));
  disp_nbr disp_nbr_5 (.E(five_zero_2_n), .S(disp_nbr_5_s));
  disp_nbr disp_nbr_6 (.E(nine_zero_2_n), .S(disp_nbr_6_s));
  S_R_Flip_Flop s_r_ff_1 (.Q(s_r_ff_1_q), .reset(or_4_out), .preset(twentythree_zero_1_bo));  // open: S, R, clk, Qn
  or or_4 (or_4_out, PoR, or_2_out);
  blink blink_1 (.E(disp_nbr_1_s), .Clk(Clk), .PoR(PoR), .blink_on(demultiplexer_2_out0), .S(A5));
  blink blink_2 (.E(disp_nbr_2_s), .Clk(Clk), .PoR(PoR), .blink_on(demultiplexer_2_out0), .S(A4));
  blink blink_3 (.E(disp_nbr_3_s), .Clk(Clk), .PoR(PoR), .blink_on(demultiplexer_2_out1), .S(A3));
  blink blink_4 (.E(disp_nbr_4_s), .Clk(Clk), .PoR(PoR), .blink_on(demultiplexer_2_out2), .S(A2));
  blink blink_5 (.E(disp_nbr_5_s), .Clk(Clk), .PoR(PoR), .blink_on(demultiplexer_2_out3), .S(A1));
  blink blink_6 (.E(disp_nbr_6_s), .Clk(Clk), .PoR(PoR), .blink_on(demultiplexer_2_out4), .S(A0));
endmodule

module test (
  input  CLK2k,
  input  PoR,
  input  [3:0] HloadT_4,
  input  HloadTEnDi,
  input  [3:0] HloadU_4,
  input  HloadUEnDi,
  input  [3:0] MINloadT_4,
  input  MINloadTEnDi,
  input  [3:0] MINloadU_4,
  input  MINloadUEnDi,
  input  [3:0] SECloadT_4,
  input  SECloadTEnDi,
  input  [3:0] SECloadU_4,
  input  SECloadUEnDi,
  output [7:0] HOUR_8,
  output [7:0] MIN_8,
  output [7:0] SEC_8
);

  wire min_o, pulse, sec_o;
  wire [3:0] hour_d, hour_u, min_d, min_u, sec_d, sec_u;
  wire [7:0] multiplier_1_out, multiplier_2_out, multiplier_3_out;

  zero_twentythree hour (
    .Oi(min_o), .set_D(HloadT_4), .set_D_on(HloadTEnDi), .set_U(HloadU_4), .set_U_on(HloadUEnDi),
    .Clk(CLK2k), .PoR(PoR), .D(hour_d), .U(hour_u));  // open: O
  zero_fiftynine min (
    .Oi(sec_o), .set_D(MINloadT_4), .set_D_on(MINloadTEnDi), .set_U(MINloadU_4), .set_U_on(MINloadUEnDi),
    .Clk(CLK2k), .PoR(PoR), .O(min_o), .D(min_d), .U(min_u));
  zero_fiftynine sec (
    .Oi(pulse), .set_D(SECloadT_4), .set_D_on(SECloadTEnDi), .set_U(SECloadU_4), .set_U_on(SECloadUEnDi),
    .Clk(CLK2k), .PoR(PoR), .O(sec_o), .D(sec_d), .U(sec_u));
  Multiplier multiplier_1 (.a({4'b0000, min_d}), .b(8'ha), .out(multiplier_1_out));  // open: cin, cout
  Multiplier multiplier_2 (.a({4'b0000, sec_d}), .b(8'ha), .out(multiplier_2_out));  // open: cin, cout
  Multiplier multiplier_3 (.a({4'b0000, hour_d}), .b(8'ha), .out(multiplier_3_out));  // open: cin, cout
  Adder adder_1 (.a(multiplier_3_out), .b({4'b0000, hour_u}), .out(HOUR_8));  // open: cin, cout
  Adder adder_2 (.a(multiplier_1_out), .b({4'b0000, min_u}), .out(MIN_8));  // open: cin, cout
  Adder adder_3 (.a(multiplier_2_out), .b({4'b0000, sec_u}), .out(SEC_8));  // open: cin, cout
  frequ_sec freq (.PoR(PoR), .Clk(CLK2k), .pulse(pulse));

  // Other names for the same wires on the sheet: c = CLK2k; p = PoR
endmodule

module testOnBoard (
);

  wire clk32k_to_2k_1_clk2k, clock_1_out, DipSwitch_1_sw1, DipSwitch_1_sw10, sevseg0_p1, sevseg1_p1,
       sevseg2_p1, sevseg3_p1, sevseg4_p1, sevseg5_p1;
  wire [7:0] test_1_hour_8, test_1_min_8, test_1_sec_8;

  Clock clock_1 (.out(clock_1_out));
  DipSwitch #(.number(10)) DipSwitch_1 (
    .sw1(DipSwitch_1_sw1), .sw10(DipSwitch_1_sw10));  // open: sw2, sw3, sw4, sw5, sw6, sw7, sw8, sw9
  clk32k_to_2k clk32k_to_2k_1 (.CLK32k(clock_1_out), .CLK2k(clk32k_to_2k_1_clk2k));
  test test_1 (
    .CLK2k(clk32k_to_2k_1_clk2k), .PoR(DipSwitch_1_sw1), .HloadT_4(4'b0000), .HloadTEnDi(DipSwitch_1_sw10),
    .HloadU_4(4'b0000), .HloadUEnDi(DipSwitch_1_sw10), .MINloadT_4(4'b0000), .MINloadTEnDi(DipSwitch_1_sw10),
    .MINloadU_4(4'b0000), .MINloadUEnDi(DipSwitch_1_sw10), .SECloadT_4(4'b0000),
    .SECloadTEnDi(DipSwitch_1_sw10), .SECloadU_4(4'b0000), .SECloadUEnDi(DipSwitch_1_sw10),
    .HOUR_8(test_1_hour_8), .MIN_8(test_1_min_8), .SEC_8(test_1_sec_8));
  // _7_Segment_Display sevseg5: pin names not known; wires that end beside it: sevseg5_p1, sevseg5_p1
  // BCD_to_7_Segment_decoder bcd_to_7_segment_decoder_1: pin names not known
  // Binairy_to_BCD_converter #(.binvalue(8)) binairy_to_bcd_converter_1: pin names not known; wires that end beside it: test_1_hour_8
  // _7_Segment_Display sevseg3: pin names not known; wires that end beside it: sevseg3_p1, sevseg3_p1
  // BCD_to_7_Segment_decoder bcd_to_7_segment_decoder_2: pin names not known
  // Binairy_to_BCD_converter #(.binvalue(8)) binairy_to_bcd_converter_2: pin names not known; wires that end beside it: test_1_min_8
  // _7_Segment_Display sevseg1: pin names not known; wires that end beside it: sevseg1_p1, sevseg1_p1
  // BCD_to_7_Segment_decoder bcd_to_7_segment_decoder_3: pin names not known
  // Binairy_to_BCD_converter #(.binvalue(8)) binairy_to_bcd_converter_3: pin names not known; wires that end beside it: test_1_sec_8
  // BCD_to_7_Segment_decoder bcd_to_7_segment_decoder_4: pin names not known
  // _7_Segment_Display sevseg4: pin names not known; wires that end beside it: sevseg4_p1, sevseg4_p1
  // BCD_to_7_Segment_decoder bcd_to_7_segment_decoder_5: pin names not known
  // _7_Segment_Display sevseg2: pin names not known; wires that end beside it: sevseg2_p1, sevseg2_p1
  // _7_Segment_Display sevseg0: pin names not known; wires that end beside it: sevseg0_p1, sevseg0_p1
  // BCD_to_7_Segment_decoder bcd_to_7_segment_decoder_6: pin names not known
endmodule

module clk32k_to_2k (
  input  CLK32k,
  output CLK2k
);

  wire d_ff_1_q, d_ff_1_qn, d_ff_2_q, d_ff_2_qn, d_ff_3_q, d_ff_3_qn, d_ff_4_qn;

  D_Flip_Flop d_ff_1 (.D(d_ff_1_qn), .clk(CLK32k), .Q(d_ff_1_q), .Qn(d_ff_1_qn));  // open: preset, reset
  D_Flip_Flop d_ff_2 (.D(d_ff_2_qn), .clk(d_ff_1_q), .Q(d_ff_2_q), .Qn(d_ff_2_qn));  // open: preset, reset
  D_Flip_Flop d_ff_3 (.D(d_ff_3_qn), .clk(d_ff_2_q), .Q(d_ff_3_q), .Qn(d_ff_3_qn));  // open: preset, reset
  D_Flip_Flop d_ff_4 (.D(d_ff_4_qn), .clk(d_ff_3_q), .Q(CLK2k), .Qn(d_ff_4_qn));  // open: preset, reset
endmodule

module copypaste (
);

  wire c, p, pulse;

  frequ_sec freq (.PoR(p), .Clk(c), .pulse(pulse));
endmodule
