// Logisim project Functions.circ as structural Verilog: 53 circuits, main circuit add
module add (
  input  O,
  input  B,
  input  A,
  output Oo,
  output P
);

  wire nand_1_out, nand_2_out, nand_3_out, nand_4_out, nand_5_out, nand_6_out, nand_7_out, nand_8_out,
       nand_9_out, nand_10_out, nand_11_out, nand_12_out, nand_13_out;

  nand nand_1 (nand_1_out, O, O);
  nand nand_2 (nand_2_out, B, B);
  nand nand_3 (nand_3_out, O, O);
  nand nand_4 (nand_4_out, A, A);
  nand nand_5 (nand_5_out, B, B);
  nand nand_6 (nand_6_out, A, A);
  nand nand_7 (nand_7_out, B, A);
  nand nand_8 (nand_8_out, O, A);
  nand nand_9 (nand_9_out, O, B);
  nand nand_10 (nand_10_out, nand_1_out, nand_2_out, A);
  nand nand_11 (nand_11_out, nand_3_out, B, nand_4_out);
  nand nand_12 (nand_12_out, O, nand_5_out, nand_6_out);
  nand nand_13 (nand_13_out, O, B, A);
  nand nand_14 (Oo, nand_7_out, nand_8_out, nand_9_out);
  nand nand_15 (P, nand_10_out, nand_11_out, nand_12_out, nand_13_out);
endmodule

module zero_nine (
  input  E3,
  input  E2,
  input  E1,
  input  E0,
  input  Oi,
  output O,
  output S3,
  output S2,
  output S1,
  output S0
);

  wire nand_1_out, nand_2_out, nand_3_out, nand_4_out, nand_5_out, nand_6_out, nand_7_out, nand_8_out,
       nand_9_out, nand_10_out, nand_11_out, nand_12_out, nand_13_out, nand_14_out, nand_15_out, nand_16_out,
       nand_17_out, nand_18_out, nand_19_out, nand_20_out, nand_21_out, nand_22_out, nand_23_out,
       nand_24_out, nand_25_out, nand_26_out, nand_27_out, nand_28_out, nand_29_out, nand_30_out,
       nand_31_out, nand_32_out, nand_33_out, nand_34_out, nand_35_out, nand_36_out, nand_37_out,
       nand_38_out, nand_39_out, nand_40_out, nand_41_out, nand_42_out, nand_43_out, nand_44_out,
       nand_45_out, nand_46_out, nand_47_out, nand_48_out;

  nand nand_1 (nand_1_out, E2, E2);
  nand nand_2 (nand_2_out, E1, E1);
  nand nand_3 (nand_3_out, Oi, Oi);
  nand nand_4 (nand_4_out, E2, E2);
  nand nand_5 (nand_5_out, E1, E1);
  nand nand_6 (nand_6_out, E2, E2);
  nand nand_7 (nand_7_out, E1, E1);
  nand nand_8 (nand_8_out, E0, E0);
  nand nand_9 (nand_9_out, E3, E3);
  nand nand_10 (nand_10_out, E3, E3);
  nand nand_11 (nand_11_out, E2, E2);
  nand nand_12 (nand_12_out, E3, E3);
  nand nand_13 (nand_13_out, E1, E1);
  nand nand_14 (nand_14_out, E3, E3);
  nand nand_15 (nand_15_out, E0, E0);
  nand nand_16 (nand_16_out, E3, E3);
  nand nand_17 (nand_17_out, Oi, Oi);
  nand nand_18 (nand_18_out, E3, E3);
  nand nand_19 (nand_19_out, E1, E1);
  nand nand_20 (nand_20_out, E3, E3);
  nand nand_21 (nand_21_out, E0, E0);
  nand nand_22 (nand_22_out, E3, E3);
  nand nand_23 (nand_23_out, Oi, Oi);
  nand nand_24 (nand_24_out, E3, E3);
  nand nand_25 (nand_25_out, E0, E0);
  nand nand_26 (nand_26_out, E2, E2);
  nand nand_27 (nand_27_out, E1, E1);
  nand nand_28 (nand_28_out, E0, E0);
  nand nand_29 (nand_29_out, E3, E3);
  nand nand_30 (nand_30_out, Oi, Oi);
  nand nand_31 (nand_31_out, E2, E2);
  nand nand_32 (nand_32_out, E1, E1);
  nand nand_33 (nand_33_out, Oi, Oi);
  nand nand_34 (nand_34_out, E3, nand_1_out, nand_2_out, E0, Oi);
  nand nand_35 (nand_35_out, nand_3_out, E3, nand_4_out, nand_5_out);
  nand nand_36 (nand_36_out, E3, nand_6_out, nand_7_out, nand_8_out);
  nand nand_37 (nand_37_out, Oi, nand_9_out, E2, E1, E0);
  nand nand_38 (nand_38_out, nand_10_out, nand_11_out, E1, E0, Oi);
  nand nand_39 (nand_39_out, nand_12_out, E2, nand_13_out);
  nand nand_40 (nand_40_out, nand_14_out, E2, nand_15_out);
  nand nand_41 (nand_41_out, nand_16_out, E2, nand_17_out);
  nand nand_42 (nand_42_out, nand_18_out, nand_19_out, E0, Oi);
  nand nand_43 (nand_43_out, nand_20_out, E1, nand_21_out);
  nand nand_44 (nand_44_out, nand_22_out, E1, nand_23_out);
  nand nand_45 (nand_45_out, nand_24_out, nand_25_out, Oi);
  nand nand_46 (nand_46_out, nand_26_out, nand_27_out, nand_28_out, Oi);
  nand nand_47 (nand_47_out, nand_29_out, E0, nand_30_out);
  nand nand_48 (nand_48_out, nand_31_out, nand_32_out, E0, nand_33_out);
  nand nand_49 (O, nand_34_out, nand_34_out);
  nand nand_50 (S3, nand_35_out, nand_36_out, nand_37_out);
  nand nand_51 (S2, nand_38_out, nand_39_out, nand_40_out, nand_41_out);
  nand nand_52 (S1, nand_42_out, nand_43_out, nand_44_out);
  nand nand_53 (S0, nand_45_out, nand_46_out, nand_47_out, nand_48_out);
endmodule

module zero_five (
  input  E2,
  input  E1,
  input  E0,
  input  Oi,
  output O,
  output S2,
  output S1,
  output S0
);

  wire nand_1_out, nand_2_out, nand_3_out, nand_4_out, nand_5_out, nand_6_out, nand_7_out, nand_8_out,
       nand_9_out, nand_10_out, nand_11_out, nand_12_out, nand_13_out, nand_14_out, nand_15_out, nand_16_out,
       nand_17_out, nand_18_out, nand_19_out, nand_20_out, nand_21_out, nand_22_out, nand_23_out,
       nand_24_out, nand_25_out, nand_26_out, nand_27_out, nand_28_out, nand_29_out, nand_30_out;

  nand nand_1 (nand_1_out, E1, E1);
  nand nand_2 (nand_2_out, E2, E2);
  nand nand_3 (nand_3_out, E1, E1);
  nand nand_4 (nand_4_out, E0, E0);
  nand nand_5 (nand_5_out, E1, E1);
  nand nand_6 (nand_6_out, Oi, Oi);
  nand nand_7 (nand_7_out, E2, E2);
  nand nand_8 (nand_8_out, E1, E1);
  nand nand_9 (nand_9_out, E2, E2);
  nand nand_10 (nand_10_out, E0, E0);
  nand nand_11 (nand_11_out, E2, E2);
  nand nand_12 (nand_12_out, Oi, Oi);
  nand nand_13 (nand_13_out, E1, E1);
  nand nand_14 (nand_14_out, E0, E0);
  nand nand_15 (nand_15_out, E2, E2);
  nand nand_16 (nand_16_out, E0, E0);
  nand nand_17 (nand_17_out, E1, E1);
  nand nand_18 (nand_18_out, Oi, Oi);
  nand nand_19 (nand_19_out, E2, E2);
  nand nand_20 (nand_20_out, Oi, E2, nand_1_out, E0);
  nand nand_21 (nand_21_out, nand_2_out, E1, E0, Oi);
  nand nand_22 (nand_22_out, E2, nand_3_out, nand_4_out);
  nand nand_23 (nand_23_out, E2, nand_5_out, nand_6_out);
  nand nand_24 (nand_24_out, nand_7_out, nand_8_out, E0, Oi);
  nand nand_25 (nand_25_out, nand_9_out, E1, nand_10_out);
  nand nand_26 (nand_26_out, nand_11_out, E1, nand_12_out);
  nand nand_27 (nand_27_out, E2, nand_13_out, nand_14_out, Oi);
  nand nand_28 (nand_28_out, nand_15_out, nand_16_out, Oi);
  nand nand_29 (nand_29_out, nand_17_out, E0, nand_18_out);
  nand nand_30 (nand_30_out, nand_19_out, E1, E0);
  nand nand_31 (O, nand_20_out, nand_20_out);
  nand nand_32 (S2, nand_21_out, nand_22_out, nand_23_out);
  nand nand_33 (S1, nand_24_out, nand_25_out, nand_26_out, nand_27_out);
  nand nand_34 (S0, nand_28_out, nand_29_out, nand_30_out);
endmodule

module zero_fiftynine (
  input  Oi,
  input  [3:0] set_D,
  input  set_D_on,
  input  [3:0] set_U,
  input  set_U_on,
  input  Clk,
  input  PoR,
  output O,
  output [3:0] D,
  output [3:0] U
);

  wire and_1_out, and_2_out, and_3_out, and_4_out, and_5_out, and_6_out, and_7_out, not_1_out, not_2_out,
       not_3_out, not_4_out, not_5_out, not_6_out, not_7_out, set_1_s0, set_1_s1, set_1_s2, set_2_s0,
       set_2_s1, set_2_s2, set_2_s3, zero_five_1_s0, zero_five_1_s1, zero_five_1_s2, zero_nine_1_o,
       zero_nine_1_s0, zero_nine_1_s1, zero_nine_1_s2, zero_nine_1_s3;

  zero_five zero_five_1 (
    .E2(D[2]), .E1(D[1]), .E0(D[0]), .Oi(zero_nine_1_o), .O(O), .S2(zero_five_1_s2), .S1(zero_five_1_s1),
    .S0(zero_five_1_s0));
  zero_nine zero_nine_1 (
    .E3(U[3]), .E2(U[2]), .E1(U[1]), .E0(U[0]), .Oi(Oi), .O(zero_nine_1_o), .S3(zero_nine_1_s3),
    .S2(zero_nine_1_s2), .S1(zero_nine_1_s1), .S0(zero_nine_1_s0));
  set set_1 (
    .E3(1'b0), .E2(zero_five_1_s2), .E1(zero_five_1_s1), .E0(zero_five_1_s0), .set_val(set_D),
    .set_on(set_D_on), .S2(set_1_s2), .S1(set_1_s1), .S0(set_1_s0));  // open: S3
  set set_2 (
    .E3(zero_nine_1_s3), .E2(zero_nine_1_s2), .E1(zero_nine_1_s1), .E0(zero_nine_1_s0), .set_val(set_U),
    .set_on(set_U_on), .S3(set_2_s3), .S2(set_2_s2), .S1(set_2_s1), .S0(set_2_s0));
  and and_1 (and_1_out, set_1_s2, ~PoR);  // AND_Gate
  and and_2 (and_2_out, set_1_s1, ~PoR);  // AND_Gate
  and and_3 (and_3_out, set_1_s0, ~PoR);  // AND_Gate
  and and_4 (and_4_out, set_2_s3, ~PoR);  // AND_Gate
  and and_5 (and_5_out, set_2_s2, ~PoR);  // AND_Gate
  and and_6 (and_6_out, set_2_s1, ~PoR);  // AND_Gate
  and and_7 (and_7_out, set_2_s0, ~PoR);  // AND_Gate
  not not_1 (not_1_out, and_1_out);
  not not_2 (not_2_out, and_2_out);
  not not_3 (not_3_out, and_3_out);
  not not_4 (not_4_out, and_4_out);
  not not_5 (not_5_out, and_5_out);
  not not_6 (not_6_out, and_6_out);
  not not_7 (not_7_out, and_7_out);
  S_R_Flip_Flop s_r_ff_1 (.S(and_1_out), .R(not_1_out), .clk(Clk), .Q(D[2]), .reset(PoR));  // open: Qn, preset
  S_R_Flip_Flop s_r_ff_2 (.S(and_2_out), .R(not_2_out), .clk(Clk), .Q(D[1]), .reset(PoR));  // open: Qn, preset
  S_R_Flip_Flop s_r_ff_3 (.S(and_3_out), .R(not_3_out), .clk(Clk), .Q(D[0]), .reset(PoR));  // open: Qn, preset
  S_R_Flip_Flop s_r_ff_4 (.S(and_4_out), .R(not_4_out), .clk(Clk), .Q(U[3]), .reset(PoR));  // open: Qn, preset
  S_R_Flip_Flop s_r_ff_5 (.S(and_5_out), .R(not_5_out), .clk(Clk), .Q(U[2]), .reset(PoR));  // open: Qn, preset
  S_R_Flip_Flop s_r_ff_6 (.S(and_6_out), .R(not_6_out), .clk(Clk), .Q(U[1]), .reset(PoR));  // open: Qn, preset
  S_R_Flip_Flop s_r_ff_7 (.S(and_7_out), .R(not_7_out), .clk(Clk), .Q(U[0]), .reset(PoR));  // open: Qn, preset

  assign D[3] = 1'b0;
endmodule

module disp_nbr (
  input  [3:0] E,
  output [6:0] S
);

  wire and_1_out, and_2_out, and_3_out, and_4_out, and_5_out, and_6_out, and_7_out, and_8_out, and_9_out,
       and_10_out, and_11_out, and_12_out, and_13_out, and_14_out, and_15_out, and_16_out, and_17_out,
       and_18_out, and_19_out, and_20_out, and_21_out, and_22_out, and_23_out, and_24_out, and_25_out,
       and_26_out, and_27_out, and_28_out, and_29_out, and_30_out, and_31_out, and_32_out, and_33_out,
       and_34_out, and_35_out, not_1_out, not_2_out, not_3_out, not_4_out;

  not not_1 (not_1_out, E[3]);
  not not_2 (not_2_out, E[2]);
  not not_3 (not_3_out, E[1]);
  not not_4 (not_4_out, E[0]);
  and and_1 (and_1_out, E[3], E[2], not_4_out);
  and and_2 (and_2_out, E[1], not_1_out);
  and and_3 (and_3_out, not_4_out, not_2_out);
  and and_4 (and_4_out, E[2], E[1], E[0]);
  and and_5 (and_5_out, not_1_out, E[2], E[0]);
  and and_6 (and_6_out, not_3_out, E[3], not_2_out);
  and and_7 (and_7_out, E[3], E[0], not_3_out);
  and and_8 (and_8_out, not_2_out, not_4_out);
  and and_9 (and_9_out, E[0], E[1], not_1_out);
  and and_10 (and_10_out, not_1_out, not_2_out, not_3_out);
  and and_11 (and_11_out, not_1_out, not_3_out, not_4_out);
  and and_12 (and_12_out, E[0], E[3], not_3_out);
  and and_13 (and_13_out, not_2_out, E[3]);
  and and_14 (and_14_out, not_2_out, E[0]);
  and and_15 (and_15_out, E[2], not_1_out);
  and and_16 (and_16_out, not_3_out, not_1_out);
  and and_17 (and_17_out, E[3], not_3_out);
  and and_18 (and_18_out, E[2], E[1], not_4_out);
  and and_19 (and_19_out, not_2_out, E[1], E[0]);
  and and_20 (and_20_out, not_2_out, not_1_out, not_4_out);
  and and_21 (and_21_out, not_3_out, E[2], E[0]);
  or or_1 (S[0], and_1_out, and_2_out, and_3_out, and_4_out, and_5_out, and_6_out);
  or or_2 (S[1], and_7_out, and_8_out, and_9_out, and_10_out, and_11_out);
  or or_3 (S[2], and_12_out, and_13_out, and_14_out, and_15_out, and_16_out);
  or or_4 (S[3], and_17_out, and_18_out, and_19_out, and_20_out, and_21_out);
  and and_22 (and_22_out, E[3], E[2]);
  and and_23 (and_23_out, E[3], E[1]);
  and and_24 (and_24_out, not_2_out, not_4_out);
  and and_25 (and_25_out, not_4_out, E[1]);
  and and_26 (and_26_out, not_1_out, E[2], not_4_out);
  and and_27 (and_27_out, E[2], not_3_out, E[0]);
  and and_28 (and_28_out, E[3], E[1]);
  and and_29 (and_29_out, E[3], not_2_out);
  and and_30 (and_30_out, E[1], not_2_out);
  and and_31 (and_31_out, E[2], not_4_out);
  and and_32 (and_32_out, E[3], not_2_out);
  and and_33 (and_33_out, E[3], E[1]);
  and and_34 (and_34_out, E[2], not_1_out, not_3_out);
  and and_35 (and_35_out, not_4_out, not_1_out, not_3_out);
  or or_5 (S[4], and_22_out, and_23_out, and_24_out, and_25_out);
  or or_6 (S[6], and_26_out, and_27_out, and_28_out, and_29_out, and_30_out);
  or or_7 (S[5], and_31_out, and_32_out, and_33_out, and_34_out, and_35_out);
endmodule

module zero_twentythree (
  input  Oi,
  input  [3:0] set_D,
  input  set_D_on,
  input  [3:0] set_U,
  input  set_U_on,
  input  Clk,
  input  PoR,
  output O,
  output [3:0] D,
  output [3:0] U
);

  wire and_1_out, and_2_out, and_3_out, and_4_out, and_5_out, and_6_out, and_7_out, not_1_out, not_2_out,
       not_3_out, not_4_out, not_5_out, not_6_out, set_0_s0, set_0_s1, set_1_s0, set_1_s1, set_1_s2,
       set_1_s3, zero_nine_spe_0_o, zero_nine_spe_0_s0, zero_nine_spe_0_s1, zero_nine_spe_0_s2,
       zero_nine_spe_0_s3, zero_two_0_s0, zero_two_0_s1;

  and and_1 (and_1_out, D[1], ~D[0]);  // AND_Gate
  zero_two zero_two_0 (.E1(D[1]), .E0(D[0]), .Oi(zero_nine_spe_0_o), .O(O), .S1(zero_two_0_s1), .S0(zero_two_0_s0));
  zero_nine_spe zero_nine_spe_0 (
    .C(and_1_out), .E3(U[3]), .E2(U[2]), .E1(U[1]), .E0(U[0]), .Oi(Oi), .O(zero_nine_spe_0_o),
    .S3(zero_nine_spe_0_s3), .S2(zero_nine_spe_0_s2), .S1(zero_nine_spe_0_s1), .S0(zero_nine_spe_0_s0));
  set set_0 (
    .E3(1'b0), .E2(1'b0), .E1(zero_two_0_s1), .E0(zero_two_0_s0), .set_val(set_D), .set_on(set_D_on),
    .S1(set_0_s1), .S0(set_0_s0));  // open: S3, S2
  set set_1 (
    .E3(zero_nine_spe_0_s3), .E2(zero_nine_spe_0_s2), .E1(zero_nine_spe_0_s1), .E0(zero_nine_spe_0_s0),
    .set_val(set_U), .set_on(set_U_on), .S3(set_1_s3), .S2(set_1_s2), .S1(set_1_s1), .S0(set_1_s0));
  and and_2 (and_2_out, set_0_s1, ~PoR);  // AND_Gate
  and and_3 (and_3_out, set_0_s0, ~PoR);  // AND_Gate
  and and_4 (and_4_out, set_1_s3, ~PoR);  // AND_Gate
  and and_5 (and_5_out, set_1_s2, ~PoR);  // AND_Gate
  and and_6 (and_6_out, set_1_s1, ~PoR);  // AND_Gate
  and and_7 (and_7_out, set_1_s0, ~PoR);  // AND_Gate
  not not_1 (not_1_out, and_2_out);
  not not_2 (not_2_out, and_3_out);
  not not_3 (not_3_out, and_4_out);
  not not_4 (not_4_out, and_5_out);
  not not_5 (not_5_out, and_6_out);
  not not_6 (not_6_out, and_7_out);
  S_R_Flip_Flop s_r_ff_1 (.S(and_2_out), .R(not_1_out), .clk(Clk), .Q(D[1]), .reset(PoR));  // open: Qn, preset
  S_R_Flip_Flop s_r_ff_2 (.S(and_3_out), .R(not_2_out), .clk(Clk), .Q(D[0]), .reset(PoR));  // open: Qn, preset
  S_R_Flip_Flop s_r_ff_3 (.S(and_4_out), .R(not_3_out), .clk(Clk), .Q(U[3]), .reset(PoR));  // open: Qn, preset
  S_R_Flip_Flop s_r_ff_4 (.S(and_5_out), .R(not_4_out), .clk(Clk), .Q(U[2]), .reset(PoR));  // open: Qn, preset
  S_R_Flip_Flop s_r_ff_5 (.S(and_6_out), .R(not_5_out), .clk(Clk), .Q(U[1]), .reset(PoR));  // open: Qn, preset
  S_R_Flip_Flop s_r_ff_6 (.S(and_7_out), .R(not_6_out), .clk(Clk), .Q(U[0]), .reset(PoR));  // open: Qn, preset

  assign D[3:2] = 2'b00;
endmodule

module zero_nine_spe (
  input  C,
  input  E3,
  input  E2,
  input  E1,
  input  E0,
  input  Oi,
  output O,
  output S3,
  output S2,
  output S1,
  output S0
);

  wire nand_1_out, nand_2_out, nand_3_out, nand_4_out, nand_5_out, nand_6_out, nand_7_out, nand_8_out,
       nand_9_out, nand_10_out, nand_11_out, nand_12_out, nand_13_out, nand_14_out, nand_15_out, nand_17_out,
       nand_18_out, nand_19_out, nand_20_out, nand_21_out, nand_22_out, nand_23_out, nand_24_out,
       nand_25_out, nand_26_out, nand_27_out, nand_28_out, nand_29_out, nand_30_out;

  nand nand_1 (nand_1_out, Oi, E3, E0);
  nand nand_2 (nand_2_out, C, Oi, E1, E0);
  nand nand_3 (nand_3_out, E0, E0);
  nand nand_4 (nand_4_out, Oi, Oi);
  nand nand_5 (nand_5_out, C, C);
  nand nand_6 (nand_6_out, E2, E2);
  nand nand_7 (nand_7_out, E1, E1);
  nand nand_8 (nand_8_out, E0, E0);
  nand nand_9 (nand_9_out, Oi, Oi);
  nand nand_10 (nand_10_out, Oi, Oi);
  nand nand_11 (nand_11_out, E0, E0);
  nand nand_12 (nand_12_out, E3, E3);
  nand nand_13 (nand_13_out, E1, E1);
  nand nand_14 (nand_14_out, Oi, Oi);
  nand nand_15 (nand_15_out, E0, E0);
  nand nand_16 (O, nand_1_out, nand_2_out);
  nand nand_17 (nand_17_out, E2, E1, E0, Oi);
  nand nand_18 (nand_18_out, E3, nand_3_out);
  nand nand_19 (nand_19_out, E3, nand_4_out);
  nand nand_20 (nand_20_out, nand_5_out, nand_6_out, E1, E0, Oi);
  nand nand_21 (nand_21_out, E2, nand_7_out);
  nand nand_22 (nand_22_out, E2, nand_8_out);
  nand nand_23 (nand_23_out, E2, nand_9_out);
  nand nand_24 (nand_24_out, nand_10_out, E1);
  nand nand_25 (nand_25_out, E1, nand_11_out);
  nand nand_26 (nand_26_out, E3, E2);
  nand nand_27 (nand_27_out, Oi, nand_12_out, nand_13_out, E0);
  nand nand_28 (nand_28_out, nand_14_out, E0);
  nand nand_29 (nand_29_out, E3, E2);
  nand nand_30 (nand_30_out, Oi, nand_15_out);
  nand nand_31 (S3, nand_17_out, nand_18_out, nand_19_out);
  nand nand_32 (S0, nand_28_out, nand_29_out, nand_30_out);
  nand nand_33 (S2, nand_20_out, nand_21_out, nand_22_out, nand_23_out);
  nand nand_34 (S1, nand_24_out, nand_25_out, nand_26_out, nand_27_out);
endmodule

module zero_two (
  input  E1,
  input  E0,
  input  Oi,
  output O,
  output S1,
  output S0
);

  wire nand_1_out, nand_2_out, nand_3_out, nand_4_out, nand_5_out, nand_7_out, nand_8_out, nand_9_out,
       nand_10_out;

  nand nand_1 (nand_1_out, Oi, E1);
  nand nand_2 (nand_2_out, Oi, Oi);
  nand nand_3 (nand_3_out, Oi, Oi);
  nand nand_4 (nand_4_out, E1, E1);
  nand nand_5 (nand_5_out, E0, E0);
  nand nand_6 (O, nand_1_out, nand_1_out);
  nand nand_7 (nand_7_out, nand_2_out, E1);
  nand nand_8 (nand_8_out, Oi, E0);
  nand nand_9 (nand_9_out, nand_3_out, E0);
  nand nand_10 (nand_10_out, Oi, nand_4_out, nand_5_out);
  nand nand_11 (S1, nand_7_out, nand_8_out);
  nand nand_12 (S0, nand_9_out, nand_10_out);
endmodule

module disp_ltr (
  input  [3:0] E,
  output [6:0] S
);

  wire nand_1_out, nand_2_out, nand_3_out, nand_4_out, nand_5_out, nand_6_out, nand_7_out, nand_8_out,
       nand_9_out, nand_10_out, nand_11_out, nand_12_out, nand_13_out, nand_14_out, nand_15_out, nand_16_out,
       nand_17_out, nand_18_out, nand_19_out, nand_20_out, nand_21_out, nand_22_out, nand_23_out,
       nand_24_out, nand_25_out, nand_26_out, nand_27_out, nand_28_out, nand_29_out, nand_30_out,
       nand_31_out, nand_32_out, nand_33_out, nand_34_out, nand_35_out, nand_36_out, nand_37_out,
       nand_38_out, nand_39_out, nand_40_out, nand_41_out, nand_43_out, nand_44_out, nand_45_out,
       nand_46_out, nand_47_out, nand_48_out, nand_49_out, nand_50_out, nand_51_out, nand_52_out, nand_53_out;

  nand nand_1 (nand_1_out, E[3], E[3]);
  nand nand_2 (nand_2_out, E[2], E[2]);
  nand nand_3 (nand_3_out, E[1], E[1]);
  nand nand_4 (nand_4_out, E[3], E[3]);
  nand nand_5 (nand_5_out, E[2], E[2]);
  nand nand_6 (nand_6_out, E[0], E[0]);
  nand nand_7 (nand_7_out, E[2], E[2]);
  nand nand_8 (nand_8_out, E[1], E[1]);
  nand nand_9 (nand_9_out, E[0], E[0]);
  nand nand_10 (nand_10_out, E[3], E[3]);
  nand nand_11 (nand_11_out, E[2], E[2]);
  nand nand_12 (nand_12_out, E[1], E[1]);
  nand nand_13 (nand_13_out, E[0], E[0]);
  nand nand_14 (nand_14_out, E[2], E[2]);
  nand nand_15 (nand_15_out, E[1], E[1]);
  nand nand_16 (nand_16_out, E[0], E[0]);
  nand nand_17 (nand_17_out, E[2], E[2]);
  nand nand_18 (nand_18_out, E[1], E[1]);
  nand nand_19 (nand_19_out, E[0], E[0]);
  nand nand_20 (nand_20_out, E[0], E[0]);
  nand nand_21 (nand_21_out, E[3], E[3]);
  nand nand_22 (nand_22_out, E[2], E[2]);
  nand nand_23 (nand_23_out, E[1], E[1]);
  nand nand_24 (nand_24_out, E[0], E[0]);
  nand nand_25 (nand_25_out, E[1], E[1]);
  nand nand_26 (nand_26_out, E[3], E[3]);
  nand nand_27 (nand_27_out, E[2], E[2]);
  nand nand_28 (nand_28_out, E[2], E[2]);
  nand nand_29 (nand_29_out, E[1], E[1]);
  nand nand_30 (nand_30_out, nand_1_out, nand_2_out, nand_3_out);
  nand nand_31 (nand_31_out, nand_4_out, nand_5_out, nand_6_out);
  nand nand_32 (nand_32_out, nand_7_out, nand_8_out, nand_9_out);
  nand nand_33 (nand_33_out, E[2], E[0]);
  nand nand_34 (nand_34_out, E[2], E[1]);
  nand nand_35 (nand_35_out, nand_14_out, nand_15_out, nand_16_out);
  nand nand_36 (nand_36_out, nand_17_out, E[1], E[0]);
  nand nand_37 (nand_37_out, E[2], nand_18_out, E[0]);
  nand nand_38 (nand_38_out, E[2], E[1], nand_19_out);
  nand nand_39 (nand_39_out, E[3], nand_20_out);
  nand nand_40 (nand_40_out, E[0], E[0]);
  nand nand_41 (nand_41_out, E[0], E[0]);
  nand nand_42 (S[4], E[3], nand_24_out, nand_25_out);
  nand nand_43 (nand_43_out, nand_26_out, nand_27_out);
  nand nand_44 (nand_44_out, nand_28_out, nand_29_out);
  nand nand_45 (nand_45_out, E[1], E[0]);
  nand nand_46 (nand_46_out, nand_10_out, nand_11_out, nand_12_out, nand_13_out);
  nand nand_47 (nand_47_out, E[1], E[0]);
  nand nand_48 (nand_48_out, E[2], E[0]);
  nand nand_49 (nand_49_out, E[2], E[1]);
  nand nand_50 (nand_50_out, E[3], E[1]);
  nand nand_51 (nand_51_out, nand_21_out, nand_22_out, nand_23_out, E[0]);
  nand nand_52 (nand_52_out, E[2], nand_40_out);
  nand nand_53 (nand_53_out, E[3], nand_41_out);
  nand nand_54 (S[6], nand_43_out, nand_44_out, nand_45_out);
  nand nand_55 (S[0], nand_30_out, nand_31_out, nand_32_out, nand_33_out, nand_34_out);
  nand nand_56 (S[1], nand_46_out, nand_47_out, nand_48_out, nand_49_out, nand_50_out);
  nand nand_57 (S[2], nand_35_out, nand_36_out, nand_37_out, nand_38_out, nand_39_out);
  nand nand_58 (S[3], nand_51_out, nand_52_out, nand_53_out);

  assign S[5] = 1'b1;
endmodule

module days (
  input  E2,
  input  E1,
  input  E0,
  input  Oi,
  output O,
  output S2,
  output S1,
  output S0
);

  wire nand_1_out, nand_2_out, nand_3_out, nand_4_out, nand_5_out, nand_6_out, nand_7_out, nand_8_out,
       nand_9_out, nand_10_out, nand_11_out, nand_12_out, nand_14_out, nand_15_out, nand_16_out, nand_17_out,
       nand_18_out, nand_19_out, nand_20_out, nand_21_out, nand_22_out;

  nand nand_1 (nand_1_out, E2, E1, Oi);
  nand nand_2 (nand_2_out, Oi, Oi);
  nand nand_3 (nand_3_out, E1, E1);
  nand nand_4 (nand_4_out, E1, E1);
  nand nand_5 (nand_5_out, E2, E2);
  nand nand_6 (nand_6_out, E0, E0);
  nand nand_7 (nand_7_out, Oi, Oi);
  nand nand_8 (nand_8_out, E2, E2);
  nand nand_9 (nand_9_out, E0, E0);
  nand nand_10 (nand_10_out, E1, E1);
  nand nand_11 (nand_11_out, E0, E0);
  nand nand_12 (nand_12_out, Oi, Oi);
  nand nand_13 (O, nand_1_out, nand_1_out);
  nand nand_14 (nand_14_out, nand_2_out, E2);
  nand nand_15 (nand_15_out, E2, nand_3_out);
  nand nand_16 (nand_16_out, Oi, E1, E0);
  nand nand_17 (nand_17_out, nand_4_out, E0, Oi);
  nand nand_18 (nand_18_out, nand_5_out, E1, nand_6_out);
  nand nand_19 (nand_19_out, E1, nand_7_out);
  nand nand_20 (nand_20_out, nand_8_out, nand_9_out, Oi);
  nand nand_21 (nand_21_out, nand_10_out, nand_11_out, Oi);
  nand nand_22 (nand_22_out, E0, nand_12_out);
  nand nand_23 (S2, nand_14_out, nand_15_out, nand_16_out);
  nand nand_24 (S1, nand_17_out, nand_18_out, nand_19_out);
  nand nand_25 (S0, nand_20_out, nand_21_out, nand_22_out);
endmodule

module mon_sun (
  input  Oi,
  input  [3:0] set_days,
  input  set_on,
  input  Clk,
  input  PoR,
  output O,
  output [3:0] D1,
  output [3:0] D0
);

  wire and_1_out, and_2_out, and_3_out, days_1_s0, days_1_s1, days_1_s2, not_1_out, not_2_out, not_3_out,
       s_r_ff_1_q, s_r_ff_2_q, s_r_ff_3_q, set_1_s0, set_1_s1, set_1_s2;

  days days_1 (
    .E2(s_r_ff_1_q), .E1(s_r_ff_2_q), .E0(s_r_ff_3_q), .Oi(Oi), .O(O), .S2(days_1_s2), .S1(days_1_s1),
    .S0(days_1_s0));
  set set_1 (
    .E3(1'b0), .E2(days_1_s2), .E1(days_1_s1), .E0(days_1_s0), .set_val(set_days), .set_on(set_on),
    .S2(set_1_s2), .S1(set_1_s1), .S0(set_1_s0));  // open: S3
  and and_1 (and_1_out, set_1_s2, ~PoR);  // AND_Gate
  and and_2 (and_2_out, set_1_s1, ~PoR);  // AND_Gate
  and and_3 (and_3_out, set_1_s0, ~PoR);  // AND_Gate
  not not_1 (not_1_out, and_1_out);
  not not_2 (not_2_out, and_2_out);
  not not_3 (not_3_out, and_3_out);
  S_R_Flip_Flop s_r_ff_1 (.S(and_1_out), .R(not_1_out), .clk(Clk), .Q(s_r_ff_1_q), .reset(PoR));  // open: Qn, preset
  S_R_Flip_Flop s_r_ff_2 (.S(and_2_out), .R(not_2_out), .clk(Clk), .Q(s_r_ff_2_q), .reset(PoR));  // open: Qn, preset
  S_R_Flip_Flop s_r_ff_3 (.S(and_3_out), .R(not_3_out), .clk(Clk), .Q(s_r_ff_3_q), .reset(PoR));  // open: Qn, preset
  days_output days_output_1 (
    .E2(s_r_ff_1_q), .E1(s_r_ff_2_q), .E0(s_r_ff_3_q), .W1(D1[3]), .X1(D1[2]), .Y1(D1[1]), .Z1(D1[0]),
    .W0(D0[3]), .X0(D0[2]), .Y0(D0[1]), .Z0(D0[0]));
endmodule

module days_output (
  input  E2,
  input  E1,
  input  E0,
  output W1,
  output X1,
  output Y1,
  output Z1,
  output W0,
  output X0,
  output Y0,
  output Z0
);

  wire nand_1_out, nand_2_out, nand_3_out, nand_4_out, nand_5_out, nand_6_out, nand_7_out, nand_8_out,
       nand_9_out, nand_10_out, nand_11_out, nand_12_out, nand_13_out, nand_14_out, nand_15_out, nand_16_out,
       nand_17_out, nand_18_out, nand_19_out, nand_20_out, nand_21_out, nand_23_out, nand_24_out,
       nand_25_out, nand_26_out, nand_27_out, nand_28_out, nand_29_out, nand_30_out, nand_31_out,
       nand_32_out, nand_33_out, nand_34_out;

  nand nand_1 (nand_1_out, E0, E0);
  nand nand_2 (nand_2_out, E1, E1);
  nand nand_3 (nand_3_out, E2, E2);
  nand nand_4 (nand_4_out, E1, E1);
  nand nand_5 (nand_5_out, E0, E0);
  nand nand_6 (nand_6_out, E2, E2);
  nand nand_7 (nand_7_out, E0, E0);
  nand nand_8 (nand_8_out, E1, E1);
  nand nand_9 (nand_9_out, E0, E0);
  nand nand_10 (nand_10_out, E2, E2);
  nand nand_11 (nand_11_out, E1, E1);
  nand nand_12 (nand_12_out, E2, E2);
  nand nand_13 (nand_13_out, E2, E2);
  nand nand_14 (nand_14_out, E1, E1);
  nand nand_15 (nand_15_out, E2, E2);
  nand nand_16 (nand_16_out, E1, E1);
  nand nand_17 (nand_17_out, E0, E0);
  nand nand_18 (nand_18_out, E2, E2);
  nand nand_19 (nand_19_out, E1, E1);
  nand nand_20 (nand_20_out, E2, E2);
  nand nand_21 (nand_21_out, E2, E2);
  nand nand_22 (W1, nand_1_out, nand_2_out);
  nand nand_23 (nand_23_out, nand_3_out, nand_4_out, nand_5_out);
  nand nand_24 (nand_24_out, nand_6_out, E1, nand_7_out);
  nand nand_25 (nand_25_out, E2, nand_8_out, nand_9_out);
  nand nand_26 (nand_26_out, nand_10_out, nand_11_out);
  nand nand_27 (nand_27_out, nand_12_out, E0);
  nand nand_28 (nand_28_out, nand_13_out, nand_14_out, E0);
  nand nand_29 (nand_29_out, E2, E1);
  nand nand_30 (nand_30_out, nand_15_out, nand_16_out, nand_17_out);
  nand nand_31 (nand_31_out, nand_18_out, nand_19_out);
  nand nand_32 (nand_32_out, nand_20_out, E0);
  nand nand_33 (nand_33_out, E2, E1);
  nand nand_34 (nand_34_out, nand_21_out, E1);
  nand nand_35 (X1, nand_23_out, nand_23_out);
  nand nand_36 (Y1, nand_24_out, nand_25_out);
  nand nand_37 (Z1, nand_26_out, nand_27_out);
  nand nand_38 (W0, nand_28_out, nand_29_out);
  nand nand_39 (X0, nand_30_out, nand_30_out);
  nand nand_40 (Y0, nand_31_out, nand_32_out, nand_33_out);
  nand nand_41 (Z0, nand_34_out, nand_34_out);
endmodule

module def_AM_PM (
  input  H13,
  input  H12,
  input  H11,
  input  H10,
  input  H03,
  input  H02,
  input  H01,
  input  H00,
  output AM_PM
);

  wire and_1_out, or_1_out, supegal_2_1_r;

  or or_1 (or_1_out, H11, H10);
  and and_1 (and_1_out, or_1_out, supegal_2_1_r);
  supegal_2 supegal_2_1 (.E3(H03), .E2(H02), .E1(H01), .E0(H00), .R(supegal_2_1_r));
  or or_2 (AM_PM, H11, and_1_out);
endmodule

module supegal_2 (
  input  E3,
  input  E2,
  input  E1,
  input  E0,
  output R
);

  wire nand_1_out, nand_2_out, nand_3_out;

  nand nand_1 (nand_1_out, E1, E1);
  nand nand_2 (nand_2_out, E2, E2);
  nand nand_3 (nand_3_out, E3, E3);
  nand nand_4 (R, nand_1_out, nand_2_out, nand_3_out);
endmodule

module EU_to_US (
  input  H13,
  input  H12,
  input  H11,
  input  H10,
  input  H03,
  input  H02,
  input  H01,
  input  H00,
  output H13_out,
  output H12_out,
  output H11_out,
  output H10_out,
  output H03_out,
  output H02_out,
  output H01_out,
  output H00_out
);

  wire and_1_out, sub_0_so, sub_2_so, sub_3_so, sub_4_so, sub_5_so;
  wire [3:0] sub_5_m;

  sub sub_2 (.Si(1'b0), .A(H00), .B(1'b0), .So(sub_2_so), .M(sub_5_m[3]));
  sub sub_0 (.Si(sub_5_so), .A(H10), .B(1'b1), .So(sub_0_so), .M(H10_out));
  sub sub_3 (.Si(sub_2_so), .A(H01), .B(1'b1), .So(sub_3_so), .M(sub_5_m[2]));
  sub sub_1 (.Si(sub_0_so), .A(H11), .B(1'b0), .M(H11_out));  // open: So
  sub sub_4 (.Si(sub_3_so), .A(H02), .B(1'b0), .So(sub_4_so), .M(sub_5_m[1]));
  sub sub_5 (.Si(sub_4_so), .A(H03), .B(1'b0), .So(sub_5_so), .M(sub_5_m[0]));
  and and_1 (and_1_out, sub_5_m[0], sub_5_m[1], sub_5_m[2]);
  Multiplexer #(.width(4), .enable("false")) multiplexer_1 (
    .in0(sub_5_m), .in1({sub_5_m[3], 3'b001}), .out({H00_out, H01_out, H02_out, H03_out}), .sel(and_1_out));

  assign H12_out = 1'b0;
  assign H13_out = 1'b0;
endmodule

module sub (
  input  Si,
  input  A,
  input  B,
  output So,
  output M
);

  wire nand_1_out, nand_2_out, nand_3_out, nand_4_out, nand_5_out, nand_6_out, nand_7_out, nand_8_out,
       nand_9_out, nand_10_out, nand_11_out, nand_12_out, nand_13_out, nand_14_out, nand_15_out;

  nand nand_1 (nand_1_out, Si, Si);
  nand nand_2 (nand_2_out, B, B);
  nand nand_3 (nand_3_out, Si, Si);
  nand nand_4 (nand_4_out, A, A);
  nand nand_5 (nand_5_out, B, B);
  nand nand_6 (nand_6_out, A, A);
  nand nand_7 (nand_7_out, A, A);
  nand nand_8 (nand_8_out, A, A);
  nand nand_9 (nand_9_out, nand_1_out, nand_2_out, A);
  nand nand_10 (nand_10_out, nand_3_out, B, nand_4_out);
  nand nand_11 (nand_11_out, Si, nand_5_out, nand_6_out);
  nand nand_12 (nand_12_out, Si, B, A);
  nand nand_13 (nand_13_out, nand_7_out, B);
  nand nand_14 (nand_14_out, Si, nand_8_out);
  nand nand_15 (nand_15_out, Si, B);
  nand nand_16 (M, nand_9_out, nand_10_out, nand_11_out, nand_12_out);
  nand nand_17 (So, nand_13_out, nand_14_out, nand_15_out);
endmodule

module gestion_US (
  input  [3:0] D_in,
  input  [3:0] U_in,
  input  US_mode,
  output [3:0] D,
  output [3:0] U,
  output AM,
  output PM
);

  wire and_1_out;
  wire [7:0] demultiplexer_1_out0, demultiplexer_1_out1, EU_to_US_1_h10_out, multiplexer_1_out,
       multiplexer_2_out;

  Demultiplexer #(.width(8), .enable("false")) demultiplexer_1 (
    .out0(demultiplexer_1_out0), .out1(demultiplexer_1_out1), .in({U_in, D_in}), .sel(US_mode));
  EU_to_US EU_to_US_1 (
    .H13(demultiplexer_1_out1[3]), .H12(demultiplexer_1_out1[2]), .H11(demultiplexer_1_out1[1]),
    .H10(demultiplexer_1_out1[0]), .H03(demultiplexer_1_out1[7]), .H02(demultiplexer_1_out1[6]),
    .H01(demultiplexer_1_out1[5]), .H00(demultiplexer_1_out1[4]), .H13_out(EU_to_US_1_h10_out[3]),
    .H12_out(EU_to_US_1_h10_out[2]), .H11_out(EU_to_US_1_h10_out[1]), .H10_out(EU_to_US_1_h10_out[0]),
    .H03_out(EU_to_US_1_h10_out[7]), .H02_out(EU_to_US_1_h10_out[6]), .H01_out(EU_to_US_1_h10_out[5]),
    .H00_out(EU_to_US_1_h10_out[4]));
  def_AM_PM def_AM_PM_1 (
    .H13(demultiplexer_1_out1[3]), .H12(demultiplexer_1_out1[2]), .H11(demultiplexer_1_out1[1]),
    .H10(demultiplexer_1_out1[0]), .H03(demultiplexer_1_out1[7]), .H02(demultiplexer_1_out1[6]),
    .H01(demultiplexer_1_out1[5]), .H00(demultiplexer_1_out1[4]), .AM_PM(PM));
  Multiplexer #(.width(8), .enable("false")) multiplexer_1 (
    .in0(demultiplexer_1_out1), .in1(EU_to_US_1_h10_out), .out(multiplexer_1_out), .sel(PM));
  and and_1 (and_1_out, ~multiplexer_1_out[0], ~multiplexer_1_out[1], ~multiplexer_1_out[2], ~multiplexer_1_out[3], ~multiplexer_1_out[4], ~multiplexer_1_out[5], ~multiplexer_1_out[6], ~multiplexer_1_out[7]);  // AND_Gate
  Multiplexer #(.width(8), .enable("false")) multiplexer_2 (
    .in0(multiplexer_1_out), .in1(8'h21), .out(multiplexer_2_out), .sel(and_1_out));
  Multiplexer #(.width(8), .enable("false")) multiplexer_3 (
    .in0(demultiplexer_1_out0), .in1(multiplexer_2_out), .out({U, D}), .sel(US_mode));
  and and_2 (AM, US_mode, ~PM);  // AND_Gate
endmodule

module switch_debouncing (
  input  PoR,
  input  E,
  input  Clk,
  output S
);

  wire and_1_out, and_2_out, and_3_out, counter_1_carry, d_ff_1_q, d_ff_2_q, d_ff_3_q, not_1_out, not_2_out,
       or_1_out, or_2_out, or_3_out, xor_1_out;

  D_Flip_Flop d_ff_1 (.D(and_1_out), .clk(Clk), .Q(d_ff_1_q), .reset(PoR));  // open: Qn, preset
  and and_1 (and_1_out, ~PoR, E);  // AND_Gate
  D_Flip_Flop d_ff_2 (.D(and_2_out), .clk(Clk), .Q(d_ff_2_q), .reset(PoR));  // open: Qn, preset
  and and_2 (and_2_out, ~PoR, d_ff_1_q);  // AND_Gate
  xor xor_1 (xor_1_out, d_ff_2_q, d_ff_1_q);
  Counter #(.width(5), .max('h1f)) counter_1 (
    .clr(or_1_out), .clk(Clk), .carry(counter_1_carry));  // open: load, up, count, D, Q
  or or_1 (or_1_out, PoR, xor_1_out);
  not not_1 (not_1_out, E);
  D_Flip_Flop d_ff_3 (.Q(d_ff_3_q), .preset(counter_1_carry), .reset(or_2_out));  // open: D, clk, Qn
  or or_2 (or_2_out, not_1_out, PoR);
  D_Flip_Flop d_ff_4 (.D(and_3_out), .clk(Clk), .Q(S), .reset(or_3_out));  // open: Qn, preset
  and and_3 (and_3_out, ~PoR, d_ff_2_q);  // AND_Gate
  or or_3 (or_3_out, not_2_out, PoR);
  not not_2 (not_2_out, d_ff_3_q);
endmodule

module zero_three (
  input  E1,
  input  E0,
  input  Oi,
  output O,
  output S1,
  output S0
);

  wire nand_1_out, nand_2_out, nand_3_out, nand_4_out, nand_5_out, nand_6_out, nand_8_out, nand_9_out,
       nand_10_out, nand_11_out, nand_12_out;

  nand nand_1 (nand_1_out, Oi, E1, E0);
  nand nand_2 (nand_2_out, Oi, Oi);
  nand nand_3 (nand_3_out, E0, E0);
  nand nand_4 (nand_4_out, E1, E1);
  nand nand_5 (nand_5_out, Oi, Oi);
  nand nand_6 (nand_6_out, E0, E0);
  nand nand_7 (O, nand_1_out, nand_1_out);
  nand nand_8 (nand_8_out, nand_2_out, E1);
  nand nand_9 (nand_9_out, E1, nand_3_out);
  nand nand_10 (nand_10_out, Oi, nand_4_out, E0);
  nand nand_11 (nand_11_out, nand_5_out, E0);
  nand nand_12 (nand_12_out, Oi, nand_6_out);
  nand nand_13 (S1, nand_8_out, nand_9_out, nand_10_out);
  nand nand_14 (S0, nand_11_out, nand_12_out);
endmodule

module zero_nine_1T (
  input  C,
  input  E3,
  input  E2,
  input  E1,
  input  E0,
  input  Oi,
  output O,
  output S3,
  output S2,
  output S1,
  output S0
);

  wire nand_1_out, nand_2_out, nand_3_out, nand_4_out, nand_5_out, nand_6_out, nand_7_out, nand_8_out,
       nand_9_out, nand_10_out, nand_11_out, nand_12_out, nand_13_out, nand_14_out, nand_15_out, nand_16_out,
       nand_18_out, nand_19_out, nand_20_out, nand_21_out, nand_22_out, nand_23_out, nand_24_out,
       nand_25_out, nand_26_out, nand_27_out, nand_28_out, nand_29_out, nand_30_out, nand_31_out;

  nand nand_1 (nand_1_out, Oi, E3, E0);
  nand nand_2 (nand_2_out, C, Oi, E0);
  nand nand_3 (nand_3_out, C, Oi, E1);
  nand nand_4 (nand_4_out, Oi, Oi);
  nand nand_5 (nand_5_out, E0, E0);
  nand nand_6 (nand_6_out, Oi, Oi);
  nand nand_7 (nand_7_out, E1, E1);
  nand nand_8 (nand_8_out, E0, E0);
  nand nand_9 (nand_9_out, E2, E2);
  nand nand_10 (nand_10_out, Oi, Oi);
  nand nand_11 (nand_11_out, E0, E0);
  nand nand_12 (nand_12_out, C, C);
  nand nand_13 (nand_13_out, E3, E3);
  nand nand_14 (nand_14_out, E1, E1);
  nand nand_15 (nand_15_out, Oi, Oi);
  nand nand_16 (nand_16_out, E0, E0);
  nand nand_17 (O, nand_1_out, nand_2_out, nand_3_out);
  nand nand_18 (nand_18_out, nand_4_out, E3);
  nand nand_19 (nand_19_out, E3, nand_5_out);
  nand nand_20 (nand_20_out, Oi, E2, E1, E0);
  nand nand_21 (nand_21_out, nand_6_out, E2);
  nand nand_22 (nand_22_out, E2, nand_7_out);
  nand nand_23 (nand_23_out, E2, nand_8_out);
  nand nand_24 (nand_24_out, Oi, nand_9_out, E1, E0);
  nand nand_25 (nand_25_out, nand_10_out, E1);
  nand nand_26 (nand_26_out, E1, nand_11_out);
  nand nand_27 (nand_27_out, nand_12_out, Oi, nand_13_out, nand_14_out, E0);
  nand nand_28 (nand_28_out, C, E1);
  nand nand_29 (nand_29_out, nand_15_out, E0);
  nand nand_30 (nand_30_out, Oi, nand_16_out);
  nand nand_31 (nand_31_out, C, Oi, E1);
  nand nand_32 (S3, nand_18_out, nand_19_out, nand_20_out);
  nand nand_33 (S0, nand_29_out, nand_30_out, nand_31_out);
  nand nand_34 (S2, nand_21_out, nand_22_out, nand_23_out, nand_24_out);
  nand nand_35 (S1, nand_25_out, nand_26_out, nand_27_out, nand_28_out);
endmodule

module set (
  input  E3,
  input  E2,
  input  E1,
  input  E0,
  input  [3:0] set_val,
  input  set_on,
  output S3,
  output S2,
  output S1,
  output S0
);

  Multiplexer #(.enable("false")) multiplexer_1 (.in0(E3), .in1(set_val[3]), .out(S3), .sel(set_on));
  Multiplexer #(.enable("false")) multiplexer_2 (.in0(E2), .in1(set_val[2]), .out(S2), .sel(set_on));
  Multiplexer #(.enable("false")) multiplexer_3 (.in0(E1), .in1(set_val[1]), .out(S1), .sel(set_on));
  Multiplexer #(.enable("false")) multiplexer_4 (.in0(E0), .in1(set_val[0]), .out(S0), .sel(set_on));
endmodule

module action_done (
  input  A_in,
  input  B_in,
  input  change_done,
  input  PoR,
  output A,
  output B,
  output action_done
);

  wire and_1_out, or_1_out, or_2_out, or_3_out;

  or or_1 (or_1_out, change_done, PoR);
  or or_2 (or_2_out, A_in, B_in);
  and and_1 (and_1_out, or_2_out, ~or_1_out);  // AND_Gate
  or or_3 (or_3_out, or_1_out, PoR);
  D_Flip_Flop d_ff_1 (.Q(action_done), .preset(and_1_out), .reset(or_3_out));  // open: D, clk, Qn

  assign A = A_in;
  assign B = B_in;
endmodule

module buttons (
  input  A,
  input  B,
  input  Clk,
  input  PoR,
  output single_A,
  output single_B,
  output double
);

  wire and_1_out, and_2_out, and_3_out, and_4_out, counter_1_carry, counter_2_carry, d_ff_1_q, d_ff_2_q,
       d_ff_3_q, d_ff_4_q, d_ff_5_q, d_ff_6_q, not_1_out, not_2_out, not_3_out, not_4_out, or_1_out,
       or_2_out, or_3_out, or_4_out, or_5_out, or_6_out, or_7_out, switch_debouncing_1_s,
       switch_debouncing_2_s, xor_1_out, xor_2_out;

  switch_debouncing switch_debouncing_1 (.PoR(PoR), .E(A), .Clk(Clk), .S(switch_debouncing_1_s));
  switch_debouncing switch_debouncing_2 (.PoR(PoR), .E(B), .Clk(Clk), .S(switch_debouncing_2_s));
  D_Flip_Flop d_ff_1 (.D(and_1_out), .clk(Clk), .Q(d_ff_1_q));  // open: Qn, preset, reset
  and and_1 (and_1_out, switch_debouncing_1_s, ~PoR);  // AND_Gate
  D_Flip_Flop d_ff_2 (.D(and_2_out), .clk(Clk), .Q(d_ff_2_q));  // open: Qn, preset, reset
  and and_2 (and_2_out, switch_debouncing_2_s, ~PoR);  // AND_Gate
  D_Flip_Flop d_ff_3 (.D(and_3_out), .clk(Clk), .Q(d_ff_3_q));  // open: Qn, preset, reset
  and and_3 (and_3_out, d_ff_1_q, ~PoR);  // AND_Gate
  D_Flip_Flop d_ff_4 (.D(and_4_out), .clk(Clk), .Q(d_ff_4_q));  // open: Qn, preset, reset
  and and_4 (and_4_out, d_ff_2_q, ~PoR);  // AND_Gate
  xor xor_1 (xor_1_out, d_ff_3_q, d_ff_1_q);
  xor xor_2 (xor_2_out, d_ff_4_q, d_ff_2_q);
  or or_1 (or_1_out, PoR, double);
  or or_2 (or_2_out, or_1_out, xor_1_out);
  or or_3 (or_3_out, or_1_out, xor_2_out);
  Counter #(.width(7), .max('h7f)) counter_1 (
    .clr(or_2_out), .clk(Clk), .carry(counter_1_carry));  // open: load, up, count, D, Q
  Counter #(.width(7), .max('h7f)) counter_2 (
    .clr(or_3_out), .clk(Clk), .carry(counter_2_carry));  // open: load, up, count, D, Q
  not not_1 (not_1_out, switch_debouncing_1_s);
  not not_2 (not_2_out, switch_debouncing_2_s);
  D_Flip_Flop d_ff_5 (.Q(d_ff_5_q), .preset(counter_1_carry), .reset(or_4_out));  // open: D, clk, Qn
  or or_4 (or_4_out, not_1_out, PoR);
  D_Flip_Flop d_ff_6 (.Q(d_ff_6_q), .preset(counter_2_carry), .reset(or_5_out));  // open: D, clk, Qn
  or or_5 (or_5_out, not_2_out, PoR);
  not not_3 (not_3_out, d_ff_5_q);
  not not_4 (not_4_out, d_ff_6_q);
  D_Flip_Flop d_ff_7 (.D(d_ff_3_q), .clk(Clk), .Q(single_A), .reset(or_6_out));  // open: Qn, preset
  or or_6 (or_6_out, not_3_out, PoR);
  D_Flip_Flop d_ff_8 (.D(d_ff_4_q), .clk(Clk), .Q(single_B), .reset(or_7_out));  // open: Qn, preset
  or or_7 (or_7_out, not_4_out, PoR);
  and and_5 (double, switch_debouncing_1_s, switch_debouncing_2_s, ~single_A, ~single_B);  // AND_Gate
  Counter #(.width(4), .max('hf)) counter_3 ();  // open: load, D, count, Q, carry, clk, clr
endmodule

module months (
  input  Oi,
  input  [3:0] set_D,
  input  set_D_on,
  input  [3:0] set_U,
  input  set_U_on,
  input  Clk,
  input  PoR,
  output [3:0] Mo1,
  output [3:0] Mo0,
  output [1:0] Output_bus_1
);

  wire and_1_out, and_2_out, and_3_out, and_4_out, and_5_out, and_6_out, and_7_out, and_8_out, and_9_out,
       not_2_out, not_3_out, not_4_out, not_5_out, not_6_out, or_1_out, or_2_out, set_1_s0, set_2_s0,
       set_2_s1, set_2_s2, set_2_s3, T, zero_nine_start_one_end_two_1_o, zero_nine_start_one_end_two_1_s0,
       zero_nine_start_one_end_two_1_s1, zero_nine_start_one_end_two_1_s2, zero_nine_start_one_end_two_1_s3,
       zero_one_1_s;

  and and_1 (and_1_out, ~zero_nine_start_one_end_two_1_s0, ~zero_nine_start_one_end_two_1_s1, ~zero_nine_start_one_end_two_1_s2, ~zero_nine_start_one_end_two_1_s3);  // AND_Gate
  zero_one zero_one_1 (.E(Mo1[0]), .Oi(zero_nine_start_one_end_two_1_o), .S(zero_one_1_s));  // open: O
  and and_2 (and_2_out, and_1_out, T);
  zero_nine_start_one_end_two zero_nine_start_one_end_two_1 (
    .C(Mo1[0]), .Oi(Oi), .E3(Mo0[3]), .E2(Mo0[2]), .E1(Mo0[1]), .E0(Mo0[0]),
    .O(zero_nine_start_one_end_two_1_o), .S3(zero_nine_start_one_end_two_1_s3),
    .S2(zero_nine_start_one_end_two_1_s2), .S1(zero_nine_start_one_end_two_1_s1),
    .S0(zero_nine_start_one_end_two_1_s0));
  not not_1 (T, zero_one_1_s);
  and and_3 (and_3_out, zero_nine_start_one_end_two_1_s3, ~and_2_out);  // AND_Gate
  and and_4 (and_4_out, zero_nine_start_one_end_two_1_s2, ~and_2_out);  // AND_Gate
  and and_5 (and_5_out, zero_nine_start_one_end_two_1_s1, ~and_2_out);  // AND_Gate
  or or_1 (or_1_out, zero_nine_start_one_end_two_1_s0, and_2_out);
  set set_1 (
    .E3(1'b0), .E2(1'b0), .E1(1'b0), .E0(zero_one_1_s), .set_val(set_D), .set_on(set_D_on), .S0(set_1_s0));  // open: S3, S2, S1
  set set_2 (
    .E3(and_3_out), .E2(and_4_out), .E1(and_5_out), .E0(or_1_out), .set_val(set_U), .set_on(set_U_on),
    .S3(set_2_s3), .S2(set_2_s2), .S1(set_2_s1), .S0(set_2_s0));
  and and_6 (and_6_out, set_1_s0, ~PoR);  // AND_Gate
  not not_2 (not_2_out, and_6_out);
  and and_7 (and_7_out, set_2_s3, ~PoR);  // AND_Gate
  not not_3 (not_3_out, and_7_out);
  and and_8 (and_8_out, set_2_s2, ~PoR);  // AND_Gate
  not not_4 (not_4_out, and_8_out);
  and and_9 (and_9_out, set_2_s1, ~PoR);  // AND_Gate
  not not_5 (not_5_out, and_9_out);
  or or_2 (or_2_out, set_2_s0, PoR);
  not not_6 (not_6_out, or_2_out);
  S_R_Flip_Flop s_r_ff_1 (.S(and_6_out), .R(not_2_out), .clk(Clk), .Q(Mo1[0]), .reset(PoR));  // open: Qn, preset
  S_R_Flip_Flop s_r_ff_2 (.S(and_7_out), .R(not_3_out), .clk(Clk), .Q(Mo0[3]), .reset(PoR));  // open: Qn, preset
  S_R_Flip_Flop s_r_ff_3 (.S(and_8_out), .R(not_4_out), .clk(Clk), .Q(Mo0[2]), .reset(PoR));  // open: Qn, preset
  S_R_Flip_Flop s_r_ff_4 (.S(and_9_out), .R(not_5_out), .clk(Clk), .Q(Mo0[1]), .reset(PoR));  // open: Qn, preset
  S_R_Flip_Flop s_r_ff_5 (.S(or_2_out), .R(not_6_out), .clk(Clk), .Q(Mo0[0]), .preset(PoR));  // open: reset, Qn
  month_select month_select_1 (
    .E4(Mo1[0]), .E3(Mo0[3]), .E2(Mo0[2]), .E1(Mo0[1]), .E0(Mo0[0]), .S1(Output_bus_1[1]),
    .S0(Output_bus_1[0]));

  assign Mo1[3:1] = 3'b000;

  // Notes on the sheet:
  //   00 = 31 jours
  //   01 = 30 jours
  //   10 = 28 jours
endmodule

module one_thirtyone (
  input  Oi,
  input  [3:0] set_D,
  input  set_D_on,
  input  [3:0] set_U,
  input  set_U_on,
  input  Clk,
  input  PoR,
  output O,
  output [3:0] N1,
  output [3:0] N0
);

  wire and_1_out, and_2_out, and_3_out, and_5_out, and_6_out, and_7_out, and_8_out, and_9_out, and_10_out,
       and_11_out, and_12_out, not_1_out, not_2_out, not_3_out, not_4_out, not_5_out, not_6_out, or_1_out,
       or_2_out, set_1_s0, set_1_s1, set_2_s0, set_2_s1, set_2_s2, set_2_s3, T,
       zero_nine_start_one_end_one_1_o, zero_nine_start_one_end_one_1_s0, zero_nine_start_one_end_one_1_s1,
       zero_nine_start_one_end_one_1_s2, zero_nine_start_one_end_one_1_s3, zero_three_1_s0, zero_three_1_s1;

  and and_1 (and_1_out, N1[0], N1[1]);
  and and_2 (and_2_out, ~zero_nine_start_one_end_one_1_s0, ~zero_nine_start_one_end_one_1_s1, ~zero_nine_start_one_end_one_1_s2, ~zero_nine_start_one_end_one_1_s3);  // AND_Gate
  and and_3 (and_3_out, and_2_out, T);
  zero_three zero_three_1 (
    .E1(N1[1]), .E0(N1[0]), .Oi(zero_nine_start_one_end_one_1_o), .O(O), .S1(zero_three_1_s1),
    .S0(zero_three_1_s0));
  zero_nine_start_one_end_one zero_nine_start_one_end_one_1 (
    .C(and_1_out), .Oi(Oi), .E3(N0[3]), .E2(N0[2]), .E1(N0[1]), .E0(N0[0]),
    .O(zero_nine_start_one_end_one_1_o), .S3(zero_nine_start_one_end_one_1_s3),
    .S2(zero_nine_start_one_end_one_1_s2), .S1(zero_nine_start_one_end_one_1_s1),
    .S0(zero_nine_start_one_end_one_1_s0));
  and and_4 (T, ~zero_three_1_s1, ~zero_three_1_s0);  // AND_Gate
  and and_5 (and_5_out, zero_nine_start_one_end_one_1_s3, ~and_3_out);  // AND_Gate
  and and_6 (and_6_out, zero_nine_start_one_end_one_1_s2, ~and_3_out);  // AND_Gate
  and and_7 (and_7_out, zero_nine_start_one_end_one_1_s1, ~and_3_out);  // AND_Gate
  or or_1 (or_1_out, zero_nine_start_one_end_one_1_s0, and_3_out);
  set set_1 (
    .E3(1'b0), .E2(1'b0), .E1(zero_three_1_s1), .E0(zero_three_1_s0), .set_val(set_D), .set_on(set_D_on),
    .S1(set_1_s1), .S0(set_1_s0));  // open: S3, S2
  set set_2 (
    .E3(and_5_out), .E2(and_6_out), .E1(and_7_out), .E0(or_1_out), .set_val(set_U), .set_on(set_U_on),
    .S3(set_2_s3), .S2(set_2_s2), .S1(set_2_s1), .S0(set_2_s0));
  and and_8 (and_8_out, set_1_s1, ~PoR);  // AND_Gate
  and and_9 (and_9_out, set_1_s0, ~PoR);  // AND_Gate
  and and_10 (and_10_out, set_2_s3, ~PoR);  // AND_Gate
  and and_11 (and_11_out, set_2_s2, ~PoR);  // AND_Gate
  and and_12 (and_12_out, set_2_s1, ~PoR);  // AND_Gate
  or or_2 (or_2_out, set_2_s0, PoR);
  not not_1 (not_1_out, and_8_out);
  not not_2 (not_2_out, and_9_out);
  not not_3 (not_3_out, and_10_out);
  not not_4 (not_4_out, and_11_out);
  not not_5 (not_5_out, and_12_out);
  not not_6 (not_6_out, or_2_out);
  S_R_Flip_Flop s_r_ff_1 (.S(and_8_out), .R(not_1_out), .clk(Clk), .Q(N1[1]), .reset(PoR));  // open: Qn, preset
  S_R_Flip_Flop s_r_ff_2 (.S(and_9_out), .R(not_2_out), .clk(Clk), .Q(N1[0]), .reset(PoR));  // open: Qn, preset
  S_R_Flip_Flop s_r_ff_3 (.S(and_10_out), .R(not_3_out), .clk(Clk), .Q(N0[3]), .reset(PoR));  // open: Qn, preset
  S_R_Flip_Flop s_r_ff_4 (.S(and_11_out), .R(not_4_out), .clk(Clk), .Q(N0[2]), .reset(PoR));  // open: Qn, preset
  S_R_Flip_Flop s_r_ff_5 (.S(and_12_out), .R(not_5_out), .clk(Clk), .Q(N0[1]), .reset(PoR));  // open: Qn, preset
  S_R_Flip_Flop s_r_ff_6 (.S(or_2_out), .R(not_6_out), .clk(Clk), .Q(N0[0]), .preset(PoR));  // open: reset, Qn

  assign N1[3:2] = 2'b00;
endmodule

module zero_nine_start_one_end_one (
  input  C,
  input  Oi,
  input  E3,
  input  E2,
  input  E1,
  input  E0,
  output O,
  output S3,
  output S2,
  output S1,
  output S0
);

  wire nand_1_out, nand_2_out, nand_3_out, nand_4_out, nand_5_out, nand_6_out, nand_7_out, nand_8_out,
       nand_9_out, nand_10_out, nand_11_out, nand_12_out, nand_13_out, nand_14_out, nand_15_out, nand_16_out,
       nand_17_out, nand_18_out, nand_19_out, nand_20_out, nand_21_out, nand_22_out, nand_23_out,
       nand_24_out, nand_26_out, nand_27_out, nand_28_out, nand_29_out, nand_30_out, nand_31_out,
       nand_32_out, nand_33_out, nand_34_out, nand_35_out, nand_36_out, nand_37_out, nand_38_out;

  nand nand_1 (nand_1_out, Oi, E3, E0);
  nand nand_2 (nand_2_out, C, Oi, E0);
  nand nand_3 (nand_3_out, C, Oi, E1);
  nand nand_4 (nand_4_out, C, Oi, E2);
  nand nand_5 (nand_5_out, C, Oi, E3);
  nand nand_6 (nand_6_out, C, C);
  nand nand_7 (nand_7_out, E0, E0);
  nand nand_8 (nand_8_out, Oi, Oi);
  nand nand_9 (nand_9_out, C, C);
  nand nand_10 (nand_10_out, C, C);
  nand nand_11 (nand_11_out, E1, E1);
  nand nand_12 (nand_12_out, C, C);
  nand nand_13 (nand_13_out, E0, E0);
  nand nand_14 (nand_14_out, Oi, Oi);
  nand nand_15 (nand_15_out, C, C);
  nand nand_16 (nand_16_out, E2, E2);
  nand nand_17 (nand_17_out, C, C);
  nand nand_18 (nand_18_out, E0, E0);
  nand nand_19 (nand_19_out, Oi, Oi);
  nand nand_20 (nand_20_out, C, C);
  nand nand_21 (nand_21_out, E3, E3);
  nand nand_22 (nand_22_out, E1, E1);
  nand nand_23 (nand_23_out, Oi, Oi);
  nand nand_24 (nand_24_out, E0, E0);
  nand nand_25 (O, nand_1_out, nand_2_out, nand_3_out, nand_4_out, nand_5_out);
  nand nand_26 (nand_26_out, nand_6_out, E3, nand_7_out);
  nand nand_27 (nand_27_out, nand_8_out, E3);
  nand nand_28 (nand_28_out, nand_9_out, Oi, E2, E1, E0);
  nand nand_29 (nand_29_out, nand_10_out, E2, nand_11_out);
  nand nand_30 (nand_30_out, nand_12_out, E2, nand_13_out);
  nand nand_31 (nand_31_out, nand_14_out, E2);
  nand nand_32 (nand_32_out, nand_15_out, Oi, nand_16_out, E1, E0);
  nand nand_33 (nand_33_out, nand_17_out, E1, nand_18_out);
  nand nand_34 (nand_34_out, nand_19_out, E1);
  nand nand_35 (nand_35_out, nand_20_out, Oi, nand_21_out, nand_22_out, E0);
  nand nand_36 (nand_36_out, nand_23_out, E0);
  nand nand_37 (nand_37_out, Oi, nand_24_out);
  nand nand_38 (nand_38_out, C, Oi);
  nand nand_39 (S3, nand_26_out, nand_27_out, nand_28_out);
  nand nand_40 (S1, nand_33_out, nand_34_out, nand_35_out);
  nand nand_41 (S0, nand_36_out, nand_37_out, nand_38_out);
  nand nand_42 (S2, nand_29_out, nand_30_out, nand_31_out, nand_32_out);
endmodule

module zero_nine_start_one_end_zero (
  input  C,
  input  Oi,
  input  E3,
  input  E2,
  input  E1,
  input  E0,
  output O,
  output S3,
  output S2,
  output S1,
  output S0
);

  wire nand_1_out, nand_2_out, nand_3_out, nand_4_out, nand_5_out, nand_6_out, nand_7_out, nand_8_out,
       nand_9_out, nand_10_out, nand_11_out, nand_12_out, nand_13_out, nand_14_out, nand_15_out, nand_16_out,
       nand_17_out, nand_18_out, nand_19_out, nand_20_out, nand_21_out, nand_23_out, nand_24_out,
       nand_25_out, nand_26_out, nand_27_out, nand_28_out, nand_29_out, nand_30_out, nand_31_out,
       nand_32_out, nand_33_out, nand_34_out, nand_35_out;

  nand nand_1 (nand_1_out, Oi, E3, E0);
  nand nand_2 (nand_2_out, C, Oi);
  nand nand_3 (nand_3_out, C, C);
  nand nand_4 (nand_4_out, E0, E0);
  nand nand_5 (nand_5_out, Oi, Oi);
  nand nand_6 (nand_6_out, C, C);
  nand nand_7 (nand_7_out, C, C);
  nand nand_8 (nand_8_out, E1, E1);
  nand nand_9 (nand_9_out, C, C);
  nand nand_10 (nand_10_out, E0, E0);
  nand nand_11 (nand_11_out, Oi, Oi);
  nand nand_12 (nand_12_out, C, C);
  nand nand_13 (nand_13_out, E2, E2);
  nand nand_14 (nand_14_out, C, C);
  nand nand_15 (nand_15_out, E0, E0);
  nand nand_16 (nand_16_out, Oi, Oi);
  nand nand_17 (nand_17_out, C, C);
  nand nand_18 (nand_18_out, E3, E3);
  nand nand_19 (nand_19_out, E1, E1);
  nand nand_20 (nand_20_out, Oi, Oi);
  nand nand_21 (nand_21_out, E0, E0);
  nand nand_22 (O, nand_1_out, nand_2_out);
  nand nand_23 (nand_23_out, nand_3_out, E3, nand_4_out);
  nand nand_24 (nand_24_out, nand_5_out, E3);
  nand nand_25 (nand_25_out, nand_6_out, Oi, E2, E1, E0);
  nand nand_26 (nand_26_out, nand_7_out, E2, nand_8_out);
  nand nand_27 (nand_27_out, nand_9_out, E2, nand_10_out);
  nand nand_28 (nand_28_out, nand_11_out, E2);
  nand nand_29 (nand_29_out, nand_12_out, Oi, nand_13_out, E1, E0);
  nand nand_30 (nand_30_out, nand_14_out, E1, nand_15_out);
  nand nand_31 (nand_31_out, nand_16_out, E1);
  nand nand_32 (nand_32_out, nand_17_out, Oi, nand_18_out, nand_19_out, E0);
  nand nand_33 (nand_33_out, nand_20_out, E0);
  nand nand_34 (nand_34_out, Oi, nand_21_out);
  nand nand_35 (nand_35_out, C, Oi);
  nand nand_36 (S3, nand_23_out, nand_24_out, nand_25_out);
  nand nand_37 (S1, nand_30_out, nand_31_out, nand_32_out);
  nand nand_38 (S0, nand_33_out, nand_34_out, nand_35_out);
  nand nand_39 (S2, nand_26_out, nand_27_out, nand_28_out, nand_29_out);
endmodule

module one_thirty (
  input  Oi,
  input  [3:0] set_D,
  input  set_D_on,
  input  [3:0] set_U,
  input  set_U_on,
  input  Clk,
  input  PoR,
  output O,
  output [3:0] N1,
  output [3:0] N0
);

  wire and_1_out, and_2_out, and_3_out, and_5_out, and_6_out, and_7_out, and_8_out, and_9_out, and_10_out,
       and_11_out, and_12_out, not_1_out, not_2_out, not_3_out, not_4_out, not_5_out, not_6_out, or_1_out,
       or_2_out, set_1_s0, set_1_s1, set_2_s0, set_2_s1, set_2_s2, set_2_s3, T,
       zero_nine_start_one_end_zero_1_o, zero_nine_start_one_end_zero_1_s0,
       zero_nine_start_one_end_zero_1_s1, zero_nine_start_one_end_zero_1_s2,
       zero_nine_start_one_end_zero_1_s3, zero_three_1_s0, zero_three_1_s1;

  and and_1 (and_1_out, N1[0], N1[1]);
  and and_2 (and_2_out, ~zero_nine_start_one_end_zero_1_s0, ~zero_nine_start_one_end_zero_1_s1, ~zero_nine_start_one_end_zero_1_s2, ~zero_nine_start_one_end_zero_1_s3);  // AND_Gate
  and and_3 (and_3_out, and_2_out, T);
  zero_three zero_three_1 (
    .E1(N1[1]), .E0(N1[0]), .Oi(zero_nine_start_one_end_zero_1_o), .O(O), .S1(zero_three_1_s1),
    .S0(zero_three_1_s0));
  zero_nine_start_one_end_zero zero_nine_start_one_end_zero_1 (
    .C(and_1_out), .Oi(Oi), .E3(N0[3]), .E2(N0[2]), .E1(N0[1]), .E0(N0[0]),
    .O(zero_nine_start_one_end_zero_1_o), .S3(zero_nine_start_one_end_zero_1_s3),
    .S2(zero_nine_start_one_end_zero_1_s2), .S1(zero_nine_start_one_end_zero_1_s1),
    .S0(zero_nine_start_one_end_zero_1_s0));
  and and_4 (T, ~zero_three_1_s1, ~zero_three_1_s0);  // AND_Gate
  and and_5 (and_5_out, zero_nine_start_one_end_zero_1_s3, ~and_3_out);  // AND_Gate
  and and_6 (and_6_out, zero_nine_start_one_end_zero_1_s2, ~and_3_out);  // AND_Gate
  and and_7 (and_7_out, zero_nine_start_one_end_zero_1_s1, ~and_3_out);  // AND_Gate
  or or_1 (or_1_out, zero_nine_start_one_end_zero_1_s0, and_3_out);
  set set_1 (
    .E3(1'b0), .E2(1'b0), .E1(zero_three_1_s1), .E0(zero_three_1_s0), .set_val(set_D), .set_on(set_D_on),
    .S1(set_1_s1), .S0(set_1_s0));  // open: S3, S2
  set set_2 (
    .E3(and_5_out), .E2(and_6_out), .E1(and_7_out), .E0(or_1_out), .set_val(set_U), .set_on(set_U_on),
    .S3(set_2_s3), .S2(set_2_s2), .S1(set_2_s1), .S0(set_2_s0));
  and and_8 (and_8_out, set_1_s1, ~PoR);  // AND_Gate
  and and_9 (and_9_out, set_1_s0, ~PoR);  // AND_Gate
  and and_10 (and_10_out, set_2_s3, ~PoR);  // AND_Gate
  and and_11 (and_11_out, set_2_s2, ~PoR);  // AND_Gate
  and and_12 (and_12_out, set_2_s1, ~PoR);  // AND_Gate
  or or_2 (or_2_out, set_2_s0, PoR);
  not not_1 (not_1_out, and_8_out);
  not not_2 (not_2_out, and_9_out);
  not not_3 (not_3_out, and_10_out);
  not not_4 (not_4_out, and_11_out);
  not not_5 (not_5_out, and_12_out);
  not not_6 (not_6_out, or_2_out);
  S_R_Flip_Flop s_r_ff_1 (.S(and_8_out), .R(not_1_out), .clk(Clk), .Q(N1[1]), .reset(PoR));  // open: Qn, preset
  S_R_Flip_Flop s_r_ff_2 (.S(and_9_out), .R(not_2_out), .clk(Clk), .Q(N1[0]), .reset(PoR));  // open: Qn, preset
  S_R_Flip_Flop s_r_ff_3 (.S(and_10_out), .R(not_3_out), .clk(Clk), .Q(N0[3]), .reset(PoR));  // open: Qn, preset
  S_R_Flip_Flop s_r_ff_4 (.S(and_11_out), .R(not_4_out), .clk(Clk), .Q(N0[2]), .reset(PoR));  // open: Qn, preset
  S_R_Flip_Flop s_r_ff_5 (.S(and_12_out), .R(not_5_out), .clk(Clk), .Q(N0[1]), .reset(PoR));  // open: Qn, preset
  S_R_Flip_Flop s_r_ff_6 (.S(or_2_out), .R(not_6_out), .clk(Clk), .Q(N0[0]), .preset(PoR));  // open: reset, Qn

  assign N1[3:2] = 2'b00;
endmodule

module zero_one (
  input  E,
  input  Oi,
  output O,
  output S
);

  wire nand_1_out, nand_2_out, nand_3_out, nand_5_out, nand_6_out;

  nand nand_1 (nand_1_out, Oi, E);
  nand nand_2 (nand_2_out, E, E);
  nand nand_3 (nand_3_out, Oi, Oi);
  nand nand_4 (O, nand_1_out, nand_1_out);
  nand nand_5 (nand_5_out, nand_2_out, Oi);
  nand nand_6 (nand_6_out, E, nand_3_out);
  nand nand_7 (S, nand_5_out, nand_6_out);
endmodule

module zero_nine_start_one_end_two (
  input  C,
  input  Oi,
  input  E3,
  input  E2,
  input  E1,
  input  E0,
  output O,
  output S3,
  output S2,
  output S1,
  output S0
);

  wire nand_1_out, nand_2_out, nand_3_out, nand_4_out, nand_5_out, nand_6_out, nand_7_out, nand_8_out,
       nand_9_out, nand_10_out, nand_11_out, nand_12_out, nand_13_out, nand_14_out, nand_15_out, nand_16_out,
       nand_17_out, nand_18_out, nand_19_out, nand_20_out, nand_21_out, nand_22_out, nand_23_out,
       nand_24_out, nand_25_out, nand_26_out, nand_27_out, nand_28_out, nand_29_out, nand_30_out,
       nand_31_out, nand_33_out, nand_34_out, nand_35_out, nand_36_out, nand_37_out, nand_38_out,
       nand_39_out, nand_40_out, nand_41_out, nand_42_out, nand_43_out, nand_44_out, nand_45_out, nand_46_out;

  nand nand_1 (nand_1_out, Oi, E3, E0);
  nand nand_2 (nand_2_out, C, Oi, E1);
  nand nand_3 (nand_3_out, C, Oi, E2);
  nand nand_4 (nand_4_out, C, Oi, E3);
  nand nand_5 (nand_5_out, C, C);
  nand nand_6 (nand_6_out, E0, E0);
  nand nand_7 (nand_7_out, Oi, Oi);
  nand nand_8 (nand_8_out, C, C);
  nand nand_9 (nand_9_out, C, C);
  nand nand_10 (nand_10_out, E1, E1);
  nand nand_11 (nand_11_out, C, C);
  nand nand_12 (nand_12_out, E0, E0);
  nand nand_13 (nand_13_out, Oi, Oi);
  nand nand_14 (nand_14_out, C, C);
  nand nand_15 (nand_15_out, E2, E2);
  nand nand_16 (nand_16_out, C, C);
  nand nand_17 (nand_17_out, E0, E0);
  nand nand_18 (nand_18_out, Oi, Oi);
  nand nand_19 (nand_19_out, C, C);
  nand nand_20 (nand_20_out, E3, E3);
  nand nand_21 (nand_21_out, E1, E1);
  nand nand_22 (nand_22_out, E3, E3);
  nand nand_23 (nand_23_out, E2, E2);
  nand nand_24 (nand_24_out, E1, E1);
  nand nand_25 (nand_25_out, Oi, Oi);
  nand nand_26 (nand_26_out, C, C);
  nand nand_27 (nand_27_out, E0, E0);
  nand nand_28 (nand_28_out, E3, E3);
  nand nand_29 (nand_29_out, E2, E2);
  nand nand_30 (nand_30_out, E1, E1);
  nand nand_31 (nand_31_out, E0, E0);
  nand nand_32 (O, nand_1_out, nand_2_out, nand_3_out, nand_4_out);
  nand nand_33 (nand_33_out, nand_5_out, E3, nand_6_out);
  nand nand_34 (nand_34_out, nand_7_out, E3);
  nand nand_35 (nand_35_out, nand_8_out, Oi, E2, E1, E0);
  nand nand_36 (nand_36_out, nand_9_out, E2, nand_10_out);
  nand nand_37 (nand_37_out, nand_11_out, E2, nand_12_out);
  nand nand_38 (nand_38_out, nand_13_out, E2);
  nand nand_39 (nand_39_out, nand_14_out, Oi, nand_15_out, E1, E0);
  nand nand_40 (nand_40_out, nand_16_out, E1, nand_17_out);
  nand nand_41 (nand_41_out, nand_18_out, E1);
  nand nand_42 (nand_42_out, nand_19_out, Oi, nand_20_out, nand_21_out, E0);
  nand nand_43 (nand_43_out, Oi, nand_22_out, nand_23_out, nand_24_out, E0);
  nand nand_44 (nand_44_out, nand_25_out, E0);
  nand nand_45 (nand_45_out, nand_26_out, Oi, nand_27_out);
  nand nand_46 (nand_46_out, Oi, nand_28_out, nand_29_out, nand_30_out, nand_31_out);
  nand nand_47 (S3, nand_33_out, nand_34_out, nand_35_out);
  nand nand_48 (S0, nand_44_out, nand_45_out, nand_46_out);
  nand nand_49 (S2, nand_36_out, nand_37_out, nand_38_out, nand_39_out);
  nand nand_50 (S1, nand_40_out, nand_41_out, nand_42_out, nand_43_out);
endmodule

module zero_nine_start_one_end_eight (
  input  E,
  input  Oi,
  input  E3,
  input  E2,
  input  E1,
  input  E0,
  output O,
  output S3,
  output S2,
  output S1,
  output S0
);

  wire nand_1_out, nand_2_out, nand_3_out, nand_4_out, nand_5_out, nand_6_out, nand_7_out, nand_8_out,
       nand_9_out, nand_10_out, nand_11_out, nand_12_out, nand_13_out, nand_14_out, nand_15_out, nand_16_out,
       nand_17_out, nand_18_out, nand_20_out, nand_21_out, nand_22_out, nand_23_out, nand_24_out,
       nand_25_out, nand_26_out, nand_27_out, nand_28_out, nand_29_out, nand_30_out, nand_31_out, nand_32_out;

  nand nand_1 (nand_1_out, Oi, E3, E0);
  nand nand_2 (nand_2_out, E, Oi, E3);
  nand nand_3 (nand_3_out, E, E);
  nand nand_4 (nand_4_out, E0, E0);
  nand nand_5 (nand_5_out, Oi, Oi);
  nand nand_6 (nand_6_out, Oi, Oi);
  nand nand_7 (nand_7_out, E1, E1);
  nand nand_8 (nand_8_out, E0, E0);
  nand nand_9 (nand_9_out, E2, E2);
  nand nand_10 (nand_10_out, Oi, Oi);
  nand nand_11 (nand_11_out, E0, E0);
  nand nand_12 (nand_12_out, E3, E3);
  nand nand_13 (nand_13_out, E1, E1);
  nand nand_14 (nand_14_out, Oi, Oi);
  nand nand_15 (nand_15_out, E, E);
  nand nand_16 (nand_16_out, E0, E0);
  nand nand_17 (nand_17_out, E3, E3);
  nand nand_18 (nand_18_out, E0, E0);
  nand nand_19 (O, nand_1_out, nand_2_out);
  nand nand_20 (nand_20_out, nand_3_out, E3, nand_4_out);
  nand nand_21 (nand_21_out, nand_5_out, E3);
  nand nand_22 (nand_22_out, Oi, E2, E1, E0);
  nand nand_23 (nand_23_out, nand_6_out, E2);
  nand nand_24 (nand_24_out, E2, nand_7_out);
  nand nand_25 (nand_25_out, E2, nand_8_out);
  nand nand_26 (nand_26_out, Oi, nand_9_out, E1, E0);
  nand nand_27 (nand_27_out, nand_10_out, E1);
  nand nand_28 (nand_28_out, E1, nand_11_out);
  nand nand_29 (nand_29_out, Oi, nand_12_out, nand_13_out, E0);
  nand nand_30 (nand_30_out, nand_14_out, E0);
  nand nand_31 (nand_31_out, nand_15_out, Oi, nand_16_out);
  nand nand_32 (nand_32_out, Oi, nand_17_out, nand_18_out);
  nand nand_33 (S3, nand_20_out, nand_21_out, nand_22_out);
  nand nand_34 (S1, nand_27_out, nand_28_out, nand_29_out);
  nand nand_35 (S0, nand_30_out, nand_31_out, nand_32_out);
  nand nand_36 (S2, nand_23_out, nand_24_out, nand_25_out, nand_26_out);
endmodule

module one_twentyeight (
  input  Oi,
  input  [3:0] set_D,
  input  set_D_on,
  input  [3:0] set_U,
  input  set_U_on,
  input  Clk,
  input  PoR,
  output O,
  output [3:0] N1,
  output [3:0] N0
);

  wire and_1_out, and_2_out, and_3_out, and_5_out, and_6_out, and_7_out, and_8_out, and_9_out, and_10_out,
       and_11_out, and_12_out, not_1_out, not_2_out, not_3_out, not_4_out, not_5_out, not_6_out, or_1_out,
       or_2_out, set_1_s0, set_1_s1, set_2_s0, set_2_s1, set_2_s2, set_2_s3, T,
       zero_nine_start_one_end_eight_1_o, zero_nine_start_one_end_eight_1_s0,
       zero_nine_start_one_end_eight_1_s1, zero_nine_start_one_end_eight_1_s2,
       zero_nine_start_one_end_eight_1_s3, zero_two_1_s0, zero_two_1_s1;

  and and_1 (and_1_out, ~N1[0], N1[1]);  // AND_Gate
  and and_2 (and_2_out, ~zero_nine_start_one_end_eight_1_s0, ~zero_nine_start_one_end_eight_1_s1, ~zero_nine_start_one_end_eight_1_s2, ~zero_nine_start_one_end_eight_1_s3);  // AND_Gate
  and and_3 (and_3_out, and_2_out, T);
  zero_two zero_two_1 (
    .E1(N1[1]), .E0(N1[0]), .Oi(zero_nine_start_one_end_eight_1_o), .O(O), .S1(zero_two_1_s1),
    .S0(zero_two_1_s0));
  zero_nine_start_one_end_eight zero_nine_start_one_end_eight_1 (
    .E(and_1_out), .Oi(Oi), .E3(N0[3]), .E2(N0[2]), .E1(N0[1]), .E0(N0[0]),
    .O(zero_nine_start_one_end_eight_1_o), .S3(zero_nine_start_one_end_eight_1_s3),
    .S2(zero_nine_start_one_end_eight_1_s2), .S1(zero_nine_start_one_end_eight_1_s1),
    .S0(zero_nine_start_one_end_eight_1_s0));
  and and_4 (T, ~zero_two_1_s1, ~zero_two_1_s0);  // AND_Gate
  and and_5 (and_5_out, zero_nine_start_one_end_eight_1_s3, ~and_3_out);  // AND_Gate
  and and_6 (and_6_out, zero_nine_start_one_end_eight_1_s2, ~and_3_out);  // AND_Gate
  and and_7 (and_7_out, zero_nine_start_one_end_eight_1_s1, ~and_3_out);  // AND_Gate
  or or_1 (or_1_out, zero_nine_start_one_end_eight_1_s0, and_3_out);
  set set_1 (
    .E3(1'b0), .E2(1'b0), .E1(zero_two_1_s1), .E0(zero_two_1_s0), .set_val(set_D), .set_on(set_D_on),
    .S1(set_1_s1), .S0(set_1_s0));  // open: S3, S2
  set set_2 (
    .E3(and_5_out), .E2(and_6_out), .E1(and_7_out), .E0(or_1_out), .set_val(set_U), .set_on(set_U_on),
    .S3(set_2_s3), .S2(set_2_s2), .S1(set_2_s1), .S0(set_2_s0));
  and and_8 (and_8_out, set_1_s1, ~PoR);  // AND_Gate
  and and_9 (and_9_out, set_1_s0, ~PoR);  // AND_Gate
  and and_10 (and_10_out, set_2_s3, ~PoR);  // AND_Gate
  and and_11 (and_11_out, set_2_s2, ~PoR);  // AND_Gate
  and and_12 (and_12_out, set_2_s1, ~PoR);  // AND_Gate
  or or_2 (or_2_out, set_2_s0, PoR);
  not not_1 (not_1_out, and_8_out);
  not not_2 (not_2_out, and_9_out);
  not not_3 (not_3_out, and_10_out);
  not not_4 (not_4_out, and_11_out);
  not not_5 (not_5_out, and_12_out);
  not not_6 (not_6_out, or_2_out);
  S_R_Flip_Flop s_r_ff_1 (.S(and_8_out), .R(not_1_out), .clk(Clk), .Q(N1[1]), .reset(PoR));  // open: Qn, preset
  S_R_Flip_Flop s_r_ff_2 (.S(and_9_out), .R(not_2_out), .clk(Clk), .Q(N1[0]), .reset(PoR));  // open: Qn, preset
  S_R_Flip_Flop s_r_ff_3 (.S(and_10_out), .R(not_3_out), .clk(Clk), .Q(N0[3]), .reset(PoR));  // open: Qn, preset
  S_R_Flip_Flop s_r_ff_4 (.S(and_11_out), .R(not_4_out), .clk(Clk), .Q(N0[2]), .reset(PoR));  // open: Qn, preset
  S_R_Flip_Flop s_r_ff_5 (.S(and_12_out), .R(not_5_out), .clk(Clk), .Q(N0[1]), .reset(PoR));  // open: Qn, preset
  S_R_Flip_Flop s_r_ff_6 (.S(or_2_out), .R(not_6_out), .clk(Clk), .Q(N0[0]), .preset(PoR));  // open: reset, Qn

  assign N1[3:2] = 2'b00;
endmodule

module switch_01 (
  input  E,
  input  PoR,
  output S
);

  wire and_1_out, and_2_out, nand_1_out, nand_2_out, nand_3_out, nand_4_out, nand_5_out, nand_6_out,
       nand_7_out, nand_8_out, nand_9_out, nand_10_out, nand_11_out, nand_12_out, nand_13_out, nand_14_out,
       or_1_out, or_2_out, s_r_ff_1_q;

  nand nand_1 (nand_1_out, E, E);
  nand nand_2 (nand_2_out, s_r_ff_1_q, s_r_ff_1_q);
  nand nand_3 (nand_3_out, s_r_ff_1_q, s_r_ff_1_q);
  nand nand_4 (nand_4_out, S, S);
  nand nand_5 (nand_5_out, E, E);
  nand nand_6 (nand_6_out, S, S);
  nand nand_7 (nand_7_out, E, s_r_ff_1_q, S);
  nand nand_8 (nand_8_out, nand_1_out, nand_2_out, S);
  nand nand_9 (nand_9_out, E, nand_3_out, nand_4_out);
  nand nand_10 (nand_10_out, nand_5_out, s_r_ff_1_q, nand_6_out);
  nand nand_11 (nand_11_out, nand_7_out, nand_7_out);
  nand nand_12 (nand_12_out, nand_8_out, nand_8_out);
  nand nand_13 (nand_13_out, nand_9_out, nand_9_out);
  nand nand_14 (nand_14_out, nand_10_out, nand_10_out);
  and and_1 (and_1_out, ~PoR, nand_12_out);  // AND_Gate
  and and_2 (and_2_out, ~PoR, nand_13_out);  // AND_Gate
  or or_1 (or_1_out, nand_14_out, PoR);
  or or_2 (or_2_out, nand_11_out, PoR);
  S_R_Flip_Flop s_r_ff_1 (.Q(s_r_ff_1_q), .reset(or_1_out), .preset(and_1_out));  // open: S, R, clk, Qn
  S_R_Flip_Flop s_r_ff_2 (.Q(S), .reset(or_2_out), .preset(and_2_out));  // open: S, R, clk, Qn
endmodule

module month_select (
  input  E4,
  input  E3,
  input  E2,
  input  E1,
  input  E0,
  output S1,
  output S0
);

  wire nand_1_out, nand_2_out, nand_3_out, nand_4_out, nand_5_out, nand_6_out, nand_7_out, nand_8_out,
       nand_9_out;

  nand nand_1 (nand_1_out, E4, E4);
  nand nand_2 (nand_2_out, E3, E3);
  nand nand_3 (nand_3_out, E2, E2);
  nand nand_4 (nand_4_out, E0, E0);
  nand nand_5 (nand_5_out, E0, E0);
  nand nand_6 (nand_6_out, nand_1_out, nand_2_out, nand_3_out, nand_4_out);
  nand nand_7 (nand_7_out, E2, nand_5_out);
  nand nand_8 (nand_8_out, E3, E0);
  nand nand_9 (nand_9_out, E4, E0);
  nand nand_10 (S1, nand_6_out, nand_6_out);
  nand nand_11 (S0, nand_7_out, nand_8_out, nand_9_out);
endmodule

module led_board (
  input  [9:0] Input_bus_1,
  output Output_1,
  output Output_2,
  output Output_3,
  output Output_4,
  output Output_5,
  output Output_6,
  output Output_7,
  output Output_8,
  output Output_9,
  output Output_10
);


  assign Output_1 = Input_bus_1[0];
  assign Output_2 = Input_bus_1[1];
  assign Output_3 = Input_bus_1[2];
  assign Output_4 = Input_bus_1[3];
  assign Output_5 = Input_bus_1[4];
  assign Output_6 = Input_bus_1[5];
  assign Output_7 = Input_bus_1[6];
  assign Output_8 = Input_bus_1[7];
  assign Output_9 = Input_bus_1[8];
  assign Output_10 = Input_bus_1[9];
endmodule

module sept_segment (
  input  [6:0] Input_bus_1,
  output A,
  output B,
  output C,
  output D,
  output E,
  output F,
  output G
);


  assign A = Input_bus_1[0];
  assign B = Input_bus_1[1];
  assign C = Input_bus_1[2];
  assign D = Input_bus_1[3];
  assign E = Input_bus_1[4];
  assign F = Input_bus_1[5];
  assign G = Input_bus_1[6];
endmodule

module plex_disp (
  input  [2:0] mode,
  input  [6:0] m0_A5,
  input  [6:0] m0_A4,
  input  [6:0] m0_A3,
  input  [6:0] m0_A2,
  input  [6:0] m0_A1,
  input  [6:0] m0_A0,
  input  [6:0] m1_A5,
  input  [6:0] m1_A4,
  input  [6:0] m1_A3,
  input  [6:0] m1_A2,
  input  [6:0] m1_A1,
  input  [6:0] m1_A0,
  input  [6:0] m2_A5,
  input  [6:0] m2_A4,
  input  [6:0] m2_A3,
  input  [6:0] m2_A2,
  input  [6:0] m2_A1,
  input  [6:0] m2_A0,
  input  [6:0] m3_A5,
  input  [6:0] m3_A4,
  input  [6:0] m3_A3,
  input  [6:0] m3_A2,
  input  [6:0] m3_A1,
  input  [6:0] m3_A0,
  input  [6:0] m4_A5,
  input  [6:0] m4_A4,
  input  [6:0] m4_A3,
  input  [6:0] m4_A2,
  input  [6:0] m4_A1,
  input  [6:0] m4_A0,
  output [6:0] A5,
  output [6:0] A4,
  output [6:0] A3,
  output [6:0] A2,
  output [6:0] A1,
  output [6:0] A0
);

  Multiplexer #(.select(3), .width(7), .enable("false")) multiplexer_1 (
    .in0(m0_A5), .in1(m1_A5), .in2(m2_A5), .in3(m3_A5), .in4(m4_A5), .out(A5), .sel(mode));  // open: in5, in6, in7
  Multiplexer #(.select(3), .width(7), .enable("false")) multiplexer_2 (
    .in0(m0_A4), .in1(m1_A4), .in2(m2_A4), .in3(m3_A4), .in4(m4_A4), .out(A4), .sel(mode));  // open: in5, in6, in7
  Multiplexer #(.select(3), .width(7), .enable("false")) multiplexer_3 (
    .in0(m0_A3), .in1(m1_A3), .in2(m2_A3), .in3(m3_A3), .in4(m4_A3), .out(A3), .sel(mode));  // open: in5, in6, in7
  Multiplexer #(.select(3), .width(7), .enable("false")) multiplexer_4 (
    .in0(m0_A2), .in1(m1_A2), .in2(m2_A2), .in3(m3_A2), .in4(m4_A2), .out(A2), .sel(mode));  // open: in5, in6, in7
  Multiplexer #(.select(3), .width(7), .enable("false")) multiplexer_5 (
    .in0(m0_A1), .in1(m1_A1), .in2(m2_A1), .in3(m3_A1), .in4(m4_A1), .out(A1), .sel(mode));  // open: in5, in6, in7
  Multiplexer #(.select(3), .width(7), .enable("false")) multiplexer_6 (
    .in0(m0_A0), .in1(m1_A0), .in2(m2_A0), .in3(m3_A0), .in4(m4_A0), .out(A0), .sel(mode));  // open: in5, in6, in7
endmodule

module animation_led_alarm (
  input  ON_OFF,
  input  Clk,
  input  PoR,
  input  off,
  output [9:0] output_led,
  output disp_led_alarm
);

  wire and_1_out, counter_1_carry, not_1_out, or_1_out;
  wire [1:0] modes_3_1_state;

  or or_1 (or_1_out, PoR, off);
  and and_1 (and_1_out, ON_OFF, ~or_1_out);  // AND_Gate
  S_R_Flip_Flop s_r_ff_1 (.Q(disp_led_alarm), .reset(or_1_out), .preset(and_1_out));  // open: S, R, clk, Qn
  Counter #(.width(9), .max('h1ff)) counter_1 (
    .clr(not_1_out), .clk(Clk), .carry(counter_1_carry));  // open: load, up, count, D, Q
  not not_1 (not_1_out, disp_led_alarm);
  modes_3 modes_3_1 (.B(counter_1_carry), .PoR(or_1_out), .Clk(Clk), .state(modes_3_1_state));
  state_led_alarm state_led_alarm_1 (.E(modes_3_1_state), .S(output_led));
endmodule

module state_led_alarm (
  input  [1:0] E,
  output [9:0] S
);

  wire nand_1_out, nand_2_out, nand_3_out, nand_4_out, nand_7_out, nand_8_out, nand_9_out, nand_10_out,
       nand_13_out, nand_14_out, nand_15_out, nand_16_out, nand_17_out, nand_18_out, nand_19_out,
       nand_20_out, nand_21_out, nand_22_out, nand_23_out, nand_24_out, nand_25_out, nand_26_out,
       nand_27_out, nand_28_out;

  nand nand_1 (nand_1_out, E[1], E[1]);
  nand nand_2 (nand_2_out, E[0], E[0]);
  nand nand_3 (nand_3_out, E[1], E[1]);
  nand nand_4 (nand_4_out, E[0], E[0]);
  nand nand_5 (S[2], E[0], E[0]);
  nand nand_6 (S[3], E[0], E[0]);
  nand nand_7 (nand_7_out, E[1], E[1]);
  nand nand_8 (nand_8_out, E[0], E[0]);
  nand nand_9 (nand_9_out, E[1], E[1]);
  nand nand_10 (nand_10_out, E[0], E[0]);
  nand nand_11 (S[6], E[0], E[0]);
  nand nand_12 (S[7], E[0], E[0]);
  nand nand_13 (nand_13_out, E[1], E[1]);
  nand nand_14 (nand_14_out, E[0], E[0]);
  nand nand_15 (nand_15_out, E[1], E[1]);
  nand nand_16 (nand_16_out, E[0], E[0]);
  nand nand_17 (nand_17_out, nand_1_out, E[0]);
  nand nand_18 (nand_18_out, E[1], nand_2_out);
  nand nand_19 (nand_19_out, nand_3_out, E[0]);
  nand nand_20 (nand_20_out, E[1], nand_4_out);
  nand nand_21 (nand_21_out, nand_7_out, E[0]);
  nand nand_22 (nand_22_out, E[1], nand_8_out);
  nand nand_23 (nand_23_out, nand_9_out, E[0]);
  nand nand_24 (nand_24_out, E[1], nand_10_out);
  nand nand_25 (nand_25_out, nand_13_out, E[0]);
  nand nand_26 (nand_26_out, E[1], nand_14_out);
  nand nand_27 (nand_27_out, nand_15_out, E[0]);
  nand nand_28 (nand_28_out, E[1], nand_16_out);
  nand nand_29 (S[0], nand_17_out, nand_18_out);
  nand nand_30 (S[1], nand_19_out, nand_20_out);
  nand nand_31 (S[4], nand_21_out, nand_22_out);
  nand nand_32 (S[5], nand_23_out, nand_24_out);
  nand nand_33 (S[8], nand_25_out, nand_26_out);
  nand nand_34 (S[9], nand_27_out, nand_28_out);
endmodule

module blink (
  input  [6:0] E,
  input  Clk,
  input  PoR,
  input  blink_on,
  output [6:0] S
);

  wire and_1_out, counter_1_carry, switch_01_1_s;

  Counter #(.width(9), .max('h1ff)) counter_1 (
    .clr(PoR), .clk(Clk), .carry(counter_1_carry));  // open: load, up, count, D, Q
  switch_01 switch_01_1 (.E(counter_1_carry), .PoR(PoR), .S(switch_01_1_s));
  and and_1 (and_1_out, switch_01_1_s, blink_on);
  Multiplexer #(.width(7), .enable("false")) multiplexer_1 (.in0(E), .in1({7{1'b0}}), .out(S), .sel(and_1_out));
endmodule

module select_reset_month (
  input  R,
  input  E1,
  input  E0,
  output R2,
  output R1,
  output R0
);

  wire nand_1_out, nand_2_out, nand_3_out, nand_4_out, nand_5_out, nand_6_out, nand_7_out, nand_8_out;

  nand nand_1 (nand_1_out, E1, E1);
  nand nand_2 (nand_2_out, E0, E0);
  nand nand_3 (nand_3_out, E0, E0);
  nand nand_4 (nand_4_out, E1, E1);
  nand nand_5 (nand_5_out, R, nand_1_out, E0);
  nand nand_6 (nand_6_out, R, E1, nand_2_out);
  nand nand_7 (nand_7_out, R, nand_3_out);
  nand nand_8 (nand_8_out, R, nand_4_out);
  nand nand_9 (R2, nand_5_out, nand_6_out);
  nand nand_10 (R1, nand_7_out, nand_7_out);
  nand nand_11 (R0, nand_8_out, nand_8_out);
endmodule

module frequ_chrono (
  input  PoR,
  input  Clk,
  output pulse
);

  wire and_1_out, not_1_out, shift_register_1_p5;

  not not_1 (not_1_out, PoR);
  and and_1 (and_1_out, ~PoR, 1'b1);  // AND_Gate
  // Shift_Register #(.length(10)) shift_register_1: pin names not known; wires that end beside it: 1'b0, PoR, and_1_out, Clk, shift_register_1_p5, shift_register_1_p5, not_1_out, not_1_out, not_1_out, not_1_out, not_1_out, not_1_out, not_1_out, not_1_out, not_1_out, pulse
  or or_1 (shift_register_1_p5, pulse, PoR);
endmodule

module frequ_sec (
  input  PoR,
  input  Clk,
  output pulse
);

  Counter #(.width(10), .max('h3ff)) counter_1 (.clr(PoR), .clk(Clk), .carry(pulse));  // open: load, up, count, D, Q
endmodule

module nine_zero (
  input  Bi,
  input  [3:0] set_val,
  input  set_on,
  input  PoR,
  input  Clk,
  output Bo,
  output [3:0] N
);

  wire and_1_out, and_2_out, and_3_out, and_4_out, nine_zero_trans_1_s0, nine_zero_trans_1_s1,
       nine_zero_trans_1_s2, nine_zero_trans_1_s3, not_1_out, not_2_out, not_3_out, not_4_out, set_1_s0,
       set_1_s1, set_1_s2, set_1_s3;

  nine_zero_trans nine_zero_trans_1 (
    .Bi(Bi), .E3(N[3]), .E2(N[2]), .E1(N[1]), .E0(N[0]), .B(Bo), .S3(nine_zero_trans_1_s3),
    .S2(nine_zero_trans_1_s2), .S1(nine_zero_trans_1_s1), .S0(nine_zero_trans_1_s0));
  set set_1 (
    .E3(nine_zero_trans_1_s3), .E2(nine_zero_trans_1_s2), .E1(nine_zero_trans_1_s1),
    .E0(nine_zero_trans_1_s0), .set_val(set_val), .set_on(set_on), .S3(set_1_s3), .S2(set_1_s2),
    .S1(set_1_s1), .S0(set_1_s0));
  and and_1 (and_1_out, set_1_s3, ~PoR);  // AND_Gate
  and and_2 (and_2_out, set_1_s2, ~PoR);  // AND_Gate
  and and_3 (and_3_out, set_1_s1, ~PoR);  // AND_Gate
  and and_4 (and_4_out, set_1_s0, ~PoR);  // AND_Gate
  not not_1 (not_1_out, and_1_out);
  not not_2 (not_2_out, and_2_out);
  not not_3 (not_3_out, and_3_out);
  not not_4 (not_4_out, and_4_out);
  S_R_Flip_Flop s_r_ff_1 (.S(and_1_out), .R(not_1_out), .clk(Clk), .Q(N[3]), .reset(PoR));  // open: Qn, preset
  S_R_Flip_Flop s_r_ff_2 (.S(and_2_out), .R(not_2_out), .clk(Clk), .Q(N[2]), .reset(PoR));  // open: Qn, preset
  S_R_Flip_Flop s_r_ff_3 (.S(and_3_out), .R(not_3_out), .clk(Clk), .Q(N[1]), .reset(PoR));  // open: Qn, preset
  S_R_Flip_Flop s_r_ff_4 (.S(and_4_out), .R(not_4_out), .clk(Clk), .Q(N[0]), .reset(PoR));  // open: Qn, preset
endmodule

module nine_zero_trans (
  input  Bi,
  input  E3,
  input  E2,
  input  E1,
  input  E0,
  output B,
  output S3,
  output S2,
  output S1,
  output S0
);

  wire nand_1_out, nand_2_out, nand_3_out, nand_4_out, nand_5_out, nand_6_out, nand_7_out, nand_8_out,
       nand_9_out, nand_10_out, nand_11_out, nand_12_out, nand_13_out, nand_14_out, nand_15_out, nand_16_out,
       nand_17_out, nand_18_out, nand_19_out, nand_20_out, nand_21_out, nand_22_out, nand_23_out,
       nand_24_out, nand_25_out, nand_26_out, nand_27_out, nand_28_out, nand_29_out, nand_30_out,
       nand_31_out, nand_32_out, nand_33_out, nand_34_out, nand_35_out, nand_36_out, nand_37_out,
       nand_38_out, nand_39_out, nand_40_out, nand_41_out, nand_42_out, nand_43_out, nand_44_out,
       nand_45_out, nand_46_out, nand_47_out, nand_48_out, nand_49_out, nand_50_out, nand_51_out,
       nand_52_out, nand_53_out, nand_54_out, nand_55_out;

  nand nand_1 (nand_1_out, E3, E3);
  nand nand_2 (nand_2_out, E2, E2);
  nand nand_3 (nand_3_out, E1, E1);
  nand nand_4 (nand_4_out, E0, E0);
  nand nand_5 (nand_5_out, Bi, Bi);
  nand nand_6 (nand_6_out, E2, E2);
  nand nand_7 (nand_7_out, E1, E1);
  nand nand_8 (nand_8_out, E2, E2);
  nand nand_9 (nand_9_out, E1, E1);
  nand nand_10 (nand_10_out, E3, E3);
  nand nand_11 (nand_11_out, E2, E2);
  nand nand_12 (nand_12_out, E1, E1);
  nand nand_13 (nand_13_out, E0, E0);
  nand nand_14 (nand_14_out, Bi, Bi);
  nand nand_15 (nand_15_out, E3, E3);
  nand nand_16 (nand_16_out, E3, E3);
  nand nand_17 (nand_17_out, E3, E3);
  nand nand_18 (nand_18_out, E2, E2);
  nand nand_19 (nand_19_out, E1, E1);
  nand nand_20 (nand_20_out, E0, E0);
  nand nand_21 (nand_21_out, Bi, Bi);
  nand nand_22 (nand_22_out, E3, E3);
  nand nand_23 (nand_23_out, E3, E3);
  nand nand_24 (nand_24_out, E3, E3);
  nand nand_25 (nand_25_out, E1, E1);
  nand nand_26 (nand_26_out, E0, E0);
  nand nand_27 (nand_27_out, E2, E2);
  nand nand_28 (nand_28_out, E1, E1);
  nand nand_29 (nand_29_out, E0, E0);
  nand nand_30 (nand_30_out, Bi, Bi);
  nand nand_31 (nand_31_out, E3, E3);
  nand nand_32 (nand_32_out, Bi, Bi);
  nand nand_33 (nand_33_out, E2, E2);
  nand nand_34 (nand_34_out, E1, E1);
  nand nand_35 (nand_35_out, E3, E3);
  nand nand_36 (nand_36_out, E0, E0);
  nand nand_37 (nand_37_out, E2, E2);
  nand nand_38 (nand_38_out, E1, E1);
  nand nand_39 (nand_39_out, E0, E0);
  nand nand_40 (nand_40_out, Bi, nand_1_out, nand_2_out, nand_3_out, nand_4_out);
  nand nand_41 (nand_41_out, nand_5_out, E3, nand_6_out, nand_7_out);
  nand nand_42 (nand_42_out, E3, nand_8_out, nand_9_out, E0);
  nand nand_43 (nand_43_out, Bi, nand_10_out, nand_11_out, nand_12_out, nand_13_out);
  nand nand_44 (nand_44_out, nand_14_out, nand_15_out, E2);
  nand nand_45 (nand_45_out, nand_16_out, E2, E0);
  nand nand_46 (nand_46_out, nand_17_out, E2, E1);
  nand nand_47 (nand_47_out, Bi, E3, nand_18_out, nand_19_out, nand_20_out);
  nand nand_48 (nand_48_out, nand_21_out, nand_22_out, E1);
  nand nand_49 (nand_49_out, nand_23_out, E1, E0);
  nand nand_50 (nand_50_out, Bi, nand_24_out, E2, nand_25_out, nand_26_out);
  nand nand_51 (nand_51_out, Bi, E3, nand_27_out, nand_28_out, nand_29_out);
  nand nand_52 (nand_52_out, nand_30_out, nand_31_out, E0);
  nand nand_53 (nand_53_out, nand_32_out, nand_33_out, nand_34_out, E0);
  nand nand_54 (nand_54_out, Bi, nand_35_out, nand_36_out);
  nand nand_55 (nand_55_out, Bi, nand_37_out, nand_38_out, nand_39_out);
  nand nand_56 (B, nand_40_out, nand_40_out);
  nand nand_57 (S3, nand_41_out, nand_42_out, nand_43_out);
  nand nand_58 (S2, nand_44_out, nand_45_out, nand_46_out, nand_47_out);
  nand nand_59 (S1, nand_48_out, nand_49_out, nand_50_out, nand_51_out);
  nand nand_60 (S0, nand_52_out, nand_53_out, nand_54_out, nand_55_out);
endmodule

module five_zero_trans (
  input  Bi,
  input  E2,
  input  E1,
  input  E0,
  output B,
  output S2,
  output S1,
  output S0
);

  wire nand_1_out, nand_2_out, nand_3_out, nand_4_out, nand_5_out, nand_6_out, nand_7_out, nand_8_out,
       nand_9_out, nand_10_out, nand_11_out, nand_12_out, nand_13_out, nand_14_out, nand_15_out, nand_16_out,
       nand_17_out, nand_18_out, nand_19_out, nand_20_out, nand_21_out, nand_22_out, nand_23_out,
       nand_24_out, nand_25_out, nand_26_out, nand_27_out, nand_28_out, nand_29_out, nand_30_out,
       nand_31_out, nand_32_out, nand_33_out;

  nand nand_1 (nand_1_out, E2, E2);
  nand nand_2 (nand_2_out, E1, E1);
  nand nand_3 (nand_3_out, E0, E0);
  nand nand_4 (nand_4_out, Bi, Bi);
  nand nand_5 (nand_5_out, E1, E1);
  nand nand_6 (nand_6_out, E1, E1);
  nand nand_7 (nand_7_out, E2, E2);
  nand nand_8 (nand_8_out, E1, E1);
  nand nand_9 (nand_9_out, E0, E0);
  nand nand_10 (nand_10_out, Bi, Bi);
  nand nand_11 (nand_11_out, E2, E2);
  nand nand_12 (nand_12_out, E2, E2);
  nand nand_13 (nand_13_out, E1, E1);
  nand nand_14 (nand_14_out, E0, E0);
  nand nand_15 (nand_15_out, Bi, Bi);
  nand nand_16 (nand_16_out, E2, E2);
  nand nand_17 (nand_17_out, Bi, Bi);
  nand nand_18 (nand_18_out, E1, E1);
  nand nand_19 (nand_19_out, E2, E2);
  nand nand_20 (nand_20_out, E0, E0);
  nand nand_21 (nand_21_out, E1, E1);
  nand nand_22 (nand_22_out, E0, E0);
  nand nand_23 (nand_23_out, Bi, nand_1_out, nand_2_out, nand_3_out);
  nand nand_24 (nand_24_out, nand_4_out, E2, nand_5_out);
  nand nand_25 (nand_25_out, E2, nand_6_out, E0);
  nand nand_26 (nand_26_out, Bi, nand_7_out, nand_8_out, nand_9_out);
  nand nand_27 (nand_27_out, nand_10_out, nand_11_out, E1);
  nand nand_28 (nand_28_out, nand_12_out, E1, E0);
  nand nand_29 (nand_29_out, Bi, E2, nand_13_out, nand_14_out);
  nand nand_30 (nand_30_out, nand_15_out, nand_16_out, E0);
  nand nand_31 (nand_31_out, nand_17_out, nand_18_out, E0);
  nand nand_32 (nand_32_out, Bi, nand_19_out, nand_20_out);
  nand nand_33 (nand_33_out, Bi, nand_21_out, nand_22_out);
  nand nand_34 (B, nand_23_out, nand_23_out);
  nand nand_35 (S2, nand_24_out, nand_25_out, nand_26_out);
  nand nand_36 (S1, nand_27_out, nand_28_out, nand_29_out);
  nand nand_37 (S0, nand_30_out, nand_31_out, nand_32_out, nand_33_out);
endmodule

module five_zero (
  input  Bi,
  input  [3:0] set_val,
  input  set_on,
  input  PoR,
  input  Clk,
  output Bo,
  output [3:0] N
);

  wire and_1_out, and_2_out, and_3_out, five_zero_trans_1_s0, five_zero_trans_1_s1, five_zero_trans_1_s2,
       not_1_out, not_2_out, not_3_out, set_1_s0, set_1_s1, set_1_s2;

  five_zero_trans five_zero_trans_1 (
    .Bi(Bi), .E2(N[2]), .E1(N[1]), .E0(N[0]), .B(Bo), .S2(five_zero_trans_1_s2), .S1(five_zero_trans_1_s1),
    .S0(five_zero_trans_1_s0));
  set set_1 (
    .E3(1'b0), .E2(five_zero_trans_1_s2), .E1(five_zero_trans_1_s1), .E0(five_zero_trans_1_s0),
    .set_val(set_val), .set_on(set_on), .S2(set_1_s2), .S1(set_1_s1), .S0(set_1_s0));  // open: S3
  and and_1 (and_1_out, set_1_s2, ~PoR);  // AND_Gate
  and and_2 (and_2_out, set_1_s1, ~PoR);  // AND_Gate
  and and_3 (and_3_out, set_1_s0, ~PoR);  // AND_Gate
  not not_1 (not_1_out, and_1_out);
  not not_2 (not_2_out, and_2_out);
  not not_3 (not_3_out, and_3_out);
  S_R_Flip_Flop s_r_ff_1 (.S(and_1_out), .R(not_1_out), .clk(Clk), .Q(N[2]), .reset(PoR));  // open: Qn, preset
  S_R_Flip_Flop s_r_ff_2 (.S(and_2_out), .R(not_2_out), .clk(Clk), .Q(N[1]), .reset(PoR));  // open: Qn, preset
  S_R_Flip_Flop s_r_ff_3 (.S(and_3_out), .R(not_3_out), .clk(Clk), .Q(N[0]), .reset(PoR));  // open: Qn, preset

  assign N[3] = 1'b0;
endmodule

module twentythree_zero_trans (
  input  Bi,
  input  E4,
  input  E3,
  input  E2,
  input  E1,
  input  E0,
  output B,
  output S4,
  output S3,
  output S2,
  output S1,
  output S0
);

  wire nand_1_out, nand_2_out, nand_3_out, nand_4_out, nand_5_out, nand_6_out, nand_7_out, nand_8_out,
       nand_9_out, nand_10_out, nand_11_out, nand_12_out, nand_13_out, nand_14_out, nand_15_out, nand_16_out,
       nand_17_out, nand_18_out, nand_19_out, nand_20_out, nand_21_out, nand_22_out, nand_23_out,
       nand_24_out, nand_25_out, nand_26_out, nand_27_out, nand_28_out, nand_29_out, nand_30_out,
       nand_31_out, nand_32_out, nand_33_out, nand_34_out, nand_35_out, nand_36_out, nand_37_out,
       nand_38_out, nand_39_out, nand_40_out, nand_41_out, nand_42_out, nand_43_out, nand_44_out,
       nand_45_out, nand_46_out, nand_47_out, nand_48_out, nand_49_out, nand_50_out, nand_51_out,
       nand_52_out, nand_53_out, nand_54_out, nand_55_out, nand_56_out, nand_57_out, nand_58_out,
       nand_59_out, nand_60_out, nand_61_out, nand_62_out, nand_63_out, nand_64_out, nand_65_out,
       nand_66_out, nand_67_out, nand_68_out, nand_69_out, nand_70_out, nand_71_out, nand_72_out,
       nand_73_out, nand_74_out, nand_75_out, nand_76_out, nand_77_out, nand_78_out, nand_79_out,
       nand_80_out, nand_81_out, nand_82_out, nand_83_out, nand_84_out, nand_85_out, nand_86_out,
       nand_87_out, nand_88_out, nand_89_out;

  nand nand_1 (nand_1_out, E4, E4);
  nand nand_2 (nand_2_out, E3, E3);
  nand nand_3 (nand_3_out, E2, E2);
  nand nand_4 (nand_4_out, E1, E1);
  nand nand_5 (nand_5_out, E0, E0);
  nand nand_6 (nand_6_out, E4, E4);
  nand nand_7 (nand_7_out, E3, E3);
  nand nand_8 (nand_8_out, E2, E2);
  nand nand_9 (nand_9_out, E1, E1);
  nand nand_10 (nand_10_out, E0, E0);
  nand nand_11 (nand_11_out, E3, E3);
  nand nand_12 (nand_12_out, E2, E2);
  nand nand_13 (nand_13_out, E1, E1);
  nand nand_14 (nand_14_out, E0, E0);
  nand nand_15 (nand_15_out, Bi, Bi);
  nand nand_16 (nand_16_out, E4, E4);
  nand nand_17 (nand_17_out, Bi, Bi);
  nand nand_18 (nand_18_out, E3, E3);
  nand nand_19 (nand_19_out, E4, E4);
  nand nand_20 (nand_20_out, E3, E3);
  nand nand_21 (nand_21_out, E4, E4);
  nand nand_22 (nand_22_out, E3, E3);
  nand nand_23 (nand_23_out, E4, E4);
  nand nand_24 (nand_24_out, E2, E2);
  nand nand_25 (nand_25_out, E1, E1);
  nand nand_26 (nand_26_out, E0, E0);
  nand nand_27 (nand_27_out, E3, E3);
  nand nand_28 (nand_28_out, E2, E2);
  nand nand_29 (nand_29_out, E1, E1);
  nand nand_30 (nand_30_out, E0, E0);
  nand nand_31 (nand_31_out, Bi, Bi);
  nand nand_32 (nand_32_out, E4, E4);
  nand nand_33 (nand_33_out, Bi, Bi);
  nand nand_34 (nand_34_out, E3, E3);
  nand nand_35 (nand_35_out, E4, E4);
  nand nand_36 (nand_36_out, E3, E3);
  nand nand_37 (nand_37_out, E4, E4);
  nand nand_38 (nand_38_out, E1, E1);
  nand nand_39 (nand_39_out, E0, E0);
  nand nand_40 (nand_40_out, E3, E3);
  nand nand_41 (nand_41_out, E1, E1);
  nand nand_42 (nand_42_out, E0, E0);
  nand nand_43 (nand_43_out, Bi, Bi);
  nand nand_44 (nand_44_out, E4, E4);
  nand nand_45 (nand_45_out, Bi, Bi);
  nand nand_46 (nand_46_out, E3, E3);
  nand nand_47 (nand_47_out, E4, E4);
  nand nand_48 (nand_48_out, E0, E0);
  nand nand_49 (nand_49_out, E3, E3);
  nand nand_50 (nand_50_out, E0, E0);
  nand nand_51 (nand_51_out, Bi, Bi);
  nand nand_52 (nand_52_out, E3, E3);
  nand nand_53 (nand_53_out, E3, E3);
  nand nand_54 (nand_54_out, E3, E3);
  nand nand_55 (nand_55_out, E3, E3);
  nand nand_56 (nand_56_out, Bi, Bi);
  nand nand_57 (nand_57_out, E4, E4);
  nand nand_58 (nand_58_out, E4, E4);
  nand nand_59 (nand_59_out, E4, E4);
  nand nand_60 (nand_60_out, E4, E4);
  nand nand_61 (nand_61_out, nand_15_out, nand_16_out, E2);
  nand nand_62 (nand_62_out, nand_17_out, nand_18_out, E2);
  nand nand_63 (nand_63_out, nand_19_out, E2, E0);
  nand nand_64 (nand_64_out, nand_20_out, E2, E0);
  nand nand_65 (nand_65_out, nand_21_out, E2, E1);
  nand nand_66 (nand_66_out, nand_22_out, E2, E1);
  nand nand_67 (nand_67_out, Bi, nand_23_out, nand_24_out, nand_25_out, nand_26_out);
  nand nand_68 (nand_68_out, Bi, nand_27_out, nand_28_out, nand_29_out, nand_30_out);
  nand nand_69 (nand_69_out, nand_31_out, nand_32_out, E1);
  nand nand_70 (nand_70_out, nand_33_out, nand_34_out, E1);
  nand nand_71 (nand_71_out, nand_35_out, E1, E0);
  nand nand_72 (nand_72_out, nand_36_out, E1, E0);
  nand nand_73 (nand_73_out, Bi, nand_37_out, nand_38_out, nand_39_out);
  nand nand_74 (nand_74_out, Bi, nand_40_out, nand_41_out, nand_42_out);
  nand nand_75 (nand_75_out, nand_43_out, nand_44_out, E0);
  nand nand_76 (nand_76_out, nand_45_out, nand_46_out, E0);
  nand nand_77 (nand_77_out, Bi, nand_47_out, nand_48_out);
  nand nand_78 (nand_78_out, Bi, nand_49_out, nand_50_out);
  nand nand_79 (nand_79_out, Bi, nand_1_out, nand_2_out, nand_3_out, nand_4_out, nand_5_out);
  nand nand_80 (nand_80_out, nand_51_out, E4, nand_52_out);
  nand nand_81 (nand_81_out, E4, nand_53_out, E0);
  nand nand_82 (nand_82_out, E4, nand_54_out, E1);
  nand nand_83 (nand_83_out, E4, nand_55_out, E2);
  nand nand_84 (nand_84_out, Bi, nand_6_out, nand_7_out, nand_8_out, nand_9_out, nand_10_out);
  nand nand_85 (nand_85_out, nand_56_out, nand_57_out, E3);
  nand nand_86 (nand_86_out, nand_58_out, E3, E0);
  nand nand_87 (nand_87_out, nand_59_out, E3, E1);
  nand nand_88 (nand_88_out, nand_60_out, E3, E2);
  nand nand_89 (nand_89_out, Bi, E4, nand_11_out, nand_12_out, nand_13_out, nand_14_out);
  nand nand_90 (S0, nand_75_out, nand_76_out, nand_77_out, nand_78_out);
  nand nand_91 (B, nand_79_out, nand_79_out);
  nand nand_92 (S4, nand_80_out, nand_81_out, nand_82_out, nand_83_out, nand_84_out);
  nand nand_93 (S3, nand_85_out, nand_86_out, nand_87_out, nand_88_out, nand_89_out);
  nand nand_94 (S2, nand_61_out, nand_62_out, nand_63_out, nand_64_out, nand_65_out, nand_66_out, nand_67_out, nand_68_out);
  nand nand_95 (S1, nand_69_out, nand_70_out, nand_71_out, nand_72_out, nand_73_out, nand_74_out);
endmodule

module twentythree_zero (
  input  Bi,
  input  [4:0] set_val,
  input  set_on,
  input  PoR,
  input  Clk,
  output Bo,
  output [3:0] N1,
  output [3:0] N0,
  output [4:0] val
);

  wire and_1_out, and_2_out, and_3_out, and_4_out, and_5_out, not_1_out, not_2_out, not_3_out, not_4_out,
       not_5_out, not_6_out, set_plus_1_s0, set_plus_1_s1, set_plus_1_s2, set_plus_1_s3, set_plus_1_s4,
       twentythree_zero_trans_1_b, twentythree_zero_trans_1_s0, twentythree_zero_trans_1_s1,
       twentythree_zero_trans_1_s2, twentythree_zero_trans_1_s3, twentythree_zero_trans_1_s4;

  twentythree_zero_trans twentythree_zero_trans_1 (
    .Bi(Bi), .E4(val[4]), .E3(val[3]), .E2(val[2]), .E1(val[1]), .E0(val[0]), .B(twentythree_zero_trans_1_b),
    .S4(twentythree_zero_trans_1_s4), .S3(twentythree_zero_trans_1_s3), .S2(twentythree_zero_trans_1_s2),
    .S1(twentythree_zero_trans_1_s1), .S0(twentythree_zero_trans_1_s0));
  set_plus set_plus_1 (
    .E4(twentythree_zero_trans_1_s4), .E3(twentythree_zero_trans_1_s3), .E2(twentythree_zero_trans_1_s2),
    .E1(twentythree_zero_trans_1_s1), .E0(twentythree_zero_trans_1_s0), .set_val(set_val), .set_on(set_on),
    .S4(set_plus_1_s4), .S3(set_plus_1_s3), .S2(set_plus_1_s2), .S1(set_plus_1_s1), .S0(set_plus_1_s0));
  and and_1 (and_1_out, set_plus_1_s4, ~PoR);  // AND_Gate
  and and_2 (and_2_out, set_plus_1_s3, ~PoR);  // AND_Gate
  and and_3 (and_3_out, set_plus_1_s2, ~PoR);  // AND_Gate
  and and_4 (and_4_out, set_plus_1_s1, ~PoR);  // AND_Gate
  and and_5 (and_5_out, set_plus_1_s0, ~PoR);  // AND_Gate
  S_R_Flip_Flop s_r_ff_1 (
    .S(twentythree_zero_trans_1_b), .R(not_1_out), .clk(Clk), .Q(Bo), .reset(PoR));  // open: Qn, preset
  not not_1 (not_1_out, twentythree_zero_trans_1_b);
  S_R_Flip_Flop s_r_ff_2 (.S(and_1_out), .R(not_2_out), .clk(Clk), .Q(val[4]), .reset(PoR));  // open: Qn, preset
  not not_2 (not_2_out, and_1_out);
  S_R_Flip_Flop s_r_ff_3 (.S(and_2_out), .R(not_3_out), .clk(Clk), .Q(val[3]), .reset(PoR));  // open: Qn, preset
  not not_3 (not_3_out, and_2_out);
  S_R_Flip_Flop s_r_ff_4 (.S(and_3_out), .R(not_4_out), .clk(Clk), .Q(val[2]), .reset(PoR));  // open: Qn, preset
  not not_4 (not_4_out, and_3_out);
  S_R_Flip_Flop s_r_ff_5 (.S(and_4_out), .R(not_5_out), .clk(Clk), .Q(val[1]), .reset(PoR));  // open: Qn, preset
  not not_5 (not_5_out, and_4_out);
  S_R_Flip_Flop s_r_ff_6 (.S(and_5_out), .R(not_6_out), .clk(Clk), .Q(val[0]), .reset(PoR));  // open: Qn, preset
  not not_6 (not_6_out, and_5_out);
  // Binairy_to_BCD_converter #(.binvalue(5)) binairy_to_bcd_converter_1: pin names not known; wires that end beside it: val, N1, N0
endmodule

module set_plus (
  input  E4,
  input  E3,
  input  E2,
  input  E1,
  input  E0,
  input  [4:0] set_val,
  input  set_on,
  output S4,
  output S3,
  output S2,
  output S1,
  output S0
);

  Multiplexer #(.enable("false")) multiplexer_1 (.in0(E4), .in1(set_val[4]), .out(S4), .sel(set_on));
  Multiplexer #(.enable("false")) multiplexer_2 (.in0(E3), .in1(set_val[3]), .out(S3), .sel(set_on));
  Multiplexer #(.enable("false")) multiplexer_3 (.in0(E2), .in1(set_val[2]), .out(S2), .sel(set_on));
  Multiplexer #(.enable("false")) multiplexer_4 (.in0(E1), .in1(set_val[1]), .out(S1), .sel(set_on));
  Multiplexer #(.enable("false")) multiplexer_5 (.in0(E0), .in1(set_val[0]), .out(S0), .sel(set_on));
endmodule

module unit_counter (
  input  Oi,
  input  PoR,
  input  Clk,
  output O,
  output state
);

  wire and_1_out, nand_1_out, nand_2_out, nand_3_out, nand_5_out, nand_6_out, nand_7_out, not_1_out;

  nand nand_1 (nand_1_out, Oi, state);
  nand nand_2 (nand_2_out, Oi, Oi);
  nand nand_3 (nand_3_out, state, state);
  nand nand_4 (O, nand_1_out, nand_1_out);
  nand nand_5 (nand_5_out, nand_2_out, state);
  nand nand_6 (nand_6_out, Oi, nand_3_out);
  nand nand_7 (nand_7_out, nand_5_out, nand_6_out);
  and and_1 (and_1_out, nand_7_out, ~PoR);  // AND_Gate
  S_R_Flip_Flop s_r_ff_1 (.S(and_1_out), .R(not_1_out), .clk(Clk), .Q(state), .reset(PoR));  // open: Qn, preset
  not not_1 (not_1_out, and_1_out);
endmodule

module frequ_sec_counter (
  input  PoR,
  input  Clk,
  output pulse
);

  wire unit_counter_2_o, unit_counter_3_o, unit_counter_4_o, unit_counter_5_o, unit_counter_6_o,
       unit_counter_7_o, unit_counter_8_o, unit_counter_9_o, unit_counter_10_o, unit_counter_11_o;

  unit_counter unit_counter_1 (.Oi(unit_counter_2_o), .PoR(PoR), .Clk(Clk), .O(pulse));  // open: state
  unit_counter unit_counter_2 (.Oi(unit_counter_3_o), .PoR(PoR), .Clk(Clk), .O(unit_counter_2_o));  // open: state
  unit_counter unit_counter_3 (.Oi(unit_counter_4_o), .PoR(PoR), .Clk(Clk), .O(unit_counter_3_o));  // open: state
  unit_counter unit_counter_4 (.Oi(unit_counter_5_o), .PoR(PoR), .Clk(Clk), .O(unit_counter_4_o));  // open: state
  unit_counter unit_counter_5 (.Oi(unit_counter_6_o), .PoR(PoR), .Clk(Clk), .O(unit_counter_5_o));  // open: state
  unit_counter unit_counter_6 (.Oi(unit_counter_7_o), .PoR(PoR), .Clk(Clk), .O(unit_counter_6_o));  // open: state
  unit_counter unit_counter_7 (.Oi(unit_counter_8_o), .PoR(PoR), .Clk(Clk), .O(unit_counter_7_o));  // open: state
  unit_counter unit_counter_8 (.Oi(unit_counter_9_o), .PoR(PoR), .Clk(Clk), .O(unit_counter_8_o));  // open: state
  unit_counter unit_counter_9 (.Oi(unit_counter_10_o), .PoR(PoR), .Clk(Clk), .O(unit_counter_9_o));  // open: state
  unit_counter unit_counter_10 (.Oi(unit_counter_11_o), .PoR(PoR), .Clk(Clk), .O(unit_counter_10_o));  // open: state
  unit_counter unit_counter_11 (.Oi(Clk), .PoR(PoR), .Clk(Clk), .O(unit_counter_11_o));  // open: state
endmodule

module modes_3 (
  input  B,
  input  PoR,
  input  Clk,
  output [1:0] state
);

  wire and_1_out, and_2_out, and_3_out, nand_1_out, nand_2_out, nand_3_out, nand_4_out, nand_5_out,
       nand_6_out, nand_7_out, nand_8_out, nand_9_out, nand_10_out, nand_11_out, nand_12_out, nand_13_out,
       nand_14_out, nand_15_out, nand_16_out, nand_17_out, nand_18_out, nand_19_out, nand_20_out,
       nand_21_out, nand_22_out, nand_23_out, nand_24_out, not_1_out, not_2_out, not_3_out, s_r_ff_1_q;

  nand nand_1 (nand_1_out, state[1], state[1]);
  nand nand_2 (nand_2_out, state[0], state[0]);
  nand nand_3 (nand_3_out, B, B);
  nand nand_4 (nand_4_out, state[0], state[0]);
  nand nand_5 (nand_5_out, state[0], state[0]);
  nand nand_6 (nand_6_out, s_r_ff_1_q, s_r_ff_1_q);
  nand nand_7 (nand_7_out, state[1], state[1]);
  nand nand_8 (nand_8_out, B, B);
  nand nand_9 (nand_9_out, state[1], state[1]);
  nand nand_10 (nand_10_out, state[1], state[1]);
  nand nand_11 (nand_11_out, s_r_ff_1_q, s_r_ff_1_q);
  nand nand_12 (nand_12_out, state[1], state[1]);
  nand nand_13 (nand_13_out, state[0], state[0]);
  nand nand_14 (nand_14_out, B, nand_1_out);
  nand nand_15 (nand_15_out, B, nand_2_out);
  nand nand_16 (nand_16_out, nand_3_out, state[1], nand_4_out);
  nand nand_17 (nand_17_out, s_r_ff_1_q, state[1], nand_5_out);
  nand nand_18 (nand_18_out, B, nand_6_out, nand_7_out, state[0]);
  nand nand_19 (nand_19_out, nand_8_out, nand_9_out, state[0]);
  nand nand_20 (nand_20_out, s_r_ff_1_q, nand_10_out, state[0]);
  nand nand_21 (nand_21_out, B, nand_11_out, nand_12_out, nand_13_out);
  nand nand_22 (nand_22_out, nand_14_out, nand_15_out);
  nand nand_23 (nand_23_out, nand_16_out, nand_17_out, nand_18_out);
  nand nand_24 (nand_24_out, nand_19_out, nand_20_out, nand_21_out);
  and and_1 (and_1_out, nand_22_out, ~PoR);  // AND_Gate
  not not_1 (not_1_out, and_1_out);
  and and_2 (and_2_out, nand_23_out, ~PoR);  // AND_Gate
  not not_2 (not_2_out, and_2_out);
  and and_3 (and_3_out, nand_24_out, ~PoR);  // AND_Gate
  not not_3 (not_3_out, and_3_out);
  S_R_Flip_Flop s_r_ff_1 (.S(and_1_out), .R(not_1_out), .clk(Clk), .Q(s_r_ff_1_q), .reset(PoR));  // open: Qn, preset
  S_R_Flip_Flop s_r_ff_2 (.S(and_2_out), .R(not_2_out), .clk(Clk), .Q(state[1]), .reset(PoR));  // open: Qn, preset
  S_R_Flip_Flop s_r_ff_3 (.S(and_3_out), .R(not_3_out), .clk(Clk), .Q(state[0]), .reset(PoR));  // open: Qn, preset
endmodule
