// Logisim project Modes.circ as structural Verilog
module n3_modes (
  input  B,
  input  PoR,
  input  Clk,
  output [1:0] mode
);

  wire and_1_out, and_2_out, and_3_out, nand_1_out, nand_2_out, nand_3_out, nand_4_out, nand_5_out,
       nand_6_out, nand_7_out, nand_8_out, nand_9_out, nand_10_out, nand_11_out, nand_12_out, nand_13_out,
       nand_14_out, nand_15_out, nand_16_out, nand_17_out, nand_18_out, nand_19_out, nand_20_out,
       nand_21_out, nand_22_out, nand_23_out, nand_24_out, not_1_out, not_2_out, not_3_out, s_r_ff_1_q;

  nand nand_1 (nand_1_out, mode[1], mode[1]);
  nand nand_2 (nand_2_out, mode[0], mode[0]);
  nand nand_3 (nand_3_out, B, B);
  nand nand_4 (nand_4_out, mode[0], mode[0]);
  nand nand_5 (nand_5_out, mode[0], mode[0]);
  nand nand_6 (nand_6_out, s_r_ff_1_q, s_r_ff_1_q);
  nand nand_7 (nand_7_out, mode[1], mode[1]);
  nand nand_8 (nand_8_out, B, B);
  nand nand_9 (nand_9_out, mode[1], mode[1]);
  nand nand_10 (nand_10_out, mode[1], mode[1]);
  nand nand_11 (nand_11_out, s_r_ff_1_q, s_r_ff_1_q);
  nand nand_12 (nand_12_out, mode[1], mode[1]);
  nand nand_13 (nand_13_out, mode[0], mode[0]);
  nand nand_14 (nand_14_out, B, nand_1_out);
  nand nand_15 (nand_15_out, B, nand_2_out);
  nand nand_16 (nand_16_out, nand_3_out, mode[1], nand_4_out);
  nand nand_17 (nand_17_out, s_r_ff_1_q, mode[1], nand_5_out);
  nand nand_18 (nand_18_out, B, nand_6_out, nand_7_out, mode[0]);
  nand nand_19 (nand_19_out, nand_8_out, nand_9_out, mode[0]);
  nand nand_20 (nand_20_out, s_r_ff_1_q, nand_10_out, mode[0]);
  nand nand_21 (nand_21_out, B, nand_11_out, nand_12_out, nand_13_out);
  nand nand_22 (nand_22_out, nand_14_out, nand_15_out);
  nand nand_23 (nand_23_out, nand_16_out, nand_17_out, nand_18_out);
  nand nand_24 (nand_24_out, nand_19_out, nand_20_out, nand_21_out);
  and and_1 (and_1_out, nand_22_out, ~PoR);  // AND_Gate
  not not_1 (not_1_out, and_1_out);
  and and_2 (and_2_out, nand_23_out, ~PoR);  // AND_Gate
  not not_2 (not_2_out, and_2_out);
  and and_3 (and_3_out, nand_24_out, ~PoR);  // AND_Gate
  not not_3 (not_3_out, and_3_out);
  S_R_Flip_Flop s_r_ff_1 (.S(and_1_out), .R(not_1_out), .clk(Clk), .Q(s_r_ff_1_q), .reset(PoR));  // open: Qn, preset
  S_R_Flip_Flop s_r_ff_2 (.S(and_2_out), .R(not_2_out), .clk(Clk), .Q(mode[1]), .reset(PoR));  // open: Qn, preset
  S_R_Flip_Flop s_r_ff_3 (.S(and_3_out), .R(not_3_out), .clk(Clk), .Q(mode[0]), .reset(PoR));  // open: Qn, preset
endmodule

module n4_modes (
  input  B,
  input  PoR,
  input  Clk,
  output [1:0] mode
);

  wire and_1_out, and_2_out, and_3_out, nand_1_out, nand_2_out, nand_3_out, nand_4_out, nand_5_out,
       nand_6_out, nand_7_out, nand_8_out, nand_9_out, nand_10_out, nand_11_out, nand_12_out, nand_13_out,
       nand_14_out, nand_15_out, nand_16_out, not_1_out, not_2_out, not_3_out, s_r_ff_1_q;

  nand nand_1 (nand_1_out, B, B);
  nand nand_2 (nand_2_out, mode[0], mode[0]);
  nand nand_3 (nand_3_out, s_r_ff_1_q, s_r_ff_1_q);
  nand nand_4 (nand_4_out, mode[1], mode[1]);
  nand nand_5 (nand_5_out, B, B);
  nand nand_6 (nand_6_out, s_r_ff_1_q, s_r_ff_1_q);
  nand nand_7 (nand_7_out, mode[0], mode[0]);
  nand nand_8 (nand_8_out, nand_1_out, mode[1]);
  nand nand_9 (nand_9_out, mode[1], nand_2_out);
  nand nand_10 (nand_10_out, s_r_ff_1_q, mode[1]);
  nand nand_11 (nand_11_out, B, nand_3_out, nand_4_out, mode[0]);
  nand nand_12 (nand_12_out, nand_5_out, mode[0]);
  nand nand_13 (nand_13_out, s_r_ff_1_q, mode[0]);
  nand nand_14 (nand_14_out, B, nand_6_out, nand_7_out);
  nand nand_15 (nand_15_out, nand_8_out, nand_9_out, nand_10_out, nand_11_out);
  nand nand_16 (nand_16_out, nand_12_out, nand_13_out, nand_14_out);
  and and_1 (and_1_out, B, ~PoR);  // AND_Gate
  not not_1 (not_1_out, and_1_out);
  and and_2 (and_2_out, nand_15_out, ~PoR);  // AND_Gate
  not not_2 (not_2_out, and_2_out);
  and and_3 (and_3_out, nand_16_out, ~PoR);  // AND_Gate
  not not_3 (not_3_out, and_3_out);
  S_R_Flip_Flop s_r_ff_1 (.S(and_1_out), .R(not_1_out), .clk(Clk), .Q(s_r_ff_1_q), .reset(PoR));  // open: Qn, preset
  S_R_Flip_Flop s_r_ff_2 (.S(and_2_out), .R(not_2_out), .clk(Clk), .Q(mode[1]), .reset(PoR));  // open: Qn, preset
  S_R_Flip_Flop s_r_ff_3 (.S(and_3_out), .R(not_3_out), .clk(Clk), .Q(mode[0]), .reset(PoR));  // open: Qn, preset
endmodule

module n5_modes (
  input  B,
  input  PoR,
  input  Clk,
  output [2:0] mode
);

  wire and_1_out, and_2_out, and_3_out, and_4_out, nand_1_out, nand_2_out, nand_3_out, nand_4_out,
       nand_5_out, nand_6_out, nand_7_out, nand_8_out, nand_9_out, nand_10_out, nand_11_out, nand_12_out,
       nand_13_out, nand_14_out, nand_15_out, nand_16_out, nand_17_out, nand_18_out, nand_19_out,
       nand_20_out, nand_21_out, nand_22_out, nand_23_out, not_1_out, not_2_out, not_3_out, not_4_out,
       s_r_ff_1_q;

  nand nand_1 (nand_1_out, B, B);
  nand nand_2 (nand_2_out, s_r_ff_1_q, s_r_ff_1_q);
  nand nand_3 (nand_3_out, B, B);
  nand nand_4 (nand_4_out, mode[0], mode[0]);
  nand nand_5 (nand_5_out, s_r_ff_1_q, s_r_ff_1_q);
  nand nand_6 (nand_6_out, mode[1], mode[1]);
  nand nand_7 (nand_7_out, B, B);
  nand nand_8 (nand_8_out, s_r_ff_1_q, s_r_ff_1_q);
  nand nand_9 (nand_9_out, mode[2], mode[2]);
  nand nand_10 (nand_10_out, mode[0], mode[0]);
  nand nand_11 (nand_11_out, nand_1_out, mode[2]);
  nand nand_12 (nand_12_out, s_r_ff_1_q, mode[2]);
  nand nand_13 (nand_13_out, B, nand_2_out, mode[1], mode[0]);
  nand nand_14 (nand_14_out, nand_3_out, mode[1]);
  nand nand_15 (nand_15_out, mode[1], nand_4_out);
  nand nand_16 (nand_16_out, s_r_ff_1_q, mode[1]);
  nand nand_17 (nand_17_out, B, nand_5_out, nand_6_out, mode[0]);
  nand nand_18 (nand_18_out, nand_7_out, mode[0]);
  nand nand_19 (nand_19_out, s_r_ff_1_q, mode[0]);
  nand nand_20 (nand_20_out, B, nand_8_out, nand_9_out, nand_10_out);
  nand nand_21 (nand_21_out, nand_11_out, nand_12_out, nand_13_out);
  nand nand_22 (nand_22_out, nand_14_out, nand_15_out, nand_16_out, nand_17_out);
  nand nand_23 (nand_23_out, nand_18_out, nand_19_out, nand_20_out);
  and and_1 (and_1_out, B, ~PoR);  // AND_Gate
  not not_1 (not_1_out, and_1_out);
  and and_2 (and_2_out, nand_21_out, ~PoR);  // AND_Gate
  not not_2 (not_2_out, and_2_out);
  and and_3 (and_3_out, nand_22_out, ~PoR);  // AND_Gate
  not not_3 (not_3_out, and_3_out);
  and and_4 (and_4_out, nand_23_out, ~PoR);  // AND_Gate
  not not_4 (not_4_out, and_4_out);
  S_R_Flip_Flop s_r_ff_1 (.S(and_1_out), .R(not_1_out), .clk(Clk), .Q(s_r_ff_1_q), .reset(PoR));  // open: Qn, preset
  S_R_Flip_Flop s_r_ff_2 (.S(and_2_out), .R(not_2_out), .clk(Clk), .Q(mode[2]), .reset(PoR));  // open: Qn, preset
  S_R_Flip_Flop s_r_ff_3 (.S(and_3_out), .R(not_3_out), .clk(Clk), .Q(mode[1]), .reset(PoR));  // open: Qn, preset
  S_R_Flip_Flop s_r_ff_4 (.S(and_4_out), .R(not_4_out), .clk(Clk), .Q(mode[0]), .reset(PoR));  // open: Qn, preset
endmodule

module n6_modes (
  input  B,
  input  PoR,
  input  Clk,
  input  [2:0] set_val,
  input  set_on,
  output [2:0] mode
);

  wire and_1_out, and_2_out, and_3_out, and_4_out, multiplexer_1_out, multiplexer_2_out, multiplexer_3_out,
       multiplexer_4_out, nand_1_out, nand_2_out, nand_3_out, nand_4_out, nand_5_out, nand_6_out, nand_7_out,
       nand_8_out, nand_9_out, nand_10_out, nand_11_out, nand_12_out, nand_13_out, nand_14_out, nand_15_out,
       nand_16_out, nand_17_out, nand_18_out, nand_19_out, nand_20_out, nand_21_out, nand_22_out,
       nand_23_out, nand_24_out, nand_25_out, not_1_out, not_2_out, not_3_out, not_4_out, s_r_ff_1_q;

  nand nand_1 (nand_1_out, B, B);
  nand nand_2 (nand_2_out, mode[0], mode[0]);
  nand nand_3 (nand_3_out, s_r_ff_1_q, s_r_ff_1_q);
  nand nand_4 (nand_4_out, B, B);
  nand nand_5 (nand_5_out, mode[0], mode[0]);
  nand nand_6 (nand_6_out, s_r_ff_1_q, s_r_ff_1_q);
  nand nand_7 (nand_7_out, mode[2], mode[2]);
  nand nand_8 (nand_8_out, mode[1], mode[1]);
  nand nand_9 (nand_9_out, B, B);
  nand nand_10 (nand_10_out, s_r_ff_1_q, s_r_ff_1_q);
  nand nand_11 (nand_11_out, mode[0], mode[0]);
  nand nand_12 (nand_12_out, nand_1_out, mode[2]);
  nand nand_13 (nand_13_out, mode[2], nand_2_out);
  nand nand_14 (nand_14_out, s_r_ff_1_q, mode[2]);
  nand nand_15 (nand_15_out, B, nand_3_out, mode[1], mode[0]);
  nand nand_16 (nand_16_out, nand_4_out, mode[1]);
  nand nand_17 (nand_17_out, mode[1], nand_5_out);
  nand nand_18 (nand_18_out, s_r_ff_1_q, mode[1]);
  nand nand_19 (nand_19_out, B, nand_6_out, nand_7_out, nand_8_out, mode[0]);
  nand nand_20 (nand_20_out, nand_9_out, mode[0]);
  nand nand_21 (nand_21_out, s_r_ff_1_q, mode[0]);
  nand nand_22 (nand_22_out, B, nand_10_out, nand_11_out);
  nand nand_23 (nand_23_out, nand_20_out, nand_21_out, nand_22_out);
  nand nand_24 (nand_24_out, nand_12_out, nand_13_out, nand_14_out, nand_15_out);
  nand nand_25 (nand_25_out, nand_16_out, nand_17_out, nand_18_out, nand_19_out);
  Multiplexer #(.enable("false")) multiplexer_1 (.in0(B), .in1(1'b0), .out(multiplexer_1_out), .sel(set_on));
  Multiplexer #(.enable("false")) multiplexer_2 (
    .in0(nand_24_out), .in1(set_val[2]), .out(multiplexer_2_out), .sel(set_on));
  Multiplexer #(.enable("false")) multiplexer_3 (
    .in0(nand_25_out), .in1(set_val[1]), .out(multiplexer_3_out), .sel(set_on));
  Multiplexer #(.enable("false")) multiplexer_4 (
    .in0(nand_23_out), .in1(set_val[0]), .out(multiplexer_4_out), .sel(set_on));
  and and_1 (and_1_out, multiplexer_1_out, ~PoR);  // AND_Gate
  and and_2 (and_2_out, multiplexer_2_out, ~PoR);  // AND_Gate
  and and_3 (and_3_out, multiplexer_3_out, ~PoR);  // AND_Gate
  and and_4 (and_4_out, multiplexer_4_out, ~PoR);  // AND_Gate
  S_R_Flip_Flop s_r_ff_1 (.S(and_1_out), .R(not_1_out), .clk(Clk), .Q(s_r_ff_1_q), .reset(PoR));  // open: Qn, preset
  not not_1 (not_1_out, and_1_out);
  S_R_Flip_Flop s_r_ff_2 (.S(and_2_out), .R(not_2_out), .clk(Clk), .Q(mode[2]), .reset(PoR));  // open: Qn, preset
  not not_2 (not_2_out, and_2_out);
  S_R_Flip_Flop s_r_ff_3 (.S(and_3_out), .R(not_3_out), .clk(Clk), .Q(mode[1]), .reset(PoR));  // open: Qn, preset
  not not_3 (not_3_out, and_3_out);
  S_R_Flip_Flop s_r_ff_4 (.S(and_4_out), .R(not_4_out), .clk(Clk), .Q(mode[0]), .reset(PoR));  // open: Qn, preset
  not not_4 (not_4_out, and_4_out);
endmodule

module n7_modes (
  input  B,
  input  PoR,
  input  Clk,
  output [2:0] mode
);

  wire and_1_out, and_2_out, and_3_out, and_4_out, nand_1_out, nand_2_out, nand_3_out, nand_4_out,
       nand_5_out, nand_6_out, nand_7_out, nand_8_out, nand_9_out, nand_10_out, nand_11_out, nand_12_out,
       nand_13_out, nand_14_out, nand_15_out, nand_16_out, nand_17_out, nand_18_out, nand_19_out,
       nand_20_out, nand_21_out, nand_22_out, nand_23_out, nand_24_out, nand_25_out, nand_26_out,
       nand_27_out, nand_28_out, nand_29_out, nand_30_out, not_1_out, not_2_out, not_3_out, not_4_out,
       s_r_ff_1_q;

  nand nand_1 (nand_1_out, B, B);
  nand nand_2 (nand_2_out, mode[1], mode[1]);
  nand nand_3 (nand_3_out, s_r_ff_1_q, s_r_ff_1_q);
  nand nand_4 (nand_4_out, B, B);
  nand nand_5 (nand_5_out, mode[2], mode[2]);
  nand nand_6 (nand_6_out, mode[0], mode[0]);
  nand nand_7 (nand_7_out, s_r_ff_1_q, s_r_ff_1_q);
  nand nand_8 (nand_8_out, mode[1], mode[1]);
  nand nand_9 (nand_9_out, B, B);
  nand nand_10 (nand_10_out, s_r_ff_1_q, s_r_ff_1_q);
  nand nand_11 (nand_11_out, mode[2], mode[2]);
  nand nand_12 (nand_12_out, mode[0], mode[0]);
  nand nand_13 (nand_13_out, s_r_ff_1_q, s_r_ff_1_q);
  nand nand_14 (nand_14_out, mode[1], mode[1]);
  nand nand_15 (nand_15_out, mode[0], mode[0]);
  nand nand_16 (nand_16_out, nand_1_out, mode[2]);
  nand nand_17 (nand_17_out, mode[2], nand_2_out);
  nand nand_18 (nand_18_out, s_r_ff_1_q, mode[2]);
  nand nand_19 (nand_19_out, B, nand_3_out, mode[1], mode[0]);
  nand nand_20 (nand_20_out, nand_4_out, mode[1]);
  nand nand_21 (nand_21_out, nand_5_out, mode[1], nand_6_out);
  nand nand_22 (nand_22_out, s_r_ff_1_q, mode[1]);
  nand nand_23 (nand_23_out, B, nand_7_out, nand_8_out, mode[0]);
  nand nand_24 (nand_24_out, nand_9_out, mode[0]);
  nand nand_25 (nand_25_out, s_r_ff_1_q, mode[0]);
  nand nand_26 (nand_26_out, B, nand_10_out, nand_11_out, nand_12_out);
  nand nand_27 (nand_27_out, B, nand_13_out, nand_14_out, nand_15_out);
  nand nand_28 (nand_28_out, nand_16_out, nand_17_out, nand_18_out, nand_19_out);
  nand nand_29 (nand_29_out, nand_20_out, nand_21_out, nand_22_out, nand_23_out);
  nand nand_30 (nand_30_out, nand_24_out, nand_25_out, nand_26_out, nand_27_out);
  and and_1 (and_1_out, B, ~PoR);  // AND_Gate
  not not_1 (not_1_out, and_1_out);
  and and_2 (and_2_out, nand_28_out, ~PoR);  // AND_Gate
  not not_2 (not_2_out, and_2_out);
  and and_3 (and_3_out, nand_29_out, ~PoR);  // AND_Gate
  not not_3 (not_3_out, and_3_out);
  and and_4 (and_4_out, nand_30_out, ~PoR);  // AND_Gate
  not not_4 (not_4_out, and_4_out);
  S_R_Flip_Flop s_r_ff_1 (.S(and_1_out), .R(not_1_out), .clk(Clk), .Q(s_r_ff_1_q), .reset(PoR));  // open: Qn, preset
  S_R_Flip_Flop s_r_ff_2 (.S(and_2_out), .R(not_2_out), .clk(Clk), .Q(mode[2]), .reset(PoR));  // open: Qn, preset
  S_R_Flip_Flop s_r_ff_3 (.S(and_3_out), .R(not_3_out), .clk(Clk), .Q(mode[1]), .reset(PoR));  // open: Qn, preset
  S_R_Flip_Flop s_r_ff_4 (.S(and_4_out), .R(not_4_out), .clk(Clk), .Q(mode[0]), .reset(PoR));  // open: Qn, preset
endmodule

module n8_modes (
  input  B,
  input  PoR,
  input  Clk,
  output [2:0] mode
);

  wire and_1_out, and_2_out, and_3_out, and_4_out, nand_1_out, nand_2_out, nand_3_out, nand_4_out,
       nand_5_out, nand_6_out, nand_7_out, nand_8_out, nand_9_out, nand_10_out, nand_11_out, nand_12_out,
       nand_13_out, nand_14_out, nand_15_out, nand_16_out, nand_17_out, nand_18_out, nand_19_out,
       nand_20_out, nand_21_out, nand_22_out, nand_23_out, nand_24_out, nand_25_out, nand_26_out,
       nand_27_out, not_1_out, not_2_out, not_3_out, not_4_out, s_r_ff_1_q;

  nand nand_1 (nand_1_out, B, B);
  nand nand_2 (nand_2_out, mode[1], mode[1]);
  nand nand_3 (nand_3_out, mode[0], mode[0]);
  nand nand_4 (nand_4_out, s_r_ff_1_q, s_r_ff_1_q);
  nand nand_5 (nand_5_out, mode[2], mode[2]);
  nand nand_6 (nand_6_out, B, B);
  nand nand_7 (nand_7_out, mode[0], mode[0]);
  nand nand_8 (nand_8_out, s_r_ff_1_q, s_r_ff_1_q);
  nand nand_9 (nand_9_out, mode[1], mode[1]);
  nand nand_10 (nand_10_out, B, B);
  nand nand_11 (nand_11_out, s_r_ff_1_q, s_r_ff_1_q);
  nand nand_12 (nand_12_out, mode[0], mode[0]);
  nand nand_13 (nand_13_out, nand_1_out, mode[2]);
  nand nand_14 (nand_14_out, mode[2], nand_2_out);
  nand nand_15 (nand_15_out, mode[2], nand_3_out);
  nand nand_16 (nand_16_out, s_r_ff_1_q, mode[2]);
  nand nand_17 (nand_17_out, B, nand_4_out, nand_5_out, mode[1], mode[0]);
  nand nand_18 (nand_18_out, nand_6_out, mode[1]);
  nand nand_19 (nand_19_out, mode[1], nand_7_out);
  nand nand_20 (nand_20_out, s_r_ff_1_q, mode[1]);
  nand nand_21 (nand_21_out, B, nand_8_out, nand_9_out, mode[0]);
  nand nand_22 (nand_22_out, nand_10_out, mode[0]);
  nand nand_23 (nand_23_out, s_r_ff_1_q, mode[0]);
  nand nand_24 (nand_24_out, B, nand_11_out, nand_12_out);
  nand nand_25 (nand_25_out, nand_13_out, nand_14_out, nand_15_out, nand_16_out, nand_17_out);
  nand nand_26 (nand_26_out, nand_18_out, nand_19_out, nand_20_out, nand_21_out);
  nand nand_27 (nand_27_out, nand_22_out, nand_23_out, nand_24_out);
  and and_1 (and_1_out, B, ~PoR);  // AND_Gate
  not not_1 (not_1_out, and_1_out);
  and and_2 (and_2_out, nand_25_out, ~PoR);  // AND_Gate
  not not_2 (not_2_out, and_2_out);
  and and_3 (and_3_out, nand_26_out, ~PoR);  // AND_Gate
  not not_3 (not_3_out, and_3_out);
  and and_4 (and_4_out, nand_27_out, ~PoR);  // AND_Gate
  not not_4 (not_4_out, and_4_out);
  S_R_Flip_Flop s_r_ff_1 (.S(and_1_out), .R(not_1_out), .clk(Clk), .Q(s_r_ff_1_q), .reset(PoR));  // open: Qn, preset
  S_R_Flip_Flop s_r_ff_2 (.S(and_2_out), .R(not_2_out), .clk(Clk), .Q(mode[2]), .reset(PoR));  // open: Qn, preset
  S_R_Flip_Flop s_r_ff_3 (.S(and_3_out), .R(not_3_out), .clk(Clk), .Q(mode[1]), .reset(PoR));  // open: Qn, preset
  S_R_Flip_Flop s_r_ff_4 (.S(and_4_out), .R(not_4_out), .clk(Clk), .Q(mode[0]), .reset(PoR));  // open: Qn, preset
endmodule

module n9_modes (
  input  B,
  input  PoR,
  input  Clk,
  output [3:0] mode
);

  wire and_1_out, and_2_out, and_3_out, and_4_out, and_5_out, nand_1_out, nand_2_out, nand_3_out, nand_4_out,
       nand_5_out, nand_6_out, nand_7_out, nand_8_out, nand_9_out, nand_10_out, nand_11_out, nand_12_out,
       nand_13_out, nand_14_out, nand_15_out, nand_16_out, nand_17_out, nand_18_out, nand_19_out,
       nand_20_out, nand_21_out, nand_22_out, nand_23_out, nand_24_out, nand_25_out, nand_26_out,
       nand_27_out, nand_28_out, nand_29_out, nand_30_out, nand_31_out, nand_32_out, nand_33_out,
       nand_34_out, not_1_out, not_2_out, not_3_out, not_4_out, not_5_out, s_r_ff_1_q;

  nand nand_1 (nand_1_out, B, B);
  nand nand_2 (nand_2_out, s_r_ff_1_q, s_r_ff_1_q);
  nand nand_3 (nand_3_out, B, B);
  nand nand_4 (nand_4_out, mode[1], mode[1]);
  nand nand_5 (nand_5_out, mode[0], mode[0]);
  nand nand_6 (nand_6_out, s_r_ff_1_q, s_r_ff_1_q);
  nand nand_7 (nand_7_out, mode[2], mode[2]);
  nand nand_8 (nand_8_out, B, B);
  nand nand_9 (nand_9_out, mode[0], mode[0]);
  nand nand_10 (nand_10_out, s_r_ff_1_q, s_r_ff_1_q);
  nand nand_11 (nand_11_out, mode[1], mode[1]);
  nand nand_12 (nand_12_out, B, B);
  nand nand_13 (nand_13_out, s_r_ff_1_q, s_r_ff_1_q);
  nand nand_14 (nand_14_out, mode[3], mode[3]);
  nand nand_15 (nand_15_out, mode[0], mode[0]);
  nand nand_16 (nand_16_out, nand_1_out, mode[3]);
  nand nand_17 (nand_17_out, s_r_ff_1_q, mode[3]);
  nand nand_18 (nand_18_out, B, nand_2_out, mode[2], mode[1], mode[0]);
  nand nand_19 (nand_19_out, nand_3_out, mode[2]);
  nand nand_20 (nand_20_out, mode[2], nand_4_out);
  nand nand_21 (nand_21_out, mode[2], nand_5_out);
  nand nand_22 (nand_22_out, s_r_ff_1_q, mode[2]);
  nand nand_23 (nand_23_out, B, nand_6_out, nand_7_out, mode[1], mode[0]);
  nand nand_24 (nand_24_out, nand_8_out, mode[1]);
  nand nand_25 (nand_25_out, mode[1], nand_9_out);
  nand nand_26 (nand_26_out, s_r_ff_1_q, mode[1]);
  nand nand_27 (nand_27_out, B, nand_10_out, nand_11_out, mode[0]);
  nand nand_28 (nand_28_out, nand_12_out, mode[0]);
  nand nand_29 (nand_29_out, s_r_ff_1_q, mode[0]);
  nand nand_30 (nand_30_out, B, nand_13_out, nand_14_out, nand_15_out);
  nand nand_31 (nand_31_out, nand_16_out, nand_17_out, nand_18_out);
  nand nand_32 (nand_32_out, nand_19_out, nand_20_out, nand_21_out, nand_22_out, nand_23_out);
  nand nand_33 (nand_33_out, nand_24_out, nand_25_out, nand_26_out, nand_27_out);
  nand nand_34 (nand_34_out, nand_28_out, nand_29_out, nand_30_out);
  and and_1 (and_1_out, B, ~PoR);  // AND_Gate
  not not_1 (not_1_out, and_1_out);
  and and_2 (and_2_out, nand_31_out, ~PoR);  // AND_Gate
  not not_2 (not_2_out, and_2_out);
  and and_3 (and_3_out, nand_32_out, ~PoR);  // AND_Gate
  not not_3 (not_3_out, and_3_out);
  and and_4 (and_4_out, nand_33_out, ~PoR);  // AND_Gate
  not not_4 (not_4_out, and_4_out);
  and and_5 (and_5_out, nand_34_out, ~PoR);  // AND_Gate
  not not_5 (not_5_out, and_5_out);
  S_R_Flip_Flop s_r_ff_1 (.S(and_1_out), .R(not_1_out), .clk(Clk), .Q(s_r_ff_1_q), .reset(PoR));  // open: Qn, preset
  S_R_Flip_Flop s_r_ff_2 (.S(and_2_out), .R(not_2_out), .clk(Clk), .Q(mode[3]), .reset(PoR));  // open: Qn, preset
  S_R_Flip_Flop s_r_ff_3 (.S(and_3_out), .R(not_3_out), .clk(Clk), .Q(mode[2]), .reset(PoR));  // open: Qn, preset
  S_R_Flip_Flop s_r_ff_4 (.S(and_4_out), .R(not_4_out), .clk(Clk), .Q(mode[1]), .reset(PoR));  // open: Qn, preset
  S_R_Flip_Flop s_r_ff_5 (.S(and_5_out), .R(not_5_out), .clk(Clk), .Q(mode[0]), .reset(PoR));  // open: Qn, preset
endmodule

module n10_modes (
  input  B,
  input  PoR,
  input  Clk,
  input  [3:0] set_val,
  input  set_on,
  output [3:0] mode
);

  wire and_1_out, and_2_out, and_3_out, and_4_out, and_5_out, multiplexer_1_out, multiplexer_2_out,
       multiplexer_3_out, multiplexer_4_out, multiplexer_5_out, nand_1_out, nand_2_out, nand_3_out,
       nand_4_out, nand_5_out, nand_6_out, nand_7_out, nand_8_out, nand_9_out, nand_10_out, nand_11_out,
       nand_12_out, nand_13_out, nand_14_out, nand_15_out, nand_16_out, nand_17_out, nand_18_out,
       nand_19_out, nand_20_out, nand_21_out, nand_22_out, nand_23_out, nand_24_out, nand_25_out,
       nand_26_out, nand_27_out, nand_28_out, nand_29_out, nand_30_out, nand_31_out, nand_32_out,
       nand_33_out, nand_34_out, nand_35_out, nand_36_out, not_1_out, not_2_out, not_3_out, not_4_out,
       not_5_out, s_r_ff_1_q;

  nand nand_1 (nand_1_out, B, B);
  nand nand_2 (nand_2_out, mode[0], mode[0]);
  nand nand_3 (nand_3_out, s_r_ff_1_q, s_r_ff_1_q);
  nand nand_4 (nand_4_out, B, B);
  nand nand_5 (nand_5_out, mode[1], mode[1]);
  nand nand_6 (nand_6_out, mode[0], mode[0]);
  nand nand_7 (nand_7_out, s_r_ff_1_q, s_r_ff_1_q);
  nand nand_8 (nand_8_out, mode[2], mode[2]);
  nand nand_9 (nand_9_out, B, B);
  nand nand_10 (nand_10_out, mode[0], mode[0]);
  nand nand_11 (nand_11_out, s_r_ff_1_q, s_r_ff_1_q);
  nand nand_12 (nand_12_out, mode[3], mode[3]);
  nand nand_13 (nand_13_out, mode[1], mode[1]);
  nand nand_14 (nand_14_out, B, B);
  nand nand_15 (nand_15_out, s_r_ff_1_q, s_r_ff_1_q);
  nand nand_16 (nand_16_out, mode[0], mode[0]);
  nand nand_17 (nand_17_out, nand_1_out, mode[3]);
  nand nand_18 (nand_18_out, mode[3], nand_2_out);
  nand nand_19 (nand_19_out, s_r_ff_1_q, mode[3]);
  nand nand_20 (nand_20_out, B, nand_3_out, mode[2], mode[1], mode[0]);
  nand nand_21 (nand_21_out, nand_4_out, mode[2]);
  nand nand_22 (nand_22_out, mode[2], nand_5_out);
  nand nand_23 (nand_23_out, mode[2], nand_6_out);
  nand nand_24 (nand_24_out, s_r_ff_1_q, mode[2]);
  nand nand_25 (nand_25_out, B, nand_7_out, nand_8_out, mode[1], mode[0]);
  nand nand_26 (nand_26_out, nand_9_out, mode[1]);
  nand nand_27 (nand_27_out, mode[1], nand_10_out);
  nand nand_28 (nand_28_out, s_r_ff_1_q, mode[1]);
  nand nand_29 (nand_29_out, B, nand_11_out, nand_12_out, nand_13_out, mode[0]);
  nand nand_30 (nand_30_out, nand_14_out, mode[0]);
  nand nand_31 (nand_31_out, s_r_ff_1_q, mode[0]);
  nand nand_32 (nand_32_out, B, nand_15_out, nand_16_out);
  nand nand_33 (nand_33_out, nand_17_out, nand_18_out, nand_19_out, nand_20_out);
  nand nand_34 (nand_34_out, nand_21_out, nand_22_out, nand_23_out, nand_24_out, nand_25_out);
  nand nand_35 (nand_35_out, nand_26_out, nand_27_out, nand_28_out, nand_29_out);
  nand nand_36 (nand_36_out, nand_30_out, nand_31_out, nand_32_out);
  Multiplexer #(.enable("false")) multiplexer_1 (.in0(B), .in1(1'b0), .out(multiplexer_1_out), .sel(set_on));
  Multiplexer #(.enable("false")) multiplexer_2 (
    .in0(nand_33_out), .in1(set_val[3]), .out(multiplexer_2_out), .sel(set_on));
  Multiplexer #(.enable("false")) multiplexer_3 (
    .in0(nand_34_out), .in1(set_val[2]), .out(multiplexer_3_out), .sel(set_on));
  Multiplexer #(.enable("false")) multiplexer_4 (
    .in0(nand_35_out), .in1(set_val[1]), .out(multiplexer_4_out), .sel(set_on));
  Multiplexer #(.enable("false")) multiplexer_5 (
    .in0(nand_36_out), .in1(set_val[0]), .out(multiplexer_5_out), .sel(set_on));
  and and_1 (and_1_out, multiplexer_1_out, ~PoR);  // AND_Gate
  not not_1 (not_1_out, and_1_out);
  and and_2 (and_2_out, multiplexer_2_out, ~PoR);  // AND_Gate
  not not_2 (not_2_out, and_2_out);
  and and_3 (and_3_out, multiplexer_3_out, ~PoR);  // AND_Gate
  not not_3 (not_3_out, and_3_out);
  and and_4 (and_4_out, multiplexer_4_out, ~PoR);  // AND_Gate
  not not_4 (not_4_out, and_4_out);
  and and_5 (and_5_out, multiplexer_5_out, ~PoR);  // AND_Gate
  not not_5 (not_5_out, and_5_out);
  S_R_Flip_Flop s_r_ff_1 (.S(and_1_out), .R(not_1_out), .clk(Clk), .Q(s_r_ff_1_q), .reset(PoR));  // open: Qn, preset
  S_R_Flip_Flop s_r_ff_2 (.S(and_2_out), .R(not_2_out), .clk(Clk), .Q(mode[3]), .reset(PoR));  // open: Qn, preset
  S_R_Flip_Flop s_r_ff_3 (.S(and_3_out), .R(not_3_out), .clk(Clk), .Q(mode[2]), .reset(PoR));  // open: Qn, preset
  S_R_Flip_Flop s_r_ff_4 (.S(and_4_out), .R(not_4_out), .clk(Clk), .Q(mode[1]), .reset(PoR));  // open: Qn, preset
  S_R_Flip_Flop s_r_ff_5 (.S(and_5_out), .R(not_5_out), .clk(Clk), .Q(mode[0]), .reset(PoR));  // open: Qn, preset
endmodule

module n12_modes (
  input  B,
  input  PoR,
  input  Clk,
  output [3:0] mode
);

  wire and_1_out, and_2_out, and_3_out, and_4_out, and_5_out, nand_1_out, nand_2_out, nand_3_out, nand_4_out,
       nand_5_out, nand_6_out, nand_7_out, nand_8_out, nand_9_out, nand_10_out, nand_11_out, nand_12_out,
       nand_13_out, nand_14_out, nand_15_out, nand_16_out, nand_17_out, nand_18_out, nand_19_out,
       nand_20_out, nand_21_out, nand_22_out, nand_23_out, nand_24_out, nand_25_out, nand_26_out,
       nand_27_out, nand_28_out, nand_29_out, nand_30_out, nand_31_out, nand_32_out, nand_33_out,
       nand_34_out, nand_35_out, nand_36_out, nand_37_out, nand_38_out, not_1_out, not_2_out, not_3_out,
       not_4_out, not_5_out, s_r_ff_1_q;

  nand nand_1 (nand_1_out, B, B);
  nand nand_2 (nand_2_out, mode[1], mode[1]);
  nand nand_3 (nand_3_out, mode[0], mode[0]);
  nand nand_4 (nand_4_out, s_r_ff_1_q, s_r_ff_1_q);
  nand nand_5 (nand_5_out, B, B);
  nand nand_6 (nand_6_out, mode[1], mode[1]);
  nand nand_7 (nand_7_out, mode[0], mode[0]);
  nand nand_8 (nand_8_out, s_r_ff_1_q, s_r_ff_1_q);
  nand nand_9 (nand_9_out, mode[3], mode[3]);
  nand nand_10 (nand_10_out, mode[2], mode[2]);
  nand nand_11 (nand_11_out, B, B);
  nand nand_12 (nand_12_out, mode[0], mode[0]);
  nand nand_13 (nand_13_out, s_r_ff_1_q, s_r_ff_1_q);
  nand nand_14 (nand_14_out, mode[1], mode[1]);
  nand nand_15 (nand_15_out, B, B);
  nand nand_16 (nand_16_out, s_r_ff_1_q, s_r_ff_1_q);
  nand nand_17 (nand_17_out, mode[0], mode[0]);
  nand nand_18 (nand_18_out, nand_1_out, mode[3]);
  nand nand_19 (nand_19_out, mode[3], nand_2_out);
  nand nand_20 (nand_20_out, mode[3], nand_3_out);
  nand nand_21 (nand_21_out, s_r_ff_1_q, mode[3]);
  nand nand_22 (nand_22_out, B, nand_4_out, mode[2], mode[1], mode[0]);
  nand nand_23 (nand_23_out, nand_5_out, mode[2]);
  nand nand_24 (nand_24_out, mode[2], nand_6_out);
  nand nand_25 (nand_25_out, mode[2], nand_7_out);
  nand nand_26 (nand_26_out, s_r_ff_1_q, mode[2]);
  nand nand_27 (nand_27_out, B, nand_8_out, nand_9_out, nand_10_out, mode[1], mode[0]);
  nand nand_28 (nand_28_out, nand_11_out, mode[1]);
  nand nand_29 (nand_29_out, mode[1], nand_12_out);
  nand nand_30 (nand_30_out, s_r_ff_1_q, mode[1]);
  nand nand_31 (nand_31_out, B, nand_13_out, nand_14_out, mode[0]);
  nand nand_32 (nand_32_out, nand_15_out, mode[0]);
  nand nand_33 (nand_33_out, s_r_ff_1_q, mode[0]);
  nand nand_34 (nand_34_out, B, nand_16_out, nand_17_out);
  nand nand_35 (nand_35_out, nand_18_out, nand_19_out, nand_20_out, nand_21_out, nand_22_out);
  nand nand_36 (nand_36_out, nand_28_out, nand_29_out, nand_30_out, nand_31_out);
  nand nand_37 (nand_37_out, nand_32_out, nand_33_out, nand_34_out);
  nand nand_38 (nand_38_out, nand_23_out, nand_24_out, nand_25_out, nand_26_out, nand_27_out);
  and and_1 (and_1_out, B, ~PoR);  // AND_Gate
  not not_1 (not_1_out, and_1_out);
  and and_2 (and_2_out, nand_35_out, ~PoR);  // AND_Gate
  not not_2 (not_2_out, and_2_out);
  and and_3 (and_3_out, nand_38_out, ~PoR);  // AND_Gate
  not not_3 (not_3_out, and_3_out);
  and and_4 (and_4_out, nand_36_out, ~PoR);  // AND_Gate
  not not_4 (not_4_out, and_4_out);
  and and_5 (and_5_out, nand_37_out, ~PoR);  // AND_Gate
  not not_5 (not_5_out, and_5_out);
  S_R_Flip_Flop s_r_ff_1 (.S(and_1_out), .R(not_1_out), .clk(Clk), .Q(s_r_ff_1_q), .reset(PoR));  // open: Qn, preset
  S_R_Flip_Flop s_r_ff_2 (.S(and_2_out), .R(not_2_out), .clk(Clk), .Q(mode[3]), .reset(PoR));  // open: Qn, preset
  S_R_Flip_Flop s_r_ff_3 (.S(and_3_out), .R(not_3_out), .clk(Clk), .Q(mode[2]), .reset(PoR));  // open: Qn, preset
  S_R_Flip_Flop s_r_ff_4 (.S(and_4_out), .R(not_4_out), .clk(Clk), .Q(mode[1]), .reset(PoR));  // open: Qn, preset
  S_R_Flip_Flop s_r_ff_5 (.S(and_5_out), .R(not_5_out), .clk(Clk), .Q(mode[0]), .reset(PoR));  // open: Qn, preset
endmodule

module n24_modes (
  input  B,
  input  PoR,
  input  Clk,
  input  [4:0] set_val,
  input  set_on,
  output [4:0] mode
);

  wire and_1_out, and_2_out, and_3_out, and_4_out, and_5_out, and_6_out, multiplexer_1_out,
       multiplexer_2_out, multiplexer_3_out, multiplexer_4_out, multiplexer_5_out, multiplexer_6_out,
       nand_1_out, nand_2_out, nand_3_out, nand_4_out, nand_5_out, nand_6_out, nand_7_out, nand_8_out,
       nand_9_out, nand_10_out, nand_11_out, nand_12_out, nand_13_out, nand_14_out, nand_15_out, nand_16_out,
       nand_17_out, nand_18_out, nand_19_out, nand_20_out, nand_21_out, nand_22_out, nand_23_out,
       nand_24_out, nand_25_out, nand_26_out, nand_27_out, nand_28_out, nand_29_out, nand_30_out,
       nand_31_out, nand_32_out, nand_33_out, nand_34_out, nand_35_out, nand_36_out, nand_37_out,
       nand_38_out, nand_39_out, nand_40_out, nand_41_out, nand_42_out, nand_43_out, nand_44_out,
       nand_45_out, nand_46_out, nand_47_out, nand_48_out, nand_49_out, nand_50_out, nand_51_out,
       nand_52_out, nand_53_out, not_1_out, not_2_out, not_3_out, not_4_out, not_5_out, not_6_out, s_r_ff_1_q;

  nand nand_1 (nand_1_out, B, B);
  nand nand_2 (nand_2_out, mode[2], mode[2]);
  nand nand_3 (nand_3_out, mode[1], mode[1]);
  nand nand_4 (nand_4_out, mode[0], mode[0]);
  nand nand_5 (nand_5_out, s_r_ff_1_q, s_r_ff_1_q);
  nand nand_6 (nand_6_out, B, B);
  nand nand_7 (nand_7_out, mode[2], mode[2]);
  nand nand_8 (nand_8_out, mode[1], mode[1]);
  nand nand_9 (nand_9_out, mode[0], mode[0]);
  nand nand_10 (nand_10_out, s_r_ff_1_q, s_r_ff_1_q);
  nand nand_11 (nand_11_out, mode[4], mode[4]);
  nand nand_12 (nand_12_out, mode[3], mode[3]);
  nand nand_13 (nand_13_out, B, B);
  nand nand_14 (nand_14_out, mode[1], mode[1]);
  nand nand_15 (nand_15_out, mode[0], mode[0]);
  nand nand_16 (nand_16_out, s_r_ff_1_q, s_r_ff_1_q);
  nand nand_17 (nand_17_out, mode[2], mode[2]);
  nand nand_18 (nand_18_out, B, B);
  nand nand_19 (nand_19_out, mode[0], mode[0]);
  nand nand_20 (nand_20_out, s_r_ff_1_q, s_r_ff_1_q);
  nand nand_21 (nand_21_out, mode[1], mode[1]);
  nand nand_22 (nand_22_out, B, B);
  nand nand_23 (nand_23_out, s_r_ff_1_q, s_r_ff_1_q);
  nand nand_24 (nand_24_out, mode[0], mode[0]);
  nand nand_25 (nand_25_out, nand_1_out, mode[4]);
  nand nand_26 (nand_26_out, mode[4], nand_2_out);
  nand nand_27 (nand_27_out, mode[4], nand_3_out);
  nand nand_28 (nand_28_out, mode[4], nand_4_out);
  nand nand_29 (nand_29_out, s_r_ff_1_q, mode[4]);
  nand nand_30 (nand_30_out, B, nand_5_out, mode[3], mode[2], mode[1], mode[0]);
  nand nand_31 (nand_31_out, nand_6_out, mode[3]);
  nand nand_32 (nand_32_out, mode[3], nand_7_out);
  nand nand_33 (nand_33_out, mode[3], nand_8_out);
  nand nand_34 (nand_34_out, mode[3], nand_9_out);
  nand nand_35 (nand_35_out, s_r_ff_1_q, mode[3]);
  nand nand_36 (nand_36_out, B, nand_10_out, nand_11_out, nand_12_out, mode[2], mode[1], mode[0]);
  nand nand_37 (nand_37_out, nand_13_out, mode[2]);
  nand nand_38 (nand_38_out, mode[2], nand_14_out);
  nand nand_39 (nand_39_out, mode[2], nand_15_out);
  nand nand_40 (nand_40_out, s_r_ff_1_q, mode[2]);
  nand nand_41 (nand_41_out, B, nand_16_out, nand_17_out, mode[1], mode[0]);
  nand nand_42 (nand_42_out, nand_18_out, mode[1]);
  nand nand_43 (nand_43_out, mode[1], nand_19_out);
  nand nand_44 (nand_44_out, s_r_ff_1_q, mode[1]);
  nand nand_45 (nand_45_out, B, nand_20_out, nand_21_out, mode[0]);
  nand nand_46 (nand_46_out, nand_22_out, mode[0]);
  nand nand_47 (nand_47_out, s_r_ff_1_q, mode[0]);
  nand nand_48 (nand_48_out, B, nand_23_out, nand_24_out);
  nand nand_49 (nand_49_out, nand_25_out, nand_26_out, nand_27_out, nand_28_out, nand_29_out, nand_30_out);
  nand nand_50 (nand_50_out, nand_31_out, nand_32_out, nand_33_out, nand_34_out, nand_35_out, nand_36_out);
  nand nand_51 (nand_51_out, nand_37_out, nand_38_out, nand_39_out, nand_40_out, nand_41_out);
  nand nand_52 (nand_52_out, nand_42_out, nand_43_out, nand_44_out, nand_45_out);
  nand nand_53 (nand_53_out, nand_46_out, nand_47_out, nand_48_out);
  Multiplexer #(.enable("false")) multiplexer_1 (.in0(B), .in1(1'b0), .out(multiplexer_1_out), .sel(set_on));
  Multiplexer #(.enable("false")) multiplexer_2 (
    .in0(nand_49_out), .in1(set_val[4]), .out(multiplexer_2_out), .sel(set_on));
  Multiplexer #(.enable("false")) multiplexer_3 (
    .in0(nand_50_out), .in1(set_val[3]), .out(multiplexer_3_out), .sel(set_on));
  Multiplexer #(.enable("false")) multiplexer_4 (
    .in0(nand_51_out), .in1(set_val[2]), .out(multiplexer_4_out), .sel(set_on));
  Multiplexer #(.enable("false")) multiplexer_5 (
    .in0(nand_52_out), .in1(set_val[1]), .out(multiplexer_5_out), .sel(set_on));
  Multiplexer #(.enable("false")) multiplexer_6 (
    .in0(nand_53_out), .in1(set_val[0]), .out(multiplexer_6_out), .sel(set_on));
  and and_1 (and_1_out, multiplexer_1_out, ~PoR);  // AND_Gate
  and and_2 (and_2_out, multiplexer_2_out, ~PoR);  // AND_Gate
  and and_3 (and_3_out, multiplexer_3_out, ~PoR);  // AND_Gate
  and and_4 (and_4_out, multiplexer_4_out, ~PoR);  // AND_Gate
  and and_5 (and_5_out, multiplexer_5_out, ~PoR);  // AND_Gate
  and and_6 (and_6_out, multiplexer_6_out, ~PoR);  // AND_Gate
  not not_1 (not_1_out, and_1_out);
  not not_2 (not_2_out, and_2_out);
  not not_3 (not_3_out, and_3_out);
  not not_4 (not_4_out, and_4_out);
  not not_5 (not_5_out, and_5_out);
  not not_6 (not_6_out, and_6_out);
  S_R_Flip_Flop s_r_ff_1 (.S(and_1_out), .R(not_1_out), .clk(Clk), .Q(s_r_ff_1_q), .reset(PoR));  // open: Qn, preset
  S_R_Flip_Flop s_r_ff_2 (.S(and_2_out), .R(not_2_out), .clk(Clk), .Q(mode[4]), .reset(PoR));  // open: Qn, preset
  S_R_Flip_Flop s_r_ff_3 (.S(and_3_out), .R(not_3_out), .clk(Clk), .Q(mode[3]), .reset(PoR));  // open: Qn, preset
  S_R_Flip_Flop s_r_ff_4 (.S(and_4_out), .R(not_4_out), .clk(Clk), .Q(mode[2]), .reset(PoR));  // open: Qn, preset
  S_R_Flip_Flop s_r_ff_5 (.S(and_5_out), .R(not_5_out), .clk(Clk), .Q(mode[1]), .reset(PoR));  // open: Qn, preset
  S_R_Flip_Flop s_r_ff_6 (.S(and_6_out), .R(not_6_out), .clk(Clk), .Q(mode[0]), .reset(PoR));  // open: Qn, preset
endmodule

module n28_modes (
  input  B,
  input  PoR,
  input  Clk,
  output [4:0] mode
);

  wire and_1_out, and_2_out, and_3_out, and_4_out, and_5_out, and_6_out, nand_1_out, nand_2_out, nand_3_out,
       nand_4_out, nand_5_out, nand_6_out, nand_7_out, nand_8_out, nand_9_out, nand_10_out, nand_11_out,
       nand_12_out, nand_13_out, nand_14_out, nand_15_out, nand_16_out, nand_17_out, nand_18_out,
       nand_19_out, nand_20_out, nand_21_out, nand_22_out, nand_23_out, nand_24_out, nand_25_out,
       nand_26_out, nand_27_out, nand_28_out, nand_29_out, nand_30_out, nand_31_out, nand_32_out,
       nand_33_out, nand_34_out, nand_35_out, nand_36_out, nand_37_out, nand_38_out, nand_39_out,
       nand_40_out, nand_41_out, nand_42_out, nand_43_out, nand_44_out, nand_45_out, nand_46_out,
       nand_47_out, nand_48_out, nand_49_out, nand_50_out, nand_51_out, nand_52_out, nand_53_out,
       nand_54_out, nand_55_out, nand_56_out, nand_57_out, nand_58_out, not_1_out, not_2_out, not_3_out,
       not_4_out, not_5_out, not_6_out, s_r_ff_1_q;

  nand nand_1 (nand_1_out, s_r_ff_1_q, s_r_ff_1_q);
  nand nand_2 (nand_2_out, s_r_ff_1_q, s_r_ff_1_q);
  nand nand_3 (nand_3_out, mode[3], mode[3]);
  nand nand_4 (nand_4_out, s_r_ff_1_q, s_r_ff_1_q);
  nand nand_5 (nand_5_out, mode[4], mode[4]);
  nand nand_6 (nand_6_out, mode[2], mode[2]);
  nand nand_7 (nand_7_out, s_r_ff_1_q, s_r_ff_1_q);
  nand nand_8 (nand_8_out, mode[3], mode[3]);
  nand nand_9 (nand_9_out, mode[2], mode[2]);
  nand nand_10 (nand_10_out, s_r_ff_1_q, s_r_ff_1_q);
  nand nand_11 (nand_11_out, mode[1], mode[1]);
  nand nand_12 (nand_12_out, B, B);
  nand nand_13 (nand_13_out, s_r_ff_1_q, s_r_ff_1_q);
  nand nand_14 (nand_14_out, mode[0], mode[0]);
  nand nand_15 (nand_15_out, B, B);
  nand nand_16 (nand_16_out, mode[3], mode[3]);
  nand nand_17 (nand_17_out, mode[1], mode[1]);
  nand nand_18 (nand_18_out, mode[0], mode[0]);
  nand nand_19 (nand_19_out, B, B);
  nand nand_20 (nand_20_out, mode[4], mode[4]);
  nand nand_21 (nand_21_out, mode[2], mode[2]);
  nand nand_22 (nand_22_out, mode[1], mode[1]);
  nand nand_23 (nand_23_out, mode[0], mode[0]);
  nand nand_24 (nand_24_out, B, B);
  nand nand_25 (nand_25_out, mode[1], mode[1]);
  nand nand_26 (nand_26_out, mode[0], mode[0]);
  nand nand_27 (nand_27_out, B, B);
  nand nand_28 (nand_28_out, mode[0], mode[0]);
  nand nand_29 (nand_29_out, nand_12_out, mode[0]);
  nand nand_30 (nand_30_out, s_r_ff_1_q, mode[0]);
  nand nand_31 (nand_31_out, B, nand_13_out, nand_14_out);
  nand nand_32 (nand_32_out, nand_15_out, mode[4]);
  nand nand_33 (nand_33_out, mode[4], nand_16_out);
  nand nand_34 (nand_34_out, mode[4], nand_17_out);
  nand nand_35 (nand_35_out, mode[4], nand_18_out);
  nand nand_36 (nand_36_out, s_r_ff_1_q, mode[4]);
  nand nand_37 (nand_37_out, B, nand_1_out, mode[3], mode[2], mode[1], mode[0]);
  nand nand_38 (nand_38_out, nand_19_out, mode[3]);
  nand nand_39 (nand_39_out, nand_20_out, mode[3], nand_21_out);
  nand nand_40 (nand_40_out, mode[3], nand_22_out);
  nand nand_41 (nand_41_out, mode[3], nand_23_out);
  nand nand_42 (nand_42_out, s_r_ff_1_q, mode[3]);
  nand nand_43 (nand_43_out, B, nand_2_out, nand_3_out, mode[2], mode[1], mode[0]);
  nand nand_44 (nand_44_out, nand_24_out, mode[2]);
  nand nand_45 (nand_45_out, mode[2], nand_25_out);
  nand nand_46 (nand_46_out, mode[2], nand_26_out);
  nand nand_47 (nand_47_out, s_r_ff_1_q, mode[2]);
  nand nand_48 (nand_48_out, B, nand_4_out, nand_5_out, nand_6_out, mode[1], mode[0]);
  nand nand_49 (nand_49_out, B, nand_7_out, nand_8_out, nand_9_out, mode[1], mode[0]);
  nand nand_50 (nand_50_out, nand_27_out, mode[1]);
  nand nand_51 (nand_51_out, mode[1], nand_28_out);
  nand nand_52 (nand_52_out, s_r_ff_1_q, mode[1]);
  nand nand_53 (nand_53_out, B, nand_10_out, nand_11_out, mode[0]);
  nand nand_54 (nand_54_out, nand_29_out, nand_30_out, nand_31_out);
  nand nand_55 (nand_55_out, nand_32_out, nand_33_out, nand_34_out, nand_35_out, nand_36_out, nand_37_out);
  nand nand_56 (nand_56_out, nand_38_out, nand_39_out, nand_40_out, nand_41_out, nand_42_out, nand_43_out);
  nand nand_57 (nand_57_out, nand_44_out, nand_45_out, nand_46_out, nand_47_out, nand_48_out, nand_49_out);
  nand nand_58 (nand_58_out, nand_50_out, nand_51_out, nand_52_out, nand_53_out);
  and and_1 (and_1_out, B, ~PoR);  // AND_Gate
  not not_1 (not_1_out, and_1_out);
  and and_2 (and_2_out, nand_55_out, ~PoR);  // AND_Gate
  not not_2 (not_2_out, and_2_out);
  and and_3 (and_3_out, nand_56_out, ~PoR);  // AND_Gate
  not not_3 (not_3_out, and_3_out);
  and and_4 (and_4_out, nand_57_out, ~PoR);  // AND_Gate
  not not_4 (not_4_out, and_4_out);
  and and_5 (and_5_out, nand_58_out, ~PoR);  // AND_Gate
  not not_5 (not_5_out, and_5_out);
  and and_6 (and_6_out, nand_54_out, ~PoR);  // AND_Gate
  not not_6 (not_6_out, and_6_out);
  S_R_Flip_Flop s_r_ff_1 (.S(and_1_out), .R(not_1_out), .clk(Clk), .Q(s_r_ff_1_q), .reset(PoR));  // open: Qn, preset
  S_R_Flip_Flop s_r_ff_2 (.S(and_2_out), .R(not_2_out), .clk(Clk), .Q(mode[4]), .reset(PoR));  // open: Qn, preset
  S_R_Flip_Flop s_r_ff_3 (.S(and_3_out), .R(not_3_out), .clk(Clk), .Q(mode[3]), .reset(PoR));  // open: Qn, preset
  S_R_Flip_Flop s_r_ff_4 (.S(and_4_out), .R(not_4_out), .clk(Clk), .Q(mode[2]), .reset(PoR));  // open: Qn, preset
  S_R_Flip_Flop s_r_ff_5 (.S(and_5_out), .R(not_5_out), .clk(Clk), .Q(mode[1]), .reset(PoR));  // open: Qn, preset
  S_R_Flip_Flop s_r_ff_6 (.S(and_6_out), .R(not_6_out), .clk(Clk), .Q(mode[0]), .reset(PoR));  // open: Qn, preset
endmodule

module n30_modes (
  input  B,
  input  PoR,
  input  Clk,
  output [4:0] mode
);

  wire and_1_out, and_2_out, and_3_out, and_4_out, and_5_out, and_6_out, nand_1_out, nand_2_out, nand_3_out,
       nand_4_out, nand_5_out, nand_6_out, nand_7_out, nand_8_out, nand_9_out, nand_10_out, nand_11_out,
       nand_12_out, nand_13_out, nand_14_out, nand_15_out, nand_16_out, nand_17_out, nand_18_out,
       nand_19_out, nand_20_out, nand_21_out, nand_22_out, nand_23_out, nand_24_out, nand_25_out,
       nand_26_out, nand_27_out, nand_28_out, nand_29_out, nand_30_out, nand_31_out, nand_32_out,
       nand_33_out, nand_34_out, nand_35_out, nand_36_out, nand_37_out, nand_38_out, nand_39_out,
       nand_40_out, nand_41_out, nand_42_out, nand_43_out, nand_44_out, nand_45_out, nand_46_out,
       nand_47_out, nand_48_out, nand_49_out, nand_50_out, nand_51_out, nand_52_out, nand_53_out,
       nand_54_out, nand_55_out, nand_56_out, nand_57_out, nand_58_out, nand_59_out, nand_60_out,
       nand_61_out, nand_62_out, nand_63_out, nand_64_out, nand_65_out, nand_66_out, not_1_out, not_2_out,
       not_3_out, not_4_out, not_5_out, not_6_out, s_r_ff_1_q;

  nand nand_1 (nand_1_out, B, B);
  nand nand_2 (nand_2_out, mode[3], mode[3]);
  nand nand_3 (nand_3_out, mode[2], mode[2]);
  nand nand_4 (nand_4_out, mode[0], mode[0]);
  nand nand_5 (nand_5_out, s_r_ff_1_q, s_r_ff_1_q);
  nand nand_6 (nand_6_out, B, B);
  nand nand_7 (nand_7_out, mode[4], mode[4]);
  nand nand_8 (nand_8_out, mode[1], mode[1]);
  nand nand_9 (nand_9_out, mode[2], mode[2]);
  nand nand_10 (nand_10_out, mode[0], mode[0]);
  nand nand_11 (nand_11_out, s_r_ff_1_q, s_r_ff_1_q);
  nand nand_12 (nand_12_out, mode[3], mode[3]);
  nand nand_13 (nand_13_out, B, B);
  nand nand_14 (nand_14_out, mode[4], mode[4]);
  nand nand_15 (nand_15_out, mode[1], mode[1]);
  nand nand_16 (nand_16_out, mode[3], mode[3]);
  nand nand_17 (nand_17_out, mode[1], mode[1]);
  nand nand_18 (nand_18_out, mode[0], mode[0]);
  nand nand_19 (nand_19_out, s_r_ff_1_q, s_r_ff_1_q);
  nand nand_20 (nand_20_out, mode[2], mode[2]);
  nand nand_21 (nand_21_out, B, B);
  nand nand_22 (nand_22_out, mode[0], mode[0]);
  nand nand_23 (nand_23_out, s_r_ff_1_q, s_r_ff_1_q);
  nand nand_24 (nand_24_out, mode[4], mode[4]);
  nand nand_25 (nand_25_out, mode[1], mode[1]);
  nand nand_26 (nand_26_out, s_r_ff_1_q, s_r_ff_1_q);
  nand nand_27 (nand_27_out, mode[3], mode[3]);
  nand nand_28 (nand_28_out, mode[1], mode[1]);
  nand nand_29 (nand_29_out, s_r_ff_1_q, s_r_ff_1_q);
  nand nand_30 (nand_30_out, mode[2], mode[2]);
  nand nand_31 (nand_31_out, mode[1], mode[1]);
  nand nand_32 (nand_32_out, B, B);
  nand nand_33 (nand_33_out, s_r_ff_1_q, s_r_ff_1_q);
  nand nand_34 (nand_34_out, mode[0], mode[0]);
  nand nand_35 (nand_35_out, nand_1_out, mode[4]);
  nand nand_36 (nand_36_out, mode[4], nand_2_out);
  nand nand_37 (nand_37_out, mode[4], nand_3_out);
  nand nand_38 (nand_38_out, mode[4], nand_4_out);
  nand nand_39 (nand_39_out, s_r_ff_1_q, mode[4]);
  nand nand_40 (nand_40_out, B, nand_5_out, mode[3], mode[2], mode[1], mode[0]);
  nand nand_41 (nand_41_out, nand_6_out, mode[3]);
  nand nand_42 (nand_42_out, nand_7_out, mode[3], nand_8_out);
  nand nand_43 (nand_43_out, mode[3], nand_9_out);
  nand nand_44 (nand_44_out, mode[3], nand_10_out);
  nand nand_45 (nand_45_out, s_r_ff_1_q, mode[3]);
  nand nand_46 (nand_46_out, B, nand_11_out, nand_12_out, mode[2], mode[1], mode[0]);
  nand nand_47 (nand_47_out, nand_13_out, mode[2]);
  nand nand_48 (nand_48_out, nand_14_out, mode[2], nand_15_out);
  nand nand_49 (nand_49_out, nand_16_out, mode[2], nand_17_out);
  nand nand_50 (nand_50_out, mode[2], nand_18_out);
  nand nand_51 (nand_51_out, s_r_ff_1_q, mode[2]);
  nand nand_52 (nand_52_out, B, nand_19_out, nand_20_out, mode[1], mode[0]);
  nand nand_53 (nand_53_out, nand_21_out, mode[1]);
  nand nand_54 (nand_54_out, mode[1], nand_22_out);
  nand nand_55 (nand_55_out, s_r_ff_1_q, mode[1]);
  nand nand_56 (nand_56_out, B, nand_23_out, nand_24_out, nand_25_out, mode[0]);
  nand nand_57 (nand_57_out, B, nand_26_out, nand_27_out, nand_28_out, mode[0]);
  nand nand_58 (nand_58_out, B, nand_29_out, nand_30_out, nand_31_out, mode[0]);
  nand nand_59 (nand_59_out, nand_32_out, mode[0]);
  nand nand_60 (nand_60_out, s_r_ff_1_q, mode[0]);
  nand nand_61 (nand_61_out, B, nand_33_out, nand_34_out);
  nand nand_62 (nand_62_out, nand_59_out, nand_60_out, nand_61_out);
  nand nand_63 (nand_63_out, nand_35_out, nand_36_out, nand_37_out, nand_38_out, nand_39_out, nand_40_out);
  nand nand_64 (nand_64_out, nand_41_out, nand_42_out, nand_43_out, nand_44_out, nand_45_out, nand_46_out);
  nand nand_65 (nand_65_out, nand_47_out, nand_48_out, nand_49_out, nand_50_out, nand_51_out, nand_52_out);
  nand nand_66 (nand_66_out, nand_53_out, nand_54_out, nand_55_out, nand_56_out, nand_57_out, nand_58_out);
  and and_1 (and_1_out, B, ~PoR);  // AND_Gate
  not not_1 (not_1_out, and_1_out);
  and and_2 (and_2_out, nand_63_out, ~PoR);  // AND_Gate
  not not_2 (not_2_out, and_2_out);
  and and_3 (and_3_out, nand_64_out, ~PoR);  // AND_Gate
  not not_3 (not_3_out, and_3_out);
  and and_4 (and_4_out, nand_65_out, ~PoR);  // AND_Gate
  not not_4 (not_4_out, and_4_out);
  and and_5 (and_5_out, nand_66_out, ~PoR);  // AND_Gate
  not not_5 (not_5_out, and_5_out);
  and and_6 (and_6_out, nand_62_out, ~PoR);  // AND_Gate
  not not_6 (not_6_out, and_6_out);
  S_R_Flip_Flop s_r_ff_1 (.S(and_1_out), .R(not_1_out), .clk(Clk), .Q(s_r_ff_1_q), .reset(PoR));  // open: Qn, preset
  S_R_Flip_Flop s_r_ff_2 (.S(and_2_out), .R(not_2_out), .clk(Clk), .Q(mode[4]), .reset(PoR));  // open: Qn, preset
  S_R_Flip_Flop s_r_ff_3 (.S(and_3_out), .R(not_3_out), .clk(Clk), .Q(mode[3]), .reset(PoR));  // open: Qn, preset
  S_R_Flip_Flop s_r_ff_4 (.S(and_4_out), .R(not_4_out), .clk(Clk), .Q(mode[2]), .reset(PoR));  // open: Qn, preset
  S_R_Flip_Flop s_r_ff_5 (.S(and_5_out), .R(not_5_out), .clk(Clk), .Q(mode[1]), .reset(PoR));  // open: Qn, preset
  S_R_Flip_Flop s_r_ff_6 (.S(and_6_out), .R(not_6_out), .clk(Clk), .Q(mode[0]), .reset(PoR));  // open: Qn, preset
endmodule

module n31_modes (
  input  B,
  input  PoR,
  input  Clk,
  output [4:0] mode
);

  wire and_1_out, and_2_out, and_3_out, and_4_out, and_5_out, and_6_out, nand_1_out, nand_2_out, nand_3_out,
       nand_4_out, nand_5_out, nand_6_out, nand_7_out, nand_8_out, nand_9_out, nand_10_out, nand_11_out,
       nand_12_out, nand_13_out, nand_14_out, nand_15_out, nand_16_out, nand_17_out, nand_18_out,
       nand_19_out, nand_20_out, nand_21_out, nand_22_out, nand_23_out, nand_24_out, nand_25_out,
       nand_26_out, nand_27_out, nand_28_out, nand_29_out, nand_30_out, nand_31_out, nand_32_out,
       nand_33_out, nand_34_out, nand_35_out, nand_36_out, nand_37_out, nand_38_out, nand_39_out,
       nand_40_out, nand_41_out, nand_42_out, nand_43_out, nand_44_out, nand_45_out, nand_46_out,
       nand_47_out, nand_48_out, nand_49_out, nand_50_out, nand_51_out, nand_52_out, nand_53_out,
       nand_54_out, nand_55_out, nand_56_out, nand_57_out, nand_58_out, nand_59_out, nand_60_out,
       nand_61_out, nand_62_out, nand_63_out, nand_64_out, nand_65_out, nand_66_out, nand_67_out,
       nand_68_out, nand_69_out, nand_70_out, nand_71_out, nand_72_out, nand_73_out, nand_74_out,
       nand_75_out, nand_76_out, nand_77_out, not_1_out, not_2_out, not_3_out, not_4_out, not_5_out,
       not_6_out, s_r_ff_1_q;

  nand nand_1 (nand_1_out, s_r_ff_1_q, s_r_ff_1_q);
  nand nand_2 (nand_2_out, s_r_ff_1_q, s_r_ff_1_q);
  nand nand_3 (nand_3_out, mode[3], mode[3]);
  nand nand_4 (nand_4_out, s_r_ff_1_q, s_r_ff_1_q);
  nand nand_5 (nand_5_out, mode[2], mode[2]);
  nand nand_6 (nand_6_out, s_r_ff_1_q, s_r_ff_1_q);
  nand nand_7 (nand_7_out, mode[1], mode[1]);
  nand nand_8 (nand_8_out, s_r_ff_1_q, s_r_ff_1_q);
  nand nand_9 (nand_9_out, mode[4], mode[4]);
  nand nand_10 (nand_10_out, mode[0], mode[0]);
  nand nand_11 (nand_11_out, s_r_ff_1_q, s_r_ff_1_q);
  nand nand_12 (nand_12_out, mode[3], mode[3]);
  nand nand_13 (nand_13_out, mode[0], mode[0]);
  nand nand_14 (nand_14_out, s_r_ff_1_q, s_r_ff_1_q);
  nand nand_15 (nand_15_out, mode[2], mode[2]);
  nand nand_16 (nand_16_out, mode[0], mode[0]);
  nand nand_17 (nand_17_out, s_r_ff_1_q, s_r_ff_1_q);
  nand nand_18 (nand_18_out, mode[1], mode[1]);
  nand nand_19 (nand_19_out, mode[0], mode[0]);
  nand nand_20 (nand_20_out, B, B);
  nand nand_21 (nand_21_out, mode[3], mode[3]);
  nand nand_22 (nand_22_out, mode[2], mode[2]);
  nand nand_23 (nand_23_out, mode[1], mode[1]);
  nand nand_24 (nand_24_out, B, B);
  nand nand_25 (nand_25_out, mode[4], mode[4]);
  nand nand_26 (nand_26_out, mode[0], mode[0]);
  nand nand_27 (nand_27_out, mode[2], mode[2]);
  nand nand_28 (nand_28_out, mode[1], mode[1]);
  nand nand_29 (nand_29_out, B, B);
  nand nand_30 (nand_30_out, mode[4], mode[4]);
  nand nand_31 (nand_31_out, mode[0], mode[0]);
  nand nand_32 (nand_32_out, mode[3], mode[3]);
  nand nand_33 (nand_33_out, mode[0], mode[0]);
  nand nand_34 (nand_34_out, mode[1], mode[1]);
  nand nand_35 (nand_35_out, B, B);
  nand nand_36 (nand_36_out, mode[4], mode[4]);
  nand nand_37 (nand_37_out, mode[0], mode[0]);
  nand nand_38 (nand_38_out, mode[3], mode[3]);
  nand nand_39 (nand_39_out, mode[0], mode[0]);
  nand nand_40 (nand_40_out, mode[2], mode[2]);
  nand nand_41 (nand_41_out, mode[0], mode[0]);
  nand nand_42 (nand_42_out, B, B);
  nand nand_43 (nand_43_out, nand_20_out, mode[4]);
  nand nand_44 (nand_44_out, mode[4], nand_21_out);
  nand nand_45 (nand_45_out, mode[4], nand_22_out);
  nand nand_46 (nand_46_out, mode[4], nand_23_out);
  nand nand_47 (nand_47_out, s_r_ff_1_q, mode[4]);
  nand nand_48 (nand_48_out, B, nand_1_out, mode[3], mode[2], mode[1], mode[0]);
  nand nand_49 (nand_49_out, nand_24_out, mode[3]);
  nand nand_50 (nand_50_out, nand_25_out, mode[3], nand_26_out);
  nand nand_51 (nand_51_out, mode[3], nand_27_out);
  nand nand_52 (nand_52_out, mode[3], nand_28_out);
  nand nand_53 (nand_53_out, s_r_ff_1_q, mode[3]);
  nand nand_54 (nand_54_out, B, nand_2_out, nand_3_out, mode[2], mode[1], mode[0]);
  nand nand_55 (nand_55_out, nand_29_out, mode[2]);
  nand nand_56 (nand_56_out, nand_30_out, mode[2], nand_31_out);
  nand nand_57 (nand_57_out, nand_32_out, mode[2], nand_33_out);
  nand nand_58 (nand_58_out, mode[2], nand_34_out);
  nand nand_59 (nand_59_out, s_r_ff_1_q, mode[2]);
  nand nand_60 (nand_60_out, B, nand_4_out, nand_5_out, mode[1], mode[0]);
  nand nand_61 (nand_61_out, nand_35_out, mode[1]);
  nand nand_62 (nand_62_out, nand_36_out, mode[1], nand_37_out);
  nand nand_63 (nand_63_out, nand_38_out, mode[1], nand_39_out);
  nand nand_64 (nand_64_out, nand_40_out, mode[1], nand_41_out);
  nand nand_65 (nand_65_out, s_r_ff_1_q, mode[1]);
  nand nand_66 (nand_66_out, B, nand_6_out, nand_7_out, mode[0]);
  nand nand_67 (nand_67_out, nand_42_out, mode[0]);
  nand nand_68 (nand_68_out, s_r_ff_1_q, mode[0]);
  nand nand_69 (nand_69_out, B, nand_8_out, nand_9_out, nand_10_out);
  nand nand_70 (nand_70_out, B, nand_11_out, nand_12_out, nand_13_out);
  nand nand_71 (nand_71_out, B, nand_14_out, nand_15_out, nand_16_out);
  nand nand_72 (nand_72_out, B, nand_17_out, nand_18_out, nand_19_out);
  nand nand_73 (nand_73_out, nand_43_out, nand_44_out, nand_45_out, nand_46_out, nand_47_out, nand_48_out);
  nand nand_74 (nand_74_out, nand_49_out, nand_50_out, nand_51_out, nand_52_out, nand_53_out, nand_54_out);
  nand nand_75 (nand_75_out, nand_55_out, nand_56_out, nand_57_out, nand_58_out, nand_59_out, nand_60_out);
  nand nand_76 (nand_76_out, nand_61_out, nand_62_out, nand_63_out, nand_64_out, nand_65_out, nand_66_out);
  nand nand_77 (nand_77_out, nand_67_out, nand_68_out, nand_69_out, nand_70_out, nand_71_out, nand_72_out);
  and and_1 (and_1_out, B, ~PoR);  // AND_Gate
  not not_1 (not_1_out, and_1_out);
  and and_2 (and_2_out, nand_73_out, ~PoR);  // AND_Gate
  not not_2 (not_2_out, and_2_out);
  and and_3 (and_3_out, nand_74_out, ~PoR);  // AND_Gate
  not not_3 (not_3_out, and_3_out);
  and and_4 (and_4_out, nand_75_out, ~PoR);  // AND_Gate
  not not_4 (not_4_out, and_4_out);
  and and_5 (and_5_out, nand_76_out, ~PoR);  // AND_Gate
  not not_5 (not_5_out, and_5_out);
  and and_6 (and_6_out, nand_77_out, ~PoR);  // AND_Gate
  not not_6 (not_6_out, and_6_out);
  S_R_Flip_Flop s_r_ff_1 (.S(and_1_out), .R(not_1_out), .clk(Clk), .Q(s_r_ff_1_q), .reset(PoR));  // open: Qn, preset
  S_R_Flip_Flop s_r_ff_2 (.S(and_2_out), .R(not_2_out), .clk(Clk), .Q(mode[4]), .reset(PoR));  // open: Qn, preset
  S_R_Flip_Flop s_r_ff_3 (.S(and_3_out), .R(not_3_out), .clk(Clk), .Q(mode[3]), .reset(PoR));  // open: Qn, preset
  S_R_Flip_Flop s_r_ff_4 (.S(and_4_out), .R(not_4_out), .clk(Clk), .Q(mode[2]), .reset(PoR));  // open: Qn, preset
  S_R_Flip_Flop s_r_ff_5 (.S(and_5_out), .R(not_5_out), .clk(Clk), .Q(mode[1]), .reset(PoR));  // open: Qn, preset
  S_R_Flip_Flop s_r_ff_6 (.S(and_6_out), .R(not_6_out), .clk(Clk), .Q(mode[0]), .reset(PoR));  // open: Qn, preset
endmodule

module n32_modes (
  input  B,
  input  PoR,
  input  Clk,
  output [4:0] mode
);

  wire and_1_out, and_2_out, and_3_out, and_4_out, and_5_out, and_6_out, nand_1_out, nand_2_out, nand_3_out,
       nand_4_out, nand_5_out, nand_6_out, nand_7_out, nand_8_out, nand_9_out, nand_10_out, nand_11_out,
       nand_12_out, nand_13_out, nand_14_out, nand_15_out, nand_16_out, nand_17_out, nand_18_out,
       nand_19_out, nand_20_out, nand_21_out, nand_22_out, nand_23_out, nand_24_out, nand_25_out,
       nand_26_out, nand_27_out, nand_28_out, nand_29_out, nand_30_out, nand_31_out, nand_32_out,
       nand_33_out, nand_34_out, nand_35_out, nand_36_out, nand_37_out, nand_38_out, nand_39_out,
       nand_40_out, nand_41_out, nand_42_out, nand_43_out, nand_44_out, nand_45_out, nand_46_out,
       nand_47_out, nand_48_out, nand_49_out, nand_50_out, nand_51_out, nand_52_out, nand_53_out,
       nand_54_out, nand_55_out, not_1_out, not_2_out, not_3_out, not_4_out, not_5_out, not_6_out, s_r_ff_1_q;

  nand nand_1 (nand_1_out, s_r_ff_1_q, s_r_ff_1_q);
  nand nand_2 (nand_2_out, mode[4], mode[4]);
  nand nand_3 (nand_3_out, s_r_ff_1_q, s_r_ff_1_q);
  nand nand_4 (nand_4_out, mode[3], mode[3]);
  nand nand_5 (nand_5_out, s_r_ff_1_q, s_r_ff_1_q);
  nand nand_6 (nand_6_out, mode[2], mode[2]);
  nand nand_7 (nand_7_out, s_r_ff_1_q, s_r_ff_1_q);
  nand nand_8 (nand_8_out, mode[1], mode[1]);
  nand nand_9 (nand_9_out, B, B);
  nand nand_10 (nand_10_out, s_r_ff_1_q, s_r_ff_1_q);
  nand nand_11 (nand_11_out, mode[0], mode[0]);
  nand nand_12 (nand_12_out, B, B);
  nand nand_13 (nand_13_out, mode[3], mode[3]);
  nand nand_14 (nand_14_out, mode[2], mode[2]);
  nand nand_15 (nand_15_out, mode[1], mode[1]);
  nand nand_16 (nand_16_out, mode[0], mode[0]);
  nand nand_17 (nand_17_out, B, B);
  nand nand_18 (nand_18_out, mode[2], mode[2]);
  nand nand_19 (nand_19_out, mode[1], mode[1]);
  nand nand_20 (nand_20_out, mode[0], mode[0]);
  nand nand_21 (nand_21_out, B, B);
  nand nand_22 (nand_22_out, mode[1], mode[1]);
  nand nand_23 (nand_23_out, mode[0], mode[0]);
  nand nand_24 (nand_24_out, B, B);
  nand nand_25 (nand_25_out, mode[0], mode[0]);
  nand nand_26 (nand_26_out, nand_9_out, mode[0]);
  nand nand_27 (nand_27_out, s_r_ff_1_q, mode[0]);
  nand nand_28 (nand_28_out, B, nand_10_out, nand_11_out);
  nand nand_29 (nand_29_out, nand_12_out, mode[4]);
  nand nand_30 (nand_30_out, mode[4], nand_13_out);
  nand nand_31 (nand_31_out, mode[4], nand_14_out);
  nand nand_32 (nand_32_out, mode[4], nand_15_out);
  nand nand_33 (nand_33_out, mode[4], nand_16_out);
  nand nand_34 (nand_34_out, s_r_ff_1_q, mode[4]);
  nand nand_35 (nand_35_out, B, nand_1_out, nand_2_out, mode[3], mode[2], mode[1], mode[0]);
  nand nand_36 (nand_36_out, nand_17_out, mode[3]);
  nand nand_37 (nand_37_out, mode[3], nand_18_out);
  nand nand_38 (nand_38_out, mode[3], nand_19_out);
  nand nand_39 (nand_39_out, mode[3], nand_20_out);
  nand nand_40 (nand_40_out, s_r_ff_1_q, mode[3]);
  nand nand_41 (nand_41_out, B, nand_3_out, nand_4_out, mode[2], mode[1], mode[0]);
  nand nand_42 (nand_42_out, nand_21_out, mode[2]);
  nand nand_43 (nand_43_out, mode[2], nand_22_out);
  nand nand_44 (nand_44_out, mode[2], nand_23_out);
  nand nand_45 (nand_45_out, s_r_ff_1_q, mode[2]);
  nand nand_46 (nand_46_out, B, nand_5_out, nand_6_out, mode[1], mode[0]);
  nand nand_47 (nand_47_out, nand_24_out, mode[1]);
  nand nand_48 (nand_48_out, mode[1], nand_25_out);
  nand nand_49 (nand_49_out, s_r_ff_1_q, mode[1]);
  nand nand_50 (nand_50_out, B, nand_7_out, nand_8_out, mode[0]);
  nand nand_51 (nand_51_out, nand_26_out, nand_27_out, nand_28_out);
  nand nand_52 (nand_52_out, nand_29_out, nand_30_out, nand_31_out, nand_32_out, nand_33_out, nand_34_out, nand_35_out);
  nand nand_53 (nand_53_out, nand_36_out, nand_37_out, nand_38_out, nand_39_out, nand_40_out, nand_41_out);
  nand nand_54 (nand_54_out, nand_42_out, nand_43_out, nand_44_out, nand_45_out, nand_46_out);
  nand nand_55 (nand_55_out, nand_47_out, nand_48_out, nand_49_out, nand_50_out);
  and and_1 (and_1_out, B, ~PoR);  // AND_Gate
  and and_2 (and_2_out, nand_52_out, ~PoR);  // AND_Gate
  and and_3 (and_3_out, nand_53_out, ~PoR);  // AND_Gate
  and and_4 (and_4_out, nand_54_out, ~PoR);  // AND_Gate
  and and_5 (and_5_out, nand_55_out, ~PoR);  // AND_Gate
  and and_6 (and_6_out, nand_51_out, ~PoR);  // AND_Gate
  S_R_Flip_Flop s_r_ff_1 (.S(and_1_out), .R(not_1_out), .clk(Clk), .Q(s_r_ff_1_q), .reset(PoR));  // open: Qn, preset
  not not_1 (not_1_out, and_1_out);
  S_R_Flip_Flop s_r_ff_2 (.S(and_2_out), .R(not_2_out), .clk(Clk), .Q(mode[4]), .reset(PoR));  // open: Qn, preset
  not not_2 (not_2_out, and_2_out);
  S_R_Flip_Flop s_r_ff_3 (.S(and_3_out), .R(not_3_out), .clk(Clk), .Q(mode[3]), .reset(PoR));  // open: Qn, preset
  not not_3 (not_3_out, and_3_out);
  S_R_Flip_Flop s_r_ff_4 (.S(and_4_out), .R(not_4_out), .clk(Clk), .Q(mode[2]), .reset(PoR));  // open: Qn, preset
  not not_4 (not_4_out, and_4_out);
  S_R_Flip_Flop s_r_ff_5 (.S(and_5_out), .R(not_5_out), .clk(Clk), .Q(mode[1]), .reset(PoR));  // open: Qn, preset
  not not_5 (not_5_out, and_5_out);
  S_R_Flip_Flop s_r_ff_6 (.S(and_6_out), .R(not_6_out), .clk(Clk), .Q(mode[0]), .reset(PoR));  // open: Qn, preset
  not not_6 (not_6_out, and_6_out);
endmodule
