// Logisim project MUSIC_FINAL2.circ as structural Verilog: 20 circuits, main circuit MUSIC
module MUSIC (
  input  ALARM,
  input  [1:0] B1_B0,
  input  RESET,
  input  CLK32k,
  output Buzzer1,
  output [7:0] L1,
  output [7:0] L2,
  output [7:0] L3,
  output [7:0] L4,
  output [7:0] L5,
  output [7:0] L6
);

  wire d_ff_1_q, d_ff_1_qn, d_ff_2_qn, MusicBox_1_reset, not_1_out, NoteControl_1_outnote, or_1_out,
       or_2_out, or_3_out;
  wire [2:0] counter_1_q;
  wire [7:0] BeatManager_1_beat, FreqToNote_1_note;
  wire [12:0] MusicBox_1_melody;

  D_Flip_Flop d_ff_1 (.D(d_ff_1_qn), .clk(B1_B0[1]), .Q(d_ff_1_q), .Qn(d_ff_1_qn), .reset(RESET));  // open: preset
  or or_1 (or_1_out, ALARM, d_ff_1_q);
  or or_2 (or_2_out, RESET, B1_B0[0], MusicBox_1_reset);
  Counter #(.width(3), .max('h7)) counter_1 (
    .clr(RESET), .count(B1_B0[0]), .clk(CLK32k), .Q(counter_1_q));  // open: load, up, D, carry
  BeatManager BeatManager_1 (.start(or_1_out), .clk(CLK32k), .reset(or_2_out), .beat(BeatManager_1_beat));
  FreqToNote FreqToNote_1 (.reset(NoteControl_1_outnote), .clk(CLK32k), .note(FreqToNote_1_note));
  MusicBox MusicBox_1 (
    .beat(BeatManager_1_beat), .songcode(counter_1_q), .melody(MusicBox_1_melody), .reset(MusicBox_1_reset));
  D_Flip_Flop d_ff_2 (
    .D(d_ff_2_qn), .clk(NoteControl_1_outnote), .Q(Buzzer1), .Qn(d_ff_2_qn), .reset(or_3_out));  // open: preset
  NoteControl NoteControl_1 (
    .frequency(FreqToNote_1_note), .noteCode(MusicBox_1_melody), .outNote(NoteControl_1_outnote));
  SongName SongName_1 (.songcode(counter_1_q), .L1(L1), .L2(L2), .L3(L3), .L4(L4), .L5(L5), .L6(L6));
  or or_3 (or_3_out, RESET, not_1_out);
  not not_1 (not_1_out, or_1_out);
endmodule

module MusicBox (
  input  [7:0] beat,
  input  [2:0] songcode,
  output [12:0] melody,
  output reset
);

  wire AnotherBrickInTheWall_1_reset, ImperialMarch_1_reset, Kalinka_1_reset, MissYou_1_reset,
       PirateCaraibe_1_output_1, RappersDelight_1_reset, ThisMustBeThePlace_1_reset;
  wire [6:2] ThisMustBeThePlace_1_a1;
  wire [7:0] demultiplexer_1_out1, demultiplexer_1_out2, demultiplexer_1_out3, demultiplexer_1_out4,
       demultiplexer_1_out5, demultiplexer_1_out6, demultiplexer_1_out7;
  wire [8:0] RappersDelight_1_c3;
  wire [8:4] MissYou_1_e2;
  wire [10:5] AnotherBrickInTheWall_1_d2;
  wire [12:0] Kalinka_1_output_bus_1, PirateCaraibe_1_output_bus_1;
  wire [12:4] ImperialMarch_1_e2;

  Demultiplexer #(.select(3), .width(8), .enable("false")) demultiplexer_1 (
    .out1(demultiplexer_1_out1), .out2(demultiplexer_1_out2), .out3(demultiplexer_1_out3),
    .out4(demultiplexer_1_out4), .out5(demultiplexer_1_out5), .out6(demultiplexer_1_out6),
    .out7(demultiplexer_1_out7), .in(beat), .sel(songcode));  // open: out0
  ImperialMarch ImperialMarch_1 (
    .Input_1(demultiplexer_1_out1[7]), .Input_2(demultiplexer_1_out1[6]), .Input_3(demultiplexer_1_out1[5]),
    .Input_4(demultiplexer_1_out1[4]), .Input_5(demultiplexer_1_out1[3]), .Input_6(demultiplexer_1_out1[2]),
    .Input_7(demultiplexer_1_out1[1]), .Input_8(demultiplexer_1_out1[0]), .e2(ImperialMarch_1_e2[4]),
    .d2(ImperialMarch_1_e2[5]), .g1(ImperialMarch_1_e2[9]), .e1(ImperialMarch_1_e2[10]),
    .c1(ImperialMarch_1_e2[12]), .reset(ImperialMarch_1_reset));
  Kalinka Kalinka_1 (
    .Input_1(demultiplexer_1_out2[7]), .Input_2(demultiplexer_1_out2[6]), .Input_3(demultiplexer_1_out2[5]),
    .Input_4(demultiplexer_1_out2[4]), .Input_5(demultiplexer_1_out2[3]), .Input_6(demultiplexer_1_out2[2]),
    .Input_7(demultiplexer_1_out2[1]), .Input_8(demultiplexer_1_out2[0]),
    .Output_bus_1(Kalinka_1_output_bus_1), .reset(Kalinka_1_reset));
  PirateCaraibe PirateCaraibe_1 (
    .Input_1(demultiplexer_1_out3[7]), .Input_2(demultiplexer_1_out3[6]), .Input_3(demultiplexer_1_out3[5]),
    .Input_4(demultiplexer_1_out3[4]), .Input_5(demultiplexer_1_out3[3]), .Input_6(demultiplexer_1_out3[2]),
    .Input_7(demultiplexer_1_out3[1]), .Input_8(demultiplexer_1_out3[0]),
    .Output_bus_1(PirateCaraibe_1_output_bus_1), .Output_1(PirateCaraibe_1_output_1));
  ThisMustBeThePlace ThisMustBeThePlace_1 (
    .Input_1(demultiplexer_1_out4[7]), .Input_2(demultiplexer_1_out4[6]), .Input_3(demultiplexer_1_out4[5]),
    .Input_4(demultiplexer_1_out4[4]), .Input_5(demultiplexer_1_out4[3]), .Input_6(demultiplexer_1_out4[2]),
    .Input_7(demultiplexer_1_out4[1]), .Input_8(demultiplexer_1_out4[0]), .A1(ThisMustBeThePlace_1_a1[2]),
    .G1(ThisMustBeThePlace_1_a1[3]), .E1(ThisMustBeThePlace_1_a1[4]), .D1(ThisMustBeThePlace_1_a1[5]),
    .C1(ThisMustBeThePlace_1_a1[6]), .reset(ThisMustBeThePlace_1_reset));
  MissYou MissYou_1 (
    .Input_1(demultiplexer_1_out5[7]), .Input_2(demultiplexer_1_out5[6]), .Input_3(demultiplexer_1_out5[5]),
    .Input_4(demultiplexer_1_out5[4]), .Input_5(demultiplexer_1_out5[3]), .Input_6(demultiplexer_1_out5[2]),
    .Input_7(demultiplexer_1_out5[1]), .Input_8(demultiplexer_1_out5[0]), .E2(MissYou_1_e2[4]),
    .D2(MissYou_1_e2[5]), .B1(MissYou_1_e2[7]), .A1(MissYou_1_e2[8]), .reset(MissYou_1_reset));
  AnotherBrickInTheWall AnotherBrickInTheWall_1 (
    .Input_1(demultiplexer_1_out6[7]), .Input_2(demultiplexer_1_out6[6]), .Input_3(demultiplexer_1_out6[5]),
    .Input_4(demultiplexer_1_out6[4]), .Input_5(demultiplexer_1_out6[3]), .Input_6(demultiplexer_1_out6[2]),
    .Input_7(demultiplexer_1_out6[1]), .Input_8(demultiplexer_1_out6[0]), .d2(AnotherBrickInTheWall_1_d2[5]),
    .c2(AnotherBrickInTheWall_1_d2[6]), .a1(AnotherBrickInTheWall_1_d2[8]),
    .e1(AnotherBrickInTheWall_1_d2[10]), .reset(AnotherBrickInTheWall_1_reset));
  RappersDelight RappersDelight_1 (
    .Input_1(demultiplexer_1_out7[7]), .Input_2(demultiplexer_1_out7[6]), .Input_3(demultiplexer_1_out7[5]),
    .Input_4(demultiplexer_1_out7[4]), .Input_5(demultiplexer_1_out7[3]), .Input_6(demultiplexer_1_out7[2]),
    .Input_7(demultiplexer_1_out7[1]), .Input_8(demultiplexer_1_out7[0]), .c3(RappersDelight_1_c3[0]),
    .b2(RappersDelight_1_c3[1]), .a2(RappersDelight_1_c3[2]), .g2(RappersDelight_1_c3[3]),
    .e2(RappersDelight_1_c3[4]), .d2(RappersDelight_1_c3[5]), .c2(RappersDelight_1_c3[6]),
    .b1(RappersDelight_1_c3[7]), .a1(RappersDelight_1_c3[8]), .reset(RappersDelight_1_reset));
  Multiplexer #(.select(3), .width(13), .enable("false")) multiplexer_1 (
    .in0({13{1'b0}}),
    .in1({ImperialMarch_1_e2[12], 1'b0, ImperialMarch_1_e2[10:9], 3'b000, ImperialMarch_1_e2[5:4], 4'b0000}),
    .in2(Kalinka_1_output_bus_1), .in3(PirateCaraibe_1_output_bus_1),
    .in4({{6{1'b0}}, ThisMustBeThePlace_1_a1, 2'b00}),
    .in5({4'b0000, MissYou_1_e2[8:7], 1'b0, MissYou_1_e2[5:4], 4'b0000}),
    .in6({2'b00, AnotherBrickInTheWall_1_d2[10], 1'b0, AnotherBrickInTheWall_1_d2[8], 1'b0, AnotherBrickInTheWall_1_d2[6:5], {5{1'b0}}}),
    .in7({4'b0000, RappersDelight_1_c3}), .out(melody), .sel(songcode));
  or or_1 (reset, ImperialMarch_1_reset, Kalinka_1_reset, PirateCaraibe_1_output_1, ThisMustBeThePlace_1_reset, MissYou_1_reset, AnotherBrickInTheWall_1_reset, RappersDelight_1_reset);
endmodule

module FreqToNote (
  input  reset,
  input  clk,
  output [7:0] note
);

  wire [5:0] counter_1_q;

  Counter #(.width(6), .max('h3c)) counter_1 (
    .clr(reset), .count(1'b1), .clk(clk), .Q(counter_1_q));  // open: load, up, D, carry
  assign note = {{2{1'b0}}, counter_1_q};  // Bit_Extender bit_extender_1
endmodule

module NoteControl (
  input  [7:0] frequency,
  input  [12:0] noteCode,
  output outNote
);

  wire and_1_out, and_2_out, and_3_out, and_4_out, and_5_out, and_6_out, and_7_out, and_8_out, and_9_out,
       and_10_out, and_11_out, and_12_out, and_13_out;
  wire [5:0] bit_extender_1_out;

  Bit_Extender #(.out_width(6), .\type ("zero")) bit_extender_1 (.in(frequency), .out(bit_extender_1_out));
  and and_1 (and_1_out, bit_extender_1_out[0], bit_extender_1_out[1], bit_extender_1_out[2], bit_extender_1_out[3], ~bit_extender_1_out[4], ~bit_extender_1_out[5], noteCode[0]);  // AND_Gate
  and and_2 (and_2_out, ~bit_extender_1_out[0], ~bit_extender_1_out[1], ~bit_extender_1_out[2], ~bit_extender_1_out[3], bit_extender_1_out[4], ~bit_extender_1_out[5], noteCode[1]);  // AND_Gate
  and and_3 (and_3_out, ~bit_extender_1_out[0], bit_extender_1_out[1], ~bit_extender_1_out[2], ~bit_extender_1_out[3], bit_extender_1_out[4], ~bit_extender_1_out[5], noteCode[2]);  // AND_Gate
  and and_4 (and_4_out, ~bit_extender_1_out[0], ~bit_extender_1_out[1], bit_extender_1_out[2], ~bit_extender_1_out[3], bit_extender_1_out[4], ~bit_extender_1_out[5], noteCode[3]);  // AND_Gate
  and and_5 (and_5_out, ~bit_extender_1_out[0], ~bit_extender_1_out[1], ~bit_extender_1_out[2], bit_extender_1_out[3], bit_extender_1_out[4], ~bit_extender_1_out[5], noteCode[4]);  // AND_Gate
  and and_6 (and_6_out, bit_extender_1_out[0], bit_extender_1_out[1], ~bit_extender_1_out[2], bit_extender_1_out[3], bit_extender_1_out[4], ~bit_extender_1_out[5], noteCode[5]);  // AND_Gate
  and and_7 (and_7_out, ~bit_extender_1_out[0], bit_extender_1_out[1], bit_extender_1_out[2], bit_extender_1_out[3], bit_extender_1_out[4], ~bit_extender_1_out[5], noteCode[6]);  // AND_Gate
  and and_8 (and_8_out, ~bit_extender_1_out[0], ~bit_extender_1_out[1], ~bit_extender_1_out[2], ~bit_extender_1_out[3], ~bit_extender_1_out[4], bit_extender_1_out[5], noteCode[7]);  // AND_Gate
  and and_9 (and_9_out, ~bit_extender_1_out[0], ~bit_extender_1_out[1], bit_extender_1_out[2], ~bit_extender_1_out[3], ~bit_extender_1_out[4], bit_extender_1_out[5], noteCode[8]);  // AND_Gate
  and and_10 (and_10_out, ~bit_extender_1_out[0], ~bit_extender_1_out[1], ~bit_extender_1_out[2], bit_extender_1_out[3], ~bit_extender_1_out[4], bit_extender_1_out[5], noteCode[9]);  // AND_Gate
  and and_11 (and_11_out, ~bit_extender_1_out[0], ~bit_extender_1_out[1], ~bit_extender_1_out[2], ~bit_extender_1_out[3], bit_extender_1_out[4], bit_extender_1_out[5], noteCode[10]);  // AND_Gate
  and and_12 (and_12_out, ~bit_extender_1_out[0], bit_extender_1_out[1], bit_extender_1_out[2], ~bit_extender_1_out[3], bit_extender_1_out[4], bit_extender_1_out[5], noteCode[11]);  // AND_Gate
  and and_13 (and_13_out, ~bit_extender_1_out[0], ~bit_extender_1_out[1], bit_extender_1_out[2], bit_extender_1_out[3], bit_extender_1_out[4], bit_extender_1_out[5], noteCode[12]);  // AND_Gate
  or or_1 (outNote, and_1_out, and_2_out, and_3_out, and_4_out, and_5_out, and_6_out, and_7_out, and_8_out, and_9_out, and_10_out, and_11_out, and_12_out, and_13_out);
endmodule

module BeatManager (
  input  start,
  input  clk,
  input  reset,
  output [7:0] beat
);

  wire Double_croche_150ms_carry, Mesure_1_o0, Mesure_1_o1, Mesure_1_o2, Mesure_1_o3, Mesure_1_o4,
       Mesure_1_o5, Mesure_1_o6, Mesure_1_o7;
  wire [11:0] Double_croche_150ms_q;

  Counter #(.width(12), .max('h9c4)) Double_croche_150ms (
    .clr(reset), .count(start), .clk(clk), .carry(Double_croche_150ms_carry), .Q(Double_croche_150ms_q));  // open: load, up, D
  Mesure Mesure_1 (
    .CarryIn(Double_croche_150ms_carry), .b7(beat[7]), .b6(beat[6]), .b5(beat[5]), .b4(beat[4]),
    .b3(beat[3]), .b2(beat[2]), .b1(beat[1]), .b0(beat[0]), .o7(Mesure_1_o7), .o6(Mesure_1_o6),
    .o5(Mesure_1_o5), .o4(Mesure_1_o4), .o3(Mesure_1_o3), .o2(Mesure_1_o2), .o1(Mesure_1_o1), .o0(Mesure_1_o0));
  D_Flip_Flop d_ff_1 (.D(Mesure_1_o7), .clk(clk), .Q(beat[7]), .reset(reset));  // open: Qn, preset
  D_Flip_Flop d_ff_2 (.D(Mesure_1_o6), .clk(clk), .Q(beat[6]), .reset(reset));  // open: Qn, preset
  D_Flip_Flop d_ff_3 (.D(Mesure_1_o5), .clk(clk), .Q(beat[5]), .reset(reset));  // open: Qn, preset
  D_Flip_Flop d_ff_4 (.D(Mesure_1_o4), .clk(clk), .Q(beat[4]), .reset(reset));  // open: Qn, preset
  D_Flip_Flop d_ff_5 (.D(Mesure_1_o3), .clk(clk), .Q(beat[3]), .reset(reset));  // open: Qn, preset
  D_Flip_Flop d_ff_6 (.D(Mesure_1_o2), .clk(clk), .Q(beat[2]), .reset(reset));  // open: Qn, preset
  D_Flip_Flop d_ff_7 (.D(Mesure_1_o1), .clk(clk), .Q(beat[1]), .reset(reset));  // open: Qn, preset
  D_Flip_Flop d_ff_8 (.D(Mesure_1_o0), .clk(clk), .Q(beat[0]), .reset(reset));  // open: Qn, preset
endmodule

module Mesure (
  input  CarryIn,
  input  b7,
  input  b6,
  input  b5,
  input  b4,
  input  b3,
  input  b2,
  input  b1,
  input  b0,
  output o7,
  output o6,
  output o5,
  output o4,
  output o3,
  output o2,
  output o1,
  output o0
);

  wire and_1_out, and_2_out, and_3_out, and_4_out, and_5_out, and_6_out, and_7_out, and_8_out, and_9_out,
       and_10_out, and_11_out, and_12_out, and_13_out, and_14_out, and_15_out, and_16_out, and_17_out,
       and_18_out, and_19_out, and_20_out, and_21_out, and_22_out, and_23_out, and_24_out, and_25_out,
       and_26_out, and_27_out, and_28_out, and_29_out, and_30_out, and_31_out, and_32_out, and_33_out,
       and_34_out, and_35_out, and_36_out, and_37_out, and_38_out, and_39_out, and_40_out, and_41_out,
       and_42_out, and_43_out, and_44_out, not_1_out, not_2_out, not_3_out, not_4_out, not_5_out, not_6_out,
       not_7_out, not_8_out, not_9_out, not_10_out, not_11_out, not_12_out, not_13_out, not_14_out,
       not_15_out, not_16_out, not_17_out, not_18_out, not_19_out, not_20_out, not_21_out, not_22_out,
       not_23_out, not_24_out, not_25_out, not_26_out, not_27_out, not_28_out, not_29_out, not_30_out,
       not_31_out, not_32_out, not_33_out, not_34_out, not_35_out, not_36_out, not_37_out, not_38_out,
       not_39_out, not_40_out, not_41_out, not_42_out, not_43_out, not_44_out;

  not not_1 (not_1_out, CarryIn);
  not not_2 (not_2_out, b6);
  not not_3 (not_3_out, b5);
  not not_4 (not_4_out, b4);
  not not_5 (not_5_out, b3);
  not not_6 (not_6_out, b2);
  not not_7 (not_7_out, b1);
  not not_8 (not_8_out, b0);
  not not_9 (not_9_out, b7);
  not not_10 (not_10_out, CarryIn);
  not not_11 (not_11_out, b5);
  not not_12 (not_12_out, b4);
  not not_13 (not_13_out, b3);
  not not_14 (not_14_out, b2);
  not not_15 (not_15_out, b1);
  not not_16 (not_16_out, b0);
  not not_17 (not_17_out, b6);
  not not_18 (not_18_out, CarryIn);
  not not_19 (not_19_out, b4);
  not not_20 (not_20_out, b3);
  not not_21 (not_21_out, b2);
  not not_22 (not_22_out, b1);
  not not_23 (not_23_out, b0);
  not not_24 (not_24_out, b5);
  not not_25 (not_25_out, CarryIn);
  not not_26 (not_26_out, b3);
  not not_27 (not_27_out, b2);
  not not_28 (not_28_out, b1);
  not not_29 (not_29_out, b0);
  not not_30 (not_30_out, b4);
  not not_31 (not_31_out, CarryIn);
  not not_32 (not_32_out, b2);
  not not_33 (not_33_out, b1);
  not not_34 (not_34_out, b0);
  not not_35 (not_35_out, b3);
  not not_36 (not_36_out, CarryIn);
  not not_37 (not_37_out, b1);
  not not_38 (not_38_out, b0);
  not not_39 (not_39_out, b2);
  not not_40 (not_40_out, CarryIn);
  not not_41 (not_41_out, b0);
  not not_42 (not_42_out, b1);
  not not_43 (not_43_out, CarryIn);
  not not_44 (not_44_out, b0);
  and and_1 (and_1_out, not_1_out, b7);
  and and_2 (and_2_out, b7, not_2_out);
  and and_3 (and_3_out, b7, not_3_out);
  and and_4 (and_4_out, b7, not_4_out);
  and and_5 (and_5_out, b7, not_5_out);
  and and_6 (and_6_out, b7, not_6_out);
  and and_7 (and_7_out, b7, not_7_out);
  and and_8 (and_8_out, b7, not_8_out);
  and and_9 (and_9_out, CarryIn, not_9_out, b6, b5, b4, b3, b2, b1, b0);
  and and_10 (and_10_out, not_10_out, b6);
  and and_11 (and_11_out, b6, not_11_out);
  and and_12 (and_12_out, b6, not_12_out);
  and and_13 (and_13_out, b6, not_13_out);
  and and_14 (and_14_out, b6, not_14_out);
  and and_15 (and_15_out, b6, not_15_out);
  and and_16 (and_16_out, b6, not_16_out);
  and and_17 (and_17_out, CarryIn, not_17_out, b5, b4, b3, b2, b1, b0);
  and and_18 (and_18_out, not_18_out, b5);
  and and_19 (and_19_out, b5, not_19_out);
  and and_20 (and_20_out, b5, not_20_out);
  and and_21 (and_21_out, b5, not_21_out);
  and and_22 (and_22_out, b5, not_22_out);
  and and_23 (and_23_out, b5, not_23_out);
  and and_24 (and_24_out, CarryIn, not_24_out, b4, b3, b2, b1, b0);
  and and_25 (and_25_out, not_25_out, b4);
  and and_26 (and_26_out, b4, not_26_out);
  and and_27 (and_27_out, b4, not_27_out);
  and and_28 (and_28_out, b4, not_28_out);
  and and_29 (and_29_out, b4, not_29_out);
  and and_30 (and_30_out, CarryIn, not_30_out, b3, b2, b1, b0);
  and and_31 (and_31_out, not_31_out, b3);
  and and_32 (and_32_out, b3, not_32_out);
  and and_33 (and_33_out, b3, not_33_out);
  and and_34 (and_34_out, b3, not_34_out);
  and and_35 (and_35_out, CarryIn, not_35_out, b2, b1, b0);
  and and_36 (and_36_out, not_36_out, b2);
  and and_37 (and_37_out, b2, not_37_out);
  and and_38 (and_38_out, b2, not_38_out);
  and and_39 (and_39_out, CarryIn, not_39_out, b1, b0);
  and and_40 (and_40_out, not_40_out, b1);
  and and_41 (and_41_out, b1, not_41_out);
  and and_42 (and_42_out, CarryIn, not_42_out, b0);
  and and_43 (and_43_out, not_43_out, b0);
  and and_44 (and_44_out, CarryIn, not_44_out);
  or or_1 (o7, and_1_out, and_2_out, and_3_out, and_4_out, and_5_out, and_6_out, and_7_out, and_8_out, and_9_out);
  or or_2 (o6, and_10_out, and_11_out, and_12_out, and_13_out, and_14_out, and_15_out, and_16_out, and_17_out);
  or or_3 (o5, and_18_out, and_19_out, and_20_out, and_21_out, and_22_out, and_23_out, and_24_out);
  or or_4 (o4, and_25_out, and_26_out, and_27_out, and_28_out, and_29_out, and_30_out);
  or or_5 (o3, and_31_out, and_32_out, and_33_out, and_34_out, and_35_out);
  or or_6 (o2, and_36_out, and_37_out, and_38_out, and_39_out);
  or or_7 (o1, and_40_out, and_41_out, and_42_out);
  or or_8 (o0, and_43_out, and_44_out);
endmodule

module ImperialMarch (
  input  Input_1,
  input  Input_2,
  input  Input_3,
  input  Input_4,
  input  Input_5,
  input  Input_6,
  input  Input_7,
  input  Input_8,
  output e2,
  output d2,
  output g1,
  output e1,
  output c1,
  output reset
);

  wire and_1_out, and_2_out, and_3_out, and_4_out, and_5_out, and_6_out, and_7_out, and_8_out, and_9_out,
       and_10_out, and_11_out, and_12_out, and_13_out, and_14_out, and_15_out, and_16_out, and_17_out,
       and_18_out, and_19_out, and_20_out, and_21_out, and_22_out, and_23_out, and_24_out, and_25_out,
       and_26_out, and_27_out, and_28_out, and_29_out, and_30_out, and_31_out, and_32_out, and_33_out,
       and_34_out, and_35_out, and_36_out, and_37_out, and_38_out, and_39_out, and_40_out, and_41_out,
       not_1_out, not_2_out, not_3_out, not_4_out, not_5_out, not_6_out, not_7_out, not_8_out, not_9_out,
       not_10_out, not_11_out, not_12_out, not_13_out, not_14_out, not_15_out, not_16_out, not_17_out,
       not_18_out, not_19_out, not_20_out, not_21_out, not_22_out, not_23_out, not_24_out, not_25_out,
       not_26_out, not_27_out, not_28_out, not_29_out, not_30_out, not_31_out, not_32_out, not_33_out,
       not_34_out, not_35_out, not_36_out, not_37_out, not_38_out, not_39_out, not_40_out, not_41_out,
       not_42_out, not_43_out, not_44_out, not_45_out, not_46_out, not_47_out, not_48_out, not_49_out,
       not_50_out, not_51_out, not_52_out, not_53_out, not_54_out, not_55_out, not_56_out, not_57_out,
       not_58_out, not_59_out, not_60_out, not_61_out, not_62_out, not_63_out, not_64_out, not_65_out,
       not_66_out, not_67_out, not_68_out, not_69_out, not_70_out, not_71_out, not_72_out, not_73_out,
       not_74_out, not_75_out, not_76_out, not_77_out, not_78_out, not_79_out, not_80_out, not_81_out,
       not_82_out, not_83_out, not_84_out, not_85_out, not_86_out, not_87_out, not_88_out, not_89_out,
       not_90_out, not_91_out, not_92_out, not_93_out, not_94_out, not_95_out, not_96_out, not_97_out,
       not_98_out, not_99_out, not_100_out, not_101_out, not_102_out, not_103_out, not_104_out, not_105_out,
       not_106_out, not_107_out, not_108_out, not_109_out, not_110_out, not_111_out, not_112_out,
       not_113_out, not_114_out, not_115_out, not_116_out, not_117_out, not_118_out, not_119_out,
       not_120_out, not_121_out, not_122_out, not_123_out, not_124_out, not_125_out, not_126_out,
       not_127_out, not_128_out, not_129_out, not_130_out, not_131_out, not_132_out, not_133_out,
       not_134_out, not_135_out, not_136_out, not_137_out, not_138_out, not_139_out;

  not not_1 (not_1_out, Input_1);
  not not_2 (not_2_out, Input_2);
  not not_3 (not_3_out, Input_4);
  not not_4 (not_4_out, Input_7);
  not not_5 (not_5_out, Input_1);
  not not_6 (not_6_out, Input_2);
  not not_7 (not_7_out, Input_4);
  not not_8 (not_8_out, Input_8);
  not not_9 (not_9_out, Input_1);
  not not_10 (not_10_out, Input_5);
  not not_11 (not_11_out, Input_2);
  not not_12 (not_12_out, Input_5);
  not not_13 (not_13_out, Input_1);
  not not_14 (not_14_out, Input_2);
  not not_15 (not_15_out, Input_4);
  not not_16 (not_16_out, Input_5);
  not not_17 (not_17_out, Input_7);
  not not_18 (not_18_out, Input_1);
  not not_19 (not_19_out, Input_2);
  not not_20 (not_20_out, Input_4);
  not not_21 (not_21_out, Input_5);
  not not_22 (not_22_out, Input_8);
  not not_23 (not_23_out, Input_1);
  not not_24 (not_24_out, Input_2);
  not not_25 (not_25_out, Input_4);
  not not_26 (not_26_out, Input_6);
  not not_27 (not_27_out, Input_7);
  not not_28 (not_28_out, Input_1);
  not not_29 (not_29_out, Input_2);
  not not_30 (not_30_out, Input_4);
  not not_31 (not_31_out, Input_6);
  not not_32 (not_32_out, Input_8);
  not not_33 (not_33_out, Input_1);
  not not_34 (not_34_out, Input_3);
  not not_35 (not_35_out, Input_5);
  not not_36 (not_36_out, Input_1);
  not not_37 (not_37_out, Input_4);
  not not_38 (not_38_out, Input_5);
  not not_39 (not_39_out, Input_2);
  not not_40 (not_40_out, Input_3);
  not not_41 (not_41_out, Input_5);
  not not_42 (not_42_out, Input_2);
  not not_43 (not_43_out, Input_4);
  not not_44 (not_44_out, Input_5);
  not not_45 (not_45_out, Input_1);
  not not_46 (not_46_out, Input_2);
  not not_47 (not_47_out, Input_4);
  not not_48 (not_48_out, Input_1);
  not not_49 (not_49_out, Input_2);
  not not_50 (not_50_out, Input_5);
  not not_51 (not_51_out, Input_4);
  not not_52 (not_52_out, Input_5);
  not not_53 (not_53_out, Input_1);
  not not_54 (not_54_out, Input_2);
  not not_55 (not_55_out, Input_3);
  not not_56 (not_56_out, Input_4);
  not not_57 (not_57_out, Input_5);
  not not_58 (not_58_out, Input_7);
  not not_59 (not_59_out, Input_1);
  not not_60 (not_60_out, Input_2);
  not not_61 (not_61_out, Input_3);
  not not_62 (not_62_out, Input_4);
  not not_63 (not_63_out, Input_5);
  not not_64 (not_64_out, Input_8);
  not not_65 (not_65_out, Input_2);
  not not_66 (not_66_out, Input_3);
  not not_67 (not_67_out, Input_6);
  not not_68 (not_68_out, Input_7);
  not not_69 (not_69_out, Input_1);
  not not_70 (not_70_out, Input_3);
  not not_71 (not_71_out, Input_6);
  not not_72 (not_72_out, Input_8);
  not not_73 (not_73_out, Input_1);
  not not_74 (not_74_out, Input_2);
  not not_75 (not_75_out, Input_6);
  not not_76 (not_76_out, Input_7);
  not not_77 (not_77_out, Input_1);
  not not_78 (not_78_out, Input_2);
  not not_79 (not_79_out, Input_6);
  not not_80 (not_80_out, Input_8);
  not not_81 (not_81_out, Input_1);
  not not_82 (not_82_out, Input_3);
  not not_83 (not_83_out, Input_6);
  not not_84 (not_84_out, Input_7);
  not not_85 (not_85_out, Input_1);
  not not_86 (not_86_out, Input_2);
  not not_87 (not_87_out, Input_6);
  not not_88 (not_88_out, Input_1);
  not not_89 (not_89_out, Input_2);
  not not_90 (not_90_out, Input_7);
  not not_91 (not_91_out, Input_3);
  not not_92 (not_92_out, Input_6);
  not not_93 (not_93_out, Input_3);
  not not_94 (not_94_out, Input_8);
  not not_95 (not_95_out, Input_1);
  not not_96 (not_96_out, Input_3);
  not not_97 (not_97_out, Input_6);
  not not_98 (not_98_out, Input_1);
  not not_99 (not_99_out, Input_3);
  not not_100 (not_100_out, Input_1);
  not not_101 (not_101_out, Input_4);
  not not_102 (not_102_out, Input_5);
  not not_103 (not_103_out, Input_6);
  not not_104 (not_104_out, Input_2);
  not not_105 (not_105_out, Input_3);
  not not_106 (not_106_out, Input_6);
  not not_107 (not_107_out, Input_2);
  not not_108 (not_108_out, Input_4);
  not not_109 (not_109_out, Input_5);
  not not_110 (not_110_out, Input_6);
  not not_111 (not_111_out, Input_3);
  not not_112 (not_112_out, Input_1);
  not not_113 (not_113_out, Input_2);
  not not_114 (not_114_out, Input_3);
  not not_115 (not_115_out, Input_4);
  not not_116 (not_116_out, Input_7);
  not not_117 (not_117_out, Input_1);
  not not_118 (not_118_out, Input_2);
  not not_119 (not_119_out, Input_3);
  not not_120 (not_120_out, Input_4);
  not not_121 (not_121_out, Input_8);
  not not_122 (not_122_out, Input_1);
  not not_123 (not_123_out, Input_2);
  not not_124 (not_124_out, Input_5);
  not not_125 (not_125_out, Input_7);
  not not_126 (not_126_out, Input_1);
  not not_127 (not_127_out, Input_2);
  not not_128 (not_128_out, Input_5);
  not not_129 (not_129_out, Input_8);
  not not_130 (not_130_out, Input_1);
  not not_131 (not_131_out, Input_4);
  not not_132 (not_132_out, Input_1);
  not not_133 (not_133_out, Input_5);
  not not_134 (not_134_out, Input_6);
  not not_135 (not_135_out, Input_2);
  not not_136 (not_136_out, Input_4);
  not not_137 (not_137_out, Input_2);
  not not_138 (not_138_out, Input_5);
  not not_139 (not_139_out, Input_6);
  and and_1 (and_1_out, not_1_out, not_2_out, Input_3, not_3_out, Input_5, Input_6, not_4_out);
  and and_2 (and_2_out, not_5_out, not_6_out, Input_3, not_7_out, Input_5, Input_6, not_8_out);
  and and_3 (and_3_out, not_9_out, Input_2, Input_3, Input_4, not_10_out, Input_6);
  and and_4 (and_4_out, Input_1, not_11_out, Input_3, Input_4, not_12_out, Input_6);
  and and_5 (and_5_out, not_13_out, not_14_out, Input_3, not_15_out, not_16_out, not_17_out);
  and and_6 (and_6_out, not_18_out, not_19_out, Input_3, not_20_out, not_21_out, not_22_out);
  and and_7 (and_7_out, not_23_out, not_24_out, Input_3, not_25_out, not_26_out, not_27_out);
  and and_8 (and_8_out, not_28_out, not_29_out, Input_3, not_30_out, not_31_out, not_32_out);
  and and_9 (and_9_out, not_33_out, Input_2, not_34_out, not_35_out, Input_6);
  and and_10 (and_10_out, not_36_out, Input_2, not_37_out, not_38_out, Input_6);
  and and_11 (and_11_out, Input_1, not_39_out, not_40_out, not_41_out, Input_6);
  and and_12 (and_12_out, Input_1, not_42_out, not_43_out, not_44_out, Input_6);
  and and_13 (and_13_out, not_45_out, not_46_out, not_47_out, Input_5, Input_6, Input_7, Input_8);
  and and_14 (and_14_out, not_48_out, not_49_out, Input_4, not_50_out, Input_6, Input_7, Input_8);
  and and_15 (and_15_out, Input_1, Input_2, Input_3, not_51_out, Input_5);
  and and_16 (and_16_out, Input_1, Input_2, Input_3, Input_4, not_52_out);
  and and_17 (and_17_out, not_53_out, not_54_out, not_55_out, not_56_out, not_57_out, not_58_out);
  and and_18 (and_18_out, not_59_out, not_60_out, not_61_out, not_62_out, not_63_out, not_64_out);
  and and_19 (and_19_out, not_65_out, not_66_out, not_67_out, not_68_out);
  and and_20 (and_20_out, not_69_out, not_70_out, not_71_out, Input_7, not_72_out);
  and and_21 (and_21_out, not_73_out, not_74_out, Input_4, not_75_out, not_76_out);
  and and_22 (and_22_out, not_77_out, not_78_out, Input_4, not_79_out, not_80_out);
  and and_23 (and_23_out, not_81_out, not_82_out, Input_4, not_83_out, not_84_out);
  and and_24 (and_24_out, not_85_out, not_86_out, Input_4, Input_5, not_87_out);
  and and_25 (and_25_out, not_88_out, not_89_out, Input_4, Input_5, not_90_out);
  and and_26 (and_26_out, not_91_out, Input_4, Input_5, not_92_out);
  and and_27 (and_27_out, not_93_out, Input_4, Input_5, not_94_out);
  and and_28 (and_28_out, not_95_out, Input_2, not_96_out, not_97_out, Input_8);
  and and_29 (and_29_out, not_98_out, Input_2, not_99_out, Input_5);
  and and_30 (and_30_out, not_100_out, Input_2, Input_3, not_101_out, not_102_out, not_103_out);
  and and_31 (and_31_out, Input_1, not_104_out, not_105_out, not_106_out);
  and and_32 (and_32_out, Input_1, not_107_out, not_108_out, not_109_out, not_110_out);
  and and_33 (and_33_out, Input_1, not_111_out, Input_5, Input_6);
  and and_34 (and_34_out, not_112_out, not_113_out, not_114_out, not_115_out, Input_5, Input_6, not_116_out);
  and and_35 (and_35_out, not_117_out, not_118_out, not_119_out, not_120_out, Input_5, Input_6, not_121_out);
  and and_36 (and_36_out, not_122_out, not_123_out, Input_4, not_124_out, Input_6, not_125_out);
  and and_37 (and_37_out, not_126_out, not_127_out, Input_4, not_128_out, Input_6, not_129_out);
  and and_38 (and_38_out, not_130_out, Input_2, Input_3, not_131_out, Input_5);
  and and_39 (and_39_out, not_132_out, Input_2, Input_3, Input_4, not_133_out, not_134_out);
  and and_40 (and_40_out, Input_1, not_135_out, Input_3, not_136_out, Input_5);
  and and_41 (and_41_out, Input_1, not_137_out, Input_3, Input_4, not_138_out, not_139_out);
  or or_1 (e2, and_1_out, and_2_out, and_3_out, and_4_out);
  or or_2 (d2, and_5_out, and_6_out, and_7_out, and_8_out, and_9_out, and_10_out, and_11_out, and_12_out);
  or or_3 (g1, and_13_out, and_14_out, and_15_out, and_16_out);
  or or_4 (c1, and_34_out, and_35_out, and_36_out, and_37_out, and_38_out, and_39_out, and_40_out, and_41_out);
  or or_5 (e1, and_17_out, and_18_out, and_19_out, and_20_out, and_21_out, and_22_out, and_23_out, and_24_out, and_25_out, and_26_out, and_27_out, and_28_out, and_29_out, and_30_out, and_31_out, and_32_out, and_33_out);

  assign reset = Input_2;
endmodule

module Kalinka (
  input  Input_1,
  input  Input_2,
  input  Input_3,
  input  Input_4,
  input  Input_5,
  input  Input_6,
  input  Input_7,
  input  Input_8,
  output [12:0] Output_bus_1,
  output reset
);

  wire and_2_out, and_3_out, and_4_out, and_5_out, and_6_out, and_7_out, and_8_out, and_9_out, and_10_out,
       and_11_out, and_12_out, and_13_out, and_14_out, and_15_out, and_16_out, and_17_out, and_18_out,
       and_19_out, and_20_out, and_21_out, and_22_out, and_23_out, and_24_out, and_25_out, and_26_out,
       and_27_out, and_28_out, and_29_out, not_1_out, not_2_out, not_3_out, not_4_out, not_5_out, not_6_out,
       not_7_out, not_8_out, not_9_out, not_10_out, not_11_out, not_12_out, not_13_out, not_14_out,
       not_15_out, not_16_out, not_17_out, not_18_out, not_19_out, not_20_out, not_21_out, not_22_out,
       not_23_out, not_24_out, not_25_out, not_26_out, not_27_out, not_28_out, not_29_out, not_30_out,
       not_31_out, not_32_out, not_33_out, not_34_out, not_35_out, not_36_out, not_37_out, not_38_out,
       not_39_out, not_40_out, not_41_out, not_42_out, not_43_out, not_44_out, not_45_out, not_46_out,
       not_47_out, not_48_out, not_49_out, not_50_out, not_51_out, not_52_out, not_53_out, not_54_out,
       not_55_out, not_56_out, not_57_out, not_58_out, not_59_out, not_60_out;

  not not_1 (not_1_out, Input_3);
  not not_2 (not_2_out, Input_4);
  not not_3 (not_3_out, Input_5);
  not not_4 (not_4_out, Input_4);
  not not_5 (not_5_out, Input_6);
  not not_6 (not_6_out, Input_2);
  not not_7 (not_7_out, Input_3);
  not not_8 (not_8_out, Input_4);
  not not_9 (not_9_out, Input_6);
  not not_10 (not_10_out, Input_6);
  not not_11 (not_11_out, Input_2);
  not not_12 (not_12_out, Input_3);
  not not_13 (not_13_out, Input_6);
  not not_14 (not_14_out, Input_2);
  not not_15 (not_15_out, Input_4);
  not not_16 (not_16_out, Input_6);
  not not_17 (not_17_out, Input_2);
  not not_18 (not_18_out, Input_7);
  not not_19 (not_19_out, Input_4);
  not not_20 (not_20_out, Input_5);
  not not_21 (not_21_out, Input_2);
  not not_22 (not_22_out, Input_3);
  not not_23 (not_23_out, Input_4);
  not not_24 (not_24_out, Input_5);
  not not_25 (not_25_out, Input_2);
  not not_26 (not_26_out, Input_3);
  not not_27 (not_27_out, Input_2);
  not not_28 (not_28_out, Input_4);
  not not_29 (not_29_out, Input_2);
  not not_30 (not_30_out, Input_6);
  not not_31 (not_31_out, Input_4);
  not not_32 (not_32_out, Input_5);
  not not_33 (not_33_out, Input_7);
  not not_34 (not_34_out, Input_2);
  not not_35 (not_35_out, Input_3);
  not not_36 (not_36_out, Input_4);
  not not_37 (not_37_out, Input_5);
  not not_38 (not_38_out, Input_7);
  not not_39 (not_39_out, Input_6);
  not not_40 (not_40_out, Input_5);
  not not_41 (not_41_out, Input_7);
  not not_42 (not_42_out, Input_2);
  not not_43 (not_43_out, Input_5);
  not not_44 (not_44_out, Input_2);
  not not_45 (not_45_out, Input_5);
  not not_46 (not_46_out, Input_5);
  not not_47 (not_47_out, Input_6);
  not not_48 (not_48_out, Input_6);
  not not_49 (not_49_out, Input_2);
  not not_50 (not_50_out, Input_5);
  not not_51 (not_51_out, Input_6);
  not not_52 (not_52_out, Input_1);
  not not_53 (not_53_out, Input_2);
  not not_54 (not_54_out, Input_3);
  not not_55 (not_55_out, Input_4);
  not not_56 (not_56_out, Input_3);
  not not_57 (not_57_out, Input_4);
  not not_58 (not_58_out, Input_3);
  not not_59 (not_59_out, Input_4);
  not not_60 (not_60_out, Input_4);
  and and_1 (reset, Input_1, Input_5, Input_6);
  and and_2 (and_2_out, Input_2, not_1_out, not_2_out, not_3_out);
  and and_3 (and_3_out, Input_2, Input_3, not_4_out, Input_5, not_5_out);
  and and_4 (and_4_out, Input_1, not_6_out, not_7_out, not_8_out, Input_5, not_9_out);
  and and_5 (and_5_out, Input_1, Input_2, Input_3, Input_5, not_10_out);
  and and_6 (and_6_out, not_11_out, not_12_out, Input_4, Input_5, not_13_out);
  and and_7 (and_7_out, not_14_out, Input_3, not_15_out, Input_5, not_16_out);
  and and_8 (and_8_out, not_17_out, Input_3, Input_4, Input_5, Input_6);
  and and_9 (and_9_out, Input_2, Input_4, Input_6, not_18_out);
  and and_10 (and_10_out, Input_2, Input_3, not_19_out, not_20_out, Input_6, Input_7);
  and and_11 (and_11_out, Input_1, not_21_out, not_22_out, not_23_out, not_24_out, Input_6, Input_7);
  and and_12 (and_12_out, Input_1, Input_2, Input_3, Input_4, Input_6);
  and and_13 (and_13_out, not_25_out, not_26_out, Input_4, Input_5, Input_6);
  and and_14 (and_14_out, not_27_out, Input_3, not_28_out, Input_5, Input_6);
  and and_15 (and_15_out, not_29_out, Input_3, Input_4, Input_5, not_30_out);
  and and_16 (and_16_out, Input_2, Input_4, Input_6, Input_7);
  and and_17 (and_17_out, Input_2, Input_3, not_31_out, not_32_out, Input_6, not_33_out);
  and and_18 (and_18_out, Input_1, not_34_out, not_35_out, not_36_out, not_37_out, Input_6, not_38_out);
  and and_19 (and_19_out, Input_1, Input_3, Input_4, Input_5, not_39_out);
  and and_20 (and_20_out, Input_1, Input_2, Input_3, not_40_out, Input_6, not_41_out);
  and and_21 (and_21_out, not_42_out, Input_4, not_43_out);
  and and_22 (and_22_out, not_44_out, Input_3, not_45_out);
  and and_23 (and_23_out, Input_3, not_46_out, not_47_out);
  and and_24 (and_24_out, Input_2, Input_4, not_48_out);
  and and_25 (and_25_out, Input_1, not_49_out, not_50_out, not_51_out);
  and and_26 (and_26_out, not_52_out, not_53_out, not_54_out, not_55_out);
  and and_27 (and_27_out, not_56_out, not_57_out, Input_5, Input_6, Input_7);
  and and_28 (and_28_out, Input_2, not_58_out, not_59_out, Input_5);
  and and_29 (and_29_out, Input_2, not_60_out, Input_5, Input_6);
  or or_1 (Output_bus_1[8], and_2_out, and_3_out, and_4_out, and_5_out);
  or or_2 (Output_bus_1[7], and_6_out, and_7_out, and_8_out, and_9_out, and_10_out, and_11_out, and_12_out);
  or or_3 (Output_bus_1[6], and_13_out, and_14_out, and_15_out, and_16_out, and_17_out, and_18_out, and_19_out, and_20_out);
  or or_4 (Output_bus_1[5], and_21_out, and_22_out, and_23_out, and_24_out, and_25_out);
  or or_5 (Output_bus_1[4], and_26_out, and_27_out, and_28_out, and_29_out);

  assign {Output_bus_1[12:9], Output_bus_1[3:0]} = {8{1'b0}};
endmodule

module PirateCaraibe (
  input  Input_1,
  input  Input_2,
  input  Input_3,
  input  Input_4,
  input  Input_5,
  input  Input_6,
  input  Input_7,
  input  Input_8,
  output [12:0] Output_bus_1,
  output Output_1
);

  wire and_2_out, and_3_out, and_4_out, and_5_out, and_6_out, and_7_out, and_8_out, and_9_out, and_10_out,
       and_11_out, and_12_out, and_13_out, and_14_out, and_15_out, and_16_out, and_17_out, and_18_out,
       and_19_out, and_20_out, and_21_out, and_22_out, and_23_out, and_24_out, and_25_out, and_26_out,
       and_27_out, and_28_out, and_29_out, and_30_out, and_31_out, and_32_out, and_33_out, and_34_out,
       and_35_out, and_36_out, not_1_out, not_2_out, not_3_out, not_4_out, not_5_out, not_6_out, not_7_out,
       not_8_out, not_9_out, not_10_out, not_11_out, not_12_out, not_13_out, not_14_out, not_15_out,
       not_16_out, not_17_out, not_18_out, not_19_out, not_20_out, not_21_out, not_22_out, not_23_out,
       not_24_out, not_25_out, not_26_out, not_27_out, not_28_out, not_29_out, not_30_out, not_31_out,
       not_32_out, not_33_out, not_34_out, not_35_out, not_36_out, not_37_out, not_38_out, not_39_out,
       not_40_out, not_41_out, not_42_out, not_43_out, not_44_out, not_45_out, not_46_out, not_47_out,
       not_48_out, not_49_out, not_50_out, not_51_out, not_52_out, not_53_out, not_54_out, not_55_out,
       not_56_out, not_57_out, not_58_out, not_59_out, not_60_out, not_61_out, not_62_out, not_63_out,
       not_64_out, not_65_out, not_66_out, not_67_out, not_68_out, not_69_out, not_70_out, not_71_out,
       not_72_out, not_73_out, not_74_out, not_75_out, not_76_out, not_77_out, not_78_out, not_79_out,
       not_80_out, not_81_out, not_82_out, not_83_out, not_84_out, not_85_out, not_86_out, not_87_out,
       not_88_out, not_89_out, not_90_out, not_91_out, not_92_out, not_93_out;

  not not_1 (not_1_out, Input_2);
  not not_2 (not_2_out, Input_3);
  not not_3 (not_3_out, Input_4);
  not not_4 (not_4_out, Input_6);
  not not_5 (not_5_out, Input_7);
  not not_6 (not_6_out, Input_8);
  not not_7 (not_7_out, Input_5);
  not not_8 (not_8_out, Input_7);
  not not_9 (not_9_out, Input_2);
  not not_10 (not_10_out, Input_3);
  not not_11 (not_11_out, Input_4);
  not not_12 (not_12_out, Input_6);
  not not_13 (not_13_out, Input_8);
  not not_14 (not_14_out, Input_4);
  not not_15 (not_15_out, Input_5);
  not not_16 (not_16_out, Input_6);
  not not_17 (not_17_out, Input_7);
  not not_18 (not_18_out, Input_2);
  not not_19 (not_19_out, Input_3);
  not not_20 (not_20_out, Input_5);
  not not_21 (not_21_out, Input_6);
  not not_22 (not_22_out, Input_7);
  not not_23 (not_23_out, Input_2);
  not not_24 (not_24_out, Input_3);
  not not_25 (not_25_out, Input_5);
  not not_26 (not_26_out, Input_6);
  not not_27 (not_27_out, Input_8);
  not not_28 (not_28_out, Input_2);
  not not_29 (not_29_out, Input_3);
  not not_30 (not_30_out, Input_5);
  not not_31 (not_31_out, Input_7);
  not not_32 (not_32_out, Input_8);
  not not_33 (not_33_out, Input_3);
  not not_34 (not_34_out, Input_4);
  not not_35 (not_35_out, Input_5);
  not not_36 (not_36_out, Input_6);
  not not_37 (not_37_out, Input_7);
  not not_38 (not_38_out, Input_2);
  not not_39 (not_39_out, Input_3);
  not not_40 (not_40_out, Input_4);
  not not_41 (not_41_out, Input_8);
  not not_42 (not_42_out, Input_2);
  not not_43 (not_43_out, Input_3);
  not not_44 (not_44_out, Input_4);
  not not_45 (not_45_out, Input_7);
  not not_46 (not_46_out, Input_3);
  not not_47 (not_47_out, Input_5);
  not not_48 (not_48_out, Input_8);
  not not_49 (not_49_out, Input_2);
  not not_50 (not_50_out, Input_4);
  not not_51 (not_51_out, Input_5);
  not not_52 (not_52_out, Input_2);
  not not_53 (not_53_out, Input_4);
  not not_54 (not_54_out, Input_5);
  not not_55 (not_55_out, Input_7);
  not not_56 (not_56_out, Input_4);
  not not_57 (not_57_out, Input_6);
  not not_58 (not_58_out, Input_7);
  not not_59 (not_59_out, Input_4);
  not not_60 (not_60_out, Input_6);
  not not_61 (not_61_out, Input_5);
  not not_62 (not_62_out, Input_6);
  not not_63 (not_63_out, Input_7);
  not not_64 (not_64_out, Input_3);
  not not_65 (not_65_out, Input_5);
  not not_66 (not_66_out, Input_6);
  not not_67 (not_67_out, Input_5);
  not not_68 (not_68_out, Input_6);
  not not_69 (not_69_out, Input_7);
  not not_70 (not_70_out, Input_5);
  not not_71 (not_71_out, Input_2);
  not not_72 (not_72_out, Input_3);
  not not_73 (not_73_out, Input_2);
  not not_74 (not_74_out, Input_3);
  not not_75 (not_75_out, Input_7);
  not not_76 (not_76_out, Input_2);
  not not_77 (not_77_out, Input_3);
  not not_78 (not_78_out, Input_3);
  not not_79 (not_79_out, Input_4);
  not not_80 (not_80_out, Input_5);
  not not_81 (not_81_out, Input_3);
  not not_82 (not_82_out, Input_4);
  not not_83 (not_83_out, Input_5);
  not not_84 (not_84_out, Input_4);
  not not_85 (not_85_out, Input_7);
  not not_86 (not_86_out, Input_4);
  not not_87 (not_87_out, Input_6);
  not not_88 (not_88_out, Input_2);
  not not_89 (not_89_out, Input_4);
  not not_90 (not_90_out, Input_5);
  not not_91 (not_91_out, Input_6);
  not not_92 (not_92_out, Input_7);
  not not_93 (not_93_out, Input_4);
  and and_1 (Output_1, Input_2, Input_3, Input_6, Input_7, Input_8);
  and and_2 (and_2_out, not_1_out, not_2_out, not_3_out, Input_5, not_4_out, not_5_out, not_6_out);
  and and_3 (and_3_out, Input_3, Input_4, not_7_out, Input_6, not_8_out, Input_8);
  and and_4 (and_4_out, not_9_out, not_10_out, not_11_out, Input_5, not_12_out, Input_7, not_13_out);
  and and_5 (and_5_out, Input_3, not_14_out, Input_5, Input_6, Input_8);
  and and_6 (and_6_out, Input_3, Input_4, not_15_out, Input_6, Input_7, Input_8);
  and and_7 (and_7_out, Input_2, Input_4, Input_5, not_16_out, Input_7, Input_8);
  and and_8 (and_8_out, Input_2, Input_4, Input_5, Input_6, not_17_out, Input_8);
  and and_9 (and_9_out, not_18_out, not_19_out, not_20_out, not_21_out, not_22_out);
  and and_10 (and_10_out, not_23_out, not_24_out, not_25_out, not_26_out, not_27_out);
  and and_11 (and_11_out, not_28_out, not_29_out, not_30_out, not_31_out, not_32_out);
  and and_12 (and_12_out, not_33_out, not_34_out, not_35_out, not_36_out, not_37_out, Input_8);
  and and_13 (and_13_out, not_38_out, not_39_out, not_40_out, Input_6, not_41_out);
  and and_14 (and_14_out, not_42_out, not_43_out, not_44_out, Input_5, Input_6, not_45_out);
  and and_15 (and_15_out, Input_3, Input_4, Input_5, Input_8);
  and and_16 (and_16_out, Input_3, Input_4, Input_5, Input_7);
  and and_17 (and_17_out, Input_2, Input_4, Input_5, Input_6, Input_7, Input_8);
  and and_18 (and_18_out, not_46_out, Input_4, not_47_out, Input_6, Input_7, not_48_out);
  and and_19 (and_19_out, not_49_out, Input_3, not_50_out, not_51_out, Input_7, Input_8);
  and and_20 (and_20_out, not_52_out, Input_3, not_53_out, not_54_out, Input_6, not_55_out);
  and and_21 (and_21_out, Input_3, not_56_out, Input_5, not_57_out, not_58_out);
  and and_22 (and_22_out, Input_3, not_59_out, Input_5, not_60_out, Input_8);
  and and_23 (and_23_out, Input_3, Input_4, not_61_out, not_62_out, not_63_out, Input_8);
  and and_24 (and_24_out, Input_2, not_64_out, not_65_out, not_66_out, Input_7, Input_8);
  and and_25 (and_25_out, Input_2, Input_4, not_67_out, Input_8);
  and and_26 (and_26_out, Input_2, Input_4, not_68_out, not_69_out, Input_8);
  and and_27 (and_27_out, Input_2, Input_4, not_70_out, Input_7);
  and and_28 (and_28_out, not_71_out, not_72_out, Input_4, Input_6, Input_7, Input_8);
  and and_29 (and_29_out, not_73_out, not_74_out, Input_4, Input_5, not_75_out);
  and and_30 (and_30_out, not_76_out, not_77_out, Input_4, Input_5, Input_8);
  and and_31 (and_31_out, Input_2, not_78_out, not_79_out, not_80_out, Input_6, Input_8);
  and and_32 (and_32_out, Input_2, not_81_out, not_82_out, not_83_out, Input_6, Input_7);
  and and_33 (and_33_out, Input_2, not_84_out, Input_5, not_85_out, Input_8);
  and and_34 (and_34_out, Input_2, not_86_out, Input_5, not_87_out, Input_7);
  and and_35 (and_35_out, not_88_out, Input_3, not_89_out, not_90_out, not_91_out, not_92_out, Input_8);
  and and_36 (and_36_out, Input_2, not_93_out, Input_5, Input_6, Input_7, Input_8);
  or or_1 (Output_bus_1[10], and_2_out, and_3_out);
  or or_2 (Output_bus_1[9], and_4_out, and_5_out, and_6_out, and_7_out, and_8_out);
  or or_3 (Output_bus_1[8], and_9_out, and_10_out, and_11_out, and_12_out, and_13_out, and_14_out, and_15_out, and_16_out, and_17_out);
  or or_4 (Output_bus_1[6], and_28_out, and_29_out, and_30_out, and_31_out, and_32_out, and_33_out, and_34_out);
  or or_5 (Output_bus_1[5], and_35_out, and_36_out);
  or or_6 (Output_bus_1[7], and_18_out, and_19_out, and_20_out, and_21_out, and_22_out, and_23_out, and_24_out, and_25_out, and_26_out, and_27_out);

  assign {Output_bus_1[12:11], Output_bus_1[4:0]} = {7{1'b0}};
endmodule

module ThisMustBeThePlace (
  input  Input_1,
  input  Input_2,
  input  Input_3,
  input  Input_4,
  input  Input_5,
  input  Input_6,
  input  Input_7,
  input  Input_8,
  output A1,
  output G1,
  output E1,
  output D1,
  output C1,
  output reset
);

  wire and_2_out, and_3_out, and_4_out, and_6_out, and_7_out, and_8_out, and_9_out, not_1_out, not_2_out,
       not_3_out, not_4_out, not_5_out, not_6_out, not_7_out, not_8_out, not_9_out, not_10_out, not_11_out,
       not_12_out, not_13_out, not_14_out, not_15_out, not_16_out, not_17_out, not_18_out, not_19_out,
       not_20_out;

  and and_1 (A1, Input_5, Input_6, Input_7);
  not not_1 (not_1_out, Input_5);
  not not_2 (not_2_out, Input_8);
  not not_3 (not_3_out, Input_4);
  not not_4 (not_4_out, Input_5);
  not not_5 (not_5_out, Input_7);
  not not_6 (not_6_out, Input_6);
  not not_7 (not_7_out, Input_8);
  not not_8 (not_8_out, Input_3);
  not not_9 (not_9_out, Input_4);
  not not_10 (not_10_out, Input_5);
  not not_11 (not_11_out, Input_6);
  not not_12 (not_12_out, Input_8);
  not not_13 (not_13_out, Input_4);
  not not_14 (not_14_out, Input_5);
  not not_15 (not_15_out, Input_7);
  not not_16 (not_16_out, Input_5);
  not not_17 (not_17_out, Input_6);
  not not_18 (not_18_out, Input_8);
  not not_19 (not_19_out, Input_5);
  not not_20 (not_20_out, Input_7);
  and and_2 (and_2_out, not_1_out, Input_6, not_2_out);
  and and_3 (and_3_out, not_3_out, not_4_out, Input_6, Input_7);
  and and_4 (and_4_out, Input_5, Input_6, not_5_out);
  and and_5 (E1, Input_5, not_6_out, not_7_out);
  and and_6 (and_6_out, not_8_out, not_9_out, not_10_out, not_11_out, not_12_out);
  and and_7 (and_7_out, not_13_out, not_14_out, Input_6, not_15_out, Input_8);
  and and_8 (and_8_out, Input_4, not_16_out, not_17_out, not_18_out);
  and and_9 (and_9_out, Input_4, not_19_out, Input_6, not_20_out, Input_8);
  or or_1 (G1, and_2_out, and_3_out, and_4_out);
  or or_2 (D1, and_6_out, and_7_out);
  or or_3 (C1, and_8_out, and_9_out);

  assign reset = Input_3;
endmodule

module MissYou (
  input  Input_1,
  input  Input_2,
  input  Input_3,
  input  Input_4,
  input  Input_5,
  input  Input_6,
  input  Input_7,
  input  Input_8,
  output E2,
  output D2,
  output B1,
  output A1,
  output reset
);

  wire and_1_out, and_2_out, and_3_out, and_4_out, and_5_out, and_6_out, and_7_out, and_8_out, and_9_out,
       and_10_out, and_11_out, and_12_out, and_13_out, and_14_out, and_15_out, and_16_out, and_17_out,
       and_18_out, and_19_out, and_20_out, and_21_out, and_22_out, and_23_out, and_24_out, and_25_out,
       and_26_out, and_27_out, and_28_out, and_29_out, and_30_out, and_31_out, and_32_out, and_33_out,
       and_34_out, and_35_out, and_36_out, not_1_out, not_2_out, not_3_out, not_4_out, not_5_out, not_6_out,
       not_7_out, not_8_out, not_9_out, not_10_out, not_11_out, not_12_out, not_13_out, not_14_out,
       not_15_out, not_16_out, not_17_out, not_18_out, not_19_out, not_20_out, not_21_out, not_22_out,
       not_23_out, not_24_out, not_25_out, not_26_out, not_27_out, not_28_out, not_29_out, not_30_out,
       not_31_out, not_32_out, not_33_out, not_34_out, not_35_out, not_36_out, not_37_out, not_38_out,
       not_39_out, not_40_out, not_41_out, not_42_out, not_43_out, not_44_out, not_45_out, not_46_out,
       not_47_out, not_48_out, not_49_out, not_50_out, not_51_out, not_52_out, not_53_out, not_54_out,
       not_55_out, not_56_out, not_57_out, not_58_out, not_59_out, not_60_out, not_61_out, not_62_out,
       not_63_out, not_64_out, not_65_out, not_66_out, not_67_out, not_68_out, not_69_out, not_70_out,
       not_71_out, not_72_out, not_73_out, not_74_out, not_75_out, not_76_out, not_77_out, not_78_out,
       not_79_out, not_80_out, not_81_out, not_82_out, not_83_out, not_84_out, not_85_out, not_86_out,
       not_87_out, not_88_out, not_89_out, not_90_out, not_91_out, not_92_out, not_93_out, not_94_out,
       not_95_out, not_96_out, not_97_out, not_98_out, not_99_out, not_100_out, not_101_out, not_102_out,
       not_103_out, not_104_out;

  not not_1 (not_1_out, Input_3);
  not not_2 (not_2_out, Input_5);
  not not_3 (not_3_out, Input_7);
  not not_4 (not_4_out, Input_8);
  not not_5 (not_5_out, Input_3);
  not not_6 (not_6_out, Input_5);
  not not_7 (not_7_out, Input_7);
  not not_8 (not_8_out, Input_3);
  not not_9 (not_9_out, Input_5);
  not not_10 (not_10_out, Input_7);
  not not_11 (not_11_out, Input_3);
  not not_12 (not_12_out, Input_5);
  not not_13 (not_13_out, Input_8);
  not not_14 (not_14_out, Input_4);
  not not_15 (not_15_out, Input_5);
  not not_16 (not_16_out, Input_7);
  not not_17 (not_17_out, Input_8);
  not not_18 (not_18_out, Input_3);
  not not_19 (not_19_out, Input_5);
  not not_20 (not_20_out, Input_4);
  not not_21 (not_21_out, Input_5);
  not not_22 (not_22_out, Input_7);
  not not_23 (not_23_out, Input_3);
  not not_24 (not_24_out, Input_5);
  not not_25 (not_25_out, Input_4);
  not not_26 (not_26_out, Input_5);
  not not_27 (not_27_out, Input_7);
  not not_28 (not_28_out, Input_3);
  not not_29 (not_29_out, Input_5);
  not not_30 (not_30_out, Input_6);
  not not_31 (not_31_out, Input_8);
  not not_32 (not_32_out, Input_4);
  not not_33 (not_33_out, Input_5);
  not not_34 (not_34_out, Input_6);
  not not_35 (not_35_out, Input_8);
  not not_36 (not_36_out, Input_3);
  not not_37 (not_37_out, Input_7);
  not not_38 (not_38_out, Input_8);
  not not_39 (not_39_out, Input_4);
  not not_40 (not_40_out, Input_7);
  not not_41 (not_41_out, Input_8);
  not not_42 (not_42_out, Input_3);
  not not_43 (not_43_out, Input_7);
  not not_44 (not_44_out, Input_3);
  not not_45 (not_45_out, Input_8);
  not not_46 (not_46_out, Input_4);
  not not_47 (not_47_out, Input_5);
  not not_48 (not_48_out, Input_4);
  not not_49 (not_49_out, Input_6);
  not not_50 (not_50_out, Input_3);
  not not_51 (not_51_out, Input_5);
  not not_52 (not_52_out, Input_6);
  not not_53 (not_53_out, Input_3);
  not not_54 (not_54_out, Input_7);
  not not_55 (not_55_out, Input_4);
  not not_56 (not_56_out, Input_7);
  not not_57 (not_57_out, Input_3);
  not not_58 (not_58_out, Input_4);
  not not_59 (not_59_out, Input_3);
  not not_60 (not_60_out, Input_5);
  not not_61 (not_61_out, Input_6);
  not not_62 (not_62_out, Input_3);
  not not_63 (not_63_out, Input_7);
  not not_64 (not_64_out, Input_3);
  not not_65 (not_65_out, Input_4);
  not not_66 (not_66_out, Input_4);
  not not_67 (not_67_out, Input_2);
  not not_68 (not_68_out, Input_3);
  not not_69 (not_69_out, Input_5);
  not not_70 (not_70_out, Input_6);
  not not_71 (not_71_out, Input_7);
  not not_72 (not_72_out, Input_8);
  not not_73 (not_73_out, Input_2);
  not not_74 (not_74_out, Input_4);
  not not_75 (not_75_out, Input_5);
  not not_76 (not_76_out, Input_6);
  not not_77 (not_77_out, Input_7);
  not not_78 (not_78_out, Input_8);
  not not_79 (not_79_out, Input_3);
  not not_80 (not_80_out, Input_6);
  not not_81 (not_81_out, Input_8);
  not not_82 (not_82_out, Input_3);
  not not_83 (not_83_out, Input_6);
  not not_84 (not_84_out, Input_2);
  not not_85 (not_85_out, Input_3);
  not not_86 (not_86_out, Input_5);
  not not_87 (not_87_out, Input_6);
  not not_88 (not_88_out, Input_7);
  not not_89 (not_89_out, Input_2);
  not not_90 (not_90_out, Input_4);
  not not_91 (not_91_out, Input_5);
  not not_92 (not_92_out, Input_6);
  not not_93 (not_93_out, Input_7);
  not not_94 (not_94_out, Input_3);
  not not_95 (not_95_out, Input_6);
  not not_96 (not_96_out, Input_1);
  not not_97 (not_97_out, Input_3);
  not not_98 (not_98_out, Input_4);
  not not_99 (not_99_out, Input_5);
  not not_100 (not_100_out, Input_6);
  not not_101 (not_101_out, Input_7);
  not not_102 (not_102_out, Input_8);
  not not_103 (not_103_out, Input_3);
  not not_104 (not_104_out, Input_7);
  and and_1 (and_1_out, not_1_out, not_2_out, Input_6, not_3_out, not_4_out);
  and and_2 (and_2_out, Input_2, not_5_out, not_6_out, Input_6, not_7_out);
  and and_3 (and_3_out, Input_1, not_8_out, not_9_out, Input_6, not_10_out);
  and and_4 (and_4_out, not_11_out, not_12_out, Input_6, Input_7, not_13_out);
  and and_5 (and_5_out, Input_3, not_14_out, not_15_out, Input_6, not_16_out, not_17_out);
  and and_6 (and_6_out, Input_2, not_18_out, not_19_out, Input_6, Input_7);
  and and_7 (and_7_out, Input_2, Input_3, not_20_out, not_21_out, Input_6, not_22_out);
  and and_8 (and_8_out, Input_1, not_23_out, not_24_out, Input_6, Input_7);
  and and_9 (and_9_out, Input_1, Input_3, not_25_out, not_26_out, Input_6, not_27_out);
  and and_10 (and_10_out, not_28_out, not_29_out, not_30_out, Input_7, not_31_out);
  and and_11 (and_11_out, not_32_out, not_33_out, not_34_out, Input_7, not_35_out);
  and and_12 (and_12_out, not_36_out, Input_5, not_37_out, not_38_out);
  and and_13 (and_13_out, not_39_out, Input_5, not_40_out, not_41_out);
  and and_14 (and_14_out, not_42_out, Input_5, Input_6, not_43_out);
  and and_15 (and_15_out, not_44_out, Input_5, Input_6, not_45_out);
  and and_16 (and_16_out, Input_3, not_46_out, not_47_out, Input_6, Input_7);
  and and_17 (and_17_out, Input_3, not_48_out, Input_5, not_49_out);
  and and_18 (and_18_out, Input_2, not_50_out, not_51_out, not_52_out, Input_7);
  and and_19 (and_19_out, Input_2, not_53_out, Input_5, not_54_out);
  and and_20 (and_20_out, Input_2, not_55_out, Input_5, not_56_out);
  and and_21 (and_21_out, Input_2, not_57_out, Input_5, Input_6);
  and and_22 (and_22_out, Input_2, Input_3, not_58_out, Input_7);
  and and_23 (and_23_out, Input_1, not_59_out, not_60_out, not_61_out, Input_7);
  and and_24 (and_24_out, Input_1, not_62_out, Input_5, not_63_out);
  and and_25 (and_25_out, Input_1, not_64_out, Input_5, Input_6);
  and and_26 (and_26_out, Input_1, not_65_out, Input_5, Input_6);
  and and_27 (and_27_out, Input_1, Input_3, not_66_out, Input_7);
  and and_28 (and_28_out, not_67_out, not_68_out, not_69_out, not_70_out, not_71_out, not_72_out);
  and and_29 (and_29_out, not_73_out, not_74_out, not_75_out, not_76_out, not_77_out, not_78_out);
  and and_30 (and_30_out, not_79_out, Input_5, not_80_out, Input_7, not_81_out);
  and and_31 (and_31_out, Input_2, not_82_out, Input_5, not_83_out, Input_7);
  and and_32 (and_32_out, Input_1, not_84_out, not_85_out, not_86_out, not_87_out, not_88_out);
  and and_33 (and_33_out, Input_1, not_89_out, not_90_out, not_91_out, not_92_out, not_93_out);
  and and_34 (and_34_out, Input_1, not_94_out, Input_5, not_95_out, Input_7);
  and and_35 (and_35_out, not_96_out, Input_2, not_97_out, not_98_out, not_99_out, not_100_out, not_101_out, not_102_out);
  and and_36 (and_36_out, Input_2, not_103_out, Input_4, Input_5, Input_6, not_104_out, Input_8);
  or or_1 (E2, and_1_out, and_2_out, and_3_out);
  or or_2 (D2, and_4_out, and_5_out, and_6_out, and_7_out, and_8_out, and_9_out);
  or or_3 (A1, and_28_out, and_29_out, and_30_out, and_31_out, and_32_out, and_33_out, and_34_out);
  or or_4 (reset, and_35_out, and_36_out);
  or or_5 (B1, and_10_out, and_11_out, and_12_out, and_13_out, and_14_out, and_15_out, and_16_out, and_17_out, and_18_out, and_19_out, and_20_out, and_21_out, and_22_out, and_23_out, and_24_out, and_25_out, and_26_out, and_27_out);
endmodule

module AnotherBrickInTheWall (
  input  Input_1,
  input  Input_2,
  input  Input_3,
  input  Input_4,
  input  Input_5,
  input  Input_6,
  input  Input_7,
  input  Input_8,
  output d2,
  output c2,
  output a1,
  output e1,
  output reset
);

  wire and_1_out, and_2_out, and_3_out, and_4_out, and_5_out, and_6_out, and_7_out, and_8_out, and_9_out,
       and_10_out, and_11_out, and_12_out, and_15_out, and_16_out, and_17_out, and_18_out, not_1_out,
       not_2_out, not_3_out, not_4_out, not_5_out, not_6_out, not_7_out, not_8_out, not_9_out, not_10_out,
       not_11_out, not_12_out, not_13_out, not_14_out, not_15_out, not_16_out, not_17_out, not_18_out,
       not_19_out, not_20_out, not_21_out, not_22_out, not_23_out, not_24_out, not_25_out, not_26_out,
       not_27_out, not_28_out, not_29_out, not_30_out, not_31_out, not_32_out, not_33_out, not_34_out,
       not_35_out, not_36_out, not_37_out, not_38_out, not_39_out, not_40_out, not_41_out, not_42_out,
       not_43_out, not_44_out;

  not not_1 (not_1_out, Input_4);
  not not_2 (not_2_out, Input_6);
  not not_3 (not_3_out, Input_1);
  not not_4 (not_4_out, Input_2);
  not not_5 (not_5_out, Input_3);
  not not_6 (not_6_out, Input_4);
  not not_7 (not_7_out, Input_7);
  not not_8 (not_8_out, Input_8);
  not not_9 (not_9_out, Input_5);
  not not_10 (not_10_out, Input_6);
  not not_11 (not_11_out, Input_5);
  not not_12 (not_12_out, Input_1);
  not not_13 (not_13_out, Input_2);
  not not_14 (not_14_out, Input_5);
  not not_15 (not_15_out, Input_6);
  not not_16 (not_16_out, Input_7);
  not not_17 (not_17_out, Input_4);
  not not_18 (not_18_out, Input_5);
  not not_19 (not_19_out, Input_1);
  not not_20 (not_20_out, Input_2);
  not not_21 (not_21_out, Input_3);
  not not_22 (not_22_out, Input_4);
  not not_23 (not_23_out, Input_6);
  not not_24 (not_24_out, Input_7);
  not not_25 (not_25_out, Input_7);
  not not_26 (not_26_out, Input_8);
  not not_27 (not_27_out, Input_4);
  not not_28 (not_28_out, Input_5);
  not not_29 (not_29_out, Input_4);
  not not_30 (not_30_out, Input_5);
  not not_31 (not_31_out, Input_4);
  not not_32 (not_32_out, Input_5);
  not not_33 (not_33_out, Input_6);
  not not_34 (not_34_out, Input_3);
  not not_35 (not_35_out, Input_4);
  not not_36 (not_36_out, Input_5);
  not not_37 (not_37_out, Input_6);
  not not_38 (not_38_out, Input_1);
  not not_39 (not_39_out, Input_2);
  not not_40 (not_40_out, Input_4);
  not not_41 (not_41_out, Input_5);
  not not_42 (not_42_out, Input_6);
  not not_43 (not_43_out, Input_7);
  not not_44 (not_44_out, Input_8);
  and and_1 (and_1_out, not_1_out, Input_5, not_2_out, Input_7);
  and and_2 (and_2_out, not_3_out, not_4_out, not_5_out, not_6_out, Input_5, Input_6, not_7_out, not_8_out);
  and and_3 (and_3_out, Input_4, not_9_out, not_10_out);
  and and_4 (and_4_out, Input_4, not_11_out, Input_7);
  and and_5 (and_5_out, not_12_out, not_13_out, Input_3, not_14_out, not_15_out, not_16_out, Input_8);
  and and_6 (and_6_out, not_17_out, not_18_out, Input_6, Input_7, Input_8);
  and and_7 (and_7_out, not_19_out, not_20_out, not_21_out, not_22_out, Input_5, not_23_out, not_24_out);
  and and_8 (and_8_out, Input_4, Input_5, Input_6, not_25_out);
  and and_9 (and_9_out, Input_4, Input_5, Input_6, not_26_out);
  and and_10 (and_10_out, Input_3, not_27_out, not_28_out, Input_6, Input_7);
  and and_11 (and_11_out, Input_2, not_29_out, not_30_out, Input_6, Input_7);
  and and_12 (and_12_out, Input_1, not_31_out, not_32_out, Input_6, Input_7);
  and and_13 (a1, Input_4, Input_5, not_33_out);
  and and_14 (e1, not_34_out, not_35_out, not_36_out, not_37_out);
  and and_15 (and_15_out, not_38_out, not_39_out, Input_3, not_40_out, not_41_out, not_42_out, not_43_out, not_44_out);
  and and_16 (and_16_out, Input_3, Input_4, Input_5, Input_6, Input_7, Input_8);
  and and_17 (and_17_out, Input_2, Input_4, Input_5, Input_6, Input_7, Input_8);
  and and_18 (and_18_out, Input_1, Input_4, Input_5, Input_6, Input_7, Input_8);
  or or_1 (d2, and_1_out, and_2_out, and_3_out, and_4_out, and_5_out);
  or or_2 (c2, and_6_out, and_7_out, and_8_out, and_9_out, and_10_out, and_11_out, and_12_out);
  or or_3 (reset, and_15_out, and_16_out, and_17_out, and_18_out);
endmodule

module RappersDelight (
  input  Input_1,
  input  Input_2,
  input  Input_3,
  input  Input_4,
  input  Input_5,
  input  Input_6,
  input  Input_7,
  input  Input_8,
  output c3,
  output b2,
  output a2,
  output g2,
  output e2,
  output d2,
  output c2,
  output b1,
  output a1,
  output reset
);

  wire and_2_out, and_3_out, and_6_out, and_7_out, and_8_out, and_9_out, and_10_out, and_11_out, and_12_out,
       and_13_out, and_14_out, and_15_out, and_16_out, and_17_out, and_18_out, and_19_out, and_20_out,
       and_21_out, and_22_out, and_23_out, not_1_out, not_2_out, not_3_out, not_4_out, not_5_out, not_6_out,
       not_7_out, not_8_out, not_9_out, not_10_out, not_11_out, not_12_out, not_13_out, not_14_out,
       not_15_out, not_16_out, not_17_out, not_18_out, not_19_out, not_20_out, not_21_out, not_22_out,
       not_23_out, not_24_out, not_25_out, not_26_out, not_27_out, not_28_out, not_29_out, not_30_out,
       not_31_out, not_32_out, not_33_out, not_34_out, not_35_out, not_36_out, not_37_out, not_38_out,
       not_39_out, not_40_out, not_41_out, not_42_out, not_43_out, not_44_out, not_45_out, not_46_out,
       not_47_out, not_48_out, not_49_out, not_50_out, not_51_out, not_52_out, not_53_out, not_54_out,
       not_55_out, not_56_out;

  not not_1 (not_1_out, Input_5);
  not not_2 (not_2_out, Input_7);
  not not_3 (not_3_out, Input_5);
  not not_4 (not_4_out, Input_5);
  not not_5 (not_5_out, Input_3);
  not not_6 (not_6_out, Input_8);
  not not_7 (not_7_out, Input_3);
  not not_8 (not_8_out, Input_7);
  not not_9 (not_9_out, Input_3);
  not not_10 (not_10_out, Input_6);
  not not_11 (not_11_out, Input_8);
  not not_12 (not_12_out, Input_5);
  not not_13 (not_13_out, Input_6);
  not not_14 (not_14_out, Input_8);
  not not_15 (not_15_out, Input_3);
  not not_16 (not_16_out, Input_5);
  not not_17 (not_17_out, Input_3);
  not not_18 (not_18_out, Input_4);
  not not_19 (not_19_out, Input_5);
  not not_20 (not_20_out, Input_7);
  not not_21 (not_21_out, Input_6);
  not not_22 (not_22_out, Input_7);
  not not_23 (not_23_out, Input_4);
  not not_24 (not_24_out, Input_8);
  not not_25 (not_25_out, Input_6);
  not not_26 (not_26_out, Input_7);
  not not_27 (not_27_out, Input_6);
  not not_28 (not_28_out, Input_7);
  not not_29 (not_29_out, Input_3);
  not not_30 (not_30_out, Input_5);
  not not_31 (not_31_out, Input_7);
  not not_32 (not_32_out, Input_8);
  not not_33 (not_33_out, Input_3);
  not not_34 (not_34_out, Input_5);
  not not_35 (not_35_out, Input_6);
  not not_36 (not_36_out, Input_2);
  not not_37 (not_37_out, Input_3);
  not not_38 (not_38_out, Input_4);
  not not_39 (not_39_out, Input_5);
  not not_40 (not_40_out, Input_7);
  not not_41 (not_41_out, Input_2);
  not not_42 (not_42_out, Input_3);
  not not_43 (not_43_out, Input_4);
  not not_44 (not_44_out, Input_6);
  not not_45 (not_45_out, Input_7);
  not not_46 (not_46_out, Input_8);
  not not_47 (not_47_out, Input_2);
  not not_48 (not_48_out, Input_3);
  not not_49 (not_49_out, Input_5);
  not not_50 (not_50_out, Input_6);
  not not_51 (not_51_out, Input_7);
  not not_52 (not_52_out, Input_2);
  not not_53 (not_53_out, Input_3);
  not not_54 (not_54_out, Input_4);
  not not_55 (not_55_out, Input_6);
  not not_56 (not_56_out, Input_7);
  and and_1 (c3, Input_3, Input_4, not_1_out, Input_6, not_2_out);
  and and_2 (and_2_out, Input_3, Input_4, not_3_out, Input_7, Input_8);
  and and_3 (and_3_out, Input_3, Input_4, not_4_out, Input_6, Input_7);
  and and_4 (a2, not_5_out, Input_4, Input_5, Input_6, Input_7, not_6_out);
  and and_5 (g2, not_7_out, Input_4, Input_5, Input_6, not_8_out);
  and and_6 (and_6_out, not_9_out, Input_4, Input_5, not_10_out, not_11_out);
  and and_7 (and_7_out, Input_3, Input_4, not_12_out, not_13_out, Input_7, not_14_out);
  and and_8 (and_8_out, not_15_out, Input_4, not_16_out, Input_6, Input_7);
  and and_9 (and_9_out, not_17_out, Input_4, Input_6, Input_7, Input_8);
  and and_10 (and_10_out, Input_3, not_18_out, not_19_out, Input_6, not_20_out);
  and and_11 (and_11_out, Input_3, Input_5, not_21_out, not_22_out);
  and and_12 (and_12_out, Input_3, not_23_out, Input_5, Input_6, Input_7, not_24_out);
  and and_13 (and_13_out, Input_3, Input_4, not_25_out, not_26_out);
  and and_14 (and_14_out, Input_3, Input_4, Input_5, not_27_out, Input_8);
  and and_15 (and_15_out, Input_3, Input_4, Input_5, not_28_out, Input_8);
  and and_16 (and_16_out, not_29_out, Input_4, not_30_out, Input_6, not_31_out);
  and and_17 (and_17_out, Input_3, Input_4, Input_5, Input_6, Input_7, not_32_out);
  and and_18 (and_18_out, not_33_out, Input_4, not_34_out, not_35_out, Input_7);
  and and_19 (and_19_out, Input_3, Input_4, Input_5, Input_6, Input_7, Input_8);
  and and_20 (and_20_out, not_36_out, not_37_out, not_38_out, not_39_out, not_40_out);
  and and_21 (and_21_out, not_41_out, not_42_out, not_43_out, not_44_out, not_45_out, not_46_out);
  and and_22 (and_22_out, not_47_out, not_48_out, not_49_out, not_50_out, not_51_out);
  and and_23 (and_23_out, Input_1, not_52_out, not_53_out, not_54_out, not_55_out, not_56_out);
  or or_1 (b2, and_2_out, and_3_out);
  or or_2 (e2, and_6_out, and_7_out);
  or or_3 (d2, and_8_out, and_9_out, and_10_out, and_11_out, and_12_out, and_13_out, and_14_out, and_15_out);
  or or_4 (c2, and_16_out, and_17_out);
  or or_5 (b1, and_18_out, and_19_out);
  or or_6 (a1, and_20_out, and_21_out, and_22_out, and_23_out);

  assign reset = Input_2;
endmodule

module SongName (
  input  [2:0] songcode,
  output [7:0] L1,
  output [7:0] L2,
  output [7:0] L3,
  output [7:0] L4,
  output [7:0] L5,
  output [7:0] L6
);

  wire [5:0] Let1_w, Let2_w, Let3_w, Let4_w, Let5_w, Let6_w;

  Letter1_song Let1 (
    .a(songcode[2]), .b(songcode[1]), .c(songcode[0]), .x(Let1_w[5]), .y(Let1_w[4]), .z(Let1_w[3]),
    .u(Let1_w[2]), .v(Let1_w[1]), .w(Let1_w[0]));
  Letter2_song Let2 (
    .a(songcode[2]), .b(songcode[1]), .c(songcode[0]), .x(Let2_w[5]), .y(Let2_w[4]), .z(Let2_w[3]),
    .u(Let2_w[2]), .v(Let2_w[1]), .w(Let2_w[0]));
  Letter3_song Let3 (
    .a(songcode[2]), .b(songcode[1]), .c(songcode[0]), .x(Let3_w[5]), .y(Let3_w[4]), .z(Let3_w[3]),
    .u(Let3_w[2]), .v(Let3_w[1]), .w(Let3_w[0]));
  Letter4_song Let4 (
    .a(songcode[2]), .b(songcode[1]), .c(songcode[0]), .x(Let4_w[5]), .y(Let4_w[4]), .z(Let4_w[3]),
    .u(Let4_w[2]), .v(Let4_w[1]), .w(Let4_w[0]));
  Letter5_song Let5 (
    .a(songcode[2]), .b(songcode[1]), .c(songcode[0]), .x(Let5_w[5]), .y(Let5_w[4]), .z(Let5_w[3]),
    .u(Let5_w[2]), .v(Let5_w[1]), .w(Let5_w[0]));
  Letter6_song Let6 (
    .a(songcode[2]), .b(songcode[1]), .c(songcode[0]), .x(Let6_w[5]), .y(Let6_w[4]), .z(Let6_w[3]),
    .u(Let6_w[2]), .v(Let6_w[1]), .w(Let6_w[0]));
  assign L1 = {{2{1'b0}}, Let1_w};  // Bit_Extender bit_extender_1
  assign L2 = {{2{1'b0}}, Let2_w};  // Bit_Extender bit_extender_2
  assign L3 = {{2{1'b0}}, Let3_w};  // Bit_Extender bit_extender_3
  assign L4 = {{2{1'b0}}, Let4_w};  // Bit_Extender bit_extender_4
  assign L5 = {{2{1'b0}}, Let5_w};  // Bit_Extender bit_extender_5
  assign L6 = {{2{1'b0}}, Let6_w};  // Bit_Extender bit_extender_6
endmodule

module Letter1_song (
  input  a,
  input  b,
  input  c,
  output x,
  output y,
  output z,
  output u,
  output v,
  output w
);

  wire and_1_out, and_2_out, and_3_out, and_4_out, and_5_out, and_6_out, and_7_out, and_8_out, not_1_out,
       not_2_out, not_3_out, not_4_out, not_5_out, not_6_out, not_7_out, not_8_out, not_9_out, not_10_out,
       not_11_out, not_12_out;

  not not_1 (not_1_out, c);
  not not_2 (not_2_out, b);
  not not_3 (not_3_out, c);
  not not_4 (not_4_out, a);
  not not_5 (not_5_out, c);
  not not_6 (not_6_out, b);
  not not_7 (not_7_out, a);
  not not_8 (not_8_out, b);
  not not_9 (not_9_out, a);
  not not_10 (not_10_out, b);
  not not_11 (not_11_out, c);
  not not_12 (not_12_out, b);
  and and_1 (and_1_out, a, not_1_out);
  or or_1 (x, and_1_out, and_2_out);
  and and_2 (and_2_out, a, b);
  or or_2 (y, not_2_out, c, a);
  or or_3 (z, not_3_out, b);
  and and_3 (and_3_out, not_4_out, not_5_out);
  or or_4 (u, and_3_out, and_4_out);
  and and_4 (and_4_out, a, not_6_out);
  and and_5 (and_5_out, not_7_out, not_8_out);
  or or_5 (v, and_5_out, and_6_out);
  and and_6 (and_6_out, a, b, c);
  and and_7 (and_7_out, not_9_out, not_10_out, not_11_out);
  or or_6 (w, and_7_out, and_8_out);
  and and_8 (and_8_out, a, not_12_out, c);
endmodule

module Letter2_song (
  input  a,
  input  b,
  input  c,
  output x,
  output y,
  output z,
  output u,
  output v,
  output w
);

  wire and_2_out, and_3_out, and_4_out, and_5_out, and_6_out, and_7_out, and_8_out, and_9_out, and_10_out,
       and_11_out, and_12_out, and_13_out, and_14_out, not_1_out, not_2_out, not_3_out, not_4_out, not_5_out,
       not_6_out, not_7_out, not_8_out, not_9_out, not_10_out, not_11_out, not_12_out, not_13_out,
       not_14_out, not_15_out, not_16_out, not_17_out;

  not not_1 (not_1_out, b);
  not not_2 (not_2_out, c);
  not not_3 (not_3_out, a);
  not not_4 (not_4_out, a);
  not not_5 (not_5_out, c);
  not not_6 (not_6_out, a);
  not not_7 (not_7_out, b);
  not not_8 (not_8_out, c);
  not not_9 (not_9_out, a);
  not not_10 (not_10_out, c);
  not not_11 (not_11_out, a);
  not not_12 (not_12_out, c);
  not not_13 (not_13_out, b);
  not not_14 (not_14_out, a);
  not not_15 (not_15_out, b);
  not not_16 (not_16_out, c);
  and and_1 (x, a, not_1_out, not_2_out);
  not not_17 (not_17_out, b);
  or or_1 (y, not_17_out, and_2_out);
  and and_2 (and_2_out, not_3_out, c);
  and and_3 (and_3_out, not_4_out, not_5_out);
  or or_2 (z, and_3_out, and_4_out);
  and and_4 (and_4_out, a, b);
  and and_5 (and_5_out, not_6_out, not_7_out);
  and and_6 (and_6_out, b, c);
  or or_3 (u, and_5_out, and_6_out, and_7_out);
  and and_7 (and_7_out, a, not_8_out);
  and and_8 (and_8_out, not_9_out, not_10_out);
  and and_9 (and_9_out, not_11_out, b);
  and and_10 (and_10_out, b, not_12_out);
  and and_11 (and_11_out, a, not_13_out, c);
  and and_12 (and_12_out, not_14_out, not_15_out);
  and and_13 (and_13_out, b, c);
  or or_4 (w, and_12_out, and_13_out, and_14_out);
  and and_14 (and_14_out, a, not_16_out);
  or or_5 (v, and_8_out, and_9_out, and_10_out, and_11_out);
endmodule

module Letter3_song (
  input  a,
  input  b,
  input  c,
  output x,
  output y,
  output z,
  output u,
  output v,
  output w
);

  wire and_2_out, and_3_out, and_4_out, and_5_out, and_6_out, and_7_out, and_8_out, and_9_out, not_1_out,
       not_2_out, not_3_out, not_4_out, not_5_out, not_6_out, not_7_out, not_8_out, not_9_out, not_10_out,
       not_11_out, not_12_out, not_13_out, not_14_out;

  not not_1 (not_1_out, b);
  not not_2 (not_2_out, c);
  not not_3 (not_3_out, a);
  not not_4 (not_4_out, b);
  not not_5 (not_5_out, b);
  not not_6 (not_6_out, c);
  not not_7 (not_7_out, b);
  not not_8 (not_8_out, a);
  not not_9 (not_9_out, c);
  not not_10 (not_10_out, b);
  not not_11 (not_11_out, c);
  not not_12 (not_12_out, b);
  not not_13 (not_13_out, c);
  not not_14 (not_14_out, b);
  and and_1 (x, a, not_1_out, not_2_out);
  and and_2 (and_2_out, not_3_out, not_4_out);
  and and_3 (and_3_out, not_5_out, c);
  or or_1 (y, and_2_out, and_3_out, and_4_out);
  and and_4 (and_4_out, b, not_6_out);
  or or_2 (z, not_7_out, c);
  and and_5 (and_5_out, not_8_out, not_9_out);
  or or_3 (u, and_5_out, b);
  and and_6 (and_6_out, not_10_out, not_11_out);
  or or_4 (v, and_6_out, and_7_out);
  and and_7 (and_7_out, a, c);
  and and_8 (and_8_out, not_12_out, not_13_out);
  or or_5 (w, and_8_out, and_9_out);
  and and_9 (and_9_out, a, not_14_out);
endmodule

module Letter4_song (
  input  a,
  input  b,
  input  c,
  output x,
  output y,
  output z,
  output u,
  output v,
  output w
);

  wire and_1_out, and_2_out, and_3_out, and_4_out, and_5_out, and_6_out, and_7_out, and_8_out, and_9_out,
       and_10_out, and_11_out, and_12_out, and_13_out, and_14_out, and_15_out, and_16_out, not_1_out,
       not_2_out, not_3_out, not_4_out, not_5_out, not_6_out, not_7_out, not_8_out, not_9_out, not_10_out,
       not_11_out, not_12_out, not_13_out, not_14_out, not_15_out, not_16_out, not_17_out, not_18_out,
       not_19_out;

  not not_1 (not_1_out, b);
  not not_2 (not_2_out, c);
  not not_3 (not_3_out, b);
  not not_4 (not_4_out, c);
  not not_5 (not_5_out, a);
  not not_6 (not_6_out, b);
  not not_7 (not_7_out, a);
  not not_8 (not_8_out, b);
  not not_9 (not_9_out, c);
  not not_10 (not_10_out, a);
  not not_11 (not_11_out, c);
  not not_12 (not_12_out, a);
  not not_13 (not_13_out, c);
  not not_14 (not_14_out, b);
  not not_15 (not_15_out, a);
  not not_16 (not_16_out, b);
  not not_17 (not_17_out, a);
  not not_18 (not_18_out, b);
  not not_19 (not_19_out, c);
  and and_1 (and_1_out, a, not_1_out, not_2_out);
  or or_1 (x, and_1_out, and_2_out);
  and and_2 (and_2_out, a, b, c);
  and and_3 (and_3_out, not_3_out, not_4_out);
  or or_2 (z, and_3_out, and_4_out, and_5_out);
  and and_4 (and_4_out, not_5_out, b, c);
  and and_5 (and_5_out, a, not_6_out);
  and and_6 (and_6_out, not_7_out, not_8_out);
  or or_3 (u, and_6_out, and_7_out, and_8_out);
  and and_7 (and_7_out, b, c);
  and and_8 (and_8_out, a, not_9_out);
  and and_9 (and_9_out, not_10_out, not_11_out);
  and and_10 (and_10_out, not_12_out, b);
  and and_11 (and_11_out, b, not_13_out);
  and and_12 (and_12_out, a, not_14_out, c);
  and and_13 (and_13_out, not_15_out, not_16_out);
  and and_14 (and_14_out, not_17_out, c);
  and and_15 (and_15_out, not_18_out, c);
  and and_16 (and_16_out, a, b, not_19_out);
  or or_4 (v, and_9_out, and_10_out, and_11_out, and_12_out);
  or or_5 (w, and_13_out, and_14_out, and_15_out, and_16_out);

  assign y = 1'b1;
endmodule

module Letter5_song (
  input  a,
  input  b,
  input  c,
  output x,
  output y,
  output z,
  output u,
  output v,
  output w
);

  wire and_2_out, not_1_out, not_2_out, not_3_out, not_4_out, not_5_out, not_6_out, not_7_out;

  not not_1 (not_1_out, b);
  not not_2 (not_2_out, c);
  not not_3 (not_3_out, b);
  not not_4 (not_4_out, a);
  not not_5 (not_5_out, a);
  not not_6 (not_6_out, a);
  not not_7 (not_7_out, b);
  and and_1 (x, a, not_1_out, not_2_out);
  or or_1 (z, not_3_out, c, a);
  or or_2 (u, not_4_out, c, b);
  or or_3 (v, not_5_out, c, b);
  and and_2 (and_2_out, not_6_out, not_7_out);
  or or_4 (w, and_2_out, c);

  assign y = 1'b1;
endmodule

module Letter6_song (
  input  a,
  input  b,
  input  c,
  output x,
  output y,
  output z,
  output u,
  output v,
  output w
);

  wire and_1_out, and_2_out, and_3_out, not_1_out, not_2_out, not_3_out, not_4_out, not_5_out, not_6_out;

  not not_1 (not_1_out, b);
  not not_2 (not_2_out, a);
  not not_3 (not_3_out, b);
  not not_4 (not_4_out, b);
  not not_5 (not_5_out, c);
  not not_6 (not_6_out, b);
  or or_1 (y, not_1_out, c);
  and and_1 (and_1_out, not_2_out, not_3_out);
  and and_2 (and_2_out, not_4_out, not_5_out);
  or or_2 (v, and_1_out, and_2_out, and_3_out);
  and and_3 (and_3_out, b, c);
  or or_3 (w, not_6_out, c, a);

  assign u = 1'b1;
  assign x = 1'b0;
  assign z = 1'b1;
endmodule
