// Logisim project TIMER.circ as structural Verilog: 10 circuits, main circuit timerFSM
module timerFSM (
  input  RESET,
  input  [1:0] B1_B0,
  input  DIP,
  input  ChM,
  input  CLK32k,
  input  CLK2k,
  input  CLK4,
  output [7:0] sevsegCode_5,
  output [7:0] sevsegCode_4,
  output [7:0] sevsegCode_3,
  output [7:0] sevsegCode_2,
  output [7:0] sevsegCode_1,
  output [7:0] sevsegCode_0
);

  wire and_1_out, and_2_out, and_3_out, and_4_out, changeTimer_1_hloadtendi, changeTimer_1_hloaduendi,
       changeTimer_1_minloadtendi, changeTimer_1_minloaduendi, changeTimer_1_secloadtendi,
       changeTimer_1_secloaduendi, counter_1_carry, d_ff_1_q, d_ff_2_q, d_ff_3_q, d_ff_4_q, d_ff_4_qn,
       fsm_1_q0, fsm_1_q1, fsm_1_q2, or_1_out, or_2_out, TIMER_1_finished, TIMER_1_hloadt, TIMER_1_hloadu,
       TIMER_1_minloadt, TIMER_1_minloadu, TIMER_1_secloadt, TIMER_1_secloadu, TransitLogic_1_reset,
       TransitLogic_1_setup, TransitLogic_1_start;
  wire [3:0] changeTimer_1_hloadt_4, changeTimer_1_hloadu_4, changeTimer_1_minloadt_4,
       changeTimer_1_minloadu_4, changeTimer_1_secloadt_4, changeTimer_1_secloadu_4, TIMER_1_ht_4,
       TIMER_1_hu_4, TIMER_1_mint_4, TIMER_1_minu_4, TIMER_1_sect_4, TIMER_1_secu_4;

  and and_1 (and_1_out, B1_B0[1], ~ChM);  // AND_Gate
  and and_2 (and_2_out, B1_B0[0], ~ChM);  // AND_Gate
  fsm fsm_1 (
    .finish(TIMER_1_finished), .D2(d_ff_3_q), .D1(d_ff_2_q), .D0(d_ff_1_q), .DIP(DIP), .B1(and_1_out),
    .B0(and_2_out), .Q2(fsm_1_q2), .Q1(fsm_1_q1), .Q0(fsm_1_q0));
  D_Flip_Flop d_ff_1 (.D(fsm_1_q0), .clk(CLK32k), .Q(d_ff_1_q), .reset(RESET));  // open: Qn, preset
  D_Flip_Flop d_ff_2 (.D(fsm_1_q1), .clk(CLK32k), .Q(d_ff_2_q), .reset(RESET));  // open: Qn, preset
  D_Flip_Flop d_ff_3 (.D(fsm_1_q2), .clk(CLK32k), .Q(d_ff_3_q), .reset(RESET));  // open: Qn, preset
  TransitLogic TransitLogic_1 (
    .Q2(d_ff_3_q), .Q1(d_ff_2_q), .Q0(d_ff_1_q), .START(TransitLogic_1_start), .RESET(TransitLogic_1_reset),
    .SETUP(TransitLogic_1_setup));
  and and_3 (and_3_out, TransitLogic_1_start, ~TIMER_1_finished);  // AND_Gate
  changeTimer changeTimer_1 (
    .DIP(TransitLogic_1_setup), .B1_B0(B1_B0), .CLK32k(CLK32k), .RESET(RESET),
    .HloadT_4(changeTimer_1_hloadt_4), .HloadTEnDi(changeTimer_1_hloadtendi),
    .HloadU_4(changeTimer_1_hloadu_4), .HloadUEnDi(changeTimer_1_hloaduendi),
    .MINloadT_4(changeTimer_1_minloadt_4), .MINloadTEnDi(changeTimer_1_minloadtendi),
    .MINloadU_4(changeTimer_1_minloadu_4), .MINloadUEnDi(changeTimer_1_minloaduendi),
    .SECloadT_4(changeTimer_1_secloadt_4), .SECloadTEnDi(changeTimer_1_secloadtendi),
    .SECloadU_4(changeTimer_1_secloadu_4), .SECloadUEnDi(changeTimer_1_secloaduendi));
  or or_1 (or_1_out, TransitLogic_1_reset, RESET);
  and and_4 (and_4_out, TransitLogic_1_start, TIMER_1_finished);
  TIMER TIMER_1 (
    .START(and_3_out), .RESET(or_1_out), .CLK2k(CLK2k), .HloadT_4(changeTimer_1_hloadt_4),
    .HloadTEnDi(changeTimer_1_hloadtendi), .HloadU_4(changeTimer_1_hloadu_4),
    .HloadUEnDi(changeTimer_1_hloaduendi), .MINloadT_4(changeTimer_1_minloadt_4),
    .MINloadTEnDi(changeTimer_1_minloadtendi), .MINloadU_4(changeTimer_1_minloadu_4),
    .MINloadUEnDi(changeTimer_1_minloaduendi), .SECloadT_4(changeTimer_1_secloadt_4),
    .SECloadTEnDi(changeTimer_1_secloadtendi), .SECloadU_4(changeTimer_1_secloadu_4),
    .SECloadUEnDi(changeTimer_1_secloaduendi), .HT_4(TIMER_1_ht_4), .HU_4(TIMER_1_hu_4),
    .MINT_4(TIMER_1_mint_4), .MINU_4(TIMER_1_minu_4), .SECT_4(TIMER_1_sect_4), .SECU_4(TIMER_1_secu_4),
    .HloadT(TIMER_1_hloadt), .HloadU(TIMER_1_hloadu), .MINloadT(TIMER_1_minloadt),
    .MINloadU(TIMER_1_minloadu), .SECloadT(TIMER_1_secloadt), .SECloadU(TIMER_1_secloadu),
    .finished(TIMER_1_finished));
  timerView timerView_1 (
    .HT_4(TIMER_1_ht_4), .HU_4(TIMER_1_hu_4), .MINT_4(TIMER_1_mint_4), .MINU_4(TIMER_1_minu_4),
    .SECT_4(TIMER_1_sect_4), .SECU_4(TIMER_1_secu_4), .HloadT(TIMER_1_hloadt), .HloadU(TIMER_1_hloadu),
    .MINloadT(TIMER_1_minloadt), .MINloadU(TIMER_1_minloadu), .SECloadT(TIMER_1_secloadt),
    .SECloadU(TIMER_1_secloadu), .RESET(TransitLogic_1_reset), .CLK4(CLK4), .sevsegCode_5(sevsegCode_5),
    .sevsegCode_4(sevsegCode_4), .sevsegCode_3(sevsegCode_3), .sevsegCode_2(sevsegCode_2),
    .sevsegCode_1(sevsegCode_1), .sevsegCode_0(sevsegCode_0));
  D_Flip_Flop d_ff_4 (
    .D(d_ff_4_qn), .clk(and_4_out), .Q(d_ff_4_q), .Qn(d_ff_4_qn), .reset(counter_1_carry));  // open: preset
  or or_2 (or_2_out, RESET, counter_1_carry);
  LED LED_1 (.in(d_ff_4_q));
  Counter #(.width(5), .max('h1f)) counter_1 (
    .clr(or_2_out), .count(d_ff_4_q), .clk(CLK4), .carry(counter_1_carry));  // open: load, up, D, Q
endmodule

module TIMER (
  input  START,
  input  RESET,
  input  CLK2k,
  input  [3:0] HloadT_4,
  input  HloadTEnDi,
  input  [3:0] HloadU_4,
  input  HloadUEnDi,
  input  [3:0] MINloadT_4,
  input  MINloadTEnDi,
  input  [3:0] MINloadU_4,
  input  MINloadUEnDi,
  input  [3:0] SECloadT_4,
  input  SECloadTEnDi,
  input  [3:0] SECloadU_4,
  input  SECloadUEnDi,
  output [3:0] HT_4,
  output [3:0] HU_4,
  output [3:0] MINT_4,
  output [3:0] MINU_4,
  output [3:0] SECT_4,
  output [3:0] SECU_4,
  output HloadT,
  output HloadU,
  output MINloadT,
  output MINloadU,
  output SECloadT,
  output SECloadU,
  output finished
);

  wire clk2k_to_ticksec_timer_1_ticksec, FiftyNineZero_1_finished, FiftyNineZero_2_finished,
       FiftyNineZero_2_tickout, FiftyNineZero_3_finished, FiftyNineZero_3_tickout;

  clk2k_to_ticksec_timer clk2k_to_ticksec_timer_1 (
    .START(START), .RESET(RESET), .CLK2k(CLK2k), .TickSEC(clk2k_to_ticksec_timer_1_ticksec));
  FiftyNineZero FiftyNineZero_1 (
    .TickIn(FiftyNineZero_2_tickout), .loadT_4(HloadT_4), .loadTEnDi(HloadTEnDi), .loadU_4(HloadU_4),
    .loadUEnDi(HloadUEnDi), .RESET(RESET), .CLK2K(CLK2k), .curT_3(HT_4), .curU_4(HU_4),
    .finished(FiftyNineZero_1_finished));  // open: TickOut
  FiftyNineZero FiftyNineZero_2 (
    .TickIn(FiftyNineZero_3_tickout), .loadT_4(MINloadT_4), .loadTEnDi(MINloadTEnDi), .loadU_4(MINloadU_4),
    .loadUEnDi(MINloadUEnDi), .RESET(RESET), .CLK2K(CLK2k), .TickOut(FiftyNineZero_2_tickout),
    .curT_3(MINT_4), .curU_4(MINU_4), .finished(FiftyNineZero_2_finished));
  FiftyNineZero FiftyNineZero_3 (
    .TickIn(clk2k_to_ticksec_timer_1_ticksec), .loadT_4(SECloadT_4), .loadTEnDi(SECloadTEnDi),
    .loadU_4(SECloadU_4), .loadUEnDi(SECloadUEnDi), .RESET(RESET), .CLK2K(CLK2k),
    .TickOut(FiftyNineZero_3_tickout), .curT_3(SECT_4), .curU_4(SECU_4), .finished(FiftyNineZero_3_finished));
  and and_1 (finished, FiftyNineZero_1_finished, FiftyNineZero_2_finished, FiftyNineZero_3_finished);

  assign HloadT = HloadTEnDi;
  assign HloadU = HloadUEnDi;
  assign MINloadT = MINloadTEnDi;
  assign MINloadU = MINloadUEnDi;
  assign SECloadT = SECloadTEnDi;
  assign SECloadU = SECloadUEnDi;
endmodule

module TransitLogic (
  input  Q2,
  input  Q1,
  input  Q0,
  output START,
  output RESET,
  output SETUP
);

  wire not_1_out;

  not not_1 (not_1_out, Q1);
  and and_1 (RESET, Q1, Q0);
  and and_2 (START, not_1_out, Q0);

  assign SETUP = Q2;
endmodule

module fsm (
  input  finish,
  input  D2,
  input  D1,
  input  D0,
  input  DIP,
  input  B1,
  input  B0,
  output Q2,
  output Q1,
  output Q0
);

  wire and_1_out, and_2_out, and_3_out, and_4_out, and_5_out, and_6_out, and_7_out, and_8_out, and_9_out,
       and_10_out, and_11_out, and_12_out, and_13_out, and_14_out, not_1_out, not_2_out, not_3_out,
       not_4_out, not_5_out, not_6_out, not_7_out, not_8_out, not_9_out, not_10_out, not_11_out, not_12_out,
       not_13_out, not_14_out, not_15_out, not_16_out, not_17_out, not_18_out, not_19_out, not_20_out,
       not_21_out, not_22_out, not_23_out, not_24_out, not_25_out, not_26_out, not_27_out, not_28_out,
       not_29_out, not_30_out, not_31_out, not_32_out, not_33_out, not_34_out, not_35_out, not_36_out;

  not not_1 (not_1_out, finish);
  not not_2 (not_2_out, D1);
  not not_3 (not_3_out, finish);
  not not_4 (not_4_out, D0);
  not not_5 (not_5_out, D1);
  not not_6 (not_6_out, D0);
  not not_7 (not_7_out, D2);
  not not_8 (not_8_out, D1);
  not not_9 (not_9_out, DIP);
  not not_10 (not_10_out, B0);
  not not_11 (not_11_out, D2);
  not not_12 (not_12_out, D0);
  not not_13 (not_13_out, DIP);
  not not_14 (not_14_out, B0);
  not not_15 (not_15_out, D2);
  not not_16 (not_16_out, D0);
  not not_17 (not_17_out, DIP);
  not not_18 (not_18_out, D2);
  not not_19 (not_19_out, D0);
  not not_20 (not_20_out, D2);
  not not_21 (not_21_out, D0);
  not not_22 (not_22_out, DIP);
  not not_23 (not_23_out, B1);
  not not_24 (not_24_out, D2);
  not not_25 (not_25_out, D1);
  not not_26 (not_26_out, DIP);
  not not_27 (not_27_out, B1);
  not not_28 (not_28_out, D2);
  not not_29 (not_29_out, D1);
  not not_30 (not_30_out, DIP);
  not not_31 (not_31_out, D2);
  not not_32 (not_32_out, D0);
  not not_33 (not_33_out, DIP);
  not not_34 (not_34_out, B0);
  and and_1 (and_1_out, not_1_out, not_2_out, DIP);
  and and_2 (and_2_out, not_3_out, not_4_out, DIP);
  and and_3 (and_3_out, not_5_out, not_6_out, DIP);
  and and_4 (and_4_out, D2, DIP);
  and and_5 (and_5_out, not_7_out, not_8_out, D0, not_9_out, B1, not_10_out);
  and and_6 (and_6_out, not_11_out, D1, not_12_out, not_13_out, not_14_out);
  and and_7 (and_7_out, not_15_out, D1, not_16_out, not_17_out, B1);
  not not_35 (not_35_out, D1);
  and and_8 (and_8_out, finish, not_35_out, D0);
  and and_9 (and_9_out, finish, not_18_out, D1, not_19_out, DIP);
  and and_10 (and_10_out, not_20_out, not_21_out, not_22_out, not_23_out, B0);
  and and_11 (and_11_out, not_24_out, not_25_out, D0, not_26_out, not_27_out);
  and and_12 (and_12_out, not_28_out, not_29_out, D0, not_30_out, B0);
  and and_13 (and_13_out, not_31_out, D1, not_32_out, not_33_out, B1, not_34_out);
  and and_14 (and_14_out, finish, not_36_out, D0);
  not not_36 (not_36_out, D1);
  or or_1 (Q2, and_1_out, and_2_out, and_3_out, and_4_out);
  or or_2 (Q1, and_5_out, and_6_out, and_7_out, and_8_out, and_9_out);
  or or_3 (Q0, and_10_out, and_11_out, and_12_out, and_13_out, and_14_out);
endmodule

module FiftyNineZero (
  input  TickIn,
  input  [3:0] loadT_4,
  input  loadTEnDi,
  input  [3:0] loadU_4,
  input  loadUEnDi,
  input  RESET,
  input  CLK2K,
  output TickOut,
  output [3:0] curT_3,
  output [3:0] curU_4,
  output finished
);

  wire and_1_out, counter_1_carry, counter_2_carry;
  wire [2:0] bit_extender_1_out, counter_1_q, load_3_timer_1_out0;
  wire [3:0] counter_2_q;

  and and_1 (and_1_out, counter_2_carry, TickIn);
  Bit_Extender #(.in_width(4), .out_width(3), .\type ("zero")) bit_extender_1 (.in(loadT_4), .out(bit_extender_1_out));
  Counter #(.width(3), .max('h5)) counter_1 (
    .clr(RESET), .load(loadTEnDi), .up(1'b0), .count(and_1_out), .clk(CLK2K), .D(bit_extender_1_out),
    .carry(counter_1_carry), .Q(counter_1_q));
  Counter #(.width(4), .max('h9)) counter_2 (
    .clr(RESET), .load(loadUEnDi), .up(1'b0), .count(TickIn), .clk(CLK2K), .D(loadU_4),
    .carry(counter_2_carry), .Q(counter_2_q));
  and and_2 (TickOut, TickIn, counter_1_carry, counter_2_carry);
  and and_3 (finished, counter_2_carry, counter_1_carry);
  load_3_timer load_3_timer_1 (
    .val(counter_1_q), .loadValue(loadT_4), .loadEnDi(loadTEnDi), .OUT0(load_3_timer_1_out0));
  assign curT_3 = {{1{1'b0}}, load_3_timer_1_out0};  // Bit_Extender bit_extender_2
  load_4_timer load_4_timer_1 (.val(counter_2_q), .loadValue(loadU_4), .loadEnDi(loadUEnDi), .OUT0(curU_4));
endmodule

module clk2k_to_ticksec_timer (
  input  START,
  input  RESET,
  input  CLK2k,
  output TickSEC
);

  Counter #(.width(10), .max('h3e9)) counter_1 (
    .clr(RESET), .count(START), .clk(CLK2k), .carry(TickSEC));  // open: load, up, D, Q
endmodule

module timerView (
  input  [3:0] HT_4,
  input  [3:0] HU_4,
  input  [3:0] MINT_4,
  input  [3:0] MINU_4,
  input  [3:0] SECT_4,
  input  [3:0] SECU_4,
  input  HloadT,
  input  HloadU,
  input  MINloadT,
  input  MINloadU,
  input  SECloadT,
  input  SECloadU,
  input  RESET,
  input  CLK4,
  output [7:0] sevsegCode_5,
  output [7:0] sevsegCode_4,
  output [7:0] sevsegCode_3,
  output [7:0] sevsegCode_2,
  output [7:0] sevsegCode_1,
  output [7:0] sevsegCode_0
);

  wire and_1_out, and_2_out, and_3_out, and_4_out, and_5_out, and_6_out, or_1_out, t_ff_1_q;
  wire [6:0] bit_extender_2_out, bit_extender_4_out, multiplexer_2_out, multiplexer_4_out;
  wire [7:0] bit_extender_1_out, bit_extender_3_out, bit_extender_5_out, bit_extender_6_out;

  assign bit_extender_1_out = {{4{1'b0}}, HT_4};  // Bit_Extender bit_extender_1
  assign bit_extender_2_out = {{3{1'b0}}, HU_4};  // Bit_Extender bit_extender_2
  assign bit_extender_3_out = {{4{1'b0}}, MINT_4};  // Bit_Extender bit_extender_3
  assign bit_extender_4_out = {{3{1'b0}}, MINU_4};  // Bit_Extender bit_extender_4
  assign bit_extender_5_out = {{4{1'b0}}, SECT_4};  // Bit_Extender bit_extender_5
  assign bit_extender_6_out = {{4{1'b0}}, SECU_4};  // Bit_Extender bit_extender_6
  T_Flip_Flop t_ff_1 (.T(or_1_out), .clk(CLK4), .Q(t_ff_1_q), .reset(RESET));  // open: Qn, preset
  or or_1 (or_1_out, HloadT, HloadU, MINloadT, MINloadU, SECloadT, SECloadU);
  Multiplexer #(.width(8), .enable("false")) multiplexer_1 (
    .in0(bit_extender_1_out), .in1(8'h7f), .out(sevsegCode_5), .sel(and_1_out));
  and and_1 (and_1_out, HloadT, t_ff_1_q);
  and and_2 (and_2_out, HloadU, t_ff_1_q);
  Multiplexer #(.width(7), .enable("false")) multiplexer_2 (
    .in0(bit_extender_2_out), .in1({7{1'b1}}), .out(multiplexer_2_out), .sel(and_2_out));
  Multiplexer #(.width(8), .enable("false")) multiplexer_3 (
    .in0(bit_extender_3_out), .in1(8'h7f), .out(sevsegCode_3), .sel(and_3_out));
  and and_3 (and_3_out, MINloadT, t_ff_1_q);
  Multiplexer #(.width(7), .enable("false")) multiplexer_4 (
    .in0(bit_extender_4_out), .in1({7{1'b1}}), .out(multiplexer_4_out), .sel(and_4_out));
  and and_4 (and_4_out, MINloadU, t_ff_1_q);
  assign sevsegCode_4 = {{1{1'b1}}, multiplexer_2_out};  // Bit_Extender bit_extender_7
  assign sevsegCode_2 = {{1{1'b1}}, multiplexer_4_out};  // Bit_Extender bit_extender_8
  Multiplexer #(.width(8), .enable("false")) multiplexer_5 (
    .in0(bit_extender_5_out), .in1(8'h7f), .out(sevsegCode_1), .sel(and_5_out));
  and and_5 (and_5_out, SECloadT, t_ff_1_q);
  Multiplexer #(.width(8), .enable("false")) multiplexer_6 (
    .in0(bit_extender_6_out), .in1(8'h7f), .out(sevsegCode_0), .sel(and_6_out));
  and and_6 (and_6_out, SECloadU, t_ff_1_q);
endmodule

module load_3_timer (
  input  [2:0] val,
  input  [3:0] loadValue,
  input  loadEnDi,
  output [2:0] OUT0
);

  wire [2:0] bit_extender_1_out;

  Bit_Extender #(.in_width(4), .out_width(3)) bit_extender_1 (.in(loadValue), .out(bit_extender_1_out));
  Multiplexer #(.width(3), .enable("false")) multiplexer_1 (
    .in0(val), .in1(bit_extender_1_out), .out(OUT0), .sel(loadEnDi));
endmodule

module load_4_timer (
  input  [3:0] val,
  input  [3:0] loadValue,
  input  loadEnDi,
  output [3:0] OUT0
);

  Multiplexer #(.width(4), .enable("false")) multiplexer_1 (.in0(val), .in1(loadValue), .out(OUT0), .sel(loadEnDi));
endmodule

module changeTimer (
  input  DIP,
  input  [1:0] B1_B0,
  input  CLK32k,
  input  RESET,
  output [3:0] HloadT_4,
  output HloadTEnDi,
  output [3:0] HloadU_4,
  output HloadUEnDi,
  output [3:0] MINloadT_4,
  output MINloadTEnDi,
  output [3:0] MINloadU_4,
  output MINloadUEnDi,
  output [3:0] SECloadT_4,
  output SECloadTEnDi,
  output [3:0] SECloadU_4,
  output SECloadUEnDi
);

  wire and_1_out, and_2_out, demultiplexer_1_out1, demultiplexer_1_out2, demultiplexer_1_out3,
       demultiplexer_1_out4, demultiplexer_1_out5, demultiplexer_1_out6, demultiplexer_2_out0, or_1_out,
       or_2_out;
  wire [2:0] counter_1_q, counter_2_q, counter_4_q, counter_6_q;

  and and_1 (and_1_out, B1_B0[0], DIP);
  and and_2 (and_2_out, DIP, B1_B0[1]);
  Counter #(.width(3), .max('h6)) counter_1 (
    .clr(or_1_out), .count(and_1_out), .clk(CLK32k), .Q(counter_1_q));  // open: load, up, D, carry
  or or_1 (or_1_out, ~DIP, RESET);  // OR_Gate
  Demultiplexer #(.select(3), .enable("false")) demultiplexer_1 (
    .out1(demultiplexer_1_out1), .out2(demultiplexer_1_out2), .out3(demultiplexer_1_out3),
    .out4(demultiplexer_1_out4), .out5(demultiplexer_1_out5), .out6(demultiplexer_1_out6), .in(and_2_out),
    .sel(counter_1_q));  // open: out0, out7
  Demultiplexer #(.select(3), .enable("false")) demultiplexer_2 (
    .out0(demultiplexer_2_out0), .out1(HloadTEnDi), .out2(HloadUEnDi), .out3(MINloadTEnDi),
    .out4(MINloadUEnDi), .out5(SECloadTEnDi), .out6(SECloadUEnDi), .in(1'b1), .sel(counter_1_q));  // open: out7
  or or_2 (or_2_out, demultiplexer_2_out0, RESET);
  Counter #(.width(3), .max('h5)) counter_2 (
    .clr(or_2_out), .count(demultiplexer_1_out1), .clk(CLK32k), .Q(counter_2_q));  // open: load, up, D, carry
  Counter #(.width(4), .max('h9)) counter_3 (
    .clr(or_2_out), .count(demultiplexer_1_out2), .clk(CLK32k), .Q(HloadU_4));  // open: load, up, D, carry
  Counter #(.width(3), .max('h5)) counter_4 (
    .clr(or_2_out), .count(demultiplexer_1_out3), .clk(CLK32k), .Q(counter_4_q));  // open: load, up, D, carry
  Counter #(.width(4), .max('h9)) counter_5 (
    .clr(or_2_out), .count(demultiplexer_1_out4), .clk(CLK32k), .Q(MINloadU_4));  // open: load, up, D, carry
  Counter #(.width(3), .max('h5)) counter_6 (
    .clr(or_2_out), .count(demultiplexer_1_out5), .clk(CLK32k), .Q(counter_6_q));  // open: load, up, D, carry
  Counter #(.width(4), .max('h9)) counter_7 (
    .clr(or_2_out), .count(demultiplexer_1_out6), .clk(CLK32k), .Q(SECloadU_4));  // open: load, up, D, carry
  assign HloadT_4 = {{1{1'b0}}, counter_2_q};  // Bit_Extender bit_extender_1
  assign MINloadT_4 = {{1{1'b0}}, counter_4_q};  // Bit_Extender bit_extender_2
  assign SECloadT_4 = {{1{1'b0}}, counter_6_q};  // Bit_Extender bit_extender_3

  // Other names for the same wires on the sheet: clk = CLK32k
endmodule
