// Logisim project FSM_ALL_test2.circ as structural Verilog: 88 circuits, main circuit DIGITAL_CLOCK
module DIGITAL_CLOCK (
  output Buzzer0,
  output Buzzer1
);

  wire AlarmOn, and_1_out, B0_out, B1_out, ButtonManager_1_chmode, ButtonManager_1_d0, ButtonManager_1_d1,
       ChM, clk, clk2k, clk4, d_ff_3_q, DipSwitch_1_sw2, or_1_out, or_2_out, or_3_out, RC, RESET;
  wire [1:0] d_ff_1_q, demultiplexer_1_out1, demultiplexer_1_out2, demultiplexer_1_out3,
       demultiplexer_1_out4, demultiplexer_1_out5, demultiplexer_1_out6;
  wire [2:0] FSM_ALL_1_state, STATE;
  wire [7:0] AllSegLeds_1_sevseg_0, AllSegLeds_1_sevseg_1, AllSegLeds_1_sevseg_2, AllSegLeds_1_sevseg_3,
       AllSegLeds_1_sevseg_4, AllSegLeds_1_sevseg_5, ChangementFuseauHoraire_1_utccode;
  wire [23:0] Alarm_1, Alarm_2, Anim_1, Anim_2, Capita_1, Capita_2, Chrono_1, Chrono_2, LT_1, LT_2,
       multiplexer_1_out, multiplexer_2_out, Music_1, Music_2, Timer_1, Timer_2, UTC_1, UTC_2;

  Clock clock_1 (.out(clk));
  Button B1 (.out(B1_out));
  Button B0 (.out(B0_out));
  DipSwitch #(.number(10)) DipSwitch_1 (
    .sw1(ChM), .sw2(DipSwitch_1_sw2), .sw5(RESET));  // open: sw3, sw4, sw6, sw7, sw8, sw9, sw10
  or or_1 (or_1_out, d_ff_1_q[0], d_ff_1_q[1], d_ff_3_q);
  Multiplexer #(.select(3), .width(24), .enable("false")) multiplexer_1 (
    .in0(Anim_1), .in1(UTC_1), .in2(Chrono_1), .in3(Timer_1), .in4(Alarm_1), .in5(Capita_1), .in6(Music_1),
    .in7(LT_1), .out(multiplexer_1_out), .sel(STATE));
  Multiplexer #(.select(3), .width(24), .enable("false")) multiplexer_2 (
    .in0(Anim_2), .in1(UTC_2), .in2(Chrono_2), .in3(Timer_2), .in4(Alarm_2), .in5(Capita_2), .in6(Music_2),
    .in7(LT_2), .out(multiplexer_2_out), .sel(STATE));
  changeFrequency32k_2k changeFrequency32k_2k_1 (.CLK32k(clk), .RESET(RESET), .CLK2k(clk2k));
  AllSegLeds AllSegLeds_1 (
    .sevsegCode_5(multiplexer_1_out[7:0]), .sevsegCode_4(multiplexer_1_out[15:8]),
    .sevsegCode_3(multiplexer_1_out[23:16]), .sevsegCode_2(multiplexer_2_out[7:0]),
    .sevsegCode_1(multiplexer_2_out[15:8]), .sevsegCode_0(multiplexer_2_out[23:16]),
    .sevseg_5(AllSegLeds_1_sevseg_5), .sevseg_4(AllSegLeds_1_sevseg_4), .sevseg_3(AllSegLeds_1_sevseg_3),
    .sevseg_2(AllSegLeds_1_sevseg_2), .sevseg_1(AllSegLeds_1_sevseg_1), .sevseg_0(AllSegLeds_1_sevseg_0));
  D_Flip_Flop d_ff_1 (.D(ButtonManager_1_d0), .clk(clk), .Q(d_ff_1_q[0]), .reset(or_2_out));  // open: Qn, preset
  ButtonManager ButtonManager_1 (
    .DIP(ChM), .RESET(or_1_out), .C2(d_ff_3_q), .C1(d_ff_1_q[1]), .C0(d_ff_1_q[0]), .B1(B1_out), .B0(B0_out),
    .D0(ButtonManager_1_d0), .D1(ButtonManager_1_d1), .chMode(ButtonManager_1_chmode));
  or or_2 (or_2_out, ChM, RESET);
  _7_Segment_Display SSD5 (
    .g(AllSegLeds_1_sevseg_5[0]), .f(AllSegLeds_1_sevseg_5[1]), .a(AllSegLeds_1_sevseg_5[6]),
    .b(AllSegLeds_1_sevseg_5[5]), .e(AllSegLeds_1_sevseg_5[2]), .d(AllSegLeds_1_sevseg_5[3]),
    .c(AllSegLeds_1_sevseg_5[4]), .dp(AllSegLeds_1_sevseg_5[7]));
  changeFrequency2k_4 changeFrequency2k_4_1 (.CLK2k(clk2k), .RESET(RESET), .CLK4(clk4));
  D_Flip_Flop d_ff_2 (.D(ButtonManager_1_d1), .clk(clk), .Q(d_ff_1_q[1]), .reset(or_3_out));  // open: Qn, preset
  or or_3 (or_3_out, ChM, RESET);
  _7_Segment_Display SSD4 (
    .g(AllSegLeds_1_sevseg_4[0]), .f(AllSegLeds_1_sevseg_4[1]), .a(AllSegLeds_1_sevseg_4[6]),
    .b(AllSegLeds_1_sevseg_4[5]), .e(AllSegLeds_1_sevseg_4[2]), .d(AllSegLeds_1_sevseg_4[3]),
    .c(AllSegLeds_1_sevseg_4[4]), .dp(AllSegLeds_1_sevseg_4[7]));
  D_Flip_Flop d_ff_3 (.D(ButtonManager_1_chmode), .clk(clk), .Q(d_ff_3_q), .reset(RESET));  // open: Qn, preset
  _7_Segment_Display SSD3 (
    .g(AllSegLeds_1_sevseg_3[0]), .f(AllSegLeds_1_sevseg_3[1]), .a(AllSegLeds_1_sevseg_3[6]),
    .b(AllSegLeds_1_sevseg_3[5]), .e(AllSegLeds_1_sevseg_3[2]), .d(AllSegLeds_1_sevseg_3[3]),
    .c(AllSegLeds_1_sevseg_3[4]), .dp(AllSegLeds_1_sevseg_3[7]));
  _7_Segment_Display SSD2 (
    .g(AllSegLeds_1_sevseg_2[0]), .f(AllSegLeds_1_sevseg_2[1]), .a(AllSegLeds_1_sevseg_2[6]),
    .b(AllSegLeds_1_sevseg_2[5]), .e(AllSegLeds_1_sevseg_2[2]), .d(AllSegLeds_1_sevseg_2[3]),
    .c(AllSegLeds_1_sevseg_2[4]), .dp(AllSegLeds_1_sevseg_2[7]));
  and and_1 (and_1_out, ~FSM_ALL_1_state[0], ~FSM_ALL_1_state[1], ~FSM_ALL_1_state[2]);  // AND_Gate
  _7_Segment_Display SSD1 (
    .g(AllSegLeds_1_sevseg_1[0]), .f(AllSegLeds_1_sevseg_1[1]), .a(AllSegLeds_1_sevseg_1[6]),
    .b(AllSegLeds_1_sevseg_1[5]), .e(AllSegLeds_1_sevseg_1[2]), .d(AllSegLeds_1_sevseg_1[3]),
    .c(AllSegLeds_1_sevseg_1[4]), .dp(AllSegLeds_1_sevseg_1[7]));
  or or_4 (RC, RESET, and_1_out);
  FSM_ALL FSM_ALL_1 (.ChMode(d_ff_3_q), .DIP(ChM), .RESET(RESET), .CLK32k(clk), .STATE(FSM_ALL_1_state));
  _7_Segment_Display SSD0 (
    .g(AllSegLeds_1_sevseg_0[0]), .f(AllSegLeds_1_sevseg_0[1]), .a(AllSegLeds_1_sevseg_0[6]),
    .b(AllSegLeds_1_sevseg_0[5]), .e(AllSegLeds_1_sevseg_0[2]), .d(AllSegLeds_1_sevseg_0[3]),
    .c(AllSegLeds_1_sevseg_0[4]), .dp(AllSegLeds_1_sevseg_0[7]));
  Demultiplexer #(.select(3), .width(2), .enable("false")) demultiplexer_1 (
    .out1(demultiplexer_1_out1), .out2(demultiplexer_1_out2), .out3(demultiplexer_1_out3),
    .out4(demultiplexer_1_out4), .out5(demultiplexer_1_out5), .out6(demultiplexer_1_out6), .in(d_ff_1_q),
    .sel(FSM_ALL_1_state));  // open: out0, out7
  hourFSM hourFSM_1 (
    .RESET(RC), .B1_B0(demultiplexer_1_out1), .ChM(ChM), .CLK32K(clk), .CLK2k(clk2k), .CLK4(clk4),
    .sevsegCode_5(UTC_1[7:0]), .sevsegCode_4(UTC_1[15:8]), .sevsegCode_3(UTC_1[23:16]),
    .sevsegCode_2(UTC_2[7:0]), .sevsegCode_1(UTC_2[15:8]), .sevsegCode_0(UTC_2[23:16]));
  CHRONO u_CHRONO_1 (
    .RESET(RC), .B1_B0(demultiplexer_1_out2), .ChMode(ChM), .CLK32k(clk), .Min_Led2(Chrono_1[7:0]),
    .Min_Led1(Chrono_1[15:8]), .Sec_Led2(Chrono_1[23:16]), .Sec_Led1(Chrono_2[7:0]),
    .Milli_Led2(Chrono_2[15:8]), .Milli_Led1(Chrono_2[23:16]));
  timerFSM timerFSM_1 (
    .RESET(RC), .B1_B0(demultiplexer_1_out3), .DIP(DipSwitch_1_sw2), .ChM(ChM), .CLK32k(clk), .CLK2k(clk2k),
    .CLK4(clk4), .sevsegCode_5(Timer_1[7:0]), .sevsegCode_4(Timer_1[15:8]), .sevsegCode_3(Timer_1[23:16]),
    .sevsegCode_2(Timer_2[7:0]), .sevsegCode_1(Timer_2[15:8]), .sevsegCode_0(Timer_2[23:16]));
  ChangementFuseauHoraire ChangementFuseauHoraire_1 (
    .RESET(RC), .B1_B0(demultiplexer_1_out5), .ChM(ChM), .CLK32k(clk), .Letter1(Capita_1[7:0]),
    .Letter2(Capita_1[15:8]), .Letter3(Capita_1[23:16]), .Letter4(Capita_2[7:0]), .Letter5(Capita_2[15:8]),
    .Letter6(Capita_2[23:16]), .UTCCode(ChangementFuseauHoraire_1_utccode));
  MUSIC u_MUSIC_1 (
    .ALARM(AlarmOn), .B1_B0(demultiplexer_1_out6), .RESET(RC), .CLK32k(clk), .Buzzer1(Buzzer1),
    .L1(Music_1[7:0]), .L2(Music_1[15:8]), .L3(Music_1[23:16]), .L4(Music_2[7:0]), .L5(Music_2[15:8]),
    .L6(Music_2[23:16]));
  ANIMATION animations (
    .State(FSM_ALL_1_state), .L1(Anim_1[7:0]), .L2(Anim_1[15:8]), .L3(Anim_1[23:16]), .L4(Anim_2[7:0]),
    .L5(Anim_2[15:8]), .L6(Anim_2[23:16]));
  AnimControl AnimControl_1 (.Transition(ChM), .State(FSM_ALL_1_state), .Anim(STATE));
  changeTimeZone changeTimeZone_1 (
    .SSDCode_5(UTC_1[7:0]), .SSDCode_4(UTC_1[15:8]), .SSDCode_3(UTC_1[23:16]), .SSDCode_2(UTC_2[7:0]),
    .SSDCode_1(UTC_2[15:8]), .SSDCode_0(UTC_2[23:16]), .UTCCode_8(ChangementFuseauHoraire_1_utccode),
    .sevsegCode_5(LT_1[7:0]), .sevsegCode_4(LT_1[15:8]), .sevsegCode_3(LT_1[23:16]),
    .sevsegCode_2(LT_2[7:0]), .sevsegCode_1(LT_2[15:8]), .sevsegCode_0(LT_2[23:16]));
  alarm u_alarm_1 (
    .RESET(RC), .B1_B0(demultiplexer_1_out4), .SSDCode_5(LT_1[7:0]), .SSDCode_4(LT_1[15:8]),
    .SSDCode_3(LT_1[23:16]), .SSDCode_2(LT_2[7:0]), .ChM(ChM), .CLK32K(clk), .CLK2k(clk2k), .CLK4(clk4),
    .sevsegCode_5(Alarm_1[7:0]), .sevsegCode_4(Alarm_1[15:8]), .sevsegCode_3(Alarm_1[23:16]),
    .sevsegCode_2(Alarm_2[7:0]), .sevsegCode_1(Alarm_2[15:8]), .sevsegCode_0(Alarm_2[23:16]), .BUZZER(AlarmOn));

  assign Buzzer0 = 1'b0;

  // Notes on the sheet:
  //   LedGauche
  //   LedDroite
endmodule

module FSM_ALL (
  input  ChMode,
  input  DIP,
  input  RESET,
  input  CLK32k,
  output [2:0] STATE
);

  wire TransLogic_1_d0, TransLogic_1_d1, TransLogic_1_d2;

  TransLogic TransLogic_1 (
    .B1(ChMode), .DIP(DIP), .C2(STATE[2]), .C1(STATE[1]), .C0(STATE[0]), .D2(TransLogic_1_d2),
    .D1(TransLogic_1_d1), .D0(TransLogic_1_d0));
  D_Flip_Flop d_ff_1 (.D(TransLogic_1_d2), .clk(CLK32k), .Q(STATE[2]), .reset(RESET));  // open: Qn, preset
  D_Flip_Flop d_ff_2 (.D(TransLogic_1_d1), .clk(CLK32k), .Q(STATE[1]), .reset(RESET));  // open: Qn, preset
  D_Flip_Flop d_ff_3 (.D(TransLogic_1_d0), .clk(CLK32k), .Q(STATE[0]), .reset(RESET));  // open: Qn, preset
endmodule

module ButtonManager (
  input  DIP,
  input  RESET,
  input  C2,
  input  C1,
  input  C0,
  input  B1,
  input  B0,
  output D0,
  output D1,
  output chMode
);

  wire d_ff_1_q, d_ff_1_qn, d_ff_2_q, d_ff_2_qn, not_1_out, not_2_out, not_3_out, not_4_out, not_5_out,
       not_6_out, not_7_out, not_8_out, not_9_out, not_10_out;

  D_Flip_Flop d_ff_1 (.D(d_ff_1_qn), .clk(B1), .Q(d_ff_1_q), .Qn(d_ff_1_qn), .reset(RESET));  // open: preset
  D_Flip_Flop d_ff_2 (.D(d_ff_2_qn), .clk(B0), .Q(d_ff_2_q), .Qn(d_ff_2_qn), .reset(RESET));  // open: preset
  not not_1 (not_1_out, DIP);
  not not_2 (not_2_out, RESET);
  not not_3 (not_3_out, C2);
  not not_4 (not_4_out, DIP);
  not not_5 (not_5_out, RESET);
  not not_6 (not_6_out, C2);
  not not_7 (not_7_out, RESET);
  not not_8 (not_8_out, C2);
  not not_9 (not_9_out, C1);
  not not_10 (not_10_out, C0);
  and and_1 (D0, not_1_out, not_2_out, not_3_out, d_ff_1_q);
  and and_2 (D1, not_4_out, not_5_out, not_6_out, d_ff_2_q);
  and and_3 (chMode, DIP, not_7_out, not_8_out, not_9_out, not_10_out, d_ff_2_q);
endmodule

module TransLogic (
  input  B1,
  input  DIP,
  input  C2,
  input  C1,
  input  C0,
  output D2,
  output D1,
  output D0
);

  wire and_1_out, and_2_out, and_3_out, and_4_out, and_5_out, and_6_out, and_7_out, and_8_out, and_9_out,
       and_10_out, and_11_out, and_12_out, and_13_out, not_1_out, not_2_out, not_3_out, not_4_out, not_5_out,
       not_6_out, not_7_out, not_8_out, not_9_out, not_10_out, not_11_out, not_12_out;

  not not_1 (not_1_out, C2);
  not not_2 (not_2_out, C1);
  not not_3 (not_3_out, B1);
  not not_4 (not_4_out, DIP);
  not not_5 (not_5_out, C0);
  not not_6 (not_6_out, B1);
  and and_1 (and_1_out, not_6_out, C2);
  not not_7 (not_7_out, DIP);
  and and_2 (and_2_out, not_7_out, C2);
  and and_3 (and_3_out, C2, not_8_out);
  not not_8 (not_8_out, C1);
  and and_4 (and_4_out, C2, not_9_out);
  not not_9 (not_9_out, C0);
  and and_5 (and_5_out, B1, DIP, not_1_out, C1, C0);
  not not_10 (not_10_out, B1);
  and and_6 (and_6_out, not_10_out, C1);
  not not_11 (not_11_out, DIP);
  and and_7 (and_7_out, not_11_out, C1);
  and and_8 (and_8_out, C1, not_12_out);
  not not_12 (not_12_out, C0);
  and and_9 (and_9_out, B1, DIP, not_2_out, C0);
  and and_10 (and_10_out, not_3_out, C0);
  and and_11 (and_11_out, not_4_out, C0);
  and and_12 (and_12_out, C2, C1, C0);
  and and_13 (and_13_out, B1, DIP, not_5_out);
  or or_1 (D2, and_1_out, and_2_out, and_3_out, and_4_out, and_5_out);
  or or_2 (D1, and_6_out, and_7_out, and_8_out, and_9_out);
  or or_3 (D0, and_10_out, and_11_out, and_12_out, and_13_out);
endmodule

module DecoderToSegLed (
  input  e5,
  input  e4,
  input  e3,
  input  e2,
  input  e1,
  input  e0,
  output o,
  output a,
  output b,
  output c,
  output d,
  output e,
  output f,
  output g
);

  wire and_1_out, and_2_out, and_3_out, and_4_out, and_5_out, and_6_out, and_7_out, and_8_out, and_9_out,
       and_10_out, and_11_out, and_12_out, and_13_out, and_14_out, and_15_out, and_16_out, and_17_out,
       and_18_out, and_19_out, and_20_out, and_21_out, and_22_out, and_23_out, and_24_out, and_25_out,
       and_26_out, and_27_out, and_28_out, and_29_out, and_30_out, and_31_out, and_32_out, and_33_out,
       and_34_out, and_35_out, and_36_out, and_37_out, and_38_out, and_39_out, and_40_out, and_41_out,
       and_42_out, and_43_out, and_44_out, and_45_out, and_46_out, and_47_out, and_48_out, and_49_out,
       and_50_out, and_51_out, and_52_out, and_53_out, not_1_out, not_2_out, not_3_out, not_4_out, not_5_out,
       not_6_out, not_7_out, not_8_out, not_9_out, not_10_out, not_11_out, not_12_out, not_13_out,
       not_14_out, not_15_out, not_16_out, not_17_out, not_18_out, not_19_out, not_20_out, not_21_out,
       not_22_out, not_23_out, not_24_out, not_25_out, not_26_out, not_27_out, not_28_out, not_29_out,
       not_30_out, not_31_out, not_32_out, not_33_out, not_34_out, not_35_out, not_36_out, not_37_out,
       not_38_out, not_39_out, not_40_out, not_41_out, not_42_out, not_43_out, not_44_out, not_45_out,
       not_46_out, not_47_out, not_48_out, not_49_out, not_50_out, not_51_out, not_52_out, not_53_out,
       not_54_out, not_55_out, not_56_out, not_57_out, not_58_out, not_59_out, not_60_out, not_61_out,
       not_62_out, not_63_out, not_64_out, not_65_out, not_66_out, not_67_out, not_68_out, not_69_out,
       not_70_out, not_71_out, not_72_out, not_73_out, not_74_out, not_75_out, not_76_out, not_77_out,
       not_78_out, not_79_out, not_80_out, not_81_out, not_82_out, not_83_out, not_84_out, not_85_out,
       not_86_out, not_87_out, not_88_out, not_89_out, not_90_out, not_91_out, not_92_out, not_93_out,
       not_94_out, not_95_out, not_96_out;

  not not_1 (not_1_out, e2);
  not not_2 (not_2_out, e1);
  not not_3 (not_3_out, e0);
  not not_4 (not_4_out, e4);
  not not_5 (not_5_out, e3);
  not not_6 (not_6_out, e3);
  not not_7 (not_7_out, e1);
  not not_8 (not_8_out, e4);
  not not_9 (not_9_out, e4);
  not not_10 (not_10_out, e0);
  not not_11 (not_11_out, e2);
  not not_12 (not_12_out, e1);
  not not_13 (not_13_out, e2);
  not not_14 (not_14_out, e4);
  not not_15 (not_15_out, e3);
  not not_16 (not_16_out, e1);
  not not_17 (not_17_out, e0);
  not not_18 (not_18_out, e4);
  not not_19 (not_19_out, e2);
  not not_20 (not_20_out, e0);
  not not_21 (not_21_out, e3);
  not not_22 (not_22_out, e2);
  not not_23 (not_23_out, e4);
  not not_24 (not_24_out, e3);
  not not_25 (not_25_out, e2);
  not not_26 (not_26_out, e1);
  not not_27 (not_27_out, e4);
  not not_28 (not_28_out, e1);
  not not_29 (not_29_out, e3);
  not not_30 (not_30_out, e1);
  not not_31 (not_31_out, e0);
  not not_32 (not_32_out, e3);
  not not_33 (not_33_out, e2);
  not not_34 (not_34_out, e1);
  not not_35 (not_35_out, e3);
  not not_36 (not_36_out, e2);
  not not_37 (not_37_out, e1);
  not not_38 (not_38_out, e4);
  not not_39 (not_39_out, e3);
  not not_40 (not_40_out, e4);
  not not_41 (not_41_out, e2);
  not not_42 (not_42_out, e0);
  not not_43 (not_43_out, e4);
  not not_44 (not_44_out, e3);
  not not_45 (not_45_out, e2);
  not not_46 (not_46_out, e0);
  not not_47 (not_47_out, e4);
  not not_48 (not_48_out, e3);
  not not_49 (not_49_out, e0);
  not not_50 (not_50_out, e2);
  not not_51 (not_51_out, e4);
  not not_52 (not_52_out, e1);
  not not_53 (not_53_out, e4);
  not not_54 (not_54_out, e1);
  not not_55 (not_55_out, e1);
  not not_56 (not_56_out, e0);
  not not_57 (not_57_out, e3);
  not not_58 (not_58_out, e1);
  not not_59 (not_59_out, e0);
  not not_60 (not_60_out, e3);
  not not_61 (not_61_out, e2);
  and and_1 (and_1_out, not_61_out, not_62_out);
  not not_62 (not_62_out, e0);
  not not_63 (not_63_out, e4);
  and and_2 (and_2_out, not_63_out, e1, not_64_out);
  not not_64 (not_64_out, e0);
  not not_65 (not_65_out, e4);
  and and_3 (and_3_out, not_65_out, e3, e1);
  and and_4 (and_4_out, e3, e2, not_66_out);
  not not_66 (not_66_out, e1);
  and and_5 (and_5_out, e4, not_67_out, not_68_out);
  not not_67 (not_67_out, e3);
  not not_68 (not_68_out, e1);
  and and_6 (and_6_out, e4, not_69_out, e2);
  not not_69 (not_69_out, e3);
  not not_70 (not_70_out, e1);
  not not_71 (not_71_out, e0);
  not not_72 (not_72_out, e4);
  not not_73 (not_73_out, e0);
  not not_74 (not_74_out, e3);
  not not_75 (not_75_out, e1);
  not not_76 (not_76_out, e2);
  not not_77 (not_77_out, e4);
  not not_78 (not_78_out, e0);
  not not_79 (not_79_out, e3);
  not not_80 (not_80_out, e2);
  not not_81 (not_81_out, e0);
  not not_82 (not_82_out, e3);
  not not_83 (not_83_out, e1);
  not not_84 (not_84_out, e4);
  not not_85 (not_85_out, e2);
  not not_86 (not_86_out, e4);
  not not_87 (not_87_out, e0);
  not not_88 (not_88_out, e4);
  not not_89 (not_89_out, e3);
  not not_90 (not_90_out, e1);
  not not_91 (not_91_out, e2);
  not not_92 (not_92_out, e4);
  not not_93 (not_93_out, e2);
  not not_94 (not_94_out, e1);
  not not_95 (not_95_out, e3);
  not not_96 (not_96_out, e0);
  and and_7 (and_7_out, not_1_out, not_2_out, not_3_out);
  and and_8 (and_8_out, not_4_out, not_5_out, e1);
  and and_9 (and_9_out, not_6_out, e2, not_7_out, e0);
  and and_10 (and_10_out, not_8_out, e2, e1);
  and and_11 (and_11_out, not_9_out, e3, not_10_out);
  and and_12 (and_12_out, e3, not_11_out, not_12_out);
  and and_13 (and_13_out, e4, e3, not_13_out, e0);
  and and_14 (and_14_out, not_14_out, not_15_out, not_16_out, not_17_out);
  and and_15 (and_15_out, not_18_out, not_19_out, not_20_out);
  and and_16 (and_16_out, not_21_out, not_22_out, e0);
  and and_17 (and_17_out, not_23_out, not_24_out, e1, e0);
  and and_18 (and_18_out, e3, not_25_out, not_26_out);
  and and_19 (and_19_out, not_27_out, e3, not_28_out, e0);
  and and_20 (and_20_out, e4, not_29_out, not_30_out, e0);
  and and_21 (and_21_out, e4, e3, e2, e1, not_31_out);
  and and_22 (and_22_out, not_32_out, not_33_out, not_34_out);
  and and_23 (and_23_out, not_35_out, e0);
  and and_24 (and_24_out, not_36_out, e0);
  and and_25 (and_25_out, not_37_out, e0);
  and and_26 (and_26_out, not_38_out, not_39_out, e2);
  and and_27 (and_27_out, not_40_out, e3, not_41_out);
  and and_28 (and_28_out, e4, e2, e1, not_42_out);
  and and_29 (and_29_out, not_43_out, not_44_out, not_45_out, not_46_out);
  and and_30 (and_30_out, not_47_out, not_48_out, e1, not_49_out);
  and and_31 (and_31_out, not_50_out, e1, e0);
  and and_32 (and_32_out, not_51_out, e2, not_52_out, e0);
  and and_33 (and_33_out, not_53_out, e3, not_54_out);
  and and_34 (and_34_out, e3, e2, not_55_out);
  and and_35 (and_35_out, e3, e2, not_56_out);
  and and_36 (and_36_out, e4, not_57_out, not_58_out, not_59_out);
  and and_37 (and_37_out, e4, not_60_out, e1, e0);
  and and_38 (and_38_out, not_70_out, not_71_out);
  and and_39 (and_39_out, not_72_out, e2, not_73_out);
  and and_40 (and_40_out, not_74_out, e2, not_75_out);
  and and_41 (and_41_out, e3, not_76_out, e0);
  and and_42 (and_42_out, not_77_out, e3, e1);
  and and_43 (and_43_out, e3, e2, not_78_out);
  and and_44 (and_44_out, e4, not_79_out, not_80_out, not_81_out);
  and and_45 (and_45_out, e4, not_82_out, not_83_out);
  and and_46 (and_46_out, not_84_out, not_85_out, e1);
  and and_47 (and_47_out, not_86_out, e1, not_87_out);
  and and_48 (and_48_out, not_88_out, not_89_out, e2, not_90_out);
  and and_49 (and_49_out, e3, not_91_out);
  and and_50 (and_50_out, not_92_out, e3, e0);
  and and_51 (and_51_out, e4, not_93_out, not_94_out, e0);
  and and_52 (and_52_out, e4, not_95_out, e2, e1);
  and and_53 (and_53_out, e4, e3, not_96_out);
  or or_1 (a, and_7_out, and_8_out, and_9_out, and_10_out, and_11_out, and_12_out, and_13_out);
  or or_2 (b, and_14_out, and_15_out, and_16_out, and_17_out, and_18_out, and_19_out, and_20_out, and_21_out);
  or or_3 (c, and_22_out, and_23_out, and_24_out, and_25_out, and_26_out, and_27_out, and_28_out);
  or or_4 (d, and_29_out, and_30_out, and_31_out, and_32_out, and_33_out, and_34_out, and_35_out, and_36_out, and_37_out);
  or or_5 (e, and_1_out, and_2_out, and_3_out, and_4_out, and_5_out, and_6_out);
  or or_6 (f, and_38_out, and_39_out, and_40_out, and_41_out, and_42_out, and_43_out, and_44_out, and_45_out);
  or or_7 (g, and_46_out, and_47_out, and_48_out, and_49_out, and_50_out, and_51_out, and_52_out, and_53_out);

  assign o = e5;
endmodule

module SegLed1 (
  input  [7:0] sevsegCode,
  output [7:0] sevensegment
);

  wire [4:0] bit_extender_1_out;

  Bit_Extender #(.in_width(7), .out_width(5), .\type ("zero")) bit_extender_1 (
    .in(sevsegCode[6:0]), .out(bit_extender_1_out));
  DecoderToSegLed DecoderToSegLed_1 (
    .e5(sevsegCode[7]), .e4(bit_extender_1_out[4]), .e3(bit_extender_1_out[3]), .e2(bit_extender_1_out[2]),
    .e1(bit_extender_1_out[1]), .e0(bit_extender_1_out[0]), .o(sevensegment[7]), .a(sevensegment[6]),
    .b(sevensegment[5]), .c(sevensegment[4]), .d(sevensegment[3]), .e(sevensegment[2]), .f(sevensegment[1]),
    .g(sevensegment[0]));
endmodule

module AllSegLeds (
  input  [7:0] sevsegCode_5,
  input  [7:0] sevsegCode_4,
  input  [7:0] sevsegCode_3,
  input  [7:0] sevsegCode_2,
  input  [7:0] sevsegCode_1,
  input  [7:0] sevsegCode_0,
  output [7:0] sevseg_5,
  output [7:0] sevseg_4,
  output [7:0] sevseg_3,
  output [7:0] sevseg_2,
  output [7:0] sevseg_1,
  output [7:0] sevseg_0
);

  SegLed1 SegLed1_1 (.sevsegCode(sevsegCode_5), .sevensegment(sevseg_5));
  SegLed1 SegLed1_2 (.sevsegCode(sevsegCode_4), .sevensegment(sevseg_4));
  SegLed1 SegLed1_3 (.sevsegCode(sevsegCode_3), .sevensegment(sevseg_3));
  SegLed1 SegLed1_4 (.sevsegCode(sevsegCode_2), .sevensegment(sevseg_2));
  SegLed1 SegLed1_5 (.sevsegCode(sevsegCode_1), .sevensegment(sevseg_1));
  SegLed1 SegLed1_6 (.sevsegCode(sevsegCode_0), .sevensegment(sevseg_0));
endmodule

module AnimControl (
  input  Transition,
  input  [2:0] State,
  output [2:0] Anim
);

  wire not_1_out, not_2_out, not_3_out;

  not not_1 (not_1_out, Transition);
  not not_2 (not_2_out, Transition);
  not not_3 (not_3_out, Transition);
  and and_1 (Anim[2], not_1_out, State[2]);
  and and_2 (Anim[1], not_2_out, State[1]);
  and and_3 (Anim[0], not_3_out, State[0]);
endmodule

module changeFrequency32k_2k (
  input  CLK32k,
  input  RESET,
  output CLK2k
);

  wire d_ff_1_q, d_ff_1_qn, d_ff_2_q, d_ff_2_qn, d_ff_3_q, d_ff_3_qn, d_ff_4_qn;

  D_Flip_Flop d_ff_1 (.D(d_ff_1_qn), .clk(CLK32k), .Q(d_ff_1_q), .Qn(d_ff_1_qn), .reset(RESET));  // open: preset
  D_Flip_Flop d_ff_2 (.D(d_ff_2_qn), .clk(d_ff_1_q), .Q(d_ff_2_q), .Qn(d_ff_2_qn), .reset(RESET));  // open: preset
  D_Flip_Flop d_ff_3 (.D(d_ff_3_qn), .clk(d_ff_2_q), .Q(d_ff_3_q), .Qn(d_ff_3_qn), .reset(RESET));  // open: preset
  D_Flip_Flop d_ff_4 (.D(d_ff_4_qn), .clk(d_ff_3_q), .Q(CLK2k), .Qn(d_ff_4_qn), .reset(RESET));  // open: preset
endmodule

module changeFrequency2k_4 (
  input  CLK2k,
  input  RESET,
  output CLK4
);

  wire d_ff_1_q, d_ff_1_qn, d_ff_2_q, d_ff_2_qn, d_ff_3_q, d_ff_3_qn, d_ff_4_q, d_ff_4_qn, d_ff_5_q,
       d_ff_5_qn, d_ff_6_q, d_ff_6_qn, d_ff_7_q, d_ff_7_qn, d_ff_8_q, d_ff_8_qn, d_ff_9_qn;

  D_Flip_Flop d_ff_1 (.D(d_ff_1_qn), .clk(CLK2k), .Q(d_ff_1_q), .Qn(d_ff_1_qn), .reset(RESET));  // open: preset
  D_Flip_Flop d_ff_2 (.D(d_ff_2_qn), .clk(d_ff_1_q), .Q(d_ff_2_q), .Qn(d_ff_2_qn), .reset(RESET));  // open: preset
  D_Flip_Flop d_ff_3 (.D(d_ff_3_qn), .clk(d_ff_2_q), .Q(d_ff_3_q), .Qn(d_ff_3_qn), .reset(RESET));  // open: preset
  D_Flip_Flop d_ff_4 (.D(d_ff_4_qn), .clk(d_ff_3_q), .Q(d_ff_4_q), .Qn(d_ff_4_qn), .reset(RESET));  // open: preset
  D_Flip_Flop d_ff_5 (.D(d_ff_5_qn), .clk(d_ff_4_q), .Q(d_ff_5_q), .Qn(d_ff_5_qn), .reset(RESET));  // open: preset
  D_Flip_Flop d_ff_6 (.D(d_ff_6_qn), .clk(d_ff_5_q), .Q(d_ff_6_q), .Qn(d_ff_6_qn), .reset(RESET));  // open: preset
  D_Flip_Flop d_ff_7 (.D(d_ff_7_qn), .clk(d_ff_6_q), .Q(d_ff_7_q), .Qn(d_ff_7_qn), .reset(RESET));  // open: preset
  D_Flip_Flop d_ff_8 (.D(d_ff_8_qn), .clk(d_ff_7_q), .Q(d_ff_8_q), .Qn(d_ff_8_qn), .reset(RESET));  // open: preset
  D_Flip_Flop d_ff_9 (.D(d_ff_9_qn), .clk(d_ff_8_q), .Q(CLK4), .Qn(d_ff_9_qn), .reset(RESET));  // open: preset
endmodule

module MUSIC (
  input  ALARM,
  input  [1:0] B1_B0,
  input  RESET,
  input  CLK32k,
  output Buzzer1,
  output [7:0] L1,
  output [7:0] L2,
  output [7:0] L3,
  output [7:0] L4,
  output [7:0] L5,
  output [7:0] L6
);

  wire d_ff_1_q, d_ff_1_qn, d_ff_2_qn, MusicBox_1_reset, not_1_out, NoteControl_1_outnote, or_1_out,
       or_2_out, or_3_out;
  wire [2:0] counter_1_q;
  wire [7:0] BeatManager_1_beat, FreqToNote_1_note;
  wire [12:0] MusicBox_1_melody;

  D_Flip_Flop d_ff_1 (.D(d_ff_1_qn), .clk(B1_B0[1]), .Q(d_ff_1_q), .Qn(d_ff_1_qn), .reset(RESET));  // open: preset
  or or_1 (or_1_out, ALARM, d_ff_1_q);
  or or_2 (or_2_out, RESET, B1_B0[0], MusicBox_1_reset);
  Counter #(.width(3), .max('h7)) counter_1 (
    .clr(RESET), .count(B1_B0[0]), .clk(CLK32k), .Q(counter_1_q));  // open: load, up, D, carry
  BeatManager BeatManager_1 (.start(or_1_out), .clk(CLK32k), .reset(or_2_out), .beat(BeatManager_1_beat));
  FreqToNote FreqToNote_1 (.reset(NoteControl_1_outnote), .clk(CLK32k), .note(FreqToNote_1_note));
  MusicBox MusicBox_1 (
    .beat(BeatManager_1_beat), .songcode(counter_1_q), .melody(MusicBox_1_melody), .reset(MusicBox_1_reset));
  D_Flip_Flop d_ff_2 (
    .D(d_ff_2_qn), .clk(NoteControl_1_outnote), .Q(Buzzer1), .Qn(d_ff_2_qn), .reset(or_3_out));  // open: preset
  NoteControl NoteControl_1 (
    .frequency(FreqToNote_1_note), .noteCode(MusicBox_1_melody), .outNote(NoteControl_1_outnote));
  SongName SongName_1 (.songcode(counter_1_q), .L1(L1), .L2(L2), .L3(L3), .L4(L4), .L5(L5), .L6(L6));
  or or_3 (or_3_out, RESET, not_1_out);
  not not_1 (not_1_out, or_1_out);
endmodule

module MusicBox (
  input  [7:0] beat,
  input  [2:0] songcode,
  output [12:0] melody,
  output reset
);

  wire AnotherBrickInTheWall_1_reset, ImperialMarch_1_reset, Kalinka_1_reset, MissYou_1_reset,
       PirateCaraibe_1_output_1, RappersDelight_1_reset, ThisMustBeThePlace_1_reset;
  wire [6:2] ThisMustBeThePlace_1_a1;
  wire [7:0] demultiplexer_1_out1, demultiplexer_1_out2, demultiplexer_1_out3, demultiplexer_1_out4,
       demultiplexer_1_out5, demultiplexer_1_out6, demultiplexer_1_out7;
  wire [8:0] RappersDelight_1_c3;
  wire [8:4] MissYou_1_e2;
  wire [10:5] AnotherBrickInTheWall_1_d2;
  wire [12:0] Kalinka_1_output_bus_1, PirateCaraibe_1_output_bus_1;
  wire [12:4] ImperialMarch_1_e2;

  Demultiplexer #(.select(3), .width(8), .enable("false")) demultiplexer_1 (
    .out1(demultiplexer_1_out1), .out2(demultiplexer_1_out2), .out3(demultiplexer_1_out3),
    .out4(demultiplexer_1_out4), .out5(demultiplexer_1_out5), .out6(demultiplexer_1_out6),
    .out7(demultiplexer_1_out7), .in(beat), .sel(songcode));  // open: out0
  ImperialMarch ImperialMarch_1 (
    .Input_1(demultiplexer_1_out1[7]), .Input_2(demultiplexer_1_out1[6]), .Input_3(demultiplexer_1_out1[5]),
    .Input_4(demultiplexer_1_out1[4]), .Input_5(demultiplexer_1_out1[3]), .Input_6(demultiplexer_1_out1[2]),
    .Input_7(demultiplexer_1_out1[1]), .Input_8(demultiplexer_1_out1[0]), .e2(ImperialMarch_1_e2[4]),
    .d2(ImperialMarch_1_e2[5]), .g1(ImperialMarch_1_e2[9]), .e1(ImperialMarch_1_e2[10]),
    .c1(ImperialMarch_1_e2[12]), .reset(ImperialMarch_1_reset));
  Kalinka Kalinka_1 (
    .Input_1(demultiplexer_1_out2[7]), .Input_2(demultiplexer_1_out2[6]), .Input_3(demultiplexer_1_out2[5]),
    .Input_4(demultiplexer_1_out2[4]), .Input_5(demultiplexer_1_out2[3]), .Input_6(demultiplexer_1_out2[2]),
    .Input_7(demultiplexer_1_out2[1]), .Input_8(demultiplexer_1_out2[0]),
    .Output_bus_1(Kalinka_1_output_bus_1), .reset(Kalinka_1_reset));
  PirateCaraibe PirateCaraibe_1 (
    .Input_1(demultiplexer_1_out3[7]), .Input_2(demultiplexer_1_out3[6]), .Input_3(demultiplexer_1_out3[5]),
    .Input_4(demultiplexer_1_out3[4]), .Input_5(demultiplexer_1_out3[3]), .Input_6(demultiplexer_1_out3[2]),
    .Input_7(demultiplexer_1_out3[1]), .Input_8(demultiplexer_1_out3[0]),
    .Output_bus_1(PirateCaraibe_1_output_bus_1), .Output_1(PirateCaraibe_1_output_1));
  ThisMustBeThePlace ThisMustBeThePlace_1 (
    .Input_1(demultiplexer_1_out4[7]), .Input_2(demultiplexer_1_out4[6]), .Input_3(demultiplexer_1_out4[5]),
    .Input_4(demultiplexer_1_out4[4]), .Input_5(demultiplexer_1_out4[3]), .Input_6(demultiplexer_1_out4[2]),
    .Input_7(demultiplexer_1_out4[1]), .Input_8(demultiplexer_1_out4[0]), .A1(ThisMustBeThePlace_1_a1[2]),
    .G1(ThisMustBeThePlace_1_a1[3]), .E1(ThisMustBeThePlace_1_a1[4]), .D1(ThisMustBeThePlace_1_a1[5]),
    .C1(ThisMustBeThePlace_1_a1[6]), .reset(ThisMustBeThePlace_1_reset));
  MissYou MissYou_1 (
    .Input_1(demultiplexer_1_out5[7]), .Input_2(demultiplexer_1_out5[6]), .Input_3(demultiplexer_1_out5[5]),
    .Input_4(demultiplexer_1_out5[4]), .Input_5(demultiplexer_1_out5[3]), .Input_6(demultiplexer_1_out5[2]),
    .Input_7(demultiplexer_1_out5[1]), .Input_8(demultiplexer_1_out5[0]), .E2(MissYou_1_e2[4]),
    .D2(MissYou_1_e2[5]), .B1(MissYou_1_e2[7]), .A1(MissYou_1_e2[8]), .reset(MissYou_1_reset));
  AnotherBrickInTheWall AnotherBrickInTheWall_1 (
    .Input_1(demultiplexer_1_out6[7]), .Input_2(demultiplexer_1_out6[6]), .Input_3(demultiplexer_1_out6[5]),
    .Input_4(demultiplexer_1_out6[4]), .Input_5(demultiplexer_1_out6[3]), .Input_6(demultiplexer_1_out6[2]),
    .Input_7(demultiplexer_1_out6[1]), .Input_8(demultiplexer_1_out6[0]), .d2(AnotherBrickInTheWall_1_d2[5]),
    .c2(AnotherBrickInTheWall_1_d2[6]), .a1(AnotherBrickInTheWall_1_d2[8]),
    .e1(AnotherBrickInTheWall_1_d2[10]), .reset(AnotherBrickInTheWall_1_reset));
  RappersDelight RappersDelight_1 (
    .Input_1(demultiplexer_1_out7[7]), .Input_2(demultiplexer_1_out7[6]), .Input_3(demultiplexer_1_out7[5]),
    .Input_4(demultiplexer_1_out7[4]), .Input_5(demultiplexer_1_out7[3]), .Input_6(demultiplexer_1_out7[2]),
    .Input_7(demultiplexer_1_out7[1]), .Input_8(demultiplexer_1_out7[0]), .c3(RappersDelight_1_c3[0]),
    .b2(RappersDelight_1_c3[1]), .a2(RappersDelight_1_c3[2]), .g2(RappersDelight_1_c3[3]),
    .e2(RappersDelight_1_c3[4]), .d2(RappersDelight_1_c3[5]), .c2(RappersDelight_1_c3[6]),
    .b1(RappersDelight_1_c3[7]), .a1(RappersDelight_1_c3[8]), .reset(RappersDelight_1_reset));
  Multiplexer #(.select(3), .width(13), .enable("false")) multiplexer_1 (
    .in0({13{1'b0}}),
    .in1({ImperialMarch_1_e2[12], 1'b0, ImperialMarch_1_e2[10:9], 3'b000, ImperialMarch_1_e2[5:4], 4'b0000}),
    .in2(Kalinka_1_output_bus_1), .in3(PirateCaraibe_1_output_bus_1),
    .in4({{6{1'b0}}, ThisMustBeThePlace_1_a1, 2'b00}),
    .in5({4'b0000, MissYou_1_e2[8:7], 1'b0, MissYou_1_e2[5:4], 4'b0000}),
    .in6({2'b00, AnotherBrickInTheWall_1_d2[10], 1'b0, AnotherBrickInTheWall_1_d2[8], 1'b0, AnotherBrickInTheWall_1_d2[6:5], {5{1'b0}}}),
    .in7({4'b0000, RappersDelight_1_c3}), .out(melody), .sel(songcode));
  or or_1 (reset, ImperialMarch_1_reset, Kalinka_1_reset, PirateCaraibe_1_output_1, ThisMustBeThePlace_1_reset, MissYou_1_reset, AnotherBrickInTheWall_1_reset, RappersDelight_1_reset);
endmodule

module FreqToNote (
  input  reset,
  input  clk,
  output [7:0] note
);

  wire [5:0] counter_1_q;

  Counter #(.width(6), .max('h3c)) counter_1 (
    .clr(reset), .count(1'b1), .clk(clk), .Q(counter_1_q));  // open: load, up, D, carry
  assign note = {{2{1'b0}}, counter_1_q};  // Bit_Extender bit_extender_1
endmodule

module NoteControl (
  input  [7:0] frequency,
  input  [12:0] noteCode,
  output outNote
);

  wire and_1_out, and_2_out, and_3_out, and_4_out, and_5_out, and_6_out, and_7_out, and_8_out, and_9_out,
       and_10_out, and_11_out, and_12_out, and_13_out;
  wire [5:0] bit_extender_1_out;

  Bit_Extender #(.out_width(6), .\type ("zero")) bit_extender_1 (.in(frequency), .out(bit_extender_1_out));
  and and_1 (and_1_out, bit_extender_1_out[0], bit_extender_1_out[1], bit_extender_1_out[2], bit_extender_1_out[3], ~bit_extender_1_out[4], ~bit_extender_1_out[5], noteCode[0]);  // AND_Gate
  and and_2 (and_2_out, ~bit_extender_1_out[0], ~bit_extender_1_out[1], ~bit_extender_1_out[2], ~bit_extender_1_out[3], bit_extender_1_out[4], ~bit_extender_1_out[5], noteCode[1]);  // AND_Gate
  and and_3 (and_3_out, ~bit_extender_1_out[0], bit_extender_1_out[1], ~bit_extender_1_out[2], ~bit_extender_1_out[3], bit_extender_1_out[4], ~bit_extender_1_out[5], noteCode[2]);  // AND_Gate
  and and_4 (and_4_out, ~bit_extender_1_out[0], ~bit_extender_1_out[1], bit_extender_1_out[2], ~bit_extender_1_out[3], bit_extender_1_out[4], ~bit_extender_1_out[5], noteCode[3]);  // AND_Gate
  and and_5 (and_5_out, ~bit_extender_1_out[0], ~bit_extender_1_out[1], ~bit_extender_1_out[2], bit_extender_1_out[3], bit_extender_1_out[4], ~bit_extender_1_out[5], noteCode[4]);  // AND_Gate
  and and_6 (and_6_out, bit_extender_1_out[0], bit_extender_1_out[1], ~bit_extender_1_out[2], bit_extender_1_out[3], bit_extender_1_out[4], ~bit_extender_1_out[5], noteCode[5]);  // AND_Gate
  and and_7 (and_7_out, ~bit_extender_1_out[0], bit_extender_1_out[1], bit_extender_1_out[2], bit_extender_1_out[3], bit_extender_1_out[4], ~bit_extender_1_out[5], noteCode[6]);  // AND_Gate
  and and_8 (and_8_out, ~bit_extender_1_out[0], ~bit_extender_1_out[1], ~bit_extender_1_out[2], ~bit_extender_1_out[3], ~bit_extender_1_out[4], bit_extender_1_out[5], noteCode[7]);  // AND_Gate
  and and_9 (and_9_out, ~bit_extender_1_out[0], ~bit_extender_1_out[1], bit_extender_1_out[2], ~bit_extender_1_out[3], ~bit_extender_1_out[4], bit_extender_1_out[5], noteCode[8]);  // AND_Gate
  and and_10 (and_10_out, ~bit_extender_1_out[0], ~bit_extender_1_out[1], ~bit_extender_1_out[2], bit_extender_1_out[3], ~bit_extender_1_out[4], bit_extender_1_out[5], noteCode[9]);  // AND_Gate
  and and_11 (and_11_out, ~bit_extender_1_out[0], ~bit_extender_1_out[1], ~bit_extender_1_out[2], ~bit_extender_1_out[3], bit_extender_1_out[4], bit_extender_1_out[5], noteCode[10]);  // AND_Gate
  and and_12 (and_12_out, ~bit_extender_1_out[0], bit_extender_1_out[1], bit_extender_1_out[2], ~bit_extender_1_out[3], bit_extender_1_out[4], bit_extender_1_out[5], noteCode[11]);  // AND_Gate
  and and_13 (and_13_out, ~bit_extender_1_out[0], ~bit_extender_1_out[1], bit_extender_1_out[2], bit_extender_1_out[3], bit_extender_1_out[4], bit_extender_1_out[5], noteCode[12]);  // AND_Gate
  or or_1 (outNote, and_1_out, and_2_out, and_3_out, and_4_out, and_5_out, and_6_out, and_7_out, and_8_out, and_9_out, and_10_out, and_11_out, and_12_out, and_13_out);
endmodule

module BeatManager (
  input  start,
  input  clk,
  input  reset,
  output [7:0] beat
);

  wire Double_croche_150ms_carry, Mesure_1_o0, Mesure_1_o1, Mesure_1_o2, Mesure_1_o3, Mesure_1_o4,
       Mesure_1_o5, Mesure_1_o6, Mesure_1_o7;
  wire [11:0] Double_croche_150ms_q;

  Counter #(.width(12), .max('h9c4)) Double_croche_150ms (
    .clr(reset), .count(start), .clk(clk), .carry(Double_croche_150ms_carry), .Q(Double_croche_150ms_q));  // open: load, up, D
  Mesure Mesure_1 (
    .CarryIn(Double_croche_150ms_carry), .b7(beat[7]), .b6(beat[6]), .b5(beat[5]), .b4(beat[4]),
    .b3(beat[3]), .b2(beat[2]), .b1(beat[1]), .b0(beat[0]), .o7(Mesure_1_o7), .o6(Mesure_1_o6),
    .o5(Mesure_1_o5), .o4(Mesure_1_o4), .o3(Mesure_1_o3), .o2(Mesure_1_o2), .o1(Mesure_1_o1), .o0(Mesure_1_o0));
  D_Flip_Flop d_ff_1 (.D(Mesure_1_o7), .clk(clk), .Q(beat[7]), .reset(reset));  // open: Qn, preset
  D_Flip_Flop d_ff_2 (.D(Mesure_1_o6), .clk(clk), .Q(beat[6]), .reset(reset));  // open: Qn, preset
  D_Flip_Flop d_ff_3 (.D(Mesure_1_o5), .clk(clk), .Q(beat[5]), .reset(reset));  // open: Qn, preset
  D_Flip_Flop d_ff_4 (.D(Mesure_1_o4), .clk(clk), .Q(beat[4]), .reset(reset));  // open: Qn, preset
  D_Flip_Flop d_ff_5 (.D(Mesure_1_o3), .clk(clk), .Q(beat[3]), .reset(reset));  // open: Qn, preset
  D_Flip_Flop d_ff_6 (.D(Mesure_1_o2), .clk(clk), .Q(beat[2]), .reset(reset));  // open: Qn, preset
  D_Flip_Flop d_ff_7 (.D(Mesure_1_o1), .clk(clk), .Q(beat[1]), .reset(reset));  // open: Qn, preset
  D_Flip_Flop d_ff_8 (.D(Mesure_1_o0), .clk(clk), .Q(beat[0]), .reset(reset));  // open: Qn, preset
endmodule

module Mesure (
  input  CarryIn,
  input  b7,
  input  b6,
  input  b5,
  input  b4,
  input  b3,
  input  b2,
  input  b1,
  input  b0,
  output o7,
  output o6,
  output o5,
  output o4,
  output o3,
  output o2,
  output o1,
  output o0
);

  wire and_1_out, and_2_out, and_3_out, and_4_out, and_5_out, and_6_out, and_7_out, and_8_out, and_9_out,
       and_10_out, and_11_out, and_12_out, and_13_out, and_14_out, and_15_out, and_16_out, and_17_out,
       and_18_out, and_19_out, and_20_out, and_21_out, and_22_out, and_23_out, and_24_out, and_25_out,
       and_26_out, and_27_out, and_28_out, and_29_out, and_30_out, and_31_out, and_32_out, and_33_out,
       and_34_out, and_35_out, and_36_out, and_37_out, and_38_out, and_39_out, and_40_out, and_41_out,
       and_42_out, and_43_out, and_44_out, not_1_out, not_2_out, not_3_out, not_4_out, not_5_out, not_6_out,
       not_7_out, not_8_out, not_9_out, not_10_out, not_11_out, not_12_out, not_13_out, not_14_out,
       not_15_out, not_16_out, not_17_out, not_18_out, not_19_out, not_20_out, not_21_out, not_22_out,
       not_23_out, not_24_out, not_25_out, not_26_out, not_27_out, not_28_out, not_29_out, not_30_out,
       not_31_out, not_32_out, not_33_out, not_34_out, not_35_out, not_36_out, not_37_out, not_38_out,
       not_39_out, not_40_out, not_41_out, not_42_out, not_43_out, not_44_out;

  not not_1 (not_1_out, CarryIn);
  not not_2 (not_2_out, b6);
  not not_3 (not_3_out, b5);
  not not_4 (not_4_out, b4);
  not not_5 (not_5_out, b3);
  not not_6 (not_6_out, b2);
  not not_7 (not_7_out, b1);
  not not_8 (not_8_out, b0);
  not not_9 (not_9_out, b7);
  not not_10 (not_10_out, CarryIn);
  not not_11 (not_11_out, b5);
  not not_12 (not_12_out, b4);
  not not_13 (not_13_out, b3);
  not not_14 (not_14_out, b2);
  not not_15 (not_15_out, b1);
  not not_16 (not_16_out, b0);
  not not_17 (not_17_out, b6);
  not not_18 (not_18_out, CarryIn);
  not not_19 (not_19_out, b4);
  not not_20 (not_20_out, b3);
  not not_21 (not_21_out, b2);
  not not_22 (not_22_out, b1);
  not not_23 (not_23_out, b0);
  not not_24 (not_24_out, b5);
  not not_25 (not_25_out, CarryIn);
  not not_26 (not_26_out, b3);
  not not_27 (not_27_out, b2);
  not not_28 (not_28_out, b1);
  not not_29 (not_29_out, b0);
  not not_30 (not_30_out, b4);
  not not_31 (not_31_out, CarryIn);
  not not_32 (not_32_out, b2);
  not not_33 (not_33_out, b1);
  not not_34 (not_34_out, b0);
  not not_35 (not_35_out, b3);
  not not_36 (not_36_out, CarryIn);
  not not_37 (not_37_out, b1);
  not not_38 (not_38_out, b0);
  not not_39 (not_39_out, b2);
  not not_40 (not_40_out, CarryIn);
  not not_41 (not_41_out, b0);
  not not_42 (not_42_out, b1);
  not not_43 (not_43_out, CarryIn);
  not not_44 (not_44_out, b0);
  and and_1 (and_1_out, not_1_out, b7);
  and and_2 (and_2_out, b7, not_2_out);
  and and_3 (and_3_out, b7, not_3_out);
  and and_4 (and_4_out, b7, not_4_out);
  and and_5 (and_5_out, b7, not_5_out);
  and and_6 (and_6_out, b7, not_6_out);
  and and_7 (and_7_out, b7, not_7_out);
  and and_8 (and_8_out, b7, not_8_out);
  and and_9 (and_9_out, CarryIn, not_9_out, b6, b5, b4, b3, b2, b1, b0);
  and and_10 (and_10_out, not_10_out, b6);
  and and_11 (and_11_out, b6, not_11_out);
  and and_12 (and_12_out, b6, not_12_out);
  and and_13 (and_13_out, b6, not_13_out);
  and and_14 (and_14_out, b6, not_14_out);
  and and_15 (and_15_out, b6, not_15_out);
  and and_16 (and_16_out, b6, not_16_out);
  and and_17 (and_17_out, CarryIn, not_17_out, b5, b4, b3, b2, b1, b0);
  and and_18 (and_18_out, not_18_out, b5);
  and and_19 (and_19_out, b5, not_19_out);
  and and_20 (and_20_out, b5, not_20_out);
  and and_21 (and_21_out, b5, not_21_out);
  and and_22 (and_22_out, b5, not_22_out);
  and and_23 (and_23_out, b5, not_23_out);
  and and_24 (and_24_out, CarryIn, not_24_out, b4, b3, b2, b1, b0);
  and and_25 (and_25_out, not_25_out, b4);
  and and_26 (and_26_out, b4, not_26_out);
  and and_27 (and_27_out, b4, not_27_out);
  and and_28 (and_28_out, b4, not_28_out);
  and and_29 (and_29_out, b4, not_29_out);
  and and_30 (and_30_out, CarryIn, not_30_out, b3, b2, b1, b0);
  and and_31 (and_31_out, not_31_out, b3);
  and and_32 (and_32_out, b3, not_32_out);
  and and_33 (and_33_out, b3, not_33_out);
  and and_34 (and_34_out, b3, not_34_out);
  and and_35 (and_35_out, CarryIn, not_35_out, b2, b1, b0);
  and and_36 (and_36_out, not_36_out, b2);
  and and_37 (and_37_out, b2, not_37_out);
  and and_38 (and_38_out, b2, not_38_out);
  and and_39 (and_39_out, CarryIn, not_39_out, b1, b0);
  and and_40 (and_40_out, not_40_out, b1);
  and and_41 (and_41_out, b1, not_41_out);
  and and_42 (and_42_out, CarryIn, not_42_out, b0);
  and and_43 (and_43_out, not_43_out, b0);
  and and_44 (and_44_out, CarryIn, not_44_out);
  or or_1 (o7, and_1_out, and_2_out, and_3_out, and_4_out, and_5_out, and_6_out, and_7_out, and_8_out, and_9_out);
  or or_2 (o6, and_10_out, and_11_out, and_12_out, and_13_out, and_14_out, and_15_out, and_16_out, and_17_out);
  or or_3 (o5, and_18_out, and_19_out, and_20_out, and_21_out, and_22_out, and_23_out, and_24_out);
  or or_4 (o4, and_25_out, and_26_out, and_27_out, and_28_out, and_29_out, and_30_out);
  or or_5 (o3, and_31_out, and_32_out, and_33_out, and_34_out, and_35_out);
  or or_6 (o2, and_36_out, and_37_out, and_38_out, and_39_out);
  or or_7 (o1, and_40_out, and_41_out, and_42_out);
  or or_8 (o0, and_43_out, and_44_out);
endmodule

module ImperialMarch (
  input  Input_1,
  input  Input_2,
  input  Input_3,
  input  Input_4,
  input  Input_5,
  input  Input_6,
  input  Input_7,
  input  Input_8,
  output e2,
  output d2,
  output g1,
  output e1,
  output c1,
  output reset
);

  wire and_1_out, and_2_out, and_3_out, and_4_out, and_5_out, and_6_out, and_7_out, and_8_out, and_9_out,
       and_10_out, and_11_out, and_12_out, and_13_out, and_14_out, and_15_out, and_16_out, and_17_out,
       and_18_out, and_19_out, and_20_out, and_21_out, and_22_out, and_23_out, and_24_out, and_25_out,
       and_26_out, and_27_out, and_28_out, and_29_out, and_30_out, and_31_out, and_32_out, and_33_out,
       and_34_out, and_35_out, and_36_out, and_37_out, and_38_out, and_39_out, and_40_out, and_41_out,
       not_1_out, not_2_out, not_3_out, not_4_out, not_5_out, not_6_out, not_7_out, not_8_out, not_9_out,
       not_10_out, not_11_out, not_12_out, not_13_out, not_14_out, not_15_out, not_16_out, not_17_out,
       not_18_out, not_19_out, not_20_out, not_21_out, not_22_out, not_23_out, not_24_out, not_25_out,
       not_26_out, not_27_out, not_28_out, not_29_out, not_30_out, not_31_out, not_32_out, not_33_out,
       not_34_out, not_35_out, not_36_out, not_37_out, not_38_out, not_39_out, not_40_out, not_41_out,
       not_42_out, not_43_out, not_44_out, not_45_out, not_46_out, not_47_out, not_48_out, not_49_out,
       not_50_out, not_51_out, not_52_out, not_53_out, not_54_out, not_55_out, not_56_out, not_57_out,
       not_58_out, not_59_out, not_60_out, not_61_out, not_62_out, not_63_out, not_64_out, not_65_out,
       not_66_out, not_67_out, not_68_out, not_69_out, not_70_out, not_71_out, not_72_out, not_73_out,
       not_74_out, not_75_out, not_76_out, not_77_out, not_78_out, not_79_out, not_80_out, not_81_out,
       not_82_out, not_83_out, not_84_out, not_85_out, not_86_out, not_87_out, not_88_out, not_89_out,
       not_90_out, not_91_out, not_92_out, not_93_out, not_94_out, not_95_out, not_96_out, not_97_out,
       not_98_out, not_99_out, not_100_out, not_101_out, not_102_out, not_103_out, not_104_out, not_105_out,
       not_106_out, not_107_out, not_108_out, not_109_out, not_110_out, not_111_out, not_112_out,
       not_113_out, not_114_out, not_115_out, not_116_out, not_117_out, not_118_out, not_119_out,
       not_120_out, not_121_out, not_122_out, not_123_out, not_124_out, not_125_out, not_126_out,
       not_127_out, not_128_out, not_129_out, not_130_out, not_131_out, not_132_out, not_133_out,
       not_134_out, not_135_out, not_136_out, not_137_out, not_138_out, not_139_out;

  not not_1 (not_1_out, Input_1);
  not not_2 (not_2_out, Input_2);
  not not_3 (not_3_out, Input_4);
  not not_4 (not_4_out, Input_7);
  not not_5 (not_5_out, Input_1);
  not not_6 (not_6_out, Input_2);
  not not_7 (not_7_out, Input_4);
  not not_8 (not_8_out, Input_8);
  not not_9 (not_9_out, Input_1);
  not not_10 (not_10_out, Input_5);
  not not_11 (not_11_out, Input_2);
  not not_12 (not_12_out, Input_5);
  not not_13 (not_13_out, Input_1);
  not not_14 (not_14_out, Input_2);
  not not_15 (not_15_out, Input_4);
  not not_16 (not_16_out, Input_5);
  not not_17 (not_17_out, Input_7);
  not not_18 (not_18_out, Input_1);
  not not_19 (not_19_out, Input_2);
  not not_20 (not_20_out, Input_4);
  not not_21 (not_21_out, Input_5);
  not not_22 (not_22_out, Input_8);
  not not_23 (not_23_out, Input_1);
  not not_24 (not_24_out, Input_2);
  not not_25 (not_25_out, Input_4);
  not not_26 (not_26_out, Input_6);
  not not_27 (not_27_out, Input_7);
  not not_28 (not_28_out, Input_1);
  not not_29 (not_29_out, Input_2);
  not not_30 (not_30_out, Input_4);
  not not_31 (not_31_out, Input_6);
  not not_32 (not_32_out, Input_8);
  not not_33 (not_33_out, Input_1);
  not not_34 (not_34_out, Input_3);
  not not_35 (not_35_out, Input_5);
  not not_36 (not_36_out, Input_1);
  not not_37 (not_37_out, Input_4);
  not not_38 (not_38_out, Input_5);
  not not_39 (not_39_out, Input_2);
  not not_40 (not_40_out, Input_3);
  not not_41 (not_41_out, Input_5);
  not not_42 (not_42_out, Input_2);
  not not_43 (not_43_out, Input_4);
  not not_44 (not_44_out, Input_5);
  not not_45 (not_45_out, Input_1);
  not not_46 (not_46_out, Input_2);
  not not_47 (not_47_out, Input_4);
  not not_48 (not_48_out, Input_1);
  not not_49 (not_49_out, Input_2);
  not not_50 (not_50_out, Input_5);
  not not_51 (not_51_out, Input_4);
  not not_52 (not_52_out, Input_5);
  not not_53 (not_53_out, Input_1);
  not not_54 (not_54_out, Input_2);
  not not_55 (not_55_out, Input_3);
  not not_56 (not_56_out, Input_4);
  not not_57 (not_57_out, Input_5);
  not not_58 (not_58_out, Input_7);
  not not_59 (not_59_out, Input_1);
  not not_60 (not_60_out, Input_2);
  not not_61 (not_61_out, Input_3);
  not not_62 (not_62_out, Input_4);
  not not_63 (not_63_out, Input_5);
  not not_64 (not_64_out, Input_8);
  not not_65 (not_65_out, Input_2);
  not not_66 (not_66_out, Input_3);
  not not_67 (not_67_out, Input_6);
  not not_68 (not_68_out, Input_7);
  not not_69 (not_69_out, Input_1);
  not not_70 (not_70_out, Input_3);
  not not_71 (not_71_out, Input_6);
  not not_72 (not_72_out, Input_8);
  not not_73 (not_73_out, Input_1);
  not not_74 (not_74_out, Input_2);
  not not_75 (not_75_out, Input_6);
  not not_76 (not_76_out, Input_7);
  not not_77 (not_77_out, Input_1);
  not not_78 (not_78_out, Input_2);
  not not_79 (not_79_out, Input_6);
  not not_80 (not_80_out, Input_8);
  not not_81 (not_81_out, Input_1);
  not not_82 (not_82_out, Input_3);
  not not_83 (not_83_out, Input_6);
  not not_84 (not_84_out, Input_7);
  not not_85 (not_85_out, Input_1);
  not not_86 (not_86_out, Input_2);
  not not_87 (not_87_out, Input_6);
  not not_88 (not_88_out, Input_1);
  not not_89 (not_89_out, Input_2);
  not not_90 (not_90_out, Input_7);
  not not_91 (not_91_out, Input_3);
  not not_92 (not_92_out, Input_6);
  not not_93 (not_93_out, Input_3);
  not not_94 (not_94_out, Input_8);
  not not_95 (not_95_out, Input_1);
  not not_96 (not_96_out, Input_3);
  not not_97 (not_97_out, Input_6);
  not not_98 (not_98_out, Input_1);
  not not_99 (not_99_out, Input_3);
  not not_100 (not_100_out, Input_1);
  not not_101 (not_101_out, Input_4);
  not not_102 (not_102_out, Input_5);
  not not_103 (not_103_out, Input_6);
  not not_104 (not_104_out, Input_2);
  not not_105 (not_105_out, Input_3);
  not not_106 (not_106_out, Input_6);
  not not_107 (not_107_out, Input_2);
  not not_108 (not_108_out, Input_4);
  not not_109 (not_109_out, Input_5);
  not not_110 (not_110_out, Input_6);
  not not_111 (not_111_out, Input_3);
  not not_112 (not_112_out, Input_1);
  not not_113 (not_113_out, Input_2);
  not not_114 (not_114_out, Input_3);
  not not_115 (not_115_out, Input_4);
  not not_116 (not_116_out, Input_7);
  not not_117 (not_117_out, Input_1);
  not not_118 (not_118_out, Input_2);
  not not_119 (not_119_out, Input_3);
  not not_120 (not_120_out, Input_4);
  not not_121 (not_121_out, Input_8);
  not not_122 (not_122_out, Input_1);
  not not_123 (not_123_out, Input_2);
  not not_124 (not_124_out, Input_5);
  not not_125 (not_125_out, Input_7);
  not not_126 (not_126_out, Input_1);
  not not_127 (not_127_out, Input_2);
  not not_128 (not_128_out, Input_5);
  not not_129 (not_129_out, Input_8);
  not not_130 (not_130_out, Input_1);
  not not_131 (not_131_out, Input_4);
  not not_132 (not_132_out, Input_1);
  not not_133 (not_133_out, Input_5);
  not not_134 (not_134_out, Input_6);
  not not_135 (not_135_out, Input_2);
  not not_136 (not_136_out, Input_4);
  not not_137 (not_137_out, Input_2);
  not not_138 (not_138_out, Input_5);
  not not_139 (not_139_out, Input_6);
  and and_1 (and_1_out, not_1_out, not_2_out, Input_3, not_3_out, Input_5, Input_6, not_4_out);
  and and_2 (and_2_out, not_5_out, not_6_out, Input_3, not_7_out, Input_5, Input_6, not_8_out);
  and and_3 (and_3_out, not_9_out, Input_2, Input_3, Input_4, not_10_out, Input_6);
  and and_4 (and_4_out, Input_1, not_11_out, Input_3, Input_4, not_12_out, Input_6);
  and and_5 (and_5_out, not_13_out, not_14_out, Input_3, not_15_out, not_16_out, not_17_out);
  and and_6 (and_6_out, not_18_out, not_19_out, Input_3, not_20_out, not_21_out, not_22_out);
  and and_7 (and_7_out, not_23_out, not_24_out, Input_3, not_25_out, not_26_out, not_27_out);
  and and_8 (and_8_out, not_28_out, not_29_out, Input_3, not_30_out, not_31_out, not_32_out);
  and and_9 (and_9_out, not_33_out, Input_2, not_34_out, not_35_out, Input_6);
  and and_10 (and_10_out, not_36_out, Input_2, not_37_out, not_38_out, Input_6);
  and and_11 (and_11_out, Input_1, not_39_out, not_40_out, not_41_out, Input_6);
  and and_12 (and_12_out, Input_1, not_42_out, not_43_out, not_44_out, Input_6);
  and and_13 (and_13_out, not_45_out, not_46_out, not_47_out, Input_5, Input_6, Input_7, Input_8);
  and and_14 (and_14_out, not_48_out, not_49_out, Input_4, not_50_out, Input_6, Input_7, Input_8);
  and and_15 (and_15_out, Input_1, Input_2, Input_3, not_51_out, Input_5);
  and and_16 (and_16_out, Input_1, Input_2, Input_3, Input_4, not_52_out);
  and and_17 (and_17_out, not_53_out, not_54_out, not_55_out, not_56_out, not_57_out, not_58_out);
  and and_18 (and_18_out, not_59_out, not_60_out, not_61_out, not_62_out, not_63_out, not_64_out);
  and and_19 (and_19_out, not_65_out, not_66_out, not_67_out, not_68_out);
  and and_20 (and_20_out, not_69_out, not_70_out, not_71_out, Input_7, not_72_out);
  and and_21 (and_21_out, not_73_out, not_74_out, Input_4, not_75_out, not_76_out);
  and and_22 (and_22_out, not_77_out, not_78_out, Input_4, not_79_out, not_80_out);
  and and_23 (and_23_out, not_81_out, not_82_out, Input_4, not_83_out, not_84_out);
  and and_24 (and_24_out, not_85_out, not_86_out, Input_4, Input_5, not_87_out);
  and and_25 (and_25_out, not_88_out, not_89_out, Input_4, Input_5, not_90_out);
  and and_26 (and_26_out, not_91_out, Input_4, Input_5, not_92_out);
  and and_27 (and_27_out, not_93_out, Input_4, Input_5, not_94_out);
  and and_28 (and_28_out, not_95_out, Input_2, not_96_out, not_97_out, Input_8);
  and and_29 (and_29_out, not_98_out, Input_2, not_99_out, Input_5);
  and and_30 (and_30_out, not_100_out, Input_2, Input_3, not_101_out, not_102_out, not_103_out);
  and and_31 (and_31_out, Input_1, not_104_out, not_105_out, not_106_out);
  and and_32 (and_32_out, Input_1, not_107_out, not_108_out, not_109_out, not_110_out);
  and and_33 (and_33_out, Input_1, not_111_out, Input_5, Input_6);
  and and_34 (and_34_out, not_112_out, not_113_out, not_114_out, not_115_out, Input_5, Input_6, not_116_out);
  and and_35 (and_35_out, not_117_out, not_118_out, not_119_out, not_120_out, Input_5, Input_6, not_121_out);
  and and_36 (and_36_out, not_122_out, not_123_out, Input_4, not_124_out, Input_6, not_125_out);
  and and_37 (and_37_out, not_126_out, not_127_out, Input_4, not_128_out, Input_6, not_129_out);
  and and_38 (and_38_out, not_130_out, Input_2, Input_3, not_131_out, Input_5);
  and and_39 (and_39_out, not_132_out, Input_2, Input_3, Input_4, not_133_out, not_134_out);
  and and_40 (and_40_out, Input_1, not_135_out, Input_3, not_136_out, Input_5);
  and and_41 (and_41_out, Input_1, not_137_out, Input_3, Input_4, not_138_out, not_139_out);
  or or_1 (e2, and_1_out, and_2_out, and_3_out, and_4_out);
  or or_2 (d2, and_5_out, and_6_out, and_7_out, and_8_out, and_9_out, and_10_out, and_11_out, and_12_out);
  or or_3 (g1, and_13_out, and_14_out, and_15_out, and_16_out);
  or or_4 (c1, and_34_out, and_35_out, and_36_out, and_37_out, and_38_out, and_39_out, and_40_out, and_41_out);
  or or_5 (e1, and_17_out, and_18_out, and_19_out, and_20_out, and_21_out, and_22_out, and_23_out, and_24_out, and_25_out, and_26_out, and_27_out, and_28_out, and_29_out, and_30_out, and_31_out, and_32_out, and_33_out);

  assign reset = Input_2;
endmodule

module Kalinka (
  input  Input_1,
  input  Input_2,
  input  Input_3,
  input  Input_4,
  input  Input_5,
  input  Input_6,
  input  Input_7,
  input  Input_8,
  output [12:0] Output_bus_1,
  output reset
);

  wire and_2_out, and_3_out, and_4_out, and_5_out, and_6_out, and_7_out, and_8_out, and_9_out, and_10_out,
       and_11_out, and_12_out, and_13_out, and_14_out, and_15_out, and_16_out, and_17_out, and_18_out,
       and_19_out, and_20_out, and_21_out, and_22_out, and_23_out, and_24_out, and_25_out, and_26_out,
       and_27_out, and_28_out, and_29_out, not_1_out, not_2_out, not_3_out, not_4_out, not_5_out, not_6_out,
       not_7_out, not_8_out, not_9_out, not_10_out, not_11_out, not_12_out, not_13_out, not_14_out,
       not_15_out, not_16_out, not_17_out, not_18_out, not_19_out, not_20_out, not_21_out, not_22_out,
       not_23_out, not_24_out, not_25_out, not_26_out, not_27_out, not_28_out, not_29_out, not_30_out,
       not_31_out, not_32_out, not_33_out, not_34_out, not_35_out, not_36_out, not_37_out, not_38_out,
       not_39_out, not_40_out, not_41_out, not_42_out, not_43_out, not_44_out, not_45_out, not_46_out,
       not_47_out, not_48_out, not_49_out, not_50_out, not_51_out, not_52_out, not_53_out, not_54_out,
       not_55_out, not_56_out, not_57_out, not_58_out, not_59_out, not_60_out;

  not not_1 (not_1_out, Input_3);
  not not_2 (not_2_out, Input_4);
  not not_3 (not_3_out, Input_5);
  not not_4 (not_4_out, Input_4);
  not not_5 (not_5_out, Input_6);
  not not_6 (not_6_out, Input_2);
  not not_7 (not_7_out, Input_3);
  not not_8 (not_8_out, Input_4);
  not not_9 (not_9_out, Input_6);
  not not_10 (not_10_out, Input_6);
  not not_11 (not_11_out, Input_2);
  not not_12 (not_12_out, Input_3);
  not not_13 (not_13_out, Input_6);
  not not_14 (not_14_out, Input_2);
  not not_15 (not_15_out, Input_4);
  not not_16 (not_16_out, Input_6);
  not not_17 (not_17_out, Input_2);
  not not_18 (not_18_out, Input_7);
  not not_19 (not_19_out, Input_4);
  not not_20 (not_20_out, Input_5);
  not not_21 (not_21_out, Input_2);
  not not_22 (not_22_out, Input_3);
  not not_23 (not_23_out, Input_4);
  not not_24 (not_24_out, Input_5);
  not not_25 (not_25_out, Input_2);
  not not_26 (not_26_out, Input_3);
  not not_27 (not_27_out, Input_2);
  not not_28 (not_28_out, Input_4);
  not not_29 (not_29_out, Input_2);
  not not_30 (not_30_out, Input_6);
  not not_31 (not_31_out, Input_4);
  not not_32 (not_32_out, Input_5);
  not not_33 (not_33_out, Input_7);
  not not_34 (not_34_out, Input_2);
  not not_35 (not_35_out, Input_3);
  not not_36 (not_36_out, Input_4);
  not not_37 (not_37_out, Input_5);
  not not_38 (not_38_out, Input_7);
  not not_39 (not_39_out, Input_6);
  not not_40 (not_40_out, Input_5);
  not not_41 (not_41_out, Input_7);
  not not_42 (not_42_out, Input_2);
  not not_43 (not_43_out, Input_5);
  not not_44 (not_44_out, Input_2);
  not not_45 (not_45_out, Input_5);
  not not_46 (not_46_out, Input_5);
  not not_47 (not_47_out, Input_6);
  not not_48 (not_48_out, Input_6);
  not not_49 (not_49_out, Input_2);
  not not_50 (not_50_out, Input_5);
  not not_51 (not_51_out, Input_6);
  not not_52 (not_52_out, Input_1);
  not not_53 (not_53_out, Input_2);
  not not_54 (not_54_out, Input_3);
  not not_55 (not_55_out, Input_4);
  not not_56 (not_56_out, Input_3);
  not not_57 (not_57_out, Input_4);
  not not_58 (not_58_out, Input_3);
  not not_59 (not_59_out, Input_4);
  not not_60 (not_60_out, Input_4);
  and and_1 (reset, Input_1, Input_5, Input_6);
  and and_2 (and_2_out, Input_2, not_1_out, not_2_out, not_3_out);
  and and_3 (and_3_out, Input_2, Input_3, not_4_out, Input_5, not_5_out);
  and and_4 (and_4_out, Input_1, not_6_out, not_7_out, not_8_out, Input_5, not_9_out);
  and and_5 (and_5_out, Input_1, Input_2, Input_3, Input_5, not_10_out);
  and and_6 (and_6_out, not_11_out, not_12_out, Input_4, Input_5, not_13_out);
  and and_7 (and_7_out, not_14_out, Input_3, not_15_out, Input_5, not_16_out);
  and and_8 (and_8_out, not_17_out, Input_3, Input_4, Input_5, Input_6);
  and and_9 (and_9_out, Input_2, Input_4, Input_6, not_18_out);
  and and_10 (and_10_out, Input_2, Input_3, not_19_out, not_20_out, Input_6, Input_7);
  and and_11 (and_11_out, Input_1, not_21_out, not_22_out, not_23_out, not_24_out, Input_6, Input_7);
  and and_12 (and_12_out, Input_1, Input_2, Input_3, Input_4, Input_6);
  and and_13 (and_13_out, not_25_out, not_26_out, Input_4, Input_5, Input_6);
  and and_14 (and_14_out, not_27_out, Input_3, not_28_out, Input_5, Input_6);
  and and_15 (and_15_out, not_29_out, Input_3, Input_4, Input_5, not_30_out);
  and and_16 (and_16_out, Input_2, Input_4, Input_6, Input_7);
  and and_17 (and_17_out, Input_2, Input_3, not_31_out, not_32_out, Input_6, not_33_out);
  and and_18 (and_18_out, Input_1, not_34_out, not_35_out, not_36_out, not_37_out, Input_6, not_38_out);
  and and_19 (and_19_out, Input_1, Input_3, Input_4, Input_5, not_39_out);
  and and_20 (and_20_out, Input_1, Input_2, Input_3, not_40_out, Input_6, not_41_out);
  and and_21 (and_21_out, not_42_out, Input_4, not_43_out);
  and and_22 (and_22_out, not_44_out, Input_3, not_45_out);
  and and_23 (and_23_out, Input_3, not_46_out, not_47_out);
  and and_24 (and_24_out, Input_2, Input_4, not_48_out);
  and and_25 (and_25_out, Input_1, not_49_out, not_50_out, not_51_out);
  and and_26 (and_26_out, not_52_out, not_53_out, not_54_out, not_55_out);
  and and_27 (and_27_out, not_56_out, not_57_out, Input_5, Input_6, Input_7);
  and and_28 (and_28_out, Input_2, not_58_out, not_59_out, Input_5);
  and and_29 (and_29_out, Input_2, not_60_out, Input_5, Input_6);
  or or_1 (Output_bus_1[8], and_2_out, and_3_out, and_4_out, and_5_out);
  or or_2 (Output_bus_1[5], and_21_out, and_22_out, and_23_out, and_24_out, and_25_out);
  or or_3 (Output_bus_1[4], and_26_out, and_27_out, and_28_out, and_29_out);
  or or_4 (Output_bus_1[7], and_6_out, and_7_out, and_8_out, and_9_out, and_10_out, and_11_out, and_12_out);
  or or_5 (Output_bus_1[6], and_13_out, and_14_out, and_15_out, and_16_out, and_17_out, and_18_out, and_19_out, and_20_out);

  assign {Output_bus_1[12:9], Output_bus_1[3:0]} = {8{1'b0}};
endmodule

module PirateCaraibe (
  input  Input_1,
  input  Input_2,
  input  Input_3,
  input  Input_4,
  input  Input_5,
  input  Input_6,
  input  Input_7,
  input  Input_8,
  output [12:0] Output_bus_1,
  output Output_1
);

  wire and_2_out, and_3_out, and_4_out, and_5_out, and_6_out, and_7_out, and_8_out, and_9_out, and_10_out,
       and_11_out, and_12_out, and_13_out, and_14_out, and_15_out, and_16_out, and_17_out, and_18_out,
       and_19_out, and_20_out, and_21_out, and_22_out, and_23_out, and_24_out, and_25_out, and_26_out,
       and_27_out, and_28_out, and_29_out, and_30_out, and_31_out, and_32_out, and_33_out, and_34_out,
       and_35_out, and_36_out, not_1_out, not_2_out, not_3_out, not_4_out, not_5_out, not_6_out, not_7_out,
       not_8_out, not_9_out, not_10_out, not_11_out, not_12_out, not_13_out, not_14_out, not_15_out,
       not_16_out, not_17_out, not_18_out, not_19_out, not_20_out, not_21_out, not_22_out, not_23_out,
       not_24_out, not_25_out, not_26_out, not_27_out, not_28_out, not_29_out, not_30_out, not_31_out,
       not_32_out, not_33_out, not_34_out, not_35_out, not_36_out, not_37_out, not_38_out, not_39_out,
       not_40_out, not_41_out, not_42_out, not_43_out, not_44_out, not_45_out, not_46_out, not_47_out,
       not_48_out, not_49_out, not_50_out, not_51_out, not_52_out, not_53_out, not_54_out, not_55_out,
       not_56_out, not_57_out, not_58_out, not_59_out, not_60_out, not_61_out, not_62_out, not_63_out,
       not_64_out, not_65_out, not_66_out, not_67_out, not_68_out, not_69_out, not_70_out, not_71_out,
       not_72_out, not_73_out, not_74_out, not_75_out, not_76_out, not_77_out, not_78_out, not_79_out,
       not_80_out, not_81_out, not_82_out, not_83_out, not_84_out, not_85_out, not_86_out, not_87_out,
       not_88_out, not_89_out, not_90_out, not_91_out, not_92_out, not_93_out;

  not not_1 (not_1_out, Input_2);
  not not_2 (not_2_out, Input_3);
  not not_3 (not_3_out, Input_4);
  not not_4 (not_4_out, Input_6);
  not not_5 (not_5_out, Input_7);
  not not_6 (not_6_out, Input_8);
  not not_7 (not_7_out, Input_5);
  not not_8 (not_8_out, Input_7);
  not not_9 (not_9_out, Input_2);
  not not_10 (not_10_out, Input_3);
  not not_11 (not_11_out, Input_4);
  not not_12 (not_12_out, Input_6);
  not not_13 (not_13_out, Input_8);
  not not_14 (not_14_out, Input_4);
  not not_15 (not_15_out, Input_5);
  not not_16 (not_16_out, Input_6);
  not not_17 (not_17_out, Input_7);
  not not_18 (not_18_out, Input_2);
  not not_19 (not_19_out, Input_3);
  not not_20 (not_20_out, Input_5);
  not not_21 (not_21_out, Input_6);
  not not_22 (not_22_out, Input_7);
  not not_23 (not_23_out, Input_2);
  not not_24 (not_24_out, Input_3);
  not not_25 (not_25_out, Input_5);
  not not_26 (not_26_out, Input_6);
  not not_27 (not_27_out, Input_8);
  not not_28 (not_28_out, Input_2);
  not not_29 (not_29_out, Input_3);
  not not_30 (not_30_out, Input_5);
  not not_31 (not_31_out, Input_7);
  not not_32 (not_32_out, Input_8);
  not not_33 (not_33_out, Input_3);
  not not_34 (not_34_out, Input_4);
  not not_35 (not_35_out, Input_5);
  not not_36 (not_36_out, Input_6);
  not not_37 (not_37_out, Input_7);
  not not_38 (not_38_out, Input_2);
  not not_39 (not_39_out, Input_3);
  not not_40 (not_40_out, Input_4);
  not not_41 (not_41_out, Input_8);
  not not_42 (not_42_out, Input_2);
  not not_43 (not_43_out, Input_3);
  not not_44 (not_44_out, Input_4);
  not not_45 (not_45_out, Input_7);
  not not_46 (not_46_out, Input_3);
  not not_47 (not_47_out, Input_5);
  not not_48 (not_48_out, Input_8);
  not not_49 (not_49_out, Input_2);
  not not_50 (not_50_out, Input_4);
  not not_51 (not_51_out, Input_5);
  not not_52 (not_52_out, Input_2);
  not not_53 (not_53_out, Input_4);
  not not_54 (not_54_out, Input_5);
  not not_55 (not_55_out, Input_7);
  not not_56 (not_56_out, Input_4);
  not not_57 (not_57_out, Input_6);
  not not_58 (not_58_out, Input_7);
  not not_59 (not_59_out, Input_4);
  not not_60 (not_60_out, Input_6);
  not not_61 (not_61_out, Input_5);
  not not_62 (not_62_out, Input_6);
  not not_63 (not_63_out, Input_7);
  not not_64 (not_64_out, Input_3);
  not not_65 (not_65_out, Input_5);
  not not_66 (not_66_out, Input_6);
  not not_67 (not_67_out, Input_5);
  not not_68 (not_68_out, Input_6);
  not not_69 (not_69_out, Input_7);
  not not_70 (not_70_out, Input_5);
  not not_71 (not_71_out, Input_2);
  not not_72 (not_72_out, Input_3);
  not not_73 (not_73_out, Input_2);
  not not_74 (not_74_out, Input_3);
  not not_75 (not_75_out, Input_7);
  not not_76 (not_76_out, Input_2);
  not not_77 (not_77_out, Input_3);
  not not_78 (not_78_out, Input_3);
  not not_79 (not_79_out, Input_4);
  not not_80 (not_80_out, Input_5);
  not not_81 (not_81_out, Input_3);
  not not_82 (not_82_out, Input_4);
  not not_83 (not_83_out, Input_5);
  not not_84 (not_84_out, Input_4);
  not not_85 (not_85_out, Input_7);
  not not_86 (not_86_out, Input_4);
  not not_87 (not_87_out, Input_6);
  not not_88 (not_88_out, Input_2);
  not not_89 (not_89_out, Input_4);
  not not_90 (not_90_out, Input_5);
  not not_91 (not_91_out, Input_6);
  not not_92 (not_92_out, Input_7);
  not not_93 (not_93_out, Input_4);
  and and_1 (Output_1, Input_2, Input_3, Input_6, Input_7, Input_8);
  and and_2 (and_2_out, not_1_out, not_2_out, not_3_out, Input_5, not_4_out, not_5_out, not_6_out);
  and and_3 (and_3_out, Input_3, Input_4, not_7_out, Input_6, not_8_out, Input_8);
  and and_4 (and_4_out, not_9_out, not_10_out, not_11_out, Input_5, not_12_out, Input_7, not_13_out);
  and and_5 (and_5_out, Input_3, not_14_out, Input_5, Input_6, Input_8);
  and and_6 (and_6_out, Input_3, Input_4, not_15_out, Input_6, Input_7, Input_8);
  and and_7 (and_7_out, Input_2, Input_4, Input_5, not_16_out, Input_7, Input_8);
  and and_8 (and_8_out, Input_2, Input_4, Input_5, Input_6, not_17_out, Input_8);
  and and_9 (and_9_out, not_18_out, not_19_out, not_20_out, not_21_out, not_22_out);
  and and_10 (and_10_out, not_23_out, not_24_out, not_25_out, not_26_out, not_27_out);
  and and_11 (and_11_out, not_28_out, not_29_out, not_30_out, not_31_out, not_32_out);
  and and_12 (and_12_out, not_33_out, not_34_out, not_35_out, not_36_out, not_37_out, Input_8);
  and and_13 (and_13_out, not_38_out, not_39_out, not_40_out, Input_6, not_41_out);
  and and_14 (and_14_out, not_42_out, not_43_out, not_44_out, Input_5, Input_6, not_45_out);
  and and_15 (and_15_out, Input_3, Input_4, Input_5, Input_8);
  and and_16 (and_16_out, Input_3, Input_4, Input_5, Input_7);
  and and_17 (and_17_out, Input_2, Input_4, Input_5, Input_6, Input_7, Input_8);
  and and_18 (and_18_out, not_46_out, Input_4, not_47_out, Input_6, Input_7, not_48_out);
  and and_19 (and_19_out, not_49_out, Input_3, not_50_out, not_51_out, Input_7, Input_8);
  and and_20 (and_20_out, not_52_out, Input_3, not_53_out, not_54_out, Input_6, not_55_out);
  and and_21 (and_21_out, Input_3, not_56_out, Input_5, not_57_out, not_58_out);
  and and_22 (and_22_out, Input_3, not_59_out, Input_5, not_60_out, Input_8);
  and and_23 (and_23_out, Input_3, Input_4, not_61_out, not_62_out, not_63_out, Input_8);
  and and_24 (and_24_out, Input_2, not_64_out, not_65_out, not_66_out, Input_7, Input_8);
  and and_25 (and_25_out, Input_2, Input_4, not_67_out, Input_8);
  and and_26 (and_26_out, Input_2, Input_4, not_68_out, not_69_out, Input_8);
  and and_27 (and_27_out, Input_2, Input_4, not_70_out, Input_7);
  and and_28 (and_28_out, not_71_out, not_72_out, Input_4, Input_6, Input_7, Input_8);
  and and_29 (and_29_out, not_73_out, not_74_out, Input_4, Input_5, not_75_out);
  and and_30 (and_30_out, not_76_out, not_77_out, Input_4, Input_5, Input_8);
  and and_31 (and_31_out, Input_2, not_78_out, not_79_out, not_80_out, Input_6, Input_8);
  and and_32 (and_32_out, Input_2, not_81_out, not_82_out, not_83_out, Input_6, Input_7);
  and and_33 (and_33_out, Input_2, not_84_out, Input_5, not_85_out, Input_8);
  and and_34 (and_34_out, Input_2, not_86_out, Input_5, not_87_out, Input_7);
  and and_35 (and_35_out, not_88_out, Input_3, not_89_out, not_90_out, not_91_out, not_92_out, Input_8);
  and and_36 (and_36_out, Input_2, not_93_out, Input_5, Input_6, Input_7, Input_8);
  or or_1 (Output_bus_1[10], and_2_out, and_3_out);
  or or_2 (Output_bus_1[9], and_4_out, and_5_out, and_6_out, and_7_out, and_8_out);
  or or_3 (Output_bus_1[8], and_9_out, and_10_out, and_11_out, and_12_out, and_13_out, and_14_out, and_15_out, and_16_out, and_17_out);
  or or_4 (Output_bus_1[7], and_18_out, and_19_out, and_20_out, and_21_out, and_22_out, and_23_out, and_24_out, and_25_out, and_26_out, and_27_out);
  or or_5 (Output_bus_1[6], and_28_out, and_29_out, and_30_out, and_31_out, and_32_out, and_33_out, and_34_out);
  or or_6 (Output_bus_1[5], and_35_out, and_36_out);

  assign {Output_bus_1[12:11], Output_bus_1[4:0]} = {7{1'b0}};
endmodule

module ThisMustBeThePlace (
  input  Input_1,
  input  Input_2,
  input  Input_3,
  input  Input_4,
  input  Input_5,
  input  Input_6,
  input  Input_7,
  input  Input_8,
  output A1,
  output G1,
  output E1,
  output D1,
  output C1,
  output reset
);

  wire and_2_out, and_3_out, and_4_out, and_6_out, and_7_out, and_8_out, and_9_out, not_1_out, not_2_out,
       not_3_out, not_4_out, not_5_out, not_6_out, not_7_out, not_8_out, not_9_out, not_10_out, not_11_out,
       not_12_out, not_13_out, not_14_out, not_15_out, not_16_out, not_17_out, not_18_out, not_19_out,
       not_20_out;

  and and_1 (A1, Input_5, Input_6, Input_7);
  not not_1 (not_1_out, Input_5);
  not not_2 (not_2_out, Input_8);
  not not_3 (not_3_out, Input_4);
  not not_4 (not_4_out, Input_5);
  not not_5 (not_5_out, Input_7);
  not not_6 (not_6_out, Input_6);
  not not_7 (not_7_out, Input_8);
  not not_8 (not_8_out, Input_3);
  not not_9 (not_9_out, Input_4);
  not not_10 (not_10_out, Input_5);
  not not_11 (not_11_out, Input_6);
  not not_12 (not_12_out, Input_8);
  not not_13 (not_13_out, Input_4);
  not not_14 (not_14_out, Input_5);
  not not_15 (not_15_out, Input_7);
  not not_16 (not_16_out, Input_5);
  not not_17 (not_17_out, Input_6);
  not not_18 (not_18_out, Input_8);
  not not_19 (not_19_out, Input_5);
  not not_20 (not_20_out, Input_7);
  and and_2 (and_2_out, not_1_out, Input_6, not_2_out);
  and and_3 (and_3_out, not_3_out, not_4_out, Input_6, Input_7);
  and and_4 (and_4_out, Input_5, Input_6, not_5_out);
  and and_5 (E1, Input_5, not_6_out, not_7_out);
  and and_6 (and_6_out, not_8_out, not_9_out, not_10_out, not_11_out, not_12_out);
  and and_7 (and_7_out, not_13_out, not_14_out, Input_6, not_15_out, Input_8);
  and and_8 (and_8_out, Input_4, not_16_out, not_17_out, not_18_out);
  and and_9 (and_9_out, Input_4, not_19_out, Input_6, not_20_out, Input_8);
  or or_1 (G1, and_2_out, and_3_out, and_4_out);
  or or_2 (D1, and_6_out, and_7_out);
  or or_3 (C1, and_8_out, and_9_out);

  assign reset = Input_3;
endmodule

module MissYou (
  input  Input_1,
  input  Input_2,
  input  Input_3,
  input  Input_4,
  input  Input_5,
  input  Input_6,
  input  Input_7,
  input  Input_8,
  output E2,
  output D2,
  output B1,
  output A1,
  output reset
);

  wire and_1_out, and_2_out, and_3_out, and_4_out, and_5_out, and_6_out, and_7_out, and_8_out, and_9_out,
       and_10_out, and_11_out, and_12_out, and_13_out, and_14_out, and_15_out, and_16_out, and_17_out,
       and_18_out, and_19_out, and_20_out, and_21_out, and_22_out, and_23_out, and_24_out, and_25_out,
       and_26_out, and_27_out, and_28_out, and_29_out, and_30_out, and_31_out, and_32_out, and_33_out,
       and_34_out, and_35_out, and_36_out, not_1_out, not_2_out, not_3_out, not_4_out, not_5_out, not_6_out,
       not_7_out, not_8_out, not_9_out, not_10_out, not_11_out, not_12_out, not_13_out, not_14_out,
       not_15_out, not_16_out, not_17_out, not_18_out, not_19_out, not_20_out, not_21_out, not_22_out,
       not_23_out, not_24_out, not_25_out, not_26_out, not_27_out, not_28_out, not_29_out, not_30_out,
       not_31_out, not_32_out, not_33_out, not_34_out, not_35_out, not_36_out, not_37_out, not_38_out,
       not_39_out, not_40_out, not_41_out, not_42_out, not_43_out, not_44_out, not_45_out, not_46_out,
       not_47_out, not_48_out, not_49_out, not_50_out, not_51_out, not_52_out, not_53_out, not_54_out,
       not_55_out, not_56_out, not_57_out, not_58_out, not_59_out, not_60_out, not_61_out, not_62_out,
       not_63_out, not_64_out, not_65_out, not_66_out, not_67_out, not_68_out, not_69_out, not_70_out,
       not_71_out, not_72_out, not_73_out, not_74_out, not_75_out, not_76_out, not_77_out, not_78_out,
       not_79_out, not_80_out, not_81_out, not_82_out, not_83_out, not_84_out, not_85_out, not_86_out,
       not_87_out, not_88_out, not_89_out, not_90_out, not_91_out, not_92_out, not_93_out, not_94_out,
       not_95_out, not_96_out, not_97_out, not_98_out, not_99_out, not_100_out, not_101_out, not_102_out,
       not_103_out, not_104_out;

  not not_1 (not_1_out, Input_3);
  not not_2 (not_2_out, Input_5);
  not not_3 (not_3_out, Input_7);
  not not_4 (not_4_out, Input_8);
  not not_5 (not_5_out, Input_3);
  not not_6 (not_6_out, Input_5);
  not not_7 (not_7_out, Input_7);
  not not_8 (not_8_out, Input_3);
  not not_9 (not_9_out, Input_5);
  not not_10 (not_10_out, Input_7);
  not not_11 (not_11_out, Input_3);
  not not_12 (not_12_out, Input_5);
  not not_13 (not_13_out, Input_8);
  not not_14 (not_14_out, Input_4);
  not not_15 (not_15_out, Input_5);
  not not_16 (not_16_out, Input_7);
  not not_17 (not_17_out, Input_8);
  not not_18 (not_18_out, Input_3);
  not not_19 (not_19_out, Input_5);
  not not_20 (not_20_out, Input_4);
  not not_21 (not_21_out, Input_5);
  not not_22 (not_22_out, Input_7);
  not not_23 (not_23_out, Input_3);
  not not_24 (not_24_out, Input_5);
  not not_25 (not_25_out, Input_4);
  not not_26 (not_26_out, Input_5);
  not not_27 (not_27_out, Input_7);
  not not_28 (not_28_out, Input_3);
  not not_29 (not_29_out, Input_5);
  not not_30 (not_30_out, Input_6);
  not not_31 (not_31_out, Input_8);
  not not_32 (not_32_out, Input_4);
  not not_33 (not_33_out, Input_5);
  not not_34 (not_34_out, Input_6);
  not not_35 (not_35_out, Input_8);
  not not_36 (not_36_out, Input_3);
  not not_37 (not_37_out, Input_7);
  not not_38 (not_38_out, Input_8);
  not not_39 (not_39_out, Input_4);
  not not_40 (not_40_out, Input_7);
  not not_41 (not_41_out, Input_8);
  not not_42 (not_42_out, Input_3);
  not not_43 (not_43_out, Input_7);
  not not_44 (not_44_out, Input_3);
  not not_45 (not_45_out, Input_8);
  not not_46 (not_46_out, Input_4);
  not not_47 (not_47_out, Input_5);
  not not_48 (not_48_out, Input_4);
  not not_49 (not_49_out, Input_6);
  not not_50 (not_50_out, Input_3);
  not not_51 (not_51_out, Input_5);
  not not_52 (not_52_out, Input_6);
  not not_53 (not_53_out, Input_3);
  not not_54 (not_54_out, Input_7);
  not not_55 (not_55_out, Input_4);
  not not_56 (not_56_out, Input_7);
  not not_57 (not_57_out, Input_3);
  not not_58 (not_58_out, Input_4);
  not not_59 (not_59_out, Input_3);
  not not_60 (not_60_out, Input_5);
  not not_61 (not_61_out, Input_6);
  not not_62 (not_62_out, Input_3);
  not not_63 (not_63_out, Input_7);
  not not_64 (not_64_out, Input_3);
  not not_65 (not_65_out, Input_4);
  not not_66 (not_66_out, Input_4);
  not not_67 (not_67_out, Input_2);
  not not_68 (not_68_out, Input_3);
  not not_69 (not_69_out, Input_5);
  not not_70 (not_70_out, Input_6);
  not not_71 (not_71_out, Input_7);
  not not_72 (not_72_out, Input_8);
  not not_73 (not_73_out, Input_2);
  not not_74 (not_74_out, Input_4);
  not not_75 (not_75_out, Input_5);
  not not_76 (not_76_out, Input_6);
  not not_77 (not_77_out, Input_7);
  not not_78 (not_78_out, Input_8);
  not not_79 (not_79_out, Input_3);
  not not_80 (not_80_out, Input_6);
  not not_81 (not_81_out, Input_8);
  not not_82 (not_82_out, Input_3);
  not not_83 (not_83_out, Input_6);
  not not_84 (not_84_out, Input_2);
  not not_85 (not_85_out, Input_3);
  not not_86 (not_86_out, Input_5);
  not not_87 (not_87_out, Input_6);
  not not_88 (not_88_out, Input_7);
  not not_89 (not_89_out, Input_2);
  not not_90 (not_90_out, Input_4);
  not not_91 (not_91_out, Input_5);
  not not_92 (not_92_out, Input_6);
  not not_93 (not_93_out, Input_7);
  not not_94 (not_94_out, Input_3);
  not not_95 (not_95_out, Input_6);
  not not_96 (not_96_out, Input_1);
  not not_97 (not_97_out, Input_3);
  not not_98 (not_98_out, Input_4);
  not not_99 (not_99_out, Input_5);
  not not_100 (not_100_out, Input_6);
  not not_101 (not_101_out, Input_7);
  not not_102 (not_102_out, Input_8);
  not not_103 (not_103_out, Input_3);
  not not_104 (not_104_out, Input_7);
  and and_1 (and_1_out, not_1_out, not_2_out, Input_6, not_3_out, not_4_out);
  and and_2 (and_2_out, Input_2, not_5_out, not_6_out, Input_6, not_7_out);
  and and_3 (and_3_out, Input_1, not_8_out, not_9_out, Input_6, not_10_out);
  and and_4 (and_4_out, not_11_out, not_12_out, Input_6, Input_7, not_13_out);
  and and_5 (and_5_out, Input_3, not_14_out, not_15_out, Input_6, not_16_out, not_17_out);
  and and_6 (and_6_out, Input_2, not_18_out, not_19_out, Input_6, Input_7);
  and and_7 (and_7_out, Input_2, Input_3, not_20_out, not_21_out, Input_6, not_22_out);
  and and_8 (and_8_out, Input_1, not_23_out, not_24_out, Input_6, Input_7);
  and and_9 (and_9_out, Input_1, Input_3, not_25_out, not_26_out, Input_6, not_27_out);
  and and_10 (and_10_out, not_28_out, not_29_out, not_30_out, Input_7, not_31_out);
  and and_11 (and_11_out, not_32_out, not_33_out, not_34_out, Input_7, not_35_out);
  and and_12 (and_12_out, not_36_out, Input_5, not_37_out, not_38_out);
  and and_13 (and_13_out, not_39_out, Input_5, not_40_out, not_41_out);
  and and_14 (and_14_out, not_42_out, Input_5, Input_6, not_43_out);
  and and_15 (and_15_out, not_44_out, Input_5, Input_6, not_45_out);
  and and_16 (and_16_out, Input_3, not_46_out, not_47_out, Input_6, Input_7);
  and and_17 (and_17_out, Input_3, not_48_out, Input_5, not_49_out);
  and and_18 (and_18_out, Input_2, not_50_out, not_51_out, not_52_out, Input_7);
  and and_19 (and_19_out, Input_2, not_53_out, Input_5, not_54_out);
  and and_20 (and_20_out, Input_2, not_55_out, Input_5, not_56_out);
  and and_21 (and_21_out, Input_2, not_57_out, Input_5, Input_6);
  and and_22 (and_22_out, Input_2, Input_3, not_58_out, Input_7);
  and and_23 (and_23_out, Input_1, not_59_out, not_60_out, not_61_out, Input_7);
  and and_24 (and_24_out, Input_1, not_62_out, Input_5, not_63_out);
  and and_25 (and_25_out, Input_1, not_64_out, Input_5, Input_6);
  and and_26 (and_26_out, Input_1, not_65_out, Input_5, Input_6);
  and and_27 (and_27_out, Input_1, Input_3, not_66_out, Input_7);
  and and_28 (and_28_out, not_67_out, not_68_out, not_69_out, not_70_out, not_71_out, not_72_out);
  and and_29 (and_29_out, not_73_out, not_74_out, not_75_out, not_76_out, not_77_out, not_78_out);
  and and_30 (and_30_out, not_79_out, Input_5, not_80_out, Input_7, not_81_out);
  and and_31 (and_31_out, Input_2, not_82_out, Input_5, not_83_out, Input_7);
  and and_32 (and_32_out, Input_1, not_84_out, not_85_out, not_86_out, not_87_out, not_88_out);
  and and_33 (and_33_out, Input_1, not_89_out, not_90_out, not_91_out, not_92_out, not_93_out);
  and and_34 (and_34_out, Input_1, not_94_out, Input_5, not_95_out, Input_7);
  and and_35 (and_35_out, not_96_out, Input_2, not_97_out, not_98_out, not_99_out, not_100_out, not_101_out, not_102_out);
  and and_36 (and_36_out, Input_2, not_103_out, Input_4, Input_5, Input_6, not_104_out, Input_8);
  or or_1 (E2, and_1_out, and_2_out, and_3_out);
  or or_2 (D2, and_4_out, and_5_out, and_6_out, and_7_out, and_8_out, and_9_out);
  or or_3 (A1, and_28_out, and_29_out, and_30_out, and_31_out, and_32_out, and_33_out, and_34_out);
  or or_4 (reset, and_35_out, and_36_out);
  or or_5 (B1, and_10_out, and_11_out, and_12_out, and_13_out, and_14_out, and_15_out, and_16_out, and_17_out, and_18_out, and_19_out, and_20_out, and_21_out, and_22_out, and_23_out, and_24_out, and_25_out, and_26_out, and_27_out);
endmodule

module AnotherBrickInTheWall (
  input  Input_1,
  input  Input_2,
  input  Input_3,
  input  Input_4,
  input  Input_5,
  input  Input_6,
  input  Input_7,
  input  Input_8,
  output d2,
  output c2,
  output a1,
  output e1,
  output reset
);

  wire and_1_out, and_2_out, and_3_out, and_4_out, and_5_out, and_6_out, and_7_out, and_8_out, and_9_out,
       and_10_out, and_11_out, and_12_out, and_15_out, and_16_out, and_17_out, and_18_out, not_1_out,
       not_2_out, not_3_out, not_4_out, not_5_out, not_6_out, not_7_out, not_8_out, not_9_out, not_10_out,
       not_11_out, not_12_out, not_13_out, not_14_out, not_15_out, not_16_out, not_17_out, not_18_out,
       not_19_out, not_20_out, not_21_out, not_22_out, not_23_out, not_24_out, not_25_out, not_26_out,
       not_27_out, not_28_out, not_29_out, not_30_out, not_31_out, not_32_out, not_33_out, not_34_out,
       not_35_out, not_36_out, not_37_out, not_38_out, not_39_out, not_40_out, not_41_out, not_42_out,
       not_43_out, not_44_out;

  not not_1 (not_1_out, Input_4);
  not not_2 (not_2_out, Input_6);
  not not_3 (not_3_out, Input_1);
  not not_4 (not_4_out, Input_2);
  not not_5 (not_5_out, Input_3);
  not not_6 (not_6_out, Input_4);
  not not_7 (not_7_out, Input_7);
  not not_8 (not_8_out, Input_8);
  not not_9 (not_9_out, Input_5);
  not not_10 (not_10_out, Input_6);
  not not_11 (not_11_out, Input_5);
  not not_12 (not_12_out, Input_1);
  not not_13 (not_13_out, Input_2);
  not not_14 (not_14_out, Input_5);
  not not_15 (not_15_out, Input_6);
  not not_16 (not_16_out, Input_7);
  not not_17 (not_17_out, Input_4);
  not not_18 (not_18_out, Input_5);
  not not_19 (not_19_out, Input_1);
  not not_20 (not_20_out, Input_2);
  not not_21 (not_21_out, Input_3);
  not not_22 (not_22_out, Input_4);
  not not_23 (not_23_out, Input_6);
  not not_24 (not_24_out, Input_7);
  not not_25 (not_25_out, Input_7);
  not not_26 (not_26_out, Input_8);
  not not_27 (not_27_out, Input_4);
  not not_28 (not_28_out, Input_5);
  not not_29 (not_29_out, Input_4);
  not not_30 (not_30_out, Input_5);
  not not_31 (not_31_out, Input_4);
  not not_32 (not_32_out, Input_5);
  not not_33 (not_33_out, Input_6);
  not not_34 (not_34_out, Input_3);
  not not_35 (not_35_out, Input_4);
  not not_36 (not_36_out, Input_5);
  not not_37 (not_37_out, Input_6);
  not not_38 (not_38_out, Input_1);
  not not_39 (not_39_out, Input_2);
  not not_40 (not_40_out, Input_4);
  not not_41 (not_41_out, Input_5);
  not not_42 (not_42_out, Input_6);
  not not_43 (not_43_out, Input_7);
  not not_44 (not_44_out, Input_8);
  and and_1 (and_1_out, not_1_out, Input_5, not_2_out, Input_7);
  and and_2 (and_2_out, not_3_out, not_4_out, not_5_out, not_6_out, Input_5, Input_6, not_7_out, not_8_out);
  and and_3 (and_3_out, Input_4, not_9_out, not_10_out);
  and and_4 (and_4_out, Input_4, not_11_out, Input_7);
  and and_5 (and_5_out, not_12_out, not_13_out, Input_3, not_14_out, not_15_out, not_16_out, Input_8);
  and and_6 (and_6_out, not_17_out, not_18_out, Input_6, Input_7, Input_8);
  and and_7 (and_7_out, not_19_out, not_20_out, not_21_out, not_22_out, Input_5, not_23_out, not_24_out);
  and and_8 (and_8_out, Input_4, Input_5, Input_6, not_25_out);
  and and_9 (and_9_out, Input_4, Input_5, Input_6, not_26_out);
  and and_10 (and_10_out, Input_3, not_27_out, not_28_out, Input_6, Input_7);
  and and_11 (and_11_out, Input_2, not_29_out, not_30_out, Input_6, Input_7);
  and and_12 (and_12_out, Input_1, not_31_out, not_32_out, Input_6, Input_7);
  and and_13 (a1, Input_4, Input_5, not_33_out);
  and and_14 (e1, not_34_out, not_35_out, not_36_out, not_37_out);
  and and_15 (and_15_out, not_38_out, not_39_out, Input_3, not_40_out, not_41_out, not_42_out, not_43_out, not_44_out);
  and and_16 (and_16_out, Input_3, Input_4, Input_5, Input_6, Input_7, Input_8);
  and and_17 (and_17_out, Input_2, Input_4, Input_5, Input_6, Input_7, Input_8);
  and and_18 (and_18_out, Input_1, Input_4, Input_5, Input_6, Input_7, Input_8);
  or or_1 (d2, and_1_out, and_2_out, and_3_out, and_4_out, and_5_out);
  or or_2 (c2, and_6_out, and_7_out, and_8_out, and_9_out, and_10_out, and_11_out, and_12_out);
  or or_3 (reset, and_15_out, and_16_out, and_17_out, and_18_out);
endmodule

module RappersDelight (
  input  Input_1,
  input  Input_2,
  input  Input_3,
  input  Input_4,
  input  Input_5,
  input  Input_6,
  input  Input_7,
  input  Input_8,
  output c3,
  output b2,
  output a2,
  output g2,
  output e2,
  output d2,
  output c2,
  output b1,
  output a1,
  output reset
);

  wire and_2_out, and_3_out, and_6_out, and_7_out, and_8_out, and_9_out, and_10_out, and_11_out, and_12_out,
       and_13_out, and_14_out, and_15_out, and_16_out, and_17_out, and_18_out, and_19_out, and_20_out,
       and_21_out, and_22_out, and_23_out, not_1_out, not_2_out, not_3_out, not_4_out, not_5_out, not_6_out,
       not_7_out, not_8_out, not_9_out, not_10_out, not_11_out, not_12_out, not_13_out, not_14_out,
       not_15_out, not_16_out, not_17_out, not_18_out, not_19_out, not_20_out, not_21_out, not_22_out,
       not_23_out, not_24_out, not_25_out, not_26_out, not_27_out, not_28_out, not_29_out, not_30_out,
       not_31_out, not_32_out, not_33_out, not_34_out, not_35_out, not_36_out, not_37_out, not_38_out,
       not_39_out, not_40_out, not_41_out, not_42_out, not_43_out, not_44_out, not_45_out, not_46_out,
       not_47_out, not_48_out, not_49_out, not_50_out, not_51_out, not_52_out, not_53_out, not_54_out,
       not_55_out, not_56_out;

  not not_1 (not_1_out, Input_5);
  not not_2 (not_2_out, Input_7);
  not not_3 (not_3_out, Input_5);
  not not_4 (not_4_out, Input_5);
  not not_5 (not_5_out, Input_3);
  not not_6 (not_6_out, Input_8);
  not not_7 (not_7_out, Input_3);
  not not_8 (not_8_out, Input_7);
  not not_9 (not_9_out, Input_3);
  not not_10 (not_10_out, Input_6);
  not not_11 (not_11_out, Input_8);
  not not_12 (not_12_out, Input_5);
  not not_13 (not_13_out, Input_6);
  not not_14 (not_14_out, Input_8);
  not not_15 (not_15_out, Input_3);
  not not_16 (not_16_out, Input_5);
  not not_17 (not_17_out, Input_3);
  not not_18 (not_18_out, Input_4);
  not not_19 (not_19_out, Input_5);
  not not_20 (not_20_out, Input_7);
  not not_21 (not_21_out, Input_6);
  not not_22 (not_22_out, Input_7);
  not not_23 (not_23_out, Input_4);
  not not_24 (not_24_out, Input_8);
  not not_25 (not_25_out, Input_6);
  not not_26 (not_26_out, Input_7);
  not not_27 (not_27_out, Input_6);
  not not_28 (not_28_out, Input_7);
  not not_29 (not_29_out, Input_3);
  not not_30 (not_30_out, Input_5);
  not not_31 (not_31_out, Input_7);
  not not_32 (not_32_out, Input_8);
  not not_33 (not_33_out, Input_3);
  not not_34 (not_34_out, Input_5);
  not not_35 (not_35_out, Input_6);
  not not_36 (not_36_out, Input_2);
  not not_37 (not_37_out, Input_3);
  not not_38 (not_38_out, Input_4);
  not not_39 (not_39_out, Input_5);
  not not_40 (not_40_out, Input_7);
  not not_41 (not_41_out, Input_2);
  not not_42 (not_42_out, Input_3);
  not not_43 (not_43_out, Input_4);
  not not_44 (not_44_out, Input_6);
  not not_45 (not_45_out, Input_7);
  not not_46 (not_46_out, Input_8);
  not not_47 (not_47_out, Input_2);
  not not_48 (not_48_out, Input_3);
  not not_49 (not_49_out, Input_5);
  not not_50 (not_50_out, Input_6);
  not not_51 (not_51_out, Input_7);
  not not_52 (not_52_out, Input_2);
  not not_53 (not_53_out, Input_3);
  not not_54 (not_54_out, Input_4);
  not not_55 (not_55_out, Input_6);
  not not_56 (not_56_out, Input_7);
  and and_1 (c3, Input_3, Input_4, not_1_out, Input_6, not_2_out);
  and and_2 (and_2_out, Input_3, Input_4, not_3_out, Input_7, Input_8);
  and and_3 (and_3_out, Input_3, Input_4, not_4_out, Input_6, Input_7);
  and and_4 (a2, not_5_out, Input_4, Input_5, Input_6, Input_7, not_6_out);
  and and_5 (g2, not_7_out, Input_4, Input_5, Input_6, not_8_out);
  and and_6 (and_6_out, not_9_out, Input_4, Input_5, not_10_out, not_11_out);
  and and_7 (and_7_out, Input_3, Input_4, not_12_out, not_13_out, Input_7, not_14_out);
  and and_8 (and_8_out, not_15_out, Input_4, not_16_out, Input_6, Input_7);
  and and_9 (and_9_out, not_17_out, Input_4, Input_6, Input_7, Input_8);
  and and_10 (and_10_out, Input_3, not_18_out, not_19_out, Input_6, not_20_out);
  and and_11 (and_11_out, Input_3, Input_5, not_21_out, not_22_out);
  and and_12 (and_12_out, Input_3, not_23_out, Input_5, Input_6, Input_7, not_24_out);
  and and_13 (and_13_out, Input_3, Input_4, not_25_out, not_26_out);
  and and_14 (and_14_out, Input_3, Input_4, Input_5, not_27_out, Input_8);
  and and_15 (and_15_out, Input_3, Input_4, Input_5, not_28_out, Input_8);
  and and_16 (and_16_out, not_29_out, Input_4, not_30_out, Input_6, not_31_out);
  and and_17 (and_17_out, Input_3, Input_4, Input_5, Input_6, Input_7, not_32_out);
  and and_18 (and_18_out, not_33_out, Input_4, not_34_out, not_35_out, Input_7);
  and and_19 (and_19_out, Input_3, Input_4, Input_5, Input_6, Input_7, Input_8);
  and and_20 (and_20_out, not_36_out, not_37_out, not_38_out, not_39_out, not_40_out);
  and and_21 (and_21_out, not_41_out, not_42_out, not_43_out, not_44_out, not_45_out, not_46_out);
  and and_22 (and_22_out, not_47_out, not_48_out, not_49_out, not_50_out, not_51_out);
  and and_23 (and_23_out, Input_1, not_52_out, not_53_out, not_54_out, not_55_out, not_56_out);
  or or_1 (b2, and_2_out, and_3_out);
  or or_2 (e2, and_6_out, and_7_out);
  or or_3 (d2, and_8_out, and_9_out, and_10_out, and_11_out, and_12_out, and_13_out, and_14_out, and_15_out);
  or or_4 (c2, and_16_out, and_17_out);
  or or_5 (b1, and_18_out, and_19_out);
  or or_6 (a1, and_20_out, and_21_out, and_22_out, and_23_out);

  assign reset = Input_2;
endmodule

module SongName (
  input  [2:0] songcode,
  output [7:0] L1,
  output [7:0] L2,
  output [7:0] L3,
  output [7:0] L4,
  output [7:0] L5,
  output [7:0] L6
);

  wire [5:0] Let1_w, Let2_w, Let3_w, Let4_w, Let5_w, Let6_w;

  Letter1_song Let1 (
    .a(songcode[2]), .b(songcode[1]), .c(songcode[0]), .x(Let1_w[5]), .y(Let1_w[4]), .z(Let1_w[3]),
    .u(Let1_w[2]), .v(Let1_w[1]), .w(Let1_w[0]));
  Letter2_song Let2 (
    .a(songcode[2]), .b(songcode[1]), .c(songcode[0]), .x(Let2_w[5]), .y(Let2_w[4]), .z(Let2_w[3]),
    .u(Let2_w[2]), .v(Let2_w[1]), .w(Let2_w[0]));
  Letter3_song Let3 (
    .a(songcode[2]), .b(songcode[1]), .c(songcode[0]), .x(Let3_w[5]), .y(Let3_w[4]), .z(Let3_w[3]),
    .u(Let3_w[2]), .v(Let3_w[1]), .w(Let3_w[0]));
  Letter4_song Let4 (
    .a(songcode[2]), .b(songcode[1]), .c(songcode[0]), .x(Let4_w[5]), .y(Let4_w[4]), .z(Let4_w[3]),
    .u(Let4_w[2]), .v(Let4_w[1]), .w(Let4_w[0]));
  Letter5_song Let5 (
    .a(songcode[2]), .b(songcode[1]), .c(songcode[0]), .x(Let5_w[5]), .y(Let5_w[4]), .z(Let5_w[3]),
    .u(Let5_w[2]), .v(Let5_w[1]), .w(Let5_w[0]));
  Letter6_song Let6 (
    .a(songcode[2]), .b(songcode[1]), .c(songcode[0]), .x(Let6_w[5]), .y(Let6_w[4]), .z(Let6_w[3]),
    .u(Let6_w[2]), .v(Let6_w[1]), .w(Let6_w[0]));
  assign L1 = {{2{1'b0}}, Let1_w};  // Bit_Extender bit_extender_1
  assign L2 = {{2{1'b0}}, Let2_w};  // Bit_Extender bit_extender_2
  assign L3 = {{2{1'b0}}, Let3_w};  // Bit_Extender bit_extender_3
  assign L4 = {{2{1'b0}}, Let4_w};  // Bit_Extender bit_extender_4
  assign L5 = {{2{1'b0}}, Let5_w};  // Bit_Extender bit_extender_5
  assign L6 = {{2{1'b0}}, Let6_w};  // Bit_Extender bit_extender_6
endmodule

module Letter1_song (
  input  a,
  input  b,
  input  c,
  output x,
  output y,
  output z,
  output u,
  output v,
  output w
);

  wire and_1_out, and_2_out, and_3_out, and_4_out, and_5_out, and_6_out, and_7_out, and_8_out, not_1_out,
       not_2_out, not_3_out, not_4_out, not_5_out, not_6_out, not_7_out, not_8_out, not_9_out, not_10_out,
       not_11_out, not_12_out;

  not not_1 (not_1_out, c);
  not not_2 (not_2_out, b);
  not not_3 (not_3_out, c);
  not not_4 (not_4_out, a);
  not not_5 (not_5_out, c);
  not not_6 (not_6_out, b);
  not not_7 (not_7_out, a);
  not not_8 (not_8_out, b);
  not not_9 (not_9_out, a);
  not not_10 (not_10_out, b);
  not not_11 (not_11_out, c);
  not not_12 (not_12_out, b);
  and and_1 (and_1_out, a, not_1_out);
  or or_1 (x, and_1_out, and_2_out);
  and and_2 (and_2_out, a, b);
  or or_2 (y, not_2_out, c, a);
  or or_3 (z, not_3_out, b);
  and and_3 (and_3_out, not_4_out, not_5_out);
  or or_4 (u, and_3_out, and_4_out);
  and and_4 (and_4_out, a, not_6_out);
  and and_5 (and_5_out, not_7_out, not_8_out);
  or or_5 (v, and_5_out, and_6_out);
  and and_6 (and_6_out, a, b, c);
  and and_7 (and_7_out, not_9_out, not_10_out, not_11_out);
  or or_6 (w, and_7_out, and_8_out);
  and and_8 (and_8_out, a, not_12_out, c);
endmodule

module Letter2_song (
  input  a,
  input  b,
  input  c,
  output x,
  output y,
  output z,
  output u,
  output v,
  output w
);

  wire and_2_out, and_3_out, and_4_out, and_5_out, and_6_out, and_7_out, and_8_out, and_9_out, and_10_out,
       and_11_out, and_12_out, and_13_out, and_14_out, not_1_out, not_2_out, not_3_out, not_4_out, not_5_out,
       not_6_out, not_7_out, not_8_out, not_9_out, not_10_out, not_11_out, not_12_out, not_13_out,
       not_14_out, not_15_out, not_16_out, not_17_out;

  not not_1 (not_1_out, b);
  not not_2 (not_2_out, c);
  not not_3 (not_3_out, a);
  not not_4 (not_4_out, a);
  not not_5 (not_5_out, c);
  not not_6 (not_6_out, a);
  not not_7 (not_7_out, b);
  not not_8 (not_8_out, c);
  not not_9 (not_9_out, a);
  not not_10 (not_10_out, c);
  not not_11 (not_11_out, a);
  not not_12 (not_12_out, c);
  not not_13 (not_13_out, b);
  not not_14 (not_14_out, a);
  not not_15 (not_15_out, b);
  not not_16 (not_16_out, c);
  and and_1 (x, a, not_1_out, not_2_out);
  not not_17 (not_17_out, b);
  or or_1 (y, not_17_out, and_2_out);
  and and_2 (and_2_out, not_3_out, c);
  and and_3 (and_3_out, not_4_out, not_5_out);
  or or_2 (z, and_3_out, and_4_out);
  and and_4 (and_4_out, a, b);
  and and_5 (and_5_out, not_6_out, not_7_out);
  or or_3 (u, and_5_out, and_6_out, and_7_out);
  and and_6 (and_6_out, b, c);
  and and_7 (and_7_out, a, not_8_out);
  and and_8 (and_8_out, not_9_out, not_10_out);
  and and_9 (and_9_out, not_11_out, b);
  and and_10 (and_10_out, b, not_12_out);
  and and_11 (and_11_out, a, not_13_out, c);
  and and_12 (and_12_out, not_14_out, not_15_out);
  and and_13 (and_13_out, b, c);
  or or_4 (w, and_12_out, and_13_out, and_14_out);
  and and_14 (and_14_out, a, not_16_out);
  or or_5 (v, and_8_out, and_9_out, and_10_out, and_11_out);
endmodule

module Letter3_song (
  input  a,
  input  b,
  input  c,
  output x,
  output y,
  output z,
  output u,
  output v,
  output w
);

  wire and_2_out, and_3_out, and_4_out, and_5_out, and_6_out, and_7_out, and_8_out, and_9_out, not_1_out,
       not_2_out, not_3_out, not_4_out, not_5_out, not_6_out, not_7_out, not_8_out, not_9_out, not_10_out,
       not_11_out, not_12_out, not_13_out, not_14_out;

  not not_1 (not_1_out, b);
  not not_2 (not_2_out, c);
  not not_3 (not_3_out, a);
  not not_4 (not_4_out, b);
  not not_5 (not_5_out, b);
  not not_6 (not_6_out, c);
  not not_7 (not_7_out, b);
  not not_8 (not_8_out, a);
  not not_9 (not_9_out, c);
  not not_10 (not_10_out, b);
  not not_11 (not_11_out, c);
  not not_12 (not_12_out, b);
  not not_13 (not_13_out, c);
  not not_14 (not_14_out, b);
  and and_1 (x, a, not_1_out, not_2_out);
  and and_2 (and_2_out, not_3_out, not_4_out);
  and and_3 (and_3_out, not_5_out, c);
  or or_1 (y, and_2_out, and_3_out, and_4_out);
  and and_4 (and_4_out, b, not_6_out);
  or or_2 (z, not_7_out, c);
  and and_5 (and_5_out, not_8_out, not_9_out);
  or or_3 (u, and_5_out, b);
  and and_6 (and_6_out, not_10_out, not_11_out);
  or or_4 (v, and_6_out, and_7_out);
  and and_7 (and_7_out, a, c);
  and and_8 (and_8_out, not_12_out, not_13_out);
  or or_5 (w, and_8_out, and_9_out);
  and and_9 (and_9_out, a, not_14_out);
endmodule

module Letter4_song (
  input  a,
  input  b,
  input  c,
  output x,
  output y,
  output z,
  output u,
  output v,
  output w
);

  wire and_1_out, and_2_out, and_3_out, and_4_out, and_5_out, and_6_out, and_7_out, and_8_out, and_9_out,
       and_10_out, and_11_out, and_12_out, and_13_out, and_14_out, and_15_out, and_16_out, not_1_out,
       not_2_out, not_3_out, not_4_out, not_5_out, not_6_out, not_7_out, not_8_out, not_9_out, not_10_out,
       not_11_out, not_12_out, not_13_out, not_14_out, not_15_out, not_16_out, not_17_out, not_18_out,
       not_19_out;

  not not_1 (not_1_out, b);
  not not_2 (not_2_out, c);
  not not_3 (not_3_out, b);
  not not_4 (not_4_out, c);
  not not_5 (not_5_out, a);
  not not_6 (not_6_out, b);
  not not_7 (not_7_out, a);
  not not_8 (not_8_out, b);
  not not_9 (not_9_out, c);
  not not_10 (not_10_out, a);
  not not_11 (not_11_out, c);
  not not_12 (not_12_out, a);
  not not_13 (not_13_out, c);
  not not_14 (not_14_out, b);
  not not_15 (not_15_out, a);
  not not_16 (not_16_out, b);
  not not_17 (not_17_out, a);
  not not_18 (not_18_out, b);
  not not_19 (not_19_out, c);
  and and_1 (and_1_out, a, not_1_out, not_2_out);
  or or_1 (x, and_1_out, and_2_out);
  and and_2 (and_2_out, a, b, c);
  and and_3 (and_3_out, not_3_out, not_4_out);
  and and_4 (and_4_out, not_5_out, b, c);
  or or_2 (z, and_3_out, and_4_out, and_5_out);
  and and_5 (and_5_out, a, not_6_out);
  and and_6 (and_6_out, not_7_out, not_8_out);
  and and_7 (and_7_out, b, c);
  or or_3 (u, and_6_out, and_7_out, and_8_out);
  and and_8 (and_8_out, a, not_9_out);
  and and_9 (and_9_out, not_10_out, not_11_out);
  and and_10 (and_10_out, not_12_out, b);
  and and_11 (and_11_out, b, not_13_out);
  and and_12 (and_12_out, a, not_14_out, c);
  and and_13 (and_13_out, not_15_out, not_16_out);
  and and_14 (and_14_out, not_17_out, c);
  and and_15 (and_15_out, not_18_out, c);
  and and_16 (and_16_out, a, b, not_19_out);
  or or_4 (v, and_9_out, and_10_out, and_11_out, and_12_out);
  or or_5 (w, and_13_out, and_14_out, and_15_out, and_16_out);

  assign y = 1'b1;
endmodule

module Letter5_song (
  input  a,
  input  b,
  input  c,
  output x,
  output y,
  output z,
  output u,
  output v,
  output w
);

  wire and_2_out, not_1_out, not_2_out, not_3_out, not_4_out, not_5_out, not_6_out, not_7_out;

  not not_1 (not_1_out, b);
  not not_2 (not_2_out, c);
  not not_3 (not_3_out, b);
  not not_4 (not_4_out, a);
  not not_5 (not_5_out, a);
  not not_6 (not_6_out, a);
  not not_7 (not_7_out, b);
  and and_1 (x, a, not_1_out, not_2_out);
  or or_1 (z, not_3_out, c, a);
  or or_2 (u, not_4_out, c, b);
  or or_3 (v, not_5_out, c, b);
  and and_2 (and_2_out, not_6_out, not_7_out);
  or or_4 (w, and_2_out, c);

  assign y = 1'b1;
endmodule

module Letter6_song (
  input  a,
  input  b,
  input  c,
  output x,
  output y,
  output z,
  output u,
  output v,
  output w
);

  wire and_1_out, and_2_out, and_3_out, not_1_out, not_2_out, not_3_out, not_4_out, not_5_out, not_6_out;

  not not_1 (not_1_out, b);
  not not_2 (not_2_out, a);
  not not_3 (not_3_out, b);
  not not_4 (not_4_out, b);
  not not_5 (not_5_out, c);
  not not_6 (not_6_out, b);
  or or_1 (y, not_1_out, c);
  and and_1 (and_1_out, not_2_out, not_3_out);
  and and_2 (and_2_out, not_4_out, not_5_out);
  or or_2 (v, and_1_out, and_2_out, and_3_out);
  and and_3 (and_3_out, b, c);
  or or_3 (w, not_6_out, c, a);

  assign u = 1'b1;
  assign x = 1'b0;
  assign z = 1'b1;
endmodule
module ChangementFuseauHoraire (
  input  RESET,
  input  [1:0] B1_B0,
  input  ChM,
  input  CLK32k,
  output [7:0] Letter1,
  output [7:0] Letter2,
  output [7:0] Letter3,
  output [7:0] Letter4,
  output [7:0] Letter5,
  output [7:0] Letter6,
  output [7:0] UTCCode
);

  wire and_1_out;
  wire [4:0] CapitalLetter1_1_v, CapitalLetter2_1_v, CapitalLetter3_1_v, CapitalLetter5_1_v,
       CapitalLetter6_1_v, counter_1_q;
  wire [6:0] Capitales_1_z;

  and and_1 (and_1_out, B1_B0[0], ~ChM);  // AND_Gate
  Counter #(.width(5), .max('h15)) counter_1 (
    .clr(RESET), .count(and_1_out), .clk(CLK32k), .Q(counter_1_q));  // open: load, up, D, carry
  CapitalLetter1 CapitalLetter1_1 (
    .a(counter_1_q[4]), .b(counter_1_q[3]), .c(counter_1_q[2]), .d(counter_1_q[1]), .e(counter_1_q[0]),
    .x(CapitalLetter1_1_v[4]), .y(CapitalLetter1_1_v[3]), .z(CapitalLetter1_1_v[2]),
    .u(CapitalLetter1_1_v[1]), .v(CapitalLetter1_1_v[0]));
  CapitalLetter2 CapitalLetter2_1 (
    .a(counter_1_q[4]), .b(counter_1_q[3]), .c(counter_1_q[2]), .d(counter_1_q[1]), .e(counter_1_q[0]),
    .x(CapitalLetter2_1_v[4]), .y(CapitalLetter2_1_v[3]), .z(CapitalLetter2_1_v[2]),
    .u(CapitalLetter2_1_v[1]), .v(CapitalLetter2_1_v[0]));
  CapitalLetter3 CapitalLetter3_1 (
    .a(counter_1_q[4]), .b(counter_1_q[3]), .c(counter_1_q[2]), .d(counter_1_q[1]), .e(counter_1_q[0]),
    .x(CapitalLetter3_1_v[4]), .y(CapitalLetter3_1_v[3]), .z(CapitalLetter3_1_v[2]),
    .u(CapitalLetter3_1_v[1]), .v(CapitalLetter3_1_v[0]));
  CapitalLetter5 CapitalLetter5_1 (
    .a(counter_1_q[4]), .b(counter_1_q[3]), .c(counter_1_q[2]), .d(counter_1_q[1]), .e(counter_1_q[0]),
    .x(CapitalLetter5_1_v[4]), .y(CapitalLetter5_1_v[3]), .z(CapitalLetter5_1_v[2]),
    .u(CapitalLetter5_1_v[1]), .v(CapitalLetter5_1_v[0]));
  CapitalLetter6 CapitalLetter6_1 (
    .a(counter_1_q[4]), .b(counter_1_q[3]), .c(counter_1_q[2]), .d(counter_1_q[1]), .e(counter_1_q[0]),
    .x(CapitalLetter6_1_v[4]), .y(CapitalLetter6_1_v[3]), .z(CapitalLetter6_1_v[2]),
    .u(CapitalLetter6_1_v[1]), .v(CapitalLetter6_1_v[0]));
  Capitales Capitales_1 (
    .a(counter_1_q[4]), .b(counter_1_q[3]), .c(counter_1_q[2]), .d(counter_1_q[1]), .e(counter_1_q[0]),
    .t(Capitales_1_z[6]), .u(Capitales_1_z[5]), .v(Capitales_1_z[4]), .w(Capitales_1_z[3]),
    .x(Capitales_1_z[2]), .y(Capitales_1_z[1]), .z(Capitales_1_z[0]));
  assign Letter1 = {{3{1'b0}}, CapitalLetter1_1_v};  // Bit_Extender bit_extender_1
  assign Letter2 = {{3{1'b0}}, CapitalLetter2_1_v};  // Bit_Extender bit_extender_2
  assign Letter3 = {{3{1'b0}}, CapitalLetter3_1_v};  // Bit_Extender bit_extender_3
  assign Letter5 = {{3{1'b0}}, CapitalLetter5_1_v};  // Bit_Extender bit_extender_4
  assign Letter6 = {{3{1'b0}}, CapitalLetter6_1_v};  // Bit_Extender bit_extender_5
  assign UTCCode = {{1{1'b0}}, Capitales_1_z};  // Bit_Extender bit_extender_6

  assign Letter4 = 8'h7f;
endmodule

module Capitales (
  input  a,
  input  b,
  input  c,
  input  d,
  input  e,
  output t,
  output u,
  output v,
  output w,
  output x,
  output y,
  output z
);

  wire and_1_out, and_2_out, and_3_out, and_4_out, and_5_out, and_6_out, and_7_out, and_8_out, and_9_out,
       and_10_out, and_11_out, and_12_out, and_13_out, and_14_out, and_15_out, and_16_out, and_17_out,
       and_18_out, and_19_out, and_20_out, and_21_out, and_22_out, and_23_out, and_24_out, and_25_out,
       not_1_out, not_2_out, not_3_out, not_4_out, not_5_out, not_6_out, not_7_out, not_8_out, not_9_out,
       not_10_out, not_11_out, not_12_out, not_13_out, not_14_out, not_15_out, not_16_out, not_17_out,
       not_18_out, not_19_out, not_20_out, not_21_out, not_22_out, not_23_out, not_24_out, not_25_out,
       not_26_out, not_27_out, not_28_out, not_29_out, not_30_out, not_31_out, not_32_out, not_33_out,
       not_34_out, not_35_out, not_36_out, not_37_out, not_38_out, not_39_out, not_40_out, not_41_out,
       not_42_out, not_43_out, not_44_out, not_45_out, not_46_out, not_47_out, not_48_out, not_49_out,
       not_50_out, not_51_out;

  not not_1 (not_1_out, b);
  not not_2 (not_2_out, c);
  not not_3 (not_3_out, b);
  not not_4 (not_4_out, d);
  not not_5 (not_5_out, b);
  not not_6 (not_6_out, c);
  not not_7 (not_7_out, b);
  not not_8 (not_8_out, d);
  not not_9 (not_9_out, b);
  not not_10 (not_10_out, c);
  not not_11 (not_11_out, b);
  not not_12 (not_12_out, d);
  not not_13 (not_13_out, a);
  not not_14 (not_14_out, a);
  not not_15 (not_15_out, b);
  not not_16 (not_16_out, c);
  not not_17 (not_17_out, b);
  not not_18 (not_18_out, d);
  not not_19 (not_19_out, a);
  not not_20 (not_20_out, b);
  not not_21 (not_21_out, a);
  not not_22 (not_22_out, c);
  not not_23 (not_23_out, d);
  not not_24 (not_24_out, a);
  not not_25 (not_25_out, c);
  not not_26 (not_26_out, e);
  not not_27 (not_27_out, b);
  not not_28 (not_28_out, d);
  not not_29 (not_29_out, b);
  not not_30 (not_30_out, c);
  not not_31 (not_31_out, a);
  not not_32 (not_32_out, b);
  not not_33 (not_33_out, d);
  not not_34 (not_34_out, a);
  not not_35 (not_35_out, b);
  not not_36 (not_36_out, e);
  not not_37 (not_37_out, a);
  not not_38 (not_38_out, d);
  not not_39 (not_39_out, a);
  not not_40 (not_40_out, e);
  not not_41 (not_41_out, a);
  not not_42 (not_42_out, b);
  not not_43 (not_43_out, c);
  not not_44 (not_44_out, b);
  not not_45 (not_45_out, d);
  not not_46 (not_46_out, a);
  not not_47 (not_47_out, e);
  not not_48 (not_48_out, a);
  not not_49 (not_49_out, e);
  not not_50 (not_50_out, b);
  not not_51 (not_51_out, c);
  and and_1 (and_1_out, a, not_1_out, not_2_out);
  and and_2 (and_2_out, a, not_3_out, not_4_out);
  and and_3 (and_3_out, a, not_5_out, not_6_out);
  and and_4 (and_4_out, a, not_7_out, not_8_out);
  and and_5 (and_5_out, a, not_9_out, not_10_out);
  and and_6 (and_6_out, a, not_11_out, not_12_out);
  and and_7 (and_7_out, not_13_out, b, d, e);
  and and_8 (and_8_out, not_14_out, b, c);
  and and_9 (and_9_out, a, not_15_out, not_16_out);
  and and_10 (and_10_out, a, not_17_out, not_18_out);
  and and_11 (and_11_out, not_19_out, not_20_out, c, d, e);
  and and_12 (and_12_out, not_21_out, b, not_22_out, not_23_out);
  and and_13 (and_13_out, not_24_out, b, not_25_out, not_26_out);
  and and_14 (and_14_out, a, not_27_out, c, not_28_out);
  and and_15 (and_15_out, not_29_out, not_30_out, d, e);
  and and_16 (and_16_out, not_31_out, not_32_out, c, not_33_out);
  and and_17 (and_17_out, not_34_out, not_35_out, c, not_36_out);
  and and_18 (and_18_out, not_37_out, b, not_38_out, e);
  and and_19 (and_19_out, not_39_out, b, d, not_40_out);
  and and_20 (and_20_out, not_41_out, b, c, d);
  and and_21 (and_21_out, a, not_42_out, not_43_out, d);
  and and_22 (and_22_out, not_44_out, not_45_out, e);
  and and_23 (and_23_out, not_46_out, d, not_47_out);
  and and_24 (and_24_out, not_48_out, b, not_49_out);
  and and_25 (and_25_out, a, not_50_out, not_51_out, e);
  or or_1 (t, and_1_out, and_2_out);
  or or_2 (u, and_3_out, and_4_out);
  or or_3 (v, and_5_out, and_6_out);
  or or_4 (w, and_7_out, and_8_out, and_9_out, and_10_out);
  or or_5 (x, and_11_out, and_12_out, and_13_out, and_14_out);
  or or_6 (y, and_15_out, and_16_out, and_17_out, and_18_out, and_19_out, and_20_out, and_21_out);
  or or_7 (z, and_22_out, and_23_out, and_24_out, and_25_out);
endmodule

module CapitalLetter1 (
  input  a,
  input  b,
  input  c,
  input  d,
  input  e,
  output x,
  output y,
  output z,
  output u,
  output v
);

  wire and_1_out, and_2_out, and_3_out, and_4_out, and_5_out, and_6_out, and_7_out, and_8_out, and_9_out,
       and_10_out, and_11_out, and_12_out, and_13_out, and_14_out, and_15_out, and_16_out, and_17_out,
       and_18_out, and_19_out, and_20_out, and_21_out, and_22_out, and_23_out, and_24_out, and_25_out,
       and_26_out, and_27_out, and_28_out, and_29_out, and_30_out, and_31_out, not_1_out, not_2_out,
       not_3_out, not_4_out, not_5_out, not_6_out, not_7_out, not_8_out, not_9_out, not_10_out, not_11_out,
       not_12_out, not_13_out, not_14_out, not_15_out, not_16_out, not_17_out, not_18_out, not_19_out,
       not_20_out, not_21_out, not_22_out, not_23_out, not_24_out, not_25_out, not_26_out, not_27_out,
       not_28_out, not_29_out, not_30_out, not_31_out, not_32_out, not_33_out, not_34_out, not_35_out,
       not_36_out, not_37_out, not_38_out, not_39_out, not_40_out, not_41_out, not_42_out, not_43_out,
       not_44_out, not_45_out, not_46_out, not_47_out, not_48_out, not_49_out, not_50_out, not_51_out,
       not_52_out, not_53_out, not_54_out, not_55_out, not_56_out, not_57_out, not_58_out, not_59_out,
       not_60_out, not_61_out, not_62_out, not_63_out, not_64_out, not_65_out, not_66_out, not_67_out,
       not_68_out, not_69_out, not_70_out, not_71_out, not_72_out;

  not not_1 (not_1_out, a);
  not not_2 (not_2_out, c);
  not not_3 (not_3_out, d);
  not not_4 (not_4_out, e);
  not not_5 (not_5_out, b);
  not not_6 (not_6_out, c);
  not not_7 (not_7_out, d);
  not not_8 (not_8_out, a);
  not not_9 (not_9_out, b);
  not not_10 (not_10_out, e);
  not not_11 (not_11_out, a);
  not not_12 (not_12_out, d);
  not not_13 (not_13_out, b);
  not not_14 (not_14_out, c);
  not not_15 (not_15_out, e);
  not not_16 (not_16_out, a);
  not not_17 (not_17_out, c);
  not not_18 (not_18_out, a);
  not not_19 (not_19_out, d);
  not not_20 (not_20_out, a);
  not not_21 (not_21_out, a);
  not not_22 (not_22_out, a);
  not not_23 (not_23_out, b);
  not not_24 (not_24_out, d);
  not not_25 (not_25_out, b);
  not not_26 (not_26_out, c);
  not not_27 (not_27_out, a);
  not not_28 (not_28_out, b);
  not not_29 (not_29_out, c);
  not not_30 (not_30_out, d);
  not not_31 (not_31_out, a);
  not not_32 (not_32_out, e);
  not not_33 (not_33_out, a);
  not not_34 (not_34_out, b);
  not not_35 (not_35_out, c);
  not not_36 (not_36_out, e);
  not not_37 (not_37_out, b);
  not not_38 (not_38_out, d);
  not not_39 (not_39_out, e);
  not not_40 (not_40_out, a);
  not not_41 (not_41_out, c);
  not not_42 (not_42_out, a);
  not not_43 (not_43_out, b);
  not not_44 (not_44_out, d);
  not not_45 (not_45_out, a);
  not not_46 (not_46_out, b);
  not not_47 (not_47_out, a);
  not not_48 (not_48_out, c);
  not not_49 (not_49_out, a);
  not not_50 (not_50_out, d);
  not not_51 (not_51_out, e);
  not not_52 (not_52_out, b);
  not not_53 (not_53_out, c);
  not not_54 (not_54_out, d);
  not not_55 (not_55_out, b);
  not not_56 (not_56_out, c);
  not not_57 (not_57_out, b);
  not not_58 (not_58_out, d);
  not not_59 (not_59_out, a);
  not not_60 (not_60_out, c);
  not not_61 (not_61_out, a);
  not not_62 (not_62_out, b);
  not not_63 (not_63_out, e);
  not not_64 (not_64_out, a);
  not not_65 (not_65_out, d);
  not not_66 (not_66_out, e);
  not not_67 (not_67_out, b);
  not not_68 (not_68_out, d);
  not not_69 (not_69_out, a);
  not not_70 (not_70_out, c);
  not not_71 (not_71_out, b);
  not not_72 (not_72_out, c);
  and and_1 (and_1_out, not_1_out, not_2_out, not_3_out, not_4_out);
  and and_2 (and_2_out, not_5_out, not_6_out, not_7_out);
  and and_3 (and_3_out, not_8_out, not_9_out, c, d, not_10_out);
  and and_4 (and_4_out, not_11_out, b, c, not_12_out);
  and and_5 (and_5_out, a, not_13_out, not_14_out, not_15_out);
  and and_6 (and_6_out, not_16_out, not_17_out, d);
  and and_7 (and_7_out, not_18_out, c, not_19_out);
  and and_8 (and_8_out, not_20_out, c, e);
  and and_9 (and_9_out, not_21_out, b, e);
  and and_10 (and_10_out, not_22_out, b, c);
  and and_11 (and_11_out, a, not_23_out, not_24_out);
  and and_12 (and_12_out, a, not_25_out, not_26_out, e);
  and and_13 (and_13_out, not_27_out, not_28_out, not_29_out, not_30_out);
  and and_14 (and_14_out, not_31_out, c, d, not_32_out);
  and and_15 (and_15_out, not_33_out, b, c, d);
  and and_16 (and_16_out, a, not_34_out, not_35_out, d, not_36_out);
  and and_17 (and_17_out, a, not_37_out, c, not_38_out, not_39_out);
  and and_18 (and_18_out, not_40_out, not_41_out, d);
  and and_19 (and_19_out, not_42_out, not_43_out, c, not_44_out);
  and and_20 (and_20_out, not_45_out, not_46_out, c, e);
  and and_21 (and_21_out, not_47_out, b, not_48_out);
  and and_22 (and_22_out, not_49_out, b, not_50_out, not_51_out);
  and and_23 (and_23_out, a, not_52_out, not_53_out, not_54_out);
  and and_24 (and_24_out, a, not_55_out, not_56_out, e);
  and and_25 (and_25_out, a, not_57_out, not_58_out, e);
  and and_26 (and_26_out, not_59_out, not_60_out, d);
  and and_27 (and_27_out, not_61_out, not_62_out, c, not_63_out);
  and and_28 (and_28_out, not_64_out, c, not_65_out, not_66_out);
  and and_29 (and_29_out, not_67_out, c, not_68_out, e);
  and and_30 (and_30_out, not_69_out, b, not_70_out, e);
  and and_31 (and_31_out, a, not_71_out, not_72_out);
  or or_1 (x, and_1_out, and_2_out, and_3_out, and_4_out, and_5_out);
  or or_2 (y, and_6_out, and_7_out, and_8_out, and_9_out, and_10_out, and_11_out, and_12_out);
  or or_3 (z, and_13_out, and_14_out, and_15_out, and_16_out, and_17_out);
  or or_4 (u, and_18_out, and_19_out, and_20_out, and_21_out, and_22_out, and_23_out, and_24_out, and_25_out);
  or or_5 (v, and_26_out, and_27_out, and_28_out, and_29_out, and_30_out, and_31_out);
endmodule

module CapitalLetter2 (
  input  a,
  input  b,
  input  c,
  input  d,
  input  e,
  output x,
  output y,
  output z,
  output u,
  output v
);

  wire and_1_out, and_2_out, and_3_out, and_4_out, and_5_out, and_6_out, and_7_out, and_8_out, and_9_out,
       and_10_out, and_11_out, and_12_out, and_13_out, and_14_out, and_15_out, and_16_out, and_17_out,
       and_18_out, and_19_out, and_20_out, and_21_out, and_22_out, and_23_out, and_24_out, not_1_out,
       not_2_out, not_3_out, not_4_out, not_5_out, not_6_out, not_7_out, not_8_out, not_9_out, not_10_out,
       not_11_out, not_12_out, not_13_out, not_14_out, not_15_out, not_16_out, not_17_out, not_18_out,
       not_19_out, not_20_out, not_21_out, not_22_out, not_23_out, not_24_out, not_25_out, not_26_out,
       not_27_out, not_28_out, not_29_out, not_30_out, not_31_out, not_32_out, not_33_out, not_34_out,
       not_35_out, not_36_out, not_37_out, not_38_out, not_39_out, not_40_out, not_41_out, not_42_out,
       not_43_out, not_44_out, not_45_out, not_46_out, not_47_out, not_48_out, not_49_out, not_50_out,
       not_51_out, not_52_out, not_53_out;

  not not_1 (not_1_out, a);
  not not_2 (not_2_out, c);
  not not_3 (not_3_out, d);
  not not_4 (not_4_out, a);
  not not_5 (not_5_out, d);
  not not_6 (not_6_out, a);
  not not_7 (not_7_out, b);
  not not_8 (not_8_out, e);
  not not_9 (not_9_out, b);
  not not_10 (not_10_out, d);
  not not_11 (not_11_out, b);
  not not_12 (not_12_out, c);
  not not_13 (not_13_out, b);
  not not_14 (not_14_out, c);
  not not_15 (not_15_out, e);
  not not_16 (not_16_out, a);
  not not_17 (not_17_out, b);
  not not_18 (not_18_out, d);
  not not_19 (not_19_out, a);
  not not_20 (not_20_out, e);
  not not_21 (not_21_out, b);
  not not_22 (not_22_out, d);
  not not_23 (not_23_out, a);
  not not_24 (not_24_out, b);
  not not_25 (not_25_out, c);
  not not_26 (not_26_out, a);
  not not_27 (not_27_out, b);
  not not_28 (not_28_out, e);
  not not_29 (not_29_out, a);
  not not_30 (not_30_out, c);
  not not_31 (not_31_out, b);
  not not_32 (not_32_out, c);
  not not_33 (not_33_out, a);
  not not_34 (not_34_out, d);
  not not_35 (not_35_out, b);
  not not_36 (not_36_out, c);
  not not_37 (not_37_out, a);
  not not_38 (not_38_out, a);
  not not_39 (not_39_out, b);
  not not_40 (not_40_out, d);
  not not_41 (not_41_out, a);
  not not_42 (not_42_out, b);
  not not_43 (not_43_out, d);
  not not_44 (not_44_out, a);
  not not_45 (not_45_out, c);
  not not_46 (not_46_out, d);
  not not_47 (not_47_out, e);
  not not_48 (not_48_out, a);
  not not_49 (not_49_out, b);
  not not_50 (not_50_out, a);
  not not_51 (not_51_out, d);
  not not_52 (not_52_out, b);
  not not_53 (not_53_out, c);
  and and_1 (and_1_out, not_1_out, not_2_out, not_3_out);
  and and_2 (and_2_out, not_4_out, not_5_out, e);
  and and_3 (and_3_out, not_6_out, not_7_out, c, not_8_out);
  and and_4 (and_4_out, not_9_out, c, not_10_out, e);
  and and_5 (and_5_out, a, not_11_out, not_12_out, d, e);
  and and_6 (and_6_out, not_13_out, not_14_out, d, not_15_out);
  and and_7 (and_7_out, not_16_out, d, e);
  and and_8 (and_8_out, not_17_out, c, not_18_out);
  and and_9 (and_9_out, not_19_out, b, not_20_out);
  and and_10 (and_10_out, a, not_21_out, not_22_out);
  and and_11 (and_11_out, not_23_out, not_24_out, not_25_out);
  and and_12 (and_12_out, not_26_out, not_27_out, not_28_out);
  and and_13 (and_13_out, not_29_out, not_30_out, d, e);
  and and_14 (and_14_out, not_31_out, not_32_out, d, e);
  and and_15 (and_15_out, not_33_out, c, not_34_out);
  and and_16 (and_16_out, not_35_out, not_36_out);
  and and_17 (and_17_out, not_37_out, d);
  and and_18 (and_18_out, not_38_out, b);
  and and_19 (and_19_out, a, not_39_out, not_40_out);
  and and_20 (and_20_out, not_41_out, not_42_out, not_43_out);
  and and_21 (and_21_out, not_44_out, not_45_out, not_46_out, not_47_out);
  and and_22 (and_22_out, not_48_out, not_49_out, c);
  and and_23 (and_23_out, not_50_out, c, not_51_out, e);
  and and_24 (and_24_out, a, not_52_out, not_53_out, d, e);
  or or_1 (x, and_1_out, and_2_out, and_3_out, and_4_out, and_5_out);
  or or_2 (y, and_6_out, and_7_out, and_8_out, and_9_out, and_10_out);
  or or_3 (z, and_11_out, and_12_out, and_13_out, and_14_out, and_15_out);
  or or_4 (u, and_16_out, and_17_out, and_18_out, and_19_out);
  or or_5 (v, and_20_out, and_21_out, and_22_out, and_23_out, and_24_out);
endmodule

module CapitalLetter3 (
  input  a,
  input  b,
  input  c,
  input  d,
  input  e,
  output x,
  output y,
  output z,
  output u,
  output v
);

  wire and_1_out, and_2_out, and_3_out, and_4_out, and_5_out, and_6_out, and_7_out, and_8_out, and_9_out,
       and_10_out, and_11_out, and_12_out, and_13_out, and_14_out, and_15_out, and_16_out, and_17_out,
       and_18_out, and_19_out, and_20_out, and_21_out, and_22_out, and_23_out, and_24_out, not_1_out,
       not_2_out, not_3_out, not_4_out, not_5_out, not_6_out, not_7_out, not_8_out, not_9_out, not_10_out,
       not_11_out, not_12_out, not_13_out, not_14_out, not_15_out, not_16_out, not_17_out, not_18_out,
       not_19_out, not_20_out, not_21_out, not_22_out, not_23_out, not_24_out, not_25_out, not_26_out,
       not_27_out, not_28_out, not_29_out, not_30_out, not_31_out, not_32_out, not_33_out, not_34_out,
       not_35_out, not_36_out, not_37_out, not_38_out, not_39_out, not_40_out, not_41_out, not_42_out,
       not_43_out, not_44_out, not_45_out, not_46_out, not_47_out, not_48_out, not_49_out, not_50_out,
       not_51_out, not_52_out, not_53_out;

  not not_1 (not_1_out, a);
  not not_2 (not_2_out, c);
  not not_3 (not_3_out, b);
  not not_4 (not_4_out, c);
  not not_5 (not_5_out, a);
  not not_6 (not_6_out, b);
  not not_7 (not_7_out, c);
  not not_8 (not_8_out, a);
  not not_9 (not_9_out, b);
  not not_10 (not_10_out, d);
  not not_11 (not_11_out, e);
  not not_12 (not_12_out, a);
  not not_13 (not_13_out, b);
  not not_14 (not_14_out, b);
  not not_15 (not_15_out, d);
  not not_16 (not_16_out, a);
  not not_17 (not_17_out, d);
  not not_18 (not_18_out, b);
  not not_19 (not_19_out, d);
  not not_20 (not_20_out, e);
  not not_21 (not_21_out, a);
  not not_22 (not_22_out, b);
  not not_23 (not_23_out, d);
  not not_24 (not_24_out, b);
  not not_25 (not_25_out, c);
  not not_26 (not_26_out, d);
  not not_27 (not_27_out, a);
  not not_28 (not_28_out, a);
  not not_29 (not_29_out, e);
  not not_30 (not_30_out, b);
  not not_31 (not_31_out, c);
  not not_32 (not_32_out, e);
  not not_33 (not_33_out, a);
  not not_34 (not_34_out, b);
  not not_35 (not_35_out, c);
  not not_36 (not_36_out, a);
  not not_37 (not_37_out, c);
  not not_38 (not_38_out, a);
  not not_39 (not_39_out, e);
  not not_40 (not_40_out, b);
  not not_41 (not_41_out, c);
  not not_42 (not_42_out, e);
  not not_43 (not_43_out, a);
  not not_44 (not_44_out, b);
  not not_45 (not_45_out, d);
  not not_46 (not_46_out, a);
  not not_47 (not_47_out, b);
  not not_48 (not_48_out, a);
  not not_49 (not_49_out, c);
  not not_50 (not_50_out, d);
  not not_51 (not_51_out, a);
  not not_52 (not_52_out, d);
  not not_53 (not_53_out, e);
  and and_1 (and_1_out, not_1_out, not_2_out);
  and and_2 (and_2_out, not_3_out, not_4_out, e);
  and and_3 (and_3_out, not_5_out, d);
  and and_4 (and_4_out, not_6_out, not_7_out, d);
  and and_5 (and_5_out, not_8_out, b);
  and and_6 (and_6_out, a, not_9_out, c, not_10_out, not_11_out);
  and and_7 (and_7_out, not_12_out, not_13_out, d);
  and and_8 (and_8_out, not_14_out, c, not_15_out);
  and and_9 (and_9_out, not_16_out, b, not_17_out, e);
  and and_10 (and_10_out, a, not_18_out, not_19_out, not_20_out);
  and and_11 (and_11_out, not_21_out, not_22_out, not_23_out);
  and and_12 (and_12_out, not_24_out, not_25_out, not_26_out);
  and and_13 (and_13_out, not_27_out, c, d, e);
  and and_14 (and_14_out, not_28_out, b, not_29_out);
  and and_15 (and_15_out, a, not_30_out, not_31_out, not_32_out);
  and and_16 (and_16_out, not_33_out, not_34_out, not_35_out);
  and and_17 (and_17_out, not_36_out, not_37_out, e);
  and and_18 (and_18_out, not_38_out, d, not_39_out);
  and and_19 (and_19_out, not_40_out, not_41_out, d, not_42_out);
  and and_20 (and_20_out, not_43_out, b, c);
  and and_21 (and_21_out, a, not_44_out, c, not_45_out);
  and and_22 (and_22_out, not_46_out, not_47_out, c, d);
  and and_23 (and_23_out, not_48_out, b, not_49_out, not_50_out, e);
  and and_24 (and_24_out, not_51_out, b, c, not_52_out, not_53_out);
  or or_1 (x, and_1_out, and_2_out, and_3_out, and_4_out, and_5_out, and_6_out);
  or or_2 (y, and_7_out, and_8_out, and_9_out, and_10_out);
  or or_3 (z, and_11_out, and_12_out, and_13_out, and_14_out, and_15_out);
  or or_4 (u, and_16_out, and_17_out, and_18_out, and_19_out, and_20_out, and_21_out);
  or or_5 (v, and_22_out, and_23_out, and_24_out);
endmodule

module CapitalLetter5 (
  input  a,
  input  b,
  input  c,
  input  d,
  input  e,
  output x,
  output y,
  output z,
  output u,
  output v
);

  wire and_1_out, and_2_out, and_3_out, not_1_out, not_2_out, not_3_out, not_4_out;

  not not_1 (not_1_out, b);
  not not_2 (not_2_out, c);
  not not_3 (not_3_out, d);
  not not_4 (not_4_out, e);
  and and_1 (and_1_out, not_1_out, c, d);
  and and_2 (and_2_out, b, not_2_out);
  and and_3 (and_3_out, b, not_3_out);
  or or_1 (z, not_4_out, and_1_out, and_2_out, and_3_out, a);

  assign u = 1'b1;
  assign v = 1'b1;
  assign x = 1'b1;
  assign y = 1'b1;
endmodule

module CapitalLetter6 (
  input  a,
  input  b,
  input  c,
  input  d,
  input  e,
  output x,
  output y,
  output z,
  output u,
  output v
);

  wire and_1_out, and_2_out, and_3_out, and_4_out, and_5_out, and_6_out, not_1_out, not_2_out, not_3_out,
       not_4_out, not_5_out, not_6_out, not_7_out, not_8_out;

  not not_1 (not_1_out, b);
  not not_2 (not_2_out, c);
  not not_3 (not_3_out, d);
  not not_4 (not_4_out, b);
  not not_5 (not_5_out, c);
  not not_6 (not_6_out, d);
  not not_7 (not_7_out, e);
  and and_1 (and_1_out, not_1_out, c, d);
  and and_2 (and_2_out, b, not_2_out);
  and and_3 (and_3_out, b, not_3_out);
  not not_8 (not_8_out, e);
  and and_4 (and_4_out, not_4_out, c, d);
  and and_5 (and_5_out, b, not_5_out);
  and and_6 (and_6_out, b, not_6_out);
  or or_1 (u, not_7_out, and_1_out, and_2_out, and_3_out, a);
  or or_2 (v, not_8_out, and_4_out, and_5_out, and_6_out, a);

  assign x = 1'b1;
  assign y = 1'b1;
  assign z = 1'b1;
endmodule

module timerFSM (
  input  RESET,
  input  [1:0] B1_B0,
  input  DIP,
  input  ChM,
  input  CLK32k,
  input  CLK2k,
  input  CLK4,
  output [7:0] sevsegCode_5,
  output [7:0] sevsegCode_4,
  output [7:0] sevsegCode_3,
  output [7:0] sevsegCode_2,
  output [7:0] sevsegCode_1,
  output [7:0] sevsegCode_0
);

  wire and_1_out, and_2_out, and_3_out, and_4_out, changeTimer_1_hloadtendi, changeTimer_1_hloaduendi,
       changeTimer_1_minloadtendi, changeTimer_1_minloaduendi, changeTimer_1_secloadtendi,
       changeTimer_1_secloaduendi, counter_1_carry, d_ff_1_q, d_ff_2_q, d_ff_3_q, d_ff_4_q, d_ff_4_qn,
       fsm_1_q0, fsm_1_q1, fsm_1_q2, or_1_out, or_2_out, TIMER_1_finished, TIMER_1_hloadt, TIMER_1_hloadu,
       TIMER_1_minloadt, TIMER_1_minloadu, TIMER_1_secloadt, TIMER_1_secloadu, TransitLogic_1_reset,
       TransitLogic_1_setup, TransitLogic_1_start;
  wire [3:0] changeTimer_1_hloadt_4, changeTimer_1_hloadu_4, changeTimer_1_minloadt_4,
       changeTimer_1_minloadu_4, changeTimer_1_secloadt_4, changeTimer_1_secloadu_4, TIMER_1_ht_4,
       TIMER_1_hu_4, TIMER_1_mint_4, TIMER_1_minu_4, TIMER_1_sect_4, TIMER_1_secu_4;

  and and_1 (and_1_out, B1_B0[1], ~ChM);  // AND_Gate
  and and_2 (and_2_out, B1_B0[0], ~ChM);  // AND_Gate
  fsm fsm_1 (
    .finish(TIMER_1_finished), .D2(d_ff_3_q), .D1(d_ff_2_q), .D0(d_ff_1_q), .DIP(DIP), .B1(and_1_out),
    .B0(and_2_out), .Q2(fsm_1_q2), .Q1(fsm_1_q1), .Q0(fsm_1_q0));
  D_Flip_Flop d_ff_1 (.D(fsm_1_q0), .clk(CLK32k), .Q(d_ff_1_q), .reset(RESET));  // open: Qn, preset
  D_Flip_Flop d_ff_2 (.D(fsm_1_q1), .clk(CLK32k), .Q(d_ff_2_q), .reset(RESET));  // open: Qn, preset
  D_Flip_Flop d_ff_3 (.D(fsm_1_q2), .clk(CLK32k), .Q(d_ff_3_q), .reset(RESET));  // open: Qn, preset
  TransitLogic TransitLogic_1 (
    .Q2(d_ff_3_q), .Q1(d_ff_2_q), .Q0(d_ff_1_q), .START(TransitLogic_1_start), .RESET(TransitLogic_1_reset),
    .SETUP(TransitLogic_1_setup));
  and and_3 (and_3_out, TransitLogic_1_start, ~TIMER_1_finished);  // AND_Gate
  changeTimer changeTimer_1 (
    .DIP(TransitLogic_1_setup), .B1_B0(B1_B0), .CLK32k(CLK32k), .RESET(RESET),
    .HloadT_4(changeTimer_1_hloadt_4), .HloadTEnDi(changeTimer_1_hloadtendi),
    .HloadU_4(changeTimer_1_hloadu_4), .HloadUEnDi(changeTimer_1_hloaduendi),
    .MINloadT_4(changeTimer_1_minloadt_4), .MINloadTEnDi(changeTimer_1_minloadtendi),
    .MINloadU_4(changeTimer_1_minloadu_4), .MINloadUEnDi(changeTimer_1_minloaduendi),
    .SECloadT_4(changeTimer_1_secloadt_4), .SECloadTEnDi(changeTimer_1_secloadtendi),
    .SECloadU_4(changeTimer_1_secloadu_4), .SECloadUEnDi(changeTimer_1_secloaduendi));
  or or_1 (or_1_out, TransitLogic_1_reset, RESET);
  and and_4 (and_4_out, TransitLogic_1_start, TIMER_1_finished);
  TIMER TIMER_1 (
    .START(and_3_out), .RESET(or_1_out), .CLK2k(CLK2k), .HloadT_4(changeTimer_1_hloadt_4),
    .HloadTEnDi(changeTimer_1_hloadtendi), .HloadU_4(changeTimer_1_hloadu_4),
    .HloadUEnDi(changeTimer_1_hloaduendi), .MINloadT_4(changeTimer_1_minloadt_4),
    .MINloadTEnDi(changeTimer_1_minloadtendi), .MINloadU_4(changeTimer_1_minloadu_4),
    .MINloadUEnDi(changeTimer_1_minloaduendi), .SECloadT_4(changeTimer_1_secloadt_4),
    .SECloadTEnDi(changeTimer_1_secloadtendi), .SECloadU_4(changeTimer_1_secloadu_4),
    .SECloadUEnDi(changeTimer_1_secloaduendi), .HT_4(TIMER_1_ht_4), .HU_4(TIMER_1_hu_4),
    .MINT_4(TIMER_1_mint_4), .MINU_4(TIMER_1_minu_4), .SECT_4(TIMER_1_sect_4), .SECU_4(TIMER_1_secu_4),
    .HloadT(TIMER_1_hloadt), .HloadU(TIMER_1_hloadu), .MINloadT(TIMER_1_minloadt),
    .MINloadU(TIMER_1_minloadu), .SECloadT(TIMER_1_secloadt), .SECloadU(TIMER_1_secloadu),
    .finished(TIMER_1_finished));
  timerView timerView_1 (
    .HT_4(TIMER_1_ht_4), .HU_4(TIMER_1_hu_4), .MINT_4(TIMER_1_mint_4), .MINU_4(TIMER_1_minu_4),
    .SECT_4(TIMER_1_sect_4), .SECU_4(TIMER_1_secu_4), .HloadT(TIMER_1_hloadt), .HloadU(TIMER_1_hloadu),
    .MINloadT(TIMER_1_minloadt), .MINloadU(TIMER_1_minloadu), .SECloadT(TIMER_1_secloadt),
    .SECloadU(TIMER_1_secloadu), .RESET(TransitLogic_1_reset), .CLK4(CLK4), .sevsegCode_5(sevsegCode_5),
    .sevsegCode_4(sevsegCode_4), .sevsegCode_3(sevsegCode_3), .sevsegCode_2(sevsegCode_2),
    .sevsegCode_1(sevsegCode_1), .sevsegCode_0(sevsegCode_0));
  D_Flip_Flop d_ff_4 (
    .D(d_ff_4_qn), .clk(and_4_out), .Q(d_ff_4_q), .Qn(d_ff_4_qn), .reset(counter_1_carry));  // open: preset
  or or_2 (or_2_out, RESET, counter_1_carry);
  LED LED_1 (.in(d_ff_4_q));
  Counter #(.width(5), .max('h1f)) counter_1 (
    .clr(or_2_out), .count(d_ff_4_q), .clk(CLK4), .carry(counter_1_carry));  // open: load, up, D, Q
endmodule

module TIMER (
  input  START,
  input  RESET,
  input  CLK2k,
  input  [3:0] HloadT_4,
  input  HloadTEnDi,
  input  [3:0] HloadU_4,
  input  HloadUEnDi,
  input  [3:0] MINloadT_4,
  input  MINloadTEnDi,
  input  [3:0] MINloadU_4,
  input  MINloadUEnDi,
  input  [3:0] SECloadT_4,
  input  SECloadTEnDi,
  input  [3:0] SECloadU_4,
  input  SECloadUEnDi,
  output [3:0] HT_4,
  output [3:0] HU_4,
  output [3:0] MINT_4,
  output [3:0] MINU_4,
  output [3:0] SECT_4,
  output [3:0] SECU_4,
  output HloadT,
  output HloadU,
  output MINloadT,
  output MINloadU,
  output SECloadT,
  output SECloadU,
  output finished
);

  wire clk2k_to_ticksec_timer_1_ticksec, FiftyNineZero_1_finished, FiftyNineZero_2_finished,
       FiftyNineZero_2_tickout, FiftyNineZero_3_finished, FiftyNineZero_3_tickout;

  clk2k_to_ticksec_timer clk2k_to_ticksec_timer_1 (
    .START(START), .RESET(RESET), .CLK2k(CLK2k), .TickSEC(clk2k_to_ticksec_timer_1_ticksec));
  FiftyNineZero FiftyNineZero_1 (
    .TickIn(FiftyNineZero_2_tickout), .loadT_4(HloadT_4), .loadTEnDi(HloadTEnDi), .loadU_4(HloadU_4),
    .loadUEnDi(HloadUEnDi), .RESET(RESET), .CLK2K(CLK2k), .curT_3(HT_4), .curU_4(HU_4),
    .finished(FiftyNineZero_1_finished));  // open: TickOut
  FiftyNineZero FiftyNineZero_2 (
    .TickIn(FiftyNineZero_3_tickout), .loadT_4(MINloadT_4), .loadTEnDi(MINloadTEnDi), .loadU_4(MINloadU_4),
    .loadUEnDi(MINloadUEnDi), .RESET(RESET), .CLK2K(CLK2k), .TickOut(FiftyNineZero_2_tickout),
    .curT_3(MINT_4), .curU_4(MINU_4), .finished(FiftyNineZero_2_finished));
  FiftyNineZero FiftyNineZero_3 (
    .TickIn(clk2k_to_ticksec_timer_1_ticksec), .loadT_4(SECloadT_4), .loadTEnDi(SECloadTEnDi),
    .loadU_4(SECloadU_4), .loadUEnDi(SECloadUEnDi), .RESET(RESET), .CLK2K(CLK2k),
    .TickOut(FiftyNineZero_3_tickout), .curT_3(SECT_4), .curU_4(SECU_4), .finished(FiftyNineZero_3_finished));
  and and_1 (finished, FiftyNineZero_1_finished, FiftyNineZero_2_finished, FiftyNineZero_3_finished);

  assign HloadT = HloadTEnDi;
  assign HloadU = HloadUEnDi;
  assign MINloadT = MINloadTEnDi;
  assign MINloadU = MINloadUEnDi;
  assign SECloadT = SECloadTEnDi;
  assign SECloadU = SECloadUEnDi;
endmodule

module TransitLogic (
  input  Q2,
  input  Q1,
  input  Q0,
  output START,
  output RESET,
  output SETUP
);

  wire not_1_out;

  not not_1 (not_1_out, Q1);
  and and_1 (RESET, Q1, Q0);
  and and_2 (START, not_1_out, Q0);

  assign SETUP = Q2;
endmodule

module fsm (
  input  finish,
  input  D2,
  input  D1,
  input  D0,
  input  DIP,
  input  B1,
  input  B0,
  output Q2,
  output Q1,
  output Q0
);

  wire and_1_out, and_2_out, and_3_out, and_4_out, and_5_out, and_6_out, and_7_out, and_8_out, and_9_out,
       and_10_out, and_11_out, and_12_out, and_13_out, and_14_out, not_1_out, not_2_out, not_3_out,
       not_4_out, not_5_out, not_6_out, not_7_out, not_8_out, not_9_out, not_10_out, not_11_out, not_12_out,
       not_13_out, not_14_out, not_15_out, not_16_out, not_17_out, not_18_out, not_19_out, not_20_out,
       not_21_out, not_22_out, not_23_out, not_24_out, not_25_out, not_26_out, not_27_out, not_28_out,
       not_29_out, not_30_out, not_31_out, not_32_out, not_33_out, not_34_out, not_35_out, not_36_out;

  not not_1 (not_1_out, finish);
  not not_2 (not_2_out, D1);
  not not_3 (not_3_out, finish);
  not not_4 (not_4_out, D0);
  not not_5 (not_5_out, D1);
  not not_6 (not_6_out, D0);
  not not_7 (not_7_out, D2);
  not not_8 (not_8_out, D1);
  not not_9 (not_9_out, DIP);
  not not_10 (not_10_out, B0);
  not not_11 (not_11_out, D2);
  not not_12 (not_12_out, D0);
  not not_13 (not_13_out, DIP);
  not not_14 (not_14_out, B0);
  not not_15 (not_15_out, D2);
  not not_16 (not_16_out, D0);
  not not_17 (not_17_out, DIP);
  not not_18 (not_18_out, D2);
  not not_19 (not_19_out, D0);
  not not_20 (not_20_out, D2);
  not not_21 (not_21_out, D0);
  not not_22 (not_22_out, DIP);
  not not_23 (not_23_out, B1);
  not not_24 (not_24_out, D2);
  not not_25 (not_25_out, D1);
  not not_26 (not_26_out, DIP);
  not not_27 (not_27_out, B1);
  not not_28 (not_28_out, D2);
  not not_29 (not_29_out, D1);
  not not_30 (not_30_out, DIP);
  not not_31 (not_31_out, D2);
  not not_32 (not_32_out, D0);
  not not_33 (not_33_out, DIP);
  not not_34 (not_34_out, B0);
  and and_1 (and_1_out, not_1_out, not_2_out, DIP);
  and and_2 (and_2_out, not_3_out, not_4_out, DIP);
  and and_3 (and_3_out, not_5_out, not_6_out, DIP);
  and and_4 (and_4_out, D2, DIP);
  and and_5 (and_5_out, not_7_out, not_8_out, D0, not_9_out, B1, not_10_out);
  and and_6 (and_6_out, not_11_out, D1, not_12_out, not_13_out, not_14_out);
  and and_7 (and_7_out, not_15_out, D1, not_16_out, not_17_out, B1);
  and and_8 (and_8_out, finish, not_35_out, D0);
  not not_35 (not_35_out, D1);
  and and_9 (and_9_out, finish, not_18_out, D1, not_19_out, DIP);
  and and_10 (and_10_out, not_20_out, not_21_out, not_22_out, not_23_out, B0);
  and and_11 (and_11_out, not_24_out, not_25_out, D0, not_26_out, not_27_out);
  and and_12 (and_12_out, not_28_out, not_29_out, D0, not_30_out, B0);
  and and_13 (and_13_out, not_31_out, D1, not_32_out, not_33_out, B1, not_34_out);
  and and_14 (and_14_out, finish, not_36_out, D0);
  not not_36 (not_36_out, D1);
  or or_1 (Q2, and_1_out, and_2_out, and_3_out, and_4_out);
  or or_2 (Q1, and_5_out, and_6_out, and_7_out, and_8_out, and_9_out);
  or or_3 (Q0, and_10_out, and_11_out, and_12_out, and_13_out, and_14_out);
endmodule

module FiftyNineZero (
  input  TickIn,
  input  [3:0] loadT_4,
  input  loadTEnDi,
  input  [3:0] loadU_4,
  input  loadUEnDi,
  input  RESET,
  input  CLK2K,
  output TickOut,
  output [3:0] curT_3,
  output [3:0] curU_4,
  output finished
);

  wire and_1_out, counter_1_carry, counter_2_carry;
  wire [2:0] bit_extender_1_out, counter_1_q, load_3_timer_1_out0;
  wire [3:0] counter_2_q;

  and and_1 (and_1_out, counter_2_carry, TickIn);
  Bit_Extender #(.in_width(4), .out_width(3), .\type ("zero")) bit_extender_1 (.in(loadT_4), .out(bit_extender_1_out));
  Counter #(.width(3), .max('h5)) counter_1 (
    .clr(RESET), .load(loadTEnDi), .up(1'b0), .count(and_1_out), .clk(CLK2K), .D(bit_extender_1_out),
    .carry(counter_1_carry), .Q(counter_1_q));
  Counter #(.width(4), .max('h9)) counter_2 (
    .clr(RESET), .load(loadUEnDi), .up(1'b0), .count(TickIn), .clk(CLK2K), .D(loadU_4),
    .carry(counter_2_carry), .Q(counter_2_q));
  and and_2 (TickOut, TickIn, counter_1_carry, counter_2_carry);
  and and_3 (finished, counter_2_carry, counter_1_carry);
  load_3_timer load_3_timer_1 (
    .val(counter_1_q), .loadValue(loadT_4), .loadEnDi(loadTEnDi), .OUT0(load_3_timer_1_out0));
  assign curT_3 = {{1{1'b0}}, load_3_timer_1_out0};  // Bit_Extender bit_extender_2
  load_4_timer load_4_timer_1 (.val(counter_2_q), .loadValue(loadU_4), .loadEnDi(loadUEnDi), .OUT0(curU_4));
endmodule

module clk2k_to_ticksec_timer (
  input  START,
  input  RESET,
  input  CLK2k,
  output TickSEC
);

  Counter #(.width(10), .max('h3e9)) counter_1 (
    .clr(RESET), .count(START), .clk(CLK2k), .carry(TickSEC));  // open: load, up, D, Q
endmodule

module timerView (
  input  [3:0] HT_4,
  input  [3:0] HU_4,
  input  [3:0] MINT_4,
  input  [3:0] MINU_4,
  input  [3:0] SECT_4,
  input  [3:0] SECU_4,
  input  HloadT,
  input  HloadU,
  input  MINloadT,
  input  MINloadU,
  input  SECloadT,
  input  SECloadU,
  input  RESET,
  input  CLK4,
  output [7:0] sevsegCode_5,
  output [7:0] sevsegCode_4,
  output [7:0] sevsegCode_3,
  output [7:0] sevsegCode_2,
  output [7:0] sevsegCode_1,
  output [7:0] sevsegCode_0
);

  wire and_1_out, and_2_out, and_3_out, and_4_out, and_5_out, and_6_out, or_1_out, t_ff_1_q;
  wire [6:0] bit_extender_2_out, bit_extender_4_out, multiplexer_2_out, multiplexer_4_out;
  wire [7:0] bit_extender_1_out, bit_extender_3_out, bit_extender_5_out, bit_extender_6_out;

  assign bit_extender_1_out = {{4{1'b0}}, HT_4};  // Bit_Extender bit_extender_1
  assign bit_extender_2_out = {{3{1'b0}}, HU_4};  // Bit_Extender bit_extender_2
  assign bit_extender_3_out = {{4{1'b0}}, MINT_4};  // Bit_Extender bit_extender_3
  assign bit_extender_4_out = {{3{1'b0}}, MINU_4};  // Bit_Extender bit_extender_4
  assign bit_extender_5_out = {{4{1'b0}}, SECT_4};  // Bit_Extender bit_extender_5
  assign bit_extender_6_out = {{4{1'b0}}, SECU_4};  // Bit_Extender bit_extender_6
  T_Flip_Flop t_ff_1 (.T(or_1_out), .clk(CLK4), .Q(t_ff_1_q), .reset(RESET));  // open: Qn, preset
  or or_1 (or_1_out, HloadT, HloadU, MINloadT, MINloadU, SECloadT, SECloadU);
  Multiplexer #(.width(8), .enable("false")) multiplexer_1 (
    .in0(bit_extender_1_out), .in1(8'h7f), .out(sevsegCode_5), .sel(and_1_out));
  and and_1 (and_1_out, HloadT, t_ff_1_q);
  and and_2 (and_2_out, HloadU, t_ff_1_q);
  Multiplexer #(.width(7), .enable("false")) multiplexer_2 (
    .in0(bit_extender_2_out), .in1({7{1'b1}}), .out(multiplexer_2_out), .sel(and_2_out));
  Multiplexer #(.width(8), .enable("false")) multiplexer_3 (
    .in0(bit_extender_3_out), .in1(8'h7f), .out(sevsegCode_3), .sel(and_3_out));
  and and_3 (and_3_out, MINloadT, t_ff_1_q);
  Multiplexer #(.width(7), .enable("false")) multiplexer_4 (
    .in0(bit_extender_4_out), .in1({7{1'b1}}), .out(multiplexer_4_out), .sel(and_4_out));
  and and_4 (and_4_out, MINloadU, t_ff_1_q);
  assign sevsegCode_4 = {{1{1'b1}}, multiplexer_2_out};  // Bit_Extender bit_extender_7
  assign sevsegCode_2 = {{1{1'b1}}, multiplexer_4_out};  // Bit_Extender bit_extender_8
  Multiplexer #(.width(8), .enable("false")) multiplexer_5 (
    .in0(bit_extender_5_out), .in1(8'h7f), .out(sevsegCode_1), .sel(and_5_out));
  and and_5 (and_5_out, SECloadT, t_ff_1_q);
  Multiplexer #(.width(8), .enable("false")) multiplexer_6 (
    .in0(bit_extender_6_out), .in1(8'h7f), .out(sevsegCode_0), .sel(and_6_out));
  and and_6 (and_6_out, SECloadU, t_ff_1_q);
endmodule

module load_3_timer (
  input  [2:0] val,
  input  [3:0] loadValue,
  input  loadEnDi,
  output [2:0] OUT0
);

  wire [2:0] bit_extender_1_out;

  Bit_Extender #(.in_width(4), .out_width(3)) bit_extender_1 (.in(loadValue), .out(bit_extender_1_out));
  Multiplexer #(.width(3), .enable("false")) multiplexer_1 (
    .in0(val), .in1(bit_extender_1_out), .out(OUT0), .sel(loadEnDi));
endmodule

module load_4_timer (
  input  [3:0] val,
  input  [3:0] loadValue,
  input  loadEnDi,
  output [3:0] OUT0
);

  Multiplexer #(.width(4), .enable("false")) multiplexer_1 (.in0(val), .in1(loadValue), .out(OUT0), .sel(loadEnDi));
endmodule

module changeTimer (
  input  DIP,
  input  [1:0] B1_B0,
  input  CLK32k,
  input  RESET,
  output [3:0] HloadT_4,
  output HloadTEnDi,
  output [3:0] HloadU_4,
  output HloadUEnDi,
  output [3:0] MINloadT_4,
  output MINloadTEnDi,
  output [3:0] MINloadU_4,
  output MINloadUEnDi,
  output [3:0] SECloadT_4,
  output SECloadTEnDi,
  output [3:0] SECloadU_4,
  output SECloadUEnDi
);

  wire and_1_out, and_2_out, demultiplexer_1_out1, demultiplexer_1_out2, demultiplexer_1_out3,
       demultiplexer_1_out4, demultiplexer_1_out5, demultiplexer_1_out6, demultiplexer_2_out0, or_1_out,
       or_2_out;
  wire [2:0] counter_1_q, counter_2_q, counter_4_q, counter_6_q;

  and and_1 (and_1_out, B1_B0[0], DIP);
  and and_2 (and_2_out, DIP, B1_B0[1]);
  Counter #(.width(3), .max('h6)) counter_1 (
    .clr(or_1_out), .count(and_1_out), .clk(CLK32k), .Q(counter_1_q));  // open: load, up, D, carry
  or or_1 (or_1_out, ~DIP, RESET);  // OR_Gate
  Demultiplexer #(.select(3), .enable("false")) demultiplexer_1 (
    .out1(demultiplexer_1_out1), .out2(demultiplexer_1_out2), .out3(demultiplexer_1_out3),
    .out4(demultiplexer_1_out4), .out5(demultiplexer_1_out5), .out6(demultiplexer_1_out6), .in(and_2_out),
    .sel(counter_1_q));  // open: out0, out7
  Demultiplexer #(.select(3), .enable("false")) demultiplexer_2 (
    .out0(demultiplexer_2_out0), .out1(HloadTEnDi), .out2(HloadUEnDi), .out3(MINloadTEnDi),
    .out4(MINloadUEnDi), .out5(SECloadTEnDi), .out6(SECloadUEnDi), .in(1'b1), .sel(counter_1_q));  // open: out7
  or or_2 (or_2_out, demultiplexer_2_out0, RESET);
  Counter #(.width(3), .max('h5)) counter_2 (
    .clr(or_2_out), .count(demultiplexer_1_out1), .clk(CLK32k), .Q(counter_2_q));  // open: load, up, D, carry
  Counter #(.width(4), .max('h9)) counter_3 (
    .clr(or_2_out), .count(demultiplexer_1_out2), .clk(CLK32k), .Q(HloadU_4));  // open: load, up, D, carry
  Counter #(.width(3), .max('h5)) counter_4 (
    .clr(or_2_out), .count(demultiplexer_1_out3), .clk(CLK32k), .Q(counter_4_q));  // open: load, up, D, carry
  Counter #(.width(4), .max('h9)) counter_5 (
    .clr(or_2_out), .count(demultiplexer_1_out4), .clk(CLK32k), .Q(MINloadU_4));  // open: load, up, D, carry
  Counter #(.width(3), .max('h5)) counter_6 (
    .clr(or_2_out), .count(demultiplexer_1_out5), .clk(CLK32k), .Q(counter_6_q));  // open: load, up, D, carry
  Counter #(.width(4), .max('h9)) counter_7 (
    .clr(or_2_out), .count(demultiplexer_1_out6), .clk(CLK32k), .Q(SECloadU_4));  // open: load, up, D, carry
  assign HloadT_4 = {{1{1'b0}}, counter_2_q};  // Bit_Extender bit_extender_1
  assign MINloadT_4 = {{1{1'b0}}, counter_4_q};  // Bit_Extender bit_extender_2
  assign SECloadT_4 = {{1{1'b0}}, counter_6_q};  // Bit_Extender bit_extender_3

  // Other names for the same wires on the sheet: clk = CLK32k
endmodule

module CHRONO (
  input  RESET,
  input  [1:0] B1_B0,
  input  ChMode,
  input  CLK32k,
  output [7:0] Min_Led2,
  output [7:0] Min_Led1,
  output [7:0] Sec_Led2,
  output [7:0] Sec_Led1,
  output [7:0] Milli_Led2,
  output [7:0] Milli_Led1
);

  wire and_1_out, and_2_out, or_1_out, TranLogic2_Chrono_1_d1, TranLogic2_Chrono_1_d2;
  wire [1:0] d_ff_1_q, OutLogic_Chrono_1_run_reset;
  wire [3:0] Dec100_Led1_1_u, Dec100_Led1_2_u, Dec100_Led1_3_u, Dec100_Led2_1_u, Dec100_Led2_2_u,
       Dec100_Led2_3_u;
  wire [6:0] bit_extender_2_out, bit_extender_4_out;
  wire [7:0] ZeroToAll_1_centi, ZeroToAll_1_min, ZeroToAll_1_sec;

  and and_1 (and_1_out, B1_B0[1], ~ChMode);  // AND_Gate
  and and_2 (and_2_out, B1_B0[0], ~ChMode);  // AND_Gate
  TranLogic2_Chrono TranLogic2_Chrono_1 (
    .Q1(d_ff_1_q[0]), .Q2(d_ff_1_q[1]), .R(and_1_out), .S(and_2_out), .D1(TranLogic2_Chrono_1_d1),
    .D2(TranLogic2_Chrono_1_d2));
  D_Flip_Flop d_ff_1 (.D(TranLogic2_Chrono_1_d1), .clk(CLK32k), .Q(d_ff_1_q[0]), .reset(RESET));  // open: Qn, preset
  D_Flip_Flop d_ff_2 (.D(TranLogic2_Chrono_1_d2), .clk(CLK32k), .Q(d_ff_1_q[1]), .reset(RESET));  // open: Qn, preset
  OutLogic_Chrono OutLogic_Chrono_1 (.D1_D2(d_ff_1_q), .Run_Reset(OutLogic_Chrono_1_run_reset));
  or or_1 (or_1_out, OutLogic_Chrono_1_run_reset[1], RESET);
  ZeroToAll ZeroToAll_1 (
    .Run(OutLogic_Chrono_1_run_reset[0]), .Reset(or_1_out), .Clk(CLK32k), .Centi(ZeroToAll_1_centi),
    .Sec(ZeroToAll_1_sec), .Min(ZeroToAll_1_min));
  Dec100_Led1 Dec100_Led1_1 (
    .a(ZeroToAll_1_centi[6]), .b(ZeroToAll_1_centi[5]), .c(ZeroToAll_1_centi[4]), .d(ZeroToAll_1_centi[3]),
    .e(ZeroToAll_1_centi[2]), .f(ZeroToAll_1_centi[1]), .g(ZeroToAll_1_centi[0]), .x(Dec100_Led1_1_u[3]),
    .y(Dec100_Led1_1_u[2]), .z(Dec100_Led1_1_u[1]), .u(Dec100_Led1_1_u[0]));
  Dec100_Led1 Dec100_Led1_2 (
    .a(ZeroToAll_1_sec[6]), .b(ZeroToAll_1_sec[5]), .c(ZeroToAll_1_sec[4]), .d(ZeroToAll_1_sec[3]),
    .e(ZeroToAll_1_sec[2]), .f(ZeroToAll_1_sec[1]), .g(ZeroToAll_1_sec[0]), .x(Dec100_Led1_2_u[3]),
    .y(Dec100_Led1_2_u[2]), .z(Dec100_Led1_2_u[1]), .u(Dec100_Led1_2_u[0]));
  Dec100_Led1 Dec100_Led1_3 (
    .a(ZeroToAll_1_min[6]), .b(ZeroToAll_1_min[5]), .c(ZeroToAll_1_min[4]), .d(ZeroToAll_1_min[3]),
    .e(ZeroToAll_1_min[2]), .f(ZeroToAll_1_min[1]), .g(ZeroToAll_1_min[0]), .x(Dec100_Led1_3_u[3]),
    .y(Dec100_Led1_3_u[2]), .z(Dec100_Led1_3_u[1]), .u(Dec100_Led1_3_u[0]));
  Dec100_Led2 Dec100_Led2_1 (
    .a(ZeroToAll_1_centi[6]), .b(ZeroToAll_1_centi[5]), .c(ZeroToAll_1_centi[4]), .d(ZeroToAll_1_centi[3]),
    .e(ZeroToAll_1_centi[2]), .f(ZeroToAll_1_centi[1]), .g(ZeroToAll_1_centi[0]), .x(Dec100_Led2_1_u[3]),
    .y(Dec100_Led2_1_u[2]), .z(Dec100_Led2_1_u[1]), .u(Dec100_Led2_1_u[0]));
  Dec100_Led2 Dec100_Led2_2 (
    .a(ZeroToAll_1_sec[6]), .b(ZeroToAll_1_sec[5]), .c(ZeroToAll_1_sec[4]), .d(ZeroToAll_1_sec[3]),
    .e(ZeroToAll_1_sec[2]), .f(ZeroToAll_1_sec[1]), .g(ZeroToAll_1_sec[0]), .x(Dec100_Led2_2_u[3]),
    .y(Dec100_Led2_2_u[2]), .z(Dec100_Led2_2_u[1]), .u(Dec100_Led2_2_u[0]));
  Dec100_Led2 Dec100_Led2_3 (
    .a(ZeroToAll_1_min[6]), .b(ZeroToAll_1_min[5]), .c(ZeroToAll_1_min[4]), .d(ZeroToAll_1_min[3]),
    .e(ZeroToAll_1_min[2]), .f(ZeroToAll_1_min[1]), .g(ZeroToAll_1_min[0]), .x(Dec100_Led2_3_u[3]),
    .y(Dec100_Led2_3_u[2]), .z(Dec100_Led2_3_u[1]), .u(Dec100_Led2_3_u[0]));
  assign Min_Led2 = {{4{1'b0}}, Dec100_Led2_3_u};  // Bit_Extender bit_extender_1
  assign bit_extender_2_out = {{3{1'b0}}, Dec100_Led1_3_u};  // Bit_Extender bit_extender_2
  assign Sec_Led2 = {{4{1'b0}}, Dec100_Led2_2_u};  // Bit_Extender bit_extender_3
  assign bit_extender_4_out = {{3{1'b0}}, Dec100_Led1_2_u};  // Bit_Extender bit_extender_4
  assign Milli_Led2 = {{4{1'b0}}, Dec100_Led2_1_u};  // Bit_Extender bit_extender_5
  assign Milli_Led1 = {{4{1'b0}}, Dec100_Led1_1_u};  // Bit_Extender bit_extender_6
  assign Min_Led1 = {{1{1'b1}}, bit_extender_2_out};  // Bit_Extender bit_extender_7
  assign Sec_Led1 = {{1{1'b1}}, bit_extender_4_out};  // Bit_Extender bit_extender_8
endmodule

module Dec100_Led1 (
  input  a,
  input  b,
  input  c,
  input  d,
  input  e,
  input  f,
  input  g,
  output x,
  output y,
  output z,
  output u
);

  wire and_1_out, and_2_out, and_3_out, and_4_out, and_5_out, and_6_out, and_7_out, and_8_out, and_9_out,
       and_10_out, and_11_out, and_12_out, and_13_out, and_14_out, and_15_out, and_16_out, and_17_out,
       and_18_out, and_19_out, and_20_out, and_21_out, and_22_out, and_23_out, and_24_out, and_25_out,
       and_26_out, and_27_out, and_28_out, and_29_out, and_30_out, and_31_out, and_32_out, and_33_out,
       and_34_out, and_35_out, and_36_out, and_37_out, and_38_out, and_39_out, and_40_out, and_41_out,
       and_42_out, not_1_out, not_2_out, not_3_out, not_4_out, not_5_out, not_6_out, not_7_out, not_8_out,
       not_9_out, not_10_out, not_11_out, not_12_out, not_13_out, not_14_out, not_15_out, not_16_out,
       not_17_out, not_18_out, not_19_out, not_20_out, not_21_out, not_22_out, not_23_out, not_24_out,
       not_25_out, not_26_out, not_27_out, not_28_out, not_29_out, not_30_out, not_31_out, not_32_out,
       not_33_out, not_34_out, not_35_out, not_36_out, not_37_out, not_38_out, not_39_out, not_40_out,
       not_41_out, not_42_out, not_43_out, not_44_out, not_45_out, not_46_out, not_47_out, not_48_out,
       not_49_out, not_50_out, not_51_out, not_52_out, not_53_out, not_54_out, not_55_out, not_56_out,
       not_57_out, not_58_out, not_59_out, not_60_out, not_61_out, not_62_out, not_63_out, not_64_out,
       not_65_out, not_66_out, not_67_out, not_68_out, not_69_out, not_70_out, not_71_out, not_72_out,
       not_73_out, not_74_out, not_75_out, not_76_out, not_77_out, not_78_out, not_79_out, not_80_out,
       not_81_out, not_82_out, not_83_out, not_84_out, not_85_out, not_86_out, not_87_out, not_88_out,
       not_89_out, not_90_out, not_91_out, not_92_out, not_93_out, not_94_out, not_95_out, not_96_out,
       not_97_out, not_98_out, not_99_out, not_100_out, not_101_out, not_102_out, not_103_out, not_104_out,
       not_105_out, not_106_out, not_107_out, not_108_out, not_109_out, not_110_out, not_111_out,
       not_112_out, not_113_out, not_114_out;

  not not_1 (not_1_out, a);
  not not_2 (not_2_out, b);
  not not_3 (not_3_out, c);
  not not_4 (not_4_out, e);
  not not_5 (not_5_out, f);
  not not_6 (not_6_out, a);
  not not_7 (not_7_out, b);
  not not_8 (not_8_out, d);
  not not_9 (not_9_out, e);
  not not_10 (not_10_out, a);
  not not_11 (not_11_out, b);
  not not_12 (not_12_out, f);
  not not_13 (not_13_out, a);
  not not_14 (not_14_out, c);
  not not_15 (not_15_out, d);
  not not_16 (not_16_out, a);
  not not_17 (not_17_out, d);
  not not_18 (not_18_out, e);
  not not_19 (not_19_out, f);
  not not_20 (not_20_out, e);
  not not_21 (not_21_out, b);
  not not_22 (not_22_out, c);
  not not_23 (not_23_out, d);
  not not_24 (not_24_out, f);
  not not_25 (not_25_out, b);
  not not_26 (not_26_out, c);
  not not_27 (not_27_out, e);
  not not_28 (not_28_out, f);
  not not_29 (not_29_out, c);
  not not_30 (not_30_out, d);
  not not_31 (not_31_out, e);
  not not_32 (not_32_out, f);
  not not_33 (not_33_out, a);
  not not_34 (not_34_out, b);
  not not_35 (not_35_out, c);
  not not_36 (not_36_out, d);
  not not_37 (not_37_out, a);
  not not_38 (not_38_out, c);
  not not_39 (not_39_out, a);
  not not_40 (not_40_out, b);
  not not_41 (not_41_out, e);
  not not_42 (not_42_out, f);
  not not_43 (not_43_out, a);
  not not_44 (not_44_out, b);
  not not_45 (not_45_out, e);
  not not_46 (not_46_out, a);
  not not_47 (not_47_out, e);
  not not_48 (not_48_out, f);
  not not_49 (not_49_out, a);
  not not_50 (not_50_out, c);
  not not_51 (not_51_out, d);
  not not_52 (not_52_out, e);
  not not_53 (not_53_out, a);
  not not_54 (not_54_out, c);
  not not_55 (not_55_out, f);
  not not_56 (not_56_out, a);
  not not_57 (not_57_out, d);
  not not_58 (not_58_out, b);
  not not_59 (not_59_out, c);
  not not_60 (not_60_out, d);
  not not_61 (not_61_out, e);
  not not_62 (not_62_out, c);
  not not_63 (not_63_out, e);
  not not_64 (not_64_out, b);
  not not_65 (not_65_out, c);
  not not_66 (not_66_out, f);
  not not_67 (not_67_out, d);
  not not_68 (not_68_out, f);
  not not_69 (not_69_out, b);
  not not_70 (not_70_out, c);
  not not_71 (not_71_out, e);
  not not_72 (not_72_out, f);
  not not_73 (not_73_out, e);
  not not_74 (not_74_out, b);
  not not_75 (not_75_out, c);
  not not_76 (not_76_out, d);
  not not_77 (not_77_out, e);
  not not_78 (not_78_out, a);
  not not_79 (not_79_out, b);
  not not_80 (not_80_out, d);
  not not_81 (not_81_out, b);
  not not_82 (not_82_out, c);
  not not_83 (not_83_out, f);
  not not_84 (not_84_out, a);
  not not_85 (not_85_out, b);
  not not_86 (not_86_out, d);
  not not_87 (not_87_out, e);
  not not_88 (not_88_out, f);
  not not_89 (not_89_out, a);
  not not_90 (not_90_out, b);
  not not_91 (not_91_out, e);
  not not_92 (not_92_out, a);
  not not_93 (not_93_out, c);
  not not_94 (not_94_out, d);
  not not_95 (not_95_out, f);
  not not_96 (not_96_out, c);
  not not_97 (not_97_out, e);
  not not_98 (not_98_out, a);
  not not_99 (not_99_out, d);
  not not_100 (not_100_out, f);
  not not_101 (not_101_out, e);
  not not_102 (not_102_out, f);
  not not_103 (not_103_out, b);
  not not_104 (not_104_out, c);
  not not_105 (not_105_out, f);
  not not_106 (not_106_out, b);
  not not_107 (not_107_out, f);
  not not_108 (not_108_out, b);
  not not_109 (not_109_out, d);
  not not_110 (not_110_out, d);
  not not_111 (not_111_out, e);
  not not_112 (not_112_out, f);
  not not_113 (not_113_out, c);
  not not_114 (not_114_out, d);
  and and_1 (and_1_out, not_1_out, not_2_out, not_3_out, d, not_4_out, not_5_out);
  and and_2 (and_2_out, not_6_out, not_7_out, c, not_8_out, not_9_out, f);
  and and_3 (and_3_out, not_10_out, not_11_out, c, d, e, not_12_out);
  and and_4 (and_4_out, not_13_out, b, not_14_out, not_15_out, e, f);
  and and_5 (and_5_out, not_16_out, b, c, not_17_out, not_18_out, not_19_out);
  and and_6 (and_6_out, b, c, d, not_20_out, f);
  and and_7 (and_7_out, a, not_21_out, not_22_out, not_23_out, e, not_24_out);
  and and_8 (and_8_out, a, not_25_out, not_26_out, d, e, f);
  and and_9 (and_9_out, a, c, d, not_27_out, not_28_out);
  and and_10 (and_10_out, a, b, not_29_out, not_30_out, not_31_out, f);
  and and_11 (and_11_out, a, b, d, e, not_32_out);
  and and_12 (and_12_out, a, b, c, e, f);
  and and_13 (and_13_out, not_33_out, not_34_out, not_35_out, not_36_out, e);
  and and_14 (and_14_out, not_37_out, not_38_out, d, e, f);
  and and_15 (and_15_out, not_39_out, not_40_out, c, not_41_out, not_42_out);
  and and_16 (and_16_out, not_43_out, not_44_out, c, d, not_45_out);
  and and_17 (and_17_out, not_46_out, c, d, not_47_out, not_48_out);
  and and_18 (and_18_out, not_49_out, b, not_50_out, not_51_out, not_52_out, f);
  and and_19 (and_19_out, not_53_out, b, not_54_out, e, not_55_out);
  and and_20 (and_20_out, not_56_out, b, c, not_57_out, e, f);
  and and_21 (and_21_out, a, not_58_out, not_59_out, not_60_out, not_61_out);
  and and_22 (and_22_out, a, not_62_out, d, not_63_out, f);
  and and_23 (and_23_out, a, not_64_out, not_65_out, d, e, not_66_out);
  and and_24 (and_24_out, a, c, not_67_out, e, not_68_out);
  and and_25 (and_25_out, a, not_69_out, c, e, f);
  and and_26 (and_26_out, a, b, not_70_out, not_71_out, not_72_out);
  and and_27 (and_27_out, a, b, c, not_73_out, f);
  and and_28 (and_28_out, not_74_out, not_75_out, not_76_out, not_77_out, f);
  and and_29 (and_29_out, not_78_out, not_79_out, not_80_out, e, f);
  and and_30 (and_30_out, not_81_out, not_82_out, d, e, not_83_out);
  and and_31 (and_31_out, not_84_out, not_85_out, c, not_86_out, not_87_out, not_88_out);
  and and_32 (and_32_out, not_89_out, not_90_out, c, d, not_91_out, f);
  and and_33 (and_33_out, not_92_out, b, not_93_out, not_94_out, not_95_out);
  and and_34 (and_34_out, b, not_96_out, d, not_97_out, f);
  and and_35 (and_35_out, not_98_out, b, d, e, f);
  and and_36 (and_36_out, b, c, not_99_out, e, not_100_out);
  and and_37 (and_37_out, b, c, d, not_101_out, not_102_out);
  and and_38 (and_38_out, a, not_103_out, not_104_out, d, not_105_out);
  and and_39 (and_39_out, a, not_106_out, d, e, not_107_out);
  and and_40 (and_40_out, a, not_108_out, c, not_109_out, f);
  and and_41 (and_41_out, a, b, not_110_out, not_111_out, not_112_out);
  and and_42 (and_42_out, a, b, not_113_out, not_114_out, e, f);
  or or_1 (x, and_1_out, and_2_out, and_3_out, and_4_out, and_5_out, and_6_out, and_7_out, and_8_out, and_9_out, and_10_out, and_11_out, and_12_out);
  or or_2 (y, and_13_out, and_14_out, and_15_out, and_16_out, and_17_out, and_18_out, and_19_out, and_20_out, and_21_out, and_22_out, and_23_out, and_24_out, and_25_out, and_26_out, and_27_out);
  or or_3 (z, and_28_out, and_29_out, and_30_out, and_31_out, and_32_out, and_33_out, and_34_out, and_35_out, and_36_out, and_37_out, and_38_out, and_39_out, and_40_out, and_41_out, and_42_out);

  assign u = g;
endmodule

module Dec100_Led2 (
  input  a,
  input  b,
  input  c,
  input  d,
  input  e,
  input  f,
  input  g,
  output x,
  output y,
  output z,
  output u
);

  wire and_1_out, and_2_out, and_3_out, and_4_out, and_5_out, and_6_out, and_7_out, and_8_out, and_9_out,
       and_10_out, and_11_out, and_12_out, and_13_out, and_14_out, and_15_out, and_16_out, and_17_out,
       and_18_out, and_19_out, and_20_out, and_21_out, and_22_out, not_1_out, not_2_out, not_3_out,
       not_4_out, not_5_out, not_6_out, not_7_out, not_8_out, not_9_out, not_10_out, not_11_out, not_12_out,
       not_13_out, not_14_out, not_15_out, not_16_out, not_17_out, not_18_out, not_19_out, not_20_out,
       not_21_out, not_22_out, not_23_out, not_24_out, not_25_out, not_26_out, not_27_out, not_28_out,
       not_29_out, not_30_out, not_31_out, not_32_out, not_33_out;

  not not_1 (not_1_out, e);
  not not_2 (not_2_out, b);
  not not_3 (not_3_out, c);
  not not_4 (not_4_out, a);
  not not_5 (not_5_out, b);
  not not_6 (not_6_out, a);
  not not_7 (not_7_out, b);
  not not_8 (not_8_out, a);
  not not_9 (not_9_out, a);
  not not_10 (not_10_out, c);
  not not_11 (not_11_out, d);
  not not_12 (not_12_out, b);
  not not_13 (not_13_out, c);
  not not_14 (not_14_out, b);
  not not_15 (not_15_out, c);
  not not_16 (not_16_out, b);
  not not_17 (not_17_out, c);
  not not_18 (not_18_out, b);
  not not_19 (not_19_out, a);
  not not_20 (not_20_out, b);
  not not_21 (not_21_out, d);
  not not_22 (not_22_out, e);
  not not_23 (not_23_out, a);
  not not_24 (not_24_out, d);
  not not_25 (not_25_out, e);
  not not_26 (not_26_out, c);
  not not_27 (not_27_out, d);
  not not_28 (not_28_out, e);
  not not_29 (not_29_out, a);
  not not_30 (not_30_out, d);
  not not_31 (not_31_out, e);
  not not_32 (not_32_out, c);
  not not_33 (not_33_out, c);
  and and_1 (and_1_out, a, c);
  or or_1 (x, and_1_out, and_2_out);
  and and_2 (and_2_out, a, b, not_1_out);
  and and_3 (and_3_out, b, d);
  or or_2 (y, and_3_out, and_4_out, and_5_out);
  and and_4 (and_4_out, b, c);
  and and_5 (and_5_out, a, not_2_out, not_3_out);
  and and_6 (and_6_out, not_4_out, not_5_out, c, e);
  and and_7 (and_7_out, not_6_out, not_7_out, c, d);
  and and_8 (and_8_out, not_8_out, c, d, e);
  and and_9 (and_9_out, not_9_out, b, not_10_out, not_11_out);
  and and_10 (and_10_out, a, not_12_out, not_13_out);
  and and_11 (and_11_out, not_14_out, not_15_out, d, f);
  and and_12 (and_12_out, not_16_out, not_17_out, d, e);
  and and_13 (and_13_out, not_18_out, d, e, f);
  and and_14 (and_14_out, not_19_out, not_20_out, c, not_21_out, not_22_out);
  and and_15 (and_15_out, not_23_out, c, not_24_out, not_25_out, f);
  and and_16 (and_16_out, b, not_26_out, not_27_out, not_28_out);
  and and_17 (and_17_out, not_29_out, b, not_30_out, e);
  and and_18 (and_18_out, b, c, d, not_31_out);
  and and_19 (and_19_out, a, not_32_out, e, f);
  and and_20 (and_20_out, a, not_33_out, d);
  and and_21 (and_21_out, a, d, f);
  and and_22 (and_22_out, a, d, e);
  or or_3 (z, and_6_out, and_7_out, and_8_out, and_9_out, and_10_out);
  or or_4 (u, and_11_out, and_12_out, and_13_out, and_14_out, and_15_out, and_16_out, and_17_out, and_18_out, and_19_out, and_20_out, and_21_out, and_22_out);
endmodule

module OutLogic_Chrono (
  input  [1:0] D1_D2,
  output [1:0] Run_Reset
);

  wire not_1_out;

  not not_1 (not_1_out, D1_D2[1]);
  and and_1 (Run_Reset[1], D1_D2[1], D1_D2[0]);
  and and_2 (Run_Reset[0], not_1_out, D1_D2[0]);
endmodule

module TranLogic2_Chrono (
  input  Q1,
  input  Q2,
  input  R,
  input  S,
  output D1,
  output D2
);

  wire and_1_out, and_2_out, and_3_out, and_4_out, and_5_out, and_6_out, and_7_out, not_1_out, not_2_out,
       not_3_out, not_4_out, not_5_out, not_6_out, not_7_out, not_8_out, not_9_out, not_10_out, not_11_out,
       not_12_out;

  not not_1 (not_1_out, S);
  not not_2 (not_2_out, Q2);
  not not_3 (not_3_out, S);
  not not_4 (not_4_out, Q1);
  not not_5 (not_5_out, S);
  and and_1 (and_1_out, not_5_out, Q2, not_6_out);
  not not_6 (not_6_out, Q1);
  and and_2 (and_2_out, not_1_out, R, not_2_out, Q1);
  and and_3 (and_3_out, R, Q2, not_7_out);
  not not_7 (not_7_out, Q1);
  not not_8 (not_8_out, R);
  not not_9 (not_9_out, Q2);
  and and_4 (and_4_out, not_8_out, not_9_out, Q1);
  and and_5 (and_5_out, not_3_out, R, Q2, not_4_out);
  not not_10 (not_10_out, R);
  and and_6 (and_6_out, S, not_10_out, not_11_out);
  not not_11 (not_11_out, Q1);
  and and_7 (and_7_out, S, not_12_out, Q1);
  not not_12 (not_12_out, Q2);
  or or_1 (D2, and_1_out, and_2_out, and_3_out);
  or or_2 (D1, and_4_out, and_5_out, and_6_out, and_7_out);
endmodule

module ZeroTo99 (
  input  CarryIn,
  input  Clk,
  input  Reset,
  output CarryOut,
  output [7:0] Count
);

  wire [6:0] counter_1_q;

  Counter #(.width(7), .max('h63)) counter_1 (
    .clr(Reset), .count(CarryIn), .clk(Clk), .carry(CarryOut), .Q(counter_1_q));  // open: load, up, D
  assign Count = {{1{1'b0}}, counter_1_q};  // Bit_Extender bit_extender_1
endmodule

module ZeroTo59 (
  input  CarryIn,
  input  Clk,
  input  Reset,
  output CarryOut,
  output [7:0] count
);

  wire [5:0] counter_1_q;

  Counter #(.width(6), .max('h3b)) counter_1 (
    .clr(Reset), .count(CarryIn), .clk(Clk), .carry(CarryOut), .Q(counter_1_q));  // open: load, up, D
  assign count = {{2{1'b0}}, counter_1_q};  // Bit_Extender bit_extender_1
endmodule

module ZeroToAll (
  input  Run,
  input  Reset,
  input  Clk,
  output [7:0] Centi,
  output [7:0] Sec,
  output [7:0] Min
);

  wire and_1_out, and_2_out, counter_1_carry, ZeroTo59_1_carryout, ZeroTo99_1_carryout;

  Counter #(.max('ha0)) counter_1 (
    .clr(Reset), .count(Run), .clk(Clk), .carry(counter_1_carry));  // open: load, up, D, Q
  and and_1 (and_1_out, ZeroTo99_1_carryout, counter_1_carry);
  and and_2 (and_2_out, ZeroTo59_1_carryout, and_1_out);
  ZeroTo99 ZeroTo99_1 (
    .CarryIn(counter_1_carry), .Clk(Clk), .Reset(Reset), .CarryOut(ZeroTo99_1_carryout), .Count(Centi));
  ZeroTo59 ZeroTo59_1 (.CarryIn(and_1_out), .Clk(Clk), .Reset(Reset), .CarryOut(ZeroTo59_1_carryout), .count(Sec));
  ZeroTo59 ZeroTo59_2 (.CarryIn(and_2_out), .Clk(Clk), .Reset(Reset), .count(Min));  // open: CarryOut
endmodule

module hourFSM (
  input  RESET,
  input  [1:0] B1_B0,
  input  ChM,
  input  CLK32K,
  input  CLK2k,
  input  CLK4,
  output [7:0] sevsegCode_5,
  output [7:0] sevsegCode_4,
  output [7:0] sevsegCode_3,
  output [7:0] sevsegCode_2,
  output [7:0] sevsegCode_1,
  output [7:0] sevsegCode_0
);

  wire changeHour_1_hloadtendi, changeHour_1_hloaduendi, changeHour_1_minloadtendi,
       changeHour_1_minloaduendi, changeHour_1_secloadtendi, changeHour_1_secloaduendi, HOUR_1_hloadt,
       HOUR_1_hloadu, HOUR_1_minloadt, HOUR_1_minloadu, HOUR_1_secloadt, HOUR_1_secloadu;
  wire [1:0] and_1_out;
  wire [3:0] changeHour_1_hloadt_4, changeHour_1_hloadu_4, changeHour_1_minloadt_4, changeHour_1_minloadu_4,
       changeHour_1_secloadt_4, changeHour_1_secloadu_4, HOUR_1_ht_4, HOUR_1_hu_4, HOUR_1_mint_4,
       HOUR_1_minu_4, HOUR_1_sect_4, HOUR_1_secu_4;

  and and_1 (and_1_out[0], B1_B0[0], ~ChM);  // AND_Gate
  and and_2 (and_1_out[1], B1_B0[1], ~ChM);  // AND_Gate
  changeHour changeHour_1 (
    .B1_B0(and_1_out), .ResetSelector(ChM), .clk(CLK32K), .HloadT_4(changeHour_1_hloadt_4),
    .HloadTEnDi(changeHour_1_hloadtendi), .HloadU_4(changeHour_1_hloadu_4),
    .HloadUEnDi(changeHour_1_hloaduendi), .MINloadT_4(changeHour_1_minloadt_4),
    .MINloadTEnDi(changeHour_1_minloadtendi), .MINloadU_4(changeHour_1_minloadu_4),
    .MINloadUEnDi(changeHour_1_minloaduendi), .SECloadT_4(changeHour_1_secloadt_4),
    .SECloadTEnDi(changeHour_1_secloadtendi), .SECloadU_4(changeHour_1_secloadu_4),
    .SECloadUEnDi(changeHour_1_secloaduendi));
  HOUR HOUR_1 (
    .RESET(RESET), .CLK2k(CLK2k), .HloadT_4(changeHour_1_hloadt_4), .HloadTEnDi(changeHour_1_hloadtendi),
    .HloadU_4(changeHour_1_hloadu_4), .HloadUEnDi(changeHour_1_hloaduendi),
    .MINloadT_4(changeHour_1_minloadt_4), .MINloadTEnDi(changeHour_1_minloadtendi),
    .MINloadU_4(changeHour_1_minloadu_4), .MINloadUEnDi(changeHour_1_minloaduendi),
    .SECloadT_4(changeHour_1_secloadt_4), .SECloadTEnDi(changeHour_1_secloadtendi),
    .SECloadU_4(changeHour_1_secloadu_4), .SECloadUEnDi(changeHour_1_secloaduendi), .HT_4(HOUR_1_ht_4),
    .HU_4(HOUR_1_hu_4), .MINT_4(HOUR_1_mint_4), .MINU_4(HOUR_1_minu_4), .SECT_4(HOUR_1_sect_4),
    .SECU_4(HOUR_1_secu_4), .HloadT(HOUR_1_hloadt), .HloadU(HOUR_1_hloadu), .MINloadT(HOUR_1_minloadt),
    .MINloadU(HOUR_1_minloadu), .SECloadT(HOUR_1_secloadt), .SECloadU(HOUR_1_secloadu));
  hourView_HMS hourView_HMS_1 (
    .HT_4(HOUR_1_ht_4), .HU_4(HOUR_1_hu_4), .MINT_4(HOUR_1_mint_4), .MINU_4(HOUR_1_minu_4),
    .SECT_4(HOUR_1_sect_4), .SECU_4(HOUR_1_secu_4), .HloadT(HOUR_1_hloadt), .HloadU(HOUR_1_hloadu),
    .MINloadT(HOUR_1_minloadt), .MINloadU(HOUR_1_minloadu), .SECloadT(HOUR_1_secloadt),
    .SECloadU(HOUR_1_secloadu), .RESET(RESET), .CLK4(CLK4), .sevsegCode_5(sevsegCode_5),
    .sevsegCode_4(sevsegCode_4), .sevsegCode_3(sevsegCode_3), .sevsegCode_2(sevsegCode_2),
    .sevsegCode_1(sevsegCode_1), .sevsegCode_0(sevsegCode_0));
endmodule

module zeroTwo (
  input  IN1,
  input  IN0,
  input  TickIN,
  output TickOUT,
  output OUT1,
  output OUT0
);

  wire and_2_out, and_3_out, and_4_out, and_5_out, not_1_out, not_2_out, not_3_out, not_4_out, not_5_out,
       not_6_out, not_7_out, not_8_out;

  not not_1 (not_1_out, IN0);
  not not_2 (not_2_out, IN1);
  not not_3 (not_3_out, IN0);
  not not_4 (not_4_out, TickIN);
  not not_5 (not_5_out, IN1);
  not not_6 (not_6_out, IN0);
  not not_7 (not_7_out, IN1);
  not not_8 (not_8_out, TickIN);
  and and_1 (TickOUT, IN1, not_1_out, TickIN);
  and and_2 (and_2_out, not_2_out, IN0, TickIN);
  and and_3 (and_3_out, IN1, not_3_out, not_4_out);
  and and_4 (and_4_out, not_5_out, not_6_out, TickIN);
  and and_5 (and_5_out, not_7_out, IN0, not_8_out);
  or or_1 (OUT1, and_2_out, and_3_out);
  or or_2 (OUT0, and_4_out, and_5_out);
endmodule

module zeroFive (
  input  IN2,
  input  IN1,
  input  IN0,
  input  TickIN,
  output TickOUT,
  output OUT2,
  output OUT1,
  output OUT0
);

  wire and_1_out, and_2_out, and_3_out, and_4_out, and_5_out, and_6_out, and_7_out, nand_1_out, nand_2_out,
       nand_3_out, nand_4_out, nand_5_out, nand_6_out, nand_7_out, nand_8_out, nand_9_out, nand_10_out,
       nand_11_out, nand_12_out, not_1_out, not_2_out, not_3_out, not_4_out, not_5_out, not_6_out, not_7_out,
       not_8_out, not_9_out, not_10_out, not_11_out, not_12_out, not_13_out, not_14_out;

  not not_1 (not_1_out, IN2);
  not not_2 (not_2_out, IN1);
  not not_3 (not_3_out, IN2);
  not not_4 (not_4_out, IN0);
  not not_5 (not_5_out, IN2);
  not not_6 (not_6_out, TickIN);
  not not_7 (not_7_out, IN2);
  not not_8 (not_8_out, IN0);
  not not_9 (not_9_out, IN1);
  not not_10 (not_10_out, IN0);
  not not_11 (not_11_out, IN2);
  not not_12 (not_12_out, TickIN);
  not not_13 (not_13_out, IN1);
  not not_14 (not_14_out, TickIN);
  nand nand_1 (nand_1_out, IN1, IN1);
  nand nand_2 (nand_2_out, IN1, IN1);
  nand nand_3 (nand_3_out, IN2, IN2);
  nand nand_4 (nand_4_out, IN1, IN1);
  nand nand_5 (nand_5_out, IN0, IN0);
  nand nand_6 (nand_6_out, IN1, IN1);
  nand nand_7 (nand_7_out, TickIN, TickIN);
  and and_1 (and_1_out, not_1_out, not_2_out, IN0, TickIN);
  and and_2 (and_2_out, not_3_out, IN1, not_4_out);
  and and_3 (and_3_out, not_5_out, IN1, not_6_out);
  and and_4 (and_4_out, not_7_out, not_8_out, TickIN);
  and and_5 (and_5_out, not_9_out, not_10_out, TickIN);
  and and_6 (and_6_out, not_11_out, IN0, not_12_out);
  and and_7 (and_7_out, not_13_out, IN0, not_14_out);
  nand nand_8 (nand_8_out, TickIN, IN2, nand_1_out, IN0);
  nand nand_9 (nand_9_out, TickIN, IN2, nand_2_out, IN0);
  nand nand_10 (nand_10_out, nand_3_out, IN1, IN0, TickIN);
  nand nand_11 (nand_11_out, IN2, nand_4_out, nand_5_out);
  nand nand_12 (nand_12_out, IN2, nand_6_out, nand_7_out);
  or or_1 (OUT1, and_1_out, and_2_out, and_3_out);
  or or_2 (OUT0, and_4_out, and_5_out, and_6_out, and_7_out);
  nand nand_13 (TickOUT, nand_8_out, nand_9_out);
  nand nand_14 (OUT2, nand_10_out, nand_11_out, nand_12_out);
endmodule

module zeroNine (
  input  IN3,
  input  IN2,
  input  IN1,
  input  IN0,
  input  TickIN,
  output TickOUT,
  output OUT3,
  output OUT2,
  output OUT1,
  output OUT0
);

  wire nand_1_out, nand_2_out, nand_3_out, nand_4_out, nand_5_out, nand_6_out, nand_7_out, nand_8_out,
       nand_9_out, nand_10_out, nand_11_out, nand_12_out, nand_13_out, nand_14_out, nand_15_out, nand_16_out,
       nand_17_out, nand_18_out, nand_19_out, nand_20_out, nand_21_out, nand_22_out, nand_23_out,
       nand_24_out, nand_25_out, nand_26_out, nand_27_out, nand_28_out, nand_29_out, nand_30_out,
       nand_31_out, nand_32_out, nand_33_out, nand_34_out, nand_35_out, nand_36_out, nand_37_out,
       nand_38_out, nand_39_out, nand_40_out, nand_41_out, nand_42_out, nand_43_out, nand_44_out,
       nand_45_out, nand_46_out, nand_47_out, nand_48_out, nand_49_out, nand_50_out, nand_51_out;

  nand nand_1 (nand_1_out, IN2, IN2);
  nand nand_2 (nand_2_out, IN1, IN1);
  nand nand_3 (nand_3_out, IN2, IN2);
  nand nand_4 (nand_4_out, IN1, IN1);
  nand nand_5 (nand_5_out, TickIN, TickIN);
  nand nand_6 (nand_6_out, IN2, IN2);
  nand nand_7 (nand_7_out, IN1, IN1);
  nand nand_8 (nand_8_out, IN2, IN2);
  nand nand_9 (nand_9_out, IN1, IN1);
  nand nand_10 (nand_10_out, IN0, IN0);
  nand nand_11 (nand_11_out, IN3, IN3);
  nand nand_12 (nand_12_out, IN3, IN3);
  nand nand_13 (nand_13_out, IN2, IN2);
  nand nand_14 (nand_14_out, IN3, IN3);
  nand nand_15 (nand_15_out, IN1, IN1);
  nand nand_16 (nand_16_out, IN3, IN3);
  nand nand_17 (nand_17_out, IN0, IN0);
  nand nand_18 (nand_18_out, IN3, IN3);
  nand nand_19 (nand_19_out, TickIN, TickIN);
  nand nand_20 (nand_20_out, IN3, IN3);
  nand nand_21 (nand_21_out, IN1, IN1);
  nand nand_22 (nand_22_out, IN3, IN3);
  nand nand_23 (nand_23_out, IN0, IN0);
  nand nand_24 (nand_24_out, IN3, IN3);
  nand nand_25 (nand_25_out, TickIN, TickIN);
  nand nand_26 (nand_26_out, IN3, IN3);
  nand nand_27 (nand_27_out, IN0, IN0);
  nand nand_28 (nand_28_out, IN2, IN2);
  nand nand_29 (nand_29_out, IN1, IN1);
  nand nand_30 (nand_30_out, IN0, IN0);
  nand nand_31 (nand_31_out, IN3, IN3);
  nand nand_32 (nand_32_out, TickIN, TickIN);
  nand nand_33 (nand_33_out, IN2, IN2);
  nand nand_34 (nand_34_out, IN1, IN1);
  nand nand_35 (nand_35_out, TickIN, TickIN);
  nand nand_36 (nand_36_out, IN3, nand_1_out, nand_2_out, IN0, TickIN);
  nand nand_37 (nand_37_out, IN3, nand_3_out, nand_4_out, IN0, TickIN);
  nand nand_38 (nand_38_out, nand_5_out, IN3, nand_6_out, nand_7_out);
  nand nand_39 (nand_39_out, IN3, nand_8_out, nand_9_out, nand_10_out);
  nand nand_40 (nand_40_out, TickIN, nand_11_out, IN2, IN1, IN0);
  nand nand_41 (nand_41_out, nand_12_out, nand_13_out, IN1, IN0, TickIN);
  nand nand_42 (nand_42_out, nand_14_out, IN2, nand_15_out);
  nand nand_43 (nand_43_out, nand_16_out, IN2, nand_17_out);
  nand nand_44 (nand_44_out, nand_18_out, IN2, nand_19_out);
  nand nand_45 (nand_45_out, nand_20_out, nand_21_out, IN0, TickIN);
  nand nand_46 (nand_46_out, nand_22_out, IN1, nand_23_out);
  nand nand_47 (nand_47_out, nand_24_out, IN1, nand_25_out);
  nand nand_48 (nand_48_out, nand_26_out, nand_27_out, TickIN);
  nand nand_49 (nand_49_out, nand_28_out, nand_29_out, nand_30_out, TickIN);
  nand nand_50 (nand_50_out, nand_31_out, IN0, nand_32_out);
  nand nand_51 (nand_51_out, nand_33_out, nand_34_out, IN0, nand_35_out);
  nand nand_52 (TickOUT, nand_36_out, nand_37_out);
  nand nand_53 (OUT3, nand_38_out, nand_39_out, nand_40_out);
  nand nand_54 (OUT2, nand_41_out, nand_42_out, nand_43_out, nand_44_out);
  nand nand_55 (OUT1, nand_45_out, nand_46_out, nand_47_out);
  nand nand_56 (OUT0, nand_48_out, nand_49_out, nand_50_out, nand_51_out);
endmodule

module zeroNineHour (
  input  H,
  input  IN3,
  input  IN2,
  input  IN1,
  input  IN0,
  input  TickIN,
  output TickOUT,
  output OUT3,
  output OUT2,
  output OUT1,
  output OUT0
);

  wire and_1_out, and_2_out, and_3_out, and_4_out, and_5_out, and_6_out, and_7_out, and_8_out, and_9_out,
       and_10_out, and_11_out, and_12_out, and_13_out, and_14_out, and_15_out, and_16_out, and_17_out,
       and_18_out, and_19_out, and_20_out, and_21_out, not_1_out, not_2_out, not_3_out, not_4_out, not_5_out,
       not_6_out, not_7_out, not_8_out, not_9_out, not_10_out, not_11_out, not_12_out, not_13_out,
       not_14_out, not_15_out, not_16_out, not_17_out, not_18_out, not_19_out, not_20_out, not_21_out,
       not_22_out, not_23_out, not_24_out, not_25_out, not_26_out, not_27_out, not_28_out, not_29_out,
       not_30_out, not_31_out, not_32_out, not_33_out, not_34_out, not_35_out, not_36_out, not_37_out,
       not_38_out, not_39_out, not_40_out, not_41_out, not_42_out, not_43_out, not_44_out;

  not not_1 (not_1_out, H);
  not not_2 (not_2_out, IN3);
  not not_3 (not_3_out, IN2);
  not not_4 (not_4_out, H);
  not not_5 (not_5_out, H);
  not not_6 (not_6_out, IN0);
  not not_7 (not_7_out, H);
  not not_8 (not_8_out, TickIN);
  not not_9 (not_9_out, H);
  not not_10 (not_10_out, IN2);
  not not_11 (not_11_out, H);
  not not_12 (not_12_out, IN1);
  not not_13 (not_13_out, H);
  not not_14 (not_14_out, IN0);
  not not_15 (not_15_out, H);
  not not_16 (not_16_out, TickIN);
  not not_17 (not_17_out, H);
  not not_18 (not_18_out, IN3);
  not not_19 (not_19_out, IN1);
  not not_20 (not_20_out, IN3);
  not not_21 (not_21_out, IN2);
  not not_22 (not_22_out, IN1);
  not not_23 (not_23_out, H);
  not not_24 (not_24_out, IN0);
  not not_25 (not_25_out, H);
  not not_26 (not_26_out, TickIN);
  not not_27 (not_27_out, IN3);
  not not_28 (not_28_out, IN2);
  not not_29 (not_29_out, IN0);
  not not_30 (not_30_out, IN3);
  not not_31 (not_31_out, IN2);
  not not_32 (not_32_out, TickIN);
  not not_33 (not_33_out, H);
  not not_34 (not_34_out, H);
  not not_35 (not_35_out, IN0);
  not not_36 (not_36_out, IN3);
  not not_37 (not_37_out, IN2);
  not not_38 (not_38_out, IN0);
  not not_39 (not_39_out, H);
  not not_40 (not_40_out, TickIN);
  not not_41 (not_41_out, IN3);
  not not_42 (not_42_out, IN2);
  not not_43 (not_43_out, TickIN);
  not not_44 (not_44_out, H);
  and and_1 (and_1_out, not_1_out, IN3, IN0, TickIN);
  and and_2 (and_2_out, H, not_2_out, not_3_out, IN1, IN0, TickIN);
  and and_3 (and_3_out, not_4_out, IN2, IN1, IN0, TickIN);
  and and_4 (and_4_out, not_5_out, IN3, not_6_out);
  and and_5 (and_5_out, not_7_out, IN3, not_8_out);
  and and_6 (and_6_out, not_9_out, not_10_out, IN1, IN0, TickIN);
  and and_7 (and_7_out, not_11_out, IN2, not_12_out);
  and and_8 (and_8_out, not_13_out, IN2, not_14_out);
  and and_9 (and_9_out, not_15_out, IN2, not_16_out);
  and and_10 (and_10_out, not_17_out, not_18_out, not_19_out, IN0, TickIN);
  and and_11 (and_11_out, not_20_out, not_21_out, not_22_out, IN0, TickIN);
  and and_12 (and_12_out, not_23_out, IN1, not_24_out);
  and and_13 (and_13_out, not_25_out, IN1, not_26_out);
  and and_14 (and_14_out, not_27_out, not_28_out, IN1, not_29_out);
  and and_15 (and_15_out, not_30_out, not_31_out, IN1, not_32_out);
  and and_16 (and_16_out, not_33_out, IN3, IN2);
  and and_17 (and_17_out, not_34_out, not_35_out, TickIN);
  and and_18 (and_18_out, not_36_out, not_37_out, not_38_out, TickIN);
  and and_19 (and_19_out, not_39_out, IN0, not_40_out);
  and and_20 (and_20_out, not_41_out, not_42_out, IN0, not_43_out);
  and and_21 (and_21_out, not_44_out, IN3, IN2);
  or or_1 (TickOUT, and_1_out, and_2_out);
  or or_2 (OUT3, and_3_out, and_4_out, and_5_out);
  or or_3 (OUT2, and_6_out, and_7_out, and_8_out, and_9_out);
  or or_4 (OUT1, and_10_out, and_11_out, and_12_out, and_13_out, and_14_out, and_15_out, and_16_out);
  or or_5 (OUT0, and_17_out, and_18_out, and_19_out, and_20_out, and_21_out);
endmodule

module zeroTwentythree (
  input  TickIN,
  input  [3:0] loadT_4,
  input  loadTEnDi,
  input  [3:0] loadU_4,
  input  loadUEnDi,
  input  CLK2k,
  input  RESET,
  output TickOUT,
  output [3:0] curT_4,
  output [3:0] curU_4
);

  wire and_1_out, and_2_out, and_3_out, and_4_out, and_5_out, and_6_out, and_7_out, load_2_1_out0,
       load_2_1_out1, load_4_1_out0, load_4_1_out1, load_4_1_out2, load_4_1_out3, zeroNineHour_1_out0,
       zeroNineHour_1_out1, zeroNineHour_1_out2, zeroNineHour_1_out3, zeroNineHour_1_tickout, zeroTwo_1_out0,
       zeroTwo_1_out1;
  wire [1:0] d_ff_2_q;

  and and_1 (and_1_out, d_ff_2_q[1], ~d_ff_2_q[0]);  // AND_Gate
  zeroTwo zeroTwo_1 (
    .IN1(d_ff_2_q[1]), .IN0(d_ff_2_q[0]), .TickIN(zeroNineHour_1_tickout), .TickOUT(TickOUT),
    .OUT1(zeroTwo_1_out1), .OUT0(zeroTwo_1_out0));
  zeroNineHour zeroNineHour_1 (
    .H(and_1_out), .IN3(curU_4[3]), .IN2(curU_4[2]), .IN1(curU_4[1]), .IN0(curU_4[0]), .TickIN(TickIN),
    .TickOUT(zeroNineHour_1_tickout), .OUT3(zeroNineHour_1_out3), .OUT2(zeroNineHour_1_out2),
    .OUT1(zeroNineHour_1_out1), .OUT0(zeroNineHour_1_out0));
  load_2 load_2_1 (
    .IN1(zeroTwo_1_out1), .IN0(zeroTwo_1_out0), .loadValue(loadT_4), .loadEnDi(loadTEnDi),
    .OUT1(load_2_1_out1), .OUT0(load_2_1_out0));
  load_4 load_4_1 (
    .IN3(zeroNineHour_1_out3), .IN2(zeroNineHour_1_out2), .IN1(zeroNineHour_1_out1),
    .IN0(zeroNineHour_1_out0), .loadValue(loadU_4), .loadEnDi(loadUEnDi), .OUT3(load_4_1_out3),
    .OUT2(load_4_1_out2), .OUT1(load_4_1_out1), .OUT0(load_4_1_out0));
  and and_2 (and_2_out, ~RESET, load_2_1_out1);  // AND_Gate
  and and_3 (and_3_out, ~RESET, load_2_1_out0);  // AND_Gate
  and and_4 (and_4_out, ~RESET, load_4_1_out3);  // AND_Gate
  and and_5 (and_5_out, ~RESET, load_4_1_out2);  // AND_Gate
  and and_6 (and_6_out, ~RESET, load_4_1_out1);  // AND_Gate
  and and_7 (and_7_out, ~RESET, load_4_1_out0);  // AND_Gate
  D_Flip_Flop d_ff_1 (.D(and_2_out), .clk(CLK2k), .Q(d_ff_2_q[1]), .reset(RESET));  // open: Qn, preset
  D_Flip_Flop d_ff_2 (.D(and_3_out), .clk(CLK2k), .Q(d_ff_2_q[0]), .reset(RESET));  // open: Qn, preset
  D_Flip_Flop d_ff_3 (.D(and_4_out), .clk(CLK2k), .Q(curU_4[3]), .reset(RESET));  // open: Qn, preset
  D_Flip_Flop d_ff_4 (.D(and_5_out), .clk(CLK2k), .Q(curU_4[2]), .reset(RESET));  // open: Qn, preset
  D_Flip_Flop d_ff_5 (.D(and_6_out), .clk(CLK2k), .Q(curU_4[1]), .reset(RESET));  // open: Qn, preset
  D_Flip_Flop d_ff_6 (.D(and_7_out), .clk(CLK2k), .Q(curU_4[0]), .reset(RESET));  // open: Qn, preset
  assign curT_4 = {{2{1'b0}}, d_ff_2_q};  // Bit_Extender bit_extender_1
endmodule

module zeroFiftynine (
  input  TickIN,
  input  [3:0] loadT_4,
  input  loadTEnDi,
  input  [3:0] loadU_4,
  input  loadUEnDi,
  input  CLK2k,
  input  RESET,
  output TickOUT,
  output [3:0] curT_4,
  output [3:0] curU_4
);

  wire and_1_out, and_2_out, and_3_out, and_4_out, and_5_out, and_6_out, and_7_out, load_3_1_out0,
       load_3_1_out1, load_3_1_out2, load_4_1_out0, load_4_1_out1, load_4_1_out2, load_4_1_out3,
       zeroFive_1_out0, zeroFive_1_out1, zeroFive_1_out2, zeroNine_1_out0, zeroNine_1_out1, zeroNine_1_out2,
       zeroNine_1_out3, zeroNine_1_tickout;
  wire [2:0] d_ff_3_q;

  zeroFive zeroFive_1 (
    .IN2(d_ff_3_q[2]), .IN1(d_ff_3_q[1]), .IN0(d_ff_3_q[0]), .TickIN(zeroNine_1_tickout), .TickOUT(TickOUT),
    .OUT2(zeroFive_1_out2), .OUT1(zeroFive_1_out1), .OUT0(zeroFive_1_out0));
  zeroNine zeroNine_1 (
    .IN3(curU_4[3]), .IN2(curU_4[2]), .IN1(curU_4[1]), .IN0(curU_4[0]), .TickIN(TickIN),
    .TickOUT(zeroNine_1_tickout), .OUT3(zeroNine_1_out3), .OUT2(zeroNine_1_out2), .OUT1(zeroNine_1_out1),
    .OUT0(zeroNine_1_out0));
  load_3 load_3_1 (
    .IN2(zeroFive_1_out2), .IN1(zeroFive_1_out1), .IN0(zeroFive_1_out0), .loadValue(loadT_4),
    .loadEnDi(loadTEnDi), .OUT2(load_3_1_out2), .OUT1(load_3_1_out1), .OUT0(load_3_1_out0));
  load_4 load_4_1 (
    .IN3(zeroNine_1_out3), .IN2(zeroNine_1_out2), .IN1(zeroNine_1_out1), .IN0(zeroNine_1_out0),
    .loadValue(loadU_4), .loadEnDi(loadUEnDi), .OUT3(load_4_1_out3), .OUT2(load_4_1_out2),
    .OUT1(load_4_1_out1), .OUT0(load_4_1_out0));
  and and_1 (and_1_out, ~RESET, load_3_1_out2);  // AND_Gate
  and and_2 (and_2_out, ~RESET, load_3_1_out1);  // AND_Gate
  and and_3 (and_3_out, ~RESET, load_3_1_out0);  // AND_Gate
  and and_4 (and_4_out, ~RESET, load_4_1_out3);  // AND_Gate
  and and_5 (and_5_out, ~RESET, load_4_1_out2);  // AND_Gate
  and and_6 (and_6_out, ~RESET, load_4_1_out1);  // AND_Gate
  and and_7 (and_7_out, ~RESET, load_4_1_out0);  // AND_Gate
  D_Flip_Flop d_ff_1 (.D(and_1_out), .clk(CLK2k), .Q(d_ff_3_q[2]), .reset(RESET));  // open: Qn, preset
  D_Flip_Flop d_ff_2 (.D(and_2_out), .clk(CLK2k), .Q(d_ff_3_q[1]), .reset(RESET));  // open: Qn, preset
  D_Flip_Flop d_ff_3 (.D(and_3_out), .clk(CLK2k), .Q(d_ff_3_q[0]), .reset(RESET));  // open: Qn, preset
  D_Flip_Flop d_ff_4 (.D(and_4_out), .clk(CLK2k), .Q(curU_4[3]), .reset(RESET));  // open: Qn, preset
  D_Flip_Flop d_ff_5 (.D(and_5_out), .clk(CLK2k), .Q(curU_4[2]), .reset(RESET));  // open: Qn, preset
  D_Flip_Flop d_ff_6 (.D(and_6_out), .clk(CLK2k), .Q(curU_4[1]), .reset(RESET));  // open: Qn, preset
  D_Flip_Flop d_ff_7 (.D(and_7_out), .clk(CLK2k), .Q(curU_4[0]), .reset(RESET));  // open: Qn, preset
  assign curT_4 = {{1{1'b0}}, d_ff_3_q};  // Bit_Extender bit_extender_1
endmodule

module clk2k_to_ticksec (
  input  RESET,
  input  CLK2k,
  output TickSEC
);

  Counter #(.width(10), .max('h3e9)) counter_1 (
    .clr(RESET), .clk(CLK2k), .carry(TickSEC));  // open: load, up, count, D, Q
endmodule

module HOUR (
  input  RESET,
  input  CLK2k,
  input  [3:0] HloadT_4,
  input  HloadTEnDi,
  input  [3:0] HloadU_4,
  input  HloadUEnDi,
  input  [3:0] MINloadT_4,
  input  MINloadTEnDi,
  input  [3:0] MINloadU_4,
  input  MINloadUEnDi,
  input  [3:0] SECloadT_4,
  input  SECloadTEnDi,
  input  [3:0] SECloadU_4,
  input  SECloadUEnDi,
  output [3:0] HT_4,
  output [3:0] HU_4,
  output [3:0] MINT_4,
  output [3:0] MINU_4,
  output [3:0] SECT_4,
  output [3:0] SECU_4,
  output HloadT,
  output HloadU,
  output MINloadT,
  output MINloadU,
  output SECloadT,
  output SECloadU
);

  wire clk2k_to_ticksec_1_ticksec, min_tickout, sec_tickout;

  clk2k_to_ticksec clk2k_to_ticksec_1 (.RESET(RESET), .CLK2k(CLK2k), .TickSEC(clk2k_to_ticksec_1_ticksec));
  zeroTwentythree hour_1 (
    .TickIN(min_tickout), .loadT_4(HloadT_4), .loadTEnDi(HloadTEnDi), .loadU_4(HloadU_4),
    .loadUEnDi(HloadUEnDi), .CLK2k(CLK2k), .RESET(RESET), .curT_4(HT_4), .curU_4(HU_4));  // open: TickOUT
  zeroFiftynine min (
    .TickIN(sec_tickout), .loadT_4(MINloadT_4), .loadTEnDi(MINloadTEnDi), .loadU_4(MINloadU_4),
    .loadUEnDi(MINloadUEnDi), .CLK2k(CLK2k), .RESET(RESET), .TickOUT(min_tickout), .curT_4(MINT_4),
    .curU_4(MINU_4));
  zeroFiftynine sec (
    .TickIN(clk2k_to_ticksec_1_ticksec), .loadT_4(SECloadT_4), .loadTEnDi(SECloadTEnDi),
    .loadU_4(SECloadU_4), .loadUEnDi(SECloadUEnDi), .CLK2k(CLK2k), .RESET(RESET), .TickOUT(sec_tickout),
    .curT_4(SECT_4), .curU_4(SECU_4));

  assign HloadT = HloadTEnDi;
  assign HloadU = HloadUEnDi;
  assign MINloadT = MINloadTEnDi;
  assign MINloadU = MINloadUEnDi;
  assign SECloadT = SECloadTEnDi;
  assign SECloadU = SECloadUEnDi;
endmodule

module hourView_HMS (
  input  [3:0] HT_4,
  input  [3:0] HU_4,
  input  [3:0] MINT_4,
  input  [3:0] MINU_4,
  input  [3:0] SECT_4,
  input  [3:0] SECU_4,
  input  HloadT,
  input  HloadU,
  input  MINloadT,
  input  MINloadU,
  input  SECloadT,
  input  SECloadU,
  input  RESET,
  input  CLK4,
  output [7:0] sevsegCode_5,
  output [7:0] sevsegCode_4,
  output [7:0] sevsegCode_3,
  output [7:0] sevsegCode_2,
  output [7:0] sevsegCode_1,
  output [7:0] sevsegCode_0
);

  wire and_1_out, and_2_out, and_3_out, and_4_out, and_5_out, and_6_out, or_1_out, t_ff_1_q;
  wire [6:0] bit_extender_2_out, bit_extender_4_out, multiplexer_2_out, multiplexer_4_out;
  wire [7:0] bit_extender_1_out, bit_extender_3_out, bit_extender_5_out, bit_extender_6_out;

  assign bit_extender_1_out = {{4{1'b0}}, HT_4};  // Bit_Extender bit_extender_1
  assign bit_extender_2_out = {{3{1'b0}}, HU_4};  // Bit_Extender bit_extender_2
  assign bit_extender_3_out = {{4{1'b0}}, MINT_4};  // Bit_Extender bit_extender_3
  assign bit_extender_4_out = {{3{1'b0}}, MINU_4};  // Bit_Extender bit_extender_4
  assign bit_extender_5_out = {{4{1'b0}}, SECT_4};  // Bit_Extender bit_extender_5
  assign bit_extender_6_out = {{4{1'b0}}, SECU_4};  // Bit_Extender bit_extender_6
  T_Flip_Flop t_ff_1 (.T(or_1_out), .clk(CLK4), .Q(t_ff_1_q), .reset(RESET));  // open: Qn, preset
  or or_1 (or_1_out, HloadT, HloadU, MINloadT, MINloadU, SECloadT, SECloadU);
  Multiplexer #(.width(8), .enable("false")) multiplexer_1 (
    .in0(bit_extender_1_out), .in1(8'h7f), .out(sevsegCode_5), .sel(and_1_out));
  and and_1 (and_1_out, HloadT, t_ff_1_q);
  and and_2 (and_2_out, HloadU, t_ff_1_q);
  Multiplexer #(.width(7), .enable("false")) multiplexer_2 (
    .in0(bit_extender_2_out), .in1({7{1'b1}}), .out(multiplexer_2_out), .sel(and_2_out));
  Multiplexer #(.width(8), .enable("false")) multiplexer_3 (
    .in0(bit_extender_3_out), .in1(8'h7f), .out(sevsegCode_3), .sel(and_3_out));
  and and_3 (and_3_out, MINloadT, t_ff_1_q);
  Multiplexer #(.width(7), .enable("false")) multiplexer_4 (
    .in0(bit_extender_4_out), .in1({7{1'b1}}), .out(multiplexer_4_out), .sel(and_4_out));
  and and_4 (and_4_out, MINloadU, t_ff_1_q);
  assign sevsegCode_4 = {{1{1'b1}}, multiplexer_2_out};  // Bit_Extender bit_extender_7
  assign sevsegCode_2 = {{1{1'b1}}, multiplexer_4_out};  // Bit_Extender bit_extender_8
  Multiplexer #(.width(8), .enable("false")) multiplexer_5 (
    .in0(bit_extender_5_out), .in1(8'h7f), .out(sevsegCode_1), .sel(and_5_out));
  and and_5 (and_5_out, SECloadT, t_ff_1_q);
  Multiplexer #(.width(8), .enable("false")) multiplexer_6 (
    .in0(bit_extender_6_out), .in1(8'h7f), .out(sevsegCode_0), .sel(and_6_out));
  and and_6 (and_6_out, SECloadU, t_ff_1_q);
endmodule

module hourView_HM_reverse (
  input  [7:0] sevsegCode_5,
  input  [7:0] sevsegCode_4,
  input  [7:0] sevsegCode_3,
  input  [7:0] sevsegCode_2,
  output [3:0] HT_4,
  output [3:0] HU_4,
  output [3:0] MINT_4,
  output [3:0] MINU_4
);

  Bit_Extender #(.out_width(4)) bit_extender_1 (.in(sevsegCode_5), .out(HT_4));
  Bit_Extender #(.out_width(4)) bit_extender_2 (.in(sevsegCode_4), .out(HU_4));
  Bit_Extender #(.out_width(4)) bit_extender_3 (.in(sevsegCode_3), .out(MINT_4));
  Bit_Extender #(.out_width(4)) bit_extender_4 (.in(sevsegCode_2), .out(MINU_4));
endmodule

module hourView_HMS_reverse (
  input  [7:0] sevsegCode_5,
  input  [7:0] sevsegCode_4,
  input  [7:0] sevsegCode_3,
  input  [7:0] sevsegCode_2,
  input  [7:0] sevsegCode_1,
  input  [7:0] sevsegCode_0,
  output [3:0] HT_4,
  output [3:0] HU_4,
  output [3:0] MINT_4,
  output [3:0] MINU_4,
  output [3:0] SECT_4,
  output [3:0] SECU_4
);

  Bit_Extender #(.out_width(4)) bit_extender_1 (.in(sevsegCode_5), .out(HT_4));
  Bit_Extender #(.out_width(4)) bit_extender_2 (.in(sevsegCode_4), .out(HU_4));
  Bit_Extender #(.out_width(4)) bit_extender_3 (.in(sevsegCode_3), .out(MINT_4));
  Bit_Extender #(.out_width(4)) bit_extender_4 (.in(sevsegCode_2), .out(MINU_4));
  Bit_Extender #(.out_width(4)) bit_extender_5 (.in(sevsegCode_1), .out(SECT_4));
  Bit_Extender #(.out_width(4)) bit_extender_6 (.in(sevsegCode_0), .out(SECU_4));
endmodule

module hourView_HMS_Ltime (
  input  [3:0] HT_4,
  input  [3:0] HU_4,
  input  [3:0] MINT_4,
  input  [3:0] MINU_4,
  input  [3:0] SECT_4,
  input  [3:0] SECU_4,
  output [7:0] sevsegCode_5,
  output [7:0] sevsegCode_4,
  output [7:0] sevsegCode_3,
  output [7:0] sevsegCode_2,
  output [7:0] sevsegCode_1,
  output [7:0] sevsegCode_0
);

  wire [6:0] bit_extender_2_out, bit_extender_4_out;

  assign sevsegCode_5 = {{4{1'b0}}, HT_4};  // Bit_Extender bit_extender_1
  assign bit_extender_2_out = {{3{1'b0}}, HU_4};  // Bit_Extender bit_extender_2
  assign sevsegCode_3 = {{4{1'b0}}, MINT_4};  // Bit_Extender bit_extender_3
  assign bit_extender_4_out = {{3{1'b0}}, MINU_4};  // Bit_Extender bit_extender_4
  assign sevsegCode_1 = {{4{1'b0}}, SECT_4};  // Bit_Extender bit_extender_5
  assign sevsegCode_0 = {{4{1'b0}}, SECU_4};  // Bit_Extender bit_extender_6
  assign sevsegCode_4 = {{1{1'b1}}, bit_extender_2_out};  // Bit_Extender bit_extender_7
  assign sevsegCode_2 = {{1{1'b1}}, bit_extender_4_out};  // Bit_Extender bit_extender_8
endmodule

module load_2 (
  input  IN1,
  input  IN0,
  input  [3:0] loadValue,
  input  loadEnDi,
  output OUT1,
  output OUT0
);

  wire [1:0] bit_extender_1_out;

  Bit_Extender #(.in_width(4), .out_width(2), .\type ("zero")) bit_extender_1 (
    .in(loadValue), .out(bit_extender_1_out));
  Multiplexer #(.enable("false")) multiplexer_1 (.in0(IN1), .in1(bit_extender_1_out[1]), .out(OUT1), .sel(loadEnDi));
  Multiplexer #(.enable("false")) multiplexer_2 (.in0(IN0), .in1(bit_extender_1_out[0]), .out(OUT0), .sel(loadEnDi));
endmodule

module load_3 (
  input  IN2,
  input  IN1,
  input  IN0,
  input  [3:0] loadValue,
  input  loadEnDi,
  output OUT2,
  output OUT1,
  output OUT0
);

  wire [2:0] bit_extender_1_out;

  Bit_Extender #(.in_width(4), .out_width(3), .\type ("zero")) bit_extender_1 (
    .in(loadValue), .out(bit_extender_1_out));
  Multiplexer #(.enable("false")) multiplexer_1 (.in0(IN2), .in1(bit_extender_1_out[2]), .out(OUT2), .sel(loadEnDi));
  Multiplexer #(.enable("false")) multiplexer_2 (.in0(IN1), .in1(bit_extender_1_out[1]), .out(OUT1), .sel(loadEnDi));
  Multiplexer #(.enable("false")) multiplexer_3 (.in0(IN0), .in1(bit_extender_1_out[0]), .out(OUT0), .sel(loadEnDi));
endmodule

module load_4 (
  input  IN3,
  input  IN2,
  input  IN1,
  input  IN0,
  input  [3:0] loadValue,
  input  loadEnDi,
  output OUT3,
  output OUT2,
  output OUT1,
  output OUT0
);

  Multiplexer #(.enable("false")) multiplexer_1 (.in0(IN3), .in1(loadValue[3]), .out(OUT3), .sel(loadEnDi));
  Multiplexer #(.enable("false")) multiplexer_2 (.in0(IN2), .in1(loadValue[2]), .out(OUT2), .sel(loadEnDi));
  Multiplexer #(.enable("false")) multiplexer_3 (.in0(IN1), .in1(loadValue[1]), .out(OUT1), .sel(loadEnDi));
  Multiplexer #(.enable("false")) multiplexer_4 (.in0(IN0), .in1(loadValue[0]), .out(OUT0), .sel(loadEnDi));
endmodule

module changeHour (
  input  [1:0] B1_B0,
  input  ResetSelector,
  input  clk,
  output [3:0] HloadT_4,
  output HloadTEnDi,
  output [3:0] HloadU_4,
  output HloadUEnDi,
  output [3:0] MINloadT_4,
  output MINloadTEnDi,
  output [3:0] MINloadU_4,
  output MINloadUEnDi,
  output [3:0] SECloadT_4,
  output SECloadTEnDi,
  output [3:0] SECloadU_4,
  output SECloadUEnDi
);

  wire demultiplexer_1_out1, demultiplexer_1_out2, demultiplexer_1_out3, demultiplexer_1_out4,
       demultiplexer_1_out5, demultiplexer_1_out6, demultiplexer_2_out0, or_1_out;
  wire [1:0] counter_2_q, counter_3_q;
  wire [2:0] counter_1_q, counter_5_q, counter_7_q;
  wire [3:0] bit_extender_2_out, counter_4_q;

  Counter #(.width(3), .max('h6)) counter_1 (
    .clr(ResetSelector), .count(B1_B0[0]), .clk(clk), .Q(counter_1_q));  // open: load, up, D, carry
  Demultiplexer #(.select(3), .enable("false")) demultiplexer_1 (
    .out1(demultiplexer_1_out1), .out2(demultiplexer_1_out2), .out3(demultiplexer_1_out3),
    .out4(demultiplexer_1_out4), .out5(demultiplexer_1_out5), .out6(demultiplexer_1_out6), .in(B1_B0[1]),
    .sel(counter_1_q));  // open: out0, out7
  Demultiplexer #(.select(3), .enable("false")) demultiplexer_2 (
    .out0(demultiplexer_2_out0), .out1(HloadTEnDi), .out2(HloadUEnDi), .out3(MINloadTEnDi),
    .out4(MINloadUEnDi), .out5(SECloadTEnDi), .out6(SECloadUEnDi), .in(1'b1), .sel(counter_1_q));  // open: out7
  or or_1 (or_1_out, demultiplexer_2_out0, ResetSelector);
  Counter #(.width(2), .max('h2)) counter_2 (
    .clr(or_1_out), .count(demultiplexer_1_out1), .clk(clk), .Q(counter_2_q));  // open: load, up, D, carry
  assign HloadT_4 = {{2{1'b0}}, counter_2_q};  // Bit_Extender bit_extender_1
  Counter #(.width(2), .max('h3)) counter_3 (
    .clr(or_1_out), .count(demultiplexer_1_out2), .clk(clk), .Q(counter_3_q));  // open: load, up, D, carry
  Counter #(.width(4), .max('h9)) counter_4 (
    .clr(or_1_out), .count(demultiplexer_1_out2), .clk(clk), .Q(counter_4_q));  // open: load, up, D, carry
  Counter #(.width(3), .max('h5)) counter_5 (
    .clr(or_1_out), .count(demultiplexer_1_out3), .clk(clk), .Q(counter_5_q));  // open: load, up, D, carry
  Counter #(.width(4), .max('h9)) counter_6 (
    .clr(or_1_out), .count(demultiplexer_1_out4), .clk(clk), .Q(MINloadU_4));  // open: load, up, D, carry
  Counter #(.width(3), .max('h5)) counter_7 (
    .clr(or_1_out), .count(demultiplexer_1_out5), .clk(clk), .Q(counter_7_q));  // open: load, up, D, carry
  Counter #(.width(4), .max('h9)) counter_8 (
    .clr(or_1_out), .count(demultiplexer_1_out6), .clk(clk), .Q(SECloadU_4));  // open: load, up, D, carry
  assign bit_extender_2_out = {{2{1'b0}}, counter_3_q};  // Bit_Extender bit_extender_2
  assign MINloadT_4 = {{1{1'b0}}, counter_5_q};  // Bit_Extender bit_extender_3
  assign SECloadT_4 = {{1{1'b0}}, counter_7_q};  // Bit_Extender bit_extender_4
  Multiplexer #(.width(4), .enable("false")) multiplexer_1 (
    .in0(counter_4_q), .in1(bit_extender_2_out), .out(HloadU_4), .sel(counter_2_q[1]));
endmodule

module alarm (
  input  RESET,
  input  [1:0] B1_B0,
  input  [7:0] SSDCode_5,
  input  [7:0] SSDCode_4,
  input  [7:0] SSDCode_3,
  input  [7:0] SSDCode_2,
  input  ChM,
  input  CLK32K,
  input  CLK2k,
  input  CLK4,
  output [7:0] sevsegCode_5,
  output [7:0] sevsegCode_4,
  output [7:0] sevsegCode_3,
  output [7:0] sevsegCode_2,
  output [7:0] sevsegCode_1,
  output [7:0] sevsegCode_0,
  output BUZZER
);

  wire alarmHM_1_curonoff, alarmHM_1_hloadt, alarmHM_1_hloadu, alarmHM_1_minloadt, alarmHM_1_minloadu,
       alarmHM_1_onoffl, changeAlarm_1_hloadtendi, changeAlarm_1_hloaduendi, changeAlarm_1_minloadtendi,
       changeAlarm_1_minloaduendi, changeAlarm_1_onoffload, changeAlarm_1_onoffloadendi, compare_1_equal;
  wire [1:0] and_1_out;
  wire [3:0] alarmHM_1_curht_4, alarmHM_1_curhu_4, alarmHM_1_curmint_4, alarmHM_1_curminu_4,
       changeAlarm_1_hloadt_4, changeAlarm_1_hloadu_4, changeAlarm_1_minloadt_4, changeAlarm_1_minloadu_4,
       hourView_HM_reverse_1_ht_4, hourView_HM_reverse_1_hu_4, hourView_HM_reverse_1_mint_4,
       hourView_HM_reverse_1_minu_4;

  and and_1 (and_1_out[0], B1_B0[0], ~ChM);  // AND_Gate
  and and_2 (and_1_out[1], B1_B0[1], ~ChM);  // AND_Gate
  hourView_HM_reverse hourView_HM_reverse_1 (
    .sevsegCode_5(SSDCode_5), .sevsegCode_4(SSDCode_4), .sevsegCode_3(SSDCode_3), .sevsegCode_2(SSDCode_2),
    .HT_4(hourView_HM_reverse_1_ht_4), .HU_4(hourView_HM_reverse_1_hu_4),
    .MINT_4(hourView_HM_reverse_1_mint_4), .MINU_4(hourView_HM_reverse_1_minu_4));
  changeAlarm changeAlarm_1 (
    .B1_B0(and_1_out), .ResetSelector(ChM), .CLK32K(CLK32K), .HloadT_4(changeAlarm_1_hloadt_4),
    .HloadTEnDi(changeAlarm_1_hloadtendi), .HloadU_4(changeAlarm_1_hloadu_4),
    .HloadUEnDi(changeAlarm_1_hloaduendi), .MINloadT_4(changeAlarm_1_minloadt_4),
    .MINloadTEnDi(changeAlarm_1_minloadtendi), .MINloadU_4(changeAlarm_1_minloadu_4),
    .MINloadUEnDi(changeAlarm_1_minloaduendi), .ONOFFload(changeAlarm_1_onoffload),
    .ONOFFloadEnDi(changeAlarm_1_onoffloadendi));
  alarmHM alarmHM_1 (
    .RESET(RESET), .CLK2k(CLK2k), .HloadT_4(changeAlarm_1_hloadt_4), .HloadTEnDi(changeAlarm_1_hloadtendi),
    .HloadU_4(changeAlarm_1_hloadu_4), .HloadUEnDi(changeAlarm_1_hloaduendi),
    .MINloadT_4(changeAlarm_1_minloadt_4), .MINloadTEnDi(changeAlarm_1_minloadtendi),
    .MINloadU_4(changeAlarm_1_minloadu_4), .MINloadUEnDi(changeAlarm_1_minloaduendi),
    .ONOFFload(changeAlarm_1_onoffload), .ONOFFloadEnDi(changeAlarm_1_onoffloadendi),
    .curHT_4(alarmHM_1_curht_4), .curHU_4(alarmHM_1_curhu_4), .curMINT_4(alarmHM_1_curmint_4),
    .curMINU_4(alarmHM_1_curminu_4), .curONOFF(alarmHM_1_curonoff), .HloadT(alarmHM_1_hloadt),
    .HloadU(alarmHM_1_hloadu), .MINloadT(alarmHM_1_minloadt), .MINloadU(alarmHM_1_minloadu),
    .ONOFFL(alarmHM_1_onoffl));
  compare compare_1 (
    .A3_4(alarmHM_1_curht_4), .A2_4(alarmHM_1_curhu_4), .A1_4(alarmHM_1_curmint_4),
    .A0_4(alarmHM_1_curminu_4), .B3_4(hourView_HM_reverse_1_ht_4), .B2_4(hourView_HM_reverse_1_hu_4),
    .B1_4(hourView_HM_reverse_1_mint_4), .B0_4(hourView_HM_reverse_1_minu_4), .EQUAL(compare_1_equal));
  alarmView_HM alarmView_HM_1 (
    .HT_4(alarmHM_1_curht_4), .HU_4(alarmHM_1_curhu_4), .MINT_4(alarmHM_1_curmint_4),
    .MINU_4(alarmHM_1_curminu_4), .curONOFF(alarmHM_1_curonoff), .HloadT(alarmHM_1_hloadt),
    .HloadU(alarmHM_1_hloadu), .MINloadT(alarmHM_1_minloadt), .MINloadU(alarmHM_1_minloadu),
    .ONOFFload(alarmHM_1_onoffl), .EQUAL(compare_1_equal), .RESET(RESET), .CLK4(CLK4),
    .sevsegCode_5(sevsegCode_5), .sevsegCode_4(sevsegCode_4), .sevsegCode_3(sevsegCode_3),
    .sevsegCode_2(sevsegCode_2), .sevsegCode_1(sevsegCode_1), .sevsegCode_0(sevsegCode_0), .BUZZER(BUZZER));
endmodule

module changeAlarm (
  input  [1:0] B1_B0,
  input  ResetSelector,
  input  CLK32K,
  output [3:0] HloadT_4,
  output HloadTEnDi,
  output [3:0] HloadU_4,
  output HloadUEnDi,
  output [3:0] MINloadT_4,
  output MINloadTEnDi,
  output [3:0] MINloadU_4,
  output MINloadUEnDi,
  output ONOFFload,
  output ONOFFloadEnDi
);

  wire demultiplexer_1_out1, demultiplexer_1_out2, demultiplexer_1_out3, demultiplexer_1_out4,
       demultiplexer_1_out5, demultiplexer_2_out0, or_1_out;
  wire [1:0] counter_2_q, counter_3_q;
  wire [2:0] counter_1_q, counter_5_q;
  wire [3:0] bit_extender_2_out, counter_4_q;

  Counter #(.width(3), .max('h5)) counter_1 (
    .clr(ResetSelector), .count(B1_B0[0]), .clk(CLK32K), .Q(counter_1_q));  // open: load, up, D, carry
  Demultiplexer #(.select(3), .enable("false")) demultiplexer_1 (
    .out1(demultiplexer_1_out1), .out2(demultiplexer_1_out2), .out3(demultiplexer_1_out3),
    .out4(demultiplexer_1_out4), .out5(demultiplexer_1_out5), .in(B1_B0[1]), .sel(counter_1_q));  // open: out0, out6, out7
  Demultiplexer #(.select(3), .enable("false")) demultiplexer_2 (
    .out0(demultiplexer_2_out0), .out1(HloadTEnDi), .out2(HloadUEnDi), .out3(MINloadTEnDi),
    .out4(MINloadUEnDi), .out5(ONOFFloadEnDi), .in(1'b1), .sel(counter_1_q));  // open: out6, out7
  or or_1 (or_1_out, demultiplexer_2_out0, ResetSelector);
  Counter #(.width(2), .max('h2)) counter_2 (
    .clr(or_1_out), .count(demultiplexer_1_out1), .clk(CLK32K), .Q(counter_2_q));  // open: load, up, D, carry
  Counter #(.width(2), .max('h3)) counter_3 (
    .clr(or_1_out), .count(demultiplexer_1_out2), .clk(CLK32K), .Q(counter_3_q));  // open: load, up, D, carry
  Counter #(.width(4), .max('h9)) counter_4 (
    .clr(or_1_out), .count(demultiplexer_1_out2), .clk(CLK32K), .Q(counter_4_q));  // open: load, up, D, carry
  Counter #(.width(3), .max('h5)) counter_5 (
    .clr(or_1_out), .count(demultiplexer_1_out3), .clk(CLK32K), .Q(counter_5_q));  // open: load, up, D, carry
  Counter #(.width(4), .max('h9)) counter_6 (
    .clr(or_1_out), .count(demultiplexer_1_out4), .clk(CLK32K), .Q(MINloadU_4));  // open: load, up, D, carry
  Counter #(.width(1), .max('h1)) counter_7 (
    .clr(or_1_out), .count(demultiplexer_1_out5), .clk(CLK32K), .Q(ONOFFload));  // open: load, up, D, carry
  assign HloadT_4 = {{2{1'b0}}, counter_2_q};  // Bit_Extender bit_extender_1
  assign bit_extender_2_out = {{2{1'b0}}, counter_3_q};  // Bit_Extender bit_extender_2
  assign MINloadT_4 = {{1{1'b0}}, counter_5_q};  // Bit_Extender bit_extender_3
  Multiplexer #(.width(4), .enable("false")) multiplexer_1 (
    .in0(counter_4_q), .in1(bit_extender_2_out), .out(HloadU_4), .sel(counter_2_q[1]));

  // Other names for the same wires on the sheet: clk = CLK32K
endmodule
module alarmView_HM (
  input  [3:0] HT_4,
  input  [3:0] HU_4,
  input  [3:0] MINT_4,
  input  [3:0] MINU_4,
  input  curONOFF,
  input  HloadT,
  input  HloadU,
  input  MINloadT,
  input  MINloadU,
  input  ONOFFload,
  input  EQUAL,
  input  RESET,
  input  CLK4,
  output [7:0] sevsegCode_5,
  output [7:0] sevsegCode_4,
  output [7:0] sevsegCode_3,
  output [7:0] sevsegCode_2,
  output [7:0] sevsegCode_1,
  output [7:0] sevsegCode_0,
  output BUZZER
);

  wire and_1_out, and_2_out, and_3_out, and_4_out, and_5_out, and_6_out, or_1_out, t_ff_1_q;
  wire [6:0] bit_extender_2_out, bit_extender_4_out, multiplexer_3_out, multiplexer_5_out;
  wire [7:0] bit_extender_1_out, bit_extender_3_out, multiplexer_1_out;

  assign bit_extender_1_out = {{4{1'b0}}, HT_4};  // Bit_Extender bit_extender_1
  assign bit_extender_2_out = {{3{1'b0}}, HU_4};  // Bit_Extender bit_extender_2
  assign bit_extender_3_out = {{4{1'b0}}, MINT_4};  // Bit_Extender bit_extender_3
  assign bit_extender_4_out = {{3{1'b0}}, MINU_4};  // Bit_Extender bit_extender_4
  Multiplexer #(.width(8), .enable("false")) multiplexer_1 (
    .in0(8'hf), .in1(8'h16), .out(multiplexer_1_out), .sel(curONOFF));
  or or_1 (or_1_out, HloadT, HloadU, MINloadT, MINloadU, ONOFFload);
  Multiplexer #(.width(8), .enable("false")) multiplexer_2 (
    .in0(bit_extender_1_out), .in1(8'h7f), .out(sevsegCode_5), .sel(and_1_out));
  and and_1 (and_1_out, HloadT, t_ff_1_q);
  T_Flip_Flop t_ff_1 (.T(or_1_out), .clk(CLK4), .Q(t_ff_1_q), .reset(RESET));  // open: Qn, preset
  Multiplexer #(.width(7), .enable("false")) multiplexer_3 (
    .in0(bit_extender_2_out), .in1({7{1'b1}}), .out(multiplexer_3_out), .sel(and_2_out));
  and and_2 (and_2_out, HloadU, t_ff_1_q);
  Multiplexer #(.width(8), .enable("false")) multiplexer_4 (
    .in0(bit_extender_3_out), .in1(8'h7f), .out(sevsegCode_3), .sel(and_3_out));
  and and_3 (and_3_out, MINloadT, t_ff_1_q);
  and and_4 (and_4_out, MINloadU, t_ff_1_q);
  assign sevsegCode_4 = {{1{1'b1}}, multiplexer_3_out};  // Bit_Extender bit_extender_5
  Multiplexer #(.width(7), .enable("false")) multiplexer_5 (
    .in0(bit_extender_4_out), .in1({7{1'b1}}), .out(multiplexer_5_out), .sel(and_4_out));
  assign sevsegCode_2 = {{1{1'b1}}, multiplexer_5_out};  // Bit_Extender bit_extender_6
  Multiplexer #(.width(8), .enable("false")) multiplexer_6 (
    .in0(8'h17), .in1(8'h7f), .out(sevsegCode_1), .sel(and_5_out));
  and and_5 (and_5_out, ONOFFload, t_ff_1_q);
  Multiplexer #(.width(8), .enable("false")) multiplexer_7 (
    .in0(multiplexer_1_out), .in1(8'h7f), .out(sevsegCode_0), .sel(and_6_out));
  and and_6 (and_6_out, ONOFFload, t_ff_1_q);
  and and_7 (BUZZER, curONOFF, EQUAL);
endmodule

module alarmHM (
  input  RESET,
  input  CLK2k,
  input  [3:0] HloadT_4,
  input  HloadTEnDi,
  input  [3:0] HloadU_4,
  input  HloadUEnDi,
  input  [3:0] MINloadT_4,
  input  MINloadTEnDi,
  input  [3:0] MINloadU_4,
  input  MINloadUEnDi,
  input  ONOFFload,
  input  ONOFFloadEnDi,
  output [3:0] curHT_4,
  output [3:0] curHU_4,
  output [3:0] curMINT_4,
  output [3:0] curMINU_4,
  output curONOFF,
  output HloadT,
  output HloadU,
  output MINloadT,
  output MINloadU,
  output ONOFFL
);

  wire and_1_out, and_2_out, and_3_out, and_4_out, and_5_out, and_6_out, and_7_out, and_8_out, and_9_out,
       and_10_out, and_11_out, and_12_out, and_13_out, load_2_1_out0, load_2_1_out1, load_3_1_out0,
       load_3_1_out1, load_3_1_out2, load_4_1_out0, load_4_1_out1, load_4_1_out2, load_4_1_out3,
       load_4_2_out0, load_4_2_out1, load_4_2_out2, load_4_2_out3, multiplexer_1_out;
  wire [1:0] d_ff_2_q;
  wire [2:0] d_ff_9_q;

  load_2 load_2_1 (
    .IN1(d_ff_2_q[1]), .IN0(d_ff_2_q[0]), .loadValue(HloadT_4), .loadEnDi(HloadTEnDi), .OUT1(load_2_1_out1),
    .OUT0(load_2_1_out0));
  load_4 load_4_2 (
    .IN3(curHU_4[3]), .IN2(curHU_4[2]), .IN1(curHU_4[1]), .IN0(curHU_4[0]), .loadValue(HloadU_4),
    .loadEnDi(HloadUEnDi), .OUT3(load_4_2_out3), .OUT2(load_4_2_out2), .OUT1(load_4_2_out1),
    .OUT0(load_4_2_out0));
  load_3 load_3_1 (
    .IN2(d_ff_9_q[2]), .IN1(d_ff_9_q[1]), .IN0(d_ff_9_q[0]), .loadValue(MINloadT_4), .loadEnDi(MINloadTEnDi),
    .OUT2(load_3_1_out2), .OUT1(load_3_1_out1), .OUT0(load_3_1_out0));
  load_4 load_4_1 (
    .IN3(curMINU_4[3]), .IN2(curMINU_4[2]), .IN1(curMINU_4[1]), .IN0(curMINU_4[0]), .loadValue(MINloadU_4),
    .loadEnDi(MINloadUEnDi), .OUT3(load_4_1_out3), .OUT2(load_4_1_out2), .OUT1(load_4_1_out1),
    .OUT0(load_4_1_out0));
  Multiplexer #(.enable("false")) multiplexer_1 (
    .in0(curONOFF), .in1(ONOFFload), .out(multiplexer_1_out), .sel(ONOFFloadEnDi));
  and and_1 (and_1_out, ~RESET, load_2_1_out1);  // AND_Gate
  and and_2 (and_2_out, ~RESET, load_2_1_out0);  // AND_Gate
  and and_3 (and_3_out, ~RESET, load_4_2_out3);  // AND_Gate
  and and_4 (and_4_out, ~RESET, load_4_2_out2);  // AND_Gate
  and and_5 (and_5_out, ~RESET, load_4_2_out1);  // AND_Gate
  and and_6 (and_6_out, ~RESET, load_4_2_out0);  // AND_Gate
  and and_7 (and_7_out, ~RESET, load_3_1_out2);  // AND_Gate
  and and_8 (and_8_out, ~RESET, load_3_1_out1);  // AND_Gate
  and and_9 (and_9_out, ~RESET, load_3_1_out0);  // AND_Gate
  and and_10 (and_10_out, ~RESET, load_4_1_out3);  // AND_Gate
  and and_11 (and_11_out, ~RESET, load_4_1_out2);  // AND_Gate
  and and_12 (and_12_out, ~RESET, load_4_1_out1);  // AND_Gate
  and and_13 (and_13_out, ~RESET, load_4_1_out0);  // AND_Gate
  D_Flip_Flop d_ff_1 (.D(and_1_out), .clk(CLK2k), .Q(d_ff_2_q[1]), .reset(RESET));  // open: Qn, preset
  D_Flip_Flop d_ff_2 (.D(and_2_out), .clk(CLK2k), .Q(d_ff_2_q[0]), .reset(RESET));  // open: Qn, preset
  D_Flip_Flop d_ff_3 (.D(and_3_out), .clk(CLK2k), .Q(curHU_4[3]), .reset(RESET));  // open: Qn, preset
  D_Flip_Flop d_ff_4 (.D(and_4_out), .clk(CLK2k), .Q(curHU_4[2]), .reset(RESET));  // open: Qn, preset
  D_Flip_Flop d_ff_5 (.D(and_5_out), .clk(CLK2k), .Q(curHU_4[1]), .reset(RESET));  // open: Qn, preset
  D_Flip_Flop d_ff_6 (.D(and_6_out), .clk(CLK2k), .Q(curHU_4[0]), .reset(RESET));  // open: Qn, preset
  D_Flip_Flop d_ff_7 (.D(and_7_out), .clk(CLK2k), .Q(d_ff_9_q[2]), .reset(RESET));  // open: Qn, preset
  D_Flip_Flop d_ff_8 (.D(and_8_out), .clk(CLK2k), .Q(d_ff_9_q[1]), .reset(RESET));  // open: Qn, preset
  D_Flip_Flop d_ff_9 (.D(and_9_out), .clk(CLK2k), .Q(d_ff_9_q[0]), .reset(RESET));  // open: Qn, preset
  D_Flip_Flop d_ff_10 (.D(and_10_out), .clk(CLK2k), .Q(curMINU_4[3]), .reset(RESET));  // open: Qn, preset
  D_Flip_Flop d_ff_11 (.D(and_11_out), .clk(CLK2k), .Q(curMINU_4[2]), .reset(RESET));  // open: Qn, preset
  D_Flip_Flop d_ff_12 (.D(and_12_out), .clk(CLK2k), .Q(curMINU_4[1]), .reset(RESET));  // open: Qn, preset
  D_Flip_Flop d_ff_13 (.D(and_13_out), .clk(CLK2k), .Q(curMINU_4[0]), .reset(RESET));  // open: Qn, preset
  D_Flip_Flop d_ff_14 (.D(multiplexer_1_out), .clk(CLK2k), .Q(curONOFF), .reset(RESET));  // open: Qn, preset
  assign curHT_4 = {{2{1'b0}}, d_ff_2_q};  // Bit_Extender bit_extender_1
  assign curMINT_4 = {{1{1'b0}}, d_ff_9_q};  // Bit_Extender bit_extender_2

  assign HloadT = HloadTEnDi;
  assign HloadU = HloadUEnDi;
  assign MINloadT = MINloadTEnDi;
  assign MINloadU = MINloadUEnDi;
  assign ONOFFL = ONOFFloadEnDi;
endmodule

module compare (
  input  [3:0] A3_4,
  input  [3:0] A2_4,
  input  [3:0] A1_4,
  input  [3:0] A0_4,
  input  [3:0] B3_4,
  input  [3:0] B2_4,
  input  [3:0] B1_4,
  input  [3:0] B0_4,
  output EQUAL
);

  wire compare_4_1_equal_4, compare_4_2_equal_4, compare_4_3_equal_4, compare_4_4_equal_4;

  compare_4 compare_4_4 (.A_4(A3_4), .B_4(B3_4), .EQUAL_4(compare_4_4_equal_4));
  compare_4 compare_4_3 (.A_4(A2_4), .B_4(B2_4), .EQUAL_4(compare_4_3_equal_4));
  compare_4 compare_4_2 (.A_4(A1_4), .B_4(B1_4), .EQUAL_4(compare_4_2_equal_4));
  compare_4 compare_4_1 (.A_4(A0_4), .B_4(B0_4), .EQUAL_4(compare_4_1_equal_4));
  and and_1 (EQUAL, compare_4_4_equal_4, compare_4_3_equal_4, compare_4_2_equal_4, compare_4_1_equal_4);
endmodule

module compare_4 (
  input  [3:0] A_4,
  input  [3:0] B_4,
  output EQUAL_4
);

  wire xnor_1_out, xnor_2_out, xnor_3_out, xnor_4_out;

  xnor xnor_1 (xnor_1_out, A_4[0], B_4[0]);
  xnor xnor_2 (xnor_2_out, A_4[1], B_4[1]);
  xnor xnor_3 (xnor_3_out, A_4[2], B_4[2]);
  xnor xnor_4 (xnor_4_out, A_4[3], B_4[3]);
  and and_1 (EQUAL_4, xnor_1_out, xnor_2_out, xnor_3_out, xnor_4_out);
endmodule

module changeTimeZone (
  input  [7:0] SSDCode_5,
  input  [7:0] SSDCode_4,
  input  [7:0] SSDCode_3,
  input  [7:0] SSDCode_2,
  input  [7:0] SSDCode_1,
  input  [7:0] SSDCode_0,
  input  [7:0] UTCCode_8,
  output [7:0] sevsegCode_5,
  output [7:0] sevsegCode_4,
  output [7:0] sevsegCode_3,
  output [7:0] sevsegCode_2,
  output [7:0] sevsegCode_1,
  output [7:0] sevsegCode_0
);

  wire [3:0] H_HTimeZone_1_httz_4, H_HTimeZone_1_hutz_4, hourView_HMS_reverse_1_ht_4,
       hourView_HMS_reverse_1_hu_4, hourView_HMS_reverse_1_mint_4, hourView_HMS_reverse_1_minu_4,
       hourView_HMS_reverse_1_sect_4, hourView_HMS_reverse_1_secu_4;

  hourView_HMS_reverse hourView_HMS_reverse_1 (
    .sevsegCode_5(SSDCode_5), .sevsegCode_4(SSDCode_4), .sevsegCode_3(SSDCode_3), .sevsegCode_2(SSDCode_2),
    .sevsegCode_1(SSDCode_1), .sevsegCode_0(SSDCode_0), .HT_4(hourView_HMS_reverse_1_ht_4),
    .HU_4(hourView_HMS_reverse_1_hu_4), .MINT_4(hourView_HMS_reverse_1_mint_4),
    .MINU_4(hourView_HMS_reverse_1_minu_4), .SECT_4(hourView_HMS_reverse_1_sect_4),
    .SECU_4(hourView_HMS_reverse_1_secu_4));
  H_HTimeZone H_HTimeZone_1 (
    .HT_4(hourView_HMS_reverse_1_ht_4), .HU_4(hourView_HMS_reverse_1_hu_4), .UTCCode_8(UTCCode_8),
    .HTTZ_4(H_HTimeZone_1_httz_4), .HUTZ_4(H_HTimeZone_1_hutz_4));
  hourView_HMS_Ltime hourView_HMS_Ltime_1 (
    .HT_4(H_HTimeZone_1_httz_4), .HU_4(H_HTimeZone_1_hutz_4), .MINT_4(hourView_HMS_reverse_1_mint_4),
    .MINU_4(hourView_HMS_reverse_1_minu_4), .SECT_4(hourView_HMS_reverse_1_sect_4),
    .SECU_4(hourView_HMS_reverse_1_secu_4), .sevsegCode_5(sevsegCode_5), .sevsegCode_4(sevsegCode_4),
    .sevsegCode_3(sevsegCode_3), .sevsegCode_2(sevsegCode_2), .sevsegCode_1(sevsegCode_1),
    .sevsegCode_0(sevsegCode_0));
endmodule

module H_HTimeZone (
  input  [3:0] HT_4,
  input  [3:0] HU_4,
  input  [7:0] UTCCode_8,
  output [3:0] HTTZ_4,
  output [3:0] HUTZ_4
);

  wire [4:0] adder_2_out, bit_extender_1_out, bit_extender_2_out, bit_extender_5_out, multiplier_1_out;
  wire [6:0] adder_1_out, adder_3_out, adder_4_out, adder_5_out, adder_6_out, adder_7_out,
       bit_extender_3_out, bit_extender_4_out, multiplexer_1_out, multiplexer_2_out;

  assign bit_extender_1_out = {{1{1'b0}}, HT_4};  // Bit_Extender bit_extender_1
  assign bit_extender_2_out = {{1{1'b0}}, HU_4};  // Bit_Extender bit_extender_2
  Bit_Extender #(.out_width(7), .\type ("zero")) bit_extender_3 (.in(UTCCode_8), .out(bit_extender_3_out));
  Multiplier #(.width(5)) multiplier_1 (
    .a(bit_extender_1_out), .b(5'b01010), .out(multiplier_1_out));  // open: cin, cout
  Adder #(.width(7)) adder_1 (.a(bit_extender_3_out), .b(7'b0011000), .out(adder_1_out));  // open: cin, cout
  Adder #(.width(5)) adder_2 (.a(multiplier_1_out), .b(bit_extender_2_out), .out(adder_2_out));  // open: cin, cout
  assign bit_extender_4_out = {{2{1'b0}}, adder_2_out};  // Bit_Extender bit_extender_4
  Adder #(.width(7)) adder_3 (.a(bit_extender_4_out), .b(7'b1101000), .out(adder_3_out));  // open: cin, cout
  Adder #(.width(7)) adder_4 (.a(adder_3_out), .b(adder_1_out), .out(adder_4_out));  // open: cin, cout
  Adder #(.width(7)) adder_5 (.a(adder_4_out), .b(7'b0011000), .out(adder_5_out));  // open: cin, cout
  Adder #(.width(7)) adder_6 (.a(adder_4_out), .b(7'b1101000), .out(adder_6_out));  // open: cin, cout
  Multiplexer #(.width(7), .enable("false")) multiplexer_1 (
    .in0(adder_6_out), .in1(adder_5_out), .out(multiplexer_1_out), .sel(adder_4_out[6]));
  Adder #(.width(7)) adder_7 (.a(multiplexer_1_out), .b(7'b0011000), .out(adder_7_out));  // open: cin, cout
  Multiplexer #(.width(7), .enable("false")) multiplexer_2 (
    .in0(multiplexer_1_out), .in1(adder_7_out), .out(multiplexer_2_out), .sel(multiplexer_1_out[6]));
  Bit_Extender #(.in_width(7), .out_width(5), .\type ("zero")) bit_extender_5 (
    .in(multiplexer_2_out), .out(bit_extender_5_out));
  fivebits_to_2_4bits fivebits_to_2_4bits_1 (
    .A4(bit_extender_5_out[4]), .A3(bit_extender_5_out[3]), .A2(bit_extender_5_out[2]),
    .A1(bit_extender_5_out[1]), .A0(bit_extender_5_out[0]), .T3(HTTZ_4[3]), .T2(HTTZ_4[2]), .T1(HTTZ_4[1]),
    .T0(HTTZ_4[0]), .U3(HUTZ_4[3]), .U2(HUTZ_4[2]), .U1(HUTZ_4[1]), .U0(HUTZ_4[0]));
endmodule

module fivebits_to_2_4bits (
  input  A4,
  input  A3,
  input  A2,
  input  A1,
  input  A0,
  output T3,
  output T2,
  output T1,
  output T0,
  output U3,
  output U2,
  output U1,
  output U0
);

  wire and_1_out, and_2_out, and_3_out, and_4_out, and_5_out, and_6_out, and_7_out, and_8_out, and_9_out,
       and_10_out, and_11_out, and_12_out, and_13_out, and_14_out, and_15_out, and_16_out, and_17_out,
       and_18_out, not_1_out, not_2_out, not_3_out, not_4_out, not_5_out, not_6_out, not_7_out, not_8_out,
       not_9_out, not_10_out, not_11_out, not_12_out, not_13_out, not_14_out, not_15_out, not_16_out,
       not_17_out, not_18_out, not_19_out, not_20_out, not_21_out, not_22_out, not_23_out, not_24_out,
       not_25_out;

  and and_1 (and_1_out, A4, A2);
  and and_2 (and_2_out, A4, A3);
  not not_1 (not_1_out, A4);
  not not_2 (not_2_out, A4);
  not not_3 (not_3_out, A3);
  not not_4 (not_4_out, A2);
  not not_5 (not_5_out, A4);
  not not_6 (not_6_out, A2);
  not not_7 (not_7_out, A1);
  not not_8 (not_8_out, A3);
  not not_9 (not_9_out, A2);
  not not_10 (not_10_out, A1);
  not not_11 (not_11_out, A4);
  not not_12 (not_12_out, A3);
  not not_13 (not_13_out, A4);
  not not_14 (not_14_out, A2);
  not not_15 (not_15_out, A1);
  not not_16 (not_16_out, A2);
  not not_17 (not_17_out, A4);
  not not_18 (not_18_out, A3);
  not not_19 (not_19_out, A3);
  not not_20 (not_20_out, A4);
  not not_21 (not_21_out, A1);
  not not_22 (not_22_out, A3);
  not not_23 (not_23_out, A2);
  not not_24 (not_24_out, A1);
  not not_25 (not_25_out, A2);
  or or_1 (T1, and_1_out, and_2_out);
  and and_3 (and_3_out, not_1_out, A3, A1);
  and and_4 (and_4_out, not_2_out, A3, A2);
  and and_5 (and_5_out, A3, A2, A1);
  and and_6 (and_6_out, A4, not_3_out, not_4_out);
  and and_7 (and_7_out, not_5_out, A3, not_6_out, not_7_out);
  and and_8 (and_8_out, A4, not_8_out, not_9_out, A1);
  and and_9 (and_9_out, A4, A3, A2, not_10_out);
  and and_10 (and_10_out, not_11_out, not_12_out, A2);
  and and_11 (and_11_out, not_13_out, A2, A1);
  and and_12 (and_12_out, A4, not_14_out, not_15_out);
  and and_13 (and_13_out, A4, A3, not_16_out);
  and and_14 (and_14_out, not_17_out, not_18_out, A1);
  and and_15 (and_15_out, not_19_out, A2, A1);
  and and_16 (and_16_out, not_20_out, A3, A2, not_21_out);
  and and_17 (and_17_out, A4, not_22_out, not_23_out, not_24_out);
  and and_18 (and_18_out, A4, A3, not_25_out, A1);
  or or_2 (T0, and_3_out, and_4_out, and_5_out, and_6_out);
  or or_3 (U3, and_7_out, and_8_out, and_9_out);
  or or_4 (U2, and_10_out, and_11_out, and_12_out, and_13_out);
  or or_5 (U1, and_14_out, and_15_out, and_16_out, and_17_out, and_18_out);

  assign T2 = 1'b0;
  assign T3 = 1'b0;
  assign U0 = A0;
endmodule

module ANIMATION (
  input  [2:0] State,
  output [7:0] L1,
  output [7:0] L2,
  output [7:0] L3,
  output [7:0] L4,
  output [7:0] L5,
  output [7:0] L6
);

  Letter1 Letter1_1 (
    .a(State[2]), .b(State[1]), .c(State[0]), .x(L1[7]), .y(L1[4]), .z(L1[3]), .u(L1[2]), .w(L1[1]), .v(L1[0]));
  Letter2 Letter2_1 (
    .a(State[2]), .b(State[1]), .c(State[0]), .x(L2[7]), .y(L2[4]), .z(L2[3]), .u(L2[2]), .v(L2[1]), .w(L2[0]));
  Letter3 Letter3_1 (
    .a(State[2]), .b(State[1]), .c(State[0]), .x(L3[7]), .y(L3[4]), .z(L3[3]), .u(L3[2]), .v(L3[1]), .w(L3[0]));
  Letter4 Letter4_1 (
    .a(State[2]), .b(State[1]), .c(State[0]), .x(L4[7]), .y(L4[4]), .z(L4[3]), .u(L4[2]), .v(L4[1]), .w(L4[0]));
  Letter5 Letter5_1 (
    .a(State[2]), .b(State[1]), .c(State[0]), .x(L5[7]), .y(L5[4]), .z(L5[3]), .u(L5[2]), .v(L5[1]), .w(L5[0]));
  Letter6 Letter6_1 (
    .a(State[2]), .b(State[1]), .c(State[0]), .x(L6[7]), .y(L6[4]), .z(L6[3]), .u(L6[2]), .v(L6[1]), .w(L6[0]));

  assign L1[6:5] = 2'b00;
  assign L2[6:5] = 2'b00;
  assign L3[6:5] = 2'b00;
  assign L4[6:5] = 2'b00;
  assign L5[6:5] = 2'b00;
  assign L6[6:5] = 2'b00;
endmodule

module Letter1 (
  input  a,
  input  b,
  input  c,
  output x,
  output y,
  output z,
  output u,
  output w,
  output v
);

  wire and_2_out, and_3_out, and_4_out, and_6_out, and_7_out, not_1_out, not_2_out, not_3_out, not_4_out,
       not_5_out, not_6_out, not_7_out, not_8_out, not_9_out, not_10_out, not_11_out;

  and and_1 (x, a, b, c);
  not not_1 (not_1_out, a);
  not not_2 (not_2_out, b);
  not not_3 (not_3_out, a);
  not not_4 (not_4_out, a);
  not not_5 (not_5_out, b);
  not not_6 (not_6_out, a);
  not not_7 (not_7_out, b);
  not not_8 (not_8_out, c);
  not not_9 (not_9_out, a);
  not not_10 (not_10_out, b);
  not not_11 (not_11_out, c);
  and and_2 (and_2_out, not_1_out, not_2_out);
  or or_1 (y, and_2_out, and_3_out, and_4_out);
  and and_3 (and_3_out, not_3_out, c);
  and and_4 (and_4_out, a, b);
  or or_2 (z, not_4_out, not_5_out);
  or or_3 (u, not_6_out, c, b);
  and and_5 (w, not_7_out, not_8_out);
  and and_6 (and_6_out, not_9_out, not_10_out);
  or or_4 (v, and_6_out, and_7_out);
  and and_7 (and_7_out, a, b, not_11_out);
endmodule

module Letter2 (
  input  a,
  input  b,
  input  c,
  output x,
  output y,
  output z,
  output u,
  output v,
  output w
);

  wire and_1_out, and_2_out, and_3_out, and_4_out, and_5_out, and_6_out, and_7_out, and_8_out, and_9_out,
       and_10_out, and_11_out, not_1_out, not_2_out, not_3_out, not_4_out, not_5_out, not_6_out, not_7_out,
       not_8_out, not_9_out, not_10_out, not_11_out, not_12_out, not_13_out, not_14_out, not_15_out,
       not_16_out, not_17_out;

  not not_1 (not_1_out, a);
  not not_2 (not_2_out, c);
  not not_3 (not_3_out, a);
  not not_4 (not_4_out, b);
  not not_5 (not_5_out, b);
  not not_6 (not_6_out, a);
  not not_7 (not_7_out, b);
  not not_8 (not_8_out, b);
  not not_9 (not_9_out, c);
  not not_10 (not_10_out, a);
  not not_11 (not_11_out, b);
  not not_12 (not_12_out, c);
  not not_13 (not_13_out, a);
  not not_14 (not_14_out, b);
  not not_15 (not_15_out, a);
  not not_16 (not_16_out, c);
  not not_17 (not_17_out, c);
  or or_1 (y, not_1_out, not_2_out, b);
  and and_1 (and_1_out, not_3_out, not_4_out);
  or or_2 (z, and_1_out, and_2_out, and_3_out);
  and and_2 (and_2_out, not_5_out, c);
  and and_3 (and_3_out, a, b);
  and and_4 (and_4_out, not_6_out, not_7_out);
  or or_3 (u, and_4_out, and_5_out, and_6_out);
  and and_5 (and_5_out, not_8_out, not_9_out);
  and and_6 (and_6_out, a, b);
  and and_7 (and_7_out, not_10_out, not_11_out, not_12_out);
  and and_8 (and_8_out, not_13_out, b, c);
  or or_4 (v, and_7_out, and_8_out, and_9_out);
  and and_9 (and_9_out, a, not_14_out, c);
  and and_10 (and_10_out, not_15_out, not_16_out);
  or or_5 (w, and_10_out, and_11_out);
  and and_11 (and_11_out, b, not_17_out);

  assign x = 1'b0;
endmodule

module Letter3 (
  input  a,
  input  b,
  input  c,
  output x,
  output y,
  output z,
  output u,
  output v,
  output w
);

  wire and_1_out, and_2_out, and_3_out, and_4_out, and_5_out, and_6_out, and_7_out, and_8_out, not_1_out,
       not_2_out, not_3_out, not_4_out, not_5_out, not_6_out, not_7_out, not_8_out, not_9_out, not_10_out,
       not_11_out, not_12_out, not_13_out;

  not not_1 (not_1_out, a);
  not not_2 (not_2_out, c);
  not not_3 (not_3_out, b);
  not not_4 (not_4_out, c);
  not not_5 (not_5_out, a);
  not not_6 (not_6_out, b);
  not not_7 (not_7_out, a);
  not not_8 (not_8_out, c);
  and and_1 (and_1_out, a, b);
  not not_9 (not_9_out, a);
  not not_10 (not_10_out, b);
  not not_11 (not_11_out, c);
  not not_12 (not_12_out, a);
  not not_13 (not_13_out, c);
  and and_2 (and_2_out, not_1_out, not_2_out);
  or or_1 (y, and_2_out, b, and_3_out);
  and and_3 (and_3_out, a, c);
  or or_2 (z, not_3_out, not_4_out);
  and and_4 (and_4_out, not_5_out, not_6_out);
  or or_3 (u, and_4_out, and_5_out);
  and and_5 (and_5_out, not_7_out, c);
  or or_4 (v, not_8_out, and_1_out);
  and and_6 (and_6_out, not_9_out, not_10_out, not_11_out);
  or or_5 (w, and_6_out, and_7_out, and_8_out);
  and and_7 (and_7_out, not_12_out, b, c);
  and and_8 (and_8_out, a, b, not_13_out);

  assign x = 1'b0;
endmodule

module Letter4 (
  input  a,
  input  b,
  input  c,
  output x,
  output y,
  output z,
  output u,
  output v,
  output w
);

  wire and_1_out, and_2_out, and_3_out, and_4_out, and_5_out, and_6_out, not_1_out, not_2_out, not_3_out,
       not_4_out, not_5_out, not_6_out, not_7_out, not_8_out, not_9_out, not_10_out, not_11_out, not_12_out,
       not_13_out;

  not not_1 (not_1_out, b);
  not not_2 (not_2_out, c);
  not not_3 (not_3_out, b);
  not not_4 (not_4_out, c);
  not not_5 (not_5_out, a);
  not not_6 (not_6_out, a);
  and and_1 (and_1_out, b, c);
  not not_7 (not_7_out, a);
  not not_8 (not_8_out, b);
  not not_9 (not_9_out, c);
  not not_10 (not_10_out, a);
  not not_11 (not_11_out, b);
  not not_12 (not_12_out, a);
  not not_13 (not_13_out, c);
  or or_1 (y, not_1_out, not_2_out, a);
  and and_2 (and_2_out, not_3_out, not_4_out);
  or or_2 (z, and_2_out, and_3_out);
  and and_3 (and_3_out, not_5_out, c);
  or or_3 (u, not_6_out, and_1_out);
  or or_4 (v, not_7_out, not_8_out, not_9_out);
  and and_4 (and_4_out, not_10_out, not_11_out);
  and and_5 (and_5_out, not_12_out, not_13_out);
  or or_5 (w, and_4_out, and_5_out, and_6_out);
  and and_6 (and_6_out, a, b, c);

  assign x = 1'b0;
endmodule

module Letter5 (
  input  a,
  input  b,
  input  c,
  output x,
  output y,
  output z,
  output u,
  output v,
  output w
);

  wire and_1_out, and_3_out, and_4_out, and_5_out, and_6_out, not_1_out, not_2_out, not_3_out, not_4_out,
       not_5_out, not_6_out, not_7_out, not_8_out, not_9_out, not_10_out, not_11_out, not_12_out;

  not not_1 (not_1_out, b);
  not not_2 (not_2_out, a);
  not not_3 (not_3_out, b);
  not not_4 (not_4_out, a);
  not not_5 (not_5_out, b);
  not not_6 (not_6_out, b);
  not not_7 (not_7_out, c);
  not not_8 (not_8_out, a);
  and and_1 (and_1_out, b, c);
  not not_9 (not_9_out, a);
  not not_10 (not_10_out, b);
  not not_11 (not_11_out, b);
  not not_12 (not_12_out, c);
  and and_2 (x, a, not_1_out, c);
  or or_1 (y, not_2_out, not_3_out);
  and and_3 (and_3_out, not_4_out, not_5_out);
  or or_2 (z, and_3_out, c, and_4_out);
  and and_4 (and_4_out, a, b);
  or or_3 (u, not_6_out, not_7_out, a);
  or or_4 (v, not_8_out, and_1_out);
  and and_5 (and_5_out, not_9_out, not_10_out);
  or or_5 (w, and_5_out, and_6_out);
  and and_6 (and_6_out, not_11_out, not_12_out);
endmodule

module Letter6 (
  input  a,
  input  b,
  input  c,
  output x,
  output y,
  output z,
  output u,
  output v,
  output w
);

  wire not_1_out;

  not not_1 (not_1_out, b);
  or or_1 (z, not_1_out, c, a);

  assign u = 1'b1;
  assign v = 1'b1;
  assign w = 1'b1;
  assign x = 1'b0;
  assign y = 1'b1;
endmodule
