// Logisim project CHRONO.circ as structural Verilog: 6 circuits, main circuit ZeroTo59
module CHRONO (
  output [7:0] Seconds,
  output [7:0] Minutes,
  output [7:0] Hours
);

  wire clock_1_out, not_1_out, not_2_out;
  wire [7:0] outlogic_chrono_1_run_reset, Start_out, tranlogic_chrono_1_d1_d2;
  wire [7:2] undriven;

  Button Start (.out(Start_out[2]));
  Button Reset (.out(Start_out[3]));
  Clock clock_1 (.out(clock_1_out));
  TranLogic_Chrono tranlogic_chrono_1 (.Q1_Q2_Start_Reset(Start_out), .D1_D2(tranlogic_chrono_1_d1_d2));
  S_R_Flip_Flop s_r_ff_1 (
    .S(tranlogic_chrono_1_d1_d2[0]), .R(not_1_out), .clk(clock_1_out), .Q(Start_out[0]));  // open: reset, Qn, preset
  not not_1 (not_1_out, tranlogic_chrono_1_d1_d2[0]);
  S_R_Flip_Flop s_r_ff_2 (
    .S(tranlogic_chrono_1_d1_d2[1]), .R(not_2_out), .clk(clock_1_out), .Q(Start_out[1]));  // open: reset, Qn, preset
  not not_2 (not_2_out, tranlogic_chrono_1_d1_d2[1]);
  OutLogic_Chrono outlogic_chrono_1 (.D1_D2({undriven, Start_out[1:0]}), .Run_Reset(outlogic_chrono_1_run_reset));
  ZeroToAll zerotoall_1 (.Run_Reset_Clk(outlogic_chrono_1_run_reset), .out_2(Seconds), .out_3(Minutes), .out_4(Hours));
endmodule

module ZeroToAll (
  input  [7:0] Run_Reset_Clk,
  output [7:0] out_2,
  output [7:0] out_3,
  output [7:0] out_4
);

  wire Hours_carryout;
  wire [7:1] Minutes_carryout, Seconds_carryout;
  wire [7:3] undriven;

  ZeroTo59 Seconds (
    .count(out_2), .Reset_CarryIn_Clk({undriven, Run_Reset_Clk[2], Run_Reset_Clk[0], Run_Reset_Clk[1]}),
    .CarryOut(Seconds_carryout[1]));
  ZeroTo59 Minutes (
    .count(out_3),
    .Reset_CarryIn_Clk({Seconds_carryout[7:3], Run_Reset_Clk[2], Seconds_carryout[1], Run_Reset_Clk[1]}),
    .CarryOut(Minutes_carryout[1]));
  ZeroTo99 Hours (
    .Count(out_4),
    .Reset_CarryIn_Clk({Minutes_carryout[7:3], Run_Reset_Clk[2], Minutes_carryout[1], Run_Reset_Clk[1]}),
    .CarryOut(Hours_carryout));
  // also tied to GND on the sheet: Hours_carryout
endmodule

module ZeroTo59 (
  input  [7:0] Reset_CarryIn_Clk,
  output CarryOut,
  output [7:0] count
);

  Counter #(.width(6), .max('h3b)) counter_1 (
    .clr(Reset_CarryIn_Clk[0]), .count(Reset_CarryIn_Clk[1]), .clk(Reset_CarryIn_Clk[2]), .carry(CarryOut),
    .Q(count[5:0]));  // open: load, up, D
endmodule

module ZeroTo99 (
  input  [7:0] Reset_CarryIn_Clk,
  output CarryOut,
  output [7:0] Count
);

  Counter #(.width(7), .max('h63)) counter_1 (
    .clr(Reset_CarryIn_Clk[0]), .count(Reset_CarryIn_Clk[1]), .clk(Reset_CarryIn_Clk[2]), .carry(CarryOut),
    .Q(Count[6:0]));  // open: load, up, D
endmodule

module TranLogic_Chrono (
  input  [7:0] Q1_Q2_Start_Reset,
  output [7:0] D1_D2
);

  wire and_1_out, and_2_out, and_3_out, and_4_out, and_5_out, and_6_out, and_7_out, not_1_out, not_2_out,
       not_3_out, not_4_out, not_5_out, not_6_out, not_7_out, not_8_out, not_9_out, not_10_out, not_11_out,
       not_12_out;

  not not_1 (not_1_out, Q1_Q2_Start_Reset[1]);
  not not_2 (not_2_out, Q1_Q2_Start_Reset[2]);
  not not_3 (not_3_out, Q1_Q2_Start_Reset[0]);
  not not_4 (not_4_out, Q1_Q2_Start_Reset[2]);
  not not_5 (not_5_out, Q1_Q2_Start_Reset[0]);
  not not_6 (not_6_out, Q1_Q2_Start_Reset[0]);
  not not_7 (not_7_out, Q1_Q2_Start_Reset[3]);
  not not_8 (not_8_out, Q1_Q2_Start_Reset[1]);
  not not_9 (not_9_out, Q1_Q2_Start_Reset[3]);
  not not_10 (not_10_out, Q1_Q2_Start_Reset[1]);
  not not_11 (not_11_out, Q1_Q2_Start_Reset[0]);
  not not_12 (not_12_out, Q1_Q2_Start_Reset[2]);
  and and_1 (and_1_out, not_1_out, Q1_Q2_Start_Reset[0], not_2_out, Q1_Q2_Start_Reset[3]);
  and and_2 (and_2_out, Q1_Q2_Start_Reset[1], not_3_out, not_4_out);
  and and_3 (and_3_out, Q1_Q2_Start_Reset[1], not_5_out, Q1_Q2_Start_Reset[3]);
  and and_4 (and_4_out, not_6_out, Q1_Q2_Start_Reset[2], not_7_out);
  and and_5 (and_5_out, not_8_out, Q1_Q2_Start_Reset[0], not_9_out);
  and and_6 (and_6_out, not_10_out, Q1_Q2_Start_Reset[0], Q1_Q2_Start_Reset[2]);
  and and_7 (and_7_out, Q1_Q2_Start_Reset[1], not_11_out, not_12_out, Q1_Q2_Start_Reset[3]);
  or or_1 (D1_D2[1], and_1_out, and_2_out, and_3_out);
  or or_2 (D1_D2[0], and_4_out, and_5_out, and_6_out, and_7_out);
endmodule

module OutLogic_Chrono (
  input  [7:0] D1_D2,
  output [7:0] Run_Reset
);

  wire not_1_out;

  not not_1 (not_1_out, D1_D2[1]);
  and and_1 (Run_Reset[0], not_1_out, D1_D2[0]);
  and and_2 (Run_Reset[1], D1_D2[1], D1_D2[0]);
endmodule
