// Logisim project FSM_Chronometre.circ as structural Verilog: 4 circuits, main circuit main
module main (
  input  Start,
  input  Stop_Reset
);

  wire C_out, d_ff_1_q, d_ff_2_q, transitionlogic_1_d1, transitionlogic_1_d2;

  TransitionLogic transitionlogic_1 (
    .Start(Start), .StopReset(Stop_Reset), .Q1(d_ff_1_q), .Q2(d_ff_2_q), .D1(transitionlogic_1_d1),
    .D2(transitionlogic_1_d2));
  Clock C (.out(C_out));
  D_Flip_Flop d_ff_1 (.D(transitionlogic_1_d1), .clk(C_out), .Q(d_ff_1_q));  // open: Qn, preset, reset
  D_Flip_Flop d_ff_2 (.D(transitionlogic_1_d2), .clk(C_out), .Q(d_ff_2_q));  // open: Qn, preset, reset
  OutputLogic outputlogic_1 (.D1(d_ff_1_q), .D2(d_ff_2_q), .C(C_out));
endmodule

module TransitionLogic (
  input  Start,
  input  StopReset,
  input  Q1,
  input  Q2,
  output D1,
  output D2
);

  wire and_1_out, and_2_out, and_3_out, and_4_out, not_1_out, not_2_out, not_3_out, not_4_out, not_5_out,
       not_6_out, not_7_out;

  not not_1 (not_1_out, StopReset);
  not not_2 (not_2_out, Start);
  not not_3 (not_3_out, Q1);
  not not_4 (not_4_out, Start);
  not not_5 (not_5_out, StopReset);
  not not_6 (not_6_out, Start);
  not not_7 (not_7_out, Q2);
  or or_1 (D1, not_1_out, Q1);
  and and_1 (and_1_out, not_2_out, not_3_out);
  and and_2 (and_2_out, not_4_out, not_5_out, Q2);
  and and_3 (and_3_out, not_6_out, StopReset, not_7_out);
  and and_4 (and_4_out, Start, StopReset, Q2);
  or or_2 (D2, and_1_out, and_2_out, and_3_out, and_4_out);
endmodule

module OutputLogic (
  input  D1,
  input  D2,
  input  C
);
endmodule

module Display (
  input  in_1,
  input  in_2,
  input  in_3,
  input  in_4,
  input  in_5
);
endmodule
