// Logisim project ChangementFuseau.circ as structural Verilog: 6 circuits, main circuit ChangementFuseauHoraire
module ChangementFuseauHoraire (
  input  Change,
  output [7:0] Letter1,
  output [7:0] Letter2,
  output [7:0] Letter3,
  output [7:0] UTCCode
);

  wire [7:0] undriven_3;
  wire [7:5] undriven, undriven_2, undriven_4;

  Counter #(.width(5), .max('h10)) counter_1 (
    .count(1'b1), .clk(Change), .Q(undriven_3[4:0]));  // open: clr, load, up, D, carry
  Capitales Capitales_1 (.Output_bus_1(UTCCode), .Input_bus_1({undriven, undriven_3[4:0]}));
  CapitalLetter1 CapitalLetter1_1 (.Input_bus_1({undriven_2, undriven_3[4:0]}), .Output_bus_1(Letter1));
  CapitalLetter2 CapitalLetter2_1 (.Input_bus_1(undriven_3), .Output_bus_1(Letter2));
  CapitalLetter3 CapitalLetter3_1 (.Input_bus_1({undriven_4, undriven_3[4:0]}), .Output_bus_1(Letter3));
endmodule

module Capitales (
  input  [7:0] Input_bus_1,
  output [7:0] Output_bus_1
);

  wire and_1_out, and_2_out, and_3_out, and_4_out, and_5_out, and_6_out, and_7_out, and_8_out, and_9_out,
       and_10_out, not_1_out, not_2_out, not_3_out, not_4_out, not_5_out, not_6_out, not_7_out, not_8_out;

  and and_1 (and_1_out, Input_bus_1[3], Input_bus_1[1], Input_bus_1[0]);
  and and_2 (and_2_out, Input_bus_1[3], Input_bus_1[2]);
  or or_1 (Output_bus_1[3], Input_bus_1[3], Input_bus_1[4]);
  not not_1 (not_1_out, Input_bus_1[3]);
  not not_2 (not_2_out, Input_bus_1[3]);
  not not_3 (not_3_out, Input_bus_1[0]);
  not not_4 (not_4_out, Input_bus_1[1]);
  not not_5 (not_5_out, Input_bus_1[3]);
  not not_6 (not_6_out, Input_bus_1[2]);
  not not_7 (not_7_out, Input_bus_1[1]);
  not not_8 (not_8_out, Input_bus_1[0]);
  or or_2 (Output_bus_1[4], and_1_out, and_2_out, Input_bus_1[4]);
  and and_3 (and_3_out, not_1_out, Input_bus_1[2]);
  and and_4 (and_4_out, Input_bus_1[2], Input_bus_1[1], Input_bus_1[0]);
  and and_5 (and_5_out, not_2_out, Input_bus_1[1]);
  and and_6 (and_6_out, Input_bus_1[1], not_3_out);
  and and_7 (and_7_out, Input_bus_1[3], Input_bus_1[2], not_4_out, Input_bus_1[0]);
  and and_8 (and_8_out, not_5_out, Input_bus_1[0]);
  and and_9 (and_9_out, not_6_out, not_7_out, Input_bus_1[0]);
  and and_10 (and_10_out, Input_bus_1[3], Input_bus_1[2], not_8_out);
  or or_3 (Output_bus_1[2], and_3_out, and_4_out, Input_bus_1[4]);
  or or_4 (Output_bus_1[1], and_5_out, and_6_out, and_7_out);
  or or_5 (Output_bus_1[0], and_8_out, and_9_out, and_10_out, Input_bus_1[4]);
endmodule

module CapitalLetter1 (
  input  [7:0] Input_bus_1,
  output [7:0] Output_bus_1
);

  wire and_1_out, and_2_out, and_3_out, and_4_out, and_5_out, and_6_out, and_7_out, and_8_out, and_9_out,
       and_10_out, and_11_out, and_12_out, and_13_out, and_14_out, and_15_out, and_16_out, not_1_out,
       not_2_out, not_3_out, not_4_out, not_5_out, not_6_out, not_7_out, not_8_out, not_9_out, not_10_out,
       not_11_out, not_12_out, not_13_out, not_14_out, not_15_out, not_16_out, not_17_out, not_18_out,
       not_19_out, not_20_out, not_21_out, not_22_out, not_23_out, not_24_out, not_25_out, not_26_out;

  not not_1 (not_1_out, Input_bus_1[2]);
  not not_2 (not_2_out, Input_bus_1[1]);
  not not_3 (not_3_out, Input_bus_1[1]);
  not not_4 (not_4_out, Input_bus_1[0]);
  not not_5 (not_5_out, Input_bus_1[2]);
  not not_6 (not_6_out, Input_bus_1[1]);
  not not_7 (not_7_out, Input_bus_1[0]);
  not not_8 (not_8_out, Input_bus_1[3]);
  not not_9 (not_9_out, Input_bus_1[2]);
  not not_10 (not_10_out, Input_bus_1[3]);
  not not_11 (not_11_out, Input_bus_1[1]);
  not not_12 (not_12_out, Input_bus_1[3]);
  not not_13 (not_13_out, Input_bus_1[2]);
  not not_14 (not_14_out, Input_bus_1[1]);
  not not_15 (not_15_out, Input_bus_1[0]);
  not not_16 (not_16_out, Input_bus_1[1]);
  not not_17 (not_17_out, Input_bus_1[2]);
  not not_18 (not_18_out, Input_bus_1[0]);
  not not_19 (not_19_out, Input_bus_1[3]);
  not not_20 (not_20_out, Input_bus_1[1]);
  not not_21 (not_21_out, Input_bus_1[3]);
  not not_22 (not_22_out, Input_bus_1[2]);
  not not_23 (not_23_out, Input_bus_1[2]);
  not not_24 (not_24_out, Input_bus_1[1]);
  not not_25 (not_25_out, Input_bus_1[3]);
  not not_26 (not_26_out, Input_bus_1[0]);
  and and_1 (and_1_out, Input_bus_1[3], not_1_out, not_2_out, Input_bus_1[0]);
  and and_2 (and_2_out, Input_bus_1[3], Input_bus_1[2], not_3_out, not_4_out);
  and and_3 (and_3_out, not_5_out, not_6_out, not_7_out);
  and and_4 (and_4_out, not_8_out, not_9_out, Input_bus_1[1], Input_bus_1[0]);
  and and_5 (and_5_out, not_10_out, Input_bus_1[2], not_11_out, Input_bus_1[0]);
  and and_6 (and_6_out, not_12_out, Input_bus_1[2], Input_bus_1[1], Input_bus_1[0]);
  and and_7 (and_7_out, Input_bus_1[3], not_13_out, not_14_out, not_15_out);
  and and_8 (and_8_out, Input_bus_1[3], Input_bus_1[2], not_16_out, Input_bus_1[0]);
  and and_9 (and_9_out, not_17_out, not_18_out);
  and and_10 (and_10_out, not_19_out, Input_bus_1[1]);
  and and_11 (and_11_out, Input_bus_1[1], Input_bus_1[0]);
  and and_12 (and_12_out, Input_bus_1[3], Input_bus_1[2], not_20_out);
  and and_13 (and_13_out, not_21_out, not_22_out, Input_bus_1[0]);
  and and_14 (and_14_out, not_23_out, not_24_out, Input_bus_1[0]);
  and and_15 (and_15_out, not_25_out, Input_bus_1[2], Input_bus_1[1]);
  and and_16 (and_16_out, Input_bus_1[3], Input_bus_1[2], not_26_out);
  or or_1 (Output_bus_1[4], and_1_out, and_2_out);
  or or_2 (Output_bus_1[3], and_3_out, and_4_out, and_5_out);
  or or_3 (Output_bus_1[2], and_6_out, and_7_out, and_8_out);
  or or_4 (Output_bus_1[1], and_9_out, and_10_out, and_11_out, and_12_out);
  or or_5 (Output_bus_1[0], and_13_out, and_14_out, and_15_out, and_16_out, Input_bus_1[4]);
endmodule

module CapitalLetter2 (
  input  [7:0] Input_bus_1,
  output [7:0] Output_bus_1
);

  wire and_1_out, and_2_out, and_3_out, and_4_out, and_5_out, and_6_out, and_7_out, and_8_out, and_9_out,
       and_10_out, and_11_out, and_12_out, not_1_out, not_2_out, not_3_out, not_4_out, not_5_out, not_6_out,
       not_7_out, not_8_out, not_9_out, not_10_out, not_11_out, not_12_out, not_13_out, not_14_out,
       not_15_out, not_16_out, not_17_out, not_18_out, not_19_out, not_20_out, not_21_out, not_22_out,
       not_23_out;

  not not_1 (not_1_out, Input_bus_1[3]);
  not not_2 (not_2_out, Input_bus_1[2]);
  not not_3 (not_3_out, Input_bus_1[1]);
  not not_4 (not_4_out, Input_bus_1[1]);
  not not_5 (not_5_out, Input_bus_1[4]);
  not not_6 (not_6_out, Input_bus_1[3]);
  not not_7 (not_7_out, Input_bus_1[2]);
  not not_8 (not_8_out, Input_bus_1[1]);
  not not_9 (not_9_out, Input_bus_1[0]);
  not not_10 (not_10_out, Input_bus_1[0]);
  not not_11 (not_11_out, Input_bus_1[4]);
  not not_12 (not_12_out, Input_bus_1[2]);
  not not_13 (not_13_out, Input_bus_1[1]);
  not not_14 (not_14_out, Input_bus_1[0]);
  not not_15 (not_15_out, Input_bus_1[1]);
  not not_16 (not_16_out, Input_bus_1[4]);
  not not_17 (not_17_out, Input_bus_1[3]);
  not not_18 (not_18_out, Input_bus_1[1]);
  not not_19 (not_19_out, Input_bus_1[0]);
  not not_20 (not_20_out, Input_bus_1[3]);
  not not_21 (not_21_out, Input_bus_1[2]);
  not not_22 (not_22_out, Input_bus_1[1]);
  not not_23 (not_23_out, Input_bus_1[0]);
  and and_1 (and_1_out, not_1_out, not_2_out, Input_bus_1[1], Input_bus_1[0]);
  and and_2 (and_2_out, Input_bus_1[2], not_3_out, Input_bus_1[0]);
  and and_3 (and_3_out, Input_bus_1[3], Input_bus_1[2], not_4_out);
  and and_4 (and_4_out, not_5_out, not_6_out, not_7_out, not_8_out, not_9_out);
  and and_5 (and_5_out, Input_bus_1[3], Input_bus_1[2], Input_bus_1[1], not_10_out);
  and and_6 (and_6_out, not_11_out, not_12_out, not_13_out);
  and and_7 (and_7_out, Input_bus_1[3], Input_bus_1[2], Input_bus_1[1], not_14_out);
  and and_8 (and_8_out, Input_bus_1[3], Input_bus_1[2], not_15_out);
  and and_9 (and_9_out, not_16_out, not_17_out, not_18_out, not_19_out);
  and and_10 (and_10_out, not_20_out, not_21_out, Input_bus_1[1], Input_bus_1[0]);
  and and_11 (and_11_out, Input_bus_1[2], not_22_out, Input_bus_1[0]);
  and and_12 (and_12_out, Input_bus_1[3], Input_bus_1[1], not_23_out);
  or or_1 (Output_bus_1[4], and_1_out, and_2_out, and_3_out, Input_bus_1[4]);
  or or_2 (Output_bus_1[3], and_4_out, and_5_out);
  or or_3 (Output_bus_1[2], and_6_out, and_7_out);
  or or_4 (Output_bus_1[1], and_8_out, Input_bus_1[4]);
  or or_5 (Output_bus_1[0], and_9_out, and_10_out, and_11_out, and_12_out);
endmodule

module CapitalLetter3 (
  input  [7:0] Input_bus_1,
  output [7:0] Output_bus_1
);

  wire and_1_out, and_2_out, and_3_out, and_4_out, and_5_out, and_6_out, and_7_out, and_8_out, and_9_out,
       and_10_out, and_11_out, and_12_out, and_13_out, and_14_out, and_15_out, and_16_out, not_1_out,
       not_2_out, not_3_out, not_4_out, not_5_out, not_6_out, not_7_out, not_8_out, not_9_out, not_10_out,
       not_11_out, not_12_out, not_13_out, not_14_out, not_15_out, not_16_out, not_17_out, not_18_out,
       not_19_out, not_20_out, not_21_out, not_22_out, not_23_out, not_24_out, not_25_out, not_26_out,
       not_27_out, not_28_out, not_29_out, not_30_out, not_31_out, not_32_out;

  not not_1 (not_1_out, Input_bus_1[3]);
  not not_2 (not_2_out, Input_bus_1[2]);
  not not_3 (not_3_out, Input_bus_1[1]);
  not not_4 (not_4_out, Input_bus_1[2]);
  not not_5 (not_5_out, Input_bus_1[0]);
  not not_6 (not_6_out, Input_bus_1[4]);
  not not_7 (not_7_out, Input_bus_1[3]);
  not not_8 (not_8_out, Input_bus_1[2]);
  not not_9 (not_9_out, Input_bus_1[0]);
  not not_10 (not_10_out, Input_bus_1[4]);
  not not_11 (not_11_out, Input_bus_1[2]);
  not not_12 (not_12_out, Input_bus_1[1]);
  not not_13 (not_13_out, Input_bus_1[0]);
  not not_14 (not_14_out, Input_bus_1[3]);
  not not_15 (not_15_out, Input_bus_1[2]);
  not not_16 (not_16_out, Input_bus_1[4]);
  not not_17 (not_17_out, Input_bus_1[2]);
  not not_18 (not_18_out, Input_bus_1[1]);
  not not_19 (not_19_out, Input_bus_1[0]);
  not not_20 (not_20_out, Input_bus_1[3]);
  not not_21 (not_21_out, Input_bus_1[2]);
  not not_22 (not_22_out, Input_bus_1[1]);
  not not_23 (not_23_out, Input_bus_1[0]);
  not not_24 (not_24_out, Input_bus_1[2]);
  not not_25 (not_25_out, Input_bus_1[3]);
  not not_26 (not_26_out, Input_bus_1[1]);
  not not_27 (not_27_out, Input_bus_1[0]);
  not not_28 (not_28_out, Input_bus_1[3]);
  not not_29 (not_29_out, Input_bus_1[1]);
  not not_30 (not_30_out, Input_bus_1[0]);
  not not_31 (not_31_out, Input_bus_1[2]);
  not not_32 (not_32_out, Input_bus_1[1]);
  and and_1 (and_1_out, not_1_out, not_2_out, not_3_out, Input_bus_1[0]);
  and and_2 (and_2_out, Input_bus_1[3], not_4_out, Input_bus_1[1], not_5_out);
  and and_3 (and_3_out, Input_bus_1[3], Input_bus_1[2], Input_bus_1[1], Input_bus_1[0]);
  and and_4 (and_4_out, not_6_out, not_7_out, not_8_out, not_9_out);
  and and_5 (and_5_out, not_10_out, not_11_out, not_12_out, not_13_out);
  and and_6 (and_6_out, not_14_out, Input_bus_1[2], Input_bus_1[0]);
  and and_7 (and_7_out, Input_bus_1[3], not_15_out, Input_bus_1[0]);
  and and_8 (and_8_out, not_16_out, not_17_out, not_18_out, not_19_out);
  and and_9 (and_9_out, not_20_out, Input_bus_1[2], Input_bus_1[1], Input_bus_1[0]);
  and and_10 (and_10_out, Input_bus_1[3], not_21_out, not_22_out);
  and and_11 (and_11_out, Input_bus_1[3], Input_bus_1[2], Input_bus_1[1], not_23_out);
  and and_12 (and_12_out, not_24_out, Input_bus_1[1], Input_bus_1[0]);
  and and_13 (and_13_out, not_25_out, Input_bus_1[2], not_26_out);
  and and_14 (and_14_out, Input_bus_1[2], Input_bus_1[1], not_27_out);
  and and_15 (and_15_out, not_28_out, Input_bus_1[2], not_29_out, not_30_out);
  and and_16 (and_16_out, Input_bus_1[3], not_31_out, not_32_out, Input_bus_1[0]);
  or or_1 (Output_bus_1[4], and_1_out, and_2_out, and_3_out);
  or or_2 (Output_bus_1[3], and_4_out, and_5_out, and_6_out, and_7_out);
  or or_3 (Output_bus_1[2], and_8_out, and_9_out, and_10_out, and_11_out);
  or or_4 (Output_bus_1[1], and_12_out, and_13_out, and_14_out, Input_bus_1[4]);
  or or_5 (Output_bus_1[0], and_15_out, and_16_out, Input_bus_1[4]);
endmodule

module test (
);

  wire Button_1_out;
  wire [7:0] ChangementFuseauHoraire_1_letter1, ChangementFuseauHoraire_1_letter2,
       ChangementFuseauHoraire_1_letter3;

  Button Button_1 (.out(Button_1_out));
  ChangementFuseauHoraire ChangementFuseauHoraire_1 (
    .Change(Button_1_out), .Letter1(ChangementFuseauHoraire_1_letter1),
    .Letter2(ChangementFuseauHoraire_1_letter2), .Letter3(ChangementFuseauHoraire_1_letter3));  // open: UTCCode
  SegLedControlAlphabet SegLedControlAlphabet_1 (
    .in_1(ChangementFuseauHoraire_1_letter1[4]), .in_2(ChangementFuseauHoraire_1_letter1[3]),
    .in_3(ChangementFuseauHoraire_1_letter1[2]), .in_4(ChangementFuseauHoraire_1_letter1[1]),
    .in_5(ChangementFuseauHoraire_1_letter1[0]));
  SegLedControlAlphabet SegLedControlAlphabet_2 (
    .in_1(ChangementFuseauHoraire_1_letter2[4]), .in_2(ChangementFuseauHoraire_1_letter2[3]),
    .in_3(ChangementFuseauHoraire_1_letter2[2]), .in_4(ChangementFuseauHoraire_1_letter2[1]),
    .in_5(ChangementFuseauHoraire_1_letter2[0]));
  SegLedControlAlphabet SegLedControlAlphabet_3 (
    .in_1(ChangementFuseauHoraire_1_letter3[4]), .in_2(ChangementFuseauHoraire_1_letter3[3]),
    .in_3(ChangementFuseauHoraire_1_letter3[2]), .in_4(ChangementFuseauHoraire_1_letter3[1]),
    .in_5(ChangementFuseauHoraire_1_letter3[0]));
endmodule
