// Logisim project ALARM.circ as structural Verilog
module ALARM (
  output Output_1
);

  wire and_1_out, Button_1_out, clock_1_out, not_1_out, or_1_p1, or_1_p2, or_1_p3, or_1_p4, or_1_p5, or_1_p6,
       or_1_p7, or_1_p8, or_1_p9, or_1_p10, or_1_p11, or_1_p12, or_1_p13, or_1_p14, or_1_p15, or_1_p16;
  wire [6:0] Scale_1_output_bus_1;

  Button Button_1 (.out(Button_1_out));
  and and_1 (and_1_out, 1'b1, not_1_out);
  // OR_Gate or_1: pin names not known; wires that end beside it: or_1_p1, or_1_p2, or_1_p3, or_1_p4, or_1_p5, or_1_p6, or_1_p7, or_1_p8, or_1_p9, or_1_p10, or_1_p11, or_1_p12, or_1_p13, or_1_p14, or_1_p15, or_1_p16
  not not_1 (not_1_out, or_1_p1);
  // Shift_Register #(.length(15)) shift_register_1: pin names not known; wires that end beside it: Button_1_out, and_1_out, or_1_p16, or_1_p15, or_1_p14, or_1_p13, or_1_p12, or_1_p11, or_1_p10, or_1_p9, or_1_p8, or_1_p7, or_1_p6, or_1_p5
  Clock #(.highDuration(2), .lowDuration(2)) clock_1 (.out(clock_1_out));
  Scale1 Scale_1 (.Input_1(clock_1_out), .Output_bus_1(Scale_1_output_bus_1));
  NoteControl NoteControl_1 (
    .Input_1(or_1_p16), .Input_2(or_1_p15), .Input_3(or_1_p14), .Input_4(or_1_p13), .Input_5(or_1_p12),
    .Input_6(or_1_p11), .Input_7(or_1_p10), .Input_bus_1(Scale_1_output_bus_1), .Output_1(Output_1));
endmodule

module NoteControl (
  input  Input_1,
  input  Input_2,
  input  Input_3,
  input  Input_4,
  input  Input_5,
  input  Input_6,
  input  Input_7,
  input  [6:0] Input_bus_1,
  output Output_1
);

  wire and_1_out, and_2_out, and_3_out, and_4_out, and_5_out, and_6_out, and_7_out;

  and and_1 (and_1_out, Input_1, Input_bus_1[0]);
  and and_2 (and_2_out, Input_2, Input_bus_1[1]);
  and and_3 (and_3_out, Input_3, Input_bus_1[2]);
  and and_4 (and_4_out, Input_4, Input_bus_1[3]);
  and and_5 (and_5_out, Input_5, Input_bus_1[4]);
  and and_6 (and_6_out, Input_6, Input_bus_1[5]);
  and and_7 (and_7_out, Input_7, Input_bus_1[6]);
  ExactlyOne xor_1 (
    .out(Output_1), .in0(and_1_out), .in1(and_2_out), .in2(and_3_out), .in3(and_4_out), .in4(and_5_out),
    .in5(and_6_out), .in6(and_7_out));
endmodule

module C1 (
  input  Input_1,
  output Output_1
);

  wire counter_1_carry, d_ff_1_qn;

  Counter #(.width(5), .max('h1e)) counter_1 (
    .count(1'b1), .clk(Input_1), .carry(counter_1_carry));  // open: clr, load, up, D, Q
  D_Flip_Flop d_ff_1 (.D(d_ff_1_qn), .clk(counter_1_carry), .Q(Output_1), .Qn(d_ff_1_qn));  // open: preset, reset
endmodule

module D1 (
  input  Input_1,
  output Output_1
);

  wire counter_1_carry, d_ff_1_qn;

  Counter #(.width(5), .max('h1b)) counter_1 (
    .count(1'b1), .clk(Input_1), .carry(counter_1_carry));  // open: clr, load, up, D, Q
  D_Flip_Flop d_ff_1 (.D(d_ff_1_qn), .clk(counter_1_carry), .Q(Output_1), .Qn(d_ff_1_qn));  // open: preset, reset
endmodule

module E1 (
  input  Input_1,
  output Output_1
);

  wire counter_1_carry, d_ff_1_qn;

  Counter #(.width(5), .max('h18)) counter_1 (
    .count(1'b1), .clk(Input_1), .carry(counter_1_carry));  // open: clr, load, up, D, Q
  D_Flip_Flop d_ff_1 (.D(d_ff_1_qn), .clk(counter_1_carry), .Q(Output_1), .Qn(d_ff_1_qn));  // open: preset, reset
endmodule

module G1 (
  input  Input_1,
  output Output_1
);

  wire counter_1_carry, d_ff_1_qn;

  Counter #(.width(5), .max('h14)) counter_1 (
    .count(1'b1), .clk(Input_1), .carry(counter_1_carry));  // open: clr, load, up, D, Q
  D_Flip_Flop d_ff_1 (.D(d_ff_1_qn), .clk(counter_1_carry), .Q(Output_1), .Qn(d_ff_1_qn));  // open: preset, reset
endmodule

module A1 (
  input  Input_1,
  output Output_1
);

  wire counter_1_carry, d_ff_1_qn;

  Counter #(.width(5), .max('h12)) counter_1 (
    .count(1'b1), .clk(Input_1), .carry(counter_1_carry));  // open: clr, load, up, D, Q
  D_Flip_Flop d_ff_1 (.D(d_ff_1_qn), .clk(counter_1_carry), .Q(Output_1), .Qn(d_ff_1_qn));  // open: preset, reset
endmodule

module B1 (
  input  Input_1,
  output Output_1
);

  wire counter_1_carry, d_ff_1_qn;

  Counter #(.width(5), .max('h10)) counter_1 (
    .count(1'b1), .clk(Input_1), .carry(counter_1_carry));  // open: clr, load, up, D, Q
  D_Flip_Flop d_ff_1 (.D(d_ff_1_qn), .clk(counter_1_carry), .Q(Output_1), .Qn(d_ff_1_qn));  // open: preset, reset
endmodule

module C2 (
  input  Input_1,
  output Output_1
);

  wire counter_1_carry, d_ff_1_qn;

  Counter #(.width(4), .max('he)) counter_1 (
    .count(1'b1), .clk(Input_1), .carry(counter_1_carry));  // open: clr, load, up, D, Q
  D_Flip_Flop d_ff_1 (.D(d_ff_1_qn), .clk(counter_1_carry), .Q(Output_1), .Qn(d_ff_1_qn));  // open: preset, reset
endmodule

module D2 (
  input  in_1,
  output out_2
);

  wire counter_1_carry, d_ff_1_qn;

  Counter #(.width(5), .max('hd)) counter_1 (
    .count(1'b1), .clk(in_1), .carry(counter_1_carry));  // open: clr, load, up, D, Q
  D_Flip_Flop d_ff_1 (.D(d_ff_1_qn), .clk(counter_1_carry), .Q(out_2), .Qn(d_ff_1_qn));  // open: preset, reset
endmodule

module E2 (
  input  in_1,
  output out_2
);

  wire counter_1_carry, d_ff_1_qn;

  Counter #(.width(5), .max('hc)) counter_1 (
    .count(1'b1), .clk(in_1), .carry(counter_1_carry));  // open: clr, load, up, D, Q
  D_Flip_Flop d_ff_1 (.D(d_ff_1_qn), .clk(counter_1_carry), .Q(out_2), .Qn(d_ff_1_qn));  // open: preset, reset
endmodule

module G2 (
  input  in_1,
  output out_2
);

  wire counter_1_carry, d_ff_1_qn;

  Counter #(.width(5), .max('ha)) counter_1 (
    .count(1'b1), .clk(in_1), .carry(counter_1_carry));  // open: clr, load, up, D, Q
  D_Flip_Flop d_ff_1 (.D(d_ff_1_qn), .clk(counter_1_carry), .Q(out_2), .Qn(d_ff_1_qn));  // open: preset, reset
endmodule

module A2 (
  input  in_1,
  output out_2
);

  wire d_ff_1_qn, undriven;

  Counter #(.width(3), .max('h1)) counter_1 (.count(1'b1), .clk(in_1));  // open: clr, load, up, D, carry, Q
  D_Flip_Flop d_ff_1 (.D(d_ff_1_qn), .clk(undriven), .Q(out_2), .Qn(d_ff_1_qn));  // open: preset, reset
endmodule

module B2 (
  input  in_1,
  output out_2
);

  wire counter_1_carry, d_ff_1_qn;

  Counter #(.width(4), .max('hf)) counter_1 (
    .count(1'b1), .clk(in_1), .carry(counter_1_carry));  // open: clr, load, up, D, Q
  D_Flip_Flop d_ff_1 (.D(d_ff_1_qn), .clk(counter_1_carry), .Q(out_2), .Qn(d_ff_1_qn));  // open: preset, reset
endmodule

module Scale1 (
  input  Input_1,
  output [6:0] Output_bus_1
);

  C1 C1_1 (.Input_1(Input_1), .Output_1(Output_bus_1[0]));
  D1 D1_1 (.Output_1(Output_bus_1[1]), .Input_1(Input_1));
  E1 E1_1 (.Output_1(Output_bus_1[2]), .Input_1(Input_1));
  G1 G1_1 (.Output_1(Output_bus_1[3]), .Input_1(Input_1));
  A1 A1_1 (.Output_1(Output_bus_1[4]), .Input_1(Input_1));
  B1 B1_1 (.Output_1(Output_bus_1[5]), .Input_1(Input_1));
  C2 C2_1 (.Output_1(Output_bus_1[6]), .Input_1(Input_1));
endmodule

module ImperialMarch (
  input  Input_1,
  input  Input_2,
  input  Input_3,
  input  Input_4,
  input  Input_5,
  input  Input_6,
  output Output_1,
  output Output_2,
  output Output_3,
  output Output_4,
  output Output_5
);

  wire and_1_out, and_2_out, and_3_out, and_4_out, and_5_out, and_6_out, and_7_out, and_8_out, and_9_out,
       and_10_out, and_11_out, and_12_out, and_13_out, and_14_out, and_15_out, and_16_out, and_17_out,
       and_18_out, and_19_out, not_1_out, not_2_out, not_3_out, not_4_out, not_5_out, not_6_out, not_7_out,
       not_8_out, not_9_out, not_10_out, not_11_out, not_12_out, not_13_out, not_14_out, not_15_out,
       not_16_out, not_17_out, not_18_out, not_19_out, not_20_out, not_21_out, not_22_out, not_23_out,
       not_24_out, not_25_out, not_26_out, not_27_out, not_28_out, not_29_out, not_30_out, not_31_out,
       not_32_out, not_33_out, not_34_out, not_35_out, not_36_out, not_37_out, not_38_out, not_39_out,
       not_40_out, not_41_out, not_42_out, not_43_out, not_44_out, not_45_out, not_46_out;

  not not_1 (not_1_out, Input_1);
  not not_2 (not_2_out, Input_2);
  not not_3 (not_3_out, Input_5);
  not not_4 (not_4_out, Input_3);
  not not_5 (not_5_out, Input_5);
  not not_6 (not_6_out, Input_1);
  not not_7 (not_7_out, Input_2);
  not not_8 (not_8_out, Input_3);
  not not_9 (not_9_out, Input_5);
  not not_10 (not_10_out, Input_1);
  not not_11 (not_11_out, Input_2);
  not not_12 (not_12_out, Input_3);
  not not_13 (not_13_out, Input_6);
  not not_14 (not_14_out, Input_1);
  not not_15 (not_15_out, Input_5);
  not not_16 (not_16_out, Input_1);
  not not_17 (not_17_out, Input_6);
  not not_18 (not_18_out, Input_2);
  not not_19 (not_19_out, Input_3);
  not not_20 (not_20_out, Input_2);
  not not_21 (not_21_out, Input_3);
  not not_22 (not_22_out, Input_5);
  not not_23 (not_23_out, Input_2);
  not not_24 (not_24_out, Input_3);
  not not_25 (not_25_out, Input_6);
  not not_26 (not_26_out, Input_2);
  not not_27 (not_27_out, Input_4);
  not not_28 (not_28_out, Input_5);
  not not_29 (not_29_out, Input_2);
  not not_30 (not_30_out, Input_4);
  not not_31 (not_31_out, Input_6);
  not not_32 (not_32_out, Input_2);
  not not_33 (not_33_out, Input_4);
  and and_1 (and_1_out, not_1_out, not_2_out, Input_3, Input_4, not_3_out);
  and and_2 (and_2_out, Input_2, not_4_out, Input_4, not_5_out);
  and and_3 (and_3_out, not_6_out, not_7_out, not_8_out, not_9_out);
  and and_4 (and_4_out, not_10_out, not_11_out, not_12_out, not_13_out);
  not not_34 (not_34_out, Input_1);
  and and_5 (and_5_out, not_34_out, not_35_out, not_36_out);
  not not_35 (not_35_out, Input_4);
  not not_36 (not_36_out, Input_5);
  not not_37 (not_37_out, Input_1);
  and and_6 (and_6_out, not_37_out, not_38_out, not_39_out);
  not not_38 (not_38_out, Input_4);
  not not_39 (not_39_out, Input_6);
  and and_7 (and_7_out, Input_2, not_40_out, not_41_out);
  not not_40 (not_40_out, Input_4);
  not not_41 (not_41_out, Input_5);
  and and_8 (and_8_out, Input_2, not_42_out, not_43_out);
  not not_42 (not_42_out, Input_4);
  not not_43 (not_43_out, Input_6);
  and and_9 (and_9_out, not_14_out, Input_2, Input_3, not_15_out);
  and and_10 (and_10_out, not_16_out, Input_2, Input_3, not_17_out);
  and and_11 (and_11_out, Input_2, Input_3, not_44_out);
  not not_44 (not_44_out, Input_4);
  and and_12 (and_12_out, not_18_out, Input_3, Input_4, Input_5, Input_6);
  and and_13 (and_13_out, Input_2, not_19_out, Input_4, Input_5, Input_6);
  and and_14 (and_14_out, Input_1, not_20_out, not_21_out, not_22_out);
  and and_15 (and_15_out, Input_1, not_23_out, not_24_out, not_25_out);
  and and_16 (and_16_out, Input_1, not_26_out, not_27_out, not_28_out);
  and and_17 (and_17_out, Input_1, not_29_out, not_30_out, not_31_out);
  not not_45 (not_45_out, Input_2);
  not not_46 (not_46_out, Input_5);
  or or_1 (Output_1, and_1_out, and_2_out);
  or or_2 (Output_3, and_12_out, and_13_out);
  or or_3 (Output_4, and_14_out, and_15_out, and_16_out, and_17_out);
  and and_18 (and_18_out, Input_1, not_32_out, Input_3, not_33_out, Input_5, Input_6);
  or or_4 (Output_5, and_18_out, and_19_out);
  and and_19 (and_19_out, Input_1, not_45_out, Input_3, Input_4, not_46_out);
  or or_5 (Output_2, and_3_out, and_4_out, and_5_out, and_6_out, and_7_out, and_8_out, and_9_out, and_10_out, and_11_out);
endmodule

module BeatManager (
  input  Input_1,
  output [5:0] Output_bus_1
);

  wire counter_1_carry;

  Counter #(.width(12), .max('hfa0)) counter_1 (
    .clk(Input_1), .carry(counter_1_carry));  // open: clr, load, up, count, D, Q
  Counter #(.width(6), .max('h3f)) counter_2 (
    .up(1'b1), .clk(counter_1_carry), .Q(Output_bus_1));  // open: clr, load, count, D, carry
endmodule

module test (
  output Output_1
);

  wire clock_1_out, d_ff_1_q, d_ff_1_qn, ImperialMarch_1_output_1, ImperialMarch_1_output_2,
       ImperialMarch_1_output_3, ImperialMarch_1_output_4, ImperialMarch_1_output_5, NoteControl_2_output_1;
  wire [5:0] BeatManager_1_output_bus_1;
  wire [6:0] Scale1_1_output_bus_1, Scale1_2_output_bus_1;

  Clock clock_1 (.out(clock_1_out));
  BeatManager BeatManager_1 (.Input_1(clock_1_out), .Output_bus_1(BeatManager_1_output_bus_1));
  D_Flip_Flop d_ff_1 (.D(d_ff_1_qn), .clk(clock_1_out), .Q(d_ff_1_q), .Qn(d_ff_1_qn));  // open: preset, reset
  Scale1 Scale1_1 (.Input_1(d_ff_1_q), .Output_bus_1(Scale1_1_output_bus_1));
  Scale1 Scale1_2 (.Input_1(clock_1_out), .Output_bus_1(Scale1_2_output_bus_1));
  ImperialMarch ImperialMarch_1 (
    .Input_1(BeatManager_1_output_bus_1[5]), .Input_2(BeatManager_1_output_bus_1[4]),
    .Input_3(BeatManager_1_output_bus_1[3]), .Input_4(BeatManager_1_output_bus_1[2]),
    .Input_5(BeatManager_1_output_bus_1[1]), .Input_6(BeatManager_1_output_bus_1[0]),
    .Output_1(ImperialMarch_1_output_1), .Output_2(ImperialMarch_1_output_2),
    .Output_3(ImperialMarch_1_output_3), .Output_4(ImperialMarch_1_output_4),
    .Output_5(ImperialMarch_1_output_5));
  NoteControl NoteControl_1 (
    .Input_1(ImperialMarch_1_output_1), .Input_2(ImperialMarch_1_output_4),
    .Input_3(ImperialMarch_1_output_2), .Input_5(ImperialMarch_1_output_3),
    .Input_bus_1(Scale1_2_output_bus_1), .Output_1(Output_1));  // open: Input_4, Input_6, Input_7
  NoteControl NoteControl_2 (
    .Input_3(ImperialMarch_1_output_5), .Input_bus_1(Scale1_1_output_bus_1), .Output_1(NoteControl_2_output_1));  // open: Input_1, Input_2, Input_4, Input_5, Input_6, Input_7
endmodule

module test2 (
  output Output_1
);

  wire clock_1_out;

  Clock clock_1 (.out(clock_1_out));
  test test_1 (.Output_1(Output_1));
endmodule
