// Logisim project ALARM_v2.circ as structural Verilog: 5 circuits, main circuit FreqToNote
module ALARM (
  output Output_1
);

  wire BeatManager_1_beat0, BeatManager_1_beat1, BeatManager_1_beat2, BeatManager_1_beat3,
       BeatManager_1_beat4, BeatManager_1_beat5, clock_1_out, d_ff_1_qn, ImperialMarch_1_c1,
       ImperialMarch_1_d2, ImperialMarch_1_e1, ImperialMarch_1_e2, ImperialMarch_1_g1, NoteControl_1_outnote,
       NoteControl_1_reset;
  wire [5:0] main_1_ct;

  Clock clock_1 (.out(clock_1_out));
  BeatManager BeatManager_1 (
    .clk(clock_1_out), .beat5(BeatManager_1_beat5), .beat4(BeatManager_1_beat4), .beat3(BeatManager_1_beat3),
    .beat2(BeatManager_1_beat2), .beat1(BeatManager_1_beat1), .beat0(BeatManager_1_beat0));
  ImperialMarch ImperialMarch_1 (
    .beat5(BeatManager_1_beat5), .beat4(BeatManager_1_beat4), .beat3(BeatManager_1_beat3),
    .beat2(BeatManager_1_beat2), .beat1(BeatManager_1_beat1), .beat0(BeatManager_1_beat0),
    .c1(ImperialMarch_1_c1), .e1(ImperialMarch_1_e1), .g1(ImperialMarch_1_g1), .d2(ImperialMarch_1_d2),
    .e2(ImperialMarch_1_e2));
  FreqToNote main_1 (.reset(NoteControl_1_reset), .clk(clock_1_out), .ct(main_1_ct));
  NoteControl NoteControl_1 (
    .ct(main_1_ct), .e2(ImperialMarch_1_e2), .d2(ImperialMarch_1_d2), .g1(ImperialMarch_1_g1),
    .e1(ImperialMarch_1_e1), .c1(ImperialMarch_1_c1), .OutNote(NoteControl_1_outnote),
    .Reset(NoteControl_1_reset));  // open: c3, b2, a2, g2, c2, b1, a1, d1
  D_Flip_Flop d_ff_1 (.D(d_ff_1_qn), .clk(NoteControl_1_outnote), .Q(Output_1), .Qn(d_ff_1_qn));  // open: preset, reset
endmodule

module FreqToNote (
  input  reset,
  input  clk,
  output [5:0] ct
);

  Counter #(.width(6), .max('h3f)) counter_1 (
    .clr(reset), .count(1'b1), .clk(clk), .Q(ct));  // open: load, up, D, carry
endmodule

module NoteControl (
  input  [5:0] ct,
  input  c3,
  input  b2,
  input  a2,
  input  g2,
  input  e2,
  input  d2,
  input  c2,
  input  b1,
  input  a1,
  input  g1,
  input  e1,
  input  d1,
  input  c1,
  output OutNote,
  output Reset
);

  wire and_1_out, and_2_out, and_3_out, and_4_out, and_5_out, and_6_out, and_7_out, and_8_out, and_9_out,
       and_10_out, and_11_out, and_12_out, and_13_out;

  and and_1 (and_1_out, ct[0], ct[1], ct[2], ct[3], ~ct[4], ~ct[5], c3);  // AND_Gate
  and and_2 (and_2_out, ~ct[0], ~ct[1], ~ct[2], ~ct[3], ct[4], ~ct[5], b2);  // AND_Gate
  and and_3 (and_3_out, ~ct[0], ct[1], ~ct[2], ~ct[3], ct[4], ~ct[5], a2);  // AND_Gate
  and and_4 (and_4_out, ~ct[0], ~ct[1], ct[2], ~ct[3], ct[4], ~ct[5], g2);  // AND_Gate
  and and_5 (and_5_out, ~ct[0], ~ct[1], ~ct[2], ct[3], ct[4], ~ct[5], e2);  // AND_Gate
  and and_6 (and_6_out, ct[0], ct[1], ~ct[2], ct[3], ct[4], ~ct[5], d2);  // AND_Gate
  and and_7 (and_7_out, ~ct[0], ct[1], ct[2], ct[3], ct[4], ~ct[5], c2);  // AND_Gate
  and and_8 (and_8_out, ~ct[0], ~ct[1], ~ct[2], ~ct[3], ~ct[4], ct[5], b1);  // AND_Gate
  and and_9 (and_9_out, ~ct[0], ~ct[1], ct[2], ~ct[3], ~ct[4], ct[5], a1);  // AND_Gate
  and and_10 (and_10_out, ~ct[0], ~ct[1], ~ct[2], ct[3], ~ct[4], ct[5], g1);  // AND_Gate
  and and_11 (and_11_out, ~ct[0], ~ct[1], ~ct[2], ~ct[3], ct[4], ct[5], e1);  // AND_Gate
  and and_12 (and_12_out, ~ct[0], ct[1], ct[2], ~ct[3], ct[4], ct[5], d1);  // AND_Gate
  and and_13 (and_13_out, ~ct[0], ~ct[1], ct[2], ct[3], ct[4], ct[5], c1);  // AND_Gate
  or or_1 (OutNote, and_1_out, and_2_out, and_3_out, and_4_out, and_5_out, and_6_out, and_7_out, and_8_out, and_9_out, and_10_out, and_11_out, and_12_out, and_13_out);

  assign Reset = OutNote;

  // Notes on the sheet:
  //   counter
endmodule

module ImperialMarch (
  input  beat5,
  input  beat4,
  input  beat3,
  input  beat2,
  input  beat1,
  input  beat0,
  output c1,
  output e1,
  output g1,
  output d2,
  output e2
);

  wire and_1_out, and_2_out, and_3_out, and_4_out, and_5_out, and_6_out, and_7_out, and_8_out, and_9_out,
       and_10_out, and_11_out, and_12_out, and_13_out, and_14_out, and_15_out, and_16_out, and_17_out,
       and_18_out, and_19_out, not_1_out, not_2_out, not_3_out, not_4_out, not_5_out, not_6_out, not_7_out,
       not_8_out, not_9_out, not_10_out, not_11_out, not_12_out, not_13_out, not_14_out, not_15_out,
       not_16_out, not_17_out, not_18_out, not_19_out, not_20_out, not_21_out, not_22_out, not_23_out,
       not_24_out, not_25_out, not_26_out, not_27_out, not_28_out, not_29_out, not_30_out, not_31_out,
       not_32_out, not_33_out, not_34_out, not_35_out, not_36_out, not_37_out, not_38_out, not_39_out,
       not_40_out, not_41_out, not_42_out, not_43_out, not_44_out, not_45_out, not_46_out;

  not not_1 (not_1_out, beat5);
  not not_2 (not_2_out, beat4);
  not not_3 (not_3_out, beat1);
  not not_4 (not_4_out, beat5);
  not not_5 (not_5_out, beat4);
  not not_6 (not_6_out, beat0);
  not not_7 (not_7_out, beat3);
  not not_8 (not_8_out, beat1);
  not not_9 (not_9_out, beat3);
  not not_10 (not_10_out, beat0);
  not not_11 (not_11_out, beat5);
  not not_12 (not_12_out, beat4);
  not not_13 (not_13_out, beat3);
  not not_14 (not_14_out, beat1);
  not not_15 (not_15_out, beat5);
  not not_16 (not_16_out, beat4);
  not not_17 (not_17_out, beat3);
  not not_18 (not_18_out, beat0);
  not not_19 (not_19_out, beat5);
  not not_20 (not_20_out, beat2);
  not not_21 (not_21_out, beat1);
  not not_22 (not_22_out, beat5);
  not not_23 (not_23_out, beat2);
  not not_24 (not_24_out, beat0);
  not not_25 (not_25_out, beat2);
  not not_26 (not_26_out, beat1);
  not not_27 (not_27_out, beat0);
  not not_28 (not_28_out, beat2);
  not not_29 (not_29_out, beat4);
  not not_30 (not_30_out, beat3);
  not not_31 (not_31_out, beat4);
  not not_32 (not_32_out, beat3);
  not not_33 (not_33_out, beat1);
  not not_34 (not_34_out, beat4);
  not not_35 (not_35_out, beat3);
  not not_36 (not_36_out, beat0);
  not not_37 (not_37_out, beat4);
  not not_38 (not_38_out, beat2);
  not not_39 (not_39_out, beat1);
  not not_40 (not_40_out, beat4);
  not not_41 (not_41_out, beat2);
  not not_42 (not_42_out, beat0);
  not not_43 (not_43_out, beat4);
  not not_44 (not_44_out, beat1);
  not not_45 (not_45_out, beat4);
  not not_46 (not_46_out, beat0);
  and and_1 (and_1_out, not_1_out, not_2_out, beat3, beat2, not_3_out);
  and and_2 (and_2_out, not_4_out, not_5_out, beat3, beat2, not_6_out);
  and and_3 (and_3_out, beat4, not_7_out, beat2, not_8_out);
  and and_4 (and_4_out, beat4, not_9_out, beat2, not_10_out);
  and and_5 (and_5_out, not_11_out, not_12_out, not_13_out, not_14_out);
  and and_6 (and_6_out, not_15_out, not_16_out, not_17_out, not_18_out);
  and and_7 (and_7_out, not_19_out, not_20_out, not_21_out);
  and and_8 (and_8_out, not_22_out, not_23_out, not_24_out);
  and and_9 (and_9_out, beat4, beat3, not_25_out);
  and and_10 (and_10_out, beat4, beat3, not_26_out, not_27_out);
  and and_11 (and_11_out, beat5, beat4, not_28_out);
  and and_12 (and_12_out, not_29_out, beat3, beat2, beat1, beat0);
  and and_13 (and_13_out, beat4, not_30_out, beat2, beat1, beat0);
  and and_14 (and_14_out, beat5, not_31_out, not_32_out, not_33_out);
  and and_15 (and_15_out, beat5, not_34_out, not_35_out, not_36_out);
  and and_16 (and_16_out, beat5, not_37_out, not_38_out, not_39_out);
  and and_17 (and_17_out, beat5, not_40_out, not_41_out, not_42_out);
  and and_18 (and_18_out, beat5, not_43_out, beat3, beat2, not_44_out);
  and and_19 (and_19_out, beat5, not_45_out, beat3, beat2, not_46_out);
  or or_1 (c1, and_1_out, and_2_out, and_3_out, and_4_out);
  or or_2 (e1, and_5_out, and_6_out, and_7_out, and_8_out, and_9_out, and_10_out, and_11_out);
  or or_3 (g1, and_12_out, and_13_out);
  or or_4 (d2, and_14_out, and_15_out, and_16_out, and_17_out);
  or or_5 (e2, and_18_out, and_19_out);
endmodule

module BeatManager (
  input  clk,
  output beat5,
  output beat4,
  output beat3,
  output beat2,
  output beat1,
  output beat0
);

  wire Double_croche_150ms_carry;

  Counter #(.width(12), .max('h9c4)) Double_croche_150ms (
    .clk(clk), .carry(Double_croche_150ms_carry));  // open: clr, load, up, count, D, Q
  Counter #(.width(6), .max('h3f)) Mesure (
    .up(1'b1), .clk(Double_croche_150ms_carry), .Q({beat5, beat4, beat3, beat2, beat1, beat0}));  // open: clr, load, count, D, carry
endmodule
