// Logisim project CHRONO.circ as structural Verilog: 6 circuits, main circuit ZeroTo59
module CHRONO (
);

  wire clock_1_out, not_1_out, not_2_out, OutLogic_Chrono_1_reset, OutLogic_Chrono_1_run, Reset_Stop_out,
       s_r_ff_1_q, s_r_ff_2_q, Start_out, TranLogic_Chrono_1_d1, TranLogic_Chrono_1_d2;

  Clock clock_1 (.out(clock_1_out));
  Button Start (.out(Start_out));
  Button Reset_Stop (.out(Reset_Stop_out));
  TranLogic_Chrono TranLogic_Chrono_1 (
    .Q2(s_r_ff_2_q), .Q1(s_r_ff_1_q), .Start(Start_out), .Reset_Stop(Reset_Stop_out),
    .D2(TranLogic_Chrono_1_d2), .D1(TranLogic_Chrono_1_d1));
  S_R_Flip_Flop s_r_ff_1 (
    .S(TranLogic_Chrono_1_d1), .R(not_1_out), .clk(clock_1_out), .Q(s_r_ff_1_q));  // open: reset, Qn, preset
  not not_1 (not_1_out, TranLogic_Chrono_1_d1);
  S_R_Flip_Flop s_r_ff_2 (
    .S(TranLogic_Chrono_1_d2), .R(not_2_out), .clk(clock_1_out), .Q(s_r_ff_2_q));  // open: reset, Qn, preset
  not not_2 (not_2_out, TranLogic_Chrono_1_d2);
  OutLogic_Chrono OutLogic_Chrono_1 (
    .D2(s_r_ff_2_q), .D1(s_r_ff_1_q), .Run(OutLogic_Chrono_1_run), .Reset(OutLogic_Chrono_1_reset));
  ZeroToAll ZeroToAll_1 (.Run(OutLogic_Chrono_1_run), .Reset(OutLogic_Chrono_1_reset), .C(clock_1_out));
endmodule

module ZeroToAll (
  input  Run,
  input  Reset,
  input  C
);

  wire and_1_out, ZeroTo59_1_carry, ZeroTo59_2_carry;
  wire [5:0] ZeroTo59_1_s, ZeroTo59_2_s, ZeroTo59_3_s;

  and and_1 (and_1_out, ZeroTo59_2_carry, ZeroTo59_1_carry);
  ZeroTo59 ZeroTo59_1 (.prev(Run), .C(C), .reset(Reset), .s(ZeroTo59_1_s), .carry(ZeroTo59_1_carry));
  ZeroTo59 ZeroTo59_2 (.prev(ZeroTo59_1_carry), .C(C), .reset(Reset), .s(ZeroTo59_2_s), .carry(ZeroTo59_2_carry));
  ZeroTo59 ZeroTo59_3 (.prev(and_1_out), .C(C), .reset(Reset), .s(ZeroTo59_3_s));  // open: carry
endmodule

module ZeroTo59 (
  input  prev,
  input  C,
  input  reset,
  output [5:0] s,
  output carry
);

  wire [5:0] undriven;

  Counter #(.width(6), .max('h3b)) counter_1 (
    .clr(reset), .count(prev), .clk(C), .D(undriven), .carry(carry), .Q(s));  // open: load, up
endmodule

module ZeroTo99 (
  input  prev,
  input  C,
  output [6:0] s,
  output carry
);

  Counter #(.width(7), .max('h63)) counter_1 (.count(prev), .clk(C), .carry(carry), .Q(s));  // open: clr, load, up, D
endmodule

module TranLogic_Chrono (
  input  Q2,
  input  Q1,
  input  Start,
  input  Reset_Stop,
  output D2,
  output D1
);

  wire and_1_out, and_2_out, and_3_out, and_4_out, and_5_out, and_6_out, and_7_out, not_1_out, not_2_out,
       not_3_out, not_4_out, not_5_out, not_6_out, not_7_out, not_8_out, not_9_out, not_10_out, not_11_out,
       not_12_out;

  not not_1 (not_1_out, Q2);
  not not_2 (not_2_out, Start);
  not not_3 (not_3_out, Q1);
  not not_4 (not_4_out, Start);
  not not_5 (not_5_out, Q1);
  not not_6 (not_6_out, Q1);
  not not_7 (not_7_out, Reset_Stop);
  not not_8 (not_8_out, Q2);
  not not_9 (not_9_out, Reset_Stop);
  not not_10 (not_10_out, Q2);
  not not_11 (not_11_out, Q1);
  not not_12 (not_12_out, Start);
  and and_1 (and_1_out, not_1_out, Q1, not_2_out, Reset_Stop);
  and and_2 (and_2_out, Q2, not_3_out, not_4_out);
  and and_3 (and_3_out, Q2, not_5_out, Reset_Stop);
  and and_4 (and_4_out, not_6_out, Start, not_7_out);
  and and_5 (and_5_out, not_8_out, Q1, not_9_out);
  and and_6 (and_6_out, not_10_out, Q1, Start);
  and and_7 (and_7_out, Q2, not_11_out, not_12_out, Reset_Stop);
  or or_1 (D2, and_1_out, and_2_out, and_3_out);
  or or_2 (D1, and_4_out, and_5_out, and_6_out, and_7_out);
endmodule

module OutLogic_Chrono (
  input  D2,
  input  D1,
  output Run,
  output Reset
);

  wire not_1_out;

  not not_1 (not_1_out, D2);
  and and_1 (Run, not_1_out, D1);
  and and_2 (Reset, D2, D1);
endmodule
