// Logisim project additionneur.circ as structural Verilog
module Add1Bit (
  input  A,
  input  B,
  input  R,
  output R1,
  output AB
);

  wire and_1_out, and_2_out, and_3_out, and_4_out, and_5_out, and_6_out, and_7_out, not_1_out, not_2_out,
       not_3_out, not_4_out, not_5_out, not_6_out;

  and and_1 (and_1_out, B, R);
  and and_2 (and_2_out, A, R);
  and and_3 (and_3_out, A, B);
  not not_1 (not_1_out, A);
  not not_2 (not_2_out, B);
  not not_3 (not_3_out, A);
  not not_4 (not_4_out, R);
  not not_5 (not_5_out, B);
  not not_6 (not_6_out, R);
  or or_1 (R1, and_1_out, and_2_out, and_3_out);
  and and_4 (and_4_out, not_1_out, not_2_out, R);
  and and_5 (and_5_out, not_3_out, B, not_4_out);
  and and_6 (and_6_out, A, not_5_out, not_6_out);
  and and_7 (and_7_out, A, B, R);
  or or_2 (AB, and_4_out, and_5_out, and_6_out, and_7_out);
endmodule

module Add6Bit (
  input  b0,
  input  b1,
  input  b2,
  input  b3,
  input  b4,
  input  a0,
  input  b5,
  input  a1,
  input  a2,
  input  a3,
  input  a4,
  input  a5,
  output o,
  output s5,
  output s4,
  output s3,
  output s2,
  output s1,
  output s0
);

  wire add1bit_1_r1, add1bit_2_r1, add1bit_3_r1, add1bit_4_r1, add1bit_5_r1;

  Add1Bit add1bit_1 (.AB(s0), .R(1'b0), .A(a0), .B(b0), .R1(add1bit_1_r1));
  Add1Bit add1bit_2 (.AB(s1), .R(add1bit_1_r1), .A(a1), .B(b1), .R1(add1bit_2_r1));
  Add1Bit add1bit_3 (.AB(s2), .R(add1bit_2_r1), .A(a2), .B(b2), .R1(add1bit_3_r1));
  Add1Bit add1bit_4 (.AB(s3), .R(add1bit_3_r1), .A(a3), .B(b3), .R1(add1bit_4_r1));
  Add1Bit add1bit_5 (.AB(s4), .R(add1bit_4_r1), .A(a4), .B(b4), .R1(add1bit_5_r1));
  Add1Bit add1bit_6 (.AB(s5), .R(add1bit_5_r1), .A(a5), .B(b5), .R1(o));
endmodule

module AddAutomatique1Bit (
  input  Clock,
  output o,
  output s0,
  output s1,
  output s2,
  output s3,
  output s4,
  output s5
);

  wire add6bit_1_s0, add6bit_1_s1, add6bit_1_s2, add6bit_1_s3, add6bit_1_s4, add6bit_1_s5;

  Add6Bit add6bit_1 (
    .a2(s2), .b5(1'b0), .b4(1'b0), .b2(1'b0), .b0(1'b1), .b1(1'b0), .b3(1'b0), .a0(s0), .a1(s1), .a3(s3),
    .a4(s4), .a5(s5), .o(o), .s5(add6bit_1_s5), .s4(add6bit_1_s4), .s3(add6bit_1_s3), .s2(add6bit_1_s2),
    .s1(add6bit_1_s1), .s0(add6bit_1_s0));
  D_Flip_Flop d_ff_1 (.D(add6bit_1_s0), .clk(Clock), .Q(s0));  // open: Qn, preset, reset
  D_Flip_Flop d_ff_2 (.D(add6bit_1_s1), .clk(Clock), .Q(s1));  // open: Qn, preset, reset
  D_Flip_Flop d_ff_3 (.D(add6bit_1_s2), .clk(Clock), .Q(s2));  // open: Qn, preset, reset
  D_Flip_Flop d_ff_4 (.D(add6bit_1_s3), .clk(Clock), .Q(s3));  // open: Qn, preset, reset
  D_Flip_Flop d_ff_5 (.D(add6bit_1_s4), .clk(Clock), .Q(s4));  // open: Qn, preset, reset
  D_Flip_Flop d_ff_6 (.D(add6bit_1_s5), .clk(Clock), .Q(s5));  // open: Qn, preset, reset
endmodule
