// Logisim project SegLedControlAlphabet.circ as structural Verilog: 2 circuits, main circuit alphabet
module alphabet (
  input  e4,
  input  e3,
  input  e2,
  input  e1,
  input  e0,
  output s6,
  output s5,
  output s4,
  output s3,
  output s2,
  output s1,
  output s0
);

  wire and_1_out, and_2_out, and_3_out, and_4_out, and_5_out, and_6_out, and_7_out, and_8_out, and_9_out,
       and_10_out, and_11_out, and_12_out, and_13_out, and_14_out, and_15_out, and_16_out, and_17_out,
       and_18_out, and_19_out, and_20_out, and_21_out, and_22_out, and_23_out, and_24_out, and_25_out,
       and_26_out, and_27_out, and_28_out, and_29_out, and_30_out, and_31_out, and_32_out, and_33_out,
       and_34_out, and_35_out, and_36_out, and_37_out, and_38_out, and_39_out, and_40_out, and_41_out,
       and_42_out, and_43_out, and_44_out, and_45_out, and_46_out, and_47_out, not_1_out, not_2_out,
       not_3_out, not_4_out, not_5_out, not_6_out, not_7_out, not_8_out, not_9_out, not_10_out, not_11_out,
       not_12_out, not_13_out, not_14_out, not_15_out, not_16_out, not_17_out, not_18_out, not_19_out,
       not_20_out, not_21_out, not_22_out, not_23_out, not_24_out, not_25_out, not_26_out, not_27_out,
       not_28_out, not_29_out, not_30_out, not_31_out, not_32_out, not_33_out, not_34_out, not_35_out,
       not_36_out, not_37_out, not_38_out, not_39_out, not_40_out, not_41_out, not_42_out, not_43_out,
       not_44_out, not_45_out, not_46_out, not_47_out, not_48_out, not_49_out, not_50_out, not_51_out,
       not_52_out, not_53_out, not_54_out, not_55_out, not_56_out, not_57_out, not_58_out, not_59_out,
       not_60_out, not_61_out, not_62_out, not_63_out, not_64_out, not_65_out, not_66_out;

  not not_1 (not_1_out, e4);
  not not_2 (not_2_out, e3);
  not not_3 (not_3_out, e0);
  not not_4 (not_4_out, e4);
  not not_5 (not_5_out, e3);
  not not_6 (not_6_out, e1);
  not not_7 (not_7_out, e4);
  not not_8 (not_8_out, e0);
  not not_9 (not_9_out, e3);
  not not_10 (not_10_out, e1);
  not not_11 (not_11_out, e1);
  not not_12 (not_12_out, e4);
  not not_13 (not_13_out, e3);
  not not_14 (not_14_out, e2);
  not not_15 (not_15_out, e1);
  not not_16 (not_16_out, e0);
  not not_17 (not_17_out, e4);
  not not_18 (not_18_out, e2);
  not not_19 (not_19_out, e1);
  not not_20 (not_20_out, e4);
  not not_21 (not_21_out, e3);
  not not_22 (not_22_out, e2);
  not not_23 (not_23_out, e1);
  not not_24 (not_24_out, e2);
  not not_25 (not_25_out, e4);
  not not_26 (not_26_out, e3);
  not not_27 (not_27_out, e1);
  not not_28 (not_28_out, e1);
  not not_29 (not_29_out, e0);
  not not_30 (not_30_out, e3);
  not not_31 (not_31_out, e2);
  not not_32 (not_32_out, e2);
  not not_33 (not_33_out, e0);
  not not_34 (not_34_out, e3);
  not not_35 (not_35_out, e0);
  not not_36 (not_36_out, e1);
  not not_37 (not_37_out, e3);
  not not_38 (not_38_out, e2);
  not not_39 (not_39_out, e1);
  not not_40 (not_40_out, e4);
  not not_41 (not_41_out, e2);
  not not_42 (not_42_out, e4);
  not not_43 (not_43_out, e1);
  not not_44 (not_44_out, e2);
  not not_45 (not_45_out, e1);
  not not_46 (not_46_out, e0);
  not not_47 (not_47_out, e3);
  not not_48 (not_48_out, e3);
  not not_49 (not_49_out, e0);
  not not_50 (not_50_out, e3);
  not not_51 (not_51_out, e4);
  not not_52 (not_52_out, e3);
  not not_53 (not_53_out, e1);
  not not_54 (not_54_out, e4);
  not not_55 (not_55_out, e2);
  not not_56 (not_56_out, e0);
  not not_57 (not_57_out, e3);
  not not_58 (not_58_out, e0);
  not not_59 (not_59_out, e2);
  not not_60 (not_60_out, e3);
  not not_61 (not_61_out, e1);
  not not_62 (not_62_out, e4);
  not not_63 (not_63_out, e3);
  not not_64 (not_64_out, e0);
  not not_65 (not_65_out, e3);
  not not_66 (not_66_out, e0);
  and and_1 (and_1_out, not_1_out, not_2_out, not_3_out);
  and and_2 (and_2_out, not_4_out, not_5_out, e2, not_6_out);
  and and_3 (and_3_out, not_7_out, e2, e1, not_8_out);
  and and_4 (and_4_out, e3, e1, e0);
  and and_5 (and_5_out, e4, not_9_out, not_10_out, e0);
  and and_6 (and_6_out, e4, e2, not_11_out, e0);
  and and_7 (and_7_out, e4, e3, e1);
  and and_8 (and_8_out, not_12_out, not_13_out, not_14_out, not_15_out, not_16_out);
  and and_9 (and_9_out, e1, e0);
  and and_10 (and_10_out, not_17_out, e2, e1);
  and and_11 (and_11_out, e3, not_18_out, e0);
  and and_12 (and_12_out, e4, e2, not_19_out);
  and and_13 (and_13_out, e4, e3, e1);
  and and_14 (and_14_out, not_20_out, not_21_out, not_22_out, not_23_out);
  and and_15 (and_15_out, not_24_out, e0);
  and and_16 (and_16_out, e1, e0);
  and and_17 (and_17_out, not_25_out, not_26_out, e2, e1);
  and and_18 (and_18_out, e3, e2, not_27_out);
  and and_19 (and_19_out, e4, e2, not_28_out, not_29_out);
  and and_20 (and_20_out, e4, e3);
  and and_21 (and_21_out, not_30_out, not_31_out, e0);
  and and_22 (and_22_out, not_32_out, e1, not_33_out);
  and and_23 (and_23_out, not_34_out, e2, not_35_out);
  and and_24 (and_24_out, e3, not_36_out, e0);
  and and_25 (and_25_out, e4, not_37_out, e2);
  and and_26 (and_26_out, e4, e3, not_38_out, not_39_out);
  and and_27 (and_27_out, not_40_out, not_41_out);
  and and_28 (and_28_out, not_42_out, not_43_out);
  and and_29 (and_29_out, not_44_out, not_45_out, not_46_out);
  and and_30 (and_30_out, not_47_out, e1, e0);
  and and_31 (and_31_out, not_48_out, e2, e0);
  and and_32 (and_32_out, e3, e2, not_49_out);
  and and_33 (and_33_out, e4, not_50_out, e1);
  and and_34 (and_34_out, not_51_out, not_52_out, not_53_out);
  and and_35 (and_35_out, not_54_out, not_55_out, not_56_out);
  and and_36 (and_36_out, not_57_out, e2, not_58_out);
  and and_37 (and_37_out, e2, e1);
  and and_38 (and_38_out, e3, e1);
  and and_39 (and_39_out, e4, not_59_out, e0);
  and and_40 (and_40_out, e4, e1);
  and and_41 (and_41_out, e4, e3, e0);
  and and_42 (and_42_out, not_60_out, not_61_out);
  and and_43 (and_43_out, not_62_out, not_63_out, e0);
  and and_44 (and_44_out, e2, not_64_out);
  and and_45 (and_45_out, e3, e2);
  and and_46 (and_46_out, e4, not_65_out, not_66_out);
  and and_47 (and_47_out, e4, e3, e0);
  or or_1 (s6, and_1_out, and_2_out, and_3_out, and_4_out, and_5_out, and_6_out, and_7_out);
  or or_2 (s5, and_8_out, and_9_out, and_10_out, and_11_out, and_12_out, and_13_out);
  or or_3 (s4, and_14_out, and_15_out, and_16_out, and_17_out, and_18_out, and_19_out, and_20_out);
  or or_4 (s3, and_21_out, and_22_out, and_23_out, and_24_out, and_25_out, and_26_out);
  or or_5 (s2, and_27_out, and_28_out, and_29_out, and_30_out, and_31_out, and_32_out, and_33_out);
  or or_6 (s1, and_34_out, and_35_out, and_36_out, and_37_out, and_38_out, and_39_out, and_40_out, and_41_out);
  or or_7 (s0, and_42_out, and_43_out, and_44_out, and_45_out, and_46_out, and_47_out);
endmodule

module SegLedControlAlphabet (
  input  in_1,
  input  in_2,
  input  in_3,
  input  in_4,
  input  in_5
);

  wire alphabet_1_s0, alphabet_1_s1, alphabet_1_s2, alphabet_1_s3, alphabet_1_s4, alphabet_1_s5,
       alphabet_1_s6;

  alphabet alphabet_1 (
    .e4(in_1), .e3(in_2), .e2(in_3), .e1(in_4), .e0(in_5), .s6(alphabet_1_s6), .s5(alphabet_1_s5),
    .s4(alphabet_1_s4), .s3(alphabet_1_s3), .s2(alphabet_1_s2), .s1(alphabet_1_s1), .s0(alphabet_1_s0));
  _7_Segment_Display u_7_segment_display_1 (
    .g(alphabet_1_s0), .f(alphabet_1_s1), .a(alphabet_1_s6), .b(alphabet_1_s5), .e(alphabet_1_s2),
    .d(alphabet_1_s3), .c(alphabet_1_s4));  // open: dp
endmodule
