// Logisim project ALARM_v2.circ as structural Verilog: 6 circuits, main circuit FreqToNote
module ALARM (
  input  [7:0] Min1,
  input  Enable,
  input  [7:0] Min2,
  input  [7:0] Hour1,
  input  [7:0] Hour2,
  output OutNote
);

  wire clock_1_out;

  Clock clock_1 (.out(clock_1_out));
  SONG song_1 (.Enable(Enable), .clk(clock_1_out), .OutNote(OutNote));
endmodule

module SONG (
  input  Enable,
  input  clk,
  output OutNote
);

  wire d_ff_1_qn, ImperialMarch_1_c1, ImperialMarch_1_d2, ImperialMarch_1_e1, ImperialMarch_1_e2,
       ImperialMarch_1_g1, not_1_out, NoteControl_1_outnote;
  wire [7:0] BeatManager_1_beat, FreqToNote_1_count;

  BeatManager BeatManager_1 (.Start(Enable), .Clk(clk), .beat(BeatManager_1_beat));
  FreqToNote FreqToNote_1 (.count(FreqToNote_1_count), .reset(NoteControl_1_outnote));
  ImperialMarch ImperialMarch_1 (
    .beat(BeatManager_1_beat), .e2(ImperialMarch_1_e2), .d2(ImperialMarch_1_d2), .g1(ImperialMarch_1_g1),
    .e1(ImperialMarch_1_e1), .c1(ImperialMarch_1_c1));
  NoteControl NoteControl_1 (
    .count(FreqToNote_1_count), .c3(1'b0), .b2(1'b0), .a2(1'b0), .g2(1'b0), .e2(ImperialMarch_1_e2),
    .d2(ImperialMarch_1_d2), .c2(1'b0), .b1(1'b0), .a1(1'b0), .g1(ImperialMarch_1_g1),
    .e1(ImperialMarch_1_e1), .d1(1'b0), .c1(ImperialMarch_1_c1), .OutNote(NoteControl_1_outnote));
  D_Flip_Flop d_ff_1 (
    .D(d_ff_1_qn), .clk(NoteControl_1_outnote), .Q(OutNote), .Qn(d_ff_1_qn), .reset(not_1_out));  // open: preset
  not not_1 (not_1_out, Enable);
endmodule

module FreqToNote (
  input  reset,
  output [7:0] count
);

  wire clock_1_out;

  Clock clock_1 (.out(clock_1_out));
  Counter #(.width(6), .max('h3f)) counter_1 (
    .clr(reset), .count(1'b1), .clk(clock_1_out), .Q(count[5:0]));  // open: load, up, D, carry
endmodule

module NoteControl (
  input  [7:0] count,
  input  c3,
  input  b2,
  input  a2,
  input  g2,
  input  e2,
  input  d2,
  input  c2,
  input  b1,
  input  a1,
  input  g1,
  input  e1,
  input  d1,
  input  c1,
  output OutNote
);

  wire and_1_out, and_2_out, and_3_out, and_4_out, and_5_out, and_6_out, and_7_out, and_8_out, and_9_out,
       and_10_out, and_11_out, and_12_out, and_13_out;

  and and_1 (and_1_out, count[0], count[1], count[2], count[3], ~count[4], ~count[5], c3);  // AND_Gate
  and and_2 (and_2_out, ~count[0], ~count[1], ~count[2], ~count[3], count[4], ~count[5], b2);  // AND_Gate
  and and_3 (and_3_out, ~count[0], count[1], ~count[2], ~count[3], count[4], ~count[5], a2);  // AND_Gate
  and and_4 (and_4_out, ~count[0], ~count[1], count[2], ~count[3], count[4], ~count[5], g2);  // AND_Gate
  and and_5 (and_5_out, ~count[0], ~count[1], ~count[2], count[3], count[4], ~count[5], e2);  // AND_Gate
  and and_6 (and_6_out, count[0], count[1], ~count[2], count[3], count[4], ~count[5], d2);  // AND_Gate
  and and_7 (and_7_out, ~count[0], count[1], count[2], count[3], count[4], ~count[5], c2);  // AND_Gate
  and and_8 (and_8_out, ~count[0], ~count[1], ~count[2], ~count[3], ~count[4], count[5], b1);  // AND_Gate
  and and_9 (and_9_out, ~count[0], ~count[1], count[2], ~count[3], ~count[4], count[5], a1);  // AND_Gate
  and and_10 (and_10_out, ~count[0], ~count[1], ~count[2], count[3], ~count[4], count[5], g1);  // AND_Gate
  and and_11 (and_11_out, ~count[0], ~count[1], ~count[2], ~count[3], count[4], count[5], e1);  // AND_Gate
  and and_12 (and_12_out, ~count[0], count[1], count[2], ~count[3], count[4], count[5], d1);  // AND_Gate
  and and_13 (and_13_out, ~count[0], ~count[1], count[2], count[3], count[4], count[5], c1);  // AND_Gate
  or or_1 (OutNote, and_1_out, and_2_out, and_3_out, and_4_out, and_5_out, and_6_out, and_7_out, and_8_out, and_9_out, and_10_out, and_11_out, and_12_out, and_13_out);

  assign count[6] = count[7];
  // also tied to GND on the sheet: count[7]

  // Notes on the sheet:
  //   counter
endmodule

module ImperialMarch (
  input  [7:0] beat,
  output e2,
  output d2,
  output g1,
  output e1,
  output c1
);

  wire and_1_out, and_2_out, and_3_out, and_4_out, and_5_out, and_6_out, and_7_out, and_8_out, and_9_out,
       and_10_out, and_11_out, and_12_out, and_13_out, and_14_out, and_15_out, and_16_out, and_17_out,
       and_18_out, and_19_out, not_1_out, not_2_out, not_3_out, not_4_out, not_5_out, not_6_out, not_7_out,
       not_8_out, not_9_out, not_10_out, not_11_out, not_12_out, not_13_out, not_14_out, not_15_out,
       not_16_out, not_17_out, not_18_out, not_19_out, not_20_out, not_21_out, not_22_out, not_23_out,
       not_24_out, not_25_out, not_26_out, not_27_out, not_28_out, not_29_out, not_30_out, not_31_out,
       not_32_out, not_33_out, not_34_out, not_35_out, not_36_out, not_37_out, not_38_out, not_39_out,
       not_40_out, not_41_out, not_42_out, not_43_out, not_44_out, not_45_out, not_46_out;

  not not_1 (not_1_out, beat[5]);
  not not_2 (not_2_out, beat[4]);
  not not_3 (not_3_out, beat[1]);
  not not_4 (not_4_out, beat[5]);
  not not_5 (not_5_out, beat[4]);
  not not_6 (not_6_out, beat[0]);
  not not_7 (not_7_out, beat[3]);
  not not_8 (not_8_out, beat[1]);
  not not_9 (not_9_out, beat[3]);
  not not_10 (not_10_out, beat[0]);
  not not_11 (not_11_out, beat[5]);
  not not_12 (not_12_out, beat[4]);
  not not_13 (not_13_out, beat[3]);
  not not_14 (not_14_out, beat[1]);
  not not_15 (not_15_out, beat[5]);
  not not_16 (not_16_out, beat[4]);
  not not_17 (not_17_out, beat[3]);
  not not_18 (not_18_out, beat[0]);
  not not_19 (not_19_out, beat[5]);
  not not_20 (not_20_out, beat[2]);
  not not_21 (not_21_out, beat[1]);
  not not_22 (not_22_out, beat[5]);
  not not_23 (not_23_out, beat[2]);
  not not_24 (not_24_out, beat[0]);
  not not_25 (not_25_out, beat[2]);
  not not_26 (not_26_out, beat[1]);
  not not_27 (not_27_out, beat[0]);
  not not_28 (not_28_out, beat[2]);
  not not_29 (not_29_out, beat[4]);
  not not_30 (not_30_out, beat[3]);
  not not_31 (not_31_out, beat[4]);
  not not_32 (not_32_out, beat[3]);
  not not_33 (not_33_out, beat[1]);
  not not_34 (not_34_out, beat[4]);
  not not_35 (not_35_out, beat[3]);
  not not_36 (not_36_out, beat[0]);
  not not_37 (not_37_out, beat[4]);
  not not_38 (not_38_out, beat[2]);
  not not_39 (not_39_out, beat[1]);
  not not_40 (not_40_out, beat[4]);
  not not_41 (not_41_out, beat[2]);
  not not_42 (not_42_out, beat[0]);
  not not_43 (not_43_out, beat[4]);
  not not_44 (not_44_out, beat[1]);
  not not_45 (not_45_out, beat[4]);
  not not_46 (not_46_out, beat[0]);
  and and_1 (and_1_out, not_1_out, not_2_out, beat[3], beat[2], not_3_out);
  and and_2 (and_2_out, not_4_out, not_5_out, beat[3], beat[2], not_6_out);
  and and_3 (and_3_out, beat[4], not_7_out, beat[2], not_8_out);
  and and_4 (and_4_out, beat[4], not_9_out, beat[2], not_10_out);
  and and_5 (and_5_out, not_11_out, not_12_out, not_13_out, not_14_out);
  and and_6 (and_6_out, not_15_out, not_16_out, not_17_out, not_18_out);
  and and_7 (and_7_out, not_19_out, not_20_out, not_21_out);
  and and_8 (and_8_out, not_22_out, not_23_out, not_24_out);
  and and_9 (and_9_out, beat[4], beat[3], not_25_out);
  and and_10 (and_10_out, beat[4], beat[3], not_26_out, not_27_out);
  and and_11 (and_11_out, beat[5], beat[4], not_28_out);
  and and_12 (and_12_out, not_29_out, beat[3], beat[2], beat[1], beat[0]);
  and and_13 (and_13_out, beat[4], not_30_out, beat[2], beat[1], beat[0]);
  and and_14 (and_14_out, beat[5], not_31_out, not_32_out, not_33_out);
  and and_15 (and_15_out, beat[5], not_34_out, not_35_out, not_36_out);
  and and_16 (and_16_out, beat[5], not_37_out, not_38_out, not_39_out);
  and and_17 (and_17_out, beat[5], not_40_out, not_41_out, not_42_out);
  and and_18 (and_18_out, beat[5], not_43_out, beat[3], beat[2], not_44_out);
  and and_19 (and_19_out, beat[5], not_45_out, beat[3], beat[2], not_46_out);
  or or_1 (c1, and_1_out, and_2_out, and_3_out, and_4_out);
  or or_2 (e1, and_5_out, and_6_out, and_7_out, and_8_out, and_9_out, and_10_out, and_11_out);
  or or_3 (g1, and_12_out, and_13_out);
  or or_4 (d2, and_14_out, and_15_out, and_16_out, and_17_out);
  or or_5 (e2, and_18_out, and_19_out);

  assign beat[6] = beat[7];
  // also tied to GND on the sheet: beat[7]
endmodule

module BeatManager (
  input  Start,
  input  Clk,
  output [7:0] beat
);

  wire Double_croche_150ms_carry;

  Counter #(.width(12), .max('h9c4)) Double_croche_150ms (
    .count(Start), .clk(Clk), .carry(Double_croche_150ms_carry));  // open: clr, load, up, D, Q
  Counter #(.width(6), .max('h3f)) Mesure (
    .up(1'b1), .clk(Double_croche_150ms_carry), .Q(beat[5:0]));  // open: clr, load, count, D, carry

  assign beat[7:6] = 2'b00;
endmodule
