// Logisim project MUSIC.circ as structural Verilog: 8 circuits, main circuit SONG
module SONG (
  input  Enable,
  output Buzzer1
);

  wire clock_1_out, d_ff_1_qn, not_1_out, undriven, undriven_5, undriven_6;
  wire [7:0] BeatManager_1_beat, FreqToNote_1_count, undriven_2, undriven_3, undriven_4;

  Clock clock_1 (.out(clock_1_out));
  BeatManager BeatManager_1 (.Start(Enable), .Clk(clock_1_out), .Reset(undriven), .beat(BeatManager_1_beat));
  Multiplexer #(.select(2), .width(8), .enable("false")) multiplexer_1 (
    .in0(undriven_2), .in1(undriven_3), .in2(undriven_4), .out(BeatManager_1_beat));  // open: in3, sel
  FreqToNote FreqToNote_1 (.count(FreqToNote_1_count), .reset(undriven_5));
  ImperialMarch ImperialMarch_1 (
    .b0(undriven_2[7]), .b1(undriven_2[6]), .b2(undriven_2[5]), .b3(undriven_2[4]), .b4(undriven_2[3]),
    .b5(undriven_2[2]), .b6(undriven_2[1]), .b7(undriven_2[0]));  // open: c3, b_2, a2, g2, e2, d2, c2, out_16, b_1, a1, g1, e1, d1, c1, reset
  Kalinka Kalinka_1 (
    .b0(undriven_3[7]), .b1(undriven_3[6]), .b2(undriven_3[5]), .b3(undriven_3[4]), .b4(undriven_3[3]),
    .b5(undriven_3[2]), .b6(undriven_3[1]), .b7(undriven_3[0]));  // open: c3, b_2, a2, g2, e2, d2, c2, b_1, a1, g1, e1, d1, c1, reset
  PirateCaraibe PirateCaraibe_1 (
    .b0(undriven_4[7]), .b1(undriven_4[6]), .b2(undriven_4[5]), .b3(undriven_4[4]), .b4(undriven_4[3]),
    .b5(undriven_4[2]), .b6(undriven_4[1]), .b7(undriven_4[0]));  // open: c3, b_2, a2, g2, e2, d2, c2, b_1, a1, g1, e1, d1, c1, reset
  NoteControl NoteControl_1 ();  // open: count, c3, b2, a2, g2, e2, d2, c2, b1, a1, g1, e1, d1, c1, OutNote
  D_Flip_Flop d_ff_1 (.D(d_ff_1_qn), .clk(undriven_5), .Q(Buzzer1), .Qn(d_ff_1_qn), .reset(not_1_out));  // open: preset
  not not_1 (not_1_out, undriven_6);
endmodule

module FreqToNote (
  input  reset,
  output [7:0] count
);

  wire clock_1_out;

  Clock clock_1 (.out(clock_1_out));
  Counter #(.width(6), .max('h3f)) counter_1 (
    .clr(reset), .count(1'b1), .clk(clock_1_out), .Q(count[5:0]));  // open: load, up, D, carry
endmodule

module NoteControl (
  input  [7:0] count,
  input  c3,
  input  b2,
  input  a2,
  input  g2,
  input  e2,
  input  d2,
  input  c2,
  input  b1,
  input  a1,
  input  g1,
  input  e1,
  input  d1,
  input  c1,
  output OutNote
);

  wire and_1_out, and_2_out, and_3_out, and_4_out, and_5_out, and_6_out, and_7_out, and_8_out, and_9_out,
       and_10_out, and_11_out, and_12_out, and_13_out;

  and and_1 (and_1_out, count[0], count[1], count[2], count[3], ~count[4], ~count[5], c3);  // AND_Gate
  and and_2 (and_2_out, ~count[0], ~count[1], ~count[2], ~count[3], count[4], ~count[5], b2);  // AND_Gate
  and and_3 (and_3_out, ~count[0], count[1], ~count[2], ~count[3], count[4], ~count[5], a2);  // AND_Gate
  and and_4 (and_4_out, ~count[0], ~count[1], count[2], ~count[3], count[4], ~count[5], g2);  // AND_Gate
  and and_5 (and_5_out, ~count[0], ~count[1], ~count[2], count[3], count[4], ~count[5], e2);  // AND_Gate
  and and_6 (and_6_out, count[0], count[1], ~count[2], count[3], count[4], ~count[5], d2);  // AND_Gate
  and and_7 (and_7_out, ~count[0], count[1], count[2], count[3], count[4], ~count[5], c2);  // AND_Gate
  and and_8 (and_8_out, ~count[0], ~count[1], ~count[2], ~count[3], ~count[4], count[5], b1);  // AND_Gate
  and and_9 (and_9_out, ~count[0], ~count[1], count[2], ~count[3], ~count[4], count[5], a1);  // AND_Gate
  and and_10 (and_10_out, ~count[0], ~count[1], ~count[2], count[3], ~count[4], count[5], g1);  // AND_Gate
  and and_11 (and_11_out, ~count[0], ~count[1], ~count[2], ~count[3], count[4], count[5], e1);  // AND_Gate
  and and_12 (and_12_out, ~count[0], count[1], count[2], ~count[3], count[4], count[5], d1);  // AND_Gate
  and and_13 (and_13_out, ~count[0], ~count[1], count[2], count[3], count[4], count[5], c1);  // AND_Gate
  or or_1 (OutNote, and_1_out, and_2_out, and_3_out, and_4_out, and_5_out, and_6_out, and_7_out, and_8_out, and_9_out, and_10_out, and_11_out, and_12_out, and_13_out);

  assign count[6] = count[7];
  // also tied to GND on the sheet: count[7]

  // Notes on the sheet:
  //   counter
endmodule

module BeatManager (
  input  Start,
  input  Clk,
  input  Reset,
  output [7:0] beat
);

  wire Double_croche_150ms_carry;

  Counter #(.width(12), .max('h9c4)) Double_croche_150ms (
    .clr(Reset), .count(Start), .clk(Clk), .carry(Double_croche_150ms_carry));  // open: load, up, D, Q
  Counter Mesure (
    .clr(Reset), .up(1'b1), .count(1'b1), .clk(Double_croche_150ms_carry), .Q(beat));  // open: load, D, carry
endmodule

module TEST (
  output Output_1,
  output Buzzer0
);

  wire Button_1_out;

  Button Button_1 (.out(Button_1_out));
  Clock clock_1 ();  // open: out
  SONG SONG_1 (.Enable(Button_1_out), .Buzzer1(Output_1));

  assign Buzzer0 = 1'b0;
endmodule

module ImperialMarch (
  input  b0,
  input  b1,
  input  b2,
  input  b3,
  input  b4,
  input  b5,
  input  b6,
  input  b7,
  output c3,
  output b_2,
  output a2,
  output g2,
  output e2,
  output d2,
  output c2,
  output [12:0] out_16,
  output b_1,
  output a1,
  output g1,
  output e1,
  output d1,
  output c1,
  output reset
);

  wire and_1_out, and_2_out, and_3_out, and_4_out, and_5_out, and_6_out, and_7_out, and_8_out, and_9_out,
       and_10_out, and_11_out, and_12_out, and_13_out, and_14_out, and_15_out, and_16_out, and_17_out,
       and_18_out, and_19_out, and_20_out, and_21_out, and_22_out, and_23_out, and_24_out, and_25_out,
       and_26_out, and_27_out, and_28_out, and_29_out, and_30_out, and_31_out, and_32_out, and_33_out,
       and_34_out, and_35_out, and_36_out, and_37_out, and_38_out, and_39_out, and_40_out, and_41_out,
       not_1_out, not_2_out, not_3_out, not_4_out, not_5_out, not_6_out, not_7_out, not_8_out, not_9_out,
       not_10_out, not_11_out, not_12_out, not_13_out, not_14_out, not_15_out, not_16_out, not_17_out,
       not_18_out, not_19_out, not_20_out, not_21_out, not_22_out, not_23_out, not_24_out, not_25_out,
       not_26_out, not_27_out, not_28_out, not_29_out, not_30_out, not_31_out, not_32_out, not_33_out,
       not_34_out, not_35_out, not_36_out, not_37_out, not_38_out, not_39_out, not_40_out, not_41_out,
       not_42_out, not_43_out, not_44_out, not_45_out, not_46_out, not_47_out, not_48_out, not_49_out,
       not_50_out, not_51_out, not_52_out, not_53_out, not_54_out, not_55_out, not_56_out, not_57_out,
       not_58_out, not_59_out, not_60_out, not_61_out, not_62_out, not_63_out, not_64_out, not_65_out,
       not_66_out, not_67_out, not_68_out, not_69_out, not_70_out, not_71_out, not_72_out, not_73_out,
       not_74_out, not_75_out, not_76_out, not_77_out, not_78_out, not_79_out, not_80_out, not_81_out,
       not_82_out, not_83_out, not_84_out, not_85_out, not_86_out, not_87_out, not_88_out, not_89_out,
       not_90_out, not_91_out, not_92_out, not_93_out, not_94_out, not_95_out, not_96_out, not_97_out,
       not_98_out, not_99_out, not_100_out, not_101_out, not_102_out, not_103_out, not_104_out, not_105_out,
       not_106_out, not_107_out, not_108_out, not_109_out, not_110_out, not_111_out, not_112_out,
       not_113_out, not_114_out, not_115_out, not_116_out, not_117_out, not_118_out, not_119_out,
       not_120_out, not_121_out, not_122_out, not_123_out, not_124_out, not_125_out, not_126_out,
       not_127_out, not_128_out, not_129_out, not_130_out, not_131_out, not_132_out, not_133_out,
       not_134_out, not_135_out, not_136_out, not_137_out, not_138_out, not_139_out;

  not not_1 (not_1_out, b0);
  not not_2 (not_2_out, b1);
  not not_3 (not_3_out, b3);
  not not_4 (not_4_out, b6);
  not not_5 (not_5_out, b0);
  not not_6 (not_6_out, b1);
  not not_7 (not_7_out, b3);
  not not_8 (not_8_out, b7);
  not not_9 (not_9_out, b0);
  not not_10 (not_10_out, b4);
  not not_11 (not_11_out, b1);
  not not_12 (not_12_out, b4);
  not not_13 (not_13_out, b0);
  not not_14 (not_14_out, b1);
  not not_15 (not_15_out, b3);
  not not_16 (not_16_out, b4);
  not not_17 (not_17_out, b6);
  not not_18 (not_18_out, b0);
  not not_19 (not_19_out, b1);
  not not_20 (not_20_out, b3);
  not not_21 (not_21_out, b4);
  not not_22 (not_22_out, b7);
  not not_23 (not_23_out, b0);
  not not_24 (not_24_out, b1);
  not not_25 (not_25_out, b3);
  not not_26 (not_26_out, b5);
  not not_27 (not_27_out, b6);
  not not_28 (not_28_out, b0);
  not not_29 (not_29_out, b1);
  not not_30 (not_30_out, b3);
  not not_31 (not_31_out, b5);
  not not_32 (not_32_out, b7);
  not not_33 (not_33_out, b0);
  not not_34 (not_34_out, b2);
  not not_35 (not_35_out, b4);
  not not_36 (not_36_out, b0);
  not not_37 (not_37_out, b3);
  not not_38 (not_38_out, b4);
  not not_39 (not_39_out, b1);
  not not_40 (not_40_out, b2);
  not not_41 (not_41_out, b4);
  not not_42 (not_42_out, b1);
  not not_43 (not_43_out, b3);
  not not_44 (not_44_out, b4);
  not not_45 (not_45_out, b0);
  not not_46 (not_46_out, b1);
  not not_47 (not_47_out, b3);
  not not_48 (not_48_out, b0);
  not not_49 (not_49_out, b1);
  not not_50 (not_50_out, b4);
  not not_51 (not_51_out, b3);
  not not_52 (not_52_out, b4);
  not not_53 (not_53_out, b0);
  not not_54 (not_54_out, b1);
  not not_55 (not_55_out, b2);
  not not_56 (not_56_out, b3);
  not not_57 (not_57_out, b4);
  not not_58 (not_58_out, b6);
  not not_59 (not_59_out, b0);
  not not_60 (not_60_out, b1);
  not not_61 (not_61_out, b2);
  not not_62 (not_62_out, b3);
  not not_63 (not_63_out, b4);
  not not_64 (not_64_out, b7);
  not not_65 (not_65_out, b1);
  not not_66 (not_66_out, b2);
  not not_67 (not_67_out, b5);
  not not_68 (not_68_out, b6);
  not not_69 (not_69_out, b0);
  not not_70 (not_70_out, b2);
  not not_71 (not_71_out, b5);
  not not_72 (not_72_out, b7);
  not not_73 (not_73_out, b0);
  not not_74 (not_74_out, b1);
  not not_75 (not_75_out, b5);
  not not_76 (not_76_out, b6);
  not not_77 (not_77_out, b0);
  not not_78 (not_78_out, b1);
  not not_79 (not_79_out, b5);
  not not_80 (not_80_out, b7);
  not not_81 (not_81_out, b0);
  not not_82 (not_82_out, b2);
  not not_83 (not_83_out, b5);
  not not_84 (not_84_out, b6);
  not not_85 (not_85_out, b0);
  not not_86 (not_86_out, b1);
  not not_87 (not_87_out, b5);
  not not_88 (not_88_out, b0);
  not not_89 (not_89_out, b1);
  not not_90 (not_90_out, b6);
  not not_91 (not_91_out, b2);
  not not_92 (not_92_out, b5);
  not not_93 (not_93_out, b2);
  not not_94 (not_94_out, b7);
  not not_95 (not_95_out, b0);
  not not_96 (not_96_out, b2);
  not not_97 (not_97_out, b5);
  not not_98 (not_98_out, b0);
  not not_99 (not_99_out, b2);
  not not_100 (not_100_out, b0);
  not not_101 (not_101_out, b3);
  not not_102 (not_102_out, b4);
  not not_103 (not_103_out, b5);
  not not_104 (not_104_out, b1);
  not not_105 (not_105_out, b2);
  not not_106 (not_106_out, b5);
  not not_107 (not_107_out, b1);
  not not_108 (not_108_out, b3);
  not not_109 (not_109_out, b4);
  not not_110 (not_110_out, b5);
  not not_111 (not_111_out, b2);
  not not_112 (not_112_out, b0);
  not not_113 (not_113_out, b1);
  not not_114 (not_114_out, b2);
  not not_115 (not_115_out, b3);
  not not_116 (not_116_out, b6);
  not not_117 (not_117_out, b0);
  not not_118 (not_118_out, b1);
  not not_119 (not_119_out, b2);
  not not_120 (not_120_out, b3);
  not not_121 (not_121_out, b7);
  not not_122 (not_122_out, b0);
  not not_123 (not_123_out, b1);
  not not_124 (not_124_out, b4);
  not not_125 (not_125_out, b6);
  not not_126 (not_126_out, b0);
  not not_127 (not_127_out, b1);
  not not_128 (not_128_out, b4);
  not not_129 (not_129_out, b7);
  not not_130 (not_130_out, b0);
  not not_131 (not_131_out, b3);
  not not_132 (not_132_out, b0);
  not not_133 (not_133_out, b4);
  not not_134 (not_134_out, b5);
  not not_135 (not_135_out, b1);
  not not_136 (not_136_out, b3);
  not not_137 (not_137_out, b1);
  not not_138 (not_138_out, b4);
  not not_139 (not_139_out, b5);
  and and_1 (and_1_out, not_1_out, not_2_out, b2, not_3_out, b4, b5, not_4_out);
  and and_2 (and_2_out, not_5_out, not_6_out, b2, not_7_out, b4, b5, not_8_out);
  and and_3 (and_3_out, not_9_out, b1, b2, b3, not_10_out, b5);
  and and_4 (and_4_out, b0, not_11_out, b2, b3, not_12_out, b5);
  and and_5 (and_5_out, not_13_out, not_14_out, b2, not_15_out, not_16_out, not_17_out);
  and and_6 (and_6_out, not_18_out, not_19_out, b2, not_20_out, not_21_out, not_22_out);
  and and_7 (and_7_out, not_23_out, not_24_out, b2, not_25_out, not_26_out, not_27_out);
  and and_8 (and_8_out, not_28_out, not_29_out, b2, not_30_out, not_31_out, not_32_out);
  and and_9 (and_9_out, not_33_out, b1, not_34_out, not_35_out, b5);
  and and_10 (and_10_out, not_36_out, b1, not_37_out, not_38_out, b5);
  and and_11 (and_11_out, b0, not_39_out, not_40_out, not_41_out, b5);
  and and_12 (and_12_out, b0, not_42_out, not_43_out, not_44_out, b5);
  and and_13 (and_13_out, not_45_out, not_46_out, not_47_out, b4, b5, b6, b7);
  and and_14 (and_14_out, not_48_out, not_49_out, b3, not_50_out, b5, b6, b7);
  and and_15 (and_15_out, b0, b1, b2, not_51_out, b4);
  and and_16 (and_16_out, b0, b1, b2, b3, not_52_out);
  and and_17 (and_17_out, not_53_out, not_54_out, not_55_out, not_56_out, not_57_out, not_58_out);
  and and_18 (and_18_out, not_59_out, not_60_out, not_61_out, not_62_out, not_63_out, not_64_out);
  and and_19 (and_19_out, not_65_out, not_66_out, not_67_out, not_68_out);
  and and_20 (and_20_out, not_69_out, not_70_out, not_71_out, b6, not_72_out);
  and and_21 (and_21_out, not_73_out, not_74_out, b3, not_75_out, not_76_out);
  and and_22 (and_22_out, not_77_out, not_78_out, b3, not_79_out, not_80_out);
  and and_23 (and_23_out, not_81_out, not_82_out, b3, not_83_out, not_84_out);
  and and_24 (and_24_out, not_85_out, not_86_out, b3, b4, not_87_out);
  and and_25 (and_25_out, not_88_out, not_89_out, b3, b4, not_90_out);
  and and_26 (and_26_out, not_91_out, b3, b4, not_92_out);
  and and_27 (and_27_out, not_93_out, b3, b4, not_94_out);
  and and_28 (and_28_out, not_95_out, b1, not_96_out, not_97_out, b7);
  and and_29 (and_29_out, not_98_out, b1, not_99_out, b4);
  and and_30 (and_30_out, not_100_out, b1, b2, not_101_out, not_102_out, not_103_out);
  and and_31 (and_31_out, b0, not_104_out, not_105_out, not_106_out);
  and and_32 (and_32_out, b0, not_107_out, not_108_out, not_109_out, not_110_out);
  and and_33 (and_33_out, b0, not_111_out, b4, b5);
  and and_34 (and_34_out, not_112_out, not_113_out, not_114_out, not_115_out, b4, b5, not_116_out);
  and and_35 (and_35_out, not_117_out, not_118_out, not_119_out, not_120_out, b4, b5, not_121_out);
  and and_36 (and_36_out, not_122_out, not_123_out, b3, not_124_out, b5, not_125_out);
  and and_37 (and_37_out, not_126_out, not_127_out, b3, not_128_out, b5, not_129_out);
  and and_38 (and_38_out, not_130_out, b1, b2, not_131_out, b4);
  and and_39 (and_39_out, not_132_out, b1, b2, b3, not_133_out, not_134_out);
  and and_40 (and_40_out, b0, not_135_out, b2, not_136_out, b4);
  and and_41 (and_41_out, b0, not_137_out, b2, b3, not_138_out, not_139_out);
  or or_1 (e2, and_1_out, and_2_out, and_3_out, and_4_out);
  or or_2 (g1, and_13_out, and_14_out, and_15_out, and_16_out);
  or or_3 (d2, and_5_out, and_6_out, and_7_out, and_8_out, and_9_out, and_10_out, and_11_out, and_12_out);
  or or_4 (e1, and_17_out, and_18_out, and_19_out, and_20_out, and_21_out, and_22_out, and_23_out, and_24_out, and_25_out, and_26_out, and_27_out, and_28_out, and_29_out, and_30_out, and_31_out, and_32_out, and_33_out);
  or or_5 (c1, and_34_out, and_35_out, and_36_out, and_37_out, and_38_out, and_39_out, and_40_out, and_41_out);

  assign a1 = 1'b0;
  assign a2 = 1'b0;
  assign b_1 = 1'b0;
  assign b_2 = 1'b0;
  assign c2 = 1'b0;
  assign c3 = 1'b0;
  assign d1 = 1'b0;
  assign g2 = 1'b0;
  assign reset = b1;
endmodule

module Kalinka (
  input  b0,
  input  b1,
  input  b2,
  input  b3,
  input  b4,
  input  b5,
  input  b6,
  input  b7,
  output c3,
  output b_2,
  output a2,
  output g2,
  output e2,
  output d2,
  output c2,
  output b_1,
  output a1,
  output g1,
  output e1,
  output d1,
  output c1,
  output reset
);

  wire and_2_out, and_3_out, and_4_out, and_5_out, and_6_out, and_7_out, and_8_out, and_9_out, and_10_out,
       and_11_out, and_12_out, and_13_out, and_14_out, and_15_out, and_16_out, and_17_out, and_18_out,
       and_19_out, and_20_out, and_21_out, and_22_out, and_23_out, and_24_out, and_25_out, and_26_out,
       and_27_out, and_28_out, and_29_out, not_1_out, not_2_out, not_3_out, not_4_out, not_5_out, not_6_out,
       not_7_out, not_8_out, not_9_out, not_10_out, not_11_out, not_12_out, not_13_out, not_14_out,
       not_15_out, not_16_out, not_17_out, not_18_out, not_19_out, not_20_out, not_21_out, not_22_out,
       not_23_out, not_24_out, not_25_out, not_26_out, not_27_out, not_28_out, not_29_out, not_30_out,
       not_31_out, not_32_out, not_33_out, not_34_out, not_35_out, not_36_out, not_37_out, not_38_out,
       not_39_out, not_40_out, not_41_out, not_42_out, not_43_out, not_44_out, not_45_out, not_46_out,
       not_47_out, not_48_out, not_49_out, not_50_out, not_51_out, not_52_out, not_53_out, not_54_out,
       not_55_out, not_56_out, not_57_out, not_58_out, not_59_out, not_60_out;

  not not_1 (not_1_out, b2);
  not not_2 (not_2_out, b3);
  not not_3 (not_3_out, b4);
  not not_4 (not_4_out, b3);
  not not_5 (not_5_out, b5);
  not not_6 (not_6_out, b1);
  not not_7 (not_7_out, b2);
  not not_8 (not_8_out, b3);
  not not_9 (not_9_out, b5);
  not not_10 (not_10_out, b5);
  not not_11 (not_11_out, b1);
  not not_12 (not_12_out, b2);
  not not_13 (not_13_out, b5);
  not not_14 (not_14_out, b1);
  not not_15 (not_15_out, b3);
  not not_16 (not_16_out, b5);
  not not_17 (not_17_out, b1);
  not not_18 (not_18_out, b6);
  not not_19 (not_19_out, b3);
  not not_20 (not_20_out, b4);
  not not_21 (not_21_out, b1);
  not not_22 (not_22_out, b2);
  not not_23 (not_23_out, b3);
  not not_24 (not_24_out, b4);
  not not_25 (not_25_out, b1);
  not not_26 (not_26_out, b2);
  not not_27 (not_27_out, b1);
  not not_28 (not_28_out, b3);
  not not_29 (not_29_out, b1);
  not not_30 (not_30_out, b5);
  not not_31 (not_31_out, b3);
  not not_32 (not_32_out, b4);
  not not_33 (not_33_out, b6);
  not not_34 (not_34_out, b1);
  not not_35 (not_35_out, b2);
  not not_36 (not_36_out, b3);
  not not_37 (not_37_out, b4);
  not not_38 (not_38_out, b6);
  not not_39 (not_39_out, b5);
  not not_40 (not_40_out, b4);
  not not_41 (not_41_out, b6);
  not not_42 (not_42_out, b1);
  not not_43 (not_43_out, b4);
  not not_44 (not_44_out, b1);
  not not_45 (not_45_out, b4);
  not not_46 (not_46_out, b4);
  not not_47 (not_47_out, b5);
  not not_48 (not_48_out, b5);
  not not_49 (not_49_out, b1);
  not not_50 (not_50_out, b4);
  not not_51 (not_51_out, b5);
  not not_52 (not_52_out, b0);
  not not_53 (not_53_out, b1);
  not not_54 (not_54_out, b2);
  not not_55 (not_55_out, b3);
  not not_56 (not_56_out, b2);
  not not_57 (not_57_out, b3);
  not not_58 (not_58_out, b2);
  not not_59 (not_59_out, b3);
  not not_60 (not_60_out, b3);
  and and_1 (reset, b0, b4, b5);
  and and_2 (and_2_out, b1, not_1_out, not_2_out, not_3_out);
  and and_3 (and_3_out, b1, b2, not_4_out, b4, not_5_out);
  and and_4 (and_4_out, b0, not_6_out, not_7_out, not_8_out, b4, not_9_out);
  and and_5 (and_5_out, b0, b1, b2, b4, not_10_out);
  and and_6 (and_6_out, not_11_out, not_12_out, b3, b4, not_13_out);
  and and_7 (and_7_out, not_14_out, b2, not_15_out, b4, not_16_out);
  and and_8 (and_8_out, not_17_out, b2, b3, b4, b5);
  and and_9 (and_9_out, b1, b3, b5, not_18_out);
  and and_10 (and_10_out, b1, b2, not_19_out, not_20_out, b5, b6);
  and and_11 (and_11_out, b0, not_21_out, not_22_out, not_23_out, not_24_out, b5, b6);
  and and_12 (and_12_out, b0, b1, b2, b3, b5);
  and and_13 (and_13_out, not_25_out, not_26_out, b3, b4, b5);
  and and_14 (and_14_out, not_27_out, b2, not_28_out, b4, b5);
  and and_15 (and_15_out, not_29_out, b2, b3, b4, not_30_out);
  and and_16 (and_16_out, b1, b3, b5, b6);
  and and_17 (and_17_out, b1, b2, not_31_out, not_32_out, b5, not_33_out);
  and and_18 (and_18_out, b0, not_34_out, not_35_out, not_36_out, not_37_out, b5, not_38_out);
  and and_19 (and_19_out, b0, b2, b3, b4, not_39_out);
  and and_20 (and_20_out, b0, b1, b2, not_40_out, b5, not_41_out);
  and and_21 (and_21_out, not_42_out, b3, not_43_out);
  and and_22 (and_22_out, not_44_out, b2, not_45_out);
  and and_23 (and_23_out, b2, not_46_out, not_47_out);
  and and_24 (and_24_out, b1, b3, not_48_out);
  and and_25 (and_25_out, b0, not_49_out, not_50_out, not_51_out);
  and and_26 (and_26_out, not_52_out, not_53_out, not_54_out, not_55_out);
  and and_27 (and_27_out, not_56_out, not_57_out, b4, b5, b6);
  and and_28 (and_28_out, b1, not_58_out, not_59_out, b4);
  and and_29 (and_29_out, b1, not_60_out, b4, b5);
  or or_1 (a1, and_2_out, and_3_out, and_4_out, and_5_out);
  or or_2 (b_1, and_6_out, and_7_out, and_8_out, and_9_out, and_10_out, and_11_out, and_12_out);
  or or_3 (c2, and_13_out, and_14_out, and_15_out, and_16_out, and_17_out, and_18_out, and_19_out, and_20_out);
  or or_4 (d2, and_21_out, and_22_out, and_23_out, and_24_out, and_25_out);
  or or_5 (e2, and_26_out, and_27_out, and_28_out, and_29_out);

  assign a2 = 1'b0;
  assign b_2 = 1'b0;
  assign c1 = 1'b0;
  assign c3 = 1'b0;
  assign d1 = 1'b0;
  assign e1 = 1'b0;
  assign g1 = 1'b0;
  assign g2 = 1'b0;
endmodule

module PirateCaraibe (
  input  b0,
  input  b1,
  input  b2,
  input  b3,
  input  b4,
  input  b5,
  input  b6,
  input  b7,
  output c3,
  output b_2,
  output a2,
  output g2,
  output e2,
  output d2,
  output c2,
  output b_1,
  output a1,
  output g1,
  output e1,
  output d1,
  output c1,
  output reset
);

  wire and_2_out, and_3_out, and_4_out, and_5_out, and_6_out, and_7_out, and_8_out, and_9_out, and_10_out,
       and_11_out, and_12_out, and_13_out, and_14_out, and_15_out, and_16_out, and_17_out, and_18_out,
       and_19_out, and_20_out, and_21_out, and_22_out, and_23_out, and_24_out, and_25_out, and_26_out,
       and_27_out, and_28_out, and_29_out, and_30_out, and_31_out, and_32_out, and_33_out, and_34_out,
       and_35_out, and_36_out, not_1_out, not_2_out, not_3_out, not_4_out, not_5_out, not_6_out, not_7_out,
       not_8_out, not_9_out, not_10_out, not_11_out, not_12_out, not_13_out, not_14_out, not_15_out,
       not_16_out, not_17_out, not_18_out, not_19_out, not_20_out, not_21_out, not_22_out, not_23_out,
       not_24_out, not_25_out, not_26_out, not_27_out, not_28_out, not_29_out, not_30_out, not_31_out,
       not_32_out, not_33_out, not_34_out, not_35_out, not_36_out, not_37_out, not_38_out, not_39_out,
       not_40_out, not_41_out, not_42_out, not_43_out, not_44_out, not_45_out, not_46_out, not_47_out,
       not_48_out, not_49_out, not_50_out, not_51_out, not_52_out, not_53_out, not_54_out, not_55_out,
       not_56_out, not_57_out, not_58_out, not_59_out, not_60_out, not_61_out, not_62_out, not_63_out,
       not_64_out, not_65_out, not_66_out, not_67_out, not_68_out, not_69_out, not_70_out, not_71_out,
       not_72_out, not_73_out, not_74_out, not_75_out, not_76_out, not_77_out, not_78_out, not_79_out,
       not_80_out, not_81_out, not_82_out, not_83_out, not_84_out, not_85_out, not_86_out, not_87_out,
       not_88_out, not_89_out, not_90_out, not_91_out, not_92_out, not_93_out;

  not not_1 (not_1_out, b1);
  not not_2 (not_2_out, b2);
  not not_3 (not_3_out, b3);
  not not_4 (not_4_out, b5);
  not not_5 (not_5_out, b6);
  not not_6 (not_6_out, b7);
  not not_7 (not_7_out, b4);
  not not_8 (not_8_out, b6);
  not not_9 (not_9_out, b1);
  not not_10 (not_10_out, b2);
  not not_11 (not_11_out, b3);
  not not_12 (not_12_out, b5);
  not not_13 (not_13_out, b7);
  not not_14 (not_14_out, b3);
  not not_15 (not_15_out, b4);
  not not_16 (not_16_out, b5);
  not not_17 (not_17_out, b6);
  not not_18 (not_18_out, b1);
  not not_19 (not_19_out, b2);
  not not_20 (not_20_out, b4);
  not not_21 (not_21_out, b5);
  not not_22 (not_22_out, b6);
  not not_23 (not_23_out, b1);
  not not_24 (not_24_out, b2);
  not not_25 (not_25_out, b4);
  not not_26 (not_26_out, b5);
  not not_27 (not_27_out, b7);
  not not_28 (not_28_out, b1);
  not not_29 (not_29_out, b2);
  not not_30 (not_30_out, b4);
  not not_31 (not_31_out, b6);
  not not_32 (not_32_out, b7);
  not not_33 (not_33_out, b2);
  not not_34 (not_34_out, b3);
  not not_35 (not_35_out, b4);
  not not_36 (not_36_out, b5);
  not not_37 (not_37_out, b6);
  not not_38 (not_38_out, b1);
  not not_39 (not_39_out, b2);
  not not_40 (not_40_out, b3);
  not not_41 (not_41_out, b7);
  not not_42 (not_42_out, b1);
  not not_43 (not_43_out, b2);
  not not_44 (not_44_out, b3);
  not not_45 (not_45_out, b6);
  not not_46 (not_46_out, b2);
  not not_47 (not_47_out, b4);
  not not_48 (not_48_out, b7);
  not not_49 (not_49_out, b1);
  not not_50 (not_50_out, b3);
  not not_51 (not_51_out, b4);
  not not_52 (not_52_out, b1);
  not not_53 (not_53_out, b3);
  not not_54 (not_54_out, b4);
  not not_55 (not_55_out, b6);
  not not_56 (not_56_out, b3);
  not not_57 (not_57_out, b5);
  not not_58 (not_58_out, b6);
  not not_59 (not_59_out, b3);
  not not_60 (not_60_out, b5);
  not not_61 (not_61_out, b4);
  not not_62 (not_62_out, b5);
  not not_63 (not_63_out, b6);
  not not_64 (not_64_out, b2);
  not not_65 (not_65_out, b4);
  not not_66 (not_66_out, b5);
  not not_67 (not_67_out, b4);
  not not_68 (not_68_out, b5);
  not not_69 (not_69_out, b6);
  not not_70 (not_70_out, b4);
  not not_71 (not_71_out, b1);
  not not_72 (not_72_out, b2);
  not not_73 (not_73_out, b1);
  not not_74 (not_74_out, b2);
  not not_75 (not_75_out, b6);
  not not_76 (not_76_out, b1);
  not not_77 (not_77_out, b2);
  not not_78 (not_78_out, b2);
  not not_79 (not_79_out, b3);
  not not_80 (not_80_out, b4);
  not not_81 (not_81_out, b2);
  not not_82 (not_82_out, b3);
  not not_83 (not_83_out, b4);
  not not_84 (not_84_out, b3);
  not not_85 (not_85_out, b6);
  not not_86 (not_86_out, b3);
  not not_87 (not_87_out, b5);
  not not_88 (not_88_out, b1);
  not not_89 (not_89_out, b3);
  not not_90 (not_90_out, b4);
  not not_91 (not_91_out, b5);
  not not_92 (not_92_out, b6);
  not not_93 (not_93_out, b3);
  and and_1 (reset, b1, b2, b5, b6, b7);
  and and_2 (and_2_out, not_1_out, not_2_out, not_3_out, b4, not_4_out, not_5_out, not_6_out);
  and and_3 (and_3_out, b2, b3, not_7_out, b5, not_8_out, b7);
  and and_4 (and_4_out, not_9_out, not_10_out, not_11_out, b4, not_12_out, b6, not_13_out);
  and and_5 (and_5_out, b2, not_14_out, b4, b5, b7);
  and and_6 (and_6_out, b2, b3, not_15_out, b5, b6, b7);
  and and_7 (and_7_out, b1, b3, b4, not_16_out, b6, b7);
  and and_8 (and_8_out, b1, b3, b4, b5, not_17_out, b7);
  and and_9 (and_9_out, not_18_out, not_19_out, not_20_out, not_21_out, not_22_out);
  and and_10 (and_10_out, not_23_out, not_24_out, not_25_out, not_26_out, not_27_out);
  and and_11 (and_11_out, not_28_out, not_29_out, not_30_out, not_31_out, not_32_out);
  and and_12 (and_12_out, not_33_out, not_34_out, not_35_out, not_36_out, not_37_out, b7);
  and and_13 (and_13_out, not_38_out, not_39_out, not_40_out, b5, not_41_out);
  and and_14 (and_14_out, not_42_out, not_43_out, not_44_out, b4, b5, not_45_out);
  and and_15 (and_15_out, b2, b3, b4, b7);
  and and_16 (and_16_out, b2, b3, b4, b6);
  and and_17 (and_17_out, b1, b3, b4, b5, b6, b7);
  and and_18 (and_18_out, not_46_out, b3, not_47_out, b5, b6, not_48_out);
  and and_19 (and_19_out, not_49_out, b2, not_50_out, not_51_out, b6, b7);
  and and_20 (and_20_out, not_52_out, b2, not_53_out, not_54_out, b5, not_55_out);
  and and_21 (and_21_out, b2, not_56_out, b4, not_57_out, not_58_out);
  and and_22 (and_22_out, b2, not_59_out, b4, not_60_out, b7);
  and and_23 (and_23_out, b2, b3, not_61_out, not_62_out, not_63_out, b7);
  and and_24 (and_24_out, b1, not_64_out, not_65_out, not_66_out, b6, b7);
  and and_25 (and_25_out, b1, b3, not_67_out, b7);
  and and_26 (and_26_out, b1, b3, not_68_out, not_69_out, b7);
  and and_27 (and_27_out, b1, b3, not_70_out, b6);
  and and_28 (and_28_out, not_71_out, not_72_out, b3, b5, b6, b7);
  and and_29 (and_29_out, not_73_out, not_74_out, b3, b4, not_75_out);
  and and_30 (and_30_out, not_76_out, not_77_out, b3, b4, b7);
  and and_31 (and_31_out, b1, not_78_out, not_79_out, not_80_out, b5, b7);
  and and_32 (and_32_out, b1, not_81_out, not_82_out, not_83_out, b5, b6);
  and and_33 (and_33_out, b1, not_84_out, b4, not_85_out, b7);
  and and_34 (and_34_out, b1, not_86_out, b4, not_87_out, b6);
  and and_35 (and_35_out, not_88_out, b2, not_89_out, not_90_out, not_91_out, not_92_out, b7);
  and and_36 (and_36_out, b1, not_93_out, b4, b5, b6, b7);
  or or_1 (e1, and_2_out, and_3_out);
  or or_2 (g1, and_4_out, and_5_out, and_6_out, and_7_out, and_8_out);
  or or_3 (a1, and_9_out, and_10_out, and_11_out, and_12_out, and_13_out, and_14_out, and_15_out, and_16_out, and_17_out);
  or or_4 (c2, and_28_out, and_29_out, and_30_out, and_31_out, and_32_out, and_33_out, and_34_out);
  or or_5 (d2, and_35_out, and_36_out);
  or or_6 (b_1, and_18_out, and_19_out, and_20_out, and_21_out, and_22_out, and_23_out, and_24_out, and_25_out, and_26_out, and_27_out);

  assign a2 = 1'b0;
  assign b_2 = 1'b0;
  assign c1 = 1'b0;
  assign c3 = 1'b0;
  assign d1 = 1'b0;
  assign e2 = 1'b0;
  assign g2 = 1'b0;
endmodule
