// Logisim project ANIMATIONS.circ as structural Verilog: 7 circuits, main circuit ANIMATION
module ANIMATION (
  input  RESET,
  input  [2:0] State,
  output [7:0] L1,
  output [7:0] L2,
  output [7:0] L3,
  output [7:0] L4,
  output [7:0] L5,
  output [7:0] L6
);

  Letter1 Letter1_1 (
    .a(State[2]), .b(State[1]), .c(State[0]), .x(L1[5]), .y(L1[4]), .z(L1[3]), .u(L1[2]), .w(L1[1]), .v(L1[0]));
  Letter2 Letter2_1 (
    .a(State[2]), .b(State[1]), .c(State[0]), .x(L2[5]), .y(L2[4]), .z(L2[3]), .u(L2[2]), .v(L2[1]), .w(L2[0]));
  Letter3 Letter3_1 (
    .a(State[2]), .b(State[1]), .c(State[0]), .x(L3[5]), .y(L3[4]), .z(L3[3]), .u(L3[2]), .v(L3[1]), .w(L3[0]));
  Letter4 Letter4_1 (
    .a(State[2]), .b(State[1]), .c(State[0]), .x(L4[5]), .y(L4[4]), .z(L4[3]), .u(L4[2]), .v(L4[1]), .w(L4[0]));
  Letter5 Letter5_1 (
    .a(State[2]), .b(State[1]), .c(State[0]), .x(L5[5]), .y(L5[4]), .z(L5[3]), .u(L5[2]), .v(L5[1]), .w(L5[0]));
  Letter6 Letter6_1 (
    .a(State[2]), .b(State[1]), .c(State[0]), .x(L6[5]), .y(L6[4]), .z(L6[3]), .u(L6[2]), .v(L6[1]), .w(L6[0]));

  assign L1[7:6] = 2'b00;
  assign L2[7:6] = 2'b00;
  assign L3[7:6] = 2'b00;
  assign L4[7:6] = 2'b00;
  assign L5[7:6] = 2'b00;
  assign L6[7:6] = 2'b00;
endmodule

module Letter1 (
  input  a,
  input  b,
  input  c,
  output x,
  output y,
  output z,
  output u,
  output w,
  output v
);

  wire and_2_out, and_3_out, and_4_out, and_6_out, and_7_out, not_1_out, not_2_out, not_3_out, not_4_out,
       not_5_out, not_6_out, not_7_out, not_8_out, not_9_out, not_10_out, not_11_out;

  and and_1 (x, a, b, c);
  not not_1 (not_1_out, a);
  not not_2 (not_2_out, b);
  not not_3 (not_3_out, a);
  not not_4 (not_4_out, a);
  not not_5 (not_5_out, b);
  not not_6 (not_6_out, a);
  not not_7 (not_7_out, b);
  not not_8 (not_8_out, c);
  not not_9 (not_9_out, a);
  not not_10 (not_10_out, b);
  not not_11 (not_11_out, c);
  and and_2 (and_2_out, not_1_out, not_2_out);
  and and_3 (and_3_out, not_3_out, c);
  or or_1 (y, and_2_out, and_3_out, and_4_out);
  and and_4 (and_4_out, a, b);
  or or_2 (z, not_4_out, not_5_out);
  or or_3 (u, not_6_out, c, b);
  and and_5 (w, not_7_out, not_8_out);
  and and_6 (and_6_out, not_9_out, not_10_out);
  or or_4 (v, and_6_out, and_7_out);
  and and_7 (and_7_out, a, b, not_11_out);
endmodule

module Letter2 (
  input  a,
  input  b,
  input  c,
  output x,
  output y,
  output z,
  output u,
  output v,
  output w
);

  wire and_2_out, and_3_out, and_4_out, and_5_out, and_6_out, and_7_out, and_8_out, and_9_out, and_10_out,
       and_11_out, and_12_out, not_1_out, not_2_out, not_3_out, not_4_out, not_5_out, not_6_out, not_7_out,
       not_8_out, not_9_out, not_10_out, not_11_out, not_12_out, not_13_out, not_14_out, not_15_out,
       not_16_out, not_17_out;

  and and_1 (x, a, b, c);
  not not_1 (not_1_out, a);
  not not_2 (not_2_out, c);
  not not_3 (not_3_out, a);
  not not_4 (not_4_out, b);
  not not_5 (not_5_out, b);
  not not_6 (not_6_out, a);
  not not_7 (not_7_out, b);
  not not_8 (not_8_out, b);
  not not_9 (not_9_out, c);
  not not_10 (not_10_out, a);
  not not_11 (not_11_out, b);
  not not_12 (not_12_out, c);
  not not_13 (not_13_out, a);
  not not_14 (not_14_out, b);
  not not_15 (not_15_out, a);
  not not_16 (not_16_out, c);
  not not_17 (not_17_out, c);
  or or_1 (y, not_1_out, not_2_out, b);
  and and_2 (and_2_out, not_3_out, not_4_out);
  and and_3 (and_3_out, not_5_out, c);
  or or_2 (z, and_2_out, and_3_out, and_4_out);
  and and_4 (and_4_out, a, b);
  and and_5 (and_5_out, not_6_out, not_7_out);
  and and_6 (and_6_out, not_8_out, not_9_out);
  or or_3 (u, and_5_out, and_6_out, and_7_out);
  and and_7 (and_7_out, a, b);
  and and_8 (and_8_out, not_10_out, not_11_out, not_12_out);
  or or_4 (v, and_8_out, and_9_out, and_10_out);
  and and_9 (and_9_out, not_13_out, b, c);
  and and_10 (and_10_out, a, not_14_out, c);
  and and_11 (and_11_out, not_15_out, not_16_out);
  or or_5 (w, and_11_out, and_12_out);
  and and_12 (and_12_out, b, not_17_out);
endmodule

module Letter3 (
  input  a,
  input  b,
  input  c,
  output x,
  output y,
  output z,
  output u,
  output v,
  output w
);

  wire and_1_out, and_2_out, and_3_out, and_4_out, and_5_out, and_6_out, and_7_out, and_8_out, not_1_out,
       not_2_out, not_3_out, not_4_out, not_5_out, not_6_out, not_7_out, not_8_out, not_9_out, not_10_out;

  not not_1 (not_1_out, a);
  not not_2 (not_2_out, c);
  not not_3 (not_3_out, b);
  not not_4 (not_4_out, c);
  not not_5 (not_5_out, a);
  not not_6 (not_6_out, b);
  not not_7 (not_7_out, c);
  and and_1 (and_1_out, a, b);
  not not_8 (not_8_out, a);
  not not_9 (not_9_out, b);
  not not_10 (not_10_out, c);
  and and_2 (and_2_out, not_1_out, not_2_out);
  or or_1 (y, and_2_out, b, and_3_out);
  and and_3 (and_3_out, a, c);
  or or_2 (z, not_3_out, not_4_out, a);
  and and_4 (and_4_out, not_5_out, not_6_out);
  or or_3 (u, and_4_out, and_5_out);
  and and_5 (and_5_out, b, c);
  or or_4 (v, not_7_out, and_1_out);
  and and_6 (and_6_out, not_8_out, not_9_out, not_10_out);
  or or_5 (w, and_6_out, and_7_out, and_8_out);
  and and_7 (and_7_out, b, c);
  and and_8 (and_8_out, a, b);

  assign x = 1'b0;
endmodule

module Letter4 (
  input  a,
  input  b,
  input  c,
  output x,
  output y,
  output z,
  output u,
  output v,
  output w
);

  wire and_1_out, and_2_out, and_3_out, and_4_out, and_5_out, and_6_out, and_7_out, not_1_out, not_2_out,
       not_3_out, not_4_out, not_5_out, not_6_out, not_7_out, not_8_out, not_9_out, not_10_out, not_11_out;

  not not_1 (not_1_out, b);
  not not_2 (not_2_out, c);
  not not_3 (not_3_out, a);
  not not_4 (not_4_out, b);
  not not_5 (not_5_out, b);
  not not_6 (not_6_out, c);
  not not_7 (not_7_out, a);
  and and_1 (and_1_out, b, c);
  not not_8 (not_8_out, a);
  not not_9 (not_9_out, b);
  not not_10 (not_10_out, a);
  not not_11 (not_11_out, c);
  or or_1 (y, not_1_out, not_2_out, a);
  and and_2 (and_2_out, not_3_out, not_4_out);
  and and_3 (and_3_out, not_5_out, not_6_out);
  or or_2 (z, and_2_out, and_3_out, and_4_out);
  and and_4 (and_4_out, b, c);
  or or_3 (u, not_7_out, and_1_out);
  and and_5 (and_5_out, not_8_out, not_9_out);
  or or_4 (w, and_5_out, and_6_out, and_7_out);
  and and_6 (and_6_out, not_10_out, not_11_out);
  and and_7 (and_7_out, a, b, c);

  assign v = 1'b1;
  assign x = 1'b0;
endmodule

module Letter5 (
  input  a,
  input  b,
  input  c,
  output x,
  output y,
  output z,
  output u,
  output v,
  output w
);

  wire and_1_out, and_2_out, and_3_out, and_4_out, and_5_out, and_6_out, not_1_out, not_2_out, not_3_out,
       not_4_out, not_5_out, not_6_out, not_7_out, not_8_out, not_9_out, not_10_out, not_11_out;

  not not_1 (not_1_out, a);
  not not_2 (not_2_out, b);
  not not_3 (not_3_out, a);
  not not_4 (not_4_out, b);
  not not_5 (not_5_out, b);
  not not_6 (not_6_out, c);
  not not_7 (not_7_out, b);
  not not_8 (not_8_out, c);
  not not_9 (not_9_out, a);
  not not_10 (not_10_out, b);
  or or_1 (y, not_1_out, not_2_out, c);
  and and_1 (and_1_out, not_3_out, not_4_out);
  or or_2 (z, and_1_out, c, and_2_out);
  and and_2 (and_2_out, a, b);
  or or_3 (u, not_5_out, not_6_out, a);
  not not_11 (not_11_out, a);
  or or_4 (v, not_11_out, and_3_out, and_4_out);
  and and_3 (and_3_out, not_7_out, not_8_out);
  and and_4 (and_4_out, b, c);
  and and_5 (and_5_out, not_9_out, not_10_out);
  or or_5 (w, and_5_out, and_6_out);
  and and_6 (and_6_out, a, b, c);

  assign x = 1'b0;
endmodule

module Letter6 (
  input  a,
  input  b,
  input  c,
  output x,
  output y,
  output z,
  output u,
  output v,
  output w
);

  wire not_1_out, not_2_out, not_3_out, not_4_out, not_5_out, not_6_out, not_7_out, not_8_out;

  not not_1 (not_1_out, b);
  not not_2 (not_2_out, a);
  not not_3 (not_3_out, c);
  not not_4 (not_4_out, b);
  not not_5 (not_5_out, a);
  not not_6 (not_6_out, c);
  not not_7 (not_7_out, a);
  not not_8 (not_8_out, c);
  and and_1 (x, a, not_1_out, c);
  or or_1 (y, not_2_out, not_3_out, b);
  or or_2 (z, not_4_out, c, a);
  or or_3 (u, not_5_out, not_6_out, b);
  or or_4 (w, not_7_out, not_8_out, b);

  assign v = 1'b1;
endmodule
