// Logisim project Edfunctions.circ as structural Verilog: 16 circuits, main circuit sevensegCustom
module sevsegBase (
  input  U,
  input  V,
  input  W,
  input  X,
  input  Y,
  input  Z,
  output a,
  output b,
  output c,
  output d,
  output e,
  output f,
  output g,
  output o
);

  wire and_1_out, and_2_out, and_3_out, and_4_out, and_5_out, and_6_out, and_7_out, and_8_out, and_9_out,
       and_10_out, and_11_out, and_12_out, and_13_out, and_14_out, and_15_out, and_16_out, and_17_out,
       and_18_out, and_19_out, and_20_out, and_21_out, and_22_out, and_23_out, and_24_out, and_25_out,
       and_26_out, and_27_out, and_28_out, and_29_out, and_30_out, and_31_out, and_32_out, and_33_out,
       and_34_out, and_35_out, and_36_out, and_37_out, and_38_out, and_39_out, and_40_out, and_41_out,
       and_42_out, and_43_out, and_44_out, and_45_out, and_46_out, and_47_out, and_48_out, and_49_out,
       and_50_out, and_51_out, and_52_out, and_53_out, and_54_out, and_55_out, and_56_out, and_57_out,
       and_58_out, and_59_out, and_60_out, and_61_out, not_1_out, not_2_out, not_3_out, not_4_out, not_5_out,
       not_6_out, not_7_out, not_8_out, not_9_out, not_10_out, not_11_out, not_12_out, not_13_out,
       not_14_out, not_15_out, not_16_out, not_17_out, not_18_out, not_19_out, not_20_out, not_21_out,
       not_22_out, not_23_out, not_24_out, not_25_out, not_26_out, not_27_out, not_28_out, not_29_out,
       not_30_out, not_31_out, not_32_out, not_33_out, not_34_out, not_35_out, not_36_out, not_37_out,
       not_38_out, not_39_out, not_40_out, not_41_out, not_42_out, not_43_out, not_44_out, not_45_out,
       not_46_out, not_47_out, not_48_out, not_49_out, not_50_out, not_51_out, not_52_out, not_53_out,
       not_54_out, not_55_out, not_56_out, not_57_out, not_58_out, not_59_out, not_60_out, not_61_out,
       not_62_out, not_63_out, not_64_out, not_65_out, not_66_out, not_67_out, not_68_out, not_69_out,
       not_70_out, not_71_out, not_72_out, not_73_out, not_74_out, not_75_out, not_76_out, not_77_out,
       not_78_out, not_79_out, not_80_out, not_81_out, not_82_out, not_83_out, not_84_out, not_85_out,
       not_86_out, not_87_out, not_88_out, not_89_out, not_90_out, not_91_out, not_92_out, not_93_out,
       not_94_out, not_95_out, not_96_out, not_97_out, not_98_out, not_99_out, not_100_out, not_101_out,
       not_102_out, not_103_out, not_104_out, not_105_out, not_106_out, not_107_out;

  not not_1 (not_1_out, V);
  not not_2 (not_2_out, W);
  not not_3 (not_3_out, V);
  not not_4 (not_4_out, X);
  not not_5 (not_5_out, Y);
  not not_6 (not_6_out, V);
  not not_7 (not_7_out, W);
  not not_8 (not_8_out, Y);
  not not_9 (not_9_out, Z);
  not not_10 (not_10_out, V);
  not not_11 (not_11_out, Y);
  not not_12 (not_12_out, W);
  not not_13 (not_13_out, Y);
  not not_14 (not_14_out, Z);
  not not_15 (not_15_out, Y);
  not not_16 (not_16_out, W);
  not not_17 (not_17_out, Z);
  not not_18 (not_18_out, Y);
  not not_19 (not_19_out, Z);
  not not_20 (not_20_out, V);
  not not_21 (not_21_out, W);
  not not_22 (not_22_out, X);
  not not_23 (not_23_out, Z);
  not not_24 (not_24_out, V);
  not not_25 (not_25_out, Y);
  not not_26 (not_26_out, V);
  not not_27 (not_27_out, Z);
  not not_28 (not_28_out, W);
  not not_29 (not_29_out, Y);
  not not_30 (not_30_out, Z);
  not not_31 (not_31_out, W);
  not not_32 (not_32_out, Z);
  not not_33 (not_33_out, X);
  not not_34 (not_34_out, Y);
  not not_35 (not_35_out, Z);
  not not_36 (not_36_out, V);
  not not_37 (not_37_out, W);
  not not_38 (not_38_out, Y);
  not not_39 (not_39_out, W);
  not not_40 (not_40_out, X);
  not not_41 (not_41_out, Y);
  not not_42 (not_42_out, W);
  not not_43 (not_43_out, Y);
  not not_44 (not_44_out, V);
  not not_45 (not_45_out, W);
  not not_46 (not_46_out, Y);
  not not_47 (not_47_out, W);
  not not_48 (not_48_out, X);
  and and_1 (and_1_out, not_48_out, not_49_out, not_50_out);
  not not_49 (not_49_out, Y);
  not not_50 (not_50_out, Z);
  not not_51 (not_51_out, V);
  not not_52 (not_52_out, W);
  and and_2 (and_2_out, not_51_out, not_52_out, Y);
  and and_3 (and_3_out, not_1_out, not_2_out, X, Z);
  not not_53 (not_53_out, V);
  and and_4 (and_4_out, not_53_out, X, Y);
  not not_54 (not_54_out, W);
  and and_5 (and_5_out, not_54_out, X, Y);
  and and_6 (and_6_out, not_3_out, W, not_4_out, not_5_out);
  not not_55 (not_55_out, V);
  and and_7 (and_7_out, not_55_out, W, not_56_out);
  not not_56 (not_56_out, Z);
  and and_8 (and_8_out, W, Y, not_57_out);
  not not_57 (not_57_out, Z);
  and and_9 (and_9_out, not_6_out, not_7_out, not_8_out, not_9_out);
  not not_58 (not_58_out, V);
  not not_59 (not_59_out, X);
  and and_10 (and_10_out, not_58_out, not_59_out, not_60_out);
  not not_60 (not_60_out, Z);
  not not_61 (not_61_out, W);
  and and_11 (and_11_out, not_61_out, not_62_out, Z);
  not not_62 (not_62_out, X);
  not not_63 (not_63_out, W);
  and and_12 (and_12_out, not_63_out, Y, Z);
  and and_13 (and_13_out, not_10_out, W, not_11_out, Z);
  and and_14 (and_14_out, V, not_12_out, X, Y);
  and and_15 (and_15_out, V, W, not_13_out, not_14_out);
  and and_16 (and_16_out, V, W, X, not_15_out);
  not not_64 (not_64_out, V);
  not not_65 (not_65_out, W);
  and and_17 (and_17_out, not_64_out, not_65_out, not_66_out);
  not not_66 (not_66_out, Y);
  not not_67 (not_67_out, W);
  not not_68 (not_68_out, X);
  and and_18 (and_18_out, not_67_out, not_68_out, not_69_out);
  not not_69 (not_69_out, Y);
  not not_70 (not_70_out, W);
  not not_71 (not_71_out, X);
  and and_19 (and_19_out, not_70_out, not_71_out, Z);
  not not_72 (not_72_out, V);
  and and_20 (and_20_out, not_72_out, not_73_out, X);
  not not_73 (not_73_out, W);
  not not_74 (not_74_out, Y);
  and and_21 (and_21_out, X, not_74_out, Z);
  and and_22 (and_22_out, not_16_out, X, Y, not_17_out);
  not not_75 (not_75_out, V);
  and and_23 (and_23_out, not_75_out, W, not_76_out);
  not not_76 (not_76_out, X);
  not not_77 (not_77_out, X);
  and and_24 (and_24_out, W, not_77_out, not_78_out);
  not not_78 (not_78_out, Z);
  and and_25 (and_25_out, V, W, not_18_out, not_19_out);
  and and_26 (and_26_out, V, W, X, Z);
  and and_27 (and_27_out, not_20_out, not_21_out, not_22_out, not_23_out);
  not not_79 (not_79_out, X);
  and and_28 (and_28_out, not_79_out, Y, Z);
  and and_29 (and_29_out, not_24_out, X, not_25_out, Z);
  and and_30 (and_30_out, not_26_out, X, Y, not_27_out);
  not not_80 (not_80_out, V);
  and and_31 (and_31_out, not_80_out, W, not_81_out);
  not not_81 (not_81_out, Y);
  and and_32 (and_32_out, W, X, not_82_out);
  not not_82 (not_82_out, Y);
  and and_33 (and_33_out, V, not_28_out, not_29_out, not_30_out);
  and and_34 (and_34_out, V, not_31_out, X, not_32_out);
  and and_35 (and_35_out, V, W, not_33_out, Y);
  and and_36 (and_36_out, V, W, X, Z);
  not not_83 (not_83_out, V);
  not not_84 (not_84_out, X);
  and and_37 (and_37_out, not_83_out, not_84_out, not_85_out);
  not not_85 (not_85_out, Z);
  not not_86 (not_86_out, W);
  and and_38 (and_38_out, not_86_out, Y, not_87_out);
  not not_87 (not_87_out, Z);
  not not_88 (not_88_out, V);
  and and_39 (and_39_out, not_88_out, W, Y);
  not not_89 (not_89_out, V);
  and and_40 (and_40_out, not_89_out, W, X);
  and and_41 (and_41_out, V, not_90_out);
  not not_90 (not_90_out, W);
  not not_91 (not_91_out, X);
  and and_42 (and_42_out, V, not_91_out, Z);
  and and_43 (and_43_out, V, X, not_34_out, not_35_out);
  not not_92 (not_92_out, Y);
  and and_44 (and_44_out, not_92_out, not_93_out);
  not not_93 (not_93_out, Z);
  and and_45 (and_45_out, not_36_out, not_37_out, X, not_38_out);
  and and_46 (and_46_out, X, not_94_out);
  not not_94 (not_94_out, Z);
  not not_95 (not_95_out, V);
  and and_47 (and_47_out, not_95_out, W, not_96_out);
  not not_96 (not_96_out, X);
  not not_97 (not_97_out, V);
  and and_48 (and_48_out, not_97_out, W, Y);
  and and_49 (and_49_out, W, not_98_out, Y);
  not not_98 (not_98_out, X);
  and and_50 (and_50_out, V, not_39_out, not_40_out, not_41_out);
  and and_51 (and_51_out, V, not_99_out);
  not not_99 (not_99_out, Z);
  and and_52 (and_52_out, V, not_42_out, X, Y);
  and and_53 (and_53_out, V, W, X, not_43_out);
  not not_100 (not_100_out, V);
  not not_101 (not_101_out, X);
  and and_54 (and_54_out, not_100_out, not_101_out, Y);
  not not_102 (not_102_out, V);
  and and_55 (and_55_out, not_102_out, Y, not_103_out);
  not not_103 (not_103_out, Z);
  and and_56 (and_56_out, not_44_out, not_45_out, X, not_46_out);
  not not_104 (not_104_out, Y);
  and and_57 (and_57_out, X, not_104_out, Z);
  and and_58 (and_58_out, W, not_105_out);
  not not_105 (not_105_out, X);
  not not_106 (not_106_out, V);
  and and_59 (and_59_out, not_106_out, W, Y);
  not not_107 (not_107_out, Y);
  and and_60 (and_60_out, V, not_107_out, Z);
  and and_61 (and_61_out, V, not_47_out, X, Z);
  or or_1 (a, and_1_out, and_2_out, and_3_out, and_4_out, and_5_out, and_6_out, and_7_out, and_8_out);
  or or_2 (b, and_9_out, and_10_out, and_11_out, and_12_out, and_13_out, and_14_out, and_15_out, and_16_out);
  or or_3 (c, and_17_out, and_18_out, and_19_out, and_20_out, and_21_out, and_22_out, and_23_out, and_24_out, and_25_out, and_26_out);
  or or_4 (d, and_27_out, and_28_out, and_29_out, and_30_out, and_31_out, and_32_out, and_33_out, and_34_out, and_35_out, and_36_out);
  or or_5 (e, and_37_out, and_38_out, and_39_out, and_40_out, and_41_out, and_42_out, and_43_out);
  or or_6 (f, and_44_out, and_45_out, and_46_out, and_47_out, and_48_out, and_49_out, and_50_out, and_51_out, and_52_out, and_53_out);
  or or_7 (g, and_54_out, and_55_out, and_56_out, and_57_out, and_58_out, and_59_out, and_60_out, and_61_out);

  assign o = U;
endmodule

module sevensegCustom (
  input  dot1bit,
  input  [4:0] A5bits,
  output [7:0] sevseg8bits
);

  sevsegBase sevsegNew_1 (
    .U(dot1bit), .V(A5bits[4]), .W(A5bits[3]), .X(A5bits[2]), .Y(A5bits[1]), .Z(A5bits[0]),
    .a(sevseg8bits[0]), .b(sevseg8bits[1]), .c(sevseg8bits[2]), .d(sevseg8bits[3]), .e(sevseg8bits[4]),
    .f(sevseg8bits[5]), .g(sevseg8bits[6]), .o(sevseg8bits[7]));
endmodule

module sevBitsevseg (
  input  dot1,
  input  [7:0] Code,
  input  dot2,
  output [7:0] sevenseg1,
  output [7:0] sevenseg2
);

  wire [3:0] converter_w1, converter_w2;

  Converter7Bit converter (
    .e6(Code[0]), .e5(Code[1]), .e4(Code[2]), .e3(Code[3]), .e2(Code[4]), .e1(Code[5]), .e0(Code[6]),
    .z2(converter_w2[3]), .y2(converter_w2[2]), .x2(converter_w2[1]), .w2(converter_w2[0]),
    .z1(converter_w1[3]), .y1(converter_w1[2]), .x1(converter_w1[1]), .w1(converter_w1[0]));
  sevensegCustom sevensegCustom_1 (.dot1bit(dot1), .A5bits({1'b0, converter_w2}), .sevseg8bits(sevenseg1));
  sevensegCustom sevensegCustom_2 (.dot1bit(dot2), .A5bits({1'b0, converter_w1}), .sevseg8bits(sevenseg2));
endmodule

module hminsec (
);

  wire clock_1_out, counter_1_carry, counter_2_carry, counter_3_carry, counter_4_carry;
  wire [7:0] counter_5_q, counter_6_q, counter_7_q, counter_8_q, sevBitsevseg_1_sevenseg1,
       sevBitsevseg_1_sevenseg2, sevBitsevseg_2_sevenseg1, sevBitsevseg_2_sevenseg2,
       sevBitsevseg_3_sevenseg1, sevBitsevseg_3_sevenseg2, sevBitsevseg_4_sevenseg1, sevBitsevseg_4_sevenseg2;

  Clock clock_1 (.out(clock_1_out));
  Counter #(.width(9), .max('h64)) counter_1 (
    .clk(counter_2_carry), .carry(counter_1_carry));  // open: clr, load, up, count, D, Q
  Counter #(.max('h4)) counter_2 (.clk(clock_1_out), .carry(counter_2_carry));  // open: clr, load, up, count, D, Q
  Counter #(.width(6), .max('h3c)) counter_3 (
    .clk(counter_1_carry), .carry(counter_3_carry));  // open: clr, load, up, count, D, Q
  Counter #(.width(6), .max('h3c)) counter_4 (
    .clk(counter_3_carry), .carry(counter_4_carry));  // open: clr, load, up, count, D, Q
  Counter #(.width(7), .max('h63)) counter_5 (
    .clk(counter_2_carry), .Q(counter_5_q[6:0]));  // open: clr, load, up, count, D, carry
  Counter #(.width(7), .max('h3b)) counter_6 (
    .clk(counter_1_carry), .Q(counter_6_q[6:0]));  // open: clr, load, up, count, D, carry
  Counter #(.width(7), .max('h3b)) counter_7 (
    .clk(counter_3_carry), .Q(counter_7_q[6:0]));  // open: clr, load, up, count, D, carry
  Counter #(.width(7), .max('h17)) counter_8 (
    .clk(counter_4_carry), .Q(counter_8_q[6:0]));  // open: clr, load, up, count, D, carry
  sevBitsevseg sevBitsevseg_1 (
    .dot1(1'b0), .Code(counter_5_q), .dot2(1'b0), .sevenseg1(sevBitsevseg_1_sevenseg1),
    .sevenseg2(sevBitsevseg_1_sevenseg2));
  sevBitsevseg sevBitsevseg_2 (
    .dot1(1'b0), .Code(counter_6_q), .dot2(1'b0), .sevenseg1(sevBitsevseg_2_sevenseg1),
    .sevenseg2(sevBitsevseg_2_sevenseg2));
  sevBitsevseg sevBitsevseg_3 (
    .dot1(1'b0), .Code(counter_7_q), .dot2(1'b0), .sevenseg1(sevBitsevseg_3_sevenseg1),
    .sevenseg2(sevBitsevseg_3_sevenseg2));
  sevBitsevseg sevBitsevseg_4 (
    .dot1(1'b0), .Code(counter_8_q), .dot2(1'b0), .sevenseg1(sevBitsevseg_4_sevenseg1),
    .sevenseg2(sevBitsevseg_4_sevenseg2));
  _7_Segment_Display L_7_Segment_Display_1 (
    .g(sevBitsevseg_1_sevenseg1[6]), .f(sevBitsevseg_1_sevenseg1[5]), .a(sevBitsevseg_1_sevenseg1[0]),
    .b(sevBitsevseg_1_sevenseg1[1]), .e(sevBitsevseg_1_sevenseg1[4]), .d(sevBitsevseg_1_sevenseg1[3]),
    .c(sevBitsevseg_1_sevenseg1[2]), .dp(sevBitsevseg_1_sevenseg1[7]));
  _7_Segment_Display L_7_Segment_Display_3 (
    .g(sevBitsevseg_2_sevenseg1[6]), .f(sevBitsevseg_2_sevenseg1[5]), .a(sevBitsevseg_2_sevenseg1[0]),
    .b(sevBitsevseg_2_sevenseg1[1]), .e(sevBitsevseg_2_sevenseg1[4]), .d(sevBitsevseg_2_sevenseg1[3]),
    .c(sevBitsevseg_2_sevenseg1[2]), .dp(sevBitsevseg_2_sevenseg1[7]));
  _7_Segment_Display L_7_Segment_Display_5 (
    .g(sevBitsevseg_3_sevenseg1[6]), .f(sevBitsevseg_3_sevenseg1[5]), .a(sevBitsevseg_3_sevenseg1[0]),
    .b(sevBitsevseg_3_sevenseg1[1]), .e(sevBitsevseg_3_sevenseg1[4]), .d(sevBitsevseg_3_sevenseg1[3]),
    .c(sevBitsevseg_3_sevenseg1[2]), .dp(sevBitsevseg_3_sevenseg1[7]));
  _7_Segment_Display L_7_Segment_Display_7 (
    .g(sevBitsevseg_4_sevenseg1[6]), .f(sevBitsevseg_4_sevenseg1[5]), .a(sevBitsevseg_4_sevenseg1[0]),
    .b(sevBitsevseg_4_sevenseg1[1]), .e(sevBitsevseg_4_sevenseg1[4]), .d(sevBitsevseg_4_sevenseg1[3]),
    .c(sevBitsevseg_4_sevenseg1[2]), .dp(sevBitsevseg_4_sevenseg1[7]));
  _7_Segment_Display L_7_Segment_Display_2 (
    .g(sevBitsevseg_1_sevenseg2[6]), .f(sevBitsevseg_1_sevenseg2[5]), .a(sevBitsevseg_1_sevenseg2[0]),
    .b(sevBitsevseg_1_sevenseg2[1]), .e(sevBitsevseg_1_sevenseg2[4]), .d(sevBitsevseg_1_sevenseg2[3]),
    .c(sevBitsevseg_1_sevenseg2[2]), .dp(sevBitsevseg_1_sevenseg2[7]));
  _7_Segment_Display L_7_Segment_Display_4 (
    .g(sevBitsevseg_2_sevenseg2[6]), .f(sevBitsevseg_2_sevenseg2[5]), .a(sevBitsevseg_2_sevenseg2[0]),
    .b(sevBitsevseg_2_sevenseg2[1]), .e(sevBitsevseg_2_sevenseg2[4]), .d(sevBitsevseg_2_sevenseg2[3]),
    .c(sevBitsevseg_2_sevenseg2[2]), .dp(sevBitsevseg_2_sevenseg2[7]));
  _7_Segment_Display L_7_Segment_Display_6 (
    .g(sevBitsevseg_3_sevenseg2[6]), .f(sevBitsevseg_3_sevenseg2[5]), .a(sevBitsevseg_3_sevenseg2[0]),
    .b(sevBitsevseg_3_sevenseg2[1]), .e(sevBitsevseg_3_sevenseg2[4]), .d(sevBitsevseg_3_sevenseg2[3]),
    .c(sevBitsevseg_3_sevenseg2[2]), .dp(sevBitsevseg_3_sevenseg2[7]));
  _7_Segment_Display L_7_Segment_Display_8 (
    .g(sevBitsevseg_4_sevenseg2[6]), .f(sevBitsevseg_4_sevenseg2[5]), .a(sevBitsevseg_4_sevenseg2[0]),
    .b(sevBitsevseg_4_sevenseg2[1]), .e(sevBitsevseg_4_sevenseg2[4]), .d(sevBitsevseg_4_sevenseg2[3]),
    .c(sevBitsevseg_4_sevenseg2[2]), .dp(sevBitsevseg_4_sevenseg2[7]));
  // Pins of 7 and 8 bits meet at counter_6_q
  // Pins of 7 and 8 bits meet at counter_5_q
  // Pins of 7 and 8 bits meet at counter_8_q
  // Pins of 7 and 8 bits meet at counter_7_q
endmodule

module horloge (
  input  CLK1000,
  input  csload,
  input  [6:0] cs,
  input  sload,
  input  [5:0] s,
  input  minload,
  input  [5:0] min,
  input  hload,
  input  [4:0] h,
  output [6:0] currcs,
  output [6:0] currs,
  output [6:0] currmin,
  output [6:0] currh
);

  wire counter_1_carry, counter_2_carry, counter_3_carry, counter_4_carry;

  Counter #(.width(7), .max('h64)) counter_1 (
    .clk(counter_2_carry), .carry(counter_1_carry));  // open: clr, load, up, count, D, Q
  Counter #(.max('h4)) counter_2 (.clk(CLK1000), .carry(counter_2_carry));  // open: clr, load, up, count, D, Q
  Counter #(.width(6), .max('h3c)) counter_3 (
    .clk(counter_1_carry), .carry(counter_3_carry));  // open: clr, load, up, count, D, Q
  Counter #(.width(6), .max('h3c)) counter_4 (
    .clk(counter_3_carry), .carry(counter_4_carry));  // open: clr, load, up, count, D, Q
  Counter #(.width(7), .max('h63)) counter_5 (
    .load(csload), .clk(counter_2_carry), .D(cs), .Q(currcs));  // open: clr, up, count, carry
  Counter #(.width(6), .max('h3f)) counter_6 (
    .load(sload), .clk(counter_1_carry), .D(s), .Q(currs[5:0]));  // open: clr, up, count, carry
  Counter #(.width(6), .max('h3f)) counter_7 (
    .load(minload), .clk(counter_3_carry), .D(min), .Q(currmin[5:0]));  // open: clr, up, count, carry
  Counter #(.width(5), .max('h1f)) counter_8 (
    .load(hload), .clk(counter_4_carry), .D(h), .Q(currh[4:0]));  // open: clr, up, count, carry

  assign currh[6:5] = 2'b00;
  assign currmin[6] = 1'b0;
  assign currs[6] = 1'b0;
endmodule

module timeAndchrono (
);

  wire clock_1_out, horloge_1_p2, horloge_1_p3;
  wire [7:0] chronoView_1_p4, chronoView_1_p5, chronoView_1_p6, chronoView_1_p7, chronoView_1_p8,
       chronoView_1_p9, horloge_1_p4, horloge_1_p5, hourView_1_sevseg0, hourView_1_sevseg1,
       hourView_1_sevseg2, hourView_1_sevseg3, hourView_1_sevseg4, hourView_1_sevseg5;

  Clock clock_1 (.out(clock_1_out));
  // horloge horloge_1: pin names not known; wires that end beside it: clock_1_out, horloge_1_p2, horloge_1_p3, horloge_1_p4, horloge_1_p5
  // chronoView chronoView_1: pin names not known; wires that end beside it: horloge_1_p2, horloge_1_p3, horloge_1_p4, chronoView_1_p4, chronoView_1_p5, chronoView_1_p6, chronoView_1_p7, chronoView_1_p8, chronoView_1_p9
  hourView hourView_1 (
    .min(horloge_1_p4), .h(horloge_1_p5), .sevseg5(hourView_1_sevseg5), .sevseg4(hourView_1_sevseg4),
    .sevseg3(hourView_1_sevseg3), .sevseg2(hourView_1_sevseg2), .sevseg1(hourView_1_sevseg1),
    .sevseg0(hourView_1_sevseg0));
  _7_Segment_Display L_7_Segment_Display_1 (
    .g(chronoView_1_p9[6]), .f(chronoView_1_p9[5]), .a(chronoView_1_p9[0]), .b(chronoView_1_p9[1]),
    .e(chronoView_1_p9[4]), .d(chronoView_1_p9[3]), .c(chronoView_1_p9[2]), .dp(chronoView_1_p9[7]));
  _7_Segment_Display L_7_Segment_Display_7 (
    .g(hourView_1_sevseg0[6]), .f(hourView_1_sevseg0[5]), .a(hourView_1_sevseg0[0]),
    .b(hourView_1_sevseg0[1]), .e(hourView_1_sevseg0[4]), .d(hourView_1_sevseg0[3]),
    .c(hourView_1_sevseg0[2]), .dp(hourView_1_sevseg0[7]));
  _7_Segment_Display L_7_Segment_Display_2 (
    .g(chronoView_1_p8[6]), .f(chronoView_1_p8[5]), .a(chronoView_1_p8[0]), .b(chronoView_1_p8[1]),
    .e(chronoView_1_p8[4]), .d(chronoView_1_p8[3]), .c(chronoView_1_p8[2]), .dp(chronoView_1_p8[7]));
  _7_Segment_Display L_7_Segment_Display_8 (
    .g(hourView_1_sevseg1[6]), .f(hourView_1_sevseg1[5]), .a(hourView_1_sevseg1[0]),
    .b(hourView_1_sevseg1[1]), .e(hourView_1_sevseg1[4]), .d(hourView_1_sevseg1[3]),
    .c(hourView_1_sevseg1[2]), .dp(hourView_1_sevseg1[7]));
  _7_Segment_Display L_7_Segment_Display_3 (
    .g(chronoView_1_p7[6]), .f(chronoView_1_p7[5]), .a(chronoView_1_p7[0]), .b(chronoView_1_p7[1]),
    .e(chronoView_1_p7[4]), .d(chronoView_1_p7[3]), .c(chronoView_1_p7[2]), .dp(chronoView_1_p7[7]));
  _7_Segment_Display L_7_Segment_Display_9 (
    .g(hourView_1_sevseg2[6]), .f(hourView_1_sevseg2[5]), .a(hourView_1_sevseg2[0]),
    .b(hourView_1_sevseg2[1]), .e(hourView_1_sevseg2[4]), .d(hourView_1_sevseg2[3]),
    .c(hourView_1_sevseg2[2]), .dp(hourView_1_sevseg2[7]));
  _7_Segment_Display L_7_Segment_Display_4 (
    .g(chronoView_1_p6[6]), .f(chronoView_1_p6[5]), .a(chronoView_1_p6[0]), .b(chronoView_1_p6[1]),
    .e(chronoView_1_p6[4]), .d(chronoView_1_p6[3]), .c(chronoView_1_p6[2]), .dp(chronoView_1_p6[7]));
  _7_Segment_Display L_7_Segment_Display_10 (
    .g(hourView_1_sevseg3[6]), .f(hourView_1_sevseg3[5]), .a(hourView_1_sevseg3[0]),
    .b(hourView_1_sevseg3[1]), .e(hourView_1_sevseg3[4]), .d(hourView_1_sevseg3[3]),
    .c(hourView_1_sevseg3[2]), .dp(hourView_1_sevseg3[7]));
  _7_Segment_Display L_7_Segment_Display_5 (
    .g(chronoView_1_p5[6]), .f(chronoView_1_p5[5]), .a(chronoView_1_p5[0]), .b(chronoView_1_p5[1]),
    .e(chronoView_1_p5[4]), .d(chronoView_1_p5[3]), .c(chronoView_1_p5[2]), .dp(chronoView_1_p5[7]));
  _7_Segment_Display L_7_Segment_Display_11 (
    .g(hourView_1_sevseg4[6]), .f(hourView_1_sevseg4[5]), .a(hourView_1_sevseg4[0]),
    .b(hourView_1_sevseg4[1]), .e(hourView_1_sevseg4[4]), .d(hourView_1_sevseg4[3]),
    .c(hourView_1_sevseg4[2]), .dp(hourView_1_sevseg4[7]));
  _7_Segment_Display L_7_Segment_Display_6 (
    .g(chronoView_1_p4[6]), .f(chronoView_1_p4[5]), .a(chronoView_1_p4[0]), .b(chronoView_1_p4[1]),
    .e(chronoView_1_p4[4]), .d(chronoView_1_p4[3]), .c(chronoView_1_p4[2]), .dp(chronoView_1_p4[7]));
  _7_Segment_Display L_7_Segment_Display_12 (
    .g(hourView_1_sevseg5[6]), .f(hourView_1_sevseg5[5]), .a(hourView_1_sevseg5[0]),
    .b(hourView_1_sevseg5[1]), .e(hourView_1_sevseg5[4]), .d(hourView_1_sevseg5[3]),
    .c(hourView_1_sevseg5[2]), .dp(hourView_1_sevseg5[7]));
endmodule

module chronoView (
  input  [7:0] cs,
  input  [7:0] s,
  input  [7:0] min,
  output [7:0] sevseg0,
  output [7:0] sevseg1,
  output [7:0] sevseg2,
  output [7:0] sevseg3,
  output [7:0] sevseg4,
  output [7:0] sevseg5
);

  wire [7:7] undriven, undriven_2, undriven_3;

  sevBitsevseg sevBitsevseg_1 (
    .dot1(1'b0), .Code({undriven[7], cs[6:0]}), .dot2(1'b0), .sevenseg1(sevseg1), .sevenseg2(sevseg0));
  sevBitsevseg sevBitsevseg_2 (
    .dot1(1'b0), .Code({undriven_2[7], s[6:0]}), .dot2(1'b1), .sevenseg1(sevseg3), .sevenseg2(sevseg2));
  sevBitsevseg sevBitsevseg_3 (
    .dot1(1'b0), .Code({undriven_3[7], min[6:0]}), .dot2(1'b1), .sevenseg1(sevseg5), .sevenseg2(sevseg4));
  // Pins of 7 and 8 bits meet at {undriven_2[7], s[6:0]}
  // Pins of 7 and 8 bits meet at {undriven[7], cs[6:0]}
  // Pins of 7 and 8 bits meet at {undriven_3[7], min[6:0]}
endmodule

module hourView (
  input  [7:0] min,
  input  [7:0] h,
  output [7:0] sevseg5,
  output [7:0] sevseg4,
  output [7:0] sevseg3,
  output [7:0] sevseg2,
  output [7:0] sevseg1,
  output [7:0] sevseg0
);

  sevBitsevseg sevBitsevseg_1 (.dot1(1'b0), .Code(min), .dot2(1'b0), .sevenseg1(sevseg2), .sevenseg2(sevseg1));
  sevBitsevseg sevBitsevseg_2 (.dot1(1'b0), .Code(h), .dot2(1'b1), .sevenseg1(sevseg4), .sevenseg2(sevseg3));

  assign sevseg0 = 8'hc;
  assign sevseg5 = 8'h21;
endmodule

module newhorloge (
  input  Input_1,
  input  Input_2,
  input  Input_3,
  input  [6:0] Input_bus_1,
  input  Input_4,
  input  Input_5,
  input  Input_6,
  input  [5:0] Input_bus_2,
  input  Input_7,
  input  Input_8,
  input  [5:0] Input_bus_3,
  input  Input_9,
  input  Input_10,
  input  [4:0] Input_bus_4,
  output [6:0] Output_bus_1,
  output [6:0] Output_bus_2,
  output [6:0] Output_bus_3,
  output [6:0] Output_bus_4
);

  wire clock_1_out, counter_1_carry, counter_2_carry, counter_3_carry, counter_4_carry, d_ff_1_q, d_ff_2_q,
       d_ff_3_q, or_1_out, or_2_out, or_3_out, or_4_out;
  wire [7:0] multiplexer_1_out, sevBitsevseg_1_sevenseg1, sevBitsevseg_1_sevenseg2, sevBitsevseg_2_sevenseg1,
       sevBitsevseg_2_sevenseg2, sevBitsevseg_3_sevenseg1, sevBitsevseg_3_sevenseg2,
       sevBitsevseg_4_sevenseg1, sevBitsevseg_4_sevenseg2;
  wire [7:7] undriven, undriven_2, undriven_3, undriven_4;

  Clock clock_1 (.out(clock_1_out));
  Counter #(.max('h4)) counter_1 (.clk(clock_1_out), .carry(counter_1_carry));  // open: clr, load, up, count, D, Q
  Multiplexer #(.width(8), .enable("false")) multiplexer_1 (
    .in0({8{1'b0}}), .in1({8{1'b1}}), .out(multiplexer_1_out), .sel(Input_6));
  // AND_Gate and_1 is placed but not wired
  Counter #(.width(7), .max('h63)) counter_2 (
    .load(multiplexer_1_out[0]), .clk(or_1_out), .D(7'b1011111), .carry(counter_2_carry), .Q(Output_bus_1));  // open: clr, up, count
  or or_1 (or_1_out, counter_1_carry, multiplexer_1_out[1]);
  Counter #(.width(6), .max('h3b)) counter_3 (
    .load(multiplexer_1_out[2]), .clk(or_2_out), .D(6'b111011), .carry(counter_3_carry), .Q(Output_bus_2[5:0]));  // open: clr, up, count
  or or_2 (or_2_out, d_ff_1_q, multiplexer_1_out[3]);
  Counter #(.width(6), .max('h3b)) counter_4 (
    .load(multiplexer_1_out[4]), .clk(or_3_out), .D(6'b111011), .carry(counter_4_carry), .Q(Output_bus_3[5:0]));  // open: clr, up, count
  or or_3 (or_3_out, d_ff_2_q, multiplexer_1_out[5]);
  Counter #(.width(5), .max('h17)) counter_5 (
    .load(multiplexer_1_out[6]), .clk(or_4_out), .D(5'b10111), .Q(Output_bus_4[4:0]));  // open: clr, up, count, carry
  or or_4 (or_4_out, d_ff_3_q, multiplexer_1_out[7]);
  D_Flip_Flop d_ff_1 (.D(counter_2_carry), .clk(counter_1_carry), .Q(d_ff_1_q));  // open: Qn, preset, reset
  D_Flip_Flop d_ff_2 (.D(counter_3_carry), .clk(d_ff_1_q), .Q(d_ff_2_q));  // open: Qn, preset, reset
  D_Flip_Flop d_ff_3 (.D(counter_4_carry), .clk(d_ff_2_q), .Q(d_ff_3_q));  // open: Qn, preset, reset
  sevBitsevseg sevBitsevseg_1 (
    .dot1(1'b0), .Code({undriven_2[7], Output_bus_1}), .dot2(1'b0), .sevenseg1(sevBitsevseg_1_sevenseg1),
    .sevenseg2(sevBitsevseg_1_sevenseg2));
  sevBitsevseg sevBitsevseg_2 (
    .dot1(1'b0), .Code({undriven_3[7], 1'b0, Output_bus_2[5:0]}), .dot2(1'b0),
    .sevenseg1(sevBitsevseg_2_sevenseg1), .sevenseg2(sevBitsevseg_2_sevenseg2));
  sevBitsevseg sevBitsevseg_3 (
    .dot1(1'b0), .Code({undriven[7], 1'b0, Output_bus_3[5:0]}), .dot2(1'b0),
    .sevenseg1(sevBitsevseg_3_sevenseg1), .sevenseg2(sevBitsevseg_3_sevenseg2));
  sevBitsevseg sevBitsevseg_4 (
    .dot1(1'b0), .Code({undriven_4[7], 2'b00, Output_bus_4[4:0]}), .dot2(1'b0),
    .sevenseg1(sevBitsevseg_4_sevenseg1), .sevenseg2(sevBitsevseg_4_sevenseg2));
  _7_Segment_Display L_7_Segment_Display_1 (
    .g(sevBitsevseg_1_sevenseg1[6]), .f(sevBitsevseg_1_sevenseg1[5]), .a(sevBitsevseg_1_sevenseg1[0]),
    .b(sevBitsevseg_1_sevenseg1[1]), .e(sevBitsevseg_1_sevenseg1[4]), .d(sevBitsevseg_1_sevenseg1[3]),
    .c(sevBitsevseg_1_sevenseg1[2]), .dp(sevBitsevseg_1_sevenseg1[7]));
  _7_Segment_Display L_7_Segment_Display_3 (
    .g(sevBitsevseg_2_sevenseg1[6]), .f(sevBitsevseg_2_sevenseg1[5]), .a(sevBitsevseg_2_sevenseg1[0]),
    .b(sevBitsevseg_2_sevenseg1[1]), .e(sevBitsevseg_2_sevenseg1[4]), .d(sevBitsevseg_2_sevenseg1[3]),
    .c(sevBitsevseg_2_sevenseg1[2]), .dp(sevBitsevseg_2_sevenseg1[7]));
  _7_Segment_Display L_7_Segment_Display_5 (
    .g(sevBitsevseg_3_sevenseg1[6]), .f(sevBitsevseg_3_sevenseg1[5]), .a(sevBitsevseg_3_sevenseg1[0]),
    .b(sevBitsevseg_3_sevenseg1[1]), .e(sevBitsevseg_3_sevenseg1[4]), .d(sevBitsevseg_3_sevenseg1[3]),
    .c(sevBitsevseg_3_sevenseg1[2]), .dp(sevBitsevseg_3_sevenseg1[7]));
  _7_Segment_Display L_7_Segment_Display_7 (
    .g(sevBitsevseg_4_sevenseg1[6]), .f(sevBitsevseg_4_sevenseg1[5]), .a(sevBitsevseg_4_sevenseg1[0]),
    .b(sevBitsevseg_4_sevenseg1[1]), .e(sevBitsevseg_4_sevenseg1[4]), .d(sevBitsevseg_4_sevenseg1[3]),
    .c(sevBitsevseg_4_sevenseg1[2]), .dp(sevBitsevseg_4_sevenseg1[7]));
  _7_Segment_Display L_7_Segment_Display_2 (
    .g(sevBitsevseg_1_sevenseg2[6]), .f(sevBitsevseg_1_sevenseg2[5]), .a(sevBitsevseg_1_sevenseg2[0]),
    .b(sevBitsevseg_1_sevenseg2[1]), .e(sevBitsevseg_1_sevenseg2[4]), .d(sevBitsevseg_1_sevenseg2[3]),
    .c(sevBitsevseg_1_sevenseg2[2]), .dp(sevBitsevseg_1_sevenseg2[7]));
  _7_Segment_Display L_7_Segment_Display_4 (
    .g(sevBitsevseg_2_sevenseg2[6]), .f(sevBitsevseg_2_sevenseg2[5]), .a(sevBitsevseg_2_sevenseg2[0]),
    .b(sevBitsevseg_2_sevenseg2[1]), .e(sevBitsevseg_2_sevenseg2[4]), .d(sevBitsevseg_2_sevenseg2[3]),
    .c(sevBitsevseg_2_sevenseg2[2]), .dp(sevBitsevseg_2_sevenseg2[7]));
  _7_Segment_Display L_7_Segment_Display_6 (
    .g(sevBitsevseg_3_sevenseg2[6]), .f(sevBitsevseg_3_sevenseg2[5]), .a(sevBitsevseg_3_sevenseg2[0]),
    .b(sevBitsevseg_3_sevenseg2[1]), .e(sevBitsevseg_3_sevenseg2[4]), .d(sevBitsevseg_3_sevenseg2[3]),
    .c(sevBitsevseg_3_sevenseg2[2]), .dp(sevBitsevseg_3_sevenseg2[7]));
  _7_Segment_Display L_7_Segment_Display_8 (
    .g(sevBitsevseg_4_sevenseg2[6]), .f(sevBitsevseg_4_sevenseg2[5]), .a(sevBitsevseg_4_sevenseg2[0]),
    .b(sevBitsevseg_4_sevenseg2[1]), .e(sevBitsevseg_4_sevenseg2[4]), .d(sevBitsevseg_4_sevenseg2[3]),
    .c(sevBitsevseg_4_sevenseg2[2]), .dp(sevBitsevseg_4_sevenseg2[7]));
  // Pins of 7 and 8 bits meet at {undriven_3[7], 1'b0, Output_bus_2[5:0]}
  // Pins of 7 and 8 bits meet at {undriven_2[7], Output_bus_1}
  // Pins of 7 and 8 bits meet at {undriven_4[7], 2'b00, Output_bus_4[4:0]}
  // Pins of 7 and 8 bits meet at {undriven[7], 1'b0, Output_bus_3[5:0]}

  assign Output_bus_2[6] = 1'b0;
  assign Output_bus_3[6] = 1'b0;
  assign Output_bus_4[6:5] = 2'b00;
endmodule

module chronoBoard (
  input  [6:0] Input_bus_1,
  input  Input_1,
  input  Input_2,
  input  [5:0] Input_bus_2,
  input  Input_3,
  input  Input_4,
  input  Input_5,
  input  [5:0] Input_bus_3,
  input  [4:0] Input_bus_4,
  output Output_1
);

  wire clock_1_out, counter_1_carry, counter_2_carry, counter_3_carry, counter_4_carry, d_ff_1_q, d_ff_2_q,
       d_ff_3_q, multiplexer_1_out, or_1_out, or_2_out, or_3_out, or_4_out;
  wire [4:0] counter_5_q;
  wire [5:0] counter_3_q, counter_4_q;
  wire [7:0] counter_2_q, multiplexer_2_out, sevBitsevseg_1_sevenseg1, sevBitsevseg_1_sevenseg2,
       sevBitsevseg_2_sevenseg1, sevBitsevseg_2_sevenseg2, sevBitsevseg_3_sevenseg1,
       sevBitsevseg_3_sevenseg2, sevBitsevseg_4_sevenseg1, sevBitsevseg_4_sevenseg2;
  wire [7:7] undriven, undriven_2, undriven_3;

  DipSwitch #(.number(10)) DipSwitch_1 ();  // open: sw1, sw2, sw3, sw4, sw5, sw6, sw7, sw8, sw9, sw10
  Clock clock_1 (.out(clock_1_out));
  Counter #(.max('h4)) counter_1 (
    .clk(multiplexer_1_out), .carry(counter_1_carry));  // open: clr, load, up, count, D, Q
  Multiplexer #(.enable("false")) multiplexer_1 (.in0(1'b0), .in1(clock_1_out), .out(multiplexer_1_out), .sel(Input_2));
  Multiplexer #(.width(8), .enable("false")) multiplexer_2 (
    .in0({8{1'b0}}), .in1({8{1'b1}}), .out(multiplexer_2_out), .sel(Input_1));
  Counter #(.width(7), .max('h63)) counter_2 (
    .load(multiplexer_2_out[0]), .clk(or_1_out), .D(Input_bus_1), .carry(counter_2_carry),
    .Q(counter_2_q[6:0]));  // open: clr, up, count
  or or_1 (or_1_out, counter_1_carry, multiplexer_2_out[1]);
  Counter #(.width(6), .max('h3b)) counter_3 (
    .load(multiplexer_2_out[2]), .clk(or_2_out), .D(Input_bus_2), .carry(counter_3_carry), .Q(counter_3_q));  // open: clr, up, count
  or or_2 (or_2_out, d_ff_1_q, multiplexer_2_out[3]);
  Counter #(.width(6), .max('h3b)) counter_4 (
    .load(multiplexer_2_out[4]), .clk(or_3_out), .D(Input_bus_3), .carry(counter_4_carry), .Q(counter_4_q));  // open: clr, up, count
  or or_3 (or_3_out, d_ff_2_q, multiplexer_2_out[5]);
  Counter #(.width(5), .max('h17)) counter_5 (
    .load(multiplexer_2_out[6]), .clk(or_4_out), .D(Input_bus_4), .Q(counter_5_q));  // open: clr, up, count, carry
  or or_4 (or_4_out, d_ff_3_q, multiplexer_2_out[7]);
  D_Flip_Flop d_ff_1 (.D(counter_2_carry), .clk(counter_1_carry), .Q(d_ff_1_q));  // open: Qn, preset, reset
  D_Flip_Flop d_ff_2 (.D(counter_3_carry), .clk(d_ff_1_q), .Q(d_ff_2_q));  // open: Qn, preset, reset
  D_Flip_Flop d_ff_3 (.D(counter_4_carry), .clk(d_ff_2_q), .Q(d_ff_3_q));  // open: Qn, preset, reset
  sevBitsevseg sevBitsevseg_1 (
    .dot1(1'b0), .Code(counter_2_q), .dot2(1'b0), .sevenseg1(sevBitsevseg_1_sevenseg1),
    .sevenseg2(sevBitsevseg_1_sevenseg2));
  sevBitsevseg sevBitsevseg_2 (
    .dot1(1'b0), .Code({undriven[7], 1'b0, counter_3_q}), .dot2(1'b0), .sevenseg1(sevBitsevseg_2_sevenseg1),
    .sevenseg2(sevBitsevseg_2_sevenseg2));
  sevBitsevseg sevBitsevseg_3 (
    .dot1(1'b0), .Code({undriven_3[7], 1'b0, counter_4_q}), .dot2(1'b0),
    .sevenseg1(sevBitsevseg_3_sevenseg1), .sevenseg2(sevBitsevseg_3_sevenseg2));
  sevBitsevseg sevBitsevseg_4 (
    .dot1(1'b0), .Code({undriven_2[7], 2'b00, counter_5_q}), .dot2(1'b0),
    .sevenseg1(sevBitsevseg_4_sevenseg1), .sevenseg2(sevBitsevseg_4_sevenseg2));
  _7_Segment_Display L_7_Segment_Display_1 (
    .g(sevBitsevseg_1_sevenseg1[6]), .f(sevBitsevseg_1_sevenseg1[5]), .a(sevBitsevseg_1_sevenseg1[0]),
    .b(sevBitsevseg_1_sevenseg1[1]), .e(sevBitsevseg_1_sevenseg1[4]), .d(sevBitsevseg_1_sevenseg1[3]),
    .c(sevBitsevseg_1_sevenseg1[2]), .dp(sevBitsevseg_1_sevenseg1[7]));
  _7_Segment_Display L_7_Segment_Display_3 (
    .g(sevBitsevseg_2_sevenseg1[6]), .f(sevBitsevseg_2_sevenseg1[5]), .a(sevBitsevseg_2_sevenseg1[0]),
    .b(sevBitsevseg_2_sevenseg1[1]), .e(sevBitsevseg_2_sevenseg1[4]), .d(sevBitsevseg_2_sevenseg1[3]),
    .c(sevBitsevseg_2_sevenseg1[2]), .dp(sevBitsevseg_2_sevenseg1[7]));
  _7_Segment_Display L_7_Segment_Display_5 (
    .g(sevBitsevseg_3_sevenseg1[6]), .f(sevBitsevseg_3_sevenseg1[5]), .a(sevBitsevseg_3_sevenseg1[0]),
    .b(sevBitsevseg_3_sevenseg1[1]), .e(sevBitsevseg_3_sevenseg1[4]), .d(sevBitsevseg_3_sevenseg1[3]),
    .c(sevBitsevseg_3_sevenseg1[2]), .dp(sevBitsevseg_3_sevenseg1[7]));
  _7_Segment_Display L_7_Segment_Display_7 (
    .g(sevBitsevseg_4_sevenseg1[6]), .f(sevBitsevseg_4_sevenseg1[5]), .a(sevBitsevseg_4_sevenseg1[0]),
    .b(sevBitsevseg_4_sevenseg1[1]), .e(sevBitsevseg_4_sevenseg1[4]), .d(sevBitsevseg_4_sevenseg1[3]),
    .c(sevBitsevseg_4_sevenseg1[2]), .dp(sevBitsevseg_4_sevenseg1[7]));
  _7_Segment_Display L_7_Segment_Display_2 (
    .g(sevBitsevseg_1_sevenseg2[6]), .f(sevBitsevseg_1_sevenseg2[5]), .a(sevBitsevseg_1_sevenseg2[0]),
    .b(sevBitsevseg_1_sevenseg2[1]), .e(sevBitsevseg_1_sevenseg2[4]), .d(sevBitsevseg_1_sevenseg2[3]),
    .c(sevBitsevseg_1_sevenseg2[2]), .dp(sevBitsevseg_1_sevenseg2[7]));
  _7_Segment_Display L_7_Segment_Display_4 (
    .g(sevBitsevseg_2_sevenseg2[6]), .f(sevBitsevseg_2_sevenseg2[5]), .a(sevBitsevseg_2_sevenseg2[0]),
    .b(sevBitsevseg_2_sevenseg2[1]), .e(sevBitsevseg_2_sevenseg2[4]), .d(sevBitsevseg_2_sevenseg2[3]),
    .c(sevBitsevseg_2_sevenseg2[2]), .dp(sevBitsevseg_2_sevenseg2[7]));
  _7_Segment_Display L_7_Segment_Display_6 (
    .g(sevBitsevseg_3_sevenseg2[6]), .f(sevBitsevseg_3_sevenseg2[5]), .a(sevBitsevseg_3_sevenseg2[0]),
    .b(sevBitsevseg_3_sevenseg2[1]), .e(sevBitsevseg_3_sevenseg2[4]), .d(sevBitsevseg_3_sevenseg2[3]),
    .c(sevBitsevseg_3_sevenseg2[2]), .dp(sevBitsevseg_3_sevenseg2[7]));
  _7_Segment_Display L_7_Segment_Display_8 (
    .g(sevBitsevseg_4_sevenseg2[6]), .f(sevBitsevseg_4_sevenseg2[5]), .a(sevBitsevseg_4_sevenseg2[0]),
    .b(sevBitsevseg_4_sevenseg2[1]), .e(sevBitsevseg_4_sevenseg2[4]), .d(sevBitsevseg_4_sevenseg2[3]),
    .c(sevBitsevseg_4_sevenseg2[2]), .dp(sevBitsevseg_4_sevenseg2[7]));
  // Pins of 7 and 8 bits meet at counter_2_q
  // Pins of 7 and 8 bits meet at {undriven_3[7], 1'b0, counter_4_q}
  // Pins of 7 and 8 bits meet at {undriven_2[7], 2'b00, counter_5_q}
  // Pins of 7 and 8 bits meet at {undriven[7], 1'b0, counter_3_q}
endmodule

module board1 (
);

  wire Button_1_out, clock_1_out, counter_1_carry, counter_2_carry, counter_3_carry, counter_4_carry,
       d_ff_1_q, d_ff_2_q, d_ff_3_q, DipSwitch_1_sw9, DipSwitch_1_sw10, multiplexer_1_out, not_1_out,
       or_1_out, or_2_out, or_3_out, or_4_out, s_r_ff_1_q;
  wire [3:0] multiplexer_3_out;
  wire [7:0] counter_2_q, counter_3_q, counter_4_q, counter_5_q, multiplexer_2_out, sevBitsevseg_1_sevenseg1,
       sevBitsevseg_1_sevenseg2, sevBitsevseg_2_sevenseg1, sevBitsevseg_2_sevenseg2,
       sevBitsevseg_3_sevenseg1, sevBitsevseg_3_sevenseg2, sevBitsevseg_4_sevenseg1, sevBitsevseg_4_sevenseg2;

  Button Button_1 (.out(Button_1_out));
  DipSwitch #(.number(10)) DipSwitch_1 (
    .sw9(DipSwitch_1_sw9), .sw10(DipSwitch_1_sw10));  // open: sw1, sw2, sw3, sw4, sw5, sw6, sw7, sw8
  Clock clock_1 (.out(clock_1_out));
  Counter #(.max('h4)) counter_1 (
    .clk(multiplexer_1_out), .carry(counter_1_carry));  // open: clr, load, up, count, D, Q
  Multiplexer #(.enable("false")) multiplexer_1 (
    .in0(1'b0), .in1(clock_1_out), .out(multiplexer_1_out), .sel(DipSwitch_1_sw10));
  Multiplexer #(.width(8), .enable("false")) multiplexer_2 (
    .in0({8{1'b0}}), .in1({8{1'b1}}), .out(multiplexer_2_out), .sel(Button_1_out));
  Multiplexer #(.width(4), .enable("false")) multiplexer_3 (
    .in0(4'b1111), .in1(4'b0000), .out(multiplexer_3_out), .sel(DipSwitch_1_sw9));
  Counter #(.width(7), .max('h63)) counter_2 (
    .load(multiplexer_2_out[0]), .up(multiplexer_3_out[0]), .clk(or_1_out), .D(7'b1100010),
    .carry(counter_2_carry), .Q(counter_2_q[6:0]));  // open: clr, count
  or or_1 (or_1_out, counter_1_carry, multiplexer_2_out[1]);
  Counter #(.width(6), .max('h3b)) counter_3 (
    .load(multiplexer_2_out[2]), .up(multiplexer_3_out[1]), .clk(or_2_out), .D(6'b111011),
    .carry(counter_3_carry), .Q(counter_3_q[5:0]));  // open: clr, count
  or or_2 (or_2_out, s_r_ff_1_q, multiplexer_2_out[3]);
  Counter #(.width(6), .max('h3b)) counter_4 (
    .load(multiplexer_2_out[4]), .up(multiplexer_3_out[2]), .clk(or_3_out), .D(6'b111011),
    .carry(counter_4_carry), .Q(counter_4_q[5:0]));  // open: clr, count
  or or_3 (or_3_out, d_ff_2_q, multiplexer_2_out[5]);
  Counter #(.width(5), .max('h17)) counter_5 (
    .load(multiplexer_2_out[6]), .up(multiplexer_3_out[3]), .clk(or_4_out), .D(5'b10111), .Q(counter_5_q[4:0]));  // open: clr, count, carry
  or or_4 (or_4_out, d_ff_3_q, multiplexer_2_out[7]);
  D_Flip_Flop d_ff_1 (.D(counter_2_carry), .clk(counter_1_carry), .Q(d_ff_1_q));  // open: Qn, preset, reset
  S_R_Flip_Flop s_r_ff_1 (.S(d_ff_1_q), .R(not_1_out), .Q(s_r_ff_1_q));  // open: clk, reset, Qn, preset
  not not_1 (not_1_out, d_ff_1_q);
  D_Flip_Flop d_ff_2 (.D(counter_3_carry), .clk(s_r_ff_1_q), .Q(d_ff_2_q));  // open: Qn, preset, reset
  D_Flip_Flop d_ff_3 (.D(counter_4_carry), .clk(d_ff_2_q), .Q(d_ff_3_q));  // open: Qn, preset, reset
  sevBitsevseg sevBitsevseg_1 (
    .dot1(1'b0), .Code(counter_2_q), .dot2(1'b0), .sevenseg1(sevBitsevseg_1_sevenseg1),
    .sevenseg2(sevBitsevseg_1_sevenseg2));
  sevBitsevseg sevBitsevseg_2 (
    .dot1(1'b0), .Code({counter_3_q[7], 1'b0, counter_3_q[5:0]}), .dot2(1'b0),
    .sevenseg1(sevBitsevseg_2_sevenseg1), .sevenseg2(sevBitsevseg_2_sevenseg2));
  sevBitsevseg sevBitsevseg_3 (
    .dot1(1'b0), .Code({counter_4_q[7], 1'b0, counter_4_q[5:0]}), .dot2(1'b0),
    .sevenseg1(sevBitsevseg_3_sevenseg1), .sevenseg2(sevBitsevseg_3_sevenseg2));
  sevBitsevseg sevBitsevseg_4 (
    .dot1(1'b0), .Code({counter_5_q[7], 2'b00, counter_5_q[4:0]}), .dot2(1'b0),
    .sevenseg1(sevBitsevseg_4_sevenseg1), .sevenseg2(sevBitsevseg_4_sevenseg2));
  _7_Segment_Display L_7_Segment_Display_1 (
    .g(sevBitsevseg_1_sevenseg1[6]), .f(sevBitsevseg_1_sevenseg1[5]), .a(sevBitsevseg_1_sevenseg1[0]),
    .b(sevBitsevseg_1_sevenseg1[1]), .e(sevBitsevseg_1_sevenseg1[4]), .d(sevBitsevseg_1_sevenseg1[3]),
    .c(sevBitsevseg_1_sevenseg1[2]), .dp(sevBitsevseg_1_sevenseg1[7]));
  _7_Segment_Display L_7_Segment_Display_3 (
    .g(sevBitsevseg_2_sevenseg1[6]), .f(sevBitsevseg_2_sevenseg1[5]), .a(sevBitsevseg_2_sevenseg1[0]),
    .b(sevBitsevseg_2_sevenseg1[1]), .e(sevBitsevseg_2_sevenseg1[4]), .d(sevBitsevseg_2_sevenseg1[3]),
    .c(sevBitsevseg_2_sevenseg1[2]), .dp(sevBitsevseg_2_sevenseg1[7]));
  _7_Segment_Display L_7_Segment_Display_5 (
    .g(sevBitsevseg_3_sevenseg1[6]), .f(sevBitsevseg_3_sevenseg1[5]), .a(sevBitsevseg_3_sevenseg1[0]),
    .b(sevBitsevseg_3_sevenseg1[1]), .e(sevBitsevseg_3_sevenseg1[4]), .d(sevBitsevseg_3_sevenseg1[3]),
    .c(sevBitsevseg_3_sevenseg1[2]), .dp(sevBitsevseg_3_sevenseg1[7]));
  _7_Segment_Display L_7_Segment_Display_7 (
    .g(sevBitsevseg_4_sevenseg1[6]), .f(sevBitsevseg_4_sevenseg1[5]), .a(sevBitsevseg_4_sevenseg1[0]),
    .b(sevBitsevseg_4_sevenseg1[1]), .e(sevBitsevseg_4_sevenseg1[4]), .d(sevBitsevseg_4_sevenseg1[3]),
    .c(sevBitsevseg_4_sevenseg1[2]), .dp(sevBitsevseg_4_sevenseg1[7]));
  _7_Segment_Display L_7_Segment_Display_2 (
    .g(sevBitsevseg_1_sevenseg2[6]), .f(sevBitsevseg_1_sevenseg2[5]), .a(sevBitsevseg_1_sevenseg2[0]),
    .b(sevBitsevseg_1_sevenseg2[1]), .e(sevBitsevseg_1_sevenseg2[4]), .d(sevBitsevseg_1_sevenseg2[3]),
    .c(sevBitsevseg_1_sevenseg2[2]), .dp(sevBitsevseg_1_sevenseg2[7]));
  _7_Segment_Display L_7_Segment_Display_4 (
    .g(sevBitsevseg_2_sevenseg2[6]), .f(sevBitsevseg_2_sevenseg2[5]), .a(sevBitsevseg_2_sevenseg2[0]),
    .b(sevBitsevseg_2_sevenseg2[1]), .e(sevBitsevseg_2_sevenseg2[4]), .d(sevBitsevseg_2_sevenseg2[3]),
    .c(sevBitsevseg_2_sevenseg2[2]), .dp(sevBitsevseg_2_sevenseg2[7]));
  _7_Segment_Display L_7_Segment_Display_6 (
    .g(sevBitsevseg_3_sevenseg2[6]), .f(sevBitsevseg_3_sevenseg2[5]), .a(sevBitsevseg_3_sevenseg2[0]),
    .b(sevBitsevseg_3_sevenseg2[1]), .e(sevBitsevseg_3_sevenseg2[4]), .d(sevBitsevseg_3_sevenseg2[3]),
    .c(sevBitsevseg_3_sevenseg2[2]), .dp(sevBitsevseg_3_sevenseg2[7]));
  _7_Segment_Display L_7_Segment_Display_8 (
    .g(sevBitsevseg_4_sevenseg2[6]), .f(sevBitsevseg_4_sevenseg2[5]), .a(sevBitsevseg_4_sevenseg2[0]),
    .b(sevBitsevseg_4_sevenseg2[1]), .e(sevBitsevseg_4_sevenseg2[4]), .d(sevBitsevseg_4_sevenseg2[3]),
    .c(sevBitsevseg_4_sevenseg2[2]), .dp(sevBitsevseg_4_sevenseg2[7]));
  // Pins of 7 and 8 bits meet at counter_2_q
  // Pins of 7 and 8 bits meet at {counter_3_q[7], 1'b0, counter_3_q[5:0]}
  // Pins of 7 and 8 bits meet at {counter_4_q[7], 1'b0, counter_4_q[5:0]}
  // Pins of 7 and 8 bits meet at {counter_5_q[7], 2'b00, counter_5_q[4:0]}
endmodule

module pulse (
  input  [7:0] minLoad,
  input  Input_1,
  input  [7:0] hLoad,
  input  Input_2,
  input  Input_3,
  input  Input_4,
  input  Input_5,
  input  Input_6,
  input  Input_7,
  input  Input_8,
  input  Input_9,
  output Output_1,
  output Output_2,
  output Output_3,
  output Output_4,
  output Output_5,
  output Output_6,
  output Output_7,
  output Output_8
);

  wire bcd_to_7_segment_decoder_1_p1, clock_1_out, clock_2_out, clock_3_out, clock_4_out, counter_1_carry,
       counter_3_carry, d_ff_1_qn, d_ff_2_q, not_1_out, not_2_out, pulsetest_1_d, t_ff_3_q, undriven_3;
  wire [3:0] undriven, undriven_2;
  wire [4:0] counter_2_q;
  wire [7:0] sevensegCustom_1_sevseg8bits;

  Clock clock_1 (.out(clock_1_out));
  _7_Segment_Display L_7_Segment_Display_2 (
    .g(undriven[3]), .f(undriven[2]), .a(undriven[1]), .b(undriven[0]), .e(undriven_2[3]), .d(undriven_2[2]),
    .c(undriven_2[1]), .dp(undriven_2[0]));
  T_Flip_Flop t_ff_1 (.T(Input_7), .clk(clock_1_out), .Qn(Output_7));  // open: Q, reset, preset
  Clock clock_2 (.out(clock_2_out));
  Clock clock_3 (.out(clock_3_out));
  D_Flip_Flop d_ff_1 (.D(d_ff_1_qn), .clk(Input_2), .Q(Output_2), .Qn(d_ff_1_qn));  // open: preset, reset
  S_R_Flip_Flop s_r_ff_1 (.S(Input_4), .R(not_1_out), .clk(clock_2_out), .Q(Output_4));  // open: reset, Qn, preset
  not not_1 (not_1_out, Input_4);
  T_Flip_Flop t_ff_2 (.T(Input_5), .clk(Input_8), .Q(Output_6));  // open: Qn, reset, preset
  Multiplexer #(.enable("false")) multiplexer_1 (.in0(1'b0), .in1(clock_3_out), .out(Output_8), .sel(pulsetest_1_d));
  pulsetest pulsetest_1 (.C(pulsetest_1_d), .A(Input_9), .B(d_ff_2_q), .D(pulsetest_1_d));
  Clock clock_4 (.out(clock_4_out));
  Counter #(.width(3), .max('h7)) counter_1 (
    .clk(Output_8), .carry(counter_1_carry));  // open: clr, load, up, count, D, Q
  nand nand_1 (Output_1, Input_1, Output_3);
  nand nand_2 (Output_3, Output_1, Input_3);
  and and_1 (Output_5, clock_4_out, Input_6, not_2_out);
  D_Flip_Flop d_ff_2 (.D(counter_1_carry), .clk(clock_3_out), .Q(d_ff_2_q));  // open: Qn, preset, reset
  Counter #(.width(5), .max('h1f)) counter_2 (
    .clk(undriven_3), .Q(counter_2_q));  // open: clr, load, up, count, D, carry
  Counter #(.width(2), .max('h3)) counter_3 (
    .clk(Output_5), .carry(counter_3_carry));  // open: clr, load, up, count, D, Q
  not not_2 (not_2_out, t_ff_3_q);
  T_Flip_Flop t_ff_3 (.T(Input_6), .clk(counter_3_carry), .Q(t_ff_3_q));  // open: Qn, reset, preset
  // BCD_to_7_Segment_decoder bcd_to_7_segment_decoder_1: pin names not known; wires that end beside it: bcd_to_7_segment_decoder_1_p1, bcd_to_7_segment_decoder_1_p1, bcd_to_7_segment_decoder_1_p1
  _7_Segment_Display L_7_Segment_Display_3 ();  // open: g, f, a, b, e, d, c, dp
  sevensegCustom sevensegCustom_1 (.A5bits(counter_2_q), .sevseg8bits(sevensegCustom_1_sevseg8bits));  // open: dot1bit
  _7_Segment_Display L_7_Segment_Display_1 (
    .g(sevensegCustom_1_sevseg8bits[6]), .f(sevensegCustom_1_sevseg8bits[5]),
    .a(sevensegCustom_1_sevseg8bits[0]), .b(sevensegCustom_1_sevseg8bits[1]),
    .e(sevensegCustom_1_sevseg8bits[4]), .d(sevensegCustom_1_sevseg8bits[3]),
    .c(sevensegCustom_1_sevseg8bits[2]), .dp(sevensegCustom_1_sevseg8bits[7]));
endmodule

module chronotest (
);

  wire and_1_out, and_2_out, button0_out, clock_1_out, counter_1_carry, counter_2_carry, counter_3_carry,
       counter_4_carry, d_ff_1_q, d_ff_2_q, d_ff_3_q, d_ff_4_q, dipswitch0_sw8, dipswitch0_sw9,
       dipswitch0_sw10, multiplexer_1_out, not_1_out, or_1_out, or_2_out, or_3_out, or_4_out;
  wire [3:0] multiplexer_2_out, multiplexer_3_out, multiplexer_4_out;
  wire [7:0] counter_2_q, counter_3_q, counter_4_q, counter_5_q, sevBitsevseg_1_sevenseg1,
       sevBitsevseg_1_sevenseg2, sevBitsevseg_2_sevenseg1, sevBitsevseg_2_sevenseg2,
       sevBitsevseg_3_sevenseg1, sevBitsevseg_3_sevenseg2;

  DipSwitch #(.number(10)) dipswitch0 (
    .sw8(dipswitch0_sw8), .sw9(dipswitch0_sw9), .sw10(dipswitch0_sw10));  // open: sw1, sw2, sw3, sw4, sw5, sw6, sw7
  Clock clock_1 (.out(clock_1_out));
  Button button0 (.out(button0_out));
  Counter #(.max('h4)) counter_1 (
    .clk(multiplexer_1_out), .carry(counter_1_carry));  // open: clr, load, up, count, D, Q
  Multiplexer #(.enable("false")) multiplexer_1 (
    .in0(1'b0), .in1(clock_1_out), .out(multiplexer_1_out), .sel(dipswitch0_sw10));
  Multiplexer #(.width(4), .enable("false")) multiplexer_2 (
    .in0(4'b0000), .in1(4'b1111), .out(multiplexer_2_out), .sel(dipswitch0_sw8));
  and and_1 (and_1_out, button0_out, dipswitch0_sw8);
  Multiplexer #(.width(4), .enable("false")) multiplexer_3 (
    .in0(4'b0000), .in1(4'b1111), .out(multiplexer_3_out), .sel(and_1_out));
  Multiplexer #(.width(4), .enable("false")) multiplexer_4 (
    .in0(4'b1111), .in1(4'b0000), .out(multiplexer_4_out), .sel(dipswitch0_sw9));
  Counter #(.width(7), .max('h63)) counter_2 (
    .load(multiplexer_2_out[0]), .up(multiplexer_4_out[0]), .clk(or_1_out), .D(7'b1100010),
    .carry(counter_2_carry), .Q(counter_2_q[6:0]));  // open: clr, count
  or or_1 (or_1_out, counter_1_carry, multiplexer_3_out[0]);
  Counter #(.width(6), .max('h3b)) counter_3 (
    .load(multiplexer_2_out[1]), .up(multiplexer_4_out[1]), .clk(or_2_out), .D(6'b111011),
    .carry(counter_3_carry), .Q(counter_3_q[5:0]));  // open: clr, count
  or or_2 (or_2_out, d_ff_1_q, multiplexer_3_out[1]);
  Counter #(.width(6), .max('h3b)) counter_4 (
    .load(multiplexer_2_out[2]), .up(multiplexer_4_out[2]), .clk(or_3_out), .D(6'b111011),
    .carry(counter_4_carry), .Q(counter_4_q[5:0]));  // open: clr, count
  or or_3 (or_3_out, and_2_out, multiplexer_3_out[2]);
  Counter #(.width(5), .max('h17)) counter_5 (
    .load(multiplexer_2_out[3]), .up(multiplexer_4_out[3]), .clk(or_4_out), .D(5'b10111), .Q(counter_5_q[4:0]));  // open: clr, count, carry
  or or_4 (or_4_out, d_ff_3_q, multiplexer_3_out[3]);
  D_Flip_Flop d_ff_1 (.D(counter_2_carry), .clk(counter_1_carry), .Q(d_ff_1_q));  // open: Qn, preset, reset
  D_Flip_Flop d_ff_2 (.D(counter_3_carry), .clk(d_ff_1_q), .Q(d_ff_2_q));  // open: Qn, preset, reset
  and and_2 (and_2_out, d_ff_2_q, d_ff_4_q);
  D_Flip_Flop d_ff_3 (.D(counter_4_carry), .clk(and_2_out), .Q(d_ff_3_q));  // open: Qn, preset, reset
  not not_1 (not_1_out, counter_1_carry);
  D_Flip_Flop d_ff_4 (.D(counter_3_carry), .clk(not_1_out), .Q(d_ff_4_q));  // open: Qn, preset, reset
  D_Flip_Flop d_ff_5 ();  // open: D, clk, Q, Qn, preset, reset
  sevBitsevseg sevBitsevseg_1 (
    .dot1(1'b0), .Code(counter_2_q), .dot2(1'b0), .sevenseg1(sevBitsevseg_1_sevenseg1),
    .sevenseg2(sevBitsevseg_1_sevenseg2));
  sevBitsevseg sevBitsevseg_2 (
    .dot1(1'b0), .Code({counter_3_q[7], 1'b0, counter_3_q[5:0]}), .dot2(1'b0),
    .sevenseg1(sevBitsevseg_2_sevenseg1), .sevenseg2(sevBitsevseg_2_sevenseg2));
  sevBitsevseg sevBitsevseg_3 (
    .dot1(1'b0), .Code({counter_4_q[7], 1'b0, counter_4_q[5:0]}), .dot2(1'b0),
    .sevenseg1(sevBitsevseg_3_sevenseg1), .sevenseg2(sevBitsevseg_3_sevenseg2));
  sevBitsevseg sevBitsevseg_4 (
    .dot1(1'b0), .Code({counter_5_q[7], 2'b00, counter_5_q[4:0]}), .dot2(1'b0));  // open: sevenseg1, sevenseg2
  _7_Segment_Display sevseg1 (
    .g(sevBitsevseg_1_sevenseg1[6]), .f(sevBitsevseg_1_sevenseg1[5]), .a(sevBitsevseg_1_sevenseg1[0]),
    .b(sevBitsevseg_1_sevenseg1[1]), .e(sevBitsevseg_1_sevenseg1[4]), .d(sevBitsevseg_1_sevenseg1[3]),
    .c(sevBitsevseg_1_sevenseg1[2]), .dp(sevBitsevseg_1_sevenseg1[7]));
  _7_Segment_Display sevseg3 (
    .g(sevBitsevseg_2_sevenseg1[6]), .f(sevBitsevseg_2_sevenseg1[5]), .a(sevBitsevseg_2_sevenseg1[0]),
    .b(sevBitsevseg_2_sevenseg1[1]), .e(sevBitsevseg_2_sevenseg1[4]), .d(sevBitsevseg_2_sevenseg1[3]),
    .c(sevBitsevseg_2_sevenseg1[2]), .dp(sevBitsevseg_2_sevenseg1[7]));
  _7_Segment_Display sevseg5 (
    .g(sevBitsevseg_3_sevenseg1[6]), .f(sevBitsevseg_3_sevenseg1[5]), .a(sevBitsevseg_3_sevenseg1[0]),
    .b(sevBitsevseg_3_sevenseg1[1]), .e(sevBitsevseg_3_sevenseg1[4]), .d(sevBitsevseg_3_sevenseg1[3]),
    .c(sevBitsevseg_3_sevenseg1[2]), .dp(sevBitsevseg_3_sevenseg1[7]));
  _7_Segment_Display sevseg0 (
    .g(sevBitsevseg_1_sevenseg2[6]), .f(sevBitsevseg_1_sevenseg2[5]), .a(sevBitsevseg_1_sevenseg2[0]),
    .b(sevBitsevseg_1_sevenseg2[1]), .e(sevBitsevseg_1_sevenseg2[4]), .d(sevBitsevseg_1_sevenseg2[3]),
    .c(sevBitsevseg_1_sevenseg2[2]), .dp(sevBitsevseg_1_sevenseg2[7]));
  _7_Segment_Display sevseg2 (
    .g(sevBitsevseg_2_sevenseg2[6]), .f(sevBitsevseg_2_sevenseg2[5]), .a(sevBitsevseg_2_sevenseg2[0]),
    .b(sevBitsevseg_2_sevenseg2[1]), .e(sevBitsevseg_2_sevenseg2[4]), .d(sevBitsevseg_2_sevenseg2[3]),
    .c(sevBitsevseg_2_sevenseg2[2]), .dp(sevBitsevseg_2_sevenseg2[7]));
  _7_Segment_Display sevseg4 (
    .g(sevBitsevseg_3_sevenseg2[6]), .f(sevBitsevseg_3_sevenseg2[5]), .a(sevBitsevseg_3_sevenseg2[0]),
    .b(sevBitsevseg_3_sevenseg2[1]), .e(sevBitsevseg_3_sevenseg2[4]), .d(sevBitsevseg_3_sevenseg2[3]),
    .c(sevBitsevseg_3_sevenseg2[2]), .dp(sevBitsevseg_3_sevenseg2[7]));
  // Pins of 7 and 8 bits meet at {counter_4_q[7], 1'b0, counter_4_q[5:0]}
  // Pins of 7 and 8 bits meet at {counter_5_q[7], 2'b00, counter_5_q[4:0]}
  // Pins of 7 and 8 bits meet at counter_2_q
  // Pins of 7 and 8 bits meet at {counter_3_q[7], 1'b0, counter_3_q[5:0]}
endmodule

module pulsetest (
  input  C,
  input  A,
  input  B,
  output D
);

  wire and_1_out, and_2_out, not_1_out;

  not not_1 (not_1_out, B);
  and and_1 (and_1_out, A, not_1_out);
  or or_1 (D, and_1_out, and_2_out);
  and and_2 (and_2_out, C, A);
endmodule

module timestampFunc (
  input  Load,
  input  startstop,
  input  updown,
  input  loadEnDi,
  input  resetEnDi,
  input  [7:0] csload,
  input  minIncrease,
  input  hIncrease,
  input  [7:0] sload,
  input  [7:0] minload,
  input  [7:0] hload,
  output [7:0] cscur,
  output [7:0] scur,
  output [7:0] mincur,
  output [7:0] hcur
);

  wire and_1_out, and_2_out, and_3_out, and_4_out, clock_1_out, clock_2_out, counter_1_carry,
       counter_2_carry, counter_3_carry, counter_4_carry, counter_5_carry, d_ff_1_q, d_ff_2_q, d_ff_3_q,
       multiplexer_1_out, multiplexer_2_out, multiplexer_3_out, or_1_out, or_2_out, or_3_out, or_4_out;
  wire [3:0] multiplexer_4_out, multiplexer_5_out, multiplexer_6_out, multiplexer_7_out;

  Clock clock_1 (.out(clock_1_out));
  Clock clock_2 (.out(clock_2_out));
  Counter #(.width(12), .max('ha00)) counter_1 (
    .clk(clock_1_out), .carry(counter_1_carry));  // open: clr, load, up, count, D, Q
  and and_1 (and_1_out, minIncrease, ~startstop);  // AND_Gate
  Multiplexer #(.enable("false")) multiplexer_1 (
    .in0(1'b0), .in1(counter_1_carry), .out(multiplexer_1_out), .sel(and_1_out));
  Multiplexer #(.enable("false")) multiplexer_2 (
    .in0(1'b0), .in1(counter_1_carry), .out(multiplexer_2_out), .sel(and_2_out));
  and and_2 (and_2_out, hIncrease, ~startstop);  // AND_Gate
  Multiplexer #(.enable("false")) multiplexer_3 (
    .in0(1'b0), .in1(clock_2_out), .out(multiplexer_3_out), .sel(startstop));
  Multiplexer #(.width(4), .enable("false")) multiplexer_4 (
    .in0(4'b0000), .in1(4'b1111), .out(multiplexer_4_out), .sel(loadEnDi));
  Counter #(.width(9), .max('h9f)) counter_2 (
    .clk(multiplexer_3_out), .carry(counter_2_carry));  // open: clr, load, up, count, D, Q
  and and_3 (and_3_out, Load, loadEnDi);
  Multiplexer #(.width(4), .enable("false")) multiplexer_5 (
    .in0(4'b0000), .in1(4'b1111), .out(multiplexer_5_out), .sel(and_3_out));
  and and_4 (and_4_out, ~startstop, resetEnDi);  // AND_Gate
  Multiplexer #(.width(4), .enable("false")) multiplexer_6 (
    .in0(4'b1111), .in1(4'b0000), .out(multiplexer_6_out), .sel(updown));
  Multiplexer #(.width(4), .enable("false")) multiplexer_7 (
    .in0(4'b0000), .in1(4'b1111), .out(multiplexer_7_out), .sel(and_4_out));
  Counter #(.width(7), .max('h63)) counter_3 (
    .clr(multiplexer_7_out[0]), .load(multiplexer_4_out[0]), .up(multiplexer_6_out[0]), .clk(or_1_out),
    .D(csload[6:0]), .carry(counter_3_carry), .Q(cscur[6:0]));  // open: count
  or or_1 (or_1_out, counter_2_carry, multiplexer_5_out[0]);
  Counter #(.width(6), .max('h3b)) counter_4 (
    .clr(multiplexer_7_out[1]), .load(multiplexer_4_out[1]), .up(multiplexer_6_out[1]), .clk(or_2_out),
    .D(sload[5:0]), .carry(counter_4_carry), .Q(scur[5:0]));  // open: count
  or or_2 (or_2_out, d_ff_1_q, multiplexer_5_out[1]);
  Counter #(.width(6), .max('h3b)) counter_5 (
    .clr(multiplexer_7_out[2]), .load(multiplexer_4_out[2]), .up(multiplexer_6_out[2]), .clk(or_3_out),
    .D(minload[5:0]), .carry(counter_5_carry), .Q(mincur[5:0]));  // open: count
  or or_3 (or_3_out, d_ff_2_q, multiplexer_1_out, multiplexer_5_out[2]);
  D_Flip_Flop d_ff_1 (.D(counter_3_carry), .clk(counter_2_carry), .Q(d_ff_1_q));  // open: Qn, preset, reset
  D_Flip_Flop d_ff_2 (.D(counter_4_carry), .clk(d_ff_1_q), .Q(d_ff_2_q));  // open: Qn, preset, reset
  D_Flip_Flop d_ff_3 (.D(counter_5_carry), .clk(d_ff_2_q), .Q(d_ff_3_q));  // open: Qn, preset, reset
  Counter #(.width(5), .max('h17)) counter_6 (
    .clr(multiplexer_7_out[3]), .load(multiplexer_4_out[3]), .up(multiplexer_6_out[3]), .clk(or_4_out),
    .D(hload[4:0]), .Q(hcur[4:0]));  // open: count, carry
  or or_4 (or_4_out, d_ff_3_q, multiplexer_2_out, multiplexer_5_out[3]);

  assign cscur[7] = 1'b0;
  assign hcur[7:5] = 3'b000;
  assign mincur[7:6] = 2'b00;
  assign scur[7:6] = 2'b00;
endmodule

module timestampFunctest (
  input  Input_1,
  input  Input_2,
  input  Input_3,
  input  Input_4,
  input  Input_5,
  input  Input_6,
  input  Input_7,
  input  [7:0] Input_bus_1,
  input  [7:0] Input_bus_2,
  input  [7:0] Input_bus_3,
  input  [7:0] Input_bus_4,
  input  CLK,
  output [7:0] Output_bus_1,
  output [7:0] Output_bus_2,
  output [7:0] Output_bus_3,
  output [7:0] Output_bus_4
);

  wire and_1_out, and_2_out, and_3_out, and_4_out, counter_1_carry, counter_2_carry, counter_3_carry,
       counter_4_carry, counter_5_carry, d_ff_1_q, d_ff_2_q, d_ff_3_q, multiplexer_1_out, multiplexer_2_out,
       multiplexer_3_out, or_1_out, or_2_out, or_3_out, or_4_out;
  wire [3:0] multiplexer_4_out, multiplexer_5_out, multiplexer_6_out, multiplexer_7_out;

  Counter #(.width(12), .max('ha00)) counter_1 (
    .clk(CLK), .carry(counter_1_carry));  // open: clr, load, up, count, D, Q
  and and_1 (and_1_out, Input_6, ~Input_2);  // AND_Gate
  Multiplexer #(.enable("false")) multiplexer_1 (
    .in0(1'b0), .in1(counter_1_carry), .out(multiplexer_1_out), .sel(and_1_out));
  Multiplexer #(.enable("false")) multiplexer_2 (
    .in0(1'b0), .in1(counter_1_carry), .out(multiplexer_2_out), .sel(and_2_out));
  and and_2 (and_2_out, Input_7, ~Input_2);  // AND_Gate
  Multiplexer #(.enable("false")) multiplexer_3 (.in0(1'b0), .in1(CLK), .out(multiplexer_3_out), .sel(Input_2));
  Multiplexer #(.width(4), .enable("false")) multiplexer_4 (
    .in0(4'b0000), .in1(4'b1111), .out(multiplexer_4_out), .sel(Input_4));
  Counter #(.width(9), .max('h9f)) counter_2 (
    .clk(multiplexer_3_out), .carry(counter_2_carry));  // open: clr, load, up, count, D, Q
  Multiplexer #(.width(4), .enable("false")) multiplexer_5 (
    .in0(4'b0000), .in1(4'b1111), .out(multiplexer_5_out), .sel(and_3_out));
  and and_3 (and_3_out, Input_1, Input_4);
  and and_4 (and_4_out, ~Input_2, Input_5);  // AND_Gate
  Multiplexer #(.width(4), .enable("false")) multiplexer_6 (
    .in0(4'b1111), .in1(4'b0000), .out(multiplexer_6_out), .sel(Input_3));
  Multiplexer #(.width(4), .enable("false")) multiplexer_7 (
    .in0(4'b0000), .in1(4'b1111), .out(multiplexer_7_out), .sel(and_4_out));
  Counter #(.width(7), .max('h63)) counter_3 (
    .clr(multiplexer_7_out[0]), .load(multiplexer_4_out[0]), .up(multiplexer_6_out[0]), .clk(or_1_out),
    .D(Input_bus_1[6:0]), .carry(counter_3_carry), .Q(Output_bus_1[6:0]));  // open: count
  or or_1 (or_1_out, counter_2_carry, multiplexer_5_out[0]);
  Counter #(.width(6), .max('h3b)) counter_4 (
    .clr(multiplexer_7_out[1]), .load(multiplexer_4_out[1]), .up(multiplexer_6_out[1]), .clk(or_2_out),
    .D(Input_bus_2[5:0]), .carry(counter_4_carry), .Q(Output_bus_2[5:0]));  // open: count
  or or_2 (or_2_out, d_ff_1_q, multiplexer_5_out[1]);
  Counter #(.width(6), .max('h3b)) counter_5 (
    .clr(multiplexer_7_out[2]), .load(multiplexer_4_out[2]), .up(multiplexer_6_out[2]), .clk(or_3_out),
    .D(Input_bus_3[5:0]), .carry(counter_5_carry), .Q(Output_bus_3[5:0]));  // open: count
  or or_3 (or_3_out, d_ff_2_q, multiplexer_1_out, multiplexer_5_out[2]);
  Counter #(.width(5), .max('h17)) counter_6 (
    .clr(multiplexer_7_out[3]), .load(multiplexer_4_out[3]), .up(multiplexer_6_out[3]), .clk(or_4_out),
    .D(Input_bus_4[4:0]), .Q(Output_bus_4[4:0]));  // open: count, carry
  or or_4 (or_4_out, d_ff_3_q, multiplexer_2_out, multiplexer_5_out[3]);
  D_Flip_Flop d_ff_1 (.D(counter_3_carry), .clk(counter_2_carry), .Q(d_ff_1_q));  // open: Qn, preset, reset
  D_Flip_Flop d_ff_2 (.D(counter_4_carry), .clk(d_ff_1_q), .Q(d_ff_2_q));  // open: Qn, preset, reset
  D_Flip_Flop d_ff_3 (.D(counter_5_carry), .clk(d_ff_2_q), .Q(d_ff_3_q));  // open: Qn, preset, reset

  assign Output_bus_1[7] = 1'b0;
  assign Output_bus_2[7:6] = 2'b00;
  assign Output_bus_3[7:6] = 2'b00;
  assign Output_bus_4[7:5] = 3'b000;
endmodule
