// Logisim project FSM_ALL_test2.circ as structural Verilog
module DIGITAL_CLOCK (
  output Buzzer0,
  output Buzzer1
);

  wire alarm_1_buzzer, B0_out, B1_out, ButtonManager_1_chmode, ButtonManager_1_d0, ButtonManager_1_d1, clk,
       d_ff_3_q, DipSwitch_1_sw8, DipSwitch_1_sw9, DipSwitch_1_sw10, or_1_out, undriven;
  wire [1:0] d_ff_1_q, demultiplexer_1_out1, demultiplexer_1_out2, demultiplexer_1_out3,
       demultiplexer_1_out4, demultiplexer_1_out5, demultiplexer_1_out6;
  wire [2:0] FSM_ALL_1_output_3, STATE;
  wire [7:0] AllSegLeds_bis_1_sevseg_0, AllSegLeds_bis_1_sevseg_1, AllSegLeds_bis_1_sevseg_2,
       AllSegLeds_bis_1_sevseg_3, AllSegLeds_bis_1_sevseg_4, AllSegLeds_bis_1_sevseg_5, CAPITA_utccode;
  wire [23:0] Alarm_1, Alarm_2, Anim_1, Anim_2, Capita_1, Capita_2, Chrono_1, Chrono_2, LT_1, LT_2,
       multiplexer_1_out, multiplexer_2_out, Music_1, Music_2, Timer_1, Timer_2, UTC_1, UTC_2;

  DipSwitch #(.number(10)) DipSwitch_1 (
    .sw8(DipSwitch_1_sw8), .sw9(DipSwitch_1_sw9), .sw10(DipSwitch_1_sw10));  // open: sw1, sw2, sw3, sw4, sw5, sw6, sw7
  Multiplexer #(.select(3), .width(24), .enable("false")) multiplexer_1 (
    .in0(Anim_1), .in1(UTC_1), .in2(Chrono_1), .in3(Timer_1), .in4(Alarm_1), .in5(Capita_1), .in6(Music_1),
    .in7(LT_1), .out(multiplexer_1_out), .sel(STATE));
  Multiplexer #(.select(3), .width(24), .enable("false")) multiplexer_2 (
    .in0(Anim_2), .in1(UTC_2), .in2(Chrono_2), .in3(Timer_2), .in4(Alarm_2), .in5(Capita_2), .in6(Music_2),
    .in7(LT_2), .out(multiplexer_2_out), .sel(STATE));
  Clock clock_1 (.out(clk));
  or or_1 (or_1_out, d_ff_1_q[0], d_ff_1_q[1], d_ff_3_q);
  Button B1 (.out(B1_out));
  Button B0 (.out(B0_out));
  AllSegLeds_bis AllSegLeds_bis_1 (
    .sevsegCode_5(multiplexer_1_out[7:0]), .sevsegCode_4(multiplexer_1_out[15:8]),
    .sevsegCode_3(multiplexer_1_out[23:16]), .sevsegCode_2(multiplexer_2_out[7:0]),
    .sevsegCode_1(multiplexer_2_out[15:8]), .sevsegCode_0(multiplexer_2_out[23:16]),
    .sevseg_5(AllSegLeds_bis_1_sevseg_5), .sevseg_4(AllSegLeds_bis_1_sevseg_4),
    .sevseg_3(AllSegLeds_bis_1_sevseg_3), .sevseg_2(AllSegLeds_bis_1_sevseg_2),
    .sevseg_1(AllSegLeds_bis_1_sevseg_1), .sevseg_0(AllSegLeds_bis_1_sevseg_0));
  ButtonManager ButtonManager_1 (
    .DIP(DipSwitch_1_sw10), .RESET(or_1_out), .C1(d_ff_1_q[0]), .C0(d_ff_1_q[1]), .B1(B1_out), .B0(B0_out),
    .D1(ButtonManager_1_d1), .D0(ButtonManager_1_d0), .chMode(ButtonManager_1_chmode));
  _7_Segment_Display L1 (
    .g(AllSegLeds_bis_1_sevseg_5[0]), .f(AllSegLeds_bis_1_sevseg_5[1]), .a(AllSegLeds_bis_1_sevseg_5[6]),
    .b(AllSegLeds_bis_1_sevseg_5[5]), .e(AllSegLeds_bis_1_sevseg_5[2]), .d(AllSegLeds_bis_1_sevseg_5[3]),
    .c(AllSegLeds_bis_1_sevseg_5[4]), .dp(AllSegLeds_bis_1_sevseg_5[7]));
  D_Flip_Flop d_ff_1 (.D(ButtonManager_1_d1), .clk(clk), .Q(d_ff_1_q[0]));  // open: Qn, preset, reset
  _7_Segment_Display L2 (
    .g(AllSegLeds_bis_1_sevseg_4[0]), .f(AllSegLeds_bis_1_sevseg_4[1]), .a(AllSegLeds_bis_1_sevseg_4[6]),
    .b(AllSegLeds_bis_1_sevseg_4[5]), .e(AllSegLeds_bis_1_sevseg_4[2]), .d(AllSegLeds_bis_1_sevseg_4[3]),
    .c(AllSegLeds_bis_1_sevseg_4[4]), .dp(AllSegLeds_bis_1_sevseg_4[7]));
  D_Flip_Flop d_ff_2 (.D(ButtonManager_1_d0), .clk(clk), .Q(d_ff_1_q[1]));  // open: Qn, preset, reset
  D_Flip_Flop d_ff_3 (.D(ButtonManager_1_chmode), .clk(clk), .Q(d_ff_3_q));  // open: Qn, preset, reset
  _7_Segment_Display L3 (
    .g(AllSegLeds_bis_1_sevseg_3[0]), .f(AllSegLeds_bis_1_sevseg_3[1]), .a(AllSegLeds_bis_1_sevseg_3[6]),
    .b(AllSegLeds_bis_1_sevseg_3[5]), .e(AllSegLeds_bis_1_sevseg_3[2]), .d(AllSegLeds_bis_1_sevseg_3[3]),
    .c(AllSegLeds_bis_1_sevseg_3[4]), .dp(AllSegLeds_bis_1_sevseg_3[7]));
  _7_Segment_Display L4 (
    .g(AllSegLeds_bis_1_sevseg_2[0]), .f(AllSegLeds_bis_1_sevseg_2[1]), .a(AllSegLeds_bis_1_sevseg_2[6]),
    .b(AllSegLeds_bis_1_sevseg_2[5]), .e(AllSegLeds_bis_1_sevseg_2[2]), .d(AllSegLeds_bis_1_sevseg_2[3]),
    .c(AllSegLeds_bis_1_sevseg_2[4]), .dp(AllSegLeds_bis_1_sevseg_2[7]));
  _7_Segment_Display L5 (
    .g(AllSegLeds_bis_1_sevseg_1[0]), .f(AllSegLeds_bis_1_sevseg_1[1]), .a(AllSegLeds_bis_1_sevseg_1[6]),
    .b(AllSegLeds_bis_1_sevseg_1[5]), .e(AllSegLeds_bis_1_sevseg_1[2]), .d(AllSegLeds_bis_1_sevseg_1[3]),
    .c(AllSegLeds_bis_1_sevseg_1[4]), .dp(AllSegLeds_bis_1_sevseg_1[7]));
  _7_Segment_Display L6 (
    .g(AllSegLeds_bis_1_sevseg_0[0]), .f(AllSegLeds_bis_1_sevseg_0[1]), .a(AllSegLeds_bis_1_sevseg_0[6]),
    .b(AllSegLeds_bis_1_sevseg_0[5]), .e(AllSegLeds_bis_1_sevseg_0[2]), .d(AllSegLeds_bis_1_sevseg_0[3]),
    .c(AllSegLeds_bis_1_sevseg_0[4]), .dp(AllSegLeds_bis_1_sevseg_0[7]));
  FSM_ALL FSM_ALL_1 (
    .Input_1(d_ff_3_q), .Input_2(DipSwitch_1_sw10), .Output_1(FSM_ALL_1_output_3[2]),
    .Output_2(FSM_ALL_1_output_3[1]), .Output_3(FSM_ALL_1_output_3[0]));
  Demultiplexer #(.select(3), .width(2), .enable("false")) demultiplexer_1 (
    .out1(demultiplexer_1_out1), .out2(demultiplexer_1_out2), .out3(demultiplexer_1_out3),
    .out4(demultiplexer_1_out4), .out5(demultiplexer_1_out5), .out6(demultiplexer_1_out6), .in(d_ff_1_q),
    .sel(FSM_ALL_1_output_3));  // open: out0, out7
  hourFSM UTC (
    .RESET(DipSwitch_1_sw9), .B1_B0(demultiplexer_1_out1), .sevsegCode_5(UTC_1[7:0]),
    .sevsegCode_4(UTC_1[15:8]), .sevsegCode_3(UTC_1[23:16]), .sevsegCode_2(UTC_2[7:0]),
    .sevsegCode_1(UTC_2[15:8]), .sevsegCode_0(UTC_2[23:16]));
  CHRONO u_CHRONO_1 (
    .RESET(DipSwitch_1_sw9), .B1_B0(demultiplexer_1_out2), .Min_Led2(Chrono_1[7:0]),
    .Min_Led1(Chrono_1[15:8]), .Sec_Led2(Chrono_1[23:16]), .Sec_Led1(Chrono_2[7:0]),
    .Milli_Led2(Chrono_2[15:8]), .Milli_Led1(Chrono_2[23:16]));  // open: Hour_Led2, Hour_Led1
  ChangementFuseauHoraire_bis CAPITA (
    .RESET(DipSwitch_1_sw9), .B1_B0(demultiplexer_1_out5), .Letter1(Capita_1[7:0]), .Letter2(Capita_1[15:8]),
    .Letter3(Capita_1[23:16]), .Letter4(Capita_2[7:0]), .Letter5(Capita_2[15:8]), .Letter6(Capita_2[23:16]),
    .UTCCode(CAPITA_utccode));
  CTDOWN CTDOWN_1 (
    .DIP(DipSwitch_1_sw8), .B1_B0(demultiplexer_1_out3), .Hour_Led2(Timer_1[7:0]), .Hour_Led1(Timer_1[15:8]),
    .Min_Led2(Timer_1[23:16]), .Min_Led1(Timer_2[7:0]), .Sec_Led2(Timer_2[15:8]), .Sec_Led1(Timer_2[23:16]));
  MUSIC u_MUSIC_1 (
    .ALARM(undriven), .B1_B0(demultiplexer_1_out6), .RESET(DipSwitch_1_sw9), .Buzzer1(Buzzer1),
    .L1(Music_1[7:0]), .L2(Music_1[15:8]), .L3(Music_1[23:16]), .L4(Music_2[7:0]), .L5(Music_2[15:8]),
    .L6(Music_2[23:16]));  // open: LedAnim
  ANIMATION ANIMATION_1 (
    .RESET(DipSwitch_1_sw9), .State(FSM_ALL_1_output_3), .L1(Anim_1[7:0]), .L2(Anim_1[15:8]),
    .L3(Anim_1[23:16]), .L4(Anim_2[7:0]), .L5(Anim_2[15:8]), .L6(Anim_2[23:16]));
  AnimControl AnimControl_1 (.Transition(DipSwitch_1_sw10), .State(FSM_ALL_1_output_3), .Anim(STATE));
  alarm u_alarm_1 (
    .RESET(DipSwitch_1_sw9), .B1_B0(demultiplexer_1_out4), .SSDCode_5(UTC_1[7:0]), .SSDCode_4(UTC_1[15:8]),
    .SSDCode_3(UTC_1[23:16]), .SSDCode_2(UTC_2[7:0]), .sevsegCode_5(Alarm_1[7:0]),
    .sevsegCode_4(Alarm_1[15:8]), .sevsegCode_3(Alarm_1[23:16]), .sevsegCode_2(Alarm_2[7:0]),
    .sevsegCode_1(Alarm_2[15:8]), .sevsegCode_0(Alarm_2[23:16]), .BUZZER(alarm_1_buzzer));
  changeTimeZone changeTimeZone_1 (
    .SSDCode_5(UTC_1[7:0]), .SSDCode_4(UTC_1[15:8]), .SSDCode_3(UTC_1[23:16]), .SSDCode_2(UTC_2[7:0]),
    .SSDCode_1(UTC_2[15:8]), .SSDCode_0(UTC_2[23:16]), .UTCCode_8(CAPITA_utccode), .sevsegCode_5(LT_1[7:0]),
    .sevsegCode_4(LT_1[15:8]), .sevsegCode_3(LT_1[23:16]), .sevsegCode_2(LT_2[7:0]),
    .sevsegCode_1(LT_2[15:8]), .sevsegCode_0(LT_2[23:16]));

  assign Buzzer0 = 1'b0;

  // Notes on the sheet:
  //   LedGauche
  //   LedDroit
endmodule

module FSM_ALL (
  input  Input_1,
  input  Input_2,
  output Output_1,
  output Output_2,
  output Output_3
);

  wire and_1_out, clock_1_out, not_1_out, not_2_out, not_3_out, TransLogic_1_d0, TransLogic_1_d1,
       TransLogic_1_d2;

  Clock clock_1 (.out(clock_1_out));
  and and_1 (and_1_out, Input_1, Input_2);
  TransLogic TransLogic_1 (
    .B1(and_1_out), .C2(Output_1), .C1(Output_2), .C0(Output_3), .D2(TransLogic_1_d2), .D1(TransLogic_1_d1),
    .D0(TransLogic_1_d0));
  S_R_Flip_Flop s_r_ff_1 (
    .S(TransLogic_1_d2), .R(not_1_out), .clk(clock_1_out), .Q(Output_1));  // open: reset, Qn, preset
  not not_1 (not_1_out, TransLogic_1_d2);
  S_R_Flip_Flop s_r_ff_2 (
    .S(TransLogic_1_d1), .R(not_2_out), .clk(clock_1_out), .Q(Output_2));  // open: reset, Qn, preset
  not not_2 (not_2_out, TransLogic_1_d1);
  S_R_Flip_Flop s_r_ff_3 (
    .S(TransLogic_1_d0), .R(not_3_out), .clk(clock_1_out), .Q(Output_3));  // open: reset, Qn, preset
  not not_3 (not_3_out, TransLogic_1_d0);
endmodule

module ButtonManager (
  input  DIP,
  input  RESET,
  input  C1,
  input  C0,
  input  B1,
  input  B0,
  output D1,
  output D0,
  output chMode
);

  wire and_3_out, and_4_out, d_ff_1_q, d_ff_1_qn, d_ff_2_q, d_ff_2_qn, not_1_out, not_2_out, not_3_out,
       not_4_out, not_5_out, not_6_out, not_7_out, not_8_out, not_9_out, not_10_out;

  D_Flip_Flop d_ff_1 (.D(d_ff_1_qn), .clk(B1), .Q(d_ff_1_q), .Qn(d_ff_1_qn), .reset(RESET));  // open: preset
  D_Flip_Flop d_ff_2 (.D(d_ff_2_qn), .clk(B0), .Q(d_ff_2_q), .Qn(d_ff_2_qn), .reset(RESET));  // open: preset
  not not_1 (not_1_out, DIP);
  not not_2 (not_2_out, RESET);
  not not_3 (not_3_out, DIP);
  not not_4 (not_4_out, RESET);
  not not_5 (not_5_out, RESET);
  not not_6 (not_6_out, C1);
  not not_7 (not_7_out, C0);
  not not_8 (not_8_out, RESET);
  not not_9 (not_9_out, C1);
  not not_10 (not_10_out, d_ff_1_q);
  and and_1 (D1, not_1_out, not_2_out, d_ff_1_q);
  and and_2 (D0, not_3_out, not_4_out, d_ff_2_q);
  and and_3 (and_3_out, DIP, not_5_out, not_6_out, not_7_out, d_ff_2_q);
  and and_4 (and_4_out, DIP, not_8_out, not_9_out, not_10_out, d_ff_2_q);
  or or_1 (chMode, and_3_out, and_4_out);
endmodule

module TransLogic (
  input  B1,
  input  C2,
  input  C1,
  input  C0,
  output D2,
  output D1,
  output D0
);

  wire and_1_out, and_2_out, and_3_out, and_4_out, and_5_out, and_6_out, and_7_out, and_8_out, and_9_out,
       and_10_out, not_1_out, not_2_out, not_3_out, not_4_out, not_5_out, not_6_out, not_7_out, not_8_out,
       not_9_out;

  not not_1 (not_1_out, B1);
  not not_2 (not_2_out, C1);
  not not_3 (not_3_out, C0);
  not not_4 (not_4_out, C2);
  not not_5 (not_5_out, B1);
  not not_6 (not_6_out, C0);
  not not_7 (not_7_out, C1);
  not not_8 (not_8_out, B1);
  not not_9 (not_9_out, C0);
  and and_1 (and_1_out, not_1_out, C2);
  and and_2 (and_2_out, C2, not_2_out);
  and and_3 (and_3_out, C2, not_3_out);
  and and_4 (and_4_out, B1, not_4_out, C1, C0);
  and and_5 (and_5_out, not_5_out, C1);
  and and_6 (and_6_out, C1, not_6_out);
  and and_7 (and_7_out, B1, not_7_out, C0);
  and and_8 (and_8_out, not_8_out, C0);
  and and_9 (and_9_out, B1, not_9_out);
  and and_10 (and_10_out, B1, C2, C1);
  or or_1 (D2, and_1_out, and_2_out, and_3_out, and_4_out);
  or or_2 (D1, and_5_out, and_6_out, and_7_out);
  or or_3 (D0, and_8_out, and_9_out, and_10_out);
endmodule

module AllSegLeds (
  input  [7:0] Input_bus_1,
  input  [7:0] Input_bus_2,
  input  [7:0] Input_bus_3,
  input  [7:0] Input_bus_4,
  input  [7:0] Input_bus_5,
  input  [7:0] Input_bus_6,
  output [7:0] Output_bus_1,
  output [7:0] Output_bus_2,
  output [7:0] Output_bus_3,
  output [7:0] Output_bus_4,
  output [7:0] Output_bus_5,
  output [7:0] Output_bus_6
);

  SegLed1 SegLed1_1 (.Input_bus_1(Input_bus_1), .Output_bus_1(Output_bus_1));
  SegLed1 SegLed1_2 (.Input_bus_1(Input_bus_2), .Output_bus_1(Output_bus_2));
  SegLed1 SegLed1_3 (.Input_bus_1(Input_bus_3), .Output_bus_1(Output_bus_3));
  SegLed1 SegLed1_4 (.Input_bus_1(Input_bus_4), .Output_bus_1(Output_bus_4));
  SegLed1 SegLed1_5 (.Input_bus_1(Input_bus_5), .Output_bus_1(Output_bus_5));
  SegLed1 SegLed1_6 (.Input_bus_1(Input_bus_6), .Output_bus_1(Output_bus_6));
endmodule

module SegLed1 (
  input  [7:0] Input_bus_1,
  output [7:0] Output_bus_1
);

  DecoderToSegLed DecoderToSegLed_1 (
    .Input_1(Input_bus_1[4]), .Input_2(Input_bus_1[3]), .Input_3(Input_bus_1[2]), .Input_4(Input_bus_1[1]),
    .Input_5(Input_bus_1[0]), .Output_1(Output_bus_1[0]), .Output_2(Output_bus_1[1]),
    .Output_3(Output_bus_1[2]), .Output_4(Output_bus_1[3]), .Output_5(Output_bus_1[4]),
    .Output_6(Output_bus_1[5]), .Output_7(Output_bus_1[6]));
endmodule

module DecoderToSegLed (
  input  Input_1,
  input  Input_2,
  input  Input_3,
  input  Input_4,
  input  Input_5,
  output Output_1,
  output Output_2,
  output Output_3,
  output Output_4,
  output Output_5,
  output Output_6,
  output Output_7
);

  wire and_1_out, and_2_out, and_3_out, and_4_out, and_5_out, and_6_out, and_7_out, and_8_out, and_9_out,
       and_10_out, and_11_out, and_12_out, and_13_out, and_14_out, and_15_out, and_16_out, and_17_out,
       and_18_out, and_19_out, and_20_out, and_21_out, and_22_out, and_23_out, and_24_out, and_25_out,
       and_26_out, and_27_out, and_28_out, and_29_out, and_30_out, and_31_out, and_32_out, and_33_out,
       and_34_out, and_35_out, and_36_out, and_37_out, and_38_out, and_39_out, and_40_out, and_41_out,
       and_42_out, and_43_out, and_44_out, and_45_out, and_46_out, and_47_out, and_48_out, and_49_out,
       and_50_out, and_51_out, and_52_out, and_53_out, and_54_out, not_1_out, not_2_out, not_3_out,
       not_4_out, not_5_out, not_6_out, not_7_out, not_8_out, not_9_out, not_10_out, not_11_out, not_12_out,
       not_13_out, not_14_out, not_15_out, not_16_out, not_17_out, not_18_out, not_19_out, not_20_out,
       not_21_out, not_22_out, not_23_out, not_24_out, not_25_out, not_26_out, not_27_out, not_28_out,
       not_29_out, not_30_out, not_31_out, not_32_out, not_33_out, not_34_out, not_35_out, not_36_out,
       not_37_out, not_38_out, not_39_out, not_40_out, not_41_out, not_42_out, not_43_out, not_44_out,
       not_45_out, not_46_out, not_47_out, not_48_out, not_49_out, not_50_out, not_51_out, not_52_out,
       not_53_out, not_54_out, not_55_out, not_56_out, not_57_out, not_58_out, not_59_out, not_60_out,
       not_61_out, not_62_out, not_63_out, not_64_out, not_65_out, not_66_out, not_67_out, not_68_out,
       not_69_out, not_70_out, not_71_out, not_72_out, not_73_out, not_74_out, not_75_out, not_76_out,
       not_77_out, not_78_out, not_79_out, not_80_out, not_81_out, not_82_out, not_83_out, not_84_out,
       not_85_out, not_86_out, not_87_out, not_88_out, not_89_out, not_90_out, not_91_out, not_92_out,
       not_93_out, not_94_out, not_95_out, not_96_out, not_97_out, not_98_out, not_99_out;

  not not_1 (not_1_out, Input_3);
  not not_2 (not_2_out, Input_4);
  not not_3 (not_3_out, Input_5);
  not not_4 (not_4_out, Input_1);
  not not_5 (not_5_out, Input_2);
  not not_6 (not_6_out, Input_2);
  not not_7 (not_7_out, Input_4);
  not not_8 (not_8_out, Input_1);
  not not_9 (not_9_out, Input_1);
  not not_10 (not_10_out, Input_5);
  not not_11 (not_11_out, Input_3);
  not not_12 (not_12_out, Input_4);
  not not_13 (not_13_out, Input_3);
  not not_14 (not_14_out, Input_1);
  not not_15 (not_15_out, Input_2);
  not not_16 (not_16_out, Input_4);
  not not_17 (not_17_out, Input_5);
  not not_18 (not_18_out, Input_1);
  not not_19 (not_19_out, Input_3);
  not not_20 (not_20_out, Input_5);
  not not_21 (not_21_out, Input_3);
  not not_22 (not_22_out, Input_4);
  not not_23 (not_23_out, Input_2);
  not not_24 (not_24_out, Input_3);
  not not_25 (not_25_out, Input_1);
  not not_26 (not_26_out, Input_2);
  not not_27 (not_27_out, Input_1);
  not not_28 (not_28_out, Input_4);
  not not_29 (not_29_out, Input_2);
  not not_30 (not_30_out, Input_4);
  not not_31 (not_31_out, Input_5);
  not not_32 (not_32_out, Input_2);
  not not_33 (not_33_out, Input_3);
  not not_34 (not_34_out, Input_4);
  not not_35 (not_35_out, Input_2);
  not not_36 (not_36_out, Input_3);
  not not_37 (not_37_out, Input_4);
  not not_38 (not_38_out, Input_1);
  not not_39 (not_39_out, Input_2);
  not not_40 (not_40_out, Input_1);
  not not_41 (not_41_out, Input_3);
  not not_42 (not_42_out, Input_5);
  not not_43 (not_43_out, Input_1);
  not not_44 (not_44_out, Input_2);
  not not_45 (not_45_out, Input_3);
  not not_46 (not_46_out, Input_5);
  not not_47 (not_47_out, Input_1);
  not not_48 (not_48_out, Input_2);
  not not_49 (not_49_out, Input_5);
  not not_50 (not_50_out, Input_3);
  not not_51 (not_51_out, Input_1);
  not not_52 (not_52_out, Input_4);
  not not_53 (not_53_out, Input_1);
  not not_54 (not_54_out, Input_4);
  not not_55 (not_55_out, Input_4);
  not not_56 (not_56_out, Input_5);
  not not_57 (not_57_out, Input_2);
  not not_58 (not_58_out, Input_4);
  not not_59 (not_59_out, Input_5);
  not not_60 (not_60_out, Input_2);
  not not_61 (not_61_out, Input_1);
  not not_62 (not_62_out, Input_3);
  not not_63 (not_63_out, Input_5);
  not not_64 (not_64_out, Input_2);
  not not_65 (not_65_out, Input_5);
  not not_66 (not_66_out, Input_3);
  not not_67 (not_67_out, Input_5);
  not not_68 (not_68_out, Input_1);
  not not_69 (not_69_out, Input_4);
  not not_70 (not_70_out, Input_2);
  not not_71 (not_71_out, Input_4);
  not not_72 (not_72_out, Input_2);
  not not_73 (not_73_out, Input_4);
  not not_74 (not_74_out, Input_5);
  not not_75 (not_75_out, Input_1);
  not not_76 (not_76_out, Input_5);
  not not_77 (not_77_out, Input_2);
  not not_78 (not_78_out, Input_4);
  not not_79 (not_79_out, Input_3);
  not not_80 (not_80_out, Input_1);
  not not_81 (not_81_out, Input_5);
  not not_82 (not_82_out, Input_2);
  not not_83 (not_83_out, Input_3);
  not not_84 (not_84_out, Input_5);
  not not_85 (not_85_out, Input_2);
  not not_86 (not_86_out, Input_4);
  not not_87 (not_87_out, Input_1);
  not not_88 (not_88_out, Input_3);
  not not_89 (not_89_out, Input_1);
  not not_90 (not_90_out, Input_5);
  not not_91 (not_91_out, Input_1);
  not not_92 (not_92_out, Input_2);
  not not_93 (not_93_out, Input_4);
  not not_94 (not_94_out, Input_3);
  not not_95 (not_95_out, Input_1);
  not not_96 (not_96_out, Input_3);
  not not_97 (not_97_out, Input_4);
  not not_98 (not_98_out, Input_2);
  not not_99 (not_99_out, Input_5);
  and and_1 (and_1_out, not_1_out, not_2_out, not_3_out);
  and and_2 (and_2_out, not_4_out, not_5_out, Input_4);
  and and_3 (and_3_out, not_6_out, Input_3, not_7_out, Input_5);
  and and_4 (and_4_out, not_8_out, Input_3, Input_4);
  and and_5 (and_5_out, not_9_out, Input_2, not_10_out);
  and and_6 (and_6_out, Input_2, not_11_out, not_12_out);
  and and_7 (and_7_out, Input_1, Input_2, not_13_out, Input_5);
  and and_8 (and_8_out, not_14_out, not_15_out, not_16_out, not_17_out);
  and and_9 (and_9_out, not_18_out, not_19_out, not_20_out);
  and and_10 (and_10_out, not_21_out, not_22_out);
  and and_11 (and_11_out, not_23_out, not_24_out, Input_5);
  and and_12 (and_12_out, not_25_out, not_26_out, Input_4, Input_5);
  and and_13 (and_13_out, not_27_out, Input_2, not_28_out, Input_5);
  and and_14 (and_14_out, Input_1, not_29_out, not_30_out, Input_5);
  and and_15 (and_15_out, Input_1, Input_2, Input_3, Input_4, not_31_out);
  and and_16 (and_16_out, not_32_out, not_33_out, not_34_out);
  and and_17 (and_17_out, not_35_out, Input_5);
  and and_18 (and_18_out, not_36_out, Input_5);
  and and_19 (and_19_out, not_37_out, Input_5);
  and and_20 (and_20_out, not_38_out, not_39_out, Input_3);
  and and_21 (and_21_out, not_40_out, Input_2, not_41_out);
  and and_22 (and_22_out, Input_1, Input_3, Input_4, not_42_out);
  and and_23 (and_23_out, not_43_out, not_44_out, not_45_out, not_46_out);
  and and_24 (and_24_out, not_47_out, not_48_out, Input_4, not_49_out);
  and and_25 (and_25_out, not_50_out, Input_4, Input_5);
  and and_26 (and_26_out, not_51_out, Input_3, not_52_out, Input_5);
  and and_27 (and_27_out, not_53_out, Input_2, not_54_out);
  and and_28 (and_28_out, Input_2, Input_3, not_55_out);
  and and_29 (and_29_out, Input_2, Input_3, not_56_out);
  and and_30 (and_30_out, Input_1, not_57_out, not_58_out, not_59_out);
  and and_31 (and_31_out, Input_1, not_60_out, Input_4, Input_5);
  and and_32 (and_32_out, not_61_out, not_62_out, not_63_out);
  and and_33 (and_33_out, not_64_out, Input_4, not_65_out);
  and and_34 (and_34_out, Input_2, not_66_out, not_67_out);
  and and_35 (and_35_out, not_68_out, Input_2, Input_4);
  and and_36 (and_36_out, Input_2, Input_3, not_69_out);
  and and_37 (and_37_out, Input_1, not_70_out, not_71_out, Input_5);
  and and_38 (and_38_out, Input_1, not_72_out, Input_3);
  and and_39 (and_39_out, not_73_out, not_74_out);
  and and_40 (and_40_out, not_75_out, Input_3, not_76_out);
  and and_41 (and_41_out, not_77_out, Input_3, not_78_out);
  and and_42 (and_42_out, Input_2, not_79_out, Input_5);
  and and_43 (and_43_out, not_80_out, Input_2, Input_4);
  and and_44 (and_44_out, Input_2, Input_3, not_81_out);
  and and_45 (and_45_out, Input_1, not_82_out, not_83_out, not_84_out);
  and and_46 (and_46_out, Input_1, not_85_out, not_86_out);
  and and_47 (and_47_out, not_87_out, not_88_out, Input_4);
  and and_48 (and_48_out, not_89_out, Input_4, not_90_out);
  and and_49 (and_49_out, not_91_out, not_92_out, Input_3, not_93_out);
  and and_50 (and_50_out, Input_2, not_94_out);
  and and_51 (and_51_out, not_95_out, Input_2, Input_5);
  and and_52 (and_52_out, Input_1, not_96_out, not_97_out);
  and and_53 (and_53_out, Input_1, not_98_out, Input_3, Input_4);
  and and_54 (and_54_out, Input_1, Input_2, not_99_out);
  or or_1 (Output_1, and_1_out, and_2_out, and_3_out, and_4_out, and_5_out, and_6_out, and_7_out);
  or or_2 (Output_3, and_16_out, and_17_out, and_18_out, and_19_out, and_20_out, and_21_out, and_22_out);
  or or_3 (Output_5, and_32_out, and_33_out, and_34_out, and_35_out, and_36_out, and_37_out, and_38_out);
  or or_4 (Output_2, and_8_out, and_9_out, and_10_out, and_11_out, and_12_out, and_13_out, and_14_out, and_15_out);
  or or_5 (Output_4, and_23_out, and_24_out, and_25_out, and_26_out, and_27_out, and_28_out, and_29_out, and_30_out, and_31_out);
  or or_6 (Output_6, and_39_out, and_40_out, and_41_out, and_42_out, and_43_out, and_44_out, and_45_out, and_46_out);
  or or_7 (Output_7, and_47_out, and_48_out, and_49_out, and_50_out, and_51_out, and_52_out, and_53_out, and_54_out);
endmodule

module DecoderToSegLed_bis (
  input  e5,
  input  e4,
  input  e3,
  input  e2,
  input  e1,
  input  e0,
  output o,
  output a,
  output b,
  output c,
  output d,
  output e,
  output f,
  output g
);

  wire and_1_out, and_2_out, and_3_out, and_4_out, and_5_out, and_6_out, and_7_out, and_8_out, and_9_out,
       and_10_out, and_11_out, and_12_out, and_13_out, and_14_out, and_15_out, and_16_out, and_17_out,
       and_18_out, and_19_out, and_20_out, and_21_out, and_22_out, and_23_out, and_24_out, and_25_out,
       and_26_out, and_27_out, and_28_out, and_29_out, and_30_out, and_31_out, and_32_out, and_33_out,
       and_34_out, and_35_out, and_36_out, and_37_out, and_38_out, and_39_out, and_40_out, and_41_out,
       and_42_out, and_43_out, and_44_out, and_45_out, and_46_out, and_47_out, and_48_out, and_49_out,
       and_50_out, and_51_out, and_52_out, and_53_out, and_54_out, and_55_out, and_56_out, and_57_out,
       and_58_out, not_1_out, not_2_out, not_3_out, not_4_out, not_5_out, not_6_out, not_7_out, not_8_out,
       not_9_out, not_10_out, not_11_out, not_12_out, not_13_out, not_14_out, not_15_out, not_16_out,
       not_17_out, not_18_out, not_19_out, not_20_out, not_21_out, not_22_out, not_23_out, not_24_out,
       not_25_out, not_26_out, not_27_out, not_28_out, not_29_out, not_30_out, not_31_out, not_32_out,
       not_33_out, not_34_out, not_35_out, not_36_out, not_37_out, not_38_out, not_39_out, not_40_out,
       not_41_out, not_42_out, not_43_out, not_44_out, not_45_out, not_46_out, not_47_out, not_48_out,
       not_49_out, not_50_out, not_51_out, not_52_out, not_53_out, not_54_out, not_55_out, not_56_out,
       not_57_out, not_58_out, not_59_out, not_60_out, not_61_out, not_62_out, not_63_out, not_64_out,
       not_65_out, not_66_out, not_67_out, not_68_out, not_69_out, not_70_out, not_71_out, not_72_out,
       not_73_out, not_74_out, not_75_out, not_76_out, not_77_out, not_78_out, not_79_out, not_80_out,
       not_81_out, not_82_out, not_83_out, not_84_out, not_85_out, not_86_out, not_87_out, not_88_out,
       not_89_out, not_90_out, not_91_out, not_92_out, not_93_out, not_94_out, not_95_out, not_96_out,
       not_97_out, not_98_out, not_99_out, not_100_out, not_101_out;

  and and_1 (and_1_out, e5, not_1_out);
  not not_1 (not_1_out, e4);
  and and_2 (and_2_out, e5, not_2_out);
  not not_2 (not_2_out, e3);
  and and_3 (and_3_out, e5, not_3_out);
  not not_3 (not_3_out, e2);
  and and_4 (and_4_out, e5, not_4_out);
  not not_4 (not_4_out, e1);
  and and_5 (and_5_out, e5, not_5_out);
  not not_5 (not_5_out, e0);
  not not_6 (not_6_out, e2);
  not not_7 (not_7_out, e1);
  not not_8 (not_8_out, e0);
  not not_9 (not_9_out, e4);
  not not_10 (not_10_out, e3);
  not not_11 (not_11_out, e3);
  not not_12 (not_12_out, e1);
  not not_13 (not_13_out, e4);
  not not_14 (not_14_out, e4);
  not not_15 (not_15_out, e0);
  not not_16 (not_16_out, e2);
  not not_17 (not_17_out, e1);
  not not_18 (not_18_out, e2);
  not not_19 (not_19_out, e4);
  not not_20 (not_20_out, e3);
  not not_21 (not_21_out, e1);
  not not_22 (not_22_out, e0);
  not not_23 (not_23_out, e4);
  not not_24 (not_24_out, e2);
  not not_25 (not_25_out, e0);
  not not_26 (not_26_out, e3);
  not not_27 (not_27_out, e2);
  not not_28 (not_28_out, e4);
  not not_29 (not_29_out, e3);
  not not_30 (not_30_out, e2);
  not not_31 (not_31_out, e1);
  not not_32 (not_32_out, e4);
  not not_33 (not_33_out, e1);
  not not_34 (not_34_out, e3);
  not not_35 (not_35_out, e1);
  not not_36 (not_36_out, e0);
  not not_37 (not_37_out, e3);
  not not_38 (not_38_out, e2);
  not not_39 (not_39_out, e1);
  not not_40 (not_40_out, e3);
  not not_41 (not_41_out, e2);
  not not_42 (not_42_out, e1);
  not not_43 (not_43_out, e4);
  not not_44 (not_44_out, e3);
  not not_45 (not_45_out, e4);
  not not_46 (not_46_out, e2);
  not not_47 (not_47_out, e0);
  not not_48 (not_48_out, e4);
  not not_49 (not_49_out, e3);
  not not_50 (not_50_out, e2);
  not not_51 (not_51_out, e0);
  not not_52 (not_52_out, e4);
  not not_53 (not_53_out, e3);
  not not_54 (not_54_out, e0);
  not not_55 (not_55_out, e2);
  not not_56 (not_56_out, e4);
  not not_57 (not_57_out, e1);
  not not_58 (not_58_out, e4);
  not not_59 (not_59_out, e1);
  not not_60 (not_60_out, e1);
  not not_61 (not_61_out, e0);
  not not_62 (not_62_out, e3);
  not not_63 (not_63_out, e1);
  not not_64 (not_64_out, e0);
  not not_65 (not_65_out, e3);
  not not_66 (not_66_out, e2);
  and and_6 (and_6_out, not_66_out, not_67_out);
  not not_67 (not_67_out, e0);
  not not_68 (not_68_out, e4);
  and and_7 (and_7_out, not_68_out, e1, not_69_out);
  not not_69 (not_69_out, e0);
  not not_70 (not_70_out, e4);
  and and_8 (and_8_out, not_70_out, e3, e1);
  and and_9 (and_9_out, e3, e2, not_71_out);
  not not_71 (not_71_out, e1);
  not not_72 (not_72_out, e3);
  and and_10 (and_10_out, e4, not_72_out, not_73_out);
  not not_73 (not_73_out, e1);
  and and_11 (and_11_out, e4, not_74_out, e2);
  not not_74 (not_74_out, e3);
  not not_75 (not_75_out, e1);
  not not_76 (not_76_out, e0);
  not not_77 (not_77_out, e4);
  not not_78 (not_78_out, e0);
  not not_79 (not_79_out, e3);
  not not_80 (not_80_out, e1);
  not not_81 (not_81_out, e2);
  not not_82 (not_82_out, e4);
  not not_83 (not_83_out, e0);
  not not_84 (not_84_out, e3);
  not not_85 (not_85_out, e2);
  not not_86 (not_86_out, e0);
  not not_87 (not_87_out, e3);
  not not_88 (not_88_out, e1);
  not not_89 (not_89_out, e4);
  not not_90 (not_90_out, e2);
  not not_91 (not_91_out, e4);
  not not_92 (not_92_out, e0);
  not not_93 (not_93_out, e4);
  not not_94 (not_94_out, e3);
  not not_95 (not_95_out, e1);
  not not_96 (not_96_out, e2);
  not not_97 (not_97_out, e4);
  not not_98 (not_98_out, e2);
  not not_99 (not_99_out, e1);
  not not_100 (not_100_out, e3);
  not not_101 (not_101_out, e0);
  or or_1 (o, and_1_out, and_2_out, and_3_out, and_4_out, and_5_out);
  and and_12 (and_12_out, not_6_out, not_7_out, not_8_out);
  and and_13 (and_13_out, not_9_out, not_10_out, e1);
  and and_14 (and_14_out, not_11_out, e2, not_12_out, e0);
  and and_15 (and_15_out, not_13_out, e2, e1);
  and and_16 (and_16_out, not_14_out, e3, not_15_out);
  and and_17 (and_17_out, e3, not_16_out, not_17_out);
  and and_18 (and_18_out, e4, e3, not_18_out, e0);
  and and_19 (and_19_out, not_19_out, not_20_out, not_21_out, not_22_out);
  and and_20 (and_20_out, not_23_out, not_24_out, not_25_out);
  and and_21 (and_21_out, not_26_out, not_27_out, e0);
  and and_22 (and_22_out, not_28_out, not_29_out, e1, e0);
  and and_23 (and_23_out, e3, not_30_out, not_31_out);
  and and_24 (and_24_out, not_32_out, e3, not_33_out, e0);
  and and_25 (and_25_out, e4, not_34_out, not_35_out, e0);
  and and_26 (and_26_out, e4, e3, e2, e1, not_36_out);
  and and_27 (and_27_out, not_37_out, not_38_out, not_39_out);
  and and_28 (and_28_out, not_40_out, e0);
  and and_29 (and_29_out, not_41_out, e0);
  and and_30 (and_30_out, not_42_out, e0);
  and and_31 (and_31_out, not_43_out, not_44_out, e2);
  and and_32 (and_32_out, not_45_out, e3, not_46_out);
  and and_33 (and_33_out, e4, e2, e1, not_47_out);
  and and_34 (and_34_out, not_48_out, not_49_out, not_50_out, not_51_out);
  and and_35 (and_35_out, not_52_out, not_53_out, e1, not_54_out);
  and and_36 (and_36_out, not_55_out, e1, e0);
  and and_37 (and_37_out, not_56_out, e2, not_57_out, e0);
  and and_38 (and_38_out, not_58_out, e3, not_59_out);
  and and_39 (and_39_out, e3, e2, not_60_out);
  and and_40 (and_40_out, e3, e2, not_61_out);
  and and_41 (and_41_out, e4, not_62_out, not_63_out, not_64_out);
  and and_42 (and_42_out, e4, not_65_out, e1, e0);
  and and_43 (and_43_out, not_75_out, not_76_out);
  and and_44 (and_44_out, not_77_out, e2, not_78_out);
  and and_45 (and_45_out, not_79_out, e2, not_80_out);
  and and_46 (and_46_out, e3, not_81_out, e0);
  and and_47 (and_47_out, not_82_out, e3, e1);
  and and_48 (and_48_out, e3, e2, not_83_out);
  and and_49 (and_49_out, e4, not_84_out, not_85_out, not_86_out);
  and and_50 (and_50_out, e4, not_87_out, not_88_out);
  and and_51 (and_51_out, not_89_out, not_90_out, e1);
  and and_52 (and_52_out, not_91_out, e1, not_92_out);
  and and_53 (and_53_out, not_93_out, not_94_out, e2, not_95_out);
  and and_54 (and_54_out, e3, not_96_out);
  and and_55 (and_55_out, not_97_out, e3, e0);
  and and_56 (and_56_out, e4, not_98_out, not_99_out, e0);
  and and_57 (and_57_out, e4, not_100_out, e2, e1);
  and and_58 (and_58_out, e4, e3, not_101_out);
  or or_2 (a, and_12_out, and_13_out, and_14_out, and_15_out, and_16_out, and_17_out, and_18_out);
  or or_3 (b, and_19_out, and_20_out, and_21_out, and_22_out, and_23_out, and_24_out, and_25_out, and_26_out);
  or or_4 (c, and_27_out, and_28_out, and_29_out, and_30_out, and_31_out, and_32_out, and_33_out);
  or or_5 (d, and_34_out, and_35_out, and_36_out, and_37_out, and_38_out, and_39_out, and_40_out, and_41_out, and_42_out);
  or or_6 (e, and_6_out, and_7_out, and_8_out, and_9_out, and_10_out, and_11_out);
  or or_7 (f, and_43_out, and_44_out, and_45_out, and_46_out, and_47_out, and_48_out, and_49_out, and_50_out);
  or or_8 (g, and_51_out, and_52_out, and_53_out, and_54_out, and_55_out, and_56_out, and_57_out, and_58_out);
endmodule

module SegLed1_bis (
  input  [7:0] sevsegCode,
  output [7:0] sevensegment
);

  DecoderToSegLed_bis DecoderToSegLed_bis_1 (
    .e5(sevsegCode[7]), .e4(sevsegCode[4]), .e3(sevsegCode[3]), .e2(sevsegCode[2]), .e1(sevsegCode[1]),
    .e0(sevsegCode[0]), .o(sevensegment[7]), .a(sevensegment[6]), .b(sevensegment[5]), .c(sevensegment[4]),
    .d(sevensegment[3]), .e(sevensegment[2]), .f(sevensegment[1]), .g(sevensegment[0]));
endmodule

module AllSegLeds_bis (
  input  [7:0] sevsegCode_5,
  input  [7:0] sevsegCode_4,
  input  [7:0] sevsegCode_3,
  input  [7:0] sevsegCode_2,
  input  [7:0] sevsegCode_1,
  input  [7:0] sevsegCode_0,
  output [7:0] sevseg_5,
  output [7:0] sevseg_4,
  output [7:0] sevseg_3,
  output [7:0] sevseg_2,
  output [7:0] sevseg_1,
  output [7:0] sevseg_0
);

  SegLed1_bis SegLed1_bis_1 (.sevsegCode(sevsegCode_5), .sevensegment(sevseg_5));
  SegLed1_bis SegLed1_bis_2 (.sevsegCode(sevsegCode_4), .sevensegment(sevseg_4));
  SegLed1_bis SegLed1_bis_3 (.sevsegCode(sevsegCode_3), .sevensegment(sevseg_3));
  SegLed1_bis SegLed1_bis_4 (.sevsegCode(sevsegCode_2), .sevensegment(sevseg_2));
  SegLed1_bis SegLed1_bis_5 (.sevsegCode(sevsegCode_1), .sevensegment(sevseg_1));
  SegLed1_bis SegLed1_bis_6 (.sevsegCode(sevsegCode_0), .sevensegment(sevseg_0));
endmodule

module AnimControl (
  input  Transition,
  input  [2:0] State,
  output [2:0] Anim
);

  wire not_1_out, not_2_out, not_3_out;

  not not_1 (not_1_out, Transition);
  not not_2 (not_2_out, Transition);
  not not_3 (not_3_out, Transition);
  and and_1 (Anim[2], not_1_out, State[2]);
  and and_2 (Anim[1], not_2_out, State[1]);
  and and_3 (Anim[0], not_3_out, State[0]);
endmodule

module copypaste (
);

  wire [7:0] AllSegLeds_1_output_bus_1, AllSegLeds_1_output_bus_2, AllSegLeds_1_output_bus_3,
       AllSegLeds_1_output_bus_4, AllSegLeds_1_output_bus_5, AllSegLeds_1_output_bus_6;

  AllSegLeds AllSegLeds_1 (
    .Output_bus_1(AllSegLeds_1_output_bus_1), .Output_bus_2(AllSegLeds_1_output_bus_2),
    .Output_bus_3(AllSegLeds_1_output_bus_3), .Output_bus_4(AllSegLeds_1_output_bus_4),
    .Output_bus_5(AllSegLeds_1_output_bus_5), .Output_bus_6(AllSegLeds_1_output_bus_6));  // open: Input_bus_1, Input_bus_2, Input_bus_3, Input_bus_4, Input_bus_5, Input_bus_6
  _7_Segment_Display L_7_Segment_Display_1 (
    .g(AllSegLeds_1_output_bus_1[6]), .f(AllSegLeds_1_output_bus_1[5]), .a(AllSegLeds_1_output_bus_1[0]),
    .b(AllSegLeds_1_output_bus_1[1]), .e(AllSegLeds_1_output_bus_1[4]), .d(AllSegLeds_1_output_bus_1[3]),
    .c(AllSegLeds_1_output_bus_1[2]), .dp(AllSegLeds_1_output_bus_1[7]));
  _7_Segment_Display L_7_Segment_Display_2 (
    .g(AllSegLeds_1_output_bus_2[6]), .f(AllSegLeds_1_output_bus_2[5]), .a(AllSegLeds_1_output_bus_2[0]),
    .b(AllSegLeds_1_output_bus_2[1]), .e(AllSegLeds_1_output_bus_2[4]), .d(AllSegLeds_1_output_bus_2[3]),
    .c(AllSegLeds_1_output_bus_2[2]), .dp(AllSegLeds_1_output_bus_2[7]));
  _7_Segment_Display L_7_Segment_Display_3 (
    .g(AllSegLeds_1_output_bus_3[6]), .f(AllSegLeds_1_output_bus_3[5]), .a(AllSegLeds_1_output_bus_3[0]),
    .b(AllSegLeds_1_output_bus_3[1]), .e(AllSegLeds_1_output_bus_3[4]), .d(AllSegLeds_1_output_bus_3[3]),
    .c(AllSegLeds_1_output_bus_3[2]), .dp(AllSegLeds_1_output_bus_3[7]));
  _7_Segment_Display L_7_Segment_Display_4 (
    .g(AllSegLeds_1_output_bus_4[6]), .f(AllSegLeds_1_output_bus_4[5]), .a(AllSegLeds_1_output_bus_4[0]),
    .b(AllSegLeds_1_output_bus_4[1]), .e(AllSegLeds_1_output_bus_4[4]), .d(AllSegLeds_1_output_bus_4[3]),
    .c(AllSegLeds_1_output_bus_4[2]), .dp(AllSegLeds_1_output_bus_4[7]));
  _7_Segment_Display L_7_Segment_Display_5 (
    .g(AllSegLeds_1_output_bus_5[6]), .f(AllSegLeds_1_output_bus_5[5]), .a(AllSegLeds_1_output_bus_5[0]),
    .b(AllSegLeds_1_output_bus_5[1]), .e(AllSegLeds_1_output_bus_5[4]), .d(AllSegLeds_1_output_bus_5[3]),
    .c(AllSegLeds_1_output_bus_5[2]), .dp(AllSegLeds_1_output_bus_5[7]));
  _7_Segment_Display L_7_Segment_Display_6 (
    .g(AllSegLeds_1_output_bus_6[6]), .f(AllSegLeds_1_output_bus_6[5]), .a(AllSegLeds_1_output_bus_6[0]),
    .b(AllSegLeds_1_output_bus_6[1]), .e(AllSegLeds_1_output_bus_6[4]), .d(AllSegLeds_1_output_bus_6[3]),
    .c(AllSegLeds_1_output_bus_6[2]), .dp(AllSegLeds_1_output_bus_6[7]));
endmodule
