// Logisim project ChangementFuseau.circ as structural Verilog: 13 circuits, main circuit ChangementFuseauHoraire
module ChangementFuseauHoraire (
  input  RESET,
  input  [1:0] B1_B0,
  output [7:0] Letter1,
  output [7:0] Letter2,
  output [7:0] Letter3,
  output [7:0] Letter4,
  output [7:0] Letter5,
  output [7:0] Letter6,
  output [7:0] UTCCode
);

  wire [4:0] counter_1_q;

  Counter #(.width(5), .max('h10)) counter_1 (
    .clr(RESET), .up(1'b1), .count(1'b1), .clk(B1_B0[0]), .Q(counter_1_q));  // open: load, D, carry
  Capitales Capitales_1 (
    .a(counter_1_q[4]), .b(counter_1_q[3]), .x(UTCCode[4]), .c(counter_1_q[2]), .y(UTCCode[3]),
    .d(counter_1_q[1]), .z(UTCCode[2]), .e(counter_1_q[0]), .u(UTCCode[1]), .v(UTCCode[0]));
  CapitalLetter1 lettre1 (
    .a(counter_1_q[4]), .b(counter_1_q[3]), .c(counter_1_q[2]), .d(counter_1_q[1]), .e(counter_1_q[0]),
    .x(Letter1[4]), .y(Letter1[3]), .z(Letter1[2]), .u(Letter1[1]), .v(Letter1[0]));
  CapitalLetter2 lettre2 (
    .a(counter_1_q[4]), .b(counter_1_q[3]), .c(counter_1_q[2]), .d(counter_1_q[1]), .e(counter_1_q[0]),
    .x(Letter2[4]), .y(Letter2[3]), .z(Letter2[2]), .u(Letter2[1]), .v(Letter2[0]));
  CapitalLetter3 lettr3 (
    .a(counter_1_q[4]), .b(counter_1_q[3]), .c(counter_1_q[2]), .d(counter_1_q[1]), .e(counter_1_q[0]),
    .x(Letter3[4]), .y(Letter3[3]), .z(Letter3[2]), .u(Letter3[1]), .v(Letter3[0]));

  assign Letter4 = {8{1'b1}};
  assign Letter5 = {8{1'b1}};
  assign Letter6 = {8{1'b1}};
endmodule

module Capitales (
  input  a,
  input  b,
  input  c,
  input  d,
  input  e,
  output x,
  output y,
  output z,
  output u,
  output v
);

  wire and_1_out, and_2_out, and_3_out, and_4_out, and_5_out, and_6_out, and_7_out, and_8_out, and_9_out,
       and_10_out, not_1_out, not_2_out, not_3_out, not_4_out, not_5_out, not_6_out, not_7_out, not_8_out;

  and and_1 (and_1_out, b, d, e);
  and and_2 (and_2_out, b, c);
  or or_1 (y, b, a);
  not not_1 (not_1_out, b);
  not not_2 (not_2_out, b);
  not not_3 (not_3_out, e);
  not not_4 (not_4_out, d);
  not not_5 (not_5_out, b);
  not not_6 (not_6_out, c);
  not not_7 (not_7_out, d);
  not not_8 (not_8_out, e);
  or or_2 (x, and_1_out, and_2_out, a);
  and and_3 (and_3_out, not_1_out, c);
  and and_4 (and_4_out, c, d, e);
  and and_5 (and_5_out, not_2_out, d);
  and and_6 (and_6_out, d, not_3_out);
  and and_7 (and_7_out, b, c, not_4_out, e);
  and and_8 (and_8_out, not_5_out, e);
  and and_9 (and_9_out, not_6_out, not_7_out, e);
  and and_10 (and_10_out, b, c, not_8_out);
  or or_3 (z, and_3_out, and_4_out, a);
  or or_4 (u, and_5_out, and_6_out, and_7_out);
  or or_5 (v, and_8_out, and_9_out, and_10_out, a);
endmodule

module CapitalLetter1 (
  input  a,
  input  b,
  input  c,
  input  d,
  input  e,
  output x,
  output y,
  output z,
  output u,
  output v
);

  wire and_1_out, and_2_out, and_3_out, and_4_out, and_5_out, and_6_out, and_7_out, and_8_out, and_9_out,
       and_10_out, and_11_out, and_12_out, and_13_out, and_14_out, and_15_out, and_16_out, and_17_out,
       and_18_out, and_19_out, and_20_out, and_21_out, not_1_out, not_2_out, not_3_out, not_4_out, not_5_out,
       not_6_out, not_7_out, not_8_out, not_9_out, not_10_out, not_11_out, not_12_out, not_13_out,
       not_14_out, not_15_out, not_16_out, not_17_out, not_18_out, not_19_out, not_20_out, not_21_out,
       not_22_out, not_23_out, not_24_out, not_25_out, not_26_out, not_27_out, not_28_out, not_29_out,
       not_30_out;

  not not_1 (not_1_out, c);
  not not_2 (not_2_out, d);
  not not_3 (not_3_out, e);
  not not_4 (not_4_out, b);
  not not_5 (not_5_out, b);
  not not_6 (not_6_out, d);
  not not_7 (not_7_out, c);
  not not_8 (not_8_out, d);
  not not_9 (not_9_out, e);
  not not_10 (not_10_out, e);
  not not_11 (not_11_out, c);
  not not_12 (not_12_out, b);
  not not_13 (not_13_out, c);
  not not_14 (not_14_out, e);
  not not_15 (not_15_out, b);
  not not_16 (not_16_out, e);
  not not_17 (not_17_out, c);
  not not_18 (not_18_out, d);
  not not_19 (not_19_out, e);
  not not_20 (not_20_out, c);
  not not_21 (not_21_out, d);
  not not_22 (not_22_out, b);
  not not_23 (not_23_out, d);
  not not_24 (not_24_out, e);
  not not_25 (not_25_out, b);
  not not_26 (not_26_out, c);
  not not_27 (not_27_out, c);
  not not_28 (not_28_out, d);
  not not_29 (not_29_out, b);
  not not_30 (not_30_out, e);
  and and_1 (and_1_out, not_1_out, not_2_out, not_3_out);
  and and_2 (and_2_out, not_4_out, d, e);
  and and_3 (and_3_out, not_5_out, c, e);
  and and_4 (and_4_out, b, not_6_out);
  and and_5 (and_5_out, not_7_out, not_8_out, e);
  and and_6 (and_6_out, d, not_9_out);
  and and_7 (and_7_out, c, not_10_out);
  and and_8 (and_8_out, b, not_11_out);
  and and_9 (and_9_out, b, d);
  and and_10 (and_10_out, not_12_out, not_13_out, not_14_out);
  and and_11 (and_11_out, not_15_out, d, not_16_out);
  and and_12 (and_12_out, not_17_out, d);
  and and_13 (and_13_out, b, d, e);
  and and_14 (and_14_out, b, c, not_18_out, not_19_out);
  and and_15 (and_15_out, not_20_out, not_21_out, e);
  and and_16 (and_16_out, not_22_out, c, not_23_out);
  and and_17 (and_17_out, b, c, d, not_24_out);
  and and_18 (and_18_out, not_25_out, not_26_out, e);
  and and_19 (and_19_out, not_27_out, not_28_out, e);
  and and_20 (and_20_out, not_29_out, c, d);
  and and_21 (and_21_out, b, c, not_30_out);
  or or_1 (x, and_1_out, and_2_out, and_3_out, and_4_out);
  or or_2 (y, and_5_out, and_6_out, and_7_out, and_8_out, and_9_out);
  or or_3 (z, and_10_out, and_11_out, and_12_out, and_13_out, and_14_out);
  or or_4 (u, and_15_out, and_16_out, and_17_out);
  or or_5 (v, and_18_out, and_19_out, and_20_out, and_21_out, a);
endmodule

module CapitalLetter2 (
  input  a,
  input  b,
  input  c,
  input  d,
  input  e,
  output x,
  output y,
  output z,
  output u,
  output v
);

  wire and_1_out, and_2_out, and_3_out, and_4_out, and_5_out, and_6_out, and_7_out, and_8_out, and_9_out,
       and_10_out, and_11_out, and_12_out, and_13_out, and_14_out, and_15_out, and_16_out, and_17_out,
       and_18_out, and_19_out, not_1_out, not_2_out, not_3_out, not_4_out, not_5_out, not_6_out, not_7_out,
       not_8_out, not_9_out, not_10_out, not_11_out, not_12_out, not_13_out, not_14_out, not_15_out,
       not_16_out, not_17_out, not_18_out, not_19_out, not_20_out, not_21_out, not_22_out, not_23_out,
       not_24_out, not_25_out, not_26_out, not_27_out, not_28_out, not_29_out;

  not not_1 (not_1_out, b);
  not not_2 (not_2_out, c);
  not not_3 (not_3_out, d);
  not not_4 (not_4_out, e);
  not not_5 (not_5_out, b);
  not not_6 (not_6_out, c);
  not not_7 (not_7_out, d);
  not not_8 (not_8_out, e);
  not not_9 (not_9_out, b);
  not not_10 (not_10_out, b);
  not not_11 (not_11_out, c);
  not not_12 (not_12_out, d);
  not not_13 (not_13_out, c);
  not not_14 (not_14_out, d);
  not not_15 (not_15_out, d);
  not not_16 (not_16_out, e);
  not not_17 (not_17_out, a);
  not not_18 (not_18_out, b);
  not not_19 (not_19_out, a);
  not not_20 (not_20_out, c);
  not not_21 (not_21_out, a);
  not not_22 (not_22_out, a);
  not not_23 (not_23_out, b);
  not not_24 (not_24_out, d);
  not not_25 (not_25_out, e);
  not not_26 (not_26_out, b);
  not not_27 (not_27_out, c);
  not not_28 (not_28_out, d);
  not not_29 (not_29_out, e);
  and and_1 (and_1_out, not_1_out, not_2_out, not_3_out, not_4_out);
  and and_2 (and_2_out, not_5_out, not_6_out, d, e);
  and and_3 (and_3_out, c, not_7_out, e);
  and and_4 (and_4_out, b, c, not_8_out);
  and and_5 (and_5_out, not_9_out, d);
  and and_6 (and_6_out, not_10_out, c);
  and and_7 (and_7_out, b, not_11_out);
  and and_8 (and_8_out, b, not_12_out);
  and and_9 (and_9_out, not_13_out, not_14_out);
  and and_10 (and_10_out, b, not_15_out);
  and and_11 (and_11_out, b, c, not_16_out);
  and and_12 (and_12_out, not_17_out, not_18_out);
  and and_13 (and_13_out, not_19_out, not_20_out);
  and and_14 (and_14_out, not_21_out, d);
  and and_15 (and_15_out, d, e);
  and and_16 (and_16_out, not_22_out, not_23_out, not_24_out, not_25_out);
  and and_17 (and_17_out, not_26_out, not_27_out, d, e);
  and and_18 (and_18_out, c, not_28_out, e);
  and and_19 (and_19_out, b, d, not_29_out);
  or or_1 (x, and_1_out, and_2_out, and_3_out, and_4_out);
  or or_2 (y, e, and_5_out, and_6_out, and_7_out, and_8_out, a);
  or or_3 (z, and_9_out, and_10_out, and_11_out);
  or or_4 (u, and_12_out, and_13_out, and_14_out, and_15_out);
  or or_5 (v, and_16_out, and_17_out, and_18_out, and_19_out);
endmodule

module CapitalLetter3 (
  input  a,
  input  b,
  input  c,
  input  d,
  input  e,
  output x,
  output y,
  output z,
  output u,
  output v
);

  wire and_1_out, and_2_out, and_3_out, and_4_out, and_5_out, and_6_out, and_7_out, and_8_out, and_9_out,
       and_10_out, and_11_out, and_12_out, and_13_out, and_14_out, and_15_out, and_16_out, and_17_out,
       and_18_out, and_19_out, and_20_out, and_21_out, not_1_out, not_2_out, not_3_out, not_4_out, not_5_out,
       not_6_out, not_7_out, not_8_out, not_9_out, not_10_out, not_11_out, not_12_out, not_13_out,
       not_14_out, not_15_out, not_16_out, not_17_out, not_18_out, not_19_out, not_20_out, not_21_out,
       not_22_out, not_23_out, not_24_out, not_25_out, not_26_out, not_27_out, not_28_out, not_29_out,
       not_30_out, not_31_out, not_32_out, not_33_out, not_34_out, not_35_out;

  not not_1 (not_1_out, a);
  not not_2 (not_2_out, c);
  not not_3 (not_3_out, d);
  not not_4 (not_4_out, a);
  not not_5 (not_5_out, c);
  not not_6 (not_6_out, e);
  not not_7 (not_7_out, b);
  not not_8 (not_8_out, a);
  not not_9 (not_9_out, b);
  not not_10 (not_10_out, c);
  not not_11 (not_11_out, b);
  not not_12 (not_12_out, e);
  not not_13 (not_13_out, d);
  not not_14 (not_14_out, e);
  not not_15 (not_15_out, c);
  not not_16 (not_16_out, e);
  not not_17 (not_17_out, c);
  not not_18 (not_18_out, d);
  not not_19 (not_19_out, e);
  not not_20 (not_20_out, b);
  not not_21 (not_21_out, b);
  not not_22 (not_22_out, c);
  not not_23 (not_23_out, a);
  not not_24 (not_24_out, c);
  not not_25 (not_25_out, d);
  not not_26 (not_26_out, a);
  not not_27 (not_27_out, c);
  not not_28 (not_28_out, e);
  not not_29 (not_29_out, a);
  not not_30 (not_30_out, d);
  not not_31 (not_31_out, b);
  not not_32 (not_32_out, d);
  not not_33 (not_33_out, e);
  not not_34 (not_34_out, c);
  not not_35 (not_35_out, d);
  and and_1 (and_1_out, not_1_out, not_2_out, not_3_out);
  and and_2 (and_2_out, not_4_out, not_5_out, not_6_out);
  and and_3 (and_3_out, not_7_out, c, e);
  and and_4 (and_4_out, not_8_out, b, d);
  and and_5 (and_5_out, b, d, e);
  and and_6 (and_6_out, not_9_out, not_10_out, e);
  and and_7 (and_7_out, not_11_out, c, not_12_out);
  and and_8 (and_8_out, c, not_13_out, not_14_out);
  and and_9 (and_9_out, b, not_15_out, d, not_16_out);
  and and_10 (and_10_out, b, c, e);
  and and_11 (and_11_out, not_17_out, not_18_out, not_19_out);
  and and_12 (and_12_out, not_20_out, d, e);
  and and_13 (and_13_out, not_21_out, c);
  and and_14 (and_14_out, b, not_22_out, e);
  and and_15 (and_15_out, not_23_out, not_24_out, not_25_out);
  and and_16 (and_16_out, not_26_out, not_27_out, not_28_out);
  and and_17 (and_17_out, c, d, e);
  and and_18 (and_18_out, not_29_out, b, not_30_out);
  and and_19 (and_19_out, a, b, c);
  and and_20 (and_20_out, not_31_out, c, not_32_out, not_33_out);
  and and_21 (and_21_out, b, not_34_out, not_35_out, e);
  or or_1 (x, and_1_out, and_2_out, and_3_out, and_4_out, and_5_out);
  or or_2 (y, and_6_out, and_7_out, and_8_out, and_9_out, and_10_out, a);
  or or_3 (z, and_11_out, and_12_out, and_13_out, and_14_out);
  or or_4 (u, and_15_out, and_16_out, and_17_out, and_18_out, and_19_out);
  or or_5 (v, and_20_out, and_21_out, a);
endmodule

module ChangementFuseauHoraire_bis (
  input  RESET,
  input  [1:0] B1_B0,
  output [7:0] Letter1,
  output [7:0] Letter2,
  output [7:0] Letter3,
  output [7:0] Letter4,
  output [7:0] Letter5,
  output [7:0] Letter6,
  output [7:0] UTCCode
);

  wire [4:0] CapitalLetter1_bis_1_v, CapitalLetter2_bis_1_v, CapitalLetter3_bis_1_v, CapitalLetter5_1_v,
       CapitalLetter6_1_v, counter_1_q;
  wire [6:0] Capitales_bis_1_z;

  Counter #(.width(5), .max('h15)) counter_1 (
    .clr(RESET), .up(1'b1), .count(1'b1), .clk(B1_B0[0]), .Q(counter_1_q));  // open: load, D, carry
  CapitalLetter1_bis CapitalLetter1_bis_1 (
    .a(counter_1_q[4]), .b(counter_1_q[3]), .c(counter_1_q[2]), .d(counter_1_q[1]), .e(counter_1_q[0]),
    .x(CapitalLetter1_bis_1_v[4]), .y(CapitalLetter1_bis_1_v[3]), .z(CapitalLetter1_bis_1_v[2]),
    .u(CapitalLetter1_bis_1_v[1]), .v(CapitalLetter1_bis_1_v[0]));
  CapitalLetter2_bis CapitalLetter2_bis_1 (
    .a(counter_1_q[4]), .b(counter_1_q[3]), .c(counter_1_q[2]), .d(counter_1_q[1]), .e(counter_1_q[0]),
    .x(CapitalLetter2_bis_1_v[4]), .y(CapitalLetter2_bis_1_v[3]), .z(CapitalLetter2_bis_1_v[2]),
    .u(CapitalLetter2_bis_1_v[1]), .v(CapitalLetter2_bis_1_v[0]));
  CapitalLetter3_bis CapitalLetter3_bis_1 (
    .a(counter_1_q[4]), .b(counter_1_q[3]), .c(counter_1_q[2]), .d(counter_1_q[1]), .e(counter_1_q[0]),
    .x(CapitalLetter3_bis_1_v[4]), .y(CapitalLetter3_bis_1_v[3]), .z(CapitalLetter3_bis_1_v[2]),
    .u(CapitalLetter3_bis_1_v[1]), .v(CapitalLetter3_bis_1_v[0]));
  CapitalLetter5 CapitalLetter5_1 (
    .a(counter_1_q[4]), .b(counter_1_q[3]), .c(counter_1_q[2]), .d(counter_1_q[1]), .e(counter_1_q[0]),
    .x(CapitalLetter5_1_v[4]), .y(CapitalLetter5_1_v[3]), .z(CapitalLetter5_1_v[2]),
    .u(CapitalLetter5_1_v[1]), .v(CapitalLetter5_1_v[0]));
  CapitalLetter6 CapitalLetter6_1 (
    .a(counter_1_q[4]), .b(counter_1_q[3]), .c(counter_1_q[2]), .d(counter_1_q[1]), .e(counter_1_q[0]),
    .x(CapitalLetter6_1_v[4]), .y(CapitalLetter6_1_v[3]), .z(CapitalLetter6_1_v[2]),
    .u(CapitalLetter6_1_v[1]), .v(CapitalLetter6_1_v[0]));
  Capitales_bis Capitales_bis_1 (
    .a(counter_1_q[4]), .b(counter_1_q[3]), .c(counter_1_q[2]), .d(counter_1_q[1]), .e(counter_1_q[0]),
    .t(Capitales_bis_1_z[6]), .u(Capitales_bis_1_z[5]), .v(Capitales_bis_1_z[4]), .w(Capitales_bis_1_z[3]),
    .x(Capitales_bis_1_z[2]), .y(Capitales_bis_1_z[1]), .z(Capitales_bis_1_z[0]));
  assign Letter1 = {{3{1'b0}}, CapitalLetter1_bis_1_v};  // Bit_Extender bit_extender_1
  assign Letter2 = {{3{1'b0}}, CapitalLetter2_bis_1_v};  // Bit_Extender bit_extender_2
  assign Letter3 = {{3{1'b0}}, CapitalLetter3_bis_1_v};  // Bit_Extender bit_extender_3
  assign Letter5 = {{3{1'b0}}, CapitalLetter5_1_v};  // Bit_Extender bit_extender_4
  assign Letter6 = {{3{1'b0}}, CapitalLetter6_1_v};  // Bit_Extender bit_extender_5
  assign UTCCode = {{1{1'b0}}, Capitales_bis_1_z};  // Bit_Extender bit_extender_6

  assign Letter4 = {8{1'b1}};
endmodule

module Capitales_bis (
  input  a,
  input  b,
  input  c,
  input  d,
  input  e,
  output t,
  output u,
  output v,
  output w,
  output x,
  output y,
  output z
);

  wire and_1_out, and_2_out, and_3_out, and_4_out, and_5_out, and_6_out, and_7_out, and_8_out, and_9_out,
       and_10_out, and_11_out, and_12_out, and_13_out, and_14_out, and_15_out, and_16_out, and_17_out,
       and_18_out, and_19_out, and_20_out, and_21_out, and_22_out, and_23_out, and_24_out, and_25_out,
       not_1_out, not_2_out, not_3_out, not_4_out, not_5_out, not_6_out, not_7_out, not_8_out, not_9_out,
       not_10_out, not_11_out, not_12_out, not_13_out, not_14_out, not_15_out, not_16_out, not_17_out,
       not_18_out, not_19_out, not_20_out, not_21_out, not_22_out, not_23_out, not_24_out, not_25_out,
       not_26_out, not_27_out, not_28_out, not_29_out, not_30_out, not_31_out, not_32_out, not_33_out,
       not_34_out, not_35_out, not_36_out, not_37_out, not_38_out, not_39_out, not_40_out, not_41_out,
       not_42_out, not_43_out, not_44_out, not_45_out, not_46_out, not_47_out, not_48_out, not_49_out,
       not_50_out, not_51_out;

  not not_1 (not_1_out, b);
  not not_2 (not_2_out, c);
  not not_3 (not_3_out, b);
  not not_4 (not_4_out, d);
  not not_5 (not_5_out, b);
  not not_6 (not_6_out, c);
  not not_7 (not_7_out, b);
  not not_8 (not_8_out, d);
  not not_9 (not_9_out, b);
  not not_10 (not_10_out, c);
  not not_11 (not_11_out, b);
  not not_12 (not_12_out, d);
  not not_13 (not_13_out, a);
  not not_14 (not_14_out, a);
  not not_15 (not_15_out, b);
  not not_16 (not_16_out, c);
  not not_17 (not_17_out, b);
  not not_18 (not_18_out, d);
  not not_19 (not_19_out, a);
  not not_20 (not_20_out, b);
  not not_21 (not_21_out, a);
  not not_22 (not_22_out, c);
  not not_23 (not_23_out, d);
  not not_24 (not_24_out, a);
  not not_25 (not_25_out, c);
  not not_26 (not_26_out, e);
  not not_27 (not_27_out, b);
  not not_28 (not_28_out, d);
  not not_29 (not_29_out, b);
  not not_30 (not_30_out, c);
  not not_31 (not_31_out, a);
  not not_32 (not_32_out, b);
  not not_33 (not_33_out, d);
  not not_34 (not_34_out, a);
  not not_35 (not_35_out, b);
  not not_36 (not_36_out, e);
  not not_37 (not_37_out, a);
  not not_38 (not_38_out, d);
  not not_39 (not_39_out, a);
  not not_40 (not_40_out, e);
  not not_41 (not_41_out, a);
  not not_42 (not_42_out, b);
  not not_43 (not_43_out, c);
  not not_44 (not_44_out, b);
  not not_45 (not_45_out, d);
  not not_46 (not_46_out, a);
  not not_47 (not_47_out, e);
  not not_48 (not_48_out, a);
  not not_49 (not_49_out, e);
  not not_50 (not_50_out, b);
  not not_51 (not_51_out, c);
  and and_1 (and_1_out, a, not_1_out, not_2_out);
  and and_2 (and_2_out, a, not_3_out, not_4_out);
  and and_3 (and_3_out, a, not_5_out, not_6_out);
  and and_4 (and_4_out, a, not_7_out, not_8_out);
  and and_5 (and_5_out, a, not_9_out, not_10_out);
  and and_6 (and_6_out, a, not_11_out, not_12_out);
  and and_7 (and_7_out, not_13_out, b, d, e);
  and and_8 (and_8_out, not_14_out, b, c);
  and and_9 (and_9_out, a, not_15_out, not_16_out);
  and and_10 (and_10_out, a, not_17_out, not_18_out);
  and and_11 (and_11_out, not_19_out, not_20_out, c, d, e);
  and and_12 (and_12_out, not_21_out, b, not_22_out, not_23_out);
  and and_13 (and_13_out, not_24_out, b, not_25_out, not_26_out);
  and and_14 (and_14_out, a, not_27_out, c, not_28_out);
  and and_15 (and_15_out, not_29_out, not_30_out, d, e);
  and and_16 (and_16_out, not_31_out, not_32_out, c, not_33_out);
  and and_17 (and_17_out, not_34_out, not_35_out, c, not_36_out);
  and and_18 (and_18_out, not_37_out, b, not_38_out, e);
  and and_19 (and_19_out, not_39_out, b, d, not_40_out);
  and and_20 (and_20_out, not_41_out, b, c, d);
  and and_21 (and_21_out, a, not_42_out, not_43_out, d);
  and and_22 (and_22_out, not_44_out, not_45_out, e);
  and and_23 (and_23_out, not_46_out, d, not_47_out);
  and and_24 (and_24_out, not_48_out, b, not_49_out);
  and and_25 (and_25_out, a, not_50_out, not_51_out, e);
  or or_1 (t, and_1_out, and_2_out);
  or or_2 (u, and_3_out, and_4_out);
  or or_3 (v, and_5_out, and_6_out);
  or or_4 (w, and_7_out, and_8_out, and_9_out, and_10_out);
  or or_5 (x, and_11_out, and_12_out, and_13_out, and_14_out);
  or or_6 (y, and_15_out, and_16_out, and_17_out, and_18_out, and_19_out, and_20_out, and_21_out);
  or or_7 (z, and_22_out, and_23_out, and_24_out, and_25_out);
endmodule

module CapitalLetter1_bis (
  input  a,
  input  b,
  input  c,
  input  d,
  input  e,
  output x,
  output y,
  output z,
  output u,
  output v
);

  wire and_1_out, and_2_out, and_3_out, and_4_out, and_5_out, and_6_out, and_7_out, and_8_out, and_9_out,
       and_10_out, and_11_out, and_12_out, and_13_out, and_14_out, and_15_out, and_16_out, and_17_out,
       and_18_out, and_19_out, and_20_out, and_21_out, and_22_out, and_23_out, and_24_out, and_25_out,
       and_26_out, and_27_out, and_28_out, and_29_out, and_30_out, and_31_out, not_1_out, not_2_out,
       not_3_out, not_4_out, not_5_out, not_6_out, not_7_out, not_8_out, not_9_out, not_10_out, not_11_out,
       not_12_out, not_13_out, not_14_out, not_15_out, not_16_out, not_17_out, not_18_out, not_19_out,
       not_20_out, not_21_out, not_22_out, not_23_out, not_24_out, not_25_out, not_26_out, not_27_out,
       not_28_out, not_29_out, not_30_out, not_31_out, not_32_out, not_33_out, not_34_out, not_35_out,
       not_36_out, not_37_out, not_38_out, not_39_out, not_40_out, not_41_out, not_42_out, not_43_out,
       not_44_out, not_45_out, not_46_out, not_47_out, not_48_out, not_49_out, not_50_out, not_51_out,
       not_52_out, not_53_out, not_54_out, not_55_out, not_56_out, not_57_out, not_58_out, not_59_out,
       not_60_out, not_61_out, not_62_out, not_63_out, not_64_out, not_65_out, not_66_out, not_67_out,
       not_68_out, not_69_out, not_70_out, not_71_out, not_72_out;

  not not_1 (not_1_out, a);
  not not_2 (not_2_out, c);
  not not_3 (not_3_out, d);
  not not_4 (not_4_out, e);
  not not_5 (not_5_out, b);
  not not_6 (not_6_out, c);
  not not_7 (not_7_out, d);
  not not_8 (not_8_out, a);
  not not_9 (not_9_out, b);
  not not_10 (not_10_out, e);
  not not_11 (not_11_out, a);
  not not_12 (not_12_out, d);
  not not_13 (not_13_out, b);
  not not_14 (not_14_out, c);
  not not_15 (not_15_out, e);
  not not_16 (not_16_out, a);
  not not_17 (not_17_out, c);
  not not_18 (not_18_out, a);
  not not_19 (not_19_out, d);
  not not_20 (not_20_out, a);
  not not_21 (not_21_out, a);
  not not_22 (not_22_out, a);
  not not_23 (not_23_out, b);
  not not_24 (not_24_out, d);
  not not_25 (not_25_out, b);
  not not_26 (not_26_out, c);
  not not_27 (not_27_out, a);
  not not_28 (not_28_out, b);
  not not_29 (not_29_out, c);
  not not_30 (not_30_out, d);
  not not_31 (not_31_out, a);
  not not_32 (not_32_out, e);
  not not_33 (not_33_out, a);
  not not_34 (not_34_out, b);
  not not_35 (not_35_out, c);
  not not_36 (not_36_out, e);
  not not_37 (not_37_out, b);
  not not_38 (not_38_out, d);
  not not_39 (not_39_out, e);
  not not_40 (not_40_out, a);
  not not_41 (not_41_out, c);
  not not_42 (not_42_out, a);
  not not_43 (not_43_out, b);
  not not_44 (not_44_out, d);
  not not_45 (not_45_out, a);
  not not_46 (not_46_out, b);
  not not_47 (not_47_out, a);
  not not_48 (not_48_out, c);
  not not_49 (not_49_out, a);
  not not_50 (not_50_out, d);
  not not_51 (not_51_out, e);
  not not_52 (not_52_out, b);
  not not_53 (not_53_out, c);
  not not_54 (not_54_out, d);
  not not_55 (not_55_out, b);
  not not_56 (not_56_out, c);
  not not_57 (not_57_out, b);
  not not_58 (not_58_out, d);
  not not_59 (not_59_out, a);
  not not_60 (not_60_out, c);
  not not_61 (not_61_out, a);
  not not_62 (not_62_out, b);
  not not_63 (not_63_out, e);
  not not_64 (not_64_out, a);
  not not_65 (not_65_out, d);
  not not_66 (not_66_out, e);
  not not_67 (not_67_out, b);
  not not_68 (not_68_out, d);
  not not_69 (not_69_out, a);
  not not_70 (not_70_out, c);
  not not_71 (not_71_out, b);
  not not_72 (not_72_out, c);
  and and_1 (and_1_out, not_1_out, not_2_out, not_3_out, not_4_out);
  and and_2 (and_2_out, not_5_out, not_6_out, not_7_out);
  and and_3 (and_3_out, not_8_out, not_9_out, c, d, not_10_out);
  and and_4 (and_4_out, not_11_out, b, c, not_12_out);
  and and_5 (and_5_out, a, not_13_out, not_14_out, not_15_out);
  and and_6 (and_6_out, not_16_out, not_17_out, d);
  and and_7 (and_7_out, not_18_out, c, not_19_out);
  and and_8 (and_8_out, not_20_out, c, e);
  and and_9 (and_9_out, not_21_out, b, e);
  and and_10 (and_10_out, not_22_out, b, c);
  and and_11 (and_11_out, a, not_23_out, not_24_out);
  and and_12 (and_12_out, a, not_25_out, not_26_out, e);
  and and_13 (and_13_out, not_27_out, not_28_out, not_29_out, not_30_out);
  and and_14 (and_14_out, not_31_out, c, d, not_32_out);
  and and_15 (and_15_out, not_33_out, b, c, d);
  and and_16 (and_16_out, a, not_34_out, not_35_out, d, not_36_out);
  and and_17 (and_17_out, a, not_37_out, c, not_38_out, not_39_out);
  and and_18 (and_18_out, not_40_out, not_41_out, d);
  and and_19 (and_19_out, not_42_out, not_43_out, c, not_44_out);
  and and_20 (and_20_out, not_45_out, not_46_out, c, e);
  and and_21 (and_21_out, not_47_out, b, not_48_out);
  and and_22 (and_22_out, not_49_out, b, not_50_out, not_51_out);
  and and_23 (and_23_out, a, not_52_out, not_53_out, not_54_out);
  and and_24 (and_24_out, a, not_55_out, not_56_out, e);
  and and_25 (and_25_out, a, not_57_out, not_58_out, e);
  and and_26 (and_26_out, not_59_out, not_60_out, d);
  and and_27 (and_27_out, not_61_out, not_62_out, c, not_63_out);
  and and_28 (and_28_out, not_64_out, c, not_65_out, not_66_out);
  and and_29 (and_29_out, not_67_out, c, not_68_out, e);
  and and_30 (and_30_out, not_69_out, b, not_70_out, e);
  and and_31 (and_31_out, a, not_71_out, not_72_out);
  or or_1 (x, and_1_out, and_2_out, and_3_out, and_4_out, and_5_out);
  or or_2 (y, and_6_out, and_7_out, and_8_out, and_9_out, and_10_out, and_11_out, and_12_out);
  or or_3 (z, and_13_out, and_14_out, and_15_out, and_16_out, and_17_out);
  or or_4 (u, and_18_out, and_19_out, and_20_out, and_21_out, and_22_out, and_23_out, and_24_out, and_25_out);
  or or_5 (v, and_26_out, and_27_out, and_28_out, and_29_out, and_30_out, and_31_out);
endmodule

module CapitalLetter2_bis (
  input  a,
  input  b,
  input  c,
  input  d,
  input  e,
  output x,
  output y,
  output z,
  output u,
  output v
);

  wire and_1_out, and_2_out, and_3_out, and_4_out, and_5_out, and_6_out, and_7_out, and_8_out, and_9_out,
       and_10_out, and_11_out, and_12_out, and_13_out, and_14_out, and_15_out, and_16_out, and_17_out,
       and_18_out, and_19_out, and_20_out, and_21_out, and_22_out, and_23_out, and_24_out, not_1_out,
       not_2_out, not_3_out, not_4_out, not_5_out, not_6_out, not_7_out, not_8_out, not_9_out, not_10_out,
       not_11_out, not_12_out, not_13_out, not_14_out, not_15_out, not_16_out, not_17_out, not_18_out,
       not_19_out, not_20_out, not_21_out, not_22_out, not_23_out, not_24_out, not_25_out, not_26_out,
       not_27_out, not_28_out, not_29_out, not_30_out, not_31_out, not_32_out, not_33_out, not_34_out,
       not_35_out, not_36_out, not_37_out, not_38_out, not_39_out, not_40_out, not_41_out, not_42_out,
       not_43_out, not_44_out, not_45_out, not_46_out, not_47_out, not_48_out, not_49_out, not_50_out,
       not_51_out, not_52_out, not_53_out;

  not not_1 (not_1_out, a);
  not not_2 (not_2_out, c);
  not not_3 (not_3_out, d);
  not not_4 (not_4_out, a);
  not not_5 (not_5_out, d);
  not not_6 (not_6_out, a);
  not not_7 (not_7_out, b);
  not not_8 (not_8_out, e);
  not not_9 (not_9_out, b);
  not not_10 (not_10_out, d);
  not not_11 (not_11_out, b);
  not not_12 (not_12_out, c);
  not not_13 (not_13_out, b);
  not not_14 (not_14_out, c);
  not not_15 (not_15_out, e);
  not not_16 (not_16_out, a);
  not not_17 (not_17_out, b);
  not not_18 (not_18_out, d);
  not not_19 (not_19_out, a);
  not not_20 (not_20_out, e);
  not not_21 (not_21_out, b);
  not not_22 (not_22_out, d);
  not not_23 (not_23_out, a);
  not not_24 (not_24_out, b);
  not not_25 (not_25_out, c);
  not not_26 (not_26_out, a);
  not not_27 (not_27_out, b);
  not not_28 (not_28_out, e);
  not not_29 (not_29_out, a);
  not not_30 (not_30_out, c);
  not not_31 (not_31_out, b);
  not not_32 (not_32_out, c);
  not not_33 (not_33_out, a);
  not not_34 (not_34_out, d);
  not not_35 (not_35_out, b);
  not not_36 (not_36_out, c);
  not not_37 (not_37_out, a);
  not not_38 (not_38_out, a);
  not not_39 (not_39_out, b);
  not not_40 (not_40_out, d);
  not not_41 (not_41_out, a);
  not not_42 (not_42_out, b);
  not not_43 (not_43_out, d);
  not not_44 (not_44_out, a);
  not not_45 (not_45_out, c);
  not not_46 (not_46_out, d);
  not not_47 (not_47_out, e);
  not not_48 (not_48_out, a);
  not not_49 (not_49_out, b);
  not not_50 (not_50_out, a);
  not not_51 (not_51_out, d);
  not not_52 (not_52_out, b);
  not not_53 (not_53_out, c);
  and and_1 (and_1_out, not_1_out, not_2_out, not_3_out);
  and and_2 (and_2_out, not_4_out, not_5_out, e);
  and and_3 (and_3_out, not_6_out, not_7_out, c, not_8_out);
  and and_4 (and_4_out, not_9_out, c, not_10_out, e);
  and and_5 (and_5_out, a, not_11_out, not_12_out, d, e);
  and and_6 (and_6_out, not_13_out, not_14_out, d, not_15_out);
  and and_7 (and_7_out, not_16_out, d, e);
  and and_8 (and_8_out, not_17_out, c, not_18_out);
  and and_9 (and_9_out, not_19_out, b, not_20_out);
  and and_10 (and_10_out, a, not_21_out, not_22_out);
  and and_11 (and_11_out, not_23_out, not_24_out, not_25_out);
  and and_12 (and_12_out, not_26_out, not_27_out, not_28_out);
  and and_13 (and_13_out, not_29_out, not_30_out, d, e);
  and and_14 (and_14_out, not_31_out, not_32_out, d, e);
  and and_15 (and_15_out, not_33_out, c, not_34_out);
  and and_16 (and_16_out, not_35_out, not_36_out);
  and and_17 (and_17_out, not_37_out, d);
  and and_18 (and_18_out, not_38_out, b);
  and and_19 (and_19_out, a, not_39_out, not_40_out);
  and and_20 (and_20_out, not_41_out, not_42_out, not_43_out);
  and and_21 (and_21_out, not_44_out, not_45_out, not_46_out, not_47_out);
  and and_22 (and_22_out, not_48_out, not_49_out, c);
  and and_23 (and_23_out, not_50_out, c, not_51_out, e);
  and and_24 (and_24_out, a, not_52_out, not_53_out, d, e);
  or or_1 (x, and_1_out, and_2_out, and_3_out, and_4_out, and_5_out);
  or or_2 (y, and_6_out, and_7_out, and_8_out, and_9_out, and_10_out);
  or or_3 (z, and_11_out, and_12_out, and_13_out, and_14_out, and_15_out);
  or or_4 (u, and_16_out, and_17_out, and_18_out, and_19_out);
  or or_5 (v, and_20_out, and_21_out, and_22_out, and_23_out, and_24_out);
endmodule

module CapitalLetter3_bis (
  input  a,
  input  b,
  input  c,
  input  d,
  input  e,
  output x,
  output y,
  output z,
  output u,
  output v
);

  wire and_1_out, and_2_out, and_3_out, and_4_out, and_5_out, and_6_out, and_7_out, and_8_out, and_9_out,
       and_10_out, and_11_out, and_12_out, and_13_out, and_14_out, and_15_out, and_16_out, and_17_out,
       and_18_out, and_19_out, and_20_out, and_21_out, and_22_out, and_23_out, and_24_out, not_1_out,
       not_2_out, not_3_out, not_4_out, not_5_out, not_6_out, not_7_out, not_8_out, not_9_out, not_10_out,
       not_11_out, not_12_out, not_13_out, not_14_out, not_15_out, not_16_out, not_17_out, not_18_out,
       not_19_out, not_20_out, not_21_out, not_22_out, not_23_out, not_24_out, not_25_out, not_26_out,
       not_27_out, not_28_out, not_29_out, not_30_out, not_31_out, not_32_out, not_33_out, not_34_out,
       not_35_out, not_36_out, not_37_out, not_38_out, not_39_out, not_40_out, not_41_out, not_42_out,
       not_43_out, not_44_out, not_45_out, not_46_out, not_47_out, not_48_out, not_49_out, not_50_out,
       not_51_out, not_52_out, not_53_out;

  not not_1 (not_1_out, a);
  not not_2 (not_2_out, c);
  not not_3 (not_3_out, b);
  not not_4 (not_4_out, c);
  not not_5 (not_5_out, a);
  not not_6 (not_6_out, b);
  not not_7 (not_7_out, c);
  not not_8 (not_8_out, a);
  not not_9 (not_9_out, b);
  not not_10 (not_10_out, d);
  not not_11 (not_11_out, e);
  not not_12 (not_12_out, a);
  not not_13 (not_13_out, b);
  not not_14 (not_14_out, b);
  not not_15 (not_15_out, d);
  not not_16 (not_16_out, a);
  not not_17 (not_17_out, d);
  not not_18 (not_18_out, b);
  not not_19 (not_19_out, d);
  not not_20 (not_20_out, e);
  not not_21 (not_21_out, a);
  not not_22 (not_22_out, b);
  not not_23 (not_23_out, d);
  not not_24 (not_24_out, b);
  not not_25 (not_25_out, c);
  not not_26 (not_26_out, d);
  not not_27 (not_27_out, a);
  not not_28 (not_28_out, a);
  not not_29 (not_29_out, e);
  not not_30 (not_30_out, b);
  not not_31 (not_31_out, c);
  not not_32 (not_32_out, e);
  not not_33 (not_33_out, a);
  not not_34 (not_34_out, b);
  not not_35 (not_35_out, c);
  not not_36 (not_36_out, a);
  not not_37 (not_37_out, c);
  not not_38 (not_38_out, a);
  not not_39 (not_39_out, e);
  not not_40 (not_40_out, b);
  not not_41 (not_41_out, c);
  not not_42 (not_42_out, e);
  not not_43 (not_43_out, a);
  not not_44 (not_44_out, b);
  not not_45 (not_45_out, d);
  not not_46 (not_46_out, a);
  not not_47 (not_47_out, b);
  not not_48 (not_48_out, a);
  not not_49 (not_49_out, c);
  not not_50 (not_50_out, d);
  not not_51 (not_51_out, a);
  not not_52 (not_52_out, d);
  not not_53 (not_53_out, e);
  and and_1 (and_1_out, not_1_out, not_2_out);
  and and_2 (and_2_out, not_3_out, not_4_out, e);
  and and_3 (and_3_out, not_5_out, d);
  and and_4 (and_4_out, not_6_out, not_7_out, d);
  and and_5 (and_5_out, not_8_out, b);
  and and_6 (and_6_out, a, not_9_out, c, not_10_out, not_11_out);
  and and_7 (and_7_out, not_12_out, not_13_out, d);
  and and_8 (and_8_out, not_14_out, c, not_15_out);
  and and_9 (and_9_out, not_16_out, b, not_17_out, e);
  and and_10 (and_10_out, a, not_18_out, not_19_out, not_20_out);
  and and_11 (and_11_out, not_21_out, not_22_out, not_23_out);
  and and_12 (and_12_out, not_24_out, not_25_out, not_26_out);
  and and_13 (and_13_out, not_27_out, c, d, e);
  and and_14 (and_14_out, not_28_out, b, not_29_out);
  and and_15 (and_15_out, a, not_30_out, not_31_out, not_32_out);
  and and_16 (and_16_out, not_33_out, not_34_out, not_35_out);
  and and_17 (and_17_out, not_36_out, not_37_out, e);
  and and_18 (and_18_out, not_38_out, d, not_39_out);
  and and_19 (and_19_out, not_40_out, not_41_out, d, not_42_out);
  and and_20 (and_20_out, not_43_out, b, c);
  and and_21 (and_21_out, a, not_44_out, c, not_45_out);
  and and_22 (and_22_out, not_46_out, not_47_out, c, d);
  and and_23 (and_23_out, not_48_out, b, not_49_out, not_50_out, e);
  and and_24 (and_24_out, not_51_out, b, c, not_52_out, not_53_out);
  or or_1 (x, and_1_out, and_2_out, and_3_out, and_4_out, and_5_out, and_6_out);
  or or_2 (y, and_7_out, and_8_out, and_9_out, and_10_out);
  or or_3 (z, and_11_out, and_12_out, and_13_out, and_14_out, and_15_out);
  or or_4 (u, and_16_out, and_17_out, and_18_out, and_19_out, and_20_out, and_21_out);
  or or_5 (v, and_22_out, and_23_out, and_24_out);
endmodule

module CapitalLetter5 (
  input  a,
  input  b,
  input  c,
  input  d,
  input  e,
  output x,
  output y,
  output z,
  output u,
  output v
);

  wire and_1_out, and_2_out, and_3_out, not_1_out, not_2_out, not_3_out, not_4_out;

  not not_1 (not_1_out, b);
  not not_2 (not_2_out, c);
  not not_3 (not_3_out, d);
  not not_4 (not_4_out, e);
  and and_1 (and_1_out, not_1_out, c, d);
  and and_2 (and_2_out, b, not_2_out);
  and and_3 (and_3_out, b, not_3_out);
  or or_1 (z, not_4_out, and_1_out, and_2_out, and_3_out, a);

  assign u = 1'b1;
  assign v = 1'b1;
  assign x = 1'b1;
  assign y = 1'b1;
endmodule

module CapitalLetter6 (
  input  a,
  input  b,
  input  c,
  input  d,
  input  e,
  output x,
  output y,
  output z,
  output u,
  output v
);

  wire and_1_out, and_2_out, and_3_out, and_4_out, and_5_out, and_6_out, not_1_out, not_2_out, not_3_out,
       not_4_out, not_5_out, not_6_out, not_7_out, not_8_out;

  not not_1 (not_1_out, b);
  not not_2 (not_2_out, c);
  not not_3 (not_3_out, d);
  not not_4 (not_4_out, b);
  not not_5 (not_5_out, c);
  not not_6 (not_6_out, d);
  not not_7 (not_7_out, e);
  and and_1 (and_1_out, not_1_out, c, d);
  and and_2 (and_2_out, b, not_2_out);
  and and_3 (and_3_out, b, not_3_out);
  not not_8 (not_8_out, e);
  and and_4 (and_4_out, not_4_out, c, d);
  and and_5 (and_5_out, b, not_5_out);
  and and_6 (and_6_out, b, not_6_out);
  or or_1 (u, not_7_out, and_1_out, and_2_out, and_3_out, a);
  or or_2 (v, not_8_out, and_4_out, and_5_out, and_6_out, a);

  assign x = 1'b1;
  assign y = 1'b1;
  assign z = 1'b1;
endmodule

module test (
);

  ChangementFuseauHoraire_bis changementfuseauhoraire_bis_1 ();  // open: RESET, B1_B0, Letter1, Letter2, Letter3, Letter4, Letter5, Letter6, UTCCode
endmodule
