// Logisim project adderCircuit.circ as structural Verilog: 3 circuits, main circuit adderBase
module adderBase (
  input  A,
  input  B,
  input  CIN,
  output AB,
  output COUT
);

  wire and_1_out, and_2_out, and_3_out, and_4_out, and_5_out, and_6_out, and_7_out, not_1_out, not_2_out,
       not_3_out, not_4_out, not_5_out, not_6_out;

  not not_1 (not_1_out, A);
  not not_2 (not_2_out, B);
  not not_3 (not_3_out, A);
  not not_4 (not_4_out, CIN);
  not not_5 (not_5_out, B);
  not not_6 (not_6_out, CIN);
  and and_1 (and_1_out, B, CIN);
  and and_2 (and_2_out, A, CIN);
  and and_3 (and_3_out, A, B);
  and and_4 (and_4_out, not_1_out, not_2_out, CIN);
  and and_5 (and_5_out, not_3_out, B, not_4_out);
  and and_6 (and_6_out, A, not_5_out, not_6_out);
  and and_7 (and_7_out, A, B, CIN);
  or or_1 (COUT, and_1_out, and_2_out, and_3_out);
  or or_2 (AB, and_4_out, and_5_out, and_6_out, and_7_out);
endmodule

module adder2bits (
  input  [1:0] A2bits,
  input  [1:0] B2bits,
  output [1:0] AB2bits,
  output OVERFLOW
);

  wire adderbase_1_cout;

  adderBase adderbase_1 (.A(A2bits[0]), .B(B2bits[0]), .CIN(1'b0), .AB(AB2bits[0]), .COUT(adderbase_1_cout));
  adderBase adderbase_2 (.A(A2bits[1]), .B(B2bits[1]), .CIN(adderbase_1_cout), .AB(AB2bits[1]), .COUT(OVERFLOW));
endmodule

module adder1bit (
  input  A1bit,
  input  B1bit,
  output AB1bit,
  output OVERFLOW
);

  adderBase adderbase_1 (.A(A1bit), .B(B1bit), .CIN(1'b0), .AB(AB1bit), .COUT(OVERFLOW));
endmodule
