// Logisim project functions.circ as structural Verilog: 15 circuits, main circuit DecoderToSegLed
module AllSegLeds (
  input  [7:0] in_1,
  input  [7:0] in_2,
  input  [7:0] in_3,
  input  [7:0] in_4,
  input  [7:0] in_5,
  input  [7:0] in_6,
  output [7:0] out_7,
  output [7:0] out_8,
  output [7:0] out_9,
  output [7:0] out_10,
  output [7:0] out_11,
  output [7:0] out_12
);

  SegLed1 L1 (.in_1(in_1), .out_2(out_7));
  SegLed1 L2 (.in_1(in_2), .out_2(out_8));
  SegLed1 L3 (.in_1(in_3), .out_2(out_9));
  SegLed1 L4 (.in_1(in_4), .out_2(out_10));
  SegLed1 L5 (.in_1(in_5), .out_2(out_11));
  SegLed1 L6 (.in_1(in_6), .out_2(out_12));
endmodule

module SegLed1 (
  input  [7:0] in_1,
  output [7:0] out_2
);

  DecoderToSegLed decodertosegled_1 (
    .e4(in_1[4]), .e3(in_1[3]), .e2(in_1[2]), .e1(in_1[1]), .e0(in_1[0]), .a(out_2[0]), .b(out_2[1]),
    .c(out_2[2]), .d(out_2[3]), .e(out_2[4]), .f(out_2[5]), .g(out_2[6]));
endmodule

module DecoderToSegLed (
  input  e4,
  input  e3,
  input  e2,
  input  e1,
  input  e0,
  output a,
  output b,
  output c,
  output d,
  output e,
  output f,
  output g
);

  wire and_1_out, and_2_out, and_3_out, and_4_out, and_5_out, and_6_out, and_7_out, and_8_out, and_9_out,
       and_10_out, and_11_out, and_12_out, and_13_out, and_14_out, and_15_out, and_16_out, and_17_out,
       and_18_out, and_19_out, and_20_out, and_21_out, and_22_out, and_23_out, and_24_out, and_25_out,
       and_26_out, and_27_out, and_28_out, and_29_out, and_30_out, and_31_out, and_32_out, and_33_out,
       and_34_out, and_35_out, and_36_out, and_37_out, and_38_out, and_39_out, and_40_out, and_41_out,
       and_42_out, and_43_out, and_44_out, and_45_out, and_46_out, and_47_out, and_48_out, and_49_out,
       and_50_out, and_51_out, and_52_out, and_53_out, and_54_out, not_1_out, not_2_out, not_3_out,
       not_4_out, not_5_out, not_6_out, not_7_out, not_8_out, not_9_out, not_10_out, not_11_out, not_12_out,
       not_13_out, not_14_out, not_15_out, not_16_out, not_17_out, not_18_out, not_19_out, not_20_out,
       not_21_out, not_22_out, not_23_out, not_24_out, not_25_out, not_26_out, not_27_out, not_28_out,
       not_29_out, not_30_out, not_31_out, not_32_out, not_33_out, not_34_out, not_35_out, not_36_out,
       not_37_out, not_38_out, not_39_out, not_40_out, not_41_out, not_42_out, not_43_out, not_44_out,
       not_45_out, not_46_out, not_47_out, not_48_out, not_49_out, not_50_out, not_51_out, not_52_out,
       not_53_out, not_54_out, not_55_out, not_56_out, not_57_out, not_58_out, not_59_out, not_60_out,
       not_61_out, not_62_out, not_63_out, not_64_out, not_65_out, not_66_out, not_67_out, not_68_out,
       not_69_out, not_70_out, not_71_out, not_72_out, not_73_out, not_74_out, not_75_out, not_76_out,
       not_77_out, not_78_out, not_79_out, not_80_out, not_81_out, not_82_out, not_83_out, not_84_out,
       not_85_out, not_86_out, not_87_out, not_88_out, not_89_out, not_90_out, not_91_out, not_92_out,
       not_93_out, not_94_out, not_95_out, not_96_out;

  not not_1 (not_1_out, e2);
  not not_2 (not_2_out, e1);
  not not_3 (not_3_out, e0);
  not not_4 (not_4_out, e4);
  not not_5 (not_5_out, e3);
  not not_6 (not_6_out, e3);
  not not_7 (not_7_out, e1);
  not not_8 (not_8_out, e4);
  not not_9 (not_9_out, e4);
  not not_10 (not_10_out, e0);
  not not_11 (not_11_out, e2);
  not not_12 (not_12_out, e1);
  not not_13 (not_13_out, e2);
  not not_14 (not_14_out, e4);
  not not_15 (not_15_out, e3);
  not not_16 (not_16_out, e1);
  not not_17 (not_17_out, e0);
  not not_18 (not_18_out, e4);
  not not_19 (not_19_out, e2);
  not not_20 (not_20_out, e0);
  not not_21 (not_21_out, e2);
  not not_22 (not_22_out, e1);
  not not_23 (not_23_out, e3);
  not not_24 (not_24_out, e2);
  not not_25 (not_25_out, e4);
  not not_26 (not_26_out, e3);
  not not_27 (not_27_out, e4);
  not not_28 (not_28_out, e1);
  not not_29 (not_29_out, e3);
  not not_30 (not_30_out, e1);
  not not_31 (not_31_out, e3);
  not not_32 (not_32_out, e2);
  not not_33 (not_33_out, e1);
  not not_34 (not_34_out, e2);
  not not_35 (not_35_out, e1);
  not not_36 (not_36_out, e4);
  not not_37 (not_37_out, e3);
  not not_38 (not_38_out, e4);
  not not_39 (not_39_out, e2);
  not not_40 (not_40_out, e4);
  not not_41 (not_41_out, e3);
  not not_42 (not_42_out, e2);
  not not_43 (not_43_out, e0);
  not not_44 (not_44_out, e4);
  not not_45 (not_45_out, e3);
  not not_46 (not_46_out, e0);
  not not_47 (not_47_out, e2);
  not not_48 (not_48_out, e4);
  not not_49 (not_49_out, e1);
  not not_50 (not_50_out, e4);
  not not_51 (not_51_out, e1);
  not not_52 (not_52_out, e1);
  not not_53 (not_53_out, e0);
  not not_54 (not_54_out, e3);
  not not_55 (not_55_out, e1);
  not not_56 (not_56_out, e0);
  not not_57 (not_57_out, e4);
  not not_58 (not_58_out, e2);
  not not_59 (not_59_out, e0);
  not not_60 (not_60_out, e3);
  not not_61 (not_61_out, e0);
  not not_62 (not_62_out, e2);
  not not_63 (not_63_out, e0);
  not not_64 (not_64_out, e4);
  not not_65 (not_65_out, e1);
  not not_66 (not_66_out, e3);
  not not_67 (not_67_out, e1);
  not not_68 (not_68_out, e3);
  not not_69 (not_69_out, e1);
  not not_70 (not_70_out, e0);
  not not_71 (not_71_out, e4);
  not not_72 (not_72_out, e0);
  not not_73 (not_73_out, e3);
  not not_74 (not_74_out, e1);
  not not_75 (not_75_out, e2);
  not not_76 (not_76_out, e4);
  not not_77 (not_77_out, e0);
  not not_78 (not_78_out, e3);
  not not_79 (not_79_out, e2);
  not not_80 (not_80_out, e0);
  not not_81 (not_81_out, e3);
  not not_82 (not_82_out, e1);
  not not_83 (not_83_out, e4);
  not not_84 (not_84_out, e3);
  not not_85 (not_85_out, e2);
  not not_86 (not_86_out, e4);
  not not_87 (not_87_out, e3);
  not not_88 (not_88_out, e1);
  not not_89 (not_89_out, e0);
  not not_90 (not_90_out, e2);
  not not_91 (not_91_out, e1);
  not not_92 (not_92_out, e4);
  not not_93 (not_93_out, e2);
  not not_94 (not_94_out, e1);
  not not_95 (not_95_out, e2);
  not not_96 (not_96_out, e0);
  and and_1 (and_1_out, not_1_out, not_2_out, not_3_out);
  and and_2 (and_2_out, not_4_out, not_5_out, e1);
  and and_3 (and_3_out, not_6_out, e2, not_7_out, e0);
  and and_4 (and_4_out, not_8_out, e2, e1);
  and and_5 (and_5_out, not_9_out, e3, not_10_out);
  and and_6 (and_6_out, e3, not_11_out, not_12_out);
  and and_7 (and_7_out, e4, e3, not_13_out, e0);
  and and_8 (and_8_out, not_14_out, not_15_out, not_16_out, not_17_out);
  and and_9 (and_9_out, not_18_out, not_19_out, not_20_out);
  and and_10 (and_10_out, not_21_out, not_22_out);
  and and_11 (and_11_out, not_23_out, not_24_out, e0);
  and and_12 (and_12_out, not_25_out, not_26_out, e1, e0);
  and and_13 (and_13_out, not_27_out, e3, not_28_out, e0);
  and and_14 (and_14_out, e4, not_29_out, not_30_out, e0);
  and and_15 (and_15_out, e4, e3, e2, e1);
  and and_16 (and_16_out, not_31_out, not_32_out, not_33_out);
  and and_17 (and_17_out, not_34_out, e0);
  and and_18 (and_18_out, not_35_out, e0);
  and and_19 (and_19_out, not_36_out, not_37_out, e2);
  and and_20 (and_20_out, not_38_out, e3, not_39_out);
  and and_21 (and_21_out, e4, e2, e1);
  and and_22 (and_22_out, not_40_out, not_41_out, not_42_out, not_43_out);
  and and_23 (and_23_out, not_44_out, not_45_out, e1, not_46_out);
  and and_24 (and_24_out, not_47_out, e1, e0);
  and and_25 (and_25_out, not_48_out, e2, not_49_out, e0);
  and and_26 (and_26_out, not_50_out, e3, not_51_out);
  and and_27 (and_27_out, e3, e2, not_52_out);
  and and_28 (and_28_out, e3, e2, not_53_out);
  and and_29 (and_29_out, e4, not_54_out, not_55_out, not_56_out);
  and and_30 (and_30_out, e4, e1, e0);
  and and_31 (and_31_out, not_57_out, not_58_out, not_59_out);
  and and_32 (and_32_out, not_60_out, e1, not_61_out);
  and and_33 (and_33_out, e3, not_62_out, not_63_out);
  and and_34 (and_34_out, not_64_out, e3, e1);
  and and_35 (and_35_out, e3, e2, not_65_out);
  and and_36 (and_36_out, e4, not_66_out, not_67_out, e0);
  and and_37 (and_37_out, e4, not_68_out, e2);
  and and_38 (and_38_out, not_69_out, not_70_out);
  and and_39 (and_39_out, not_71_out, e2, not_72_out);
  and and_40 (and_40_out, not_73_out, e2, not_74_out);
  and and_41 (and_41_out, e3, not_75_out, e0);
  and and_42 (and_42_out, not_76_out, e3, e1);
  and and_43 (and_43_out, e3, e2, not_77_out);
  and and_44 (and_44_out, e4, not_78_out, not_79_out, not_80_out);
  and and_45 (and_45_out, e4, not_81_out, not_82_out);
  and and_46 (and_46_out, not_83_out, not_84_out, not_85_out, e1);
  and and_47 (and_47_out, not_86_out, not_87_out, e2, not_88_out);
  and and_48 (and_48_out, e2, e1, not_89_out);
  and and_49 (and_49_out, e3, not_90_out, not_91_out);
  and and_50 (and_50_out, not_92_out, e3, e0);
  and and_51 (and_51_out, e4, not_93_out, not_94_out);
  and and_52 (and_52_out, e4, e2, e1);
  and and_53 (and_53_out, e4, e3, not_95_out);
  and and_54 (and_54_out, e4, e3, not_96_out);
  or or_1 (a, and_1_out, and_2_out, and_3_out, and_4_out, and_5_out, and_6_out, and_7_out);
  or or_2 (b, and_8_out, and_9_out, and_10_out, and_11_out, and_12_out, and_13_out, and_14_out, and_15_out);
  or or_3 (c, and_16_out, and_17_out, and_18_out, and_19_out, and_20_out, and_21_out);
  or or_4 (d, and_22_out, and_23_out, and_24_out, and_25_out, and_26_out, and_27_out, and_28_out, and_29_out, and_30_out);
  or or_5 (e, and_31_out, and_32_out, and_33_out, and_34_out, and_35_out, and_36_out, and_37_out);
  or or_6 (f, and_38_out, and_39_out, and_40_out, and_41_out, and_42_out, and_43_out, and_44_out, and_45_out);
  or or_7 (g, and_46_out, and_47_out, and_48_out, and_49_out, and_50_out, and_51_out, and_52_out, and_53_out, and_54_out);
endmodule

module SegLed2_7Bit (
  input  [6:0] in_1
);

  wire converter7bit_1_w1, converter7bit_1_w2, converter7bit_1_x1, converter7bit_1_x2, converter7bit_1_y1,
       converter7bit_1_y2, converter7bit_1_z1, converter7bit_1_z2;

  Converter7Bit converter7bit_1 (
    .e6(in_1[6]), .e5(in_1[5]), .e4(in_1[4]), .e3(in_1[3]), .e2(in_1[2]), .e1(in_1[1]), .e0(in_1[0]),
    .z2(converter7bit_1_z2), .y2(converter7bit_1_y2), .x2(converter7bit_1_x2), .w2(converter7bit_1_w2),
    .z1(converter7bit_1_z1), .y1(converter7bit_1_y1), .x1(converter7bit_1_x1), .w1(converter7bit_1_w1));
  SegLed1_4Bit segled1_4bit_1 (
    .w(converter7bit_1_w2), .x(converter7bit_1_x2), .y(converter7bit_1_y2), .z(converter7bit_1_z2));
  SegLed1_4Bit segled1_4bit_2 (
    .w(converter7bit_1_w1), .x(converter7bit_1_x1), .y(converter7bit_1_y1), .z(converter7bit_1_z1));
endmodule

module SegLed2_6Bit (
  input  [5:0] in_1
);

  wire conv_p1, conv_p2, undriven, undriven_2, undriven_3, undriven_4, undriven_5, undriven_6;

  // Converter6Bit conv: pin names not known; wires that end beside it: conv_p1, conv_p2
  SegLed1_4Bit LegSeg2 (.w(undriven_5), .x(undriven_6), .y(conv_p1), .z(conv_p2));
  SegLed1_4Bit LedSeg1 (.w(undriven), .x(undriven_2), .y(undriven_3), .z(undriven_4));
endmodule

module SegLed1_4Bit (
  input  w,
  input  x,
  input  y,
  input  z
);

  wire a_1_o, b_1_o, c_1_o, d_1_o, e_1_o, f_1_output_1, g_1_output_1;

  a a_1 (.w(z), .x(y), .y(x), .z(w), .o(a_1_o));
  b b_1 (.w(z), .x(y), .y(x), .z(w), .o(b_1_o));
  c c_1 (.w(z), .x(y), .y(x), .z(w), .o(c_1_o));
  d d_1 (.w(z), .x(y), .y(x), .z(w), .o(d_1_o));
  e e_1 (.w(z), .x(y), .y(x), .z(w), .o(e_1_o));
  f f_1 (.w(z), .x(y), .y(x), .z(w), .Output_1(f_1_output_1));
  g g_1 (.w(z), .x(y), .y(x), .z(w), .Output_1(g_1_output_1));
  _7_Segment_Display L_7_Segment_Display_1 (
    .g(g_1_output_1), .f(f_1_output_1), .a(a_1_o), .b(b_1_o), .e(e_1_o), .d(d_1_o), .c(c_1_o));  // open: dp
endmodule

module Converter7Bit (
  input  e6,
  input  e5,
  input  e4,
  input  e3,
  input  e2,
  input  e1,
  input  e0,
  output z2,
  output y2,
  output x2,
  output w2,
  output z1,
  output y1,
  output x1,
  output w1
);

  wire and_1_out, and_2_out, and_3_out, and_4_out, and_5_out, and_6_out, and_7_out, and_8_out, and_9_out,
       and_10_out, and_11_out, and_12_out, and_13_out, and_14_out, and_15_out, and_16_out, and_17_out,
       and_18_out, and_19_out, and_20_out, and_21_out, and_22_out, and_23_out, and_24_out, and_25_out,
       and_26_out, and_27_out, and_28_out, and_29_out, and_30_out, and_31_out, and_32_out, and_33_out,
       and_34_out, and_35_out, and_36_out, and_37_out, and_38_out, and_39_out, and_40_out, and_41_out,
       and_42_out, and_43_out, and_44_out, and_45_out, and_46_out, and_47_out, and_48_out, and_49_out,
       and_50_out, and_51_out, and_52_out, and_53_out, and_54_out, and_55_out, and_56_out, and_57_out,
       and_58_out, and_59_out, and_60_out, and_61_out, and_62_out, and_63_out, and_64_out, and_65_out,
       and_66_out, not_1_out, not_2_out, not_3_out, not_4_out, not_5_out, not_6_out, not_7_out, not_8_out,
       not_9_out, not_10_out, not_11_out, not_12_out, not_13_out, not_14_out, not_15_out, not_16_out,
       not_17_out, not_18_out, not_19_out, not_20_out, not_21_out, not_22_out, not_23_out, not_24_out,
       not_25_out, not_26_out, not_27_out, not_28_out, not_29_out, not_30_out, not_31_out, not_32_out,
       not_33_out, not_34_out, not_35_out, not_36_out, not_37_out, not_38_out, not_39_out, not_40_out,
       not_41_out, not_42_out, not_43_out, not_44_out, not_45_out, not_46_out, not_47_out, not_48_out,
       not_49_out, not_50_out, not_51_out, not_52_out, not_53_out, not_54_out, not_55_out, not_56_out,
       not_57_out, not_58_out, not_59_out, not_60_out, not_61_out, not_62_out, not_63_out, not_64_out,
       not_65_out, not_66_out, not_67_out, not_68_out, not_69_out, not_70_out, not_71_out, not_72_out,
       not_73_out, not_74_out, not_75_out, not_76_out, not_77_out, not_78_out, not_79_out, not_80_out,
       not_81_out, not_82_out, not_83_out, not_84_out, not_85_out, not_86_out, not_87_out, not_88_out,
       not_89_out, not_90_out, not_91_out, not_92_out, not_93_out, not_94_out, not_95_out, not_96_out,
       not_97_out, not_98_out, not_99_out, not_100_out, not_101_out, not_102_out, not_103_out, not_104_out,
       not_105_out, not_106_out, not_107_out, not_108_out, not_109_out, not_110_out, not_111_out,
       not_112_out, not_113_out, not_114_out, not_115_out, not_116_out, not_117_out, not_118_out,
       not_119_out, not_120_out, not_121_out, not_122_out, not_123_out, not_124_out, not_125_out,
       not_126_out, not_127_out, not_128_out, not_129_out, not_130_out, not_131_out, not_132_out,
       not_133_out, not_134_out, not_135_out, not_136_out, not_137_out, not_138_out, not_139_out,
       not_140_out, not_141_out, not_142_out, not_143_out, not_144_out, not_145_out, not_146_out,
       not_147_out, not_148_out, not_149_out, not_150_out, not_151_out, not_152_out, not_153_out,
       not_154_out, not_155_out, not_156_out, not_157_out, not_158_out, not_159_out, not_160_out,
       not_161_out, not_162_out, not_163_out, not_164_out, not_165_out;

  not not_1 (not_1_out, e5);
  not not_2 (not_2_out, e4);
  not not_3 (not_3_out, e3);
  not not_4 (not_4_out, e2);
  not not_5 (not_5_out, e6);
  not not_6 (not_6_out, e6);
  not not_7 (not_7_out, e5);
  not not_8 (not_8_out, e4);
  not not_9 (not_9_out, e6);
  not not_10 (not_10_out, e5);
  not not_11 (not_11_out, e6);
  not not_12 (not_12_out, e5);
  not not_13 (not_13_out, e6);
  not not_14 (not_14_out, e6);
  not not_15 (not_15_out, e4);
  not not_16 (not_16_out, e3);
  not not_17 (not_17_out, e5);
  not not_18 (not_18_out, e4);
  not not_19 (not_19_out, e5);
  not not_20 (not_20_out, e4);
  not not_21 (not_21_out, e5);
  not not_22 (not_22_out, e4);
  not not_23 (not_23_out, e5);
  not not_24 (not_24_out, e6);
  not not_25 (not_25_out, e5);
  not not_26 (not_26_out, e3);
  not not_27 (not_27_out, e2);
  not not_28 (not_28_out, e4);
  not not_29 (not_29_out, e3);
  not not_30 (not_30_out, e2);
  not not_31 (not_31_out, e6);
  not not_32 (not_32_out, e3);
  not not_33 (not_33_out, e6);
  not not_34 (not_34_out, e3);
  not not_35 (not_35_out, e6);
  not not_36 (not_36_out, e2);
  not not_37 (not_37_out, e5);
  not not_38 (not_38_out, e4);
  not not_39 (not_39_out, e5);
  not not_40 (not_40_out, e4);
  not not_41 (not_41_out, e5);
  not not_42 (not_42_out, e5);
  not not_43 (not_43_out, e6);
  not not_44 (not_44_out, e5);
  not not_45 (not_45_out, e4);
  not not_46 (not_46_out, e2);
  not not_47 (not_47_out, e1);
  not not_48 (not_48_out, e6);
  not not_49 (not_49_out, e5);
  not not_50 (not_50_out, e3);
  not not_51 (not_51_out, e2);
  not not_52 (not_52_out, e6);
  not not_53 (not_53_out, e5);
  not not_54 (not_54_out, e1);
  not not_55 (not_55_out, e6);
  not not_56 (not_56_out, e4);
  not not_57 (not_57_out, e3);
  not not_58 (not_58_out, e6);
  not not_59 (not_59_out, e3);
  not not_60 (not_60_out, e2);
  not not_61 (not_61_out, e1);
  not not_62 (not_62_out, e6);
  not not_63 (not_63_out, e2);
  not not_64 (not_64_out, e5);
  not not_65 (not_65_out, e4);
  not not_66 (not_66_out, e3);
  not not_67 (not_67_out, e1);
  not not_68 (not_68_out, e5);
  not not_69 (not_69_out, e4);
  not not_70 (not_70_out, e5);
  not not_71 (not_71_out, e2);
  not not_72 (not_72_out, e1);
  not not_73 (not_73_out, e4);
  not not_74 (not_74_out, e3);
  not not_75 (not_75_out, e2);
  not not_76 (not_76_out, e4);
  not not_77 (not_77_out, e1);
  not not_78 (not_78_out, e6);
  not not_79 (not_79_out, e4);
  not not_80 (not_80_out, e3);
  not not_81 (not_81_out, e1);
  not not_82 (not_82_out, e6);
  not not_83 (not_83_out, e5);
  not not_84 (not_84_out, e4);
  not not_85 (not_85_out, e6);
  not not_86 (not_86_out, e5);
  not not_87 (not_87_out, e2);
  not not_88 (not_88_out, e1);
  not not_89 (not_89_out, e6);
  not not_90 (not_90_out, e5);
  not not_91 (not_91_out, e2);
  not not_92 (not_92_out, e6);
  not not_93 (not_93_out, e2);
  not not_94 (not_94_out, e1);
  not not_95 (not_95_out, e6);
  not not_96 (not_96_out, e4);
  not not_97 (not_97_out, e3);
  not not_98 (not_98_out, e2);
  not not_99 (not_99_out, e6);
  not not_100 (not_100_out, e4);
  not not_101 (not_101_out, e6);
  not not_102 (not_102_out, e3);
  not not_103 (not_103_out, e4);
  not not_104 (not_104_out, e3);
  not not_105 (not_105_out, e2);
  not not_106 (not_106_out, e1);
  not not_107 (not_107_out, e5);
  not not_108 (not_108_out, e4);
  not not_109 (not_109_out, e2);
  not not_110 (not_110_out, e5);
  not not_111 (not_111_out, e4);
  not not_112 (not_112_out, e1);
  not not_113 (not_113_out, e5);
  not not_114 (not_114_out, e3);
  not not_115 (not_115_out, e5);
  not not_116 (not_116_out, e4);
  not not_117 (not_117_out, e2);
  not not_118 (not_118_out, e5);
  not not_119 (not_119_out, e4);
  not not_120 (not_120_out, e3);
  not not_121 (not_121_out, e2);
  not not_122 (not_122_out, e6);
  not not_123 (not_123_out, e5);
  not not_124 (not_124_out, e3);
  not not_125 (not_125_out, e5);
  not not_126 (not_126_out, e4);
  not not_127 (not_127_out, e1);
  not not_128 (not_128_out, e6);
  not not_129 (not_129_out, e5);
  not not_130 (not_130_out, e3);
  not not_131 (not_131_out, e2);
  not not_132 (not_132_out, e1);
  not not_133 (not_133_out, e6);
  not not_134 (not_134_out, e5);
  not not_135 (not_135_out, e2);
  not not_136 (not_136_out, e4);
  not not_137 (not_137_out, e3);
  not not_138 (not_138_out, e2);
  not not_139 (not_139_out, e1);
  not not_140 (not_140_out, e6);
  not not_141 (not_141_out, e3);
  not not_142 (not_142_out, e1);
  not not_143 (not_143_out, e4);
  not not_144 (not_144_out, e2);
  not not_145 (not_145_out, e6);
  not not_146 (not_146_out, e6);
  not not_147 (not_147_out, e2);
  not not_148 (not_148_out, e1);
  not not_149 (not_149_out, e5);
  not not_150 (not_150_out, e4);
  not not_151 (not_151_out, e1);
  not not_152 (not_152_out, e5);
  not not_153 (not_153_out, e1);
  not not_154 (not_154_out, e5);
  not not_155 (not_155_out, e3);
  not not_156 (not_156_out, e4);
  not not_157 (not_157_out, e3);
  not not_158 (not_158_out, e6);
  not not_159 (not_159_out, e5);
  not not_160 (not_160_out, e4);
  not not_161 (not_161_out, e2);
  not not_162 (not_162_out, e4);
  not not_163 (not_163_out, e3);
  not not_164 (not_164_out, e4);
  not not_165 (not_165_out, e1);
  and and_1 (and_1_out, e6, not_1_out, e4);
  and and_2 (and_2_out, e6, e5, not_2_out, not_3_out, not_4_out);
  and and_3 (and_3_out, not_5_out, e5, e3);
  and and_4 (and_4_out, not_6_out, e5, e4);
  and and_5 (and_5_out, e6, not_7_out, not_8_out);
  and and_6 (and_6_out, not_9_out, not_10_out, e4, e2);
  and and_7 (and_7_out, not_11_out, not_12_out, e4, e3);
  and and_8 (and_8_out, not_13_out, e4, e3, e2);
  and and_9 (and_9_out, not_14_out, e5, not_15_out, not_16_out);
  and and_10 (and_10_out, e6, not_17_out, not_18_out);
  and and_11 (and_11_out, not_19_out, not_20_out, e3, e1);
  and and_12 (and_12_out, not_21_out, not_22_out, e3, e2);
  and and_13 (and_13_out, not_23_out, e3, e2, e1);
  and and_14 (and_14_out, not_24_out, not_25_out, e4, not_26_out, not_27_out);
  and and_15 (and_15_out, e5, not_28_out, not_29_out, not_30_out);
  and and_16 (and_16_out, not_31_out, e5, not_32_out, e1);
  and and_17 (and_17_out, not_33_out, e5, not_34_out, e2);
  and and_18 (and_18_out, not_35_out, e5, e4, e3, not_36_out);
  and and_19 (and_19_out, e6, not_37_out, not_38_out, e2, e1);
  and and_20 (and_20_out, e6, not_39_out, not_40_out, e3);
  and and_21 (and_21_out, e6, not_41_out, e3, e1);
  and and_22 (and_22_out, e6, not_42_out, e3, e2);
  and and_23 (and_23_out, not_43_out, not_44_out, not_45_out, e3, not_46_out, not_47_out);
  and and_24 (and_24_out, not_48_out, not_49_out, e4, not_50_out, not_51_out, e1);
  and and_25 (and_25_out, not_52_out, not_53_out, e4, e3, e2, not_54_out);
  and and_26 (and_26_out, not_55_out, e5, not_56_out, not_57_out, e2, e1);
  and and_27 (and_27_out, not_58_out, e5, e4, not_59_out, not_60_out, not_61_out);
  and and_28 (and_28_out, not_62_out, e5, e4, e3, not_63_out, e1);
  and and_29 (and_29_out, e6, not_64_out, not_65_out, not_66_out, e2, not_67_out);
  and and_30 (and_30_out, e6, not_68_out, not_69_out, e3, e2, e1);
  and and_31 (and_31_out, e6, not_70_out, e4, e3, not_71_out, not_72_out);
  and and_32 (and_32_out, e6, e5, not_73_out, not_74_out, not_75_out, e1);
  and and_33 (and_33_out, e6, e5, not_76_out, e3, e2, not_77_out);
  and and_34 (and_34_out, not_78_out, not_79_out, not_80_out, e2, not_81_out);
  and and_35 (and_35_out, not_82_out, not_83_out, not_84_out, e2, e1);
  and and_36 (and_36_out, not_85_out, not_86_out, e4, not_87_out, not_88_out);
  and and_37 (and_37_out, not_89_out, not_90_out, e4, e3, not_91_out);
  and and_38 (and_38_out, not_92_out, e4, e3, not_93_out, not_94_out);
  and and_39 (and_39_out, not_95_out, e5, not_96_out, not_97_out, not_98_out, e1);
  and and_40 (and_40_out, not_99_out, e5, not_100_out, e3, e2);
  and and_41 (and_41_out, not_101_out, e5, e4, not_102_out, e2, e1);
  and and_42 (and_42_out, e6, not_103_out, not_104_out, not_105_out, not_106_out);
  and and_43 (and_43_out, e6, not_107_out, not_108_out, not_109_out, e1);
  and and_44 (and_44_out, e6, not_110_out, not_111_out, e3, e2, not_112_out);
  and and_45 (and_45_out, e6, not_113_out, e4, not_114_out, e2);
  and and_46 (and_46_out, e6, not_115_out, e4, e2, e1);
  and and_47 (and_47_out, e6, e5, not_116_out, e3, not_117_out);
  and and_48 (and_48_out, not_118_out, not_119_out, not_120_out, not_121_out, e1);
  and and_49 (and_49_out, not_122_out, not_123_out, not_124_out, e2, e1);
  and and_50 (and_50_out, not_125_out, not_126_out, e3, e2, not_127_out);
  and and_51 (and_51_out, not_128_out, not_129_out, e4, not_130_out, not_131_out, not_132_out);
  and and_52 (and_52_out, not_133_out, not_134_out, e4, e3, not_135_out, e1);
  and and_53 (and_53_out, e5, not_136_out, not_137_out, not_138_out, not_139_out);
  and and_54 (and_54_out, not_140_out, e5, not_141_out, e2, not_142_out);
  and and_55 (and_55_out, e5, not_143_out, e3, not_144_out, e1);
  and and_56 (and_56_out, not_145_out, e5, e3, e2, e1);
  and and_57 (and_57_out, not_146_out, e5, e4, e3, not_147_out, not_148_out);
  and and_58 (and_58_out, e6, not_149_out, not_150_out, e3, not_151_out);
  and and_59 (and_59_out, e6, not_152_out, e3, e2, not_153_out);
  and and_60 (and_60_out, e6, not_154_out, e4, not_155_out, e1);
  and and_61 (and_61_out, e6, e5, not_156_out, not_157_out, e2, e1);
  and and_62 (and_62_out, not_158_out, e0);
  and and_63 (and_63_out, not_159_out, e0);
  and and_64 (and_64_out, not_160_out, not_161_out, e0);
  and and_65 (and_65_out, not_162_out, not_163_out, e1, e0);
  and and_66 (and_66_out, not_164_out, e3, not_165_out, e0);
  or or_1 (z2, and_1_out, and_2_out);
  or or_2 (y2, and_3_out, and_4_out, and_5_out);
  or or_3 (x2, and_6_out, and_7_out, and_8_out, and_9_out, and_10_out);
  or or_4 (w2, and_11_out, and_12_out, and_13_out, and_14_out, and_15_out, and_16_out, and_17_out, and_18_out, and_19_out, and_20_out, and_21_out, and_22_out);
  or or_5 (z1, and_23_out, and_24_out, and_25_out, and_26_out, and_27_out, and_28_out, and_29_out, and_30_out, and_31_out, and_32_out, and_33_out);
  or or_6 (w1, and_62_out, and_63_out, and_64_out, and_65_out, and_66_out);
  or or_7 (y1, and_34_out, and_35_out, and_36_out, and_37_out, and_38_out, and_39_out, and_40_out, and_41_out, and_42_out, and_43_out, and_44_out, and_45_out, and_46_out, and_47_out);
  or or_8 (x1, and_48_out, and_49_out, and_50_out, and_51_out, and_52_out, and_53_out, and_54_out, and_55_out, and_56_out, and_57_out, and_58_out, and_59_out, and_60_out, and_61_out);
endmodule

module Converter6Bit (
  input  e5,
  input  e4,
  input  e3,
  input  e2,
  input  e1,
  input  e0,
  output z2,
  output y2,
  output x2,
  output w2,
  output z1,
  output y1,
  output x1,
  output w1
);

  wire and_1_out, and_2_out, and_3_out, and_4_out, and_5_out, and_6_out, and_7_out, and_8_out, and_9_out,
       and_10_out, and_11_out, and_12_out, and_13_out, and_14_out, and_15_out, and_16_out, and_17_out,
       and_18_out, and_19_out, and_20_out, and_21_out, and_22_out, and_23_out, and_24_out, and_25_out,
       and_26_out, and_27_out, and_28_out, and_29_out, and_30_out, and_31_out, and_32_out, and_33_out,
       and_34_out, and_35_out, and_36_out, and_37_out, and_38_out, not_1_out, not_2_out, not_3_out,
       not_4_out, not_5_out, not_6_out, not_7_out, not_8_out, not_9_out, not_10_out, not_11_out, not_12_out,
       not_13_out, not_14_out, not_15_out, not_16_out, not_17_out, not_18_out, not_19_out, not_20_out,
       not_21_out, not_22_out, not_23_out, not_24_out, not_25_out, not_26_out, not_27_out, not_28_out,
       not_29_out, not_30_out, not_31_out, not_32_out, not_33_out, not_34_out, not_35_out, not_36_out,
       not_37_out, not_38_out, not_39_out, not_40_out, not_41_out, not_42_out, not_43_out, not_44_out,
       not_45_out, not_46_out, not_47_out, not_48_out, not_49_out, not_50_out, not_51_out, not_52_out,
       not_53_out, not_54_out, not_55_out, not_56_out, not_57_out, not_58_out, not_59_out, not_60_out,
       not_61_out, not_62_out, not_63_out, not_64_out, not_65_out, not_66_out, not_67_out, not_68_out,
       not_69_out, not_70_out;

  and and_1 (and_1_out, e5, e3);
  and and_2 (and_2_out, e5, e4);
  not not_1 (not_1_out, e5);
  and and_3 (and_3_out, not_1_out, e4, e2);
  not not_2 (not_2_out, e5);
  and and_4 (and_4_out, not_2_out, e4, e3);
  and and_5 (and_5_out, e4, e3, e2);
  not not_3 (not_3_out, e4);
  and and_6 (and_6_out, e5, not_3_out, not_4_out);
  not not_4 (not_4_out, e3);
  not not_5 (not_5_out, e5);
  not not_6 (not_6_out, e4);
  not not_7 (not_7_out, e5);
  not not_8 (not_8_out, e4);
  not not_9 (not_9_out, e5);
  not not_10 (not_10_out, e5);
  not not_11 (not_11_out, e3);
  not not_12 (not_12_out, e2);
  not not_13 (not_13_out, e4);
  not not_14 (not_14_out, e3);
  not not_15 (not_15_out, e3);
  not not_16 (not_16_out, e3);
  not not_17 (not_17_out, e5);
  not not_18 (not_18_out, e4);
  not not_19 (not_19_out, e2);
  not not_20 (not_20_out, e1);
  not not_21 (not_21_out, e5);
  not not_22 (not_22_out, e3);
  not not_23 (not_23_out, e2);
  not not_24 (not_24_out, e5);
  not not_25 (not_25_out, e1);
  not not_26 (not_26_out, e4);
  not not_27 (not_27_out, e3);
  not not_28 (not_28_out, e3);
  not not_29 (not_29_out, e2);
  not not_30 (not_30_out, e1);
  not not_31 (not_31_out, e2);
  not not_32 (not_32_out, e4);
  not not_33 (not_33_out, e3);
  not not_34 (not_34_out, e1);
  not not_35 (not_35_out, e5);
  not not_36 (not_36_out, e4);
  not not_37 (not_37_out, e5);
  not not_38 (not_38_out, e2);
  not not_39 (not_39_out, e1);
  not not_40 (not_40_out, e5);
  not not_41 (not_41_out, e2);
  not not_42 (not_42_out, e2);
  not not_43 (not_43_out, e1);
  not not_44 (not_44_out, e4);
  not not_45 (not_45_out, e3);
  not not_46 (not_46_out, e2);
  not not_47 (not_47_out, e4);
  not not_48 (not_48_out, e3);
  not not_49 (not_49_out, e5);
  not not_50 (not_50_out, e4);
  not not_51 (not_51_out, e3);
  not not_52 (not_52_out, e5);
  not not_53 (not_53_out, e3);
  not not_54 (not_54_out, e5);
  not not_55 (not_55_out, e4);
  not not_56 (not_56_out, e1);
  not not_57 (not_57_out, e5);
  not not_58 (not_58_out, e3);
  not not_59 (not_59_out, e2);
  not not_60 (not_60_out, e1);
  not not_61 (not_61_out, e5);
  not not_62 (not_62_out, e2);
  not not_63 (not_63_out, e4);
  not not_64 (not_64_out, e3);
  not not_65 (not_65_out, e1);
  not not_66 (not_66_out, e3);
  not not_67 (not_67_out, e1);
  not not_68 (not_68_out, e4);
  not not_69 (not_69_out, e2);
  not not_70 (not_70_out, e1);
  or or_1 (y2, and_1_out, and_2_out);
  or or_2 (x2, and_3_out, and_4_out, and_5_out, and_6_out);
  and and_7 (and_7_out, not_5_out, not_6_out, e3, e1);
  and and_8 (and_8_out, not_7_out, not_8_out, e3, e2);
  and and_9 (and_9_out, not_9_out, e3, e2, e1);
  and and_10 (and_10_out, not_10_out, e4, not_11_out, not_12_out);
  and and_11 (and_11_out, e5, not_13_out, not_14_out);
  and and_12 (and_12_out, e5, not_15_out, e1);
  and and_13 (and_13_out, e5, not_16_out, e2);
  and and_14 (and_14_out, e5, e4, e3);
  and and_15 (and_15_out, not_17_out, not_18_out, e3, not_19_out, not_20_out);
  and and_16 (and_16_out, not_21_out, e4, not_22_out, not_23_out, e1);
  and and_17 (and_17_out, not_24_out, e4, e3, e2, not_25_out);
  and and_18 (and_18_out, e5, not_26_out, not_27_out, e2, e1);
  and and_19 (and_19_out, e5, e4, not_28_out, not_29_out, not_30_out);
  and and_20 (and_20_out, e5, e4, e3, not_31_out, e1);
  and and_21 (and_21_out, not_32_out, not_33_out, e2, not_34_out);
  and and_22 (and_22_out, not_35_out, not_36_out, e2, e1);
  and and_23 (and_23_out, not_37_out, e4, not_38_out, not_39_out);
  and and_24 (and_24_out, not_40_out, e4, e3, not_41_out);
  and and_25 (and_25_out, e4, e3, not_42_out, not_43_out);
  and and_26 (and_26_out, e5, not_44_out, not_45_out, not_46_out, e1);
  and and_27 (and_27_out, e5, not_47_out, e3, e2);
  and and_28 (and_28_out, e5, e4, not_48_out, e2, e1);
  and and_29 (and_29_out, not_49_out, not_50_out, not_51_out, e1);
  and and_30 (and_30_out, not_52_out, not_53_out, e2, e1);
  and and_31 (and_31_out, not_54_out, not_55_out, e3, e2, not_56_out);
  and and_32 (and_32_out, not_57_out, e4, not_58_out, not_59_out, not_60_out);
  and and_33 (and_33_out, not_61_out, e4, e3, not_62_out, e1);
  and and_34 (and_34_out, e5, not_63_out, not_64_out, not_65_out);
  and and_35 (and_35_out, e5, not_66_out, e2, not_67_out);
  and and_36 (and_36_out, e5, not_68_out, e3, e1);
  and and_37 (and_37_out, e5, e3, e2, e1);
  and and_38 (and_38_out, e5, e4, e3, not_69_out, not_70_out);
  or or_3 (w2, and_7_out, and_8_out, and_9_out, and_10_out, and_11_out, and_12_out, and_13_out, and_14_out);
  or or_4 (z1, and_15_out, and_16_out, and_17_out, and_18_out, and_19_out, and_20_out);
  or or_5 (y1, and_21_out, and_22_out, and_23_out, and_24_out, and_25_out, and_26_out, and_27_out, and_28_out);
  or or_6 (x1, and_29_out, and_30_out, and_31_out, and_32_out, and_33_out, and_34_out, and_35_out, and_36_out, and_37_out, and_38_out);

  assign w1 = e0;
  assign z2 = 1'b0;
endmodule

module a (
  input  w,
  input  x,
  input  y,
  input  z,
  output o
);

  wire and_1_out, and_2_out, and_3_out, and_4_out, and_5_out, and_6_out, not_1_out, not_2_out, not_3_out,
       not_4_out, or_1_out, or_2_out, or_3_out;

  and and_1 (and_1_out, x, y);
  or or_1 (or_1_out, x, y);
  and and_2 (and_2_out, x, z);
  or or_2 (or_2_out, x, z);
  not not_1 (not_1_out, and_1_out);
  not not_2 (not_2_out, and_2_out);
  and and_3 (and_3_out, not_1_out, or_1_out);
  and and_4 (and_4_out, not_2_out, or_2_out);
  not not_3 (not_3_out, w);
  and and_5 (and_5_out, w, z, and_3_out);
  and and_6 (and_6_out, not_3_out, not_4_out, and_4_out);
  not not_4 (not_4_out, y);
  or or_3 (or_3_out, and_5_out, and_6_out);
  not not_5 (o, or_3_out);
endmodule

module b (
  input  w,
  input  x,
  input  y,
  input  z,
  output o
);

  wire and_1_out, and_2_out, and_3_out, and_4_out, not_1_out, not_2_out, not_3_out, not_4_out, not_5_out,
       xor_1_out;

  not not_1 (not_1_out, w);
  not not_2 (not_2_out, y);
  not not_3 (not_3_out, z);
  xor xor_1 (xor_1_out, w, y);
  and and_1 (and_1_out, w, z);
  and and_2 (and_2_out, x, not_1_out, not_2_out, not_3_out);
  and and_3 (and_3_out, xor_1_out, z);
  not not_4 (not_4_out, x);
  not not_5 (not_5_out, and_1_out);
  and and_4 (and_4_out, not_4_out, not_5_out);
  or or_1 (o, and_3_out, and_2_out, and_4_out);
endmodule

module c (
  input  w,
  input  x,
  input  y,
  input  z,
  output o
);

  wire and_1_out, and_2_out, not_1_out, not_2_out, not_3_out, or_1_out, or_2_out, xor_1_out;

  xor xor_1 (xor_1_out, w, x);
  not not_1 (not_1_out, y);
  not not_2 (not_2_out, x);
  not not_3 (not_3_out, w);
  or or_1 (or_1_out, not_2_out, not_3_out, z);
  or or_2 (or_2_out, not_3_out, not_2_out);
  and and_1 (and_1_out, not_1_out, or_1_out);
  and and_2 (and_2_out, or_2_out, z);
  or or_3 (o, xor_1_out, and_1_out, and_2_out);
endmodule

module d (
  input  w,
  input  x,
  input  y,
  input  z,
  output o
);

  wire and_1_out, and_2_out, and_3_out, and_4_out, and_5_out, not_1_out, not_2_out, not_3_out, not_4_out,
       or_1_out, xor_1_out;

  and and_1 (and_1_out, w, not_1_out);
  not not_1 (not_1_out, y);
  not not_2 (not_2_out, w);
  and and_2 (and_2_out, not_2_out, not_3_out);
  not not_3 (not_3_out, z);
  and and_3 (and_3_out, y, z);
  xor xor_1 (xor_1_out, y, z);
  or or_1 (or_1_out, and_2_out, and_3_out);
  and and_4 (and_4_out, x, xor_1_out);
  and and_5 (and_5_out, or_1_out, not_4_out);
  not not_4 (not_4_out, x);
  or or_2 (o, and_1_out, and_5_out, and_4_out);
endmodule

module e (
  input  w,
  input  x,
  input  y,
  input  z,
  output o
);

  wire and_1_out, and_2_out, not_1_out, not_2_out, or_1_out, or_2_out;

  or or_1 (or_1_out, x, y);
  not not_1 (not_1_out, x);
  or or_2 (or_2_out, not_1_out, y);
  not not_2 (not_2_out, z);
  and and_1 (and_1_out, w, or_1_out);
  and and_2 (and_2_out, or_2_out, not_2_out);
  or or_3 (o, and_1_out, and_2_out);
endmodule

module f (
  input  w,
  input  x,
  input  y,
  input  z,
  output Output_1
);

  wire and_1_out, and_2_out, and_3_out, and_4_out, not_1_out, not_2_out, not_3_out, not_4_out, or_1_out,
       or_2_out;

  not not_1 (not_1_out, x);
  not not_2 (not_2_out, y);
  not not_3 (not_3_out, w);
  or or_1 (or_1_out, y, not_1_out);
  and and_1 (and_1_out, or_1_out, w);
  and and_2 (and_2_out, z, not_2_out, not_3_out);
  not not_4 (not_4_out, z);
  or or_2 (or_2_out, and_2_out, not_4_out);
  and and_3 (and_3_out, ~x, ~y, ~z);  // AND_Gate
  and and_4 (and_4_out, or_2_out, x);
  or or_3 (Output_1, and_4_out, and_3_out, and_1_out);
endmodule

module g (
  input  w,
  input  x,
  input  y,
  input  z,
  output Output_1
);

  wire not_1_out, or_1_out, or_2_out, xnor_1_out, xnor_2_out, xor_1_out;

  or or_1 (or_1_out, w, y, x);
  xnor xnor_1 (xnor_1_out, w, z);
  xor xor_1 (xor_1_out, y, z);
  xnor xnor_2 (xnor_2_out, y, w);
  not not_1 (not_1_out, x);
  or or_2 (or_2_out, not_1_out, xnor_1_out, xnor_2_out, xor_1_out);
  and and_1 (Output_1, or_1_out, or_2_out);
endmodule
