// Logisim project chrono.circ as structural Verilog: 2 circuits, main circuit chronoOnBoard
module chronoOnBoard (
);

  wire DipSwitch_1_sw1, DipSwitch_1_sw2;
  wire [7:0] CHRONO_1_sevseg0, CHRONO_1_sevseg1, CHRONO_1_sevseg2, CHRONO_1_sevseg3, CHRONO_1_sevseg4,
       CHRONO_1_sevseg5;

  DipSwitch #(.number(10)) DipSwitch_1 (
    .sw1(DipSwitch_1_sw1), .sw2(DipSwitch_1_sw2));  // open: sw3, sw4, sw5, sw6, sw7, sw8, sw9, sw10
  CHRONO CHRONO_1 (
    .StartStop(DipSwitch_1_sw1), .ResetEnDI(DipSwitch_1_sw2), .sevseg0(CHRONO_1_sevseg0),
    .sevseg1(CHRONO_1_sevseg1), .sevseg2(CHRONO_1_sevseg2), .sevseg3(CHRONO_1_sevseg3),
    .sevseg4(CHRONO_1_sevseg4), .sevseg5(CHRONO_1_sevseg5));  // open: minInc
  _7_Segment_Display L_7_Segment_Display_1 (
    .g(CHRONO_1_sevseg5[6]), .f(CHRONO_1_sevseg5[5]), .a(CHRONO_1_sevseg5[0]), .b(CHRONO_1_sevseg5[1]),
    .e(CHRONO_1_sevseg5[4]), .d(CHRONO_1_sevseg5[3]), .c(CHRONO_1_sevseg5[2]), .dp(CHRONO_1_sevseg5[7]));
  _7_Segment_Display L_7_Segment_Display_2 (
    .g(CHRONO_1_sevseg4[6]), .f(CHRONO_1_sevseg4[5]), .a(CHRONO_1_sevseg4[0]), .b(CHRONO_1_sevseg4[1]),
    .e(CHRONO_1_sevseg4[4]), .d(CHRONO_1_sevseg4[3]), .c(CHRONO_1_sevseg4[2]), .dp(CHRONO_1_sevseg4[7]));
  _7_Segment_Display L_7_Segment_Display_3 (
    .g(CHRONO_1_sevseg3[6]), .f(CHRONO_1_sevseg3[5]), .a(CHRONO_1_sevseg3[0]), .b(CHRONO_1_sevseg3[1]),
    .e(CHRONO_1_sevseg3[4]), .d(CHRONO_1_sevseg3[3]), .c(CHRONO_1_sevseg3[2]), .dp(CHRONO_1_sevseg3[7]));
  _7_Segment_Display L_7_Segment_Display_4 (
    .g(CHRONO_1_sevseg2[6]), .f(CHRONO_1_sevseg2[5]), .a(CHRONO_1_sevseg2[0]), .b(CHRONO_1_sevseg2[1]),
    .e(CHRONO_1_sevseg2[4]), .d(CHRONO_1_sevseg2[3]), .c(CHRONO_1_sevseg2[2]), .dp(CHRONO_1_sevseg2[7]));
  _7_Segment_Display L_7_Segment_Display_5 (
    .g(CHRONO_1_sevseg1[6]), .f(CHRONO_1_sevseg1[5]), .a(CHRONO_1_sevseg1[0]), .b(CHRONO_1_sevseg1[1]),
    .e(CHRONO_1_sevseg1[4]), .d(CHRONO_1_sevseg1[3]), .c(CHRONO_1_sevseg1[2]), .dp(CHRONO_1_sevseg1[7]));
  _7_Segment_Display L_7_Segment_Display_6 (
    .g(CHRONO_1_sevseg0[6]), .f(CHRONO_1_sevseg0[5]), .a(CHRONO_1_sevseg0[0]), .b(CHRONO_1_sevseg0[1]),
    .e(CHRONO_1_sevseg0[4]), .d(CHRONO_1_sevseg0[3]), .c(CHRONO_1_sevseg0[2]), .dp(CHRONO_1_sevseg0[7]));
endmodule

module CHRONO (
  input  StartStop,
  input  ResetEnDI,
  input  minInc,
  output [7:0] sevseg0,
  output [7:0] sevseg1,
  output [7:0] sevseg2,
  output [7:0] sevseg3,
  output [7:0] sevseg4,
  output [7:0] sevseg5
);

  wire [7:0] timestampFunc_1_p4, timestampFunc_1_p5, timestampFunc_1_p6;

  // timestampFunc timestampFunc_1: pin names not known; wires that end beside it: StartStop, ResetEnDI, minInc, timestampFunc_1_p4, timestampFunc_1_p5, timestampFunc_1_p6
  chronoView chronoView_1 (
    .cs(timestampFunc_1_p4), .s(timestampFunc_1_p5), .min(timestampFunc_1_p6), .sevseg0(sevseg0),
    .sevseg1(sevseg1), .sevseg2(sevseg2), .sevseg3(sevseg3), .sevseg4(sevseg4), .sevseg5(sevseg5));
endmodule
