// Logisim project hour.circ as structural Verilog: 19 circuits, main circuit HOUR
module HOUR (
  input  StartStop,
  input  ResetEnDI,
  input  minInc,
  input  hInc,
  output [7:0] sevseg1,
  output [7:0] sevseg2,
  output [7:0] sevseg3,
  output [7:0] sevseg4
);

  wire [7:0] timestampFunc_1_p5, timestampFunc_1_p6;

  // timestampFunc timestampFunc_1: pin names not known; wires that end beside it: StartStop, ResetEnDI, minInc, hInc, timestampFunc_1_p5, timestampFunc_1_p6
  hourView hourView_1 (
    .min(timestampFunc_1_p5), .h(timestampFunc_1_p6), .sevseg4(sevseg1), .sevseg3(sevseg2),
    .sevseg2(sevseg3), .sevseg1(sevseg4));  // open: sevseg5, sevseg0
endmodule

module hourOnBoard (
);

  wire button0_out, button1_out, DipSwitch_1_sw1, DipSwitch_1_sw2;
  wire [7:0] HOUR_1_sevseg1, HOUR_1_sevseg2, HOUR_1_sevseg3, HOUR_1_sevseg4;

  Button button0 (.out(button0_out));
  Button button1 (.out(button1_out));
  DipSwitch #(.number(10)) DipSwitch_1 (
    .sw1(DipSwitch_1_sw1), .sw2(DipSwitch_1_sw2));  // open: sw3, sw4, sw5, sw6, sw7, sw8, sw9, sw10
  HOUR HOUR_1 (
    .StartStop(DipSwitch_1_sw1), .ResetEnDI(DipSwitch_1_sw2), .minInc(button0_out), .hInc(button1_out),
    .sevseg1(HOUR_1_sevseg1), .sevseg2(HOUR_1_sevseg2), .sevseg3(HOUR_1_sevseg3), .sevseg4(HOUR_1_sevseg4));
  _7_Segment_Display L_7_Segment_Display_1 (
    .g(HOUR_1_sevseg4[6]), .f(HOUR_1_sevseg4[5]), .a(HOUR_1_sevseg4[0]), .b(HOUR_1_sevseg4[1]),
    .e(HOUR_1_sevseg4[4]), .d(HOUR_1_sevseg4[3]), .c(HOUR_1_sevseg4[2]), .dp(HOUR_1_sevseg4[7]));
  _7_Segment_Display L_7_Segment_Display_2 (
    .g(HOUR_1_sevseg3[6]), .f(HOUR_1_sevseg3[5]), .a(HOUR_1_sevseg3[0]), .b(HOUR_1_sevseg3[1]),
    .e(HOUR_1_sevseg3[4]), .d(HOUR_1_sevseg3[3]), .c(HOUR_1_sevseg3[2]), .dp(HOUR_1_sevseg3[7]));
  _7_Segment_Display L_7_Segment_Display_3 (
    .g(HOUR_1_sevseg2[6]), .f(HOUR_1_sevseg2[5]), .a(HOUR_1_sevseg2[0]), .b(HOUR_1_sevseg2[1]),
    .e(HOUR_1_sevseg2[4]), .d(HOUR_1_sevseg2[3]), .c(HOUR_1_sevseg2[2]), .dp(HOUR_1_sevseg2[7]));
  _7_Segment_Display L_7_Segment_Display_4 (
    .g(HOUR_1_sevseg1[6]), .f(HOUR_1_sevseg1[5]), .a(HOUR_1_sevseg1[0]), .b(HOUR_1_sevseg1[1]),
    .e(HOUR_1_sevseg1[4]), .d(HOUR_1_sevseg1[3]), .c(HOUR_1_sevseg1[2]), .dp(HOUR_1_sevseg1[7]));
endmodule

module clk32ktocsec (
  input  CLK32k,
  output CLKcsec
);

  Counter #(.max('h9f)) counter_1 (.clk(CLK32k), .carry(CLKcsec));  // open: clr, load, up, count, D, Q
endmodule

module clk32ktosec (
  input  CLK32k,
  output CLKsec
);

  wire clk32ktocsec_1_clkcsec;

  Counter #(.width(7), .max('h63)) counter_1 (
    .clk(clk32ktocsec_1_clkcsec), .carry(CLKsec));  // open: clr, load, up, count, D, Q
  clk32ktocsec clk32ktocsec_1 (.CLK32k(CLK32k), .CLKcsec(clk32ktocsec_1_clkcsec));
endmodule

module clk32ktomin (
  input  CLK32k,
  output CLKmin
);

  wire clk32ktosec_1_clksec;

  Counter #(.max('h3b)) counter_1 (.clk(clk32ktosec_1_clksec), .carry(CLKmin));  // open: clr, load, up, count, D, Q
  clk32ktosec clk32ktosec_1 (.CLK32k(CLK32k), .CLKsec(clk32ktosec_1_clksec));
endmodule

module hourOnboardnew (
);

  HOURNEW hournew_1 ();  // open: CLK1k, StartStop, ResetEnDi, minload, hload, LoadEnDi, mincur, hcur
endmodule

module HOURNEW (
  input  CLK1k,
  input  StartStop,
  input  ResetEnDi,
  input  [7:0] minload,
  input  [7:0] hload,
  input  LoadEnDi,
  output [7:0] mincur,
  output [7:0] hcur
);

  wire clk1ktomin_1_tickcsec, d_ff_1_q, mincounter_carry, multiplexer_1_out, or_1_out, or_2_out;

  clk1k_to_tickcsec clk1ktomin_1 (.CLK1k(CLK1k), .TICKcsec(clk1ktomin_1_tickcsec));
  Multiplexer #(.enable("false")) multiplexer_1 (
    .in0(1'b0), .in1(clk1ktomin_1_tickcsec), .out(multiplexer_1_out), .sel(StartStop));
  Counter #(.width(6), .max('h3f)) mincounter (
    .clr(ResetEnDi), .load(LoadEnDi), .up(1'b1), .clk(or_1_out), .D(minload[5:0]), .carry(mincounter_carry),
    .Q(mincur[5:0]));  // open: count
  or or_1 (or_1_out, multiplexer_1_out, LoadEnDi);
  Counter #(.width(5), .max('h1f)) hcounter (
    .clr(ResetEnDi), .load(LoadEnDi), .up(1'b1), .clk(or_2_out), .D(hload[4:0]), .Q(hcur[4:0]));  // open: count, carry
  or or_2 (or_2_out, d_ff_1_q, LoadEnDi);
  D_Flip_Flop d_ff_1 (.D(mincounter_carry), .clk(multiplexer_1_out), .Q(d_ff_1_q));  // open: Qn, preset, reset

  assign hcur[7:5] = 3'b000;
  assign mincur[7:6] = 2'b00;
endmodule

module hourFsmOnBoard (
);

  wire clock_1_out, DipSwitch_1_sw1, DipSwitch_1_sw2, DipSwitch_1_sw10;
  wire [7:0] hourfsm_1_hcur, hourfsm_1_mincur, hourviewdecoder_sevseg0, hourviewdecoder_sevseg1,
       hourviewdecoder_sevseg2, hourviewdecoder_sevseg3, hourviewdecoder_sevseg4, hourviewdecoder_sevseg5;

  DipSwitch #(.number(10)) DipSwitch_1 (
    .sw1(DipSwitch_1_sw1), .sw2(DipSwitch_1_sw2), .sw10(DipSwitch_1_sw10));  // open: sw3, sw4, sw5, sw6, sw7, sw8, sw9
  Clock clock_1 (.out(clock_1_out));
  HOURFSM hourfsm_1 (
    .ResetEnDi(DipSwitch_1_sw10), .minLoad(8'h14), .hLoad(8'h17), .LoadEnDi(DipSwitch_1_sw2),
    .StartStop(DipSwitch_1_sw1), .CLK32k(clock_1_out), .minCur(hourfsm_1_mincur), .hCur(hourfsm_1_hcur));
  hourView hourviewdecoder (
    .min(hourfsm_1_mincur), .h(hourfsm_1_hcur), .sevseg5(hourviewdecoder_sevseg5),
    .sevseg4(hourviewdecoder_sevseg4), .sevseg3(hourviewdecoder_sevseg3), .sevseg2(hourviewdecoder_sevseg2),
    .sevseg1(hourviewdecoder_sevseg1), .sevseg0(hourviewdecoder_sevseg0));
  _7_Segment_Display disp5 (
    .g(hourviewdecoder_sevseg0[6]), .f(hourviewdecoder_sevseg0[5]), .a(hourviewdecoder_sevseg0[0]),
    .b(hourviewdecoder_sevseg0[1]), .e(hourviewdecoder_sevseg0[4]), .d(hourviewdecoder_sevseg0[3]),
    .c(hourviewdecoder_sevseg0[2]), .dp(hourviewdecoder_sevseg0[7]));
  _7_Segment_Display disp4 (
    .g(hourviewdecoder_sevseg1[6]), .f(hourviewdecoder_sevseg1[5]), .a(hourviewdecoder_sevseg1[0]),
    .b(hourviewdecoder_sevseg1[1]), .e(hourviewdecoder_sevseg1[4]), .d(hourviewdecoder_sevseg1[3]),
    .c(hourviewdecoder_sevseg1[2]), .dp(hourviewdecoder_sevseg1[7]));
  _7_Segment_Display disp3 (
    .g(hourviewdecoder_sevseg2[6]), .f(hourviewdecoder_sevseg2[5]), .a(hourviewdecoder_sevseg2[0]),
    .b(hourviewdecoder_sevseg2[1]), .e(hourviewdecoder_sevseg2[4]), .d(hourviewdecoder_sevseg2[3]),
    .c(hourviewdecoder_sevseg2[2]), .dp(hourviewdecoder_sevseg2[7]));
  _7_Segment_Display disp2 (
    .g(hourviewdecoder_sevseg3[6]), .f(hourviewdecoder_sevseg3[5]), .a(hourviewdecoder_sevseg3[0]),
    .b(hourviewdecoder_sevseg3[1]), .e(hourviewdecoder_sevseg3[4]), .d(hourviewdecoder_sevseg3[3]),
    .c(hourviewdecoder_sevseg3[2]), .dp(hourviewdecoder_sevseg3[7]));
  _7_Segment_Display disp1 (
    .g(hourviewdecoder_sevseg4[6]), .f(hourviewdecoder_sevseg4[5]), .a(hourviewdecoder_sevseg4[0]),
    .b(hourviewdecoder_sevseg4[1]), .e(hourviewdecoder_sevseg4[4]), .d(hourviewdecoder_sevseg4[3]),
    .c(hourviewdecoder_sevseg4[2]), .dp(hourviewdecoder_sevseg4[7]));
  _7_Segment_Display disp0 (
    .g(hourviewdecoder_sevseg5[6]), .f(hourviewdecoder_sevseg5[5]), .a(hourviewdecoder_sevseg5[0]),
    .b(hourviewdecoder_sevseg5[1]), .e(hourviewdecoder_sevseg5[4]), .d(hourviewdecoder_sevseg5[3]),
    .c(hourviewdecoder_sevseg5[2]), .dp(hourviewdecoder_sevseg5[7]));
endmodule

module HOURFSM (
  input  ResetEnDi,
  input  [7:0] minLoad,
  input  [7:0] hLoad,
  input  LoadEnDi,
  input  StartStop,
  input  CLK32k,
  output [7:0] minCur,
  output [7:0] hCur
);

  wire clk32kto1k_1_clk1k, d_ff_1_q;

  clk32k_to_clk1k clk32kto1k_1 (.CLK32k(CLK32k), .CLK1k(clk32kto1k_1_clk1k));
  HOURNEW hournew1 (
    .CLK1k(clk32kto1k_1_clk1k), .StartStop(d_ff_1_q), .ResetEnDi(ResetEnDi), .minload(minLoad),
    .hload(hLoad), .LoadEnDi(LoadEnDi), .mincur(minCur), .hcur(hCur));
  D_Flip_Flop d_ff_1 (.D(StartStop), .clk(clk32kto1k_1_clk1k), .Q(d_ff_1_q));  // open: Qn, preset, reset
endmodule

module clk32k_to_clk1k (
  input  CLK32k,
  output CLK1k
);

  wire d_ff_1_q, d_ff_1_qn, d_ff_2_q, d_ff_2_qn, d_ff_3_q, d_ff_3_qn, d_ff_4_q, d_ff_4_qn, d_ff_5_qn;

  D_Flip_Flop d_ff_1 (.D(d_ff_1_qn), .clk(CLK32k), .Q(d_ff_1_q), .Qn(d_ff_1_qn));  // open: preset, reset
  D_Flip_Flop d_ff_2 (.D(d_ff_2_qn), .clk(d_ff_1_q), .Q(d_ff_2_q), .Qn(d_ff_2_qn));  // open: preset, reset
  D_Flip_Flop d_ff_3 (.D(d_ff_3_qn), .clk(d_ff_2_q), .Q(d_ff_3_q), .Qn(d_ff_3_qn));  // open: preset, reset
  D_Flip_Flop d_ff_4 (.D(d_ff_4_qn), .clk(d_ff_3_q), .Q(d_ff_4_q), .Qn(d_ff_4_qn));  // open: preset, reset
  D_Flip_Flop d_ff_5 (.D(d_ff_5_qn), .clk(d_ff_4_q), .Q(CLK1k), .Qn(d_ff_5_qn));  // open: preset, reset
endmodule

module clk32k_to_tickcsec (
  input  CLK32k,
  output TICKcsec
);

  wire clk32k_to_clk1k_1_clk1k;

  clk32k_to_clk1k clk32k_to_clk1k_1 (.CLK32k(CLK32k), .CLK1k(clk32k_to_clk1k_1_clk1k));
  clk1k_to_tickcsec clk1k_to_tickcsec_1 (.CLK1k(clk32k_to_clk1k_1_clk1k), .TICKcsec(TICKcsec));
endmodule

module clk32k_to_ticksec (
  input  CLK32k,
  output TICKsec
);

  wire clk1k_to_tickcsec_1_tickcsec, clk32k_to_clk1k_1_clk1k;

  clk32k_to_clk1k clk32k_to_clk1k_1 (.CLK32k(CLK32k), .CLK1k(clk32k_to_clk1k_1_clk1k));
  clk1k_to_tickcsec clk1k_to_tickcsec_1 (.CLK1k(clk32k_to_clk1k_1_clk1k), .TICKcsec(clk1k_to_tickcsec_1_tickcsec));
  tickcsec_to_ticksec tickcsec_to_ticksec_1 (.TICKcsec(clk1k_to_tickcsec_1_tickcsec), .TICKsec(TICKsec));
endmodule

module clk32k_to_tickmin (
  input  CLK32k,
  output TICKmin
);

  wire clk1k_to_tickcsec_1_tickcsec, clk32k_to_clk1k_1_clk1k, tickcsec_to_ticksec_1_ticksec;

  clk32k_to_clk1k clk32k_to_clk1k_1 (.CLK32k(CLK32k), .CLK1k(clk32k_to_clk1k_1_clk1k));
  clk1k_to_tickcsec clk1k_to_tickcsec_1 (.CLK1k(clk32k_to_clk1k_1_clk1k), .TICKcsec(clk1k_to_tickcsec_1_tickcsec));
  tickcsec_to_ticksec tickcsec_to_ticksec_1 (
    .TICKcsec(clk1k_to_tickcsec_1_tickcsec), .TICKsec(tickcsec_to_ticksec_1_ticksec));
  ticksec_to_tickmin ticksec_to_tickmin_1 (.TICKsec(tickcsec_to_ticksec_1_ticksec), .TICKmin(TICKmin));
endmodule

module clk32k_to_tickh (
  input  CLK32k,
  output TICKh
);

  wire clk1k_to_tickcsec_1_tickcsec, clk32k_to_clk1k_1_clk1k, tickcsec_to_ticksec_1_ticksec,
       ticksec_to_tickmin_1_tickmin;

  clk32k_to_clk1k clk32k_to_clk1k_1 (.CLK32k(CLK32k), .CLK1k(clk32k_to_clk1k_1_clk1k));
  clk1k_to_tickcsec clk1k_to_tickcsec_1 (.CLK1k(clk32k_to_clk1k_1_clk1k), .TICKcsec(clk1k_to_tickcsec_1_tickcsec));
  tickcsec_to_ticksec tickcsec_to_ticksec_1 (
    .TICKcsec(clk1k_to_tickcsec_1_tickcsec), .TICKsec(tickcsec_to_ticksec_1_ticksec));
  ticksec_to_tickmin ticksec_to_tickmin_1 (
    .TICKsec(tickcsec_to_ticksec_1_ticksec), .TICKmin(ticksec_to_tickmin_1_tickmin));
  tickmin_to_tickh tickmin_to_tickh_1 (.TICKmin(ticksec_to_tickmin_1_tickmin), .TICKh(TICKh));
endmodule

module clk1k_to_tickcsec (
  input  CLK1k,
  output TICKcsec
);

  Counter #(.width(3), .max('h4)) counter_1 (.clk(CLK1k), .carry(TICKcsec));  // open: clr, load, up, count, D, Q
endmodule

module tickcsec_to_ticksec (
  input  TICKcsec,
  output TICKsec
);

  Counter #(.width(7), .max('h64)) counter_1 (.clk(TICKcsec), .carry(TICKsec));  // open: clr, load, up, count, D, Q
endmodule

module ticksec_to_tickmin (
  input  TICKsec,
  output TICKmin
);

  Counter #(.width(6), .max('h3c)) counter_1 (.clk(TICKsec), .carry(TICKmin));  // open: clr, load, up, count, D, Q
endmodule

module tickmin_to_tickh (
  input  TICKmin,
  output TICKh
);

  Counter #(.width(6), .max('h3c)) counter_1 (.clk(TICKmin), .carry(TICKh));  // open: clr, load, up, count, D, Q
endmodule

module testclocktick (
);

  wire bcd_to_7_segment_decoder_4_p1, bcd_to_7_segment_decoder_5_p1, binairy_to_bcd_converter_1_p2,
       binairy_to_bcd_converter_2_p2, binairy_to_bcd_converter_2_p4, binairy_to_bcd_converter_3_p3,
       clk32k_to_tickcsec_1_tickcsec, clk32k_to_tickh_1_tickh, clk32k_to_tickmin_1_tickmin,
       clk32k_to_ticksec_1_ticksec, clock_1_out;
  wire [4:0] counter_4_q;
  wire [5:0] counter_2_q, counter_3_q;
  wire [6:0] counter_1_q;

  Clock clock_1 (.out(clock_1_out));
  clk32k_to_tickcsec clk32k_to_tickcsec_1 (.CLK32k(clock_1_out), .TICKcsec(clk32k_to_tickcsec_1_tickcsec));
  clk32k_to_ticksec clk32k_to_ticksec_1 (.CLK32k(clock_1_out), .TICKsec(clk32k_to_ticksec_1_ticksec));
  clk32k_to_tickmin clk32k_to_tickmin_1 (.CLK32k(clock_1_out), .TICKmin(clk32k_to_tickmin_1_tickmin));
  clk32k_to_tickh clk32k_to_tickh_1 (.CLK32k(clock_1_out), .TICKh(clk32k_to_tickh_1_tickh));
  Counter #(.width(7), .max('h63)) counter_1 (
    .clk(clk32k_to_tickcsec_1_tickcsec), .Q(counter_1_q));  // open: clr, load, up, count, D, carry
  Counter #(.width(6), .max('h3b)) counter_2 (
    .clk(clk32k_to_ticksec_1_ticksec), .Q(counter_2_q));  // open: clr, load, up, count, D, carry
  Counter #(.width(6), .max('h3b)) counter_3 (
    .clk(clk32k_to_tickmin_1_tickmin), .Q(counter_3_q));  // open: clr, load, up, count, D, carry
  Counter #(.width(5), .max('h17)) counter_4 (
    .clk(clk32k_to_tickh_1_tickh), .Q(counter_4_q));  // open: clr, load, up, count, D, carry
  // Binairy_to_BCD_converter #(.binvalue(7)) binairy_to_bcd_converter_1: pin names not known; wires that end beside it: counter_1_q, binairy_to_bcd_converter_1_p2
  // BCD_to_7_Segment_decoder bcd_to_7_segment_decoder_1: pin names not known; wires that end beside it: binairy_to_bcd_converter_1_p2
  _7_Segment_Display u_7_segment_display_1 ();  // open: g, f, a, b, e, d, c, dp
  // BCD_to_7_Segment_decoder bcd_to_7_segment_decoder_2: pin names not known
  _7_Segment_Display u_7_segment_display_2 ();  // open: g, f, a, b, e, d, c, dp
  // Binairy_to_BCD_converter #(.binvalue(6)) binairy_to_bcd_converter_2: pin names not known; wires that end beside it: counter_2_q, binairy_to_bcd_converter_2_p2, binairy_to_bcd_converter_2_p2, binairy_to_bcd_converter_2_p4
  _7_Segment_Display u_7_segment_display_3 ();  // open: g, f, a, b, e, d, c, dp
  // BCD_to_7_Segment_decoder bcd_to_7_segment_decoder_3: pin names not known
  // BCD_to_7_Segment_decoder bcd_to_7_segment_decoder_4: pin names not known; wires that end beside it: bcd_to_7_segment_decoder_4_p1
  _7_Segment_Display u_7_segment_display_4 ();  // open: g, f, a, b, e, d, c, dp
  // Binairy_to_BCD_converter #(.binvalue(6)) binairy_to_bcd_converter_3: pin names not known; wires that end beside it: counter_4_q, counter_3_q, binairy_to_bcd_converter_3_p3, binairy_to_bcd_converter_3_p3, bcd_to_7_segment_decoder_4_p1
  // BCD_to_7_Segment_decoder bcd_to_7_segment_decoder_5: pin names not known; wires that end beside it: bcd_to_7_segment_decoder_5_p1, bcd_to_7_segment_decoder_5_p1
  _7_Segment_Display u_7_segment_display_5 ();  // open: g, f, a, b, e, d, c, dp
  _7_Segment_Display u_7_segment_display_6 ();  // open: g, f, a, b, e, d, c, dp
  // BCD_to_7_Segment_decoder bcd_to_7_segment_decoder_6: pin names not known; wires that end beside it: binairy_to_bcd_converter_2_p4
endmodule
