// Logisim project hourLW.circ as structural Verilog: 20 circuits, main circuit zeroTwo
module zeroTwo (
  input  IN1,
  input  IN0,
  input  TickIN,
  output TickOUT,
  output OUT1,
  output OUT0
);

  wire and_2_out, and_3_out, and_4_out, and_5_out, not_1_out, not_2_out, not_3_out, not_4_out, not_5_out,
       not_6_out, not_7_out, not_8_out;

  not not_1 (not_1_out, IN0);
  not not_2 (not_2_out, IN1);
  not not_3 (not_3_out, IN0);
  not not_4 (not_4_out, TickIN);
  not not_5 (not_5_out, IN1);
  not not_6 (not_6_out, IN0);
  not not_7 (not_7_out, IN1);
  not not_8 (not_8_out, TickIN);
  and and_1 (TickOUT, IN1, not_1_out, TickIN);
  and and_2 (and_2_out, not_2_out, IN0, TickIN);
  and and_3 (and_3_out, IN1, not_3_out, not_4_out);
  and and_4 (and_4_out, not_5_out, not_6_out, TickIN);
  and and_5 (and_5_out, not_7_out, IN0, not_8_out);
  or or_1 (OUT1, and_2_out, and_3_out);
  or or_2 (OUT0, and_4_out, and_5_out);
endmodule

module zeroFive (
  input  IN2,
  input  IN1,
  input  IN0,
  input  TickIN,
  output TickOUT,
  output OUT2,
  output OUT1,
  output OUT0
);

  wire and_1_out, and_2_out, and_3_out, and_4_out, and_5_out, and_6_out, and_7_out, nand_1_out, nand_2_out,
       nand_3_out, nand_4_out, nand_5_out, nand_6_out, nand_7_out, nand_8_out, nand_9_out, nand_10_out,
       nand_11_out, nand_12_out, not_1_out, not_2_out, not_3_out, not_4_out, not_5_out, not_6_out, not_7_out,
       not_8_out, not_9_out, not_10_out, not_11_out, not_12_out, not_13_out, not_14_out;

  not not_1 (not_1_out, IN2);
  not not_2 (not_2_out, IN1);
  not not_3 (not_3_out, IN2);
  not not_4 (not_4_out, IN0);
  not not_5 (not_5_out, IN2);
  not not_6 (not_6_out, TickIN);
  not not_7 (not_7_out, IN2);
  not not_8 (not_8_out, IN0);
  not not_9 (not_9_out, IN1);
  not not_10 (not_10_out, IN0);
  not not_11 (not_11_out, IN2);
  not not_12 (not_12_out, TickIN);
  not not_13 (not_13_out, IN1);
  not not_14 (not_14_out, TickIN);
  nand nand_1 (nand_1_out, IN1, IN1);
  nand nand_2 (nand_2_out, IN1, IN1);
  nand nand_3 (nand_3_out, IN2, IN2);
  nand nand_4 (nand_4_out, IN1, IN1);
  nand nand_5 (nand_5_out, IN0, IN0);
  nand nand_6 (nand_6_out, IN1, IN1);
  nand nand_7 (nand_7_out, TickIN, TickIN);
  and and_1 (and_1_out, not_1_out, not_2_out, IN0, TickIN);
  and and_2 (and_2_out, not_3_out, IN1, not_4_out);
  and and_3 (and_3_out, not_5_out, IN1, not_6_out);
  and and_4 (and_4_out, not_7_out, not_8_out, TickIN);
  and and_5 (and_5_out, not_9_out, not_10_out, TickIN);
  and and_6 (and_6_out, not_11_out, IN0, not_12_out);
  and and_7 (and_7_out, not_13_out, IN0, not_14_out);
  nand nand_8 (nand_8_out, TickIN, IN2, nand_1_out, IN0);
  nand nand_9 (nand_9_out, TickIN, IN2, nand_2_out, IN0);
  nand nand_10 (nand_10_out, nand_3_out, IN1, IN0, TickIN);
  nand nand_11 (nand_11_out, IN2, nand_4_out, nand_5_out);
  nand nand_12 (nand_12_out, IN2, nand_6_out, nand_7_out);
  or or_1 (OUT1, and_1_out, and_2_out, and_3_out);
  or or_2 (OUT0, and_4_out, and_5_out, and_6_out, and_7_out);
  nand nand_13 (TickOUT, nand_8_out, nand_9_out);
  nand nand_14 (OUT2, nand_10_out, nand_11_out, nand_12_out);
endmodule

module zeroNine (
  input  IN3,
  input  IN2,
  input  IN1,
  input  IN0,
  input  TickIN,
  output TickOUT,
  output OUT3,
  output OUT2,
  output OUT1,
  output OUT0
);

  wire nand_1_out, nand_2_out, nand_3_out, nand_4_out, nand_5_out, nand_6_out, nand_7_out, nand_8_out,
       nand_9_out, nand_10_out, nand_11_out, nand_12_out, nand_13_out, nand_14_out, nand_15_out, nand_16_out,
       nand_17_out, nand_18_out, nand_19_out, nand_20_out, nand_21_out, nand_22_out, nand_23_out,
       nand_24_out, nand_25_out, nand_26_out, nand_27_out, nand_28_out, nand_29_out, nand_30_out,
       nand_31_out, nand_32_out, nand_33_out, nand_34_out, nand_35_out, nand_36_out, nand_37_out,
       nand_38_out, nand_39_out, nand_40_out, nand_41_out, nand_42_out, nand_43_out, nand_44_out,
       nand_45_out, nand_46_out, nand_47_out, nand_48_out, nand_49_out, nand_50_out, nand_51_out;

  nand nand_1 (nand_1_out, IN2, IN2);
  nand nand_2 (nand_2_out, IN1, IN1);
  nand nand_3 (nand_3_out, IN2, IN2);
  nand nand_4 (nand_4_out, IN1, IN1);
  nand nand_5 (nand_5_out, TickIN, TickIN);
  nand nand_6 (nand_6_out, IN2, IN2);
  nand nand_7 (nand_7_out, IN1, IN1);
  nand nand_8 (nand_8_out, IN2, IN2);
  nand nand_9 (nand_9_out, IN1, IN1);
  nand nand_10 (nand_10_out, IN0, IN0);
  nand nand_11 (nand_11_out, IN3, IN3);
  nand nand_12 (nand_12_out, IN3, IN3);
  nand nand_13 (nand_13_out, IN2, IN2);
  nand nand_14 (nand_14_out, IN3, IN3);
  nand nand_15 (nand_15_out, IN1, IN1);
  nand nand_16 (nand_16_out, IN3, IN3);
  nand nand_17 (nand_17_out, IN0, IN0);
  nand nand_18 (nand_18_out, IN3, IN3);
  nand nand_19 (nand_19_out, TickIN, TickIN);
  nand nand_20 (nand_20_out, IN3, IN3);
  nand nand_21 (nand_21_out, IN1, IN1);
  nand nand_22 (nand_22_out, IN3, IN3);
  nand nand_23 (nand_23_out, IN0, IN0);
  nand nand_24 (nand_24_out, IN3, IN3);
  nand nand_25 (nand_25_out, TickIN, TickIN);
  nand nand_26 (nand_26_out, IN3, IN3);
  nand nand_27 (nand_27_out, IN0, IN0);
  nand nand_28 (nand_28_out, IN2, IN2);
  nand nand_29 (nand_29_out, IN1, IN1);
  nand nand_30 (nand_30_out, IN0, IN0);
  nand nand_31 (nand_31_out, IN3, IN3);
  nand nand_32 (nand_32_out, TickIN, TickIN);
  nand nand_33 (nand_33_out, IN2, IN2);
  nand nand_34 (nand_34_out, IN1, IN1);
  nand nand_35 (nand_35_out, TickIN, TickIN);
  nand nand_36 (nand_36_out, IN3, nand_1_out, nand_2_out, IN0, TickIN);
  nand nand_37 (nand_37_out, IN3, nand_3_out, nand_4_out, IN0, TickIN);
  nand nand_38 (nand_38_out, nand_5_out, IN3, nand_6_out, nand_7_out);
  nand nand_39 (nand_39_out, IN3, nand_8_out, nand_9_out, nand_10_out);
  nand nand_40 (nand_40_out, TickIN, nand_11_out, IN2, IN1, IN0);
  nand nand_41 (nand_41_out, nand_12_out, nand_13_out, IN1, IN0, TickIN);
  nand nand_42 (nand_42_out, nand_14_out, IN2, nand_15_out);
  nand nand_43 (nand_43_out, nand_16_out, IN2, nand_17_out);
  nand nand_44 (nand_44_out, nand_18_out, IN2, nand_19_out);
  nand nand_45 (nand_45_out, nand_20_out, nand_21_out, IN0, TickIN);
  nand nand_46 (nand_46_out, nand_22_out, IN1, nand_23_out);
  nand nand_47 (nand_47_out, nand_24_out, IN1, nand_25_out);
  nand nand_48 (nand_48_out, nand_26_out, nand_27_out, TickIN);
  nand nand_49 (nand_49_out, nand_28_out, nand_29_out, nand_30_out, TickIN);
  nand nand_50 (nand_50_out, nand_31_out, IN0, nand_32_out);
  nand nand_51 (nand_51_out, nand_33_out, nand_34_out, IN0, nand_35_out);
  nand nand_52 (TickOUT, nand_36_out, nand_37_out);
  nand nand_53 (OUT3, nand_38_out, nand_39_out, nand_40_out);
  nand nand_54 (OUT2, nand_41_out, nand_42_out, nand_43_out, nand_44_out);
  nand nand_55 (OUT1, nand_45_out, nand_46_out, nand_47_out);
  nand nand_56 (OUT0, nand_48_out, nand_49_out, nand_50_out, nand_51_out);
endmodule

module zeroNineH (
  input  H,
  input  IN3,
  input  IN2,
  input  IN1,
  input  IN0,
  input  TickIN,
  output TickOUT,
  output OUT3,
  output OUT2,
  output OUT1,
  output OUT0
);

  wire and_1_out, and_2_out, and_3_out, and_4_out, and_5_out, and_6_out, and_7_out, and_8_out, and_9_out,
       and_10_out, and_11_out, and_12_out, and_13_out, and_14_out, and_15_out, and_16_out, and_17_out,
       and_18_out, and_19_out, and_20_out, and_21_out, not_1_out, not_2_out, not_3_out, not_4_out, not_5_out,
       not_6_out, not_7_out, not_8_out, not_9_out, not_10_out, not_11_out, not_12_out, not_13_out,
       not_14_out, not_15_out, not_16_out, not_17_out, not_18_out, not_19_out, not_20_out, not_21_out,
       not_22_out, not_23_out, not_24_out, not_25_out, not_26_out, not_27_out, not_28_out, not_29_out,
       not_30_out, not_31_out, not_32_out, not_33_out, not_34_out, not_35_out, not_36_out, not_37_out,
       not_38_out, not_39_out, not_40_out, not_41_out, not_42_out, not_43_out, not_44_out;

  not not_1 (not_1_out, H);
  not not_2 (not_2_out, IN3);
  not not_3 (not_3_out, IN2);
  not not_4 (not_4_out, H);
  not not_5 (not_5_out, H);
  not not_6 (not_6_out, IN0);
  not not_7 (not_7_out, H);
  not not_8 (not_8_out, TickIN);
  not not_9 (not_9_out, H);
  not not_10 (not_10_out, IN2);
  not not_11 (not_11_out, H);
  not not_12 (not_12_out, IN1);
  not not_13 (not_13_out, H);
  not not_14 (not_14_out, IN0);
  not not_15 (not_15_out, H);
  not not_16 (not_16_out, TickIN);
  not not_17 (not_17_out, H);
  not not_18 (not_18_out, IN3);
  not not_19 (not_19_out, IN1);
  not not_20 (not_20_out, IN3);
  not not_21 (not_21_out, IN2);
  not not_22 (not_22_out, IN1);
  not not_23 (not_23_out, H);
  not not_24 (not_24_out, IN0);
  not not_25 (not_25_out, H);
  not not_26 (not_26_out, TickIN);
  not not_27 (not_27_out, IN3);
  not not_28 (not_28_out, IN2);
  not not_29 (not_29_out, IN0);
  not not_30 (not_30_out, IN3);
  not not_31 (not_31_out, IN2);
  not not_32 (not_32_out, TickIN);
  not not_33 (not_33_out, H);
  not not_34 (not_34_out, H);
  not not_35 (not_35_out, IN0);
  not not_36 (not_36_out, IN3);
  not not_37 (not_37_out, IN2);
  not not_38 (not_38_out, IN0);
  not not_39 (not_39_out, H);
  not not_40 (not_40_out, TickIN);
  not not_41 (not_41_out, IN3);
  not not_42 (not_42_out, IN2);
  not not_43 (not_43_out, TickIN);
  not not_44 (not_44_out, H);
  and and_1 (and_1_out, not_1_out, IN3, IN0, TickIN);
  and and_2 (and_2_out, H, not_2_out, not_3_out, IN1, IN0, TickIN);
  and and_3 (and_3_out, not_4_out, IN2, IN1, IN0, TickIN);
  and and_4 (and_4_out, not_5_out, IN3, not_6_out);
  and and_5 (and_5_out, not_7_out, IN3, not_8_out);
  and and_6 (and_6_out, not_9_out, not_10_out, IN1, IN0, TickIN);
  and and_7 (and_7_out, not_11_out, IN2, not_12_out);
  and and_8 (and_8_out, not_13_out, IN2, not_14_out);
  and and_9 (and_9_out, not_15_out, IN2, not_16_out);
  and and_10 (and_10_out, not_17_out, not_18_out, not_19_out, IN0, TickIN);
  and and_11 (and_11_out, not_20_out, not_21_out, not_22_out, IN0, TickIN);
  and and_12 (and_12_out, not_23_out, IN1, not_24_out);
  and and_13 (and_13_out, not_25_out, IN1, not_26_out);
  and and_14 (and_14_out, not_27_out, not_28_out, IN1, not_29_out);
  and and_15 (and_15_out, not_30_out, not_31_out, IN1, not_32_out);
  and and_16 (and_16_out, not_33_out, IN3, IN2);
  and and_17 (and_17_out, not_34_out, not_35_out, TickIN);
  and and_18 (and_18_out, not_36_out, not_37_out, not_38_out, TickIN);
  and and_19 (and_19_out, not_39_out, IN0, not_40_out);
  and and_20 (and_20_out, not_41_out, not_42_out, IN0, not_43_out);
  and and_21 (and_21_out, not_44_out, IN3, IN2);
  or or_1 (TickOUT, and_1_out, and_2_out);
  or or_2 (OUT3, and_3_out, and_4_out, and_5_out);
  or or_3 (OUT2, and_6_out, and_7_out, and_8_out, and_9_out);
  or or_4 (OUT1, and_10_out, and_11_out, and_12_out, and_13_out, and_14_out, and_15_out, and_16_out);
  or or_5 (OUT0, and_17_out, and_18_out, and_19_out, and_20_out, and_21_out);
endmodule

module zeroTwentythree (
  input  TickIN,
  input  [3:0] loadT_4,
  input  loadTEnDi,
  input  [3:0] loadU_4,
  input  loadUEnDi,
  input  CLK2k,
  input  RESET,
  output TickOUT,
  output [3:0] curT_4,
  output [3:0] curU_4
);

  wire and_1_out, and_2_out, and_3_out, and_4_out, and_5_out, and_6_out, and_7_out, load_2_1_out0,
       load_2_1_out1, load_4_1_out0, load_4_1_out1, load_4_1_out2, load_4_1_out3, zeroNineH_1_out0,
       zeroNineH_1_out1, zeroNineH_1_out2, zeroNineH_1_out3, zeroNineH_1_tickout, zeroTwo_1_out0,
       zeroTwo_1_out1;
  wire [1:0] d_ff_2_q;

  and and_1 (and_1_out, d_ff_2_q[1], ~d_ff_2_q[0]);  // AND_Gate
  zeroTwo zeroTwo_1 (
    .IN1(d_ff_2_q[1]), .IN0(d_ff_2_q[0]), .TickIN(zeroNineH_1_tickout), .TickOUT(TickOUT),
    .OUT1(zeroTwo_1_out1), .OUT0(zeroTwo_1_out0));
  zeroNineH zeroNineH_1 (
    .H(and_1_out), .IN3(curU_4[3]), .IN2(curU_4[2]), .IN1(curU_4[1]), .IN0(curU_4[0]), .TickIN(TickIN),
    .TickOUT(zeroNineH_1_tickout), .OUT3(zeroNineH_1_out3), .OUT2(zeroNineH_1_out2), .OUT1(zeroNineH_1_out1),
    .OUT0(zeroNineH_1_out0));
  load_2 load_2_1 (
    .IN1(zeroTwo_1_out1), .IN0(zeroTwo_1_out0), .loadValue(loadT_4), .loadEnDi(loadTEnDi),
    .OUT1(load_2_1_out1), .OUT0(load_2_1_out0));
  load_4 load_4_1 (
    .IN3(zeroNineH_1_out3), .IN2(zeroNineH_1_out2), .IN1(zeroNineH_1_out1), .IN0(zeroNineH_1_out0),
    .loadValue(loadU_4), .loadEnDi(loadUEnDi), .OUT3(load_4_1_out3), .OUT2(load_4_1_out2),
    .OUT1(load_4_1_out1), .OUT0(load_4_1_out0));
  and and_2 (and_2_out, ~RESET, load_2_1_out1);  // AND_Gate
  and and_3 (and_3_out, ~RESET, load_2_1_out0);  // AND_Gate
  and and_4 (and_4_out, ~RESET, load_4_1_out3);  // AND_Gate
  and and_5 (and_5_out, ~RESET, load_4_1_out2);  // AND_Gate
  and and_6 (and_6_out, ~RESET, load_4_1_out1);  // AND_Gate
  and and_7 (and_7_out, ~RESET, load_4_1_out0);  // AND_Gate
  D_Flip_Flop d_ff_1 (.D(and_2_out), .clk(CLK2k), .Q(d_ff_2_q[1]), .reset(RESET));  // open: Qn, preset
  D_Flip_Flop d_ff_2 (.D(and_3_out), .clk(CLK2k), .Q(d_ff_2_q[0]), .reset(RESET));  // open: Qn, preset
  D_Flip_Flop d_ff_3 (.D(and_4_out), .clk(CLK2k), .Q(curU_4[3]), .reset(RESET));  // open: Qn, preset
  D_Flip_Flop d_ff_4 (.D(and_5_out), .clk(CLK2k), .Q(curU_4[2]), .reset(RESET));  // open: Qn, preset
  D_Flip_Flop d_ff_5 (.D(and_6_out), .clk(CLK2k), .Q(curU_4[1]), .reset(RESET));  // open: Qn, preset
  D_Flip_Flop d_ff_6 (.D(and_7_out), .clk(CLK2k), .Q(curU_4[0]), .reset(RESET));  // open: Qn, preset
  assign curT_4 = {{2{1'b0}}, d_ff_2_q};  // Bit_Extender bit_extender_1
endmodule

module zeroFiftynine (
  input  TickIN,
  input  [3:0] loadT_4,
  input  loadTEnDi,
  input  [3:0] loadU_4,
  input  loadUEnDi,
  input  CLK2k,
  input  RESET,
  output TickOUT,
  output [3:0] curT_4,
  output [3:0] curU_4
);

  wire and_1_out, and_2_out, and_3_out, and_4_out, and_5_out, and_6_out, and_7_out, load_3_1_out0,
       load_3_1_out1, load_3_1_out2, load_4_1_out0, load_4_1_out1, load_4_1_out2, load_4_1_out3,
       zeroFive_1_out0, zeroFive_1_out1, zeroFive_1_out2, zeroNine_1_out0, zeroNine_1_out1, zeroNine_1_out2,
       zeroNine_1_out3, zeroNine_1_tickout;
  wire [2:0] d_ff_3_q;

  zeroFive zeroFive_1 (
    .IN2(d_ff_3_q[2]), .IN1(d_ff_3_q[1]), .IN0(d_ff_3_q[0]), .TickIN(zeroNine_1_tickout), .TickOUT(TickOUT),
    .OUT2(zeroFive_1_out2), .OUT1(zeroFive_1_out1), .OUT0(zeroFive_1_out0));
  zeroNine zeroNine_1 (
    .IN3(curU_4[3]), .IN2(curU_4[2]), .IN1(curU_4[1]), .IN0(curU_4[0]), .TickIN(TickIN),
    .TickOUT(zeroNine_1_tickout), .OUT3(zeroNine_1_out3), .OUT2(zeroNine_1_out2), .OUT1(zeroNine_1_out1),
    .OUT0(zeroNine_1_out0));
  load_3 load_3_1 (
    .IN2(zeroFive_1_out2), .IN1(zeroFive_1_out1), .IN0(zeroFive_1_out0), .loadValue(loadT_4),
    .loadEnDi(loadTEnDi), .OUT2(load_3_1_out2), .OUT1(load_3_1_out1), .OUT0(load_3_1_out0));
  load_4 load_4_1 (
    .IN3(zeroNine_1_out3), .IN2(zeroNine_1_out2), .IN1(zeroNine_1_out1), .IN0(zeroNine_1_out0),
    .loadValue(loadU_4), .loadEnDi(loadUEnDi), .OUT3(load_4_1_out3), .OUT2(load_4_1_out2),
    .OUT1(load_4_1_out1), .OUT0(load_4_1_out0));
  and and_1 (and_1_out, ~RESET, load_3_1_out2);  // AND_Gate
  and and_2 (and_2_out, ~RESET, load_3_1_out1);  // AND_Gate
  and and_3 (and_3_out, ~RESET, load_3_1_out0);  // AND_Gate
  and and_4 (and_4_out, ~RESET, load_4_1_out3);  // AND_Gate
  and and_5 (and_5_out, ~RESET, load_4_1_out2);  // AND_Gate
  and and_6 (and_6_out, ~RESET, load_4_1_out1);  // AND_Gate
  and and_7 (and_7_out, ~RESET, load_4_1_out0);  // AND_Gate
  D_Flip_Flop d_ff_1 (.D(and_1_out), .clk(CLK2k), .Q(d_ff_3_q[2]), .reset(RESET));  // open: Qn, preset
  D_Flip_Flop d_ff_2 (.D(and_2_out), .clk(CLK2k), .Q(d_ff_3_q[1]), .reset(RESET));  // open: Qn, preset
  D_Flip_Flop d_ff_3 (.D(and_3_out), .clk(CLK2k), .Q(d_ff_3_q[0]), .reset(RESET));  // open: Qn, preset
  D_Flip_Flop d_ff_4 (.D(and_4_out), .clk(CLK2k), .Q(curU_4[3]), .reset(RESET));  // open: Qn, preset
  D_Flip_Flop d_ff_5 (.D(and_5_out), .clk(CLK2k), .Q(curU_4[2]), .reset(RESET));  // open: Qn, preset
  D_Flip_Flop d_ff_6 (.D(and_6_out), .clk(CLK2k), .Q(curU_4[1]), .reset(RESET));  // open: Qn, preset
  D_Flip_Flop d_ff_7 (.D(and_7_out), .clk(CLK2k), .Q(curU_4[0]), .reset(RESET));  // open: Qn, preset
  assign curT_4 = {{1{1'b0}}, d_ff_3_q};  // Bit_Extender bit_extender_1
endmodule

module clk32k_to_2k (
  input  CLK32k,
  output CLK2k
);

  wire d_ff_1_q, d_ff_1_qn, d_ff_2_q, d_ff_2_qn, d_ff_3_q, d_ff_3_qn, d_ff_4_qn;

  D_Flip_Flop d_ff_1 (.D(d_ff_1_qn), .clk(CLK32k), .Q(d_ff_1_q), .Qn(d_ff_1_qn));  // open: preset, reset
  D_Flip_Flop d_ff_2 (.D(d_ff_2_qn), .clk(d_ff_1_q), .Q(d_ff_2_q), .Qn(d_ff_2_qn));  // open: preset, reset
  D_Flip_Flop d_ff_3 (.D(d_ff_3_qn), .clk(d_ff_2_q), .Q(d_ff_3_q), .Qn(d_ff_3_qn));  // open: preset, reset
  D_Flip_Flop d_ff_4 (.D(d_ff_4_qn), .clk(d_ff_3_q), .Q(CLK2k), .Qn(d_ff_4_qn));  // open: preset, reset
endmodule

module clk2k_to_ticksec (
  input  RESET,
  input  CLK2k,
  output TickSEC
);

  Counter #(.width(10), .max('h3e9)) counter_1 (
    .clr(RESET), .clk(CLK2k), .carry(TickSEC));  // open: load, up, count, D, Q
endmodule

module HOUR (
  input  RESET,
  input  CLK2k,
  input  [3:0] HloadT_4,
  input  HloadTEnDi,
  input  [3:0] HloadU_4,
  input  HloadUEnDi,
  input  [3:0] MINloadT_4,
  input  MINloadTEnDi,
  input  [3:0] MINloadU_4,
  input  MINloadUEnDi,
  input  [3:0] SECloadT_4,
  input  SECloadTEnDi,
  input  [3:0] SECloadU_4,
  input  SECloadUEnDi,
  output [3:0] HT_4,
  output [3:0] HU_4,
  output [3:0] MINT_4,
  output [3:0] MINU_4,
  output [3:0] SECT_4,
  output [3:0] SECU_4
);

  wire clk2k_to_ticksec_1_ticksec, min_tickout, sec_tickout;

  clk2k_to_ticksec clk2k_to_ticksec_1 (.RESET(RESET), .CLK2k(CLK2k), .TickSEC(clk2k_to_ticksec_1_ticksec));
  zeroTwentythree hour_1 (
    .TickIN(min_tickout), .loadT_4(HloadT_4), .loadTEnDi(HloadTEnDi), .loadU_4(HloadU_4),
    .loadUEnDi(HloadUEnDi), .CLK2k(CLK2k), .RESET(RESET), .curT_4(HT_4), .curU_4(HU_4));  // open: TickOUT
  zeroFiftynine min (
    .TickIN(sec_tickout), .loadT_4(MINloadT_4), .loadTEnDi(MINloadTEnDi), .loadU_4(MINloadU_4),
    .loadUEnDi(MINloadUEnDi), .CLK2k(CLK2k), .RESET(RESET), .TickOUT(min_tickout), .curT_4(MINT_4),
    .curU_4(MINU_4));
  zeroFiftynine sec (
    .TickIN(clk2k_to_ticksec_1_ticksec), .loadT_4(SECloadT_4), .loadTEnDi(SECloadTEnDi),
    .loadU_4(SECloadU_4), .loadUEnDi(SECloadUEnDi), .CLK2k(CLK2k), .RESET(RESET), .TickOUT(sec_tickout),
    .curT_4(SECT_4), .curU_4(SECU_4));
endmodule

module hourOnBoard_HM (
);

  wire clk_clk2k, clock_1_out, DipSwitch_1_sw1, DipSwitch_1_sw10;
  wire [3:0] hour_1_ht_4, hour_1_hu_4, hour_1_mint_4, hour_1_minu_4;
  wire [7:0] hourView_bis_1_sevsegcode_0, hourView_bis_1_sevsegcode_1, hourView_bis_1_sevsegcode_2,
       hourView_bis_1_sevsegcode_3, hourView_bis_1_sevsegcode_4, hourView_bis_1_sevsegcode_5;

  Clock clock_1 (.out(clock_1_out));
  DipSwitch #(.number(10)) DipSwitch_1 (
    .sw1(DipSwitch_1_sw1), .sw10(DipSwitch_1_sw10));  // open: sw2, sw3, sw4, sw5, sw6, sw7, sw8, sw9
  clk32k_to_2k clk (.CLK32k(clock_1_out), .CLK2k(clk_clk2k));
  HOUR hour_1 (
    .RESET(DipSwitch_1_sw1), .CLK2k(clk_clk2k), .HloadT_4(4'b0001), .HloadTEnDi(DipSwitch_1_sw10),
    .HloadU_4(4'b0111), .HloadUEnDi(DipSwitch_1_sw10), .MINloadT_4(4'b0101), .MINloadTEnDi(DipSwitch_1_sw10),
    .MINloadU_4(4'b0110), .MINloadUEnDi(DipSwitch_1_sw10), .SECloadT_4(4'b0000),
    .SECloadTEnDi(DipSwitch_1_sw10), .SECloadU_4(4'b0000), .SECloadUEnDi(DipSwitch_1_sw10),
    .HT_4(hour_1_ht_4), .HU_4(hour_1_hu_4), .MINT_4(hour_1_mint_4), .MINU_4(hour_1_minu_4));  // open: SECT_4, SECU_4
  hourView_HM hourView_bis_1 (
    .HT_4(hour_1_ht_4), .HU_4(hour_1_hu_4), .MINT_4(hour_1_mint_4), .MINU_4(hour_1_minu_4),
    .sevsegCode_5(hourView_bis_1_sevsegcode_5), .sevsegCode_4(hourView_bis_1_sevsegcode_4),
    .sevsegCode_3(hourView_bis_1_sevsegcode_3), .sevsegCode_2(hourView_bis_1_sevsegcode_2),
    .sevsegCode_1(hourView_bis_1_sevsegcode_1), .sevsegCode_0(hourView_bis_1_sevsegcode_0));
  AllSegLeds_bis allsegleds_bis_1 (
    .sevsegCode_5(hourView_bis_1_sevsegcode_5), .sevsegCode_4(hourView_bis_1_sevsegcode_4),
    .sevsegCode_3(hourView_bis_1_sevsegcode_3), .sevsegCode_2(hourView_bis_1_sevsegcode_2),
    .sevsegCode_1(hourView_bis_1_sevsegcode_1), .sevsegCode_0(hourView_bis_1_sevsegcode_0));  // open: sevseg_5, sevseg_4, sevseg_3, sevseg_2, sevseg_1, sevseg_0
endmodule

module hourOnBoard_HMS (
);

  wire changeHour_1_hloadtendi, changeHour_1_hloaduendi, changeHour_1_minloadtendi,
       changeHour_1_minloaduendi, changeHour_1_secloadtendi, changeHour_1_secloaduendi, clk32k_to_2k_1_clk2k,
       clock_1_out, DipSwitch_1_sw1;
  wire [1:0] Button_0_out;
  wire [3:0] changeHour_1_hloadt_4, changeHour_1_hloadu_4, changeHour_1_minloadt_4, changeHour_1_minloadu_4,
       changeHour_1_secloadt_4, changeHour_1_secloadu_4, HOUR_1_ht_4, HOUR_1_hu_4, HOUR_1_mint_4,
       HOUR_1_minu_4, HOUR_1_sect_4, HOUR_1_secu_4;
  wire [7:0] AllSegLeds_bis_1_sevseg_0, AllSegLeds_bis_1_sevseg_1, AllSegLeds_bis_1_sevseg_2,
       AllSegLeds_bis_1_sevseg_3, AllSegLeds_bis_1_sevseg_4, AllSegLeds_bis_1_sevseg_5,
       hourViewHMS_1_sevsegcode_0, hourViewHMS_1_sevsegcode_1, hourViewHMS_1_sevsegcode_2,
       hourViewHMS_1_sevsegcode_3, hourViewHMS_1_sevsegcode_4, hourViewHMS_1_sevsegcode_5;

  Clock clock_1 (.out(clock_1_out));
  Button Button_1 (.out(Button_0_out[1]));
  Button Button_0 (.out(Button_0_out[0]));
  DipSwitch #(.number(10)) DipSwitch_1 (.sw1(DipSwitch_1_sw1));  // open: sw2, sw3, sw4, sw5, sw6, sw7, sw8, sw9, sw10
  clk32k_to_2k clk32k_to_2k_1 (.CLK32k(clock_1_out), .CLK2k(clk32k_to_2k_1_clk2k));
  changeHour changeHour_1 (
    .B0_B1(Button_0_out), .HloadT_4(changeHour_1_hloadt_4), .HloadTEnDi(changeHour_1_hloadtendi),
    .HloadU_4(changeHour_1_hloadu_4), .HloadUEnDi(changeHour_1_hloaduendi),
    .MINloadT_4(changeHour_1_minloadt_4), .MINloadTEnDi(changeHour_1_minloadtendi),
    .MINloadU_4(changeHour_1_minloadu_4), .MINloadUEnDi(changeHour_1_minloaduendi),
    .SECloadT_4(changeHour_1_secloadt_4), .SECloadTEnDi(changeHour_1_secloadtendi),
    .SECloadU_4(changeHour_1_secloadu_4), .SECloadUEnDi(changeHour_1_secloaduendi));
  HOUR HOUR_1 (
    .RESET(DipSwitch_1_sw1), .CLK2k(clk32k_to_2k_1_clk2k), .HloadT_4(changeHour_1_hloadt_4),
    .HloadTEnDi(changeHour_1_hloadtendi), .HloadU_4(changeHour_1_hloadu_4),
    .HloadUEnDi(changeHour_1_hloaduendi), .MINloadT_4(changeHour_1_minloadt_4),
    .MINloadTEnDi(changeHour_1_minloadtendi), .MINloadU_4(changeHour_1_minloadu_4),
    .MINloadUEnDi(changeHour_1_minloaduendi), .SECloadT_4(changeHour_1_secloadt_4),
    .SECloadTEnDi(changeHour_1_secloadtendi), .SECloadU_4(changeHour_1_secloadu_4),
    .SECloadUEnDi(changeHour_1_secloaduendi), .HT_4(HOUR_1_ht_4), .HU_4(HOUR_1_hu_4), .MINT_4(HOUR_1_mint_4),
    .MINU_4(HOUR_1_minu_4), .SECT_4(HOUR_1_sect_4), .SECU_4(HOUR_1_secu_4));
  hourView_HMS hourViewHMS_1 (
    .HT_4(HOUR_1_ht_4), .HU_4(HOUR_1_hu_4), .MINT_4(HOUR_1_mint_4), .MINU_4(HOUR_1_minu_4),
    .SECT_4(HOUR_1_sect_4), .SECU_4(HOUR_1_secu_4), .sevsegCode_5(hourViewHMS_1_sevsegcode_5),
    .sevsegCode_4(hourViewHMS_1_sevsegcode_4), .sevsegCode_3(hourViewHMS_1_sevsegcode_3),
    .sevsegCode_2(hourViewHMS_1_sevsegcode_2), .sevsegCode_1(hourViewHMS_1_sevsegcode_1),
    .sevsegCode_0(hourViewHMS_1_sevsegcode_0));
  AllSegLeds_bis AllSegLeds_bis_1 (
    .sevsegCode_5(hourViewHMS_1_sevsegcode_5), .sevsegCode_4(hourViewHMS_1_sevsegcode_4),
    .sevsegCode_3(hourViewHMS_1_sevsegcode_3), .sevsegCode_2(hourViewHMS_1_sevsegcode_2),
    .sevsegCode_1(hourViewHMS_1_sevsegcode_1), .sevsegCode_0(hourViewHMS_1_sevsegcode_0),
    .sevseg_5(AllSegLeds_bis_1_sevseg_5), .sevseg_4(AllSegLeds_bis_1_sevseg_4),
    .sevseg_3(AllSegLeds_bis_1_sevseg_3), .sevseg_2(AllSegLeds_bis_1_sevseg_2),
    .sevseg_1(AllSegLeds_bis_1_sevseg_1), .sevseg_0(AllSegLeds_bis_1_sevseg_0));
  _7_Segment_Display L_7_Segment_Display_5 (
    .g(AllSegLeds_bis_1_sevseg_5[0]), .f(AllSegLeds_bis_1_sevseg_5[1]), .a(AllSegLeds_bis_1_sevseg_5[6]),
    .b(AllSegLeds_bis_1_sevseg_5[5]), .e(AllSegLeds_bis_1_sevseg_5[2]), .d(AllSegLeds_bis_1_sevseg_5[3]),
    .c(AllSegLeds_bis_1_sevseg_5[4]), .dp(AllSegLeds_bis_1_sevseg_5[7]));
  _7_Segment_Display L_7_Segment_Display_4 (
    .g(AllSegLeds_bis_1_sevseg_4[0]), .f(AllSegLeds_bis_1_sevseg_4[1]), .a(AllSegLeds_bis_1_sevseg_4[6]),
    .b(AllSegLeds_bis_1_sevseg_4[5]), .e(AllSegLeds_bis_1_sevseg_4[2]), .d(AllSegLeds_bis_1_sevseg_4[3]),
    .c(AllSegLeds_bis_1_sevseg_4[4]), .dp(AllSegLeds_bis_1_sevseg_4[7]));
  _7_Segment_Display L_7_Segment_Display_3 (
    .g(AllSegLeds_bis_1_sevseg_3[0]), .f(AllSegLeds_bis_1_sevseg_3[1]), .a(AllSegLeds_bis_1_sevseg_3[6]),
    .b(AllSegLeds_bis_1_sevseg_3[5]), .e(AllSegLeds_bis_1_sevseg_3[2]), .d(AllSegLeds_bis_1_sevseg_3[3]),
    .c(AllSegLeds_bis_1_sevseg_3[4]), .dp(AllSegLeds_bis_1_sevseg_3[7]));
  _7_Segment_Display L_7_Segment_Display_2 (
    .g(AllSegLeds_bis_1_sevseg_2[0]), .f(AllSegLeds_bis_1_sevseg_2[1]), .a(AllSegLeds_bis_1_sevseg_2[6]),
    .b(AllSegLeds_bis_1_sevseg_2[5]), .e(AllSegLeds_bis_1_sevseg_2[2]), .d(AllSegLeds_bis_1_sevseg_2[3]),
    .c(AllSegLeds_bis_1_sevseg_2[4]), .dp(AllSegLeds_bis_1_sevseg_2[7]));
  _7_Segment_Display L_7_Segment_Display_1 (
    .g(AllSegLeds_bis_1_sevseg_1[0]), .f(AllSegLeds_bis_1_sevseg_1[1]), .a(AllSegLeds_bis_1_sevseg_1[6]),
    .b(AllSegLeds_bis_1_sevseg_1[5]), .e(AllSegLeds_bis_1_sevseg_1[2]), .d(AllSegLeds_bis_1_sevseg_1[3]),
    .c(AllSegLeds_bis_1_sevseg_1[4]), .dp(AllSegLeds_bis_1_sevseg_1[7]));
  _7_Segment_Display L_7_Segment_Display_0 (
    .g(AllSegLeds_bis_1_sevseg_0[0]), .f(AllSegLeds_bis_1_sevseg_0[1]), .a(AllSegLeds_bis_1_sevseg_0[6]),
    .b(AllSegLeds_bis_1_sevseg_0[5]), .e(AllSegLeds_bis_1_sevseg_0[2]), .d(AllSegLeds_bis_1_sevseg_0[3]),
    .c(AllSegLeds_bis_1_sevseg_0[4]), .dp(AllSegLeds_bis_1_sevseg_0[7]));
endmodule

module hourView_HM (
  input  [3:0] HT_4,
  input  [3:0] HU_4,
  input  [3:0] MINT_4,
  input  [3:0] MINU_4,
  output [7:0] sevsegCode_5,
  output [7:0] sevsegCode_4,
  output [7:0] sevsegCode_3,
  output [7:0] sevsegCode_2,
  output [7:0] sevsegCode_1,
  output [7:0] sevsegCode_0
);

  wire [6:0] bit_extender_2_out;

  assign sevsegCode_4 = {{4{1'b0}}, HT_4};  // Bit_Extender bit_extender_1
  assign bit_extender_2_out = {{3{1'b0}}, HU_4};  // Bit_Extender bit_extender_2
  assign sevsegCode_2 = {{4{1'b0}}, MINT_4};  // Bit_Extender bit_extender_3
  assign sevsegCode_1 = {{4{1'b0}}, MINU_4};  // Bit_Extender bit_extender_4
  assign sevsegCode_3 = {{1{1'b1}}, bit_extender_2_out};  // Bit_Extender bit_extender_5

  assign sevsegCode_0 = 8'h1f;
  assign sevsegCode_5 = 8'h1f;
endmodule

module hourView_HMS (
  input  [3:0] HT_4,
  input  [3:0] HU_4,
  input  [3:0] MINT_4,
  input  [3:0] MINU_4,
  input  [3:0] SECT_4,
  input  [3:0] SECU_4,
  output [7:0] sevsegCode_5,
  output [7:0] sevsegCode_4,
  output [7:0] sevsegCode_3,
  output [7:0] sevsegCode_2,
  output [7:0] sevsegCode_1,
  output [7:0] sevsegCode_0
);

  wire [6:0] bit_extender_2_out, bit_extender_4_out;

  assign sevsegCode_5 = {{4{1'b0}}, HT_4};  // Bit_Extender bit_extender_1
  assign bit_extender_2_out = {{3{1'b0}}, HU_4};  // Bit_Extender bit_extender_2
  assign sevsegCode_3 = {{4{1'b0}}, MINT_4};  // Bit_Extender bit_extender_3
  assign bit_extender_4_out = {{3{1'b0}}, MINU_4};  // Bit_Extender bit_extender_4
  assign sevsegCode_1 = {{4{1'b0}}, SECT_4};  // Bit_Extender bit_extender_5
  assign sevsegCode_0 = {{4{1'b0}}, SECU_4};  // Bit_Extender bit_extender_6
  assign sevsegCode_4 = {{1{1'b1}}, bit_extender_2_out};  // Bit_Extender bit_extender_7
  assign sevsegCode_2 = {{1{1'b1}}, bit_extender_4_out};  // Bit_Extender bit_extender_8
endmodule

module copypasteLW (
  output out_1,
  output [7:0] H_8,
  output [7:0] MIN_8,
  output [7:0] SEC_8
);

  wire bcd_to_7_segment_decoder_1_p1, bcd_to_7_segment_decoder_4_p1, bcd_to_7_segment_decoder_6_p1,
       binairy_to_bcd_converter_1_p2, clock_1_out, d_ff_1_q, d_ff_1_qn, L_7_Segment_Display_0_p1,
       L_7_Segment_Display_1_p1, L_7_Segment_Display_2_p1, L_7_Segment_Display_3_p1,
       L_7_Segment_Display_4_p1, L_7_Segment_Display_5_p1, n7_segment_display_3_p1, n7_segment_display_5_p1,
       n7_segment_display_7_p1;
  wire [3:0] undriven, undriven_2, undriven_3, undriven_4, undriven_5, undriven_6;
  wire [7:0] multiplier_1_out, multiplier_2_out, multiplier_3_out;
  wire [8:0] counter_2_q;
  wire [9:0] counter_1_q;

  Clock clock_1 (.out(clock_1_out));
  D_Flip_Flop d_ff_1 (.D(d_ff_1_qn), .clk(clock_1_out), .Q(d_ff_1_q), .Qn(d_ff_1_qn));  // open: preset, reset
  Counter #(.width(10), .max('h3e7)) counter_1 (
    .clk(clock_1_out), .Q(counter_1_q));  // open: clr, load, up, count, D, carry
  Counter #(.width(9), .max('h1f3)) counter_2 (
    .clk(d_ff_1_q), .Q(counter_2_q));  // open: clr, load, up, count, D, carry
  Multiplier multiplier_1 (.a({4'b0000, undriven_2}), .b(8'ha), .out(multiplier_1_out));  // open: cin, cout
  Multiplier multiplier_2 (.a({4'b0000, undriven_3}), .b(8'ha), .out(multiplier_2_out));  // open: cin, cout
  Multiplier multiplier_3 (.a({4'b0000, undriven_4}), .b(8'ha), .out(multiplier_3_out));  // open: cin, cout
  Adder adder_1 (.a(multiplier_1_out), .b({4'b0000, undriven_5}), .out(H_8));  // open: cin, cout
  Adder adder_2 (.a(multiplier_2_out), .b({4'b0000, undriven}), .out(MIN_8));  // open: cin, cout
  Adder adder_3 (.a(multiplier_3_out), .b({4'b0000, undriven_6}), .out(SEC_8));  // open: cin, cout
  _7_Segment_Display u_7_segment_display_1 ();  // open: g, f, a, b, e, d, c, dp
  _7_Segment_Display u_7_segment_display_2 ();  // open: g, f, a, b, e, d, c, dp
  // BCD_to_7_Segment_decoder bcd_to_7_segment_decoder_1: pin names not known; wires that end beside it: bcd_to_7_segment_decoder_1_p1
  // BCD_to_7_Segment_decoder bcd_to_7_segment_decoder_2: pin names not known; wires that end beside it: out_1
  // Binairy_to_BCD_converter #(.binvalue(10)) binairy_to_bcd_converter_1: pin names not known; wires that end beside it: counter_1_q, binairy_to_bcd_converter_1_p2, binairy_to_bcd_converter_1_p2, bcd_to_7_segment_decoder_1_p1
  // BCD_to_7_Segment_decoder bcd_to_7_segment_decoder_3: pin names not known
  // _7_Segment_Display 7_segment_display_3: pin names not known; wires that end beside it: n7_segment_display_3_p1, n7_segment_display_3_p1
  // Binairy_to_BCD_converter binairy_to_bcd_converter_2: pin names not known; wires that end beside it: counter_2_q
  // BCD_to_7_Segment_decoder bcd_to_7_segment_decoder_4: pin names not known; wires that end beside it: bcd_to_7_segment_decoder_4_p1, bcd_to_7_segment_decoder_4_p1
  _7_Segment_Display u_7_segment_display_4 ();  // open: g, f, a, b, e, d, c, dp
  // BCD_to_7_Segment_decoder bcd_to_7_segment_decoder_5: pin names not known
  // _7_Segment_Display 7_segment_display_5: pin names not known; wires that end beside it: n7_segment_display_5_p1, n7_segment_display_5_p1
  _7_Segment_Display u_7_segment_display_6 ();  // open: g, f, a, b, e, d, c, dp
  // BCD_to_7_Segment_decoder bcd_to_7_segment_decoder_6: pin names not known; wires that end beside it: bcd_to_7_segment_decoder_6_p1, bcd_to_7_segment_decoder_6_p1
  // BCD_to_7_Segment_decoder bcd_to_7_segment_decoder_7: pin names not known
  // _7_Segment_Display 7_segment_display_7: pin names not known; wires that end beside it: n7_segment_display_7_p1, n7_segment_display_7_p1
  // _7_Segment_Display L_7_Segment_Display_5: pin names not known; wires that end beside it: L_7_Segment_Display_5_p1, L_7_Segment_Display_5_p1
  // BCD_to_7_Segment_decoder bcd_to_7_segment_decoder_8: pin names not known
  // Binairy_to_BCD_converter #(.binvalue(8)) binairy_to_bcd_converter_3: pin names not known
  // _7_Segment_Display L_7_Segment_Display_3: pin names not known; wires that end beside it: L_7_Segment_Display_3_p1, L_7_Segment_Display_3_p1
  // BCD_to_7_Segment_decoder bcd_to_7_segment_decoder_9: pin names not known
  // Binairy_to_BCD_converter #(.binvalue(8)) binairy_to_bcd_converter_4: pin names not known
  // BCD_to_7_Segment_decoder bcd_to_7_segment_decoder_10: pin names not known
  // _7_Segment_Display L_7_Segment_Display_1: pin names not known; wires that end beside it: L_7_Segment_Display_1_p1, L_7_Segment_Display_1_p1
  // Binairy_to_BCD_converter #(.binvalue(8)) binairy_to_bcd_converter_5: pin names not known
  // _7_Segment_Display L_7_Segment_Display_4: pin names not known; wires that end beside it: L_7_Segment_Display_4_p1, L_7_Segment_Display_4_p1
  // BCD_to_7_Segment_decoder bcd_to_7_segment_decoder_11: pin names not known
  // _7_Segment_Display L_7_Segment_Display_2: pin names not known; wires that end beside it: L_7_Segment_Display_2_p1, L_7_Segment_Display_2_p1
  // BCD_to_7_Segment_decoder bcd_to_7_segment_decoder_12: pin names not known
  // _7_Segment_Display L_7_Segment_Display_0: pin names not known; wires that end beside it: L_7_Segment_Display_0_p1, L_7_Segment_Display_0_p1
  // BCD_to_7_Segment_decoder bcd_to_7_segment_decoder_13: pin names not known
endmodule

module load_2 (
  input  IN1,
  input  IN0,
  input  [3:0] loadValue,
  input  loadEnDi,
  output OUT1,
  output OUT0
);

  Multiplexer #(.enable("false")) multiplexer_1 (.in0(IN1), .in1(loadValue[1]), .out(OUT1), .sel(loadEnDi));
  Multiplexer #(.enable("false")) multiplexer_2 (.in0(IN0), .in1(loadValue[0]), .out(OUT0), .sel(loadEnDi));
endmodule

module load_3 (
  input  IN2,
  input  IN1,
  input  IN0,
  input  [3:0] loadValue,
  input  loadEnDi,
  output OUT2,
  output OUT1,
  output OUT0
);

  Multiplexer #(.enable("false")) multiplexer_1 (.in0(IN2), .in1(loadValue[2]), .out(OUT2), .sel(loadEnDi));
  Multiplexer #(.enable("false")) multiplexer_2 (.in0(IN1), .in1(loadValue[1]), .out(OUT1), .sel(loadEnDi));
  Multiplexer #(.enable("false")) multiplexer_3 (.in0(IN0), .in1(loadValue[0]), .out(OUT0), .sel(loadEnDi));
endmodule

module load_4 (
  input  IN3,
  input  IN2,
  input  IN1,
  input  IN0,
  input  [3:0] loadValue,
  input  loadEnDi,
  output OUT3,
  output OUT2,
  output OUT1,
  output OUT0
);

  Multiplexer #(.enable("false")) multiplexer_1 (.in0(IN3), .in1(loadValue[3]), .out(OUT3), .sel(loadEnDi));
  Multiplexer #(.enable("false")) multiplexer_2 (.in0(IN2), .in1(loadValue[2]), .out(OUT2), .sel(loadEnDi));
  Multiplexer #(.enable("false")) multiplexer_3 (.in0(IN1), .in1(loadValue[1]), .out(OUT1), .sel(loadEnDi));
  Multiplexer #(.enable("false")) multiplexer_4 (.in0(IN0), .in1(loadValue[0]), .out(OUT0), .sel(loadEnDi));
endmodule

module changeHour (
  input  [1:0] B0_B1,
  output [3:0] HloadT_4,
  output HloadTEnDi,
  output [3:0] HloadU_4,
  output HloadUEnDi,
  output [3:0] MINloadT_4,
  output MINloadTEnDi,
  output [3:0] MINloadU_4,
  output MINloadUEnDi,
  output [3:0] SECloadT_4,
  output SECloadTEnDi,
  output [3:0] SECloadU_4,
  output SECloadUEnDi
);

  wire demultiplexer_1_out1, demultiplexer_1_out2, demultiplexer_1_out3, demultiplexer_1_out4,
       demultiplexer_1_out5, demultiplexer_1_out6, demultiplexer_2_out0;
  wire [1:0] counter_2_q, counter_3_q;
  wire [2:0] counter_1_q, counter_5_q, counter_8_q;
  wire [3:0] bit_extender_2_out, counter_4_q;

  Counter #(.width(3), .max('h6)) counter_1 (.clk(B0_B1[0]), .Q(counter_1_q));  // open: clr, load, up, count, D, carry
  Demultiplexer #(.select(3), .enable("false")) demultiplexer_1 (
    .out1(demultiplexer_1_out1), .out2(demultiplexer_1_out2), .out3(demultiplexer_1_out3),
    .out4(demultiplexer_1_out4), .out5(demultiplexer_1_out5), .out6(demultiplexer_1_out6), .in(B0_B1[1]),
    .sel(counter_1_q));  // open: out0, out7
  Demultiplexer #(.select(3), .enable("false")) demultiplexer_2 (
    .out0(demultiplexer_2_out0), .out1(HloadTEnDi), .out2(HloadUEnDi), .out3(MINloadTEnDi),
    .out4(MINloadUEnDi), .out5(SECloadTEnDi), .out6(SECloadUEnDi), .in(1'b1), .sel(counter_1_q));  // open: out7
  Counter #(.width(2), .max('h2)) counter_2 (
    .clr(demultiplexer_2_out0), .clk(demultiplexer_1_out1), .Q(counter_2_q));  // open: load, up, count, D, carry
  assign HloadT_4 = {{2{1'b0}}, counter_2_q};  // Bit_Extender bit_extender_1
  Counter #(.width(2), .max('h3)) counter_3 (
    .clr(demultiplexer_2_out0), .clk(demultiplexer_1_out2), .Q(counter_3_q));  // open: load, up, count, D, carry
  Counter #(.width(4), .max('h9)) counter_4 (
    .clr(demultiplexer_2_out0), .clk(demultiplexer_1_out2), .Q(counter_4_q));  // open: load, up, count, D, carry
  Counter #(.width(3), .max('h5)) counter_5 (
    .clr(demultiplexer_2_out0), .clk(demultiplexer_1_out3), .Q(counter_5_q));  // open: load, up, count, D, carry
  Counter #(.width(4), .max('h9)) counter_6 (
    .clr(demultiplexer_2_out0), .clk(demultiplexer_1_out4), .Q(MINloadU_4));  // open: load, up, count, D, carry
  Counter #(.width(4), .max('h9)) counter_7 (
    .clr(demultiplexer_2_out0), .clk(demultiplexer_1_out6), .Q(SECloadU_4));  // open: load, up, count, D, carry
  Counter #(.width(3), .max('h5)) counter_8 (
    .clr(demultiplexer_2_out0), .clk(demultiplexer_1_out5), .Q(counter_8_q));  // open: load, up, count, D, carry
  assign bit_extender_2_out = {{2{1'b0}}, counter_3_q};  // Bit_Extender bit_extender_2
  Multiplexer #(.width(4), .enable("false")) multiplexer_1 (
    .in0(counter_4_q), .in1(bit_extender_2_out), .out(HloadU_4), .sel(counter_2_q[1]));
  assign MINloadT_4 = {{1{1'b0}}, counter_5_q};  // Bit_Extender bit_extender_3
  assign SECloadT_4 = {{1{1'b0}}, counter_8_q};  // Bit_Extender bit_extender_4
endmodule

module changeTimeZoneOnBoard (
);

  wire [3:0] HOUR_1_ht_4, HOUR_1_hu_4, HOUR_1_mint_4, HOUR_1_minu_4, HOUR_1_sect_4, HOUR_1_secu_4;
  wire [7:0] hourView_HMS_1_sevsegcode_0, hourView_HMS_1_sevsegcode_1, hourView_HMS_1_sevsegcode_2,
       hourView_HMS_1_sevsegcode_3, hourView_HMS_1_sevsegcode_4, hourView_HMS_1_sevsegcode_5;

  HOUR HOUR_1 (
    .HT_4(HOUR_1_ht_4), .HU_4(HOUR_1_hu_4), .MINT_4(HOUR_1_mint_4), .MINU_4(HOUR_1_minu_4),
    .SECT_4(HOUR_1_sect_4), .SECU_4(HOUR_1_secu_4));  // open: RESET, CLK2k, HloadT_4, HloadTEnDi, HloadU_4, HloadUEnDi, MINloadT_4, MINloadTEnDi, MINloadU_4, MINloadUEnDi, SECloadT_4, SECloadTEnDi, SECloadU_4, SECloadUEnDi
  hourView_HMS hourView_HMS_1 (
    .HT_4(HOUR_1_ht_4), .HU_4(HOUR_1_hu_4), .MINT_4(HOUR_1_mint_4), .MINU_4(HOUR_1_minu_4),
    .SECT_4(HOUR_1_sect_4), .SECU_4(HOUR_1_secu_4), .sevsegCode_5(hourView_HMS_1_sevsegcode_5),
    .sevsegCode_4(hourView_HMS_1_sevsegcode_4), .sevsegCode_3(hourView_HMS_1_sevsegcode_3),
    .sevsegCode_2(hourView_HMS_1_sevsegcode_2), .sevsegCode_1(hourView_HMS_1_sevsegcode_1),
    .sevsegCode_0(hourView_HMS_1_sevsegcode_0));
  AllSegLeds_bis allsegleds_bis_1 (
    .sevsegCode_5(hourView_HMS_1_sevsegcode_5), .sevsegCode_4(hourView_HMS_1_sevsegcode_4),
    .sevsegCode_3(hourView_HMS_1_sevsegcode_3), .sevsegCode_2(hourView_HMS_1_sevsegcode_2),
    .sevsegCode_1(hourView_HMS_1_sevsegcode_1), .sevsegCode_0(hourView_HMS_1_sevsegcode_0));  // open: sevseg_5, sevseg_4, sevseg_3, sevseg_2, sevseg_1, sevseg_0
endmodule

module changeTimeZone (
  input  [7:0] UTCCode_8
);
endmodule
