// Logisim project hournew.circ as structural Verilog: 20 circuits, main circuit HOUR
module HOUR (
  input  [3:0] HloadT_4,
  input  HloadTEnDi,
  input  [3:0] HloadU_4,
  input  HloadUEnDi,
  input  [3:0] MINloadT_4,
  input  MINloadTEnDi,
  input  [3:0] MINloadU_4,
  input  MINloadUEnDi,
  input  [3:0] SECloadT_4,
  input  SECloadTEnDi,
  input  [3:0] SECloadU_4,
  input  SECloadUEnDi,
  input  CLK2k,
  output [7:0] sevseg5,
  output [7:0] sevseg4,
  output [7:0] sevseg3,
  output [7:0] sevseg2,
  output [7:0] sevseg1,
  output [7:0] sevseg0
);

  wire approx_sec_ticksec, bcd_to_7_segment_decoder_3_p1, clk32_2k_clk2k, minute_module_1_tickout, sec0_p1,
       sec1_p1, seconde_module_1_tickout, sevenseg1_p1, sevenseg2_p1, sevenseg3_p1, sevenseg4_p1;
  wire [3:0] hour_module_1_curt_4, hour_module_1_curu_4, minute_module_1_curt_4, minute_module_1_curu_4,
       seconde_module_1_curt_4, seconde_module_1_curu_4;
  wire [7:0] adder_1_out, adder_2_out, adder_3_out, multiplier_1_out, multiplier_2_out, multiplier_3_out;

  clk32k_to_2k clk32_2k (.CLK32k(CLK2k), .CLK2k(clk32_2k_clk2k));
  clk32k_to_approx_sec approx_sec (.CLK32k(CLK2k), .TickSEC(approx_sec_ticksec));
  hour_module hour_module_1 (
    .loadT_4(HloadT_4), .loadTEnDi(HloadTEnDi), .loadU_4(HloadU_4), .loadUEnDI(HloadUEnDi),
    .CLK32k(clk32_2k_clk2k), .TickIN(minute_module_1_tickout), .curT_4(hour_module_1_curt_4),
    .curU_4(hour_module_1_curu_4));  // open: TickOUT
  minute_module minute_module_1 (
    .loadT_4(MINloadT_4), .loadTEnDi(MINloadTEnDi), .loadU_4(MINloadU_4), .loadUEnDi(MINloadUEnDi),
    .CLK2k(clk32_2k_clk2k), .TickIN(seconde_module_1_tickout), .TickOUT(minute_module_1_tickout),
    .curT_4(minute_module_1_curt_4), .curU_4(minute_module_1_curu_4));
  minute_module seconde_module_1 (
    .loadT_4(SECloadT_4), .loadTEnDi(SECloadTEnDi), .loadU_4(SECloadU_4), .loadUEnDi(SECloadUEnDi),
    .CLK2k(clk32_2k_clk2k), .TickIN(approx_sec_ticksec), .TickOUT(seconde_module_1_tickout),
    .curT_4(seconde_module_1_curt_4), .curU_4(seconde_module_1_curu_4));
  Multiplier multiplier_1 (.a({4'b0000, hour_module_1_curt_4}), .b(8'ha), .out(multiplier_1_out));  // open: cin, cout
  Multiplier multiplier_2 (.a({4'b0000, minute_module_1_curt_4}), .b(8'ha), .out(multiplier_2_out));  // open: cin, cout
  Multiplier multiplier_3 (
    .a({4'b0000, seconde_module_1_curt_4}), .b(8'ha), .out(multiplier_3_out));  // open: cin, cout
  Adder adder_1 (.a(multiplier_1_out), .b({4'b0000, hour_module_1_curu_4}), .out(adder_1_out));  // open: cin, cout
  Adder adder_2 (.a(multiplier_2_out), .b({4'b0000, minute_module_1_curu_4}), .out(adder_2_out));  // open: cin, cout
  Adder adder_3 (.a(multiplier_3_out), .b({4'b0000, seconde_module_1_curu_4}), .out(adder_3_out));  // open: cin, cout
  // _7_Segment_Display sevenseg2: pin names not known; wires that end beside it: sevenseg2_p1, sevenseg2_p1
  // BCD_to_7_Segment_decoder bcd_to_7_segment_decoder_1: pin names not known
  // Binairy_to_BCD_converter #(.binvalue(8)) binairy_to_bcd_converter_1: pin names not known; wires that end beside it: adder_2_out
  // BCD_to_7_Segment_decoder bcd_to_7_segment_decoder_2: pin names not known
  // _7_Segment_Display sec1: pin names not known; wires that end beside it: sec1_p1, sec1_p1
  // Binairy_to_BCD_converter #(.binvalue(8)) binairy_to_bcd_converter_2: pin names not known; wires that end beside it: adder_3_out
  // Binairy_to_BCD_converter #(.binvalue(8)) binairy_to_bcd_converter_3: pin names not known; wires that end beside it: adder_1_out
  // BCD_to_7_Segment_decoder bcd_to_7_segment_decoder_3: pin names not known; wires that end beside it: bcd_to_7_segment_decoder_3_p1, bcd_to_7_segment_decoder_3_p1
  // _7_Segment_Display sevenseg1: pin names not known; wires that end beside it: sevenseg1_p1, sevenseg1_p1
  // BCD_to_7_Segment_decoder bcd_to_7_segment_decoder_4: pin names not known
  // _7_Segment_Display sec0: pin names not known; wires that end beside it: sec0_p1, sec0_p1
  // _7_Segment_Display sevenseg3: pin names not known; wires that end beside it: sevenseg3_p1, sevenseg3_p1
  // BCD_to_7_Segment_decoder bcd_to_7_segment_decoder_5: pin names not known
  // _7_Segment_Display sevenseg4: pin names not known; wires that end beside it: sevenseg4_p1, sevenseg4_p1
  // BCD_to_7_Segment_decoder bcd_to_7_segment_decoder_6: pin names not known
  hourView hourView_1 (
    .min(adder_2_out), .h(adder_1_out), .sevseg5(sevseg5), .sevseg4(sevseg4), .sevseg3(sevseg3),
    .sevseg2(sevseg2), .sevseg1(sevseg1), .sevseg0(sevseg0));
endmodule

module set (
  input  [3:0] IN_4,
  input  [3:0] loadVal_4,
  input  loadEnDi,
  output [3:0] OUT_4
);

  Multiplexer #(.enable("false")) multiplexer_1 (.in0(IN_4[3]), .in1(loadVal_4[3]), .out(OUT_4[3]), .sel(loadEnDi));
  Multiplexer #(.enable("false")) multiplexer_2 (.in0(IN_4[2]), .in1(loadVal_4[2]), .out(OUT_4[2]), .sel(loadEnDi));
  Multiplexer #(.enable("false")) multiplexer_3 (.in0(IN_4[1]), .in1(loadVal_4[1]), .out(OUT_4[1]), .sel(loadEnDi));
  Multiplexer #(.enable("false")) multiplexer_4 (.in0(IN_4[0]), .in1(loadVal_4[0]), .out(OUT_4[0]), .sel(loadEnDi));
endmodule

module hour_module (
  input  [3:0] loadT_4,
  input  loadTEnDi,
  input  [3:0] loadU_4,
  input  loadUEnDI,
  input  CLK32k,
  input  TickIN,
  output TickOUT,
  output [3:0] curT_4,
  output [3:0] curU_4
);

  wire not_1_out, not_2_out, not_3_out, not_4_out, not_5_out, not_6_out, zero_nine_1_tickout;
  wire [3:0] set_1_out_4, set_2_out_4, zero_nine_1_out_4, zero_to_two_1_out_4;

  zero_to_two zero_to_two_1 (
    .IN_4({2'b00, curT_4[1:0]}), .TickIN(zero_nine_1_tickout), .TickOUT(TickOUT), .OUT_4(zero_to_two_1_out_4));
  zero_nine zero_nine_1 (.IN_4(curU_4), .TickIN(TickIN), .TickOUT(zero_nine_1_tickout), .OUT_4(zero_nine_1_out_4));
  set set_1 (.IN_4(zero_to_two_1_out_4), .loadVal_4(loadT_4), .loadEnDi(loadTEnDi), .OUT_4(set_1_out_4));
  set set_2 (.IN_4(zero_nine_1_out_4), .loadVal_4(loadU_4), .loadEnDi(loadUEnDI), .OUT_4(set_2_out_4));
  not not_1 (not_1_out, set_1_out_4[1]);
  not not_2 (not_2_out, set_1_out_4[0]);
  not not_3 (not_3_out, set_2_out_4[3]);
  not not_4 (not_4_out, set_2_out_4[2]);
  not not_5 (not_5_out, set_2_out_4[1]);
  not not_6 (not_6_out, set_2_out_4[0]);
  S_R_Flip_Flop s_r_ff_1 (.S(set_1_out_4[1]), .R(not_1_out), .clk(CLK32k), .Q(curT_4[1]));  // open: reset, Qn, preset
  S_R_Flip_Flop s_r_ff_2 (.S(set_1_out_4[0]), .R(not_2_out), .clk(CLK32k), .Q(curT_4[0]));  // open: reset, Qn, preset
  S_R_Flip_Flop s_r_ff_3 (.S(set_2_out_4[3]), .R(not_3_out), .clk(CLK32k), .Q(curU_4[3]));  // open: reset, Qn, preset
  S_R_Flip_Flop s_r_ff_4 (.S(set_2_out_4[2]), .R(not_4_out), .clk(CLK32k), .Q(curU_4[2]));  // open: reset, Qn, preset
  S_R_Flip_Flop s_r_ff_5 (.S(set_2_out_4[1]), .R(not_5_out), .clk(CLK32k), .Q(curU_4[1]));  // open: reset, Qn, preset
  S_R_Flip_Flop s_r_ff_6 (.S(set_2_out_4[0]), .R(not_6_out), .clk(CLK32k), .Q(curU_4[0]));  // open: reset, Qn, preset

  assign curT_4[3:2] = 2'b00;
endmodule

module minute_module (
  input  [3:0] loadT_4,
  input  loadTEnDi,
  input  [3:0] loadU_4,
  input  loadUEnDi,
  input  CLK2k,
  input  TickIN,
  output TickOUT,
  output [3:0] curT_4,
  output [3:0] curU_4
);

  wire not_1_out, not_2_out, not_3_out, not_4_out, not_5_out, not_6_out, not_7_out, zero_nine_1_tickout;
  wire [3:0] set_1_out_4, set_2_out_4, zero_five_1_out_4, zero_nine_1_out_4;

  zero_five zero_five_1 (
    .IN_4({1'b0, curT_4[2:0]}), .TickIN(zero_nine_1_tickout), .TickOUT(TickOUT), .OUT_4(zero_five_1_out_4));
  zero_nine zero_nine_1 (.IN_4(curU_4), .TickIN(TickIN), .TickOUT(zero_nine_1_tickout), .OUT_4(zero_nine_1_out_4));
  set set_1 (.IN_4(zero_five_1_out_4), .loadVal_4(loadT_4), .loadEnDi(loadTEnDi), .OUT_4(set_1_out_4));
  set set_2 (.IN_4(zero_nine_1_out_4), .loadVal_4(loadU_4), .loadEnDi(loadUEnDi), .OUT_4(set_2_out_4));
  not not_1 (not_1_out, set_1_out_4[2]);
  not not_2 (not_2_out, set_1_out_4[1]);
  not not_3 (not_3_out, set_1_out_4[0]);
  not not_4 (not_4_out, set_2_out_4[3]);
  not not_5 (not_5_out, set_2_out_4[2]);
  not not_6 (not_6_out, set_2_out_4[1]);
  not not_7 (not_7_out, set_2_out_4[0]);
  S_R_Flip_Flop s_r_ff_1 (.S(set_1_out_4[2]), .R(not_1_out), .clk(CLK2k), .Q(curT_4[2]));  // open: reset, Qn, preset
  S_R_Flip_Flop s_r_ff_2 (.S(set_1_out_4[1]), .R(not_2_out), .clk(CLK2k), .Q(curT_4[1]));  // open: reset, Qn, preset
  S_R_Flip_Flop s_r_ff_3 (.S(set_1_out_4[0]), .R(not_3_out), .clk(CLK2k), .Q(curT_4[0]));  // open: reset, Qn, preset
  S_R_Flip_Flop s_r_ff_4 (.S(set_2_out_4[3]), .R(not_4_out), .clk(CLK2k), .Q(curU_4[3]));  // open: reset, Qn, preset
  S_R_Flip_Flop s_r_ff_5 (.S(set_2_out_4[2]), .R(not_5_out), .clk(CLK2k), .Q(curU_4[2]));  // open: reset, Qn, preset
  S_R_Flip_Flop s_r_ff_6 (.S(set_2_out_4[1]), .R(not_6_out), .clk(CLK2k), .Q(curU_4[1]));  // open: reset, Qn, preset
  S_R_Flip_Flop s_r_ff_7 (.S(set_2_out_4[0]), .R(not_7_out), .clk(CLK2k), .Q(curU_4[0]));  // open: reset, Qn, preset

  assign curT_4[3] = 1'b0;
endmodule

module zero_to_nine (
  input  C,
  input  [3:0] IN_4,
  input  TickIN,
  output TickOUT,
  output [3:0] OUT_4
);

  wire and_1_out, and_2_out, and_3_out, and_4_out, and_5_out, and_6_out, and_7_out, and_8_out, and_9_out,
       and_10_out, and_11_out, and_12_out, and_13_out, and_14_out, and_15_out, and_16_out, not_1_out,
       not_2_out, not_3_out, not_4_out, not_5_out, not_6_out, not_7_out, not_8_out, not_9_out, not_10_out,
       not_11_out, not_12_out, not_13_out;

  and and_1 (and_1_out, IN_4[3], IN_4[0], TickIN);
  and and_2 (and_2_out, C, IN_4[1], IN_4[0], TickIN);
  not not_1 (not_1_out, IN_4[0]);
  not not_2 (not_2_out, TickIN);
  not not_3 (not_3_out, C);
  not not_4 (not_4_out, IN_4[2]);
  not not_5 (not_5_out, IN_4[1]);
  not not_6 (not_6_out, IN_4[0]);
  not not_7 (not_7_out, TickIN);
  not not_8 (not_8_out, IN_4[3]);
  not not_9 (not_9_out, IN_4[1]);
  not not_10 (not_10_out, IN_4[0]);
  not not_11 (not_11_out, TickIN);
  not not_12 (not_12_out, IN_4[0]);
  not not_13 (not_13_out, TickIN);
  or or_1 (TickOUT, and_1_out, and_2_out);
  and and_3 (and_3_out, IN_4[2], IN_4[1], IN_4[0], TickIN);
  and and_4 (and_4_out, IN_4[3], not_1_out);
  and and_5 (and_5_out, IN_4[3], not_2_out);
  and and_6 (and_6_out, not_3_out, not_4_out, IN_4[1], IN_4[0], TickIN);
  and and_7 (and_7_out, IN_4[2], not_5_out);
  and and_8 (and_8_out, IN_4[2], not_6_out);
  and and_9 (and_9_out, IN_4[2], not_7_out);
  and and_10 (and_10_out, not_8_out, not_9_out, IN_4[0], TickIN);
  and and_11 (and_11_out, IN_4[1], not_10_out);
  and and_12 (and_12_out, IN_4[1], not_11_out);
  and and_13 (and_13_out, IN_4[3], IN_4[2]);
  and and_14 (and_14_out, not_12_out, TickIN);
  and and_15 (and_15_out, IN_4[0], not_13_out);
  and and_16 (and_16_out, IN_4[3], IN_4[2]);
  or or_2 (OUT_4[3], and_3_out, and_4_out, and_5_out);
  or or_3 (OUT_4[2], and_6_out, and_7_out, and_8_out, and_9_out);
  or or_4 (OUT_4[1], and_10_out, and_11_out, and_12_out, and_13_out);
  or or_5 (OUT_4[0], and_14_out, and_15_out, and_16_out);
endmodule

module zero_to_two (
  input  [3:0] IN_4,
  input  TickIN,
  output TickOUT,
  output [3:0] OUT_4
);

  wire and_2_out, and_3_out, and_4_out, and_5_out, not_1_out, not_2_out, not_3_out, not_4_out;

  and and_1 (TickOUT, IN_4[1], TickIN);
  not not_1 (not_1_out, TickIN);
  not not_2 (not_2_out, IN_4[1]);
  not not_3 (not_3_out, IN_4[0]);
  not not_4 (not_4_out, TickIN);
  and and_2 (and_2_out, IN_4[0], TickIN);
  and and_3 (and_3_out, IN_4[1], not_1_out);
  and and_4 (and_4_out, not_2_out, not_3_out, TickIN);
  and and_5 (and_5_out, IN_4[0], not_4_out);
  or or_1 (OUT_4[1], and_2_out, and_3_out);
  or or_2 (OUT_4[0], and_4_out, and_5_out);

  assign OUT_4[3:2] = 2'b00;
endmodule

module zero_nine (
  input  [3:0] IN_4,
  input  TickIN,
  output TickOUT,
  output [3:0] OUT_4
);

  wire and_2_out, and_3_out, and_4_out, and_5_out, and_6_out, and_7_out, and_8_out, and_9_out, and_10_out,
       and_11_out, and_12_out, and_13_out, and_14_out, and_15_out, not_1_out, not_2_out, not_3_out,
       not_4_out, not_5_out, not_6_out, not_7_out, not_8_out, not_9_out, not_10_out, not_11_out, not_12_out,
       not_13_out, not_14_out, not_15_out, not_16_out, not_17_out, not_18_out, not_19_out, not_20_out,
       not_21_out, not_22_out, not_23_out, not_24_out, not_25_out, not_26_out, not_27_out, not_28_out,
       not_29_out, not_30_out, not_31_out, not_32_out, not_33_out;

  not not_1 (not_1_out, IN_4[2]);
  not not_2 (not_2_out, IN_4[1]);
  not not_3 (not_3_out, IN_4[3]);
  not not_4 (not_4_out, IN_4[2]);
  not not_5 (not_5_out, IN_4[1]);
  not not_6 (not_6_out, IN_4[0]);
  not not_7 (not_7_out, IN_4[2]);
  not not_8 (not_8_out, IN_4[1]);
  not not_9 (not_9_out, TickIN);
  not not_10 (not_10_out, IN_4[3]);
  not not_11 (not_11_out, IN_4[2]);
  not not_12 (not_12_out, IN_4[3]);
  not not_13 (not_13_out, IN_4[1]);
  not not_14 (not_14_out, IN_4[2]);
  not not_15 (not_15_out, IN_4[1]);
  not not_16 (not_16_out, IN_4[0]);
  not not_17 (not_17_out, IN_4[2]);
  not not_18 (not_18_out, IN_4[1]);
  not not_19 (not_19_out, TickIN);
  and and_1 (TickOUT, IN_4[3], not_1_out, not_2_out, IN_4[0], TickIN);
  and and_2 (and_2_out, not_3_out, IN_4[2], IN_4[1], IN_4[0], TickIN);
  and and_3 (and_3_out, IN_4[3], not_4_out, not_5_out, not_6_out);
  and and_4 (and_4_out, IN_4[3], not_7_out, not_8_out, not_9_out);
  and and_5 (and_5_out, not_10_out, not_11_out, IN_4[1], IN_4[0], TickIN);
  not not_20 (not_20_out, IN_4[3]);
  and and_6 (and_6_out, not_20_out, IN_4[2], not_21_out);
  not not_21 (not_21_out, IN_4[1]);
  not not_22 (not_22_out, IN_4[3]);
  and and_7 (and_7_out, not_22_out, IN_4[2], not_23_out);
  not not_23 (not_23_out, IN_4[0]);
  not not_24 (not_24_out, IN_4[3]);
  and and_8 (and_8_out, not_24_out, IN_4[2], not_25_out);
  not not_25 (not_25_out, TickIN);
  and and_9 (and_9_out, not_12_out, not_13_out, IN_4[0], TickIN);
  not not_26 (not_26_out, IN_4[3]);
  and and_10 (and_10_out, not_26_out, IN_4[1], not_27_out);
  not not_27 (not_27_out, IN_4[0]);
  not not_28 (not_28_out, IN_4[3]);
  and and_11 (and_11_out, not_28_out, IN_4[1], not_29_out);
  not not_29 (not_29_out, TickIN);
  not not_30 (not_30_out, IN_4[3]);
  not not_31 (not_31_out, IN_4[0]);
  and and_12 (and_12_out, not_30_out, not_31_out, TickIN);
  and and_13 (and_13_out, not_14_out, not_15_out, not_16_out, TickIN);
  not not_32 (not_32_out, IN_4[3]);
  and and_14 (and_14_out, not_32_out, IN_4[0], not_33_out);
  not not_33 (not_33_out, TickIN);
  and and_15 (and_15_out, not_17_out, not_18_out, IN_4[0], not_19_out);
  or or_1 (OUT_4[3], and_2_out, and_3_out, and_4_out);
  or or_2 (OUT_4[2], and_5_out, and_6_out, and_7_out, and_8_out);
  or or_3 (OUT_4[1], and_9_out, and_10_out, and_11_out);
  or or_4 (OUT_4[0], and_12_out, and_13_out, and_14_out, and_15_out);
endmodule

module zero_five (
  input  [3:0] IN_4,
  input  TickIN,
  output TickOUT,
  output [3:0] OUT_4
);

  wire and_2_out, and_3_out, and_4_out, and_5_out, and_6_out, and_7_out, and_8_out, and_9_out, and_10_out,
       and_11_out, not_1_out, not_2_out, not_3_out, not_4_out, not_5_out, not_6_out, not_7_out, not_8_out,
       not_9_out, not_10_out, not_11_out, not_12_out, not_13_out, not_14_out, not_15_out, not_16_out,
       not_17_out, not_18_out, not_19_out;

  not not_1 (not_1_out, IN_4[1]);
  not not_2 (not_2_out, IN_4[2]);
  not not_3 (not_3_out, IN_4[1]);
  not not_4 (not_4_out, IN_4[0]);
  not not_5 (not_5_out, IN_4[1]);
  not not_6 (not_6_out, TickIN);
  not not_7 (not_7_out, IN_4[2]);
  not not_8 (not_8_out, IN_4[1]);
  not not_9 (not_9_out, IN_4[2]);
  not not_10 (not_10_out, IN_4[0]);
  not not_11 (not_11_out, IN_4[2]);
  not not_12 (not_12_out, TickIN);
  not not_13 (not_13_out, IN_4[1]);
  not not_14 (not_14_out, IN_4[0]);
  not not_15 (not_15_out, IN_4[2]);
  not not_16 (not_16_out, IN_4[0]);
  not not_17 (not_17_out, IN_4[1]);
  not not_18 (not_18_out, TickIN);
  not not_19 (not_19_out, IN_4[2]);
  and and_1 (TickOUT, IN_4[2], not_1_out, IN_4[0], TickIN);
  and and_2 (and_2_out, not_2_out, IN_4[1], IN_4[0], TickIN);
  and and_3 (and_3_out, IN_4[2], not_3_out, not_4_out);
  and and_4 (and_4_out, IN_4[2], not_5_out, not_6_out);
  and and_5 (and_5_out, not_7_out, not_8_out, IN_4[0], TickIN);
  and and_6 (and_6_out, not_9_out, IN_4[1], not_10_out);
  and and_7 (and_7_out, not_11_out, IN_4[1], not_12_out);
  and and_8 (and_8_out, IN_4[2], not_13_out, not_14_out, TickIN);
  and and_9 (and_9_out, not_15_out, not_16_out, TickIN);
  or or_1 (OUT_4[0], and_9_out, and_10_out, and_11_out);
  and and_10 (and_10_out, not_17_out, IN_4[0], not_18_out);
  and and_11 (and_11_out, not_19_out, IN_4[1], IN_4[0]);
  or or_2 (OUT_4[2], and_2_out, and_3_out, and_4_out);
  or or_3 (OUT_4[1], and_5_out, and_6_out, and_7_out, and_8_out);

  assign OUT_4[3] = 1'b0;
endmodule

module clk32k_to_1k (
  input  CLK32k,
  output CLK1k
);

  wire d_ff_1_q, d_ff_1_qn, d_ff_2_q, d_ff_2_qn, d_ff_3_q, d_ff_3_qn, d_ff_4_q, d_ff_4_qn, d_ff_5_qn;

  D_Flip_Flop d_ff_1 (.D(d_ff_1_qn), .clk(CLK32k), .Q(d_ff_1_q), .Qn(d_ff_1_qn));  // open: preset, reset
  D_Flip_Flop d_ff_2 (.D(d_ff_2_qn), .clk(d_ff_1_q), .Q(d_ff_2_q), .Qn(d_ff_2_qn));  // open: preset, reset
  D_Flip_Flop d_ff_3 (.D(d_ff_3_qn), .clk(d_ff_2_q), .Q(d_ff_3_q), .Qn(d_ff_3_qn));  // open: preset, reset
  D_Flip_Flop d_ff_4 (.D(d_ff_4_qn), .clk(d_ff_3_q), .Q(d_ff_4_q), .Qn(d_ff_4_qn));  // open: preset, reset
  D_Flip_Flop d_ff_5 (.D(d_ff_5_qn), .clk(d_ff_4_q), .Q(CLK1k), .Qn(d_ff_5_qn));  // open: preset, reset
endmodule

module clk32k_to_tickcsec (
  input  CLK32k,
  output TICKcsec
);

  wire clk32k_to_1k_1_clk1k;

  clk32k_to_1k clk32k_to_1k_1 (.CLK32k(CLK32k), .CLK1k(clk32k_to_1k_1_clk1k));
  Counter #(.width(3), .max('h4)) counter_1 (
    .clk(clk32k_to_1k_1_clk1k), .carry(TICKcsec));  // open: clr, load, up, count, D, Q
endmodule

module clk32k_to_ticksec (
  input  CLK32k,
  output TICKsec
);

  wire clk32k_to_tickcsec_1_tickcsec;

  LED LED2 (.in(clk32k_to_tickcsec_1_tickcsec));
  Counter #(.width(7), .max('h64)) counter_1 (
    .clk(clk32k_to_tickcsec_1_tickcsec), .carry(TICKsec));  // open: clr, load, up, count, D, Q
  clk32k_to_tickcsec clk32k_to_tickcsec_1 (.CLK32k(CLK32k), .TICKcsec(clk32k_to_tickcsec_1_tickcsec));
endmodule

module clk32k_to_tickmin (
  input  CLK32k,
  output TICKmin
);

  wire clk32k_to_ticksec_1_ticksec;

  clk32k_to_ticksec clk32k_to_ticksec_1 (.CLK32k(CLK32k), .TICKsec(clk32k_to_ticksec_1_ticksec));
  LED LED0 (.in(clk32k_to_ticksec_1_ticksec));
  Counter #(.width(6), .max('h3c)) counter_1 (
    .clk(clk32k_to_ticksec_1_ticksec), .carry(TICKmin));  // open: clr, load, up, count, D, Q
  LED LED1 (.in(TICKmin));
endmodule

module hourOnBoard (
);

  wire clock_1_out, DipSwitch_1_sw1;

  Clock clock_1 (.out(clock_1_out));
  DipSwitch #(.number(10)) DipSwitch_1 (.sw1(DipSwitch_1_sw1));  // open: sw2, sw3, sw4, sw5, sw6, sw7, sw8, sw9, sw10
  HOUR horloge (
    .HloadT_4(4'b0001), .HloadTEnDi(DipSwitch_1_sw1), .HloadU_4(4'b0010), .HloadUEnDi(DipSwitch_1_sw1),
    .MINloadT_4(4'b0011), .MINloadTEnDi(DipSwitch_1_sw1), .MINloadU_4(4'b1001),
    .MINloadUEnDi(DipSwitch_1_sw1), .SECloadT_4(4'b0011), .SECloadTEnDi(DipSwitch_1_sw1),
    .SECloadU_4(4'b1001), .SECloadUEnDi(DipSwitch_1_sw1), .CLK2k(clock_1_out));  // open: sevseg5, sevseg4, sevseg3, sevseg2, sevseg1, sevseg0
endmodule

module copypaste (
  input  in_1,
  input  in_2,
  input  in_3,
  output out_4,
  output out_5,
  output out_6,
  output out_7
);

  wire clk2k_to_aprox_sec_1_tickout, clock_1_out, counterBase_12_tickout, counterBase_13_tickout,
       counterBase_14_tickout, counterBase_15_tickout, counterBase_16_tickout, counterBase_17_tickout,
       undriven, undriven_2, undriven_3, undriven_4;
  wire [7:0] undriven_5, undriven_6, undriven_7, undriven_8, undriven_9, undriven_10;

  Clock clock_1 (.out(clock_1_out));
  D_Flip_Flop d_ff_1 (.D(in_2), .clk(undriven_3), .Q(out_6));  // open: Qn, preset, reset
  T_Flip_Flop t_ff_1 (.T(in_3), .clk(undriven_2), .Q(out_7));  // open: Qn, reset, preset
  clk2k_to_aprox_sec clk2k_to_aprox_sec_1 (.CLK2k(clock_1_out), .TickOUT(clk2k_to_aprox_sec_1_tickout));
  S_R_Flip_Flop s_r_ff_1 (.S(in_1), .R(in_1), .clk(undriven), .Q(out_5));  // open: reset, Qn, preset
  Counter counter_1 (.clk(clk2k_to_aprox_sec_1_tickout));  // open: clr, load, up, count, D, carry, Q
  _7_Segment_Display sevseg5 (
    .g(undriven_5[6]), .f(undriven_5[5]), .a(undriven_5[0]), .b(undriven_5[1]), .e(undriven_5[4]),
    .d(undriven_5[3]), .c(undriven_5[2]), .dp(undriven_5[7]));
  counterBase counterBase_12 (
    .TickIN(counterBase_13_tickout), .CLK2k(undriven_4), .TickOUT(counterBase_12_tickout));  // open: curVal
  counterBase counterBase_13 (
    .TickIN(counterBase_14_tickout), .CLK2k(undriven_4), .TickOUT(counterBase_13_tickout));  // open: curVal
  counterBase counterBase_14 (
    .TickIN(counterBase_15_tickout), .CLK2k(undriven_4), .TickOUT(counterBase_14_tickout));  // open: curVal
  counterBase counterBase_15 (
    .TickIN(counterBase_16_tickout), .CLK2k(undriven_4), .TickOUT(counterBase_15_tickout));  // open: curVal
  counterBase counterBase_16 (
    .TickIN(counterBase_17_tickout), .CLK2k(undriven_4), .TickOUT(counterBase_16_tickout));  // open: curVal
  counterBase counterBase_17 (.CLK2k(undriven_4), .TickOUT(counterBase_17_tickout));  // open: TickIN, curVal
  _7_Segment_Display sevseg4 (
    .g(undriven_6[6]), .f(undriven_6[5]), .a(undriven_6[0]), .b(undriven_6[1]), .e(undriven_6[4]),
    .d(undriven_6[3]), .c(undriven_6[2]), .dp(undriven_6[7]));
  _7_Segment_Display sevseg3 (
    .g(undriven_7[6]), .f(undriven_7[5]), .a(undriven_7[0]), .b(undriven_7[1]), .e(undriven_7[4]),
    .d(undriven_7[3]), .c(undriven_7[2]), .dp(undriven_7[7]));
  _7_Segment_Display sevseg2 (
    .g(undriven_9[6]), .f(undriven_9[5]), .a(undriven_9[0]), .b(undriven_9[1]), .e(undriven_9[4]),
    .d(undriven_9[3]), .c(undriven_9[2]), .dp(undriven_9[7]));
  _7_Segment_Display sevseg1 (
    .g(undriven_8[6]), .f(undriven_8[5]), .a(undriven_8[0]), .b(undriven_8[1]), .e(undriven_8[4]),
    .d(undriven_8[3]), .c(undriven_8[2]), .dp(undriven_8[7]));
  _7_Segment_Display sevseg0 (
    .g(undriven_10[6]), .f(undriven_10[5]), .a(undriven_10[0]), .b(undriven_10[1]), .e(undriven_10[4]),
    .d(undriven_10[3]), .c(undriven_10[2]), .dp(undriven_10[7]));
endmodule

module minuteOnly (
  input  [3:0] loadT_4,
  input  LoadT,
  input  [3:0] loadU_4,
  input  LoadU,
  input  CLK32k
);

  wire clk32k_to_2k_1_clk2k, clk32k_to_aprox_min_1_tickout, sevsegg1_p1, sevsegg2_p1;
  wire [3:0] minmodule_curt_4, minmodule_curu_4;
  wire [7:0] adder_1_out, multiplier_1_out;

  clk32k_to_2k clk32k_to_2k_1 (.CLK32k(CLK32k), .CLK2k(clk32k_to_2k_1_clk2k));
  clk2k_to_aprox_sec clk32k_to_aprox_min_1 (.CLK2k(CLK32k), .TickOUT(clk32k_to_aprox_min_1_tickout));
  minute_module minmodule (
    .loadT_4(loadT_4), .loadTEnDi(LoadT), .loadU_4(loadU_4), .loadUEnDi(LoadU), .CLK2k(clk32k_to_2k_1_clk2k),
    .TickIN(clk32k_to_aprox_min_1_tickout), .curT_4(minmodule_curt_4), .curU_4(minmodule_curu_4));  // open: TickOUT
  Multiplier multiplier_1 (.a({4'b0000, minmodule_curt_4}), .b(8'ha), .out(multiplier_1_out));  // open: cin, cout
  Adder adder_1 (.a(multiplier_1_out), .b({4'b0000, minmodule_curu_4}), .out(adder_1_out));  // open: cin, cout
  // BCD_to_7_Segment_decoder bcd_to_7_segment_decoder_1: pin names not known
  // _7_Segment_Display sevsegg2: pin names not known; wires that end beside it: sevsegg2_p1, sevsegg2_p1
  // Binairy_to_BCD_converter #(.binvalue(8)) binairy_to_bcd_converter_1: pin names not known; wires that end beside it: adder_1_out
  // BCD_to_7_Segment_decoder bcd_to_7_segment_decoder_2: pin names not known
  // _7_Segment_Display sevsegg1: pin names not known; wires that end beside it: sevsegg1_p1, sevsegg1_p1
endmodule

module minOnlyOnBoard (
);

  wire clock_1_out, DipSwitch_1_sw1;

  Clock clock_1 (.out(clock_1_out));
  DipSwitch #(.number(10)) DipSwitch_1 (.sw1(DipSwitch_1_sw1));  // open: sw2, sw3, sw4, sw5, sw6, sw7, sw8, sw9, sw10
  minuteOnly minonly (
    .loadT_4(4'b0100), .LoadT(DipSwitch_1_sw1), .loadU_4(4'b0111), .LoadU(DipSwitch_1_sw1),
    .CLK32k(clock_1_out));
endmodule

module counterBase (
  input  TickIN,
  input  CLK2k,
  output TickOUT,
  output curVal
);

  wire nand_1_out, nand_2_out, nand_3_out, nand_5_out, nand_6_out, nand_7_out, not_1_out;

  nand nand_1 (nand_1_out, TickIN, curVal);
  nand nand_2 (nand_2_out, TickIN, TickIN);
  nand nand_3 (nand_3_out, curVal, curVal);
  nand nand_4 (TickOUT, nand_1_out, nand_1_out);
  nand nand_5 (nand_5_out, nand_2_out, curVal);
  nand nand_6 (nand_6_out, TickIN, nand_3_out);
  nand nand_7 (nand_7_out, nand_5_out, nand_6_out);
  S_R_Flip_Flop s_r_ff_1 (.S(nand_7_out), .R(not_1_out), .clk(CLK2k), .Q(curVal));  // open: reset, Qn, preset
  not not_1 (not_1_out, nand_7_out);
endmodule

module clk2k_to_aprox_sec (
  input  CLK2k,
  output TickOUT
);

  wire counterBase_2_tickout, counterBase_3_tickout, counterBase_4_tickout, counterBase_5_tickout,
       counterBase_6_tickout, counterBase_7_tickout, counterBase_8_tickout, counterBase_9_tickout,
       counterBase_10_tickout, counterBase_11_tickout;

  counterBase counterBase_1 (.TickIN(counterBase_2_tickout), .CLK2k(CLK2k), .TickOUT(TickOUT));  // open: curVal
  counterBase counterBase_2 (
    .TickIN(counterBase_3_tickout), .CLK2k(CLK2k), .TickOUT(counterBase_2_tickout));  // open: curVal
  counterBase counterBase_3 (
    .TickIN(counterBase_4_tickout), .CLK2k(CLK2k), .TickOUT(counterBase_3_tickout));  // open: curVal
  counterBase counterBase_4 (
    .TickIN(counterBase_5_tickout), .CLK2k(CLK2k), .TickOUT(counterBase_4_tickout));  // open: curVal
  counterBase counterBase_5 (
    .TickIN(counterBase_6_tickout), .CLK2k(CLK2k), .TickOUT(counterBase_5_tickout));  // open: curVal
  counterBase counterBase_6 (
    .TickIN(counterBase_7_tickout), .CLK2k(CLK2k), .TickOUT(counterBase_6_tickout));  // open: curVal
  counterBase counterBase_7 (
    .TickIN(counterBase_8_tickout), .CLK2k(CLK2k), .TickOUT(counterBase_7_tickout));  // open: curVal
  counterBase counterBase_8 (
    .TickIN(counterBase_9_tickout), .CLK2k(CLK2k), .TickOUT(counterBase_8_tickout));  // open: curVal
  counterBase counterBase_9 (
    .TickIN(counterBase_10_tickout), .CLK2k(CLK2k), .TickOUT(counterBase_9_tickout));  // open: curVal
  counterBase counterBase_10 (
    .TickIN(counterBase_11_tickout), .CLK2k(CLK2k), .TickOUT(counterBase_10_tickout));  // open: curVal
  counterBase counterBase_11 (.CLK2k(CLK2k), .TickOUT(counterBase_11_tickout));  // open: TickIN, curVal
endmodule

module clk32k_to_2k (
  input  CLK32k,
  output CLK2k
);

  wire d_ff_1_q, d_ff_1_qn, d_ff_2_q, d_ff_2_qn, d_ff_3_q, d_ff_3_qn, d_ff_4_qn;

  D_Flip_Flop d_ff_1 (.D(d_ff_1_qn), .clk(CLK32k), .Q(d_ff_1_q), .Qn(d_ff_1_qn));  // open: preset, reset
  D_Flip_Flop d_ff_2 (.D(d_ff_2_qn), .clk(d_ff_1_q), .Q(d_ff_2_q), .Qn(d_ff_2_qn));  // open: preset, reset
  D_Flip_Flop d_ff_3 (.D(d_ff_3_qn), .clk(d_ff_2_q), .Q(d_ff_3_q), .Qn(d_ff_3_qn));  // open: preset, reset
  D_Flip_Flop d_ff_4 (.D(d_ff_4_qn), .clk(d_ff_3_q), .Q(CLK2k), .Qn(d_ff_4_qn));  // open: preset, reset
endmodule

module clk32k_to_approx_sec (
  input  CLK32k,
  output TickSEC
);

  wire clk32k_to_2k_1_clk2k;

  Counter #(.width(10), .max('h3ff)) counter_1 (
    .clk(clk32k_to_2k_1_clk2k), .carry(TickSEC));  // open: clr, load, up, count, D, Q
  clk32k_to_2k clk32k_to_2k_1 (.CLK32k(CLK32k), .CLK2k(clk32k_to_2k_1_clk2k));
endmodule
