// Logisim project timer.circ as structural Verilog: 2 circuits, main circuit timerOnboard
module timerOnboard (
);

  wire button0_out, dipswitch_1_sw1, dipswitch_1_sw2;
  wire [7:0] TIMER_1_sevseg0, TIMER_1_sevseg1, TIMER_1_sevseg2, TIMER_1_sevseg3, TIMER_1_sevseg4,
       TIMER_1_sevseg5;

  Button button0 (.out(button0_out));
  DipSwitch #(.number(10)) dipswitch_1 (
    .sw1(dipswitch_1_sw1), .sw2(dipswitch_1_sw2));  // open: sw3, sw4, sw5, sw6, sw7, sw8, sw9, sw10
  TIMER TIMER_1 (
    .StartStop(dipswitch_1_sw1), .ResetEnDi(dipswitch_1_sw2), .minInc(button0_out),
    .sevseg0(TIMER_1_sevseg0), .sevseg1(TIMER_1_sevseg1), .sevseg2(TIMER_1_sevseg2),
    .sevseg3(TIMER_1_sevseg3), .sevseg4(TIMER_1_sevseg4), .sevseg5(TIMER_1_sevseg5));
  _7_Segment_Display L_7_Segment_Display_1 (
    .g(TIMER_1_sevseg5[6]), .f(TIMER_1_sevseg5[5]), .a(TIMER_1_sevseg5[0]), .b(TIMER_1_sevseg5[1]),
    .e(TIMER_1_sevseg5[4]), .d(TIMER_1_sevseg5[3]), .c(TIMER_1_sevseg5[2]), .dp(TIMER_1_sevseg5[7]));
  _7_Segment_Display L_7_Segment_Display_2 (
    .g(TIMER_1_sevseg4[6]), .f(TIMER_1_sevseg4[5]), .a(TIMER_1_sevseg4[0]), .b(TIMER_1_sevseg4[1]),
    .e(TIMER_1_sevseg4[4]), .d(TIMER_1_sevseg4[3]), .c(TIMER_1_sevseg4[2]), .dp(TIMER_1_sevseg4[7]));
  _7_Segment_Display L_7_Segment_Display_3 (
    .g(TIMER_1_sevseg3[6]), .f(TIMER_1_sevseg3[5]), .a(TIMER_1_sevseg3[0]), .b(TIMER_1_sevseg3[1]),
    .e(TIMER_1_sevseg3[4]), .d(TIMER_1_sevseg3[3]), .c(TIMER_1_sevseg3[2]), .dp(TIMER_1_sevseg3[7]));
  _7_Segment_Display L_7_Segment_Display_4 (
    .g(TIMER_1_sevseg2[6]), .f(TIMER_1_sevseg2[5]), .a(TIMER_1_sevseg2[0]), .b(TIMER_1_sevseg2[1]),
    .e(TIMER_1_sevseg2[4]), .d(TIMER_1_sevseg2[3]), .c(TIMER_1_sevseg2[2]), .dp(TIMER_1_sevseg2[7]));
  _7_Segment_Display L_7_Segment_Display_5 (
    .g(TIMER_1_sevseg1[6]), .f(TIMER_1_sevseg1[5]), .a(TIMER_1_sevseg1[0]), .b(TIMER_1_sevseg1[1]),
    .e(TIMER_1_sevseg1[4]), .d(TIMER_1_sevseg1[3]), .c(TIMER_1_sevseg1[2]), .dp(TIMER_1_sevseg1[7]));
  _7_Segment_Display L_7_Segment_Display_6 (
    .g(TIMER_1_sevseg0[6]), .f(TIMER_1_sevseg0[5]), .a(TIMER_1_sevseg0[0]), .b(TIMER_1_sevseg0[1]),
    .e(TIMER_1_sevseg0[4]), .d(TIMER_1_sevseg0[3]), .c(TIMER_1_sevseg0[2]), .dp(TIMER_1_sevseg0[7]));
endmodule

module TIMER (
  input  StartStop,
  input  ResetEnDi,
  input  minInc,
  output [7:0] sevseg0,
  output [7:0] sevseg1,
  output [7:0] sevseg2,
  output [7:0] sevseg3,
  output [7:0] sevseg4,
  output [7:0] sevseg5
);

  wire [7:0] timestampFunc_1_p5, timestampFunc_1_p6, timestampFunc_1_p7;

  // timestampFunc timestampFunc_1: pin names not known; wires that end beside it: StartStop, 1'b1, ResetEnDi, minInc, timestampFunc_1_p5, timestampFunc_1_p6, timestampFunc_1_p7
  chronoView chronoView_1 (
    .cs(timestampFunc_1_p5), .s(timestampFunc_1_p6), .min(timestampFunc_1_p7), .sevseg0(sevseg0),
    .sevseg1(sevseg1), .sevseg2(sevseg2), .sevseg3(sevseg3), .sevseg4(sevseg4), .sevseg5(sevseg5));
endmodule
