// Logisim project c5a.circ as structural Verilog: 18 circuits, main circuit c5a_Tripple_counter
module c5a_tristate (
  input  ctrl,
  output out0,
  output out1,
  output out2
);

  wire clk_out, not_1_out, sysclk_out;

  Clock sysclk (.out(sysclk_out));
  Clock clk (.out(clk_out));
  assign out0 = ctrl ? clk_out : 1'bz;  // Controlled_Buffer controlled_buffer_1
  assign out1 = ctrl ? ~clk_out : 1'bz;  // Controlled_Inverter controlled_inverter_1
  not not_1 (not_1_out, ctrl);
  // Transmission_Gate transmission_1: pin names not known; wires that end beside it: sysclk_out, clk_out, not_1_out, ctrl, out2

  // Notes on the sheet:
  //   Tristate buffer and tristate inverter
  //   Tristate buffer
  //   Tristate inverter
  //   of the tristate gate
  //   Simulation procedure: Ticks enabled, Simulation enabled;
  //   change ctrl; observe on schematic or chronogram
  //   Transmission gate: transistor-level possible realization
endmodule

module c5a_3to8_decoder (
  input  en,
  input  RESET,
  output [7:0] decoder_output,
  output [2:0] out_4
);

  wire clk_out;

  Clock sysclk ();  // open: out
  Counter #(.width(3), .max('h7)) counter_1 (.clr(RESET), .clk(clk_out), .Q(out_4));  // open: load, up, count, D, carry
  Clock clk (.out(clk_out));
  Decoder #(.select(3)) decoder_1 (
    .out0(decoder_output[0]), .out1(decoder_output[1]), .out2(decoder_output[2]), .out3(decoder_output[3]),
    .out4(decoder_output[4]), .out5(decoder_output[5]), .out6(decoder_output[6]), .out7(decoder_output[7]),
    .sel(out_4), .en(en));
  DotMatrix #(.matrixcols(1), .matrixrows(8), .dotshape("circle")) dotmatrix_1 (.col0(decoder_output));

  // Other names for the same wires on the sheet: input_code[2:0] = out_4

  // Notes on the sheet:
  //   3-to-8 Decoder
  //   decoder input
  //   Counter that generates consecutive binary input codes (for simulation purposes)
  //   Simulation procedure: Simulation enabled, ticks enabled; en at logic-1
  //   decoder
endmodule

module c5a_5to32_decoder (
  input  en,
  input  in_2,
  output [31:0] out_3,
  output [4:0] out_4
);

  wire clock_1_out, decoder_1_out0, decoder_1_out1, decoder_1_out2, decoder_1_out3;

  Clock sysclk ();  // open: out
  Counter #(.width(5), .max('h1f)) counter_1 (
    .clr(in_2), .clk(clock_1_out), .Q(out_4));  // open: load, up, count, D, carry
  Clock clock_1 (.out(clock_1_out));
  Decoder #(.select(3)) decoder_1 (
    .out0(decoder_1_out0), .out1(decoder_1_out1), .out2(decoder_1_out2), .out3(decoder_1_out3),
    .sel({1'b0, out_4[4:3]}), .en(en));  // open: out4, out5, out6, out7
  Decoder #(.select(3)) decoder_2 (
    .out0(out_3[0]), .out1(out_3[1]), .out2(out_3[2]), .out3(out_3[3]), .out4(out_3[4]), .out5(out_3[5]),
    .out6(out_3[6]), .out7(out_3[7]), .sel(out_4[2:0]), .en(decoder_1_out0));
  Decoder #(.select(3)) decoder_3 (
    .out0(out_3[8]), .out1(out_3[9]), .out2(out_3[10]), .out3(out_3[11]), .out4(out_3[12]), .out5(out_3[13]),
    .out6(out_3[14]), .out7(out_3[15]), .sel(out_4[2:0]), .en(decoder_1_out1));
  Decoder #(.select(3)) decoder_4 (
    .out0(out_3[16]), .out1(out_3[17]), .out2(out_3[18]), .out3(out_3[19]), .out4(out_3[20]),
    .out5(out_3[21]), .out6(out_3[22]), .out7(out_3[23]), .sel(out_4[2:0]), .en(decoder_1_out2));
  Decoder #(.select(3)) decoder_5 (
    .out0(out_3[24]), .out1(out_3[25]), .out2(out_3[26]), .out3(out_3[27]), .out4(out_3[28]),
    .out5(out_3[29]), .out6(out_3[30]), .out7(out_3[31]), .sel(out_4[2:0]), .en(decoder_1_out3));
  DotMatrix #(.matrixcols(1), .matrixrows(32), .dotshape("circle")) dotmatrix_1 (.col0(out_3));

  // Other names for the same wires on the sheet: input_code[4:0] = out_4

  // Notes on the sheet:
  //   5-to-32 Decoder
  //   decoder input
  //   Simulation procedure: Simulation enabled, ticks enabled; en at logic-1
  //   Counter that generates consecutive binary input codes (for simulation purposes)
  //   decoder L1
  //   decoder L2A
  //   decoder L2B
  //   decoder L2C
  //   decoder L2D
  //   decoder output
endmodule

module c5a_8to3_encoder (
  input  in_1,
  output [2:0] encoder_output,
  output [7:0] out_3
);

  wire clock_1_out;

  Clock sysclk ();  // open: out
  Counter counter_1 (.clr(in_1), .clk(clock_1_out), .Q(out_3));  // open: load, up, count, D, carry
  Clock clock_1 (.out(clock_1_out));
  or or_1 (encoder_output[0], out_3[1], out_3[3], out_3[5], out_3[7]);
  or or_2 (encoder_output[1], out_3[2], out_3[3], out_3[6], out_3[7]);
  or or_3 (encoder_output[2], out_3[4], out_3[5], out_3[6], out_3[7]);
  DotMatrix #(.matrixcols(1), .matrixrows(3), .dotshape("circle")) dotmatrix_1 (.col0(encoder_output));

  // Other names for the same wires on the sheet: input_code[7:0] = out_3

  // Notes on the sheet:
  //   8-to-3 Encoder
  //   Counter that generates consecutive binary input codes (for simulation purposes)
  //   encoder
endmodule

module c5a_priority_encoder (
  input  en,
  input  in_2,
  output [2:0] out_3,
  output [7:0] out_4
);

  wire clock_1_out;

  Clock sysclk ();  // open: out
  Counter counter_1 (.clr(in_2), .clk(clock_1_out), .Q(out_4));  // open: load, up, count, D, carry
  Clock clock_1 (.out(clock_1_out));
  Priority_Encoder priority_encoder_1 (
    .in0(out_4[0]), .in1(out_4[1]), .in2(out_4[2]), .in3(out_4[3]), .in4(out_4[4]), .in5(out_4[5]),
    .in6(out_4[6]), .in7(out_4[7]), .out(out_3), .en_in(en));  // open: gs, en_out
  DotMatrix #(.matrixcols(1), .matrixrows(3), .dotshape("circle")) dotmatrix_1 (.col0(out_3));

  // Other names for the same wires on the sheet: input_code[7:0] = out_4

  // Notes on the sheet:
  //   Priority Encoder
  //   Counter that generates consecutive binary input codes (for simulation purposes)
  //   Simulation procedure: Simulation enabled, ticks enabled; en at logic-1
  //   Simulation procedure: Simulation enabled, ticks enabled; en at logic-1
  //   priority encoder
  //   priority encoder output
endmodule

module c5a_mux (
  input  sel0,
  input  sel1,
  input  sel2,
  output encoder_output
);

  wire clk_d1_out, clk_d2_out, clk_d3_out, clk_d4_out, clk_d5_out, clk_d6_out, clk_d7_out, clk_d8_out;

  Clock clock_1 ();  // open: out
  Clock clk_d1 (.out(clk_d1_out));
  Clock #(.highDuration(2), .lowDuration(2)) clk_d2 (.out(clk_d2_out));
  Clock #(.highDuration(3), .lowDuration(3)) clk_d3 (.out(clk_d3_out));
  Clock #(.highDuration(4), .lowDuration(4)) clk_d4 (.out(clk_d4_out));
  Clock #(.highDuration(5), .lowDuration(5)) clk_d5 (.out(clk_d5_out));
  Clock #(.highDuration(6), .lowDuration(6)) clk_d6 (.out(clk_d6_out));
  Clock #(.highDuration(7), .lowDuration(7)) clk_d7 (.out(clk_d7_out));
  Clock #(.highDuration(8), .lowDuration(87)) clk_d8 (.out(clk_d8_out));
  DotMatrix #(.matrixcols(8), .matrixrows(1), .dotshape("circle")) dotmatrix_1 (
    .col0(clk_d8_out), .col1(clk_d7_out), .col2(clk_d6_out), .col3(clk_d5_out), .col4(clk_d4_out),
    .col5(clk_d3_out), .col6(clk_d2_out), .col7(clk_d1_out));
  Multiplexer #(.select(3), .enable("false")) multiplexer_1 (
    .in0(clk_d1_out), .in1(clk_d2_out), .in2(clk_d3_out), .in3(clk_d4_out), .in4(clk_d5_out),
    .in5(clk_d6_out), .in6(clk_d7_out), .in7(clk_d8_out), .out(encoder_output), .sel({sel2, sel1, sel0}));
  DotMatrix #(.matrixcols(1), .matrixrows(1), .dotshape("circle")) dotmatrix_2 (.col0(encoder_output));

  // Notes on the sheet:
  //   multiplexer
  //   use sel0, sel1, sel2 code to select input
  //   use sel0, sel1, sel2 code to select input
  //   Simulation procedure: Simulation enabled, ticks enabled;
  //   Simulation procedure: Simulation enabled, ticks enabled;
  //   multiplexer
endmodule

module c5a_demux (
  input  in_1,
  input  in_2,
  input  in_3,
  output [7:0] demux_output
);

  wire clock_2_out;

  Clock clock_1 ();  // open: out
  Clock clock_2 (.out(clock_2_out));
  DotMatrix #(.matrixcols(1), .matrixrows(1), .dotshape("circle")) dotmatrix_1 (.col0(clock_2_out));
  Demultiplexer #(.select(3), .enable("false")) demultiplexer_1 (
    .out0(demux_output[0]), .out1(demux_output[1]), .out2(demux_output[2]), .out3(demux_output[3]),
    .out4(demux_output[4]), .out5(demux_output[5]), .out6(demux_output[6]), .out7(demux_output[7]),
    .in(clock_2_out), .sel({in_3, in_2, in_1}));
  DotMatrix #(.matrixcols(1), .matrixrows(8), .dotshape("circle")) dotmatrix_2 (.col0(demux_output));

  // Notes on the sheet:
  //   demultiplexer
  //   use sel0, sel1, sel2 code to select output
  //   use sel0, sel1, sel2 code to select output
  //   Simulation procedure: Simulation enabled, ticks enabled;
  //   Simulation procedure: Simulation enabled, ticks enabled;
  //   demultiplexer
endmodule

module c5a_sub_FA (
  input  x,
  input  y,
  input  cin,
  output s,
  output cout
);

  wire and_1_out, and_2_out, and_3_out, xor_1_out;

  xor xor_1 (xor_1_out, x, y);
  and and_1 (and_1_out, x, cin);
  and and_2 (and_2_out, y, cin);
  and and_3 (and_3_out, y, x);
  or or_1 (cout, and_1_out, and_2_out, and_3_out);
  xor xor_2 (s, xor_1_out, cin);

  // Notes on the sheet:
  //   full-adder
endmodule

module c5a_4bit_ripple_carry_adder (
  input  y3,
  input  y2,
  input  y1,
  input  y0,
  input  x3,
  input  x2,
  input  x1,
  input  x0,
  input  cin,
  output cout,
  output s3,
  output s2,
  output s1,
  output s0
);

  wire FA0_cout, FA1_cout, FA2_cout;

  c5a_sub_FA FA0 (.x(x0), .y(y0), .cin(cin), .s(s0), .cout(FA0_cout));
  c5a_sub_FA FA1 (.x(x1), .y(y1), .cin(FA0_cout), .s(s1), .cout(FA1_cout));
  c5a_sub_FA FA2 (.x(x2), .y(y2), .cin(FA1_cout), .s(s2), .cout(FA2_cout));
  c5a_sub_FA FA3 (.x(x3), .y(y3), .cin(FA2_cout), .s(s3), .cout(cout));

  // Notes on the sheet:
  //   4-bit ripple-carry adder
endmodule

module c5a_sub_FS (
  input  x,
  input  y,
  input  bin,
  output d,
  output bout
);

  wire c5a_sub_fa_1_cout, not_1_out, not_2_out;

  not not_1 (not_1_out, y);
  not not_2 (not_2_out, bin);
  c5a_sub_FA c5a_sub_fa_1 (.x(x), .y(not_1_out), .cin(not_2_out), .s(d), .cout(c5a_sub_fa_1_cout));
  not not_3 (bout, c5a_sub_fa_1_cout);

  // Notes on the sheet:
  //   full-subtractor
  //   d=x-y
endmodule

module c5a_ripple_borrow_subtractor (
  input  y3,
  input  y2,
  input  y1,
  input  y0,
  input  x3,
  input  x2,
  input  x1,
  input  x0,
  input  bin,
  output bout,
  output d3,
  output d2,
  output d1,
  output d0
);

  wire FS0_bout, FS1_bout, FS2_bout;

  c5a_sub_FS FS0 (.x(x0), .y(y0), .bin(bin), .d(d0), .bout(FS0_bout));
  c5a_sub_FS FS1 (.x(x1), .y(y1), .bin(FS0_bout), .d(d1), .bout(FS1_bout));
  c5a_sub_FS FS2 (.x(x2), .y(y2), .bin(FS1_bout), .d(d2), .bout(FS2_bout));
  c5a_sub_FS FS3 (.x(x3), .y(y3), .bin(FS2_bout), .d(d3), .bout(bout));

  // Notes on the sheet:
  //   4-bit ripple-borrow subtractor
endmodule

module c5a_Tripple_counter (
  input  RESET,
  output [3:0] Qn,
  output Q0,
  output Q1,
  output Q2,
  output Q3
);

  wire clk_out, t_ff_1_qn, t_ff_2_qn, t_ff_3_qn;

  Clock sysclk ();  // open: out
  Clock clk (.out(clk_out));
  T_Flip_Flop t_ff_1 (.T(1'b1), .clk(clk_out), .Q(Q0), .Qn(t_ff_1_qn), .reset(RESET));  // open: preset
  T_Flip_Flop t_ff_2 (.T(1'b1), .clk(t_ff_1_qn), .Q(Q1), .Qn(t_ff_2_qn), .reset(RESET));  // open: preset
  T_Flip_Flop t_ff_3 (.T(1'b1), .clk(t_ff_2_qn), .Q(Q2), .Qn(t_ff_3_qn), .reset(RESET));  // open: preset
  T_Flip_Flop t_ff_4 (.T(1'b1), .clk(t_ff_3_qn), .Q(Q3), .reset(RESET));  // open: Qn, preset

  assign Qn = {Q3, Q2, Q1, Q0};

  // Notes on the sheet:
  //   T flip-flop ripple binary counter
  //   Simulation procedure: Ticks enabled, Simulation enabled;
endmodule

module c5a_Tsynchrnous_counter (
  input  en,
  input  RESET,
  output [3:0] out_3,
  output out_4,
  output out_5,
  output out_6,
  output out_7
);

  wire and_1_out, and_2_out, and_3_out, clk_out;

  Clock sysclk ();  // open: out
  Clock clk (.out(clk_out));
  T_Flip_Flop t_ff_1 (.T(en), .clk(clk_out), .Q(out_3[0]), .reset(RESET));  // open: Qn, preset
  T_Flip_Flop t_ff_2 (.T(and_1_out), .clk(clk_out), .Q(out_3[1]), .reset(RESET));  // open: Qn, preset
  and and_1 (and_1_out, out_3[0], en);
  T_Flip_Flop t_ff_3 (.T(and_2_out), .clk(clk_out), .Q(out_3[2]), .reset(RESET));  // open: Qn, preset
  and and_2 (and_2_out, out_3[1], out_3[0], en);
  T_Flip_Flop t_ff_4 (.T(and_3_out), .clk(clk_out), .Q(out_3[3]), .reset(RESET));  // open: Qn, preset
  and and_3 (and_3_out, out_3[2], out_3[1], out_3[0], en);

  assign out_4 = out_3[0];
  assign out_5 = out_3[1];
  assign out_6 = out_3[2];
  assign out_7 = out_3[3];

  // Notes on the sheet:
  //   T flip-flop synchronous binary counter
  //   Simulation procedure: Ticks enabled, Simulation enabled;
  //   switch en from logic-0 to logic-1
endmodule

module c5a_fifo (
  input  ser_in,
  input  RESET,
  output [3:0] out_3,
  output D3_Dout
);

  wire clk_out, d_ff_3_q, d_ff_3_qn, d_ff_5_q, d_ff_5_qn, undriven, undriven_2, undriven_3, undriven_4,
       undriven_5, undriven_6, undriven_7, undriven_8;

  Clock sysclk ();  // open: out
  Clock clk (.out(clk_out));
  D_Flip_Flop d_ff_1 (.D(ser_in), .clk(clk_out), .Q(out_3[0]), .reset(RESET));  // open: Qn, preset
  D_Flip_Flop d_ff_2 (.D(out_3[0]), .clk(clk_out), .Q(out_3[1]), .reset(RESET));  // open: Qn, preset
  D_Flip_Flop d_ff_3 (
    .clk(undriven), .D(undriven_2), .Q(d_ff_3_q), .Qn(d_ff_3_qn), .preset(undriven_5), .reset(undriven_7));
  D_Flip_Flop d_ff_4 (
    .clk(undriven), .D(undriven_2), .Q(d_ff_3_q), .Qn(d_ff_3_qn), .preset(undriven_5), .reset(undriven_7));
  D_Flip_Flop d_ff_5 (
    .clk(undriven_3), .D(undriven_4), .Q(d_ff_5_q), .Qn(d_ff_5_qn), .preset(undriven_6), .reset(undriven_8));
  D_Flip_Flop d_ff_6 (
    .clk(undriven_3), .D(undriven_4), .Q(d_ff_5_q), .Qn(d_ff_5_qn), .preset(undriven_6), .reset(undriven_8));

  assign out_3[3] = D3_Dout;

  // Notes on the sheet:
  //   D flip-flop FIFO, 4-bit
  //   serial data input
  //   Simulation procedure: Ticks enabled, Simulation enabled;
  //   change input at ser_in;
  //   serial data output
endmodule

module c5a_sipo (
  input  ser_in,
  input  clk_en,
  input  RESET,
  output [3:0] out_4,
  output D0,
  output D1,
  output D2,
  output D3
);

  wire and_1_out, clk_out, d_ff_3_q, d_ff_3_qn, d_ff_5_q, d_ff_5_qn, undriven, undriven_2, undriven_3,
       undriven_4, undriven_5, undriven_6, undriven_7, undriven_8;

  Clock sysclk ();  // open: out
  Clock clk (.out(clk_out));
  and and_1 (and_1_out, clk_en, clk_out);
  D_Flip_Flop d_ff_1 (.D(ser_in), .clk(and_1_out), .Q(D0), .reset(RESET));  // open: Qn, preset
  D_Flip_Flop d_ff_2 (.D(D0), .clk(and_1_out), .Q(D1), .reset(RESET));  // open: Qn, preset
  D_Flip_Flop d_ff_3 (
    .clk(undriven), .D(undriven_2), .Q(d_ff_3_q), .Qn(d_ff_3_qn), .preset(undriven_5), .reset(undriven_7));
  D_Flip_Flop d_ff_4 (
    .clk(undriven), .D(undriven_2), .Q(d_ff_3_q), .Qn(d_ff_3_qn), .preset(undriven_5), .reset(undriven_7));
  D_Flip_Flop d_ff_5 (
    .clk(undriven_3), .D(undriven_4), .Q(d_ff_5_q), .Qn(d_ff_5_qn), .preset(undriven_6), .reset(undriven_8));
  D_Flip_Flop d_ff_6 (
    .clk(undriven_3), .D(undriven_4), .Q(d_ff_5_q), .Qn(d_ff_5_qn), .preset(undriven_6), .reset(undriven_8));

  assign out_4 = {D3, D2, D1, D0};

  // Notes on the sheet:
  //   D flip-flop SIPO, 4-bit
  //   serial data input
  //   serial data input
  //   Simulation procedure: Ticks enabled, Simulation enabled;
  //   change input at ser_in;
  //   parallel data output
endmodule

module c5a_4bit_ring_counter (
  input  RESET,
  output [3:0] out_2
);

  wire clk_out;

  Clock sysclk ();  // open: out
  Clock clk (.out(clk_out));
  D_Flip_Flop d_ff_1 (.D(out_2[0]), .clk(clk_out), .Q(out_2[3]), .preset(RESET));  // open: Qn, reset
  D_Flip_Flop d_ff_2 (.D(out_2[3]), .clk(clk_out), .Q(out_2[2]), .reset(RESET));  // open: Qn, preset
  D_Flip_Flop d_ff_3 (.D(out_2[2]), .clk(clk_out), .Q(out_2[1]), .reset(RESET));  // open: Qn, preset
  D_Flip_Flop d_ff_4 (.D(out_2[1]), .clk(clk_out), .Q(out_2[0]), .reset(RESET));  // open: Qn, preset

  // Notes on the sheet:
  //   synchronous binary counter
  //   Simulation procedure: Ticks enabled, Simulation enabled;
  //   reset; observe on schematic or chronogram
endmodule

module c5a_Johnson_counter (
  input  RESET,
  output [3:0] out_2
);

  wire clk_out, not_1_out;

  Clock sysclk ();  // open: out
  Clock clk (.out(clk_out));
  D_Flip_Flop d_ff_1 (.D(not_1_out), .clk(clk_out), .Q(out_2[3]), .preset(RESET));  // open: Qn, reset
  D_Flip_Flop d_ff_2 (.D(out_2[3]), .clk(clk_out), .Q(out_2[2]), .reset(RESET));  // open: Qn, preset
  D_Flip_Flop d_ff_3 (.D(out_2[2]), .clk(clk_out), .Q(out_2[1]), .reset(RESET));  // open: Qn, preset
  D_Flip_Flop d_ff_4 (.D(out_2[1]), .clk(clk_out), .Q(out_2[0]), .reset(RESET));  // open: Qn, preset
  not not_1 (not_1_out, out_2[0]);

  // Notes on the sheet:
  //   Johnson synchronous binary counter
  //   Simulation procedure: Ticks enabled, Simulation enabled;
  //   reset; observe on schematic or chronogram
endmodule

module c5a_lfsr (
  input  RESET,
  output [5:0] out_2
);

  wire clk_out, xor_1_out;

  Clock sysclk ();  // open: out
  Clock clk (.out(clk_out));
  D_Flip_Flop d_ff_1 (.D(xor_1_out), .clk(clk_out), .Q(out_2[5]), .preset(RESET));  // open: Qn, reset
  xor xor_1 (xor_1_out, out_2[0], out_2[1]);
  D_Flip_Flop d_ff_2 (.D(out_2[5]), .clk(clk_out), .Q(out_2[4]), .reset(RESET));  // open: Qn, preset
  D_Flip_Flop d_ff_3 (.D(out_2[4]), .clk(clk_out), .Q(out_2[3]), .reset(RESET));  // open: Qn, preset
  D_Flip_Flop d_ff_4 (.D(out_2[3]), .clk(clk_out), .Q(out_2[2]), .reset(RESET));  // open: Qn, preset
  D_Flip_Flop d_ff_5 (.D(out_2[2]), .clk(clk_out), .Q(out_2[1]), .reset(RESET));  // open: Qn, preset
  D_Flip_Flop d_ff_6 (.D(out_2[1]), .clk(clk_out), .Q(out_2[0]), .reset(RESET));  // open: Qn, preset

  // Notes on the sheet:
  //   linear feedback shift register
  //   Simulation procedure: Ticks enabled, Simulation enabled;
  //   reset; observe on schematic or chronogram
  //   x6 = x1 XOR x0
  //   x5
  //   x6
  //   x4
  //   x3
  //   x2
  //   x1
  //   x0
endmodule
