// Logisim project counter_TP4.circ as structural Verilog: 11 circuits, main circuit main
module main (
);

  wire and_1_out, and_2_out, and_3_out, borrow_carry1_cb, borrow_carry_0_cb, But_out,
       Button_memory_fsm_button_pressed, Change_direction, clock_1_out, Comp1_equal, Comp2_equal,
       Comp3_equal, Comp4_equal, Decoder0_a, Decoder0_b, Decoder0_c, Decoder0_d, Decoder0_e, Decoder0_f,
       Decoder0_g, Decoder1_a, Decoder1_b, Decoder1_c, Decoder1_d, Decoder1_e, Decoder1_f, Decoder1_g,
       Decoder2_a, Decoder2_b, Decoder2_c, Decoder2_d, Decoder2_e, Decoder2_f, Decoder2_g,
       Direction_fsm_count_direction, not_1_out, or_1_out, reset_out;
  wire [1:0] Const1_state1, Const2_state1, Const3_state2, Const4_state0, Counter_LSB_count_value,
       Counter_Middle_count_value, Counter_MSB_count_value;

  Button But (.out(But_out));
  Clock clock_1 (.out(clock_1_out));
  Button reset (.out(reset_out));
  and and_1 (and_1_out, borrow_carry1_cb, borrow_carry_0_cb);
  borrow_carry_logic borrow_carry_0 (
    .Q1(Counter_LSB_count_value[1]), .Q0(Counter_LSB_count_value[0]), .D(Direction_fsm_count_direction),
    .cb(borrow_carry_0_cb));
  borrow_carry_logic borrow_carry1 (
    .Q1(Counter_Middle_count_value[1]), .Q0(Counter_Middle_count_value[0]),
    .D(Direction_fsm_count_direction), .cb(borrow_carry1_cb));
  Button_memory Button_memory_fsm (
    .Button(But_out), .Change_direction(Change_direction), .Clock(clock_1_out), .Reset(reset_out),
    .Button_pressed(Button_memory_fsm_button_pressed));
  fsm_counter Counter_LSB (
    .Enable(1'b1), .Direction(Direction_fsm_count_direction), .Clock(clock_1_out), .Reset(reset_out),
    .Count_value(Counter_LSB_count_value));
  fsm_counter Counter_Middle (
    .Enable(borrow_carry_0_cb), .Direction(Direction_fsm_count_direction), .Clock(clock_1_out),
    .Reset(reset_out), .Count_value(Counter_Middle_count_value));
  fsm_counter Counter_MSB (
    .Enable(and_1_out), .Direction(Direction_fsm_count_direction), .Clock(clock_1_out), .Reset(reset_out),
    .Count_value(Counter_MSB_count_value));
  state_0_contant Const4 (.state0(Const4_state0));
  state_2_constant Const3 (.state2(Const3_state2));
  state_1_constant Const2 (.state1(Const2_state1));
  state_1_constant Const1 (.state1(Const1_state1));
  _7_Segment_Display Disp2 (
    .g(Decoder2_g), .f(Decoder2_f), .a(Decoder2_a), .b(Decoder2_b), .e(Decoder2_e), .d(Decoder2_d),
    .c(Decoder2_c));  // open: dp
  comparator Comp4 (.A(Counter_LSB_count_value), .B(Const4_state0), .Equal(Comp4_equal));
  comparator Comp3 (.A(Counter_LSB_count_value), .B(Const3_state2), .Equal(Comp3_equal));
  comparator Comp2 (.A(Counter_Middle_count_value), .B(Const2_state1), .Equal(Comp2_equal));
  comparator Comp1 (.A(Counter_MSB_count_value), .B(Const1_state1), .Equal(Comp1_equal));
  seven_segment_decoder Decoder2 (
    .Q1(Counter_MSB_count_value[1]), .Q0(Counter_MSB_count_value[0]), .a(Decoder2_a), .b(Decoder2_b),
    .c(Decoder2_c), .d(Decoder2_d), .e(Decoder2_e), .f(Decoder2_f), .g(Decoder2_g));
  and and_2 (and_2_out, Comp4_equal, Direction_fsm_count_direction);
  and and_3 (and_3_out, Comp3_equal, not_1_out);
  not not_1 (not_1_out, Direction_fsm_count_direction);
  _7_Segment_Display Disp1 (
    .g(Decoder1_g), .f(Decoder1_f), .a(Decoder1_a), .b(Decoder1_b), .e(Decoder1_e), .d(Decoder1_d),
    .c(Decoder1_c));  // open: dp
  or or_1 (or_1_out, and_2_out, and_3_out);
  seven_segment_decoder Decoder1 (
    .Q1(Counter_Middle_count_value[1]), .Q0(Counter_Middle_count_value[0]), .a(Decoder1_a), .b(Decoder1_b),
    .c(Decoder1_c), .d(Decoder1_d), .e(Decoder1_e), .f(Decoder1_f), .g(Decoder1_g));
  and and_4 (Change_direction, Button_memory_fsm_button_pressed, or_1_out, Comp2_equal, Comp1_equal);
  _7_Segment_Display Disp0 (
    .g(Decoder0_g), .f(Decoder0_f), .a(Decoder0_a), .b(Decoder0_b), .e(Decoder0_e), .d(Decoder0_d),
    .c(Decoder0_c));  // open: dp
  seven_segment_decoder Decoder0 (
    .Q1(Counter_LSB_count_value[1]), .Q0(Counter_LSB_count_value[0]), .a(Decoder0_a), .b(Decoder0_b),
    .c(Decoder0_c), .d(Decoder0_d), .e(Decoder0_e), .f(Decoder0_f), .g(Decoder0_g));
  direction Direction_fsm (
    .Reset(reset_out), .Change_direction(Change_direction), .Clock(clock_1_out),
    .Count_direction(Direction_fsm_count_direction));
endmodule

module update_logic_counter (
  input  e,
  input  d,
  input  Q1,
  input  Q0,
  output D1,
  output D0
);

  wire and_1_out, and_2_out, and_3_out, and_4_out, and_5_out, and_6_out, and_7_out, not_1_out, not_2_out,
       not_3_out, not_4_out, not_5_out, not_6_out, not_7_out, not_8_out;

  not not_1 (not_1_out, e);
  and and_1 (and_1_out, not_1_out, Q1);
  and and_2 (and_2_out, d, Q0);
  not not_2 (not_2_out, d);
  and and_3 (and_3_out, e, not_2_out, not_3_out);
  not not_3 (not_3_out, Q0);
  and and_4 (and_4_out, e, not_4_out);
  not not_4 (not_4_out, Q1);
  not not_5 (not_5_out, e);
  not not_6 (not_6_out, d);
  not not_7 (not_7_out, Q0);
  not not_8 (not_8_out, Q1);
  or or_1 (D1, and_1_out, and_2_out, and_3_out, and_4_out);
  and and_5 (and_5_out, not_5_out, Q0);
  and and_6 (and_6_out, e, not_6_out, Q1, not_7_out);
  or or_2 (D0, and_5_out, and_6_out, and_7_out);
  and and_7 (and_7_out, e, d, not_8_out);
endmodule

module fsm_counter (
  input  Enable,
  input  Direction,
  input  Clock,
  input  Reset,
  output [1:0] Count_value
);

  wire Update_d0, Update_d1;

  update_logic_counter Update (
    .e(Enable), .d(Direction), .D1(Update_d1), .Q1(Count_value[1]), .Q0(Count_value[0]), .D0(Update_d0));
  D_Flip_Flop d_ff_1 (.D(Update_d1), .clk(Clock), .Q(Count_value[1]), .preset(Reset));  // open: Qn, reset
  D_Flip_Flop d_ff_2 (.D(Update_d0), .clk(Clock), .Q(Count_value[0]), .preset(Reset));  // open: Qn, reset
endmodule

module seven_segment_decoder (
  input  Q1,
  input  Q0,
  output a,
  output b,
  output c,
  output d,
  output e,
  output f,
  output g
);

  wire not_1_out, not_2_out, not_3_out;

  not not_1 (not_1_out, Q1);
  not not_2 (not_2_out, Q1);
  not not_3 (not_3_out, Q1);
  not not_4 (g, Q1);
  or or_1 (a, not_1_out, Q0);
  or or_2 (d, not_2_out, Q0);
  or or_3 (e, not_3_out, Q0);

  assign b = 1'b1;
  assign c = Q1;
  assign f = Q0;
endmodule

module borrow_carry_logic (
  input  Q1,
  input  Q0,
  input  D,
  output cb
);

  wire and_1_out, and_2_out, not_1_out, not_2_out, not_3_out;

  not not_1 (not_1_out, Q1);
  not not_2 (not_2_out, Q0);
  not not_3 (not_3_out, D);
  and and_1 (and_1_out, not_1_out, not_2_out, D);
  and and_2 (and_2_out, Q1, Q0, not_3_out);
  or or_1 (cb, and_1_out, and_2_out);
endmodule

module Button_memory (
  input  Button,
  input  Change_direction,
  input  Clock,
  input  Reset,
  output Button_pressed
);

  wire and_1_out, not_1_out;

  not not_1 (not_1_out, Change_direction);
  D_Flip_Flop d_ff_1 (.D(and_1_out), .clk(Clock), .Q(Button_pressed), .preset(Button), .reset(Reset));  // open: Qn
  and and_1 (and_1_out, Button_pressed, not_1_out);
endmodule

module state_0_contant (
  output [1:0] state0
);


  assign state0 = 2'b11;
endmodule

module state_1_constant (
  output [1:0] state1
);


  assign state1 = 2'b10;
endmodule

module state_2_constant (
  output [1:0] state2
);


  assign state2 = 2'b00;
endmodule

module comparator (
  input  [1:0] A,
  input  [1:0] B,
  output Equal
);

  wire xnor_1_out, xnor_2_out;

  xnor xnor_1 (xnor_1_out, A[1], B[1]);
  xnor xnor_2 (xnor_2_out, A[0], B[0]);
  and and_1 (Equal, xnor_1_out, xnor_2_out);
endmodule

module direction (
  input  Reset,
  input  Change_direction,
  input  Clock,
  output Count_direction
);

  wire xor_1_out;

  xor xor_1 (xor_1_out, Count_direction, Change_direction);
  D_Flip_Flop d_ff_1 (.D(xor_1_out), .clk(Clock), .Q(Count_direction), .preset(Reset));  // open: Qn, reset
endmodule
