// Logisim project exercise_2-4-5.circ as structural Verilog: 8 circuits, main circuit exercise_2
module exercise_2 (
  input  [3:0] A,
  input  [3:0] B,
  output Overflow,
  output [3:0] P
);

  wire Full_adder_1_rn, Full_adder_2_rn, Half_adder_1_r0;

  Prob_1 Half_adder_1 (.r0(Half_adder_1_r0), .P0(P[0]), .A0(A[0]), .B0(B[0]));
  Prob_2_3_4 Full_adder_3 (.An(A[3]), .Pn(P[3]), .Bn(B[3]), .rn_1(Full_adder_2_rn), .rn(Overflow));
  Prob_2_3_4 Full_adder_2 (.An(A[2]), .Pn(P[2]), .Bn(B[2]), .rn_1(Full_adder_1_rn), .rn(Full_adder_2_rn));
  Prob_2_3_4 Full_adder_1 (.An(A[1]), .Pn(P[1]), .Bn(B[1]), .rn_1(Half_adder_1_r0), .rn(Full_adder_1_rn));
endmodule

module Prob_1 (
  input  A0,
  input  B0,
  output P0,
  output r0
);

  and and_1 (r0, A0, B0);
  xor xor_1 (P0, A0, B0);
endmodule

module Prob_2_3_4 (
  input  An,
  input  Bn,
  input  rn_1,
  output Pn,
  output rn
);

  wire and_1_out, and_2_out, and_3_out, xor_1_out;

  xor xor_1 (xor_1_out, An, Bn);
  and and_1 (and_1_out, An, Bn);
  and and_2 (and_2_out, An, rn_1);
  and and_3 (and_3_out, Bn, rn_1);
  xor xor_2 (Pn, xor_1_out, rn_1);
  or or_1 (rn, and_1_out, and_2_out, and_3_out);
endmodule

module exercise_4 (
  input  [3:0] A,
  input  [3:0] B,
  output Underflow,
  output [3:0] M
);

  wire Full_sub_2_en, Full_subtractor1_en, Half_subtractor_1_e0;

  Prob_5 Half_subtractor_1 (.B0(B[0]), .e0(Half_subtractor_1_e0), .A0(A[0]), .M0(M[0]));
  Prob_6_7_8 Full_sub_3 (.en(Underflow), .en_1(Full_sub_2_en), .Mn(M[3]), .An(A[3]), .Bn(B[3]));
  Prob_6_7_8 Full_sub_2 (.en(Full_sub_2_en), .en_1(Full_subtractor1_en), .Mn(M[2]), .An(A[2]), .Bn(B[2]));
  Prob_6_7_8 Full_subtractor1 (.en(Full_subtractor1_en), .en_1(Half_subtractor_1_e0), .Mn(M[1]), .An(A[1]), .Bn(B[1]));
endmodule

module Prob_5 (
  input  A0,
  input  B0,
  output M0,
  output e0
);

  wire not_1_out;

  not not_1 (not_1_out, A0);
  and and_1 (e0, not_1_out, B0);
  xor xor_1 (M0, A0, B0);
endmodule

module Prob_6_7_8 (
  input  An,
  input  Bn,
  input  en_1,
  output Mn,
  output en
);

  wire and_1_out, and_2_out, and_3_out, not_1_out, xor_1_out;

  not not_1 (not_1_out, An);
  xor xor_1 (xor_1_out, An, Bn);
  and and_1 (and_1_out, not_1_out, Bn);
  and and_2 (and_2_out, not_1_out, en_1);
  and and_3 (and_3_out, Bn, en_1);
  xor xor_2 (Mn, xor_1_out, en_1);
  or or_1 (en, and_1_out, and_2_out, and_3_out);
endmodule

module exercise_5 (
);

  wire and_1_out, and_2_out, and_3_out, and_4_out, and_5_out, and_6_out, But_out, or_1_out, or_2_out,
       or_3_out, POR_out, sr_latch_1_q, sr_latch_2_q, sr_latch_3_q;

  Button But (.out(But_out));
  Button POR (.out(POR_out));
  and and_1 (and_1_out, sr_latch_1_q, sr_latch_2_q, sr_latch_3_q, ~But_out);  // AND_Gate
  and and_2 (and_2_out, ~sr_latch_1_q, ~sr_latch_2_q, ~sr_latch_3_q, But_out);  // AND_Gate
  and and_3 (and_3_out, ~sr_latch_1_q, sr_latch_2_q, sr_latch_3_q, But_out);  // AND_Gate
  and and_4 (and_4_out, sr_latch_1_q, ~sr_latch_2_q, ~sr_latch_3_q, ~But_out);  // AND_Gate
  and and_5 (and_5_out, ~sr_latch_1_q, ~sr_latch_2_q, sr_latch_3_q, ~But_out);  // AND_Gate
  and and_6 (and_6_out, sr_latch_1_q, sr_latch_2_q, ~sr_latch_3_q, But_out);  // AND_Gate
  or or_1 (or_1_out, and_1_out, POR_out);
  or or_2 (or_2_out, and_3_out, POR_out);
  or or_3 (or_3_out, and_5_out, POR_out);
  sr_latch sr_latch_1 (.Reset(or_1_out), .Set(and_2_out), .Q(sr_latch_1_q));
  sr_latch sr_latch_2 (.Reset(or_2_out), .Set(and_4_out), .Q(sr_latch_2_q));
  sr_latch sr_latch_3 (.Reset(or_3_out), .Set(and_6_out), .Q(sr_latch_3_q));
  LED Lamp1 (.in(sr_latch_1_q));
  LED Lamp2 (.in(sr_latch_2_q));
  LED Lamp3 (.in(sr_latch_3_q));
endmodule

module sr_latch (
  input  Reset,
  input  Set,
  output Q
);

  wire nor_2_out;

  nor nor_1 (Q, Reset, nor_2_out);
  nor nor_2 (nor_2_out, Q, Set);
endmodule
