// Logisim project ALL.circ as structural Verilog: 8 circuits, main circuit main
module main (
);

  wire A_1_output_1, B_1_output_1, C_1_output_1, D_1_output_1, DipSwitch_1_sw1, DipSwitch_1_sw2,
       DipSwitch_1_sw3, DipSwitch_1_sw4, E_1_output_1, F_1_output_1, G_1_output_1;

  DipSwitch #(.number(10)) DipSwitch_1 (
    .sw1(DipSwitch_1_sw1), .sw2(DipSwitch_1_sw2), .sw3(DipSwitch_1_sw3), .sw4(DipSwitch_1_sw4));  // open: sw5, sw6, sw7, sw8, sw9, sw10
  A A_1 (.W(DipSwitch_1_sw1), .X(DipSwitch_1_sw2), .Y(DipSwitch_1_sw3), .Z(DipSwitch_1_sw4), .Output_1(A_1_output_1));
  B B_1 (.W(DipSwitch_1_sw1), .X(DipSwitch_1_sw2), .Y(DipSwitch_1_sw3), .Z(DipSwitch_1_sw4), .Output_1(B_1_output_1));
  C C_1 (.W(DipSwitch_1_sw1), .X(DipSwitch_1_sw2), .Y(DipSwitch_1_sw3), .Z(DipSwitch_1_sw4), .Output_1(C_1_output_1));
  D D_1 (.W(DipSwitch_1_sw1), .X(DipSwitch_1_sw2), .Y(DipSwitch_1_sw3), .Z(DipSwitch_1_sw4), .Output_1(D_1_output_1));
  E E_1 (.W(DipSwitch_1_sw1), .X(DipSwitch_1_sw2), .Y(DipSwitch_1_sw3), .Z(DipSwitch_1_sw4), .Output_1(E_1_output_1));
  F F_1 (.W(DipSwitch_1_sw1), .X(DipSwitch_1_sw2), .Y(DipSwitch_1_sw3), .Z(DipSwitch_1_sw4), .Output_1(F_1_output_1));
  G G_1 (.W(DipSwitch_1_sw1), .X(DipSwitch_1_sw2), .Y(DipSwitch_1_sw3), .Z(DipSwitch_1_sw4), .Output_1(G_1_output_1));
  _7_Segment_Display L_7_Segment_Display_1 (
    .g(G_1_output_1), .f(F_1_output_1), .a(A_1_output_1), .b(B_1_output_1), .e(E_1_output_1),
    .d(D_1_output_1), .c(C_1_output_1));  // open: dp
endmodule

module A (
  input  W,
  input  X,
  input  Y,
  input  Z,
  output Output_1
);

  wire and_1_out, and_2_out, and_3_out, and_4_out, and_5_out, and_6_out, not_1_out, not_2_out, not_3_out,
       not_4_out, or_1_out, or_2_out, or_3_out;

  and and_1 (and_1_out, X, Y);
  or or_1 (or_1_out, X, Y);
  and and_2 (and_2_out, X, Z);
  or or_2 (or_2_out, X, Z);
  not not_1 (not_1_out, and_1_out);
  not not_2 (not_2_out, and_2_out);
  and and_3 (and_3_out, not_1_out, or_1_out);
  and and_4 (and_4_out, not_2_out, or_2_out);
  not not_3 (not_3_out, W);
  and and_5 (and_5_out, W, Z, and_3_out);
  not not_4 (not_4_out, Y);
  and and_6 (and_6_out, not_3_out, not_4_out, and_4_out);
  or or_3 (or_3_out, and_5_out, and_6_out);
  not not_5 (Output_1, or_3_out);
endmodule

module B (
  input  W,
  input  X,
  input  Y,
  input  Z,
  output Output_1
);

  wire and_1_out, and_2_out, and_3_out, and_4_out, not_1_out, not_2_out, not_3_out, not_4_out, not_5_out,
       xor_1_out;

  not not_1 (not_1_out, W);
  not not_2 (not_2_out, Y);
  not not_3 (not_3_out, Z);
  xor xor_1 (xor_1_out, W, Y);
  and and_1 (and_1_out, W, Z);
  and and_2 (and_2_out, X, not_1_out, not_2_out, not_3_out);
  and and_3 (and_3_out, xor_1_out, Z);
  not not_4 (not_4_out, X);
  not not_5 (not_5_out, and_1_out);
  and and_4 (and_4_out, not_4_out, not_5_out);
  or or_1 (Output_1, and_3_out, and_2_out, and_4_out);
endmodule

module C (
  input  W,
  input  X,
  input  Y,
  input  Z,
  output Output_1
);

  wire and_1_out, and_2_out, not_1_out, not_2_out, not_3_out, or_1_out, or_2_out, xor_1_out;

  xor xor_1 (xor_1_out, W, X);
  not not_1 (not_1_out, Y);
  not not_2 (not_2_out, X);
  not not_3 (not_3_out, W);
  or or_1 (or_1_out, not_2_out, not_3_out, Z);
  or or_2 (or_2_out, not_3_out, not_2_out);
  and and_1 (and_1_out, not_1_out, or_1_out);
  and and_2 (and_2_out, or_2_out, Z);
  or or_3 (Output_1, xor_1_out, and_1_out, and_2_out);
endmodule

module D (
  input  W,
  input  X,
  input  Y,
  input  Z,
  output Output_1
);

  wire and_1_out, and_2_out, and_3_out, and_4_out, and_5_out, not_1_out, not_2_out, not_3_out, not_4_out,
       or_1_out, xor_1_out;

  not not_1 (not_1_out, Y);
  not not_2 (not_2_out, W);
  not not_3 (not_3_out, Z);
  and and_1 (and_1_out, W, not_1_out);
  and and_2 (and_2_out, not_2_out, not_3_out);
  and and_3 (and_3_out, Y, Z);
  xor xor_1 (xor_1_out, Y, Z);
  or or_1 (or_1_out, and_2_out, and_3_out);
  and and_4 (and_4_out, X, xor_1_out);
  and and_5 (and_5_out, or_1_out, not_4_out);
  not not_4 (not_4_out, X);
  or or_2 (Output_1, and_1_out, and_5_out, and_4_out);
endmodule

module E (
  input  W,
  input  X,
  input  Y,
  input  Z,
  output Output_1
);

  wire and_1_out, and_2_out, not_1_out, not_2_out, or_1_out, or_2_out;

  not not_1 (not_1_out, X);
  or or_1 (or_1_out, X, Y);
  or or_2 (or_2_out, not_1_out, Y);
  not not_2 (not_2_out, Z);
  and and_1 (and_1_out, W, or_1_out);
  and and_2 (and_2_out, or_2_out, not_2_out);
  or or_3 (Output_1, and_1_out, and_2_out);
endmodule

module F (
  input  W,
  input  X,
  input  Y,
  input  Z,
  output Output_1
);

  wire and_1_out, and_2_out, and_3_out, and_4_out, not_1_out, not_2_out, not_3_out, not_4_out, or_1_out,
       or_2_out;

  or or_1 (or_1_out, Y, not_1_out);
  not not_1 (not_1_out, X);
  not not_2 (not_2_out, Y);
  not not_3 (not_3_out, W);
  and and_1 (and_1_out, or_1_out, W);
  and and_2 (and_2_out, Z, not_2_out, not_3_out);
  or or_2 (or_2_out, and_2_out, not_4_out);
  not not_4 (not_4_out, Z);
  and and_3 (and_3_out, ~X, ~Y, ~Z);  // AND_Gate
  and and_4 (and_4_out, or_2_out, X);
  or or_3 (Output_1, and_4_out, and_3_out, and_1_out);
endmodule

module G (
  input  W,
  input  X,
  input  Y,
  input  Z,
  output Output_1
);

  wire not_1_out, or_1_out, or_2_out, xnor_1_out, xnor_2_out, xor_1_out;

  or or_1 (or_1_out, W, Y, X);
  xnor xnor_1 (xnor_1_out, W, Z);
  xor xor_1 (xor_1_out, Y, Z);
  xnor xnor_2 (xnor_2_out, Y, W);
  not not_1 (not_1_out, X);
  or or_2 (or_2_out, not_1_out, xnor_1_out, xnor_2_out, xor_1_out);
  and and_1 (Output_1, or_1_out, or_2_out);
endmodule
