// Logisim project a.circ as structural Verilog: 1 circuit, main circuit main
module main (
  input  W,
  input  X,
  input  Y,
  input  Z,
  output a
);

  wire and_1_out, and_2_out, and_3_out, and_4_out, and_5_out, and_6_out, not_1_out, not_2_out, not_3_out,
       not_4_out, or_1_out, or_2_out, or_3_out;

  not not_1 (not_1_out, and_1_out);
  and and_1 (and_1_out, X, Y);
  or or_1 (or_1_out, X, Y);
  and and_2 (and_2_out, X, Z);
  not not_2 (not_2_out, and_2_out);
  or or_2 (or_2_out, X, Z);
  and and_3 (and_3_out, not_1_out, or_1_out);
  and and_4 (and_4_out, not_2_out, or_2_out);
  not not_3 (not_3_out, W);
  and and_5 (and_5_out, W, Z, and_3_out);
  not not_4 (not_4_out, Y);
  and and_6 (and_6_out, not_3_out, not_4_out, and_4_out);
  or or_3 (or_3_out, and_5_out, and_6_out);
  not not_5 (a, or_3_out);
endmodule
