// Logisim project soustracteurr.circ as structural Verilog: 2 circuits, main circuit soustracteur4bit
module soustracteur4bit (
  input  A0,
  input  B0,
  input  A1,
  input  B1,
  input  A2,
  input  B2,
  input  B3,
  input  A3,
  output P0,
  output P1,
  output P2,
  output P3,
  output U
);

  wire soustracteur_1_r1, soustracteur_2_r1, soustracteur_3_r1;

  soustracteur soustracteur_1 (.r(1'b0), .a(A0), .b(B0), .P(P0), .R1(soustracteur_1_r1));
  soustracteur soustracteur_2 (.r(soustracteur_1_r1), .a(A1), .b(B1), .P(P1), .R1(soustracteur_2_r1));
  soustracteur soustracteur_3 (.r(soustracteur_2_r1), .a(A2), .b(B2), .P(P2), .R1(soustracteur_3_r1));
  soustracteur soustracteur_4 (.r(soustracteur_3_r1), .a(B3), .b(A3), .P(P3), .R1(U));
endmodule

module soustracteur (
  input  r,
  input  a,
  input  b,
  output P,
  output R1
);

  wire and_2_out, and_3_out, and_4_out, not_1_out, not_2_out, not_3_out, not_4_out;

  not not_1 (not_1_out, a);
  not not_2 (not_2_out, r);
  not not_3 (not_3_out, b);
  not not_4 (not_4_out, b);
  and and_1 (P, not_1_out, b, not_2_out);
  and and_2 (and_2_out, not_3_out, r);
  or or_1 (R1, and_2_out, and_3_out, and_4_out);
  and and_3 (and_3_out, a, not_4_out);
  and and_4 (and_4_out, a, r);
endmodule
