// Logisim project tp1_2_Ed.circ as structural Verilog: 2 circuits, main circuit main
module main (
);

  wire a_1_output_1, DipSwitch_1_sw7, DipSwitch_1_sw8, DipSwitch_1_sw9, DipSwitch_1_sw10;

  DipSwitch #(.number(10)) DipSwitch_1 (
    .sw7(DipSwitch_1_sw7), .sw8(DipSwitch_1_sw8), .sw9(DipSwitch_1_sw9), .sw10(DipSwitch_1_sw10));  // open: sw1, sw2, sw3, sw4, sw5, sw6
  a a_1 (
    .Input_1(DipSwitch_1_sw10), .Input_2(DipSwitch_1_sw9), .Input_3(DipSwitch_1_sw8),
    .Input_4(DipSwitch_1_sw7), .Output_1(a_1_output_1));
  _7_Segment_Display L_7_Segment_Display_1 (.a(a_1_output_1));  // open: g, f, b, e, d, c, dp
endmodule

module a (
  input  Input_1,
  input  Input_2,
  input  Input_3,
  input  Input_4,
  output Output_1
);

  wire and_1_out, and_2_out, and_3_out, and_4_out, and_5_out, and_6_out, and_7_out, and_8_out, not_1_out,
       not_2_out, not_3_out, not_4_out, or_1_out, or_2_out, or_3_out;

  not not_1 (not_1_out, Input_1);
  not not_2 (not_2_out, Input_2);
  not not_3 (not_3_out, Input_3);
  not not_4 (not_4_out, Input_4);
  and and_1 (and_1_out, Input_4, not_2_out);
  and and_2 (and_2_out, not_1_out, not_3_out);
  and and_3 (and_3_out, Input_2, not_4_out);
  and and_4 (and_4_out, not_2_out, Input_3);
  and and_5 (and_5_out, Input_2, not_3_out);
  and and_6 (and_6_out, Input_1, Input_4);
  or or_1 (or_1_out, and_1_out, and_3_out);
  or or_2 (or_2_out, and_4_out, and_5_out);
  and and_7 (and_7_out, or_2_out, and_6_out);
  and and_8 (and_8_out, or_1_out, and_2_out);
  or or_3 (or_3_out, and_8_out, and_7_out);
  not not_5 (Output_1, or_3_out);
endmodule
