// Logisim project tp2_3_Ed.circ as structural Verilog: 10 circuits, main circuit main
module main (
);

  wire a_1_a, b_1_b, c_1_c, d_1_d, dipswitch_1_sw7, dipswitch_1_sw8, dipswitch_1_sw9, dipswitch_1_sw10,
       e_1_e, f_1_f, g_1_g;

  DipSwitch #(.number(10)) dipswitch_1 (
    .sw7(dipswitch_1_sw7), .sw8(dipswitch_1_sw8), .sw9(dipswitch_1_sw9), .sw10(dipswitch_1_sw10));  // open: sw1, sw2, sw3, sw4, sw5, sw6
  a a_1 (.W(dipswitch_1_sw10), .X(dipswitch_1_sw9), .Y(dipswitch_1_sw8), .Z(dipswitch_1_sw7), .a(a_1_a));
  b b_1 (.W(dipswitch_1_sw10), .X(dipswitch_1_sw9), .Y(dipswitch_1_sw8), .Z(dipswitch_1_sw7), .b(b_1_b));
  c c_1 (.W(dipswitch_1_sw10), .X(dipswitch_1_sw9), .Y(dipswitch_1_sw8), .Z(dipswitch_1_sw7), .c(c_1_c));
  d d_1 (.W(dipswitch_1_sw10), .X(dipswitch_1_sw9), .Y(dipswitch_1_sw8), .Z(dipswitch_1_sw7), .d(d_1_d));
  e e_1 (.W(dipswitch_1_sw10), .X(dipswitch_1_sw9), .Y(dipswitch_1_sw8), .Z(dipswitch_1_sw7), .e(e_1_e));
  f f_1 (.W(dipswitch_1_sw10), .X(dipswitch_1_sw9), .Y(dipswitch_1_sw8), .Z(dipswitch_1_sw7), .f(f_1_f));
  g g_1 (.W(dipswitch_1_sw10), .X(dipswitch_1_sw9), .Y(dipswitch_1_sw8), .Z(dipswitch_1_sw7), .g(g_1_g));
  _7_Segment_Display u_7_segment_display_1 (
    .g(g_1_g), .f(f_1_f), .a(a_1_a), .b(b_1_b), .e(e_1_e), .d(d_1_d), .c(c_1_c));  // open: dp
endmodule

module a (
  input  W,
  input  X,
  input  Y,
  input  Z,
  output a
);

  wire and_1_out, and_2_out, and_3_out, and_4_out, and_5_out, and_6_out, and_7_out, and_8_out, not_1_out,
       not_2_out, not_3_out, not_4_out, not_5_out, not_6_out, not_7_out, or_1_out, or_2_out, or_3_out,
       or_4_out;

  not not_1 (not_1_out, X);
  not not_2 (not_2_out, X);
  not not_3 (not_3_out, Z);
  not not_4 (not_4_out, W);
  not not_5 (not_5_out, W);
  and and_1 (and_1_out, W, not_1_out);
  not not_6 (not_6_out, Y);
  and and_2 (and_2_out, not_2_out, not_3_out);
  and and_3 (and_3_out, not_4_out, Y);
  and and_4 (and_4_out, not_5_out, X);
  and and_5 (and_5_out, X, Y);
  and and_6 (and_6_out, and_1_out, not_6_out);
  not not_7 (not_7_out, Z);
  or or_1 (or_1_out, and_2_out, and_3_out);
  or or_2 (or_2_out, or_1_out, and_7_out);
  and and_7 (and_7_out, and_4_out, Z);
  or or_3 (or_3_out, and_5_out, and_6_out);
  or or_4 (or_4_out, or_3_out, and_8_out);
  and and_8 (and_8_out, W, not_7_out);
  or or_5 (a, or_2_out, or_4_out);
endmodule

module b (
  input  W,
  input  X,
  input  Y,
  input  Z,
  output b
);

  wire and_1_out, and_2_out, and_3_out, and_4_out, and_5_out, and_6_out, and_7_out, and_8_out, not_1_out,
       not_2_out, not_3_out, not_4_out, not_5_out, not_6_out, not_7_out, not_8_out, not_9_out, or_1_out,
       or_2_out, or_3_out;

  not not_1 (not_1_out, W);
  not not_2 (not_2_out, Y);
  not not_3 (not_3_out, W);
  not not_4 (not_4_out, X);
  and and_1 (and_1_out, not_1_out, not_2_out);
  not not_5 (not_5_out, Z);
  not not_6 (not_6_out, W);
  not not_7 (not_7_out, Y);
  and and_2 (and_2_out, not_3_out, not_4_out);
  and and_3 (and_3_out, and_1_out, not_5_out);
  not not_8 (not_8_out, X);
  not not_9 (not_9_out, Z);
  and and_4 (and_4_out, not_6_out, Y);
  and and_5 (and_5_out, W, not_7_out);
  or or_1 (or_1_out, and_2_out, and_3_out);
  or or_2 (or_2_out, or_1_out, and_6_out);
  and and_6 (and_6_out, not_8_out, not_9_out);
  and and_7 (and_7_out, and_4_out, Z);
  or or_3 (or_3_out, and_7_out, and_8_out);
  and and_8 (and_8_out, and_5_out, Z);
  or or_4 (b, or_2_out, or_3_out);
endmodule

module c (
  input  W,
  input  X,
  input  Y,
  input  Z,
  output c
);

  wire and_1_out, and_2_out, and_3_out, and_4_out, and_5_out, not_1_out, not_2_out, not_3_out, not_4_out,
       not_5_out, not_6_out, or_1_out, or_2_out, or_4_out;

  not not_1 (not_1_out, W);
  not not_2 (not_2_out, Y);
  not not_3 (not_3_out, W);
  and and_1 (and_1_out, not_1_out, not_2_out);
  and and_2 (and_2_out, not_3_out, Z);
  not not_4 (not_4_out, Y);
  not not_5 (not_5_out, W);
  not not_6 (not_6_out, X);
  or or_1 (or_1_out, and_1_out, and_2_out);
  and and_3 (and_3_out, not_4_out, Z);
  and and_4 (and_4_out, not_5_out, X);
  and and_5 (and_5_out, W, not_6_out);
  or or_2 (or_2_out, or_1_out, and_3_out);
  or or_3 (c, or_2_out, or_4_out);
  or or_4 (or_4_out, and_4_out, and_5_out);
endmodule

module d (
  input  W,
  input  X,
  input  Y,
  input  Z,
  output d
);

  wire and_1_out, and_2_out, and_3_out, and_4_out, and_5_out, not_1_out, not_2_out, not_3_out, not_4_out,
       not_5_out, not_6_out, not_7_out;

  not not_1 (not_1_out, W);
  not not_2 (not_2_out, X);
  not not_3 (not_3_out, Z);
  not not_4 (not_4_out, X);
  not not_5 (not_5_out, Y);
  not not_6 (not_6_out, Z);
  not not_7 (not_7_out, Y);
  and and_1 (and_1_out, not_1_out, not_2_out, not_3_out);
  and and_2 (and_2_out, not_4_out, Y, Z);
  and and_3 (and_3_out, X, not_5_out, Z);
  and and_4 (and_4_out, X, Y, not_6_out);
  and and_5 (and_5_out, W, not_7_out);
  or or_1 (d, and_1_out, and_2_out, and_3_out, and_4_out, and_5_out);
endmodule

module e (
  input  W,
  input  X,
  input  Y,
  input  Z,
  output e
);

  wire and_1_out, and_2_out, and_3_out, and_4_out, not_1_out, not_2_out, or_1_out, or_2_out;

  not not_1 (not_1_out, X);
  not not_2 (not_2_out, Z);
  and and_1 (and_1_out, not_1_out, not_2_out);
  and and_2 (and_2_out, X, Y);
  and and_3 (and_3_out, W, Y);
  and and_4 (and_4_out, W, X);
  or or_1 (or_1_out, and_1_out, and_2_out);
  or or_2 (or_2_out, and_3_out, and_4_out);
  or or_3 (e, or_1_out, or_2_out);
endmodule

module f (
  input  W,
  input  X,
  input  Y,
  input  Z,
  output f
);

  wire and_1_out, and_2_out, and_3_out, and_4_out, and_5_out, and_6_out, not_1_out, not_2_out, not_3_out,
       not_4_out, not_5_out, not_6_out, or_1_out, or_2_out, or_3_out;

  not not_1 (not_1_out, W);
  not not_2 (not_2_out, Y);
  not not_3 (not_3_out, Z);
  and and_1 (and_1_out, not_1_out, X);
  not not_4 (not_4_out, Y);
  and and_2 (and_2_out, not_2_out, not_3_out);
  and and_3 (and_3_out, and_1_out, not_4_out);
  not not_5 (not_5_out, Z);
  not not_6 (not_6_out, X);
  or or_1 (or_1_out, and_2_out, and_3_out);
  or or_2 (or_2_out, or_1_out, and_4_out);
  and and_4 (and_4_out, X, not_5_out);
  and and_5 (and_5_out, W, not_6_out);
  or or_3 (or_3_out, and_5_out, and_6_out);
  and and_6 (and_6_out, W, Y);
  or or_4 (f, or_2_out, or_3_out);
endmodule

module g (
  input  W,
  input  X,
  input  Y,
  input  Z,
  output g
);

  wire and_1_out, and_2_out, and_3_out, and_4_out, and_5_out, and_6_out, not_1_out, not_2_out, not_3_out,
       not_4_out, not_5_out, or_1_out, or_2_out, or_4_out;

  not not_1 (not_1_out, X);
  not not_2 (not_2_out, Z);
  not not_3 (not_3_out, W);
  and and_1 (and_1_out, not_1_out, Y);
  and and_2 (and_2_out, Y, not_2_out);
  and and_3 (and_3_out, not_3_out, X);
  not not_4 (not_4_out, Y);
  not not_5 (not_5_out, X);
  or or_1 (or_1_out, and_1_out, and_2_out);
  and and_4 (and_4_out, and_3_out, not_4_out);
  and and_5 (and_5_out, W, not_5_out);
  and and_6 (and_6_out, W, Z);
  or or_2 (or_2_out, or_1_out, and_4_out);
  or or_3 (g, or_2_out, or_4_out);
  or or_4 (or_4_out, and_5_out, and_6_out);
endmodule

module add (
  input  A,
  input  B,
  input  R,
  output AB
);

  wire and_1_out, and_2_out, and_3_out, and_4_out, not_1_out, not_2_out, not_3_out, not_4_out, not_5_out,
       not_6_out;

  not not_1 (not_1_out, A);
  not not_2 (not_2_out, B);
  not not_3 (not_3_out, A);
  not not_4 (not_4_out, R);
  not not_5 (not_5_out, B);
  not not_6 (not_6_out, R);
  and and_1 (and_1_out, not_1_out, not_2_out, R);
  and and_2 (and_2_out, not_3_out, B, not_4_out);
  and and_3 (and_3_out, A, not_5_out, not_6_out);
  and and_4 (and_4_out, A, B, R);
  or or_1 (AB, and_1_out, and_2_out, and_3_out, and_4_out);
endmodule

module ff (
  input  A,
  input  B,
  input  R,
  output AB,
  output R1
);

  wire and_1_out, and_2_out, and_3_out, and_4_out, and_5_out, and_6_out, and_7_out, not_1_out, not_2_out,
       not_3_out, not_4_out, not_5_out, not_6_out;

  not not_1 (not_1_out, A);
  not not_2 (not_2_out, B);
  not not_3 (not_3_out, A);
  not not_4 (not_4_out, R);
  not not_5 (not_5_out, B);
  not not_6 (not_6_out, R);
  and and_1 (and_1_out, B, R);
  and and_2 (and_2_out, A, R);
  and and_3 (and_3_out, A, B);
  and and_4 (and_4_out, not_1_out, not_2_out, R);
  and and_5 (and_5_out, not_3_out, B, not_4_out);
  and and_6 (and_6_out, A, not_5_out, not_6_out);
  and and_7 (and_7_out, A, B, R);
  or or_1 (R1, and_1_out, and_2_out, and_3_out);
  or or_2 (AB, and_4_out, and_5_out, and_6_out, and_7_out);
endmodule
