// Logisim project tp_3_Ed.circ as structural Verilog: 4 circuits, main circuit main
module main (
);

  wire additionneur4bits_1_overflow, dipswitch_1_sw3, dipswitch_1_sw4, dipswitch_1_sw5, dipswitch_1_sw6,
       dipswitch_1_sw7, dipswitch_1_sw8, dipswitch_1_sw9, dipswitch_1_sw10;

  DipSwitch #(.number(10)) dipswitch_1 (
    .sw3(dipswitch_1_sw3), .sw4(dipswitch_1_sw4), .sw5(dipswitch_1_sw5), .sw6(dipswitch_1_sw6),
    .sw7(dipswitch_1_sw7), .sw8(dipswitch_1_sw8), .sw9(dipswitch_1_sw9), .sw10(dipswitch_1_sw10));  // open: sw1, sw2
  additionneur4bits additionneur4bits_1 (
    .A0(dipswitch_1_sw10), .A1(dipswitch_1_sw9), .A2(dipswitch_1_sw8), .A3(dipswitch_1_sw7),
    .B0(dipswitch_1_sw6), .B1(dipswitch_1_sw5), .B2(dipswitch_1_sw4), .B3(dipswitch_1_sw3),
    .Overflow(additionneur4bits_1_overflow));  // open: AB3, AB2, AB1, AB0
  LED led_1 (.in(additionneur4bits_1_overflow));
endmodule

module additionneur (
  input  A,
  input  B,
  input  R,
  output AB,
  output R1
);

  wire and_1_out, and_2_out, and_3_out, and_4_out, and_5_out, and_6_out, and_7_out, not_1_out, not_2_out,
       not_3_out, not_4_out, not_5_out, not_6_out;

  not not_1 (not_1_out, A);
  not not_2 (not_2_out, B);
  not not_3 (not_3_out, A);
  not not_4 (not_4_out, R);
  not not_5 (not_5_out, B);
  not not_6 (not_6_out, R);
  and and_1 (and_1_out, B, R);
  and and_2 (and_2_out, A, R);
  and and_3 (and_3_out, A, B);
  and and_4 (and_4_out, not_1_out, not_2_out, R);
  and and_5 (and_5_out, not_3_out, B, not_4_out);
  and and_6 (and_6_out, A, not_5_out, not_6_out);
  and and_7 (and_7_out, A, B, R);
  or or_1 (R1, and_1_out, and_2_out, and_3_out);
  or or_2 (AB, and_4_out, and_5_out, and_6_out, and_7_out);
endmodule

module additionneur1 (
  input  A,
  input  B,
  input  R,
  output R1,
  output AB
);

  wire and_1_out, and_2_out, and_3_out, and_4_out, and_5_out, and_6_out, and_7_out, not_1_out, not_2_out,
       not_3_out, not_4_out, not_5_out, not_6_out;

  and and_1 (and_1_out, B, R);
  and and_2 (and_2_out, A, R);
  and and_3 (and_3_out, A, B);
  not not_1 (not_1_out, A);
  not not_2 (not_2_out, B);
  not not_3 (not_3_out, A);
  not not_4 (not_4_out, R);
  not not_5 (not_5_out, B);
  not not_6 (not_6_out, R);
  or or_1 (R1, and_1_out, and_2_out, and_3_out);
  and and_4 (and_4_out, not_1_out, not_2_out, R);
  and and_5 (and_5_out, not_3_out, B, not_4_out);
  and and_6 (and_6_out, A, not_5_out, not_6_out);
  and and_7 (and_7_out, A, B, R);
  or or_2 (AB, and_4_out, and_5_out, and_6_out, and_7_out);
endmodule

module additionneur4bits (
  input  A0,
  input  A1,
  input  A2,
  input  A3,
  input  B0,
  input  B1,
  input  B2,
  input  B3,
  output Overflow,
  output AB3,
  output AB2,
  output AB1,
  output AB0
);

  wire additionneur1_1_r1, additionneur1_2_r1, additionneur1_3_r1;

  additionneur1 additionneur1_1 (.A(A0), .B(B0), .R(1'b0), .R1(additionneur1_1_r1), .AB(AB0));
  additionneur1 additionneur1_2 (.A(A1), .B(B1), .R(additionneur1_1_r1), .R1(additionneur1_2_r1), .AB(AB1));
  additionneur1 additionneur1_3 (.A(A2), .B(B2), .R(additionneur1_2_r1), .R1(additionneur1_3_r1), .AB(AB2));
  additionneur1 additionneur1_4 (.A(A3), .B(B3), .R(additionneur1_3_r1), .R1(Overflow), .AB(AB3));
endmodule
