// Logisim project tp_3_working.circ as structural Verilog: 13 circuits, main circuit main
module main (
);

  wire additionneur4bits_1_ab0, additionneur4bits_1_ab1, additionneur4bits_1_ab2, additionneur4bits_1_ab3,
       additionneur4bits_1_overflow, DipSwitch_1_sw3, DipSwitch_1_sw4, DipSwitch_1_sw5, DipSwitch_1_sw6,
       DipSwitch_1_sw7, DipSwitch_1_sw8, DipSwitch_1_sw9, DipSwitch_1_sw10, septsegment_1_pina,
       septsegment_1_pinb, septsegment_1_pinc, septsegment_1_pind, septsegment_1_pine, septsegment_1_pinf,
       septsegment_1_ping;

  DipSwitch #(.number(10)) DipSwitch_1 (
    .sw3(DipSwitch_1_sw3), .sw4(DipSwitch_1_sw4), .sw5(DipSwitch_1_sw5), .sw6(DipSwitch_1_sw6),
    .sw7(DipSwitch_1_sw7), .sw8(DipSwitch_1_sw8), .sw9(DipSwitch_1_sw9), .sw10(DipSwitch_1_sw10));  // open: sw1, sw2
  additionneur4bits additionneur4bits_1 (
    .A0(DipSwitch_1_sw10), .A1(DipSwitch_1_sw9), .A2(DipSwitch_1_sw8), .A3(DipSwitch_1_sw7),
    .B0(DipSwitch_1_sw6), .B1(DipSwitch_1_sw5), .B2(DipSwitch_1_sw4), .B3(DipSwitch_1_sw3),
    .Overflow(additionneur4bits_1_overflow), .AB3(additionneur4bits_1_ab3), .AB2(additionneur4bits_1_ab2),
    .AB1(additionneur4bits_1_ab1), .AB0(additionneur4bits_1_ab0));
  LED LED_1 (.in(additionneur4bits_1_overflow));
  septsegment septsegment_1 (
    .W(additionneur4bits_1_ab3), .X(additionneur4bits_1_ab2), .Y(additionneur4bits_1_ab1),
    .Z(additionneur4bits_1_ab0), .pinb(septsegment_1_pinb), .pina(septsegment_1_pina),
    .pinf(septsegment_1_pinf), .ping(septsegment_1_ping), .pine(septsegment_1_pine),
    .pind(septsegment_1_pind), .pinc(septsegment_1_pinc));
  _7_Segment_Display L_7_Segment_Display_1 (
    .g(septsegment_1_ping), .f(septsegment_1_pinf), .a(septsegment_1_pina), .b(septsegment_1_pinb),
    .e(septsegment_1_pine), .d(septsegment_1_pind), .c(septsegment_1_pinc));  // open: dp
endmodule

module additionneur1 (
  input  A,
  input  B,
  input  R,
  output R1,
  output AB
);

  wire and_1_out, and_2_out, and_3_out, and_4_out, and_5_out, and_6_out, and_7_out, not_1_out, not_2_out,
       not_3_out, not_4_out, not_5_out, not_6_out;

  and and_1 (and_1_out, B, R);
  and and_2 (and_2_out, A, R);
  and and_3 (and_3_out, A, B);
  not not_1 (not_1_out, A);
  not not_2 (not_2_out, B);
  not not_3 (not_3_out, A);
  not not_4 (not_4_out, R);
  not not_5 (not_5_out, B);
  not not_6 (not_6_out, R);
  or or_1 (R1, and_1_out, and_2_out, and_3_out);
  and and_4 (and_4_out, not_1_out, not_2_out, R);
  and and_5 (and_5_out, not_3_out, B, not_4_out);
  and and_6 (and_6_out, A, not_5_out, not_6_out);
  and and_7 (and_7_out, A, B, R);
  or or_2 (AB, and_4_out, and_5_out, and_6_out, and_7_out);
endmodule

module additionneur4bits (
  input  A0,
  input  A1,
  input  A2,
  input  A3,
  input  B0,
  input  B1,
  input  B2,
  input  B3,
  output Overflow,
  output AB3,
  output AB2,
  output AB1,
  output AB0
);

  wire additionneur1_2_r1, additionneur1_3_r1, additionneur1_4_r1;

  additionneur1 additionneur1_4 (.A(A0), .B(B0), .R(1'b0), .R1(additionneur1_4_r1), .AB(AB0));
  additionneur1 additionneur1_3 (.A(A1), .B(B1), .R(additionneur1_4_r1), .R1(additionneur1_3_r1), .AB(AB1));
  additionneur1 additionneur1_2 (.A(A2), .B(B2), .R(additionneur1_3_r1), .R1(additionneur1_2_r1), .AB(AB2));
  additionneur1 additionneur1_1 (.A(A3), .B(B3), .R(additionneur1_2_r1), .R1(Overflow), .AB(AB3));
endmodule

module a (
  input  W,
  input  X,
  input  Y,
  input  Z,
  output a
);

  wire and_1_out, and_2_out, and_3_out, and_4_out, and_5_out, and_6_out, and_7_out, and_8_out, not_1_out,
       not_2_out, not_3_out, not_4_out, not_5_out, not_6_out, not_7_out, or_1_out, or_2_out, or_3_out,
       or_4_out;

  not not_1 (not_1_out, X);
  not not_2 (not_2_out, X);
  not not_3 (not_3_out, Z);
  not not_4 (not_4_out, W);
  not not_5 (not_5_out, W);
  and and_1 (and_1_out, W, not_1_out);
  not not_6 (not_6_out, Y);
  and and_2 (and_2_out, not_2_out, not_3_out);
  and and_3 (and_3_out, not_4_out, Y);
  and and_4 (and_4_out, not_5_out, X);
  and and_5 (and_5_out, X, Y);
  and and_6 (and_6_out, and_1_out, not_6_out);
  not not_7 (not_7_out, Z);
  or or_1 (or_1_out, and_2_out, and_3_out);
  or or_2 (or_2_out, or_1_out, and_7_out);
  and and_7 (and_7_out, and_4_out, Z);
  or or_3 (or_3_out, and_5_out, and_6_out);
  or or_4 (or_4_out, or_3_out, and_8_out);
  and and_8 (and_8_out, W, not_7_out);
  or or_5 (a, or_2_out, or_4_out);
endmodule

module b (
  input  W,
  input  X,
  input  Y,
  input  Z,
  output b
);

  wire and_1_out, and_2_out, and_3_out, and_4_out, and_5_out, and_6_out, and_7_out, and_8_out, not_1_out,
       not_2_out, not_3_out, not_4_out, not_5_out, not_6_out, not_7_out, not_8_out, not_9_out, or_1_out,
       or_2_out, or_3_out;

  not not_1 (not_1_out, W);
  not not_2 (not_2_out, Y);
  not not_3 (not_3_out, W);
  not not_4 (not_4_out, X);
  and and_1 (and_1_out, not_1_out, not_2_out);
  not not_5 (not_5_out, Z);
  not not_6 (not_6_out, W);
  not not_7 (not_7_out, Y);
  and and_2 (and_2_out, not_3_out, not_4_out);
  and and_3 (and_3_out, and_1_out, not_5_out);
  not not_8 (not_8_out, X);
  not not_9 (not_9_out, Z);
  and and_4 (and_4_out, not_6_out, Y);
  and and_5 (and_5_out, W, not_7_out);
  or or_1 (or_1_out, and_2_out, and_3_out);
  or or_2 (or_2_out, or_1_out, and_6_out);
  and and_6 (and_6_out, not_8_out, not_9_out);
  and and_7 (and_7_out, and_4_out, Z);
  or or_3 (or_3_out, and_7_out, and_8_out);
  and and_8 (and_8_out, and_5_out, Z);
  or or_4 (b, or_2_out, or_3_out);
endmodule

module c (
  input  W,
  input  X,
  input  Y,
  input  Z,
  output c
);

  wire and_1_out, and_2_out, and_3_out, and_4_out, and_5_out, not_1_out, not_2_out, not_3_out, not_4_out,
       not_5_out, not_6_out, or_1_out, or_2_out, or_4_out;

  not not_1 (not_1_out, W);
  not not_2 (not_2_out, Y);
  not not_3 (not_3_out, W);
  and and_1 (and_1_out, not_1_out, not_2_out);
  and and_2 (and_2_out, not_3_out, Z);
  not not_4 (not_4_out, Y);
  not not_5 (not_5_out, W);
  not not_6 (not_6_out, X);
  or or_1 (or_1_out, and_1_out, and_2_out);
  and and_3 (and_3_out, not_4_out, Z);
  and and_4 (and_4_out, not_5_out, X);
  and and_5 (and_5_out, W, not_6_out);
  or or_2 (or_2_out, or_1_out, and_3_out);
  or or_3 (c, or_2_out, or_4_out);
  or or_4 (or_4_out, and_4_out, and_5_out);
endmodule

module d (
  input  W,
  input  X,
  input  Y,
  input  Z,
  output d
);

  wire and_1_out, and_2_out, and_3_out, and_4_out, and_5_out, not_1_out, not_2_out, not_3_out, not_4_out,
       not_5_out, not_6_out, not_7_out;

  not not_1 (not_1_out, W);
  not not_2 (not_2_out, X);
  not not_3 (not_3_out, Z);
  not not_4 (not_4_out, X);
  not not_5 (not_5_out, Y);
  not not_6 (not_6_out, Z);
  not not_7 (not_7_out, Y);
  and and_1 (and_1_out, not_1_out, not_2_out, not_3_out);
  and and_2 (and_2_out, not_4_out, Y, Z);
  and and_3 (and_3_out, X, not_5_out, Z);
  and and_4 (and_4_out, X, Y, not_6_out);
  and and_5 (and_5_out, W, not_7_out);
  or or_1 (d, and_1_out, and_2_out, and_3_out, and_4_out, and_5_out);
endmodule

module e (
  input  W,
  input  X,
  input  Y,
  input  Z,
  output e
);

  wire and_1_out, and_2_out, and_3_out, and_4_out, not_1_out, not_2_out, or_1_out, or_2_out;

  not not_1 (not_1_out, X);
  not not_2 (not_2_out, Z);
  and and_1 (and_1_out, not_1_out, not_2_out);
  and and_2 (and_2_out, X, Y);
  and and_3 (and_3_out, W, Y);
  and and_4 (and_4_out, W, X);
  or or_1 (or_1_out, and_1_out, and_2_out);
  or or_2 (or_2_out, and_3_out, and_4_out);
  or or_3 (e, or_1_out, or_2_out);
endmodule

module f (
  input  W,
  input  X,
  input  Y,
  input  Z,
  output f
);

  wire and_1_out, and_2_out, and_3_out, and_4_out, and_5_out, and_6_out, not_1_out, not_2_out, not_3_out,
       not_4_out, not_5_out, not_6_out, or_1_out, or_2_out, or_3_out;

  not not_1 (not_1_out, W);
  not not_2 (not_2_out, Y);
  not not_3 (not_3_out, Z);
  and and_1 (and_1_out, not_1_out, X);
  not not_4 (not_4_out, Y);
  and and_2 (and_2_out, not_2_out, not_3_out);
  and and_3 (and_3_out, and_1_out, not_4_out);
  not not_5 (not_5_out, Z);
  not not_6 (not_6_out, X);
  or or_1 (or_1_out, and_2_out, and_3_out);
  or or_2 (or_2_out, or_1_out, and_4_out);
  and and_4 (and_4_out, X, not_5_out);
  and and_5 (and_5_out, W, not_6_out);
  or or_3 (or_3_out, and_5_out, and_6_out);
  and and_6 (and_6_out, W, Y);
  or or_4 (f, or_2_out, or_3_out);
endmodule

module g (
  input  W,
  input  X,
  input  Y,
  input  Z,
  output g
);

  wire and_1_out, and_2_out, and_3_out, and_4_out, and_5_out, and_6_out, not_1_out, not_2_out, not_3_out,
       not_4_out, not_5_out, or_1_out, or_2_out, or_4_out;

  not not_1 (not_1_out, X);
  not not_2 (not_2_out, Z);
  not not_3 (not_3_out, W);
  and and_1 (and_1_out, not_1_out, Y);
  and and_2 (and_2_out, Y, not_2_out);
  and and_3 (and_3_out, not_3_out, X);
  not not_4 (not_4_out, Y);
  not not_5 (not_5_out, X);
  or or_1 (or_1_out, and_1_out, and_2_out);
  and and_4 (and_4_out, and_3_out, not_4_out);
  and and_5 (and_5_out, W, not_5_out);
  and and_6 (and_6_out, W, Z);
  or or_2 (or_2_out, or_1_out, and_4_out);
  or or_3 (g, or_2_out, or_4_out);
  or or_4 (or_4_out, and_5_out, and_6_out);
endmodule

module add (
  input  A,
  input  B,
  input  R,
  output AB
);

  wire and_1_out, and_2_out, and_3_out, and_4_out, not_1_out, not_2_out, not_3_out, not_4_out, not_5_out,
       not_6_out;

  not not_1 (not_1_out, A);
  not not_2 (not_2_out, B);
  not not_3 (not_3_out, A);
  not not_4 (not_4_out, R);
  not not_5 (not_5_out, B);
  not not_6 (not_6_out, R);
  and and_1 (and_1_out, not_1_out, not_2_out, R);
  and and_2 (and_2_out, not_3_out, B, not_4_out);
  and and_3 (and_3_out, A, not_5_out, not_6_out);
  and and_4 (and_4_out, A, B, R);
  or or_1 (AB, and_1_out, and_2_out, and_3_out, and_4_out);
endmodule

module ff (
  input  A,
  input  B,
  input  R,
  output AB,
  output R1
);

  wire and_1_out, and_2_out, and_3_out, and_4_out, and_5_out, and_6_out, and_7_out, not_1_out, not_2_out,
       not_3_out, not_4_out, not_5_out, not_6_out;

  not not_1 (not_1_out, A);
  not not_2 (not_2_out, B);
  not not_3 (not_3_out, A);
  not not_4 (not_4_out, R);
  not not_5 (not_5_out, B);
  not not_6 (not_6_out, R);
  and and_1 (and_1_out, B, R);
  and and_2 (and_2_out, A, R);
  and and_3 (and_3_out, A, B);
  and and_4 (and_4_out, not_1_out, not_2_out, R);
  and and_5 (and_5_out, not_3_out, B, not_4_out);
  and and_6 (and_6_out, A, not_5_out, not_6_out);
  and and_7 (and_7_out, A, B, R);
  or or_1 (R1, and_1_out, and_2_out, and_3_out);
  or or_2 (AB, and_4_out, and_5_out, and_6_out, and_7_out);
endmodule

module septsegment (
  input  W,
  input  X,
  input  Y,
  input  Z,
  output pinb,
  output pina,
  output pinf,
  output ping,
  output pine,
  output pind,
  output pinc
);

  a a_1 (.W(W), .X(X), .Y(Y), .Z(Z), .a(pina));
  b b_1 (.W(W), .X(X), .Y(Y), .Z(Z), .b(pinb));
  c c_1 (.W(W), .X(X), .Y(Y), .Z(Z), .c(pinc));
  d d_1 (.W(W), .X(X), .Y(Y), .Z(Z), .d(pind));
  e e_1 (.W(W), .X(X), .Y(Y), .Z(Z), .e(pine));
  f f_1 (.W(W), .X(X), .Y(Y), .Z(Z), .f(pinf));
  g g_1 (.W(W), .X(X), .Y(Y), .Z(Z), .g(ping));
endmodule
